// Logisim project 8.2.c Cache test.circ as structural Verilog: 1 circuit, main circuit main
module main (
  input  in_1,
  input  in_2,
  input  in_3,
  input  Keyboard_IN,
  input  in_5,
  input  in_6,
  input  in_7,
  input  in_8,
  input  in_9,
  input  [7:0] Data_In,
  input  [11:0] Adr_In,
  input  Write_Ram,
  input  in_13,
  output [11:0] PC,
  output [15:0] Instruc,
  output [7:0] Reg_0,
  output [7:0] Reg_1,
  output [7:0] Reg_2,
  output [7:0] Reg_3,
  output [15:0] out_20,
  output [7:0] Reg_4,
  output [7:0] Reg_5,
  output [7:0] Reg_6,
  output [7:0] Reg_7,
  output [7:0] Read_Ram,
  output [7:0] Reg_8,
  output [7:0] Reg_9,
  output [7:0] Reg_A,
  output [7:0] Reg_B,
  output [7:0] Reg_C,
  output [7:0] Reg_D,
  output [7:0] Reg_E,
  output [7:0] Reg_F
);

  wire _0_out, _1_out, _2a_out, _2b_out, _3_out, _4_out, _5_out, _6_out, _7_out, _8_out, _9_out, _20_out,
       _21_out, _22_out, _23_out, _24_out, _25_out, _26_out, _27_out, _28_out, _29_out, a_out, adder_2_cout,
       and_1_out, and_2_out, and_3_out, and_4_out, and_5_out, and_6_out, and_7_out, and_8_out, and_9_out,
       and_10_out, and_11_out, and_12_out, and_13_out, and_14_out, and_15_out, and_16_out, and_17_out,
       and_18_out, and_20_out, and_21_out, and_22_out, and_23_out, and_24_out, and_25_out, and_26_out,
       and_27_out, and_28_out, and_29_out, and_30_out, and_31_out, and_32_out, and_33_out, and_34_out,
       and_35_out, and_36_out, and_37_out, and_38_out, and_39_out, and_40_out, and_41_out, and_42_out,
       and_43_out, and_44_out, and_45_out, and_46_out, and_47_out, and_48_out, and_49_out, and_50_out,
       and_51_out, and_52_out, and_53_out, and_54_out, and_55_out, and_56_out, and_57_out, and_58_out,
       and_59_out, and_60_out, and_61_out, and_62_out, and_63_out, and_64_out, and_65_out, and_66_out,
       and_67_out, and_68_out, and_69_out, and_70_out, and_71_out, and_72_out, and_73_out, and_74_out,
       and_75_out, and_76_out, and_77_out, and_78_out, and_79_out, and_80_out, and_81_out, and_82_out,
       and_83_out, and_84_out, and_85_out, and_86_out, and_87_out, and_88_out, and_89_out, and_90_out,
       and_91_out, and_92_out, and_93_out, and_94_out, and_95_out, and_96_out, and_97_out, and_98_out,
       and_99_out, and_100_out, and_101_out, and_102_out, and_103_out, and_104_out, and_105_out, and_106_out,
       and_107_out, and_108_out, and_109_out, b_out, button_1_out, c_out, clock_1_out, d_ff_1_q, d_ff_1_qn,
       d_ff_2_q, d_ff_2_qn, d_ff_3_q, d_ff_4_q, d_ff_4_qn, d_ff_5_q, d_ff_5_qn, d_ff_6_q, d_ff_7_q, d_ff_8_q,
       d_ff_8_qn, d_ff_9_q, d_ff_9_qn, d_ff_10_q, d_ff_10_qn, d_ff_11_q, d_ff_12_q, d_ff_13_q, d_ff_13_qn,
       d_ff_14_q, d_ff_14_qn, d_ff_15_q, d_ff_15_qn, d_ff_16_q, d_ff_16_qn, d_ff_17_q, d_out, decoder_1_out0,
       decoder_1_out1, decoder_1_out2, decoder_1_out3, decoder_1_out4, decoder_1_out5, decoder_1_out6,
       decoder_1_out7, decoder_1_out8, decoder_1_out9, decoder_1_out10, decoder_1_out11, decoder_1_out12,
       decoder_1_out13, decoder_1_out14, decoder_1_out15, decoder_2_out0, decoder_2_out1, decoder_2_out2,
       decoder_2_out3, decoder_2_out4, decoder_2_out5, decoder_2_out6, decoder_2_out7, decoder_2_out8,
       decoder_2_out9, decoder_2_out10, decoder_2_out11, decoder_2_out12, decoder_2_out13, decoder_2_out14,
       decoder_2_out15, decoder_3_out0, decoder_3_out1, decoder_3_out2, decoder_3_out3, decoder_3_out4,
       decoder_3_out5, decoder_3_out6, decoder_3_out7, decoder_3_out8, decoder_3_out9, decoder_3_out10,
       decoder_3_out11, decoder_3_out12, decoder_3_out13, decoder_3_out14, decoder_3_out15, decoder_4_out0,
       decoder_4_out1, decoder_4_out2, decoder_4_out3, decoder_4_out4, decoder_4_out5, decoder_4_out6,
       decoder_4_out7, decoder_4_out8, decoder_4_out9, decoder_4_out10, decoder_4_out11, decoder_4_out12,
       decoder_4_out13, decoder_4_out14, decoder_4_out15, decoder_5_out0, decoder_5_out1, decoder_5_out2,
       decoder_5_out3, decoder_5_out4, decoder_5_out5, decoder_5_out6, decoder_5_out7, decoder_5_out8,
       decoder_5_out9, decoder_5_out10, decoder_5_out11, decoder_5_out12, decoder_5_out13, decoder_5_out14,
       decoder_5_out15, decoder_6_out0, decoder_6_out1, decoder_6_out2, decoder_6_out3, decoder_6_out4,
       decoder_6_out5, decoder_6_out6, decoder_6_out7, decoder_6_out8, decoder_6_out9, decoder_6_out10,
       decoder_6_out11, decoder_6_out12, decoder_6_out13, decoder_6_out14, decoder_6_out15, decoder_7_out0,
       decoder_7_out1, decoder_7_out2, decoder_7_out3, decoder_7_out4, decoder_7_out5, decoder_7_out6,
       decoder_7_out7, decoder_7_out8, decoder_7_out9, decoder_7_out10, decoder_7_out11, decoder_7_out12,
       decoder_7_out13, decoder_7_out14, decoder_7_out15, decoder_8_out0, decoder_8_out1, decoder_8_out2,
       decoder_8_out3, decoder_8_out4, decoder_8_out5, decoder_8_out6, decoder_8_out7, decoder_8_out8,
       decoder_8_out9, decoder_8_out10, decoder_8_out11, decoder_8_out12, decoder_8_out13, decoder_8_out14,
       decoder_8_out15, decoder_9_out0, decoder_9_out1, decoder_9_out2, decoder_9_out3, decoder_9_out4,
       decoder_9_out5, decoder_9_out6, decoder_9_out7, decoder_9_out8, decoder_9_out9, decoder_9_out10,
       decoder_9_out11, decoder_9_out12, decoder_9_out13, decoder_9_out14, decoder_9_out15, decoder_10_out0,
       decoder_10_out1, decoder_10_out2, decoder_10_out3, decoder_10_out4, decoder_10_out5, decoder_10_out6,
       decoder_10_out7, decoder_10_out8, decoder_10_out9, decoder_10_out10, decoder_10_out11,
       decoder_10_out12, decoder_10_out13, decoder_10_out14, decoder_10_out15, decoder_11_out0,
       decoder_11_out1, decoder_11_out2, decoder_11_out3, decoder_11_out4, decoder_11_out5, decoder_11_out6,
       decoder_11_out7, decoder_11_out8, decoder_11_out9, decoder_11_out10, decoder_11_out11,
       decoder_11_out12, decoder_11_out13, decoder_11_out14, decoder_11_out15, decoder_12_out0,
       decoder_12_out1, decoder_12_out2, decoder_12_out3, decoder_12_out4, decoder_12_out5, decoder_12_out6,
       decoder_12_out7, decoder_12_out8, decoder_12_out9, decoder_12_out10, decoder_12_out11,
       decoder_12_out12, decoder_12_out13, decoder_12_out14, decoder_12_out15, decoder_13_out0,
       decoder_13_out1, decoder_13_out2, decoder_13_out3, decoder_13_out4, decoder_13_out5, decoder_13_out6,
       decoder_13_out7, decoder_13_out8, decoder_13_out9, decoder_13_out10, decoder_13_out11,
       decoder_13_out12, decoder_13_out13, decoder_13_out14, decoder_13_out15, decoder_14_out0,
       decoder_14_out1, decoder_14_out2, decoder_14_out3, decoder_14_out4, decoder_14_out5, decoder_14_out6,
       decoder_14_out7, decoder_14_out8, decoder_14_out9, decoder_14_out10, decoder_14_out11,
       decoder_14_out12, decoder_14_out13, decoder_14_out14, decoder_14_out15, decoder_15_out0,
       decoder_15_out1, decoder_15_out2, decoder_15_out3, decoder_16_out0, decoder_16_out1, decoder_16_out2,
       decoder_16_out3, decoder_16_out4, decoder_16_out5, decoder_16_out6, decoder_16_out7, decoder_16_out8,
       decoder_16_out9, decoder_16_out10, decoder_16_out11, decoder_16_out12, decoder_16_out13,
       decoder_16_out14, decoder_16_out15, decoder_17_out0, decoder_17_out1, decoder_17_out2,
       decoder_17_out3, decoder_17_out4, decoder_17_out5, decoder_17_out6, decoder_17_out7, decoder_17_out8,
       decoder_17_out9, decoder_17_out10, decoder_17_out11, decoder_17_out12, decoder_17_out13,
       decoder_17_out14, decoder_17_out15, decoder_18_out0, decoder_18_out1, decoder_18_out2,
       decoder_18_out3, decoder_18_out4, decoder_18_out5, decoder_18_out6, decoder_18_out7, decoder_18_out8,
       decoder_18_out9, decoder_18_out10, decoder_18_out11, decoder_18_out12, decoder_18_out13,
       decoder_18_out14, decoder_18_out15, decoder_19_out0, decoder_19_out1, decoder_19_out2,
       decoder_19_out3, decoder_19_out4, decoder_19_out5, decoder_19_out6, decoder_19_out7, decoder_20_out0,
       decoder_20_out1, decoder_20_out2, decoder_20_out3, decoder_20_out4, decoder_20_out5, decoder_20_out6,
       decoder_20_out7, decoder_21_out0, decoder_21_out1, decoder_21_out2, decoder_21_out3, decoder_21_out4,
       decoder_21_out5, decoder_21_out6, decoder_21_out7, decoder_22_out0, decoder_22_out1, decoder_22_out2,
       decoder_22_out3, decoder_22_out4, decoder_22_out5, decoder_22_out6, decoder_22_out7, decoder_23_out0,
       decoder_23_out1, decoder_23_out2, decoder_23_out3, decoder_23_out4, decoder_23_out5, decoder_23_out6,
       decoder_23_out7, decoder_23_out8, decoder_23_out9, decoder_23_out10, decoder_23_out11,
       decoder_23_out12, decoder_23_out13, decoder_23_out14, decoder_23_out15, decoder_24_out0,
       decoder_24_out1, decoder_24_out2, decoder_24_out3, decoder_25_out0, decoder_25_out1, decoder_25_out2,
       decoder_25_out3, e_out, f0_out, f1_out, fe_out, fffe_out, ffff_out, multiplexer_101_out,
       multiplexer_102_out, multiplexer_138_out, nand_1_out, nand_2_out, nand_3_out, nand_4_out, nand_5_out,
       nand_6_out, Off_out, On_2_out, On_out, or_1_out, or_2_out, or_3_out, or_4_out, or_5_out, or_6_out,
       or_7_out, or_8_out, or_9_out, or_10_out, or_11_out, or_12_out, or_13_out, or_14_out, or_15_out,
       or_16_out, or_17_out, or_18_out, or_19_out, or_20_out, or_21_out, or_22_out, or_23_out, or_24_out,
       or_25_out, or_26_out, or_27_out, or_28_out, or_29_out, or_30_out, or_31_out, or_32_out, or_33_out,
       or_34_out, or_35_out, or_36_out, or_37_out, or_38_out, or_39_out, or_40_out, or_41_out, or_42_out,
       or_43_out, or_44_out, or_45_out, or_46_out, or_47_out, or_48_out, or_49_out, or_50_out, or_51_out,
       or_52_out, or_53_out, or_54_out, or_55_out, or_56_out, or_57_out, or_58_out, or_59_out, or_60_out,
       or_61_out, or_62_out, or_63_out, or_64_out, or_65_out, or_66_out, or_67_out, or_68_out, or_69_out,
       or_70_out, or_71_out, or_72_out, or_73_out, or_74_out, or_75_out, or_76_out, or_77_out, or_78_out,
       or_79_out, or_80_out, or_81_out, or_82_out, or_83_out, or_84_out, or_85_out, or_86_out, or_87_out,
       or_88_out, or_89_out, or_90_out, or_91_out, or_92_out, or_93_out, or_94_out, or_95_out, or_96_out,
       or_97_out, or_98_out, or_99_out, or_100_out, or_101_out, or_105_out, or_106_out, or_107_out,
       or_108_out, or_109_out, or_110_out, or_111_out, or_112_out, or_113_out, or_114_out, or_115_out,
       or_116_out, or_117_out, or_118_out, or_119_out, or_120_out, or_121_out, or_122_out, or_123_out,
       or_124_out, or_125_out, or_126_out, or_147_out, or_148_out, or_149_out, or_150_out, or_151_out,
       or_152_out, or_153_out, or_154_out, or_155_out, or_156_out, or_157_out, or_158_out, or_159_out,
       or_160_out, or_161_out, or_162_out, or_163_out, or_164_out, or_165_out, or_166_out, or_167_out,
       or_168_out, or_169_out, or_170_out, or_171_out, or_172_out, or_173_out, undriven, undriven_2,
       undriven_3, undriven_4, undriven_5, undriven_6, undriven_7, undriven_8, undriven_9, undriven_10,
       undriven_11, undriven_12, undriven_13, undriven_14, undriven_15, undriven_16, undriven_17,
       undriven_18, undriven_19, undriven_20, undriven_21, undriven_22, undriven_23, undriven_24,
       undriven_25, undriven_26, undriven_27, undriven_28, undriven_29, undriven_30, undriven_31,
       undriven_32, undriven_33, undriven_34, undriven_35, undriven_36, undriven_37, undriven_38;
  wire [1:0] adder_5_out, adder_9_out, multiplexer_129_out, multiplexer_141_out, multiplexer_142_out,
       multiplexer_143_out, multiplexer_144_out, register_18_q, register_26_q;
  wire [2:0] or_131_out_2;
  wire [3:0] adder_6_out, adder_8_out, demultiplexer_1_out0, demultiplexer_1_out1, demultiplexer_2_out0,
       demultiplexer_2_out1, multiplexer_21_out, multiplexer_22_out, multiplexer_23_out, multiplexer_24_out,
       multiplexer_25_out, multiplexer_26_out, multiplexer_76_out_2, multiplexer_76_out_3,
       multiplexer_77_out_2, multiplexer_130_out, multiplexer_131_out, multiplexer_132_out,
       multiplexer_137_out, register_19_q, register_21_q;
  wire [7:0] adder_2_out, adder_3_out, divider_1_out, divider_1_rem, Exc_Code_q, Exc_Data_q, Hi_q, Lo_q,
       multiplexer_1_out, multiplexer_2_out, multiplexer_3_out, multiplexer_4_out, multiplexer_5_out,
       multiplexer_6_out, multiplexer_7_out, multiplexer_8_out, multiplexer_9_out, multiplexer_10_out,
       multiplexer_11_out, multiplexer_12_out, multiplexer_13_out, multiplexer_14_out, multiplexer_15_out,
       multiplexer_16_out, multiplexer_17_out, multiplexer_18_out, multiplexer_19_out, multiplexer_20_out,
       multiplexer_27_out, multiplexer_28_out, multiplexer_29_out, multiplexer_30_out, multiplexer_31_out,
       multiplexer_32_out, multiplexer_33_out, multiplexer_34_out, multiplexer_35_out, multiplexer_36_out,
       multiplexer_37_out, multiplexer_38_out, multiplexer_39_out, multiplexer_40_out, multiplexer_41_out,
       multiplexer_42_out, multiplexer_43_out, multiplexer_44_out, multiplexer_45_out, multiplexer_46_out,
       multiplexer_47_out, multiplexer_48_out, multiplexer_49_out, multiplexer_50_out, multiplexer_51_out,
       multiplexer_52_out, multiplexer_53_out, multiplexer_54_out, multiplexer_55_out, multiplexer_56_out,
       multiplexer_57_out, multiplexer_58_out, multiplexer_59_out, multiplexer_60_out, multiplexer_61_out,
       multiplexer_62_out, multiplexer_63_out, multiplexer_64_out, multiplexer_65_out, multiplexer_66_out,
       multiplexer_67_out, multiplexer_68_out, multiplexer_69_out, multiplexer_70_out, multiplexer_71_out,
       multiplexer_72_out, multiplexer_73_out, multiplexer_74_out, multiplexer_76_out, multiplexer_77_out,
       multiplexer_79_out, multiplexer_80_out, multiplexer_81_out, multiplexer_82_out, multiplexer_83_out,
       multiplexer_84_out, multiplexer_85_out, multiplexer_86_out, multiplexer_87_out, multiplexer_88_out,
       multiplexer_89_out, multiplexer_90_out, multiplexer_91_out, multiplexer_92_out, multiplexer_93_out,
       multiplexer_94_out, multiplexer_100_out, multiplexer_103_out, multiplexer_104_out,
       multiplexer_105_out, multiplexer_106_out, multiplexer_107_out, multiplexer_108_out,
       multiplexer_109_out, multiplexer_110_out, multiplexer_111_out, multiplexer_112_out,
       multiplexer_113_out, multiplexer_114_out, multiplexer_115_out, multiplexer_121_out,
       multiplexer_122_out, multiplexer_123_out, multiplexer_124_out, multiplexer_125_out,
       multiplexer_133_out, multiplexer_135_out, multiplexer_136_out, multiplexer_137_out_2,
       multiplexer_139_out, multiplexer_140_out, multiplexer_157_out, multiplexer_158_out,
       multiplexer_159_out, multiplexer_160_out, multiplexer_161_out, multiplexer_162_out,
       multiplexer_163_out, multiplexer_164_out, multiplexer_173_out, multiplexer_174_out,
       multiplexer_175_out, multiplexer_176_out, multiplexer_177_out, multiplexer_178_out,
       multiplexer_179_out, multiplexer_180_out, multiplier_1_cout, multiplier_1_out, not_1_out, or_127_out,
       or_129_out, or_130_out, or_132_out, or_133_out, ram_1_data, ram_2_data, ram_3_data, ram_4_data,
       ram_5_data, ram_6_data, ram_7_data, ram_8_data, ram_9_data, ram_10_data, ram_11_data, ram_12_data,
       ram_13_data, ram_14_data, ram_15_data, ram_16_data, ram_17_data, ram_18_data, register_1_q,
       register_2_q, register_3_q, register_4_q, register_5_q, register_6_q, register_7_q, register_8_q,
       register_9_q, register_10_q, register_11_q, register_12_q, register_13_q, register_14_q,
       register_15_q, register_16_q, register_22_q, register_23_q, register_24_q, register_25_q, xor_1_out,
       xor_3_out, xor_4_out, xor_5_out, xor_6_out;
  wire [7:1] or_140_out;
  wire [7:7] Carry_q;
  wire [11:0] adder_1_out, adder_7_out, multiplexer_75_out, multiplexer_95_out, multiplexer_97_out,
       multiplexer_98_out, multiplexer_116_out, multiplexer_117_out, multiplexer_118_out,
       multiplexer_119_out, multiplexer_120_out, multiplexer_134_out, or_102_out, or_103_out, or_104_out,
       or_131_out;
  wire [11:4] register_20_q;
  wire [15:0] adder_4_out, multiplexer_78_out, multiplexer_96_out, multiplexer_99_out, multiplexer_126_out,
       multiplexer_127_out, multiplexer_128_out, multiplexer_145_out, multiplexer_146_out,
       multiplexer_147_out, multiplexer_148_out, multiplexer_149_out, multiplexer_150_out,
       multiplexer_151_out, multiplexer_152_out, multiplexer_153_out, multiplexer_154_out,
       multiplexer_155_out, multiplexer_156_out, multiplexer_165_out, multiplexer_166_out,
       multiplexer_167_out, multiplexer_168_out, multiplexer_169_out, multiplexer_170_out,
       multiplexer_171_out, multiplexer_172_out, multiplexer_181_out, multiplexer_182_out,
       multiplexer_183_out, multiplexer_184_out, multiplexer_185_out, multiplexer_185_out_2,
       multiplexer_186_out, multiplexer_186_out_2, multiplexer_187_out, multiplexer_187_out_2,
       multiplexer_188_out, multiplexer_188_out_2, multiplexer_189_out, multiplexer_190_out,
       multiplexer_191_out, multiplexer_192_out, multiplexer_193_out, multiplexer_194_out,
       multiplexer_195_out, multiplexer_196_out, register_27_q, register_28_q, register_29_q, register_30_q,
       register_31_q, register_32_q, register_33_q, register_34_q, register_35_q, register_36_q,
       register_37_q, register_38_q, register_39_q, register_40_q, register_41_q, register_42_q,
       register_43_q, register_44_q, register_45_q, register_46_q, register_47_q, register_48_q,
       register_49_q, register_50_q, register_51_q, register_52_q, register_53_q, register_54_q,
       register_55_q, register_56_q, register_57_q, register_58_q, xor_2_out;

  nand nand_1 (nand_1_out, undriven_16, undriven_9);
  nand nand_2 (nand_2_out, undriven_5, undriven);
  nand nand_3 (nand_3_out, undriven_10, undriven_11);
  nand nand_4 (nand_4_out, undriven_2, undriven_6);
  or or_1 (or_1_out, undriven_7, undriven_3);
  or or_2 (or_2_out, undriven_12, undriven_13);
  or or_3 (or_3_out, undriven_4, undriven_8);
  or or_4 (or_4_out, undriven_14, undriven_15);
  D_Flip_Flop d_ff_1 (
    .clk(undriven_21), .D(undriven_17), .Q(d_ff_1_q), .Qn(d_ff_1_qn), .en(undriven_18), .reset(undriven_24));  // open: preset
  and and_1 (and_1_out, undriven_22, undriven_19);
  and and_2 (and_2_out, undriven_20, undriven_23);
  D_Flip_Flop d_ff_2 (
    .clk(undriven_27), .D(undriven_25), .Q(d_ff_2_q), .Qn(d_ff_2_qn), .en(undriven_26), .reset(undriven_32));  // open: preset
  and and_3 (and_3_out, undriven_28, undriven_29);
  and and_4 (and_4_out, undriven_30, undriven_31);
  Multiplexer #(.width(8), .disabled(0), .enable("false")) multiplexer_1 (
    .in0(Read_Ram), .in1({or_131_out[7:4], or_131_out_2, or_131_out[0]}), .out(multiplexer_1_out),
    .sel(or_59_out));
  Multiplexer #(.width(8), .disabled(0), .enable("false")) multiplexer_2 (
    .in0(Read_Ram), .in1({4'b0000, or_131_out[11:8]}), .out(multiplexer_2_out), .sel(or_59_out));
  Multiplexer #(.width(8), .disabled(0), .enable("false")) multiplexer_3 (
    .in0(multiplexer_1_out), .in1(multiplexer_77_out), .out(multiplexer_3_out), .sel(c_out));
  Multiplexer #(.width(8), .disabled(0), .enable("false")) multiplexer_4 (
    .in0(multiplexer_2_out), .in1({4'b0000, multiplexer_77_out_2}), .out(multiplexer_4_out), .sel(c_out));
  LED led_1 (.in(register_19_q[3]));
  LED led_2 (.in(register_19_q[2]));
  Button On (.out(On_out));
  Clock clock_1 (.out(clock_1_out));
  Button Off (.out(Off_out));
  Counter #(.width(32), .max('hffffffff)) Clocks (
    .count(d_ff_12_q), .clk(clock_1_out), .clr(On_out));  // open: load, D, Q, carry
  Counter #(.width(32), .max('hffffffff)) u_Instruc (
    .count(decoder_14_out1), .clk(clock_1_out), .clr(On_out));  // open: load, D, Q, carry
  LED led_3 (.in(register_19_q[0]));
  LED led_4 (.in(register_19_q[1]));
  Decoder #(.select(4), .disabled(0)) decoder_1 (
    .out0(decoder_1_out0), .out1(decoder_1_out1), .out2(decoder_1_out2), .out3(decoder_1_out3),
    .out4(decoder_1_out4), .out5(decoder_1_out5), .out6(decoder_1_out6), .out7(decoder_1_out7),
    .out8(decoder_1_out8), .out9(decoder_1_out9), .out10(decoder_1_out10), .out11(decoder_1_out11),
    .out12(decoder_1_out12), .out13(decoder_1_out13), .out14(decoder_1_out14), .out15(decoder_1_out15),
    .sel(multiplexer_76_out[3:0]), .en(decoder_2_out15));
  Button On_2 (.out(On_2_out));
  or or_5 (or_5_out, Write_Ram, or_109_out);
  Decoder #(.select(4), .disabled(0)) decoder_2 (
    .out0(decoder_2_out0), .out1(decoder_2_out1), .out2(decoder_2_out2), .out3(decoder_2_out3),
    .out4(decoder_2_out4), .out5(decoder_2_out5), .out6(decoder_2_out6), .out7(decoder_2_out7),
    .out8(decoder_2_out8), .out9(decoder_2_out9), .out10(decoder_2_out10), .out11(decoder_2_out11),
    .out12(decoder_2_out12), .out13(decoder_2_out13), .out14(decoder_2_out14), .out15(decoder_2_out15),
    .sel(multiplexer_76_out[7:4]), .en(decoder_4_out15));
  or or_6 (or_6_out, in_13, or_69_out);
  Decoder #(.select(4), .disabled(0)) decoder_3 (
    .out0(decoder_3_out0), .out1(decoder_3_out1), .out2(decoder_3_out2), .out3(decoder_3_out3),
    .out4(decoder_3_out4), .out5(decoder_3_out5), .out6(decoder_3_out6), .out7(decoder_3_out7),
    .out8(decoder_3_out8), .out9(decoder_3_out9), .out10(decoder_3_out10), .out11(decoder_3_out11),
    .out12(decoder_3_out12), .out13(decoder_3_out13), .out14(decoder_3_out14), .out15(decoder_3_out15),
    .sel(multiplexer_76_out_2), .en(decoder_5_out2));
  Decoder #(.select(4), .disabled(0)) decoder_4 (
    .out0(decoder_4_out0), .out1(decoder_4_out1), .out2(decoder_4_out2), .out3(decoder_4_out3),
    .out4(decoder_4_out4), .out5(decoder_4_out5), .out6(decoder_4_out6), .out7(decoder_4_out7),
    .out8(decoder_4_out8), .out9(decoder_4_out9), .out10(decoder_4_out10), .out11(decoder_4_out11),
    .out12(decoder_4_out12), .out13(decoder_4_out13), .out14(decoder_4_out14), .out15(decoder_4_out15),
    .sel(multiplexer_76_out_2), .en(decoder_5_out15));
  Decoder #(.select(4), .disabled(0), .enable("false")) decoder_5 (
    .out0(decoder_5_out0), .out1(decoder_5_out1), .out2(decoder_5_out2), .out3(decoder_5_out3),
    .out4(decoder_5_out4), .out5(decoder_5_out5), .out6(decoder_5_out6), .out7(decoder_5_out7),
    .out8(decoder_5_out8), .out9(decoder_5_out9), .out10(decoder_5_out10), .out11(decoder_5_out11),
    .out12(decoder_5_out12), .out13(decoder_5_out13), .out14(decoder_5_out14), .out15(decoder_5_out15),
    .sel(multiplexer_76_out_3));
  Register u_Reg_0 (.D(multiplexer_3_out), .en(decoder_6_out0), .Q(Reg_0), .clk(clock_1_out));  // open: clr
  Register u_Reg_1 (.D(multiplexer_4_out), .en(decoder_6_out1), .Q(Reg_1), .clk(clock_1_out));  // open: clr
  Register u_Reg_2 (.D(multiplexer_3_out), .en(decoder_6_out2), .Q(Reg_2), .clk(clock_1_out));  // open: clr
  Register u_Reg_3 (.D(multiplexer_4_out), .en(decoder_6_out3), .Q(Reg_3), .clk(clock_1_out));  // open: clr
  Register u_Reg_4 (.D(multiplexer_3_out), .en(decoder_6_out4), .Q(Reg_4), .clk(clock_1_out));  // open: clr
  Register u_Reg_5 (.D(multiplexer_4_out), .en(decoder_6_out5), .Q(Reg_5), .clk(clock_1_out));  // open: clr
  Register u_Reg_6 (.D(multiplexer_3_out), .en(or_91_out), .Q(Reg_6), .clk(clock_1_out));  // open: clr
  Register u_Reg_7 (.D(multiplexer_4_out), .en(decoder_6_out7), .Q(Reg_7), .clk(clock_1_out));  // open: clr
  Register u_Reg_8 (.D(multiplexer_3_out), .en(or_90_out), .Q(Reg_8), .clk(clock_1_out));  // open: clr
  Register u_Reg_9 (.D(multiplexer_4_out), .en(or_89_out), .Q(Reg_9), .clk(clock_1_out));  // open: clr
  Register u_Reg_A (.D(multiplexer_3_out), .en(or_88_out), .Q(Reg_A), .clk(clock_1_out));  // open: clr
  Register u_Reg_B (.D(multiplexer_4_out), .en(or_86_out), .Q(Reg_B), .clk(clock_1_out));  // open: clr
  Register u_Reg_C (.D(multiplexer_3_out), .en(or_87_out), .Q(Reg_C), .clk(clock_1_out));  // open: clr
  Register u_Reg_D (.D(multiplexer_4_out), .en(or_84_out), .Q(Reg_D), .clk(clock_1_out));  // open: clr
  Register u_Reg_E (.D(multiplexer_3_out), .en(or_85_out), .Q(Reg_E), .clk(clock_1_out));  // open: clr
  Register u_Reg_F (.D(multiplexer_4_out), .en(or_83_out), .Q(Reg_F), .clk(clock_1_out));  // open: clr
  Multiplexer #(.width(8), .enable("false")) multiplexer_5 (
    .in0({8{1'b0}}), .in1(Reg_0), .out(multiplexer_5_out), .sel(decoder_7_out0));
  Multiplexer #(.width(8), .enable("false")) multiplexer_6 (
    .in0(multiplexer_5_out), .in1(Reg_1), .out(multiplexer_6_out), .sel(decoder_7_out1));
  Multiplexer #(.width(8), .enable("false")) multiplexer_7 (
    .in0(multiplexer_6_out), .in1(Reg_2), .out(multiplexer_7_out), .sel(decoder_7_out2));
  Multiplexer #(.width(8), .enable("false")) multiplexer_8 (
    .in0(multiplexer_7_out), .in1(Reg_3), .out(multiplexer_8_out), .sel(decoder_7_out3));
  Multiplexer #(.width(8), .enable("false")) multiplexer_9 (
    .in0(multiplexer_8_out), .in1(Reg_4), .out(multiplexer_9_out), .sel(decoder_7_out4));
  Multiplexer #(.width(8), .enable("false")) multiplexer_10 (
    .in0(multiplexer_9_out), .in1(Reg_5), .out(multiplexer_10_out), .sel(decoder_7_out5));
  Multiplexer #(.width(8), .enable("false")) multiplexer_11 (
    .in0(multiplexer_10_out), .in1(Reg_6), .out(multiplexer_11_out), .sel(or_92_out));
  Multiplexer #(.width(8), .enable("false")) multiplexer_12 (
    .in0(multiplexer_11_out), .in1(Reg_7), .out(multiplexer_12_out), .sel(decoder_7_out7));
  Multiplexer #(.width(8), .enable("false")) multiplexer_13 (
    .in0(multiplexer_12_out), .in1(Reg_8), .out(multiplexer_13_out), .sel(decoder_7_out8));
  Multiplexer #(.width(8), .enable("false")) multiplexer_14 (
    .in0(multiplexer_13_out), .in1(Reg_9), .out(multiplexer_14_out), .sel(decoder_7_out9));
  Multiplexer #(.width(8), .enable("false")) multiplexer_15 (
    .in0(multiplexer_14_out), .in1(Reg_A), .out(multiplexer_15_out), .sel(decoder_7_out10));
  Multiplexer #(.width(8), .enable("false")) multiplexer_16 (
    .in0(multiplexer_15_out), .in1(Reg_B), .out(multiplexer_16_out), .sel(decoder_7_out11));
  Multiplexer #(.width(8), .enable("false")) multiplexer_17 (
    .in0(multiplexer_16_out), .in1(Reg_C), .out(multiplexer_17_out), .sel(decoder_7_out12));
  Multiplexer #(.width(8), .enable("false")) multiplexer_18 (
    .in0(multiplexer_17_out), .in1(Reg_D), .out(multiplexer_18_out), .sel(decoder_7_out13));
  Multiplexer #(.width(8), .enable("false")) multiplexer_19 (
    .in0(multiplexer_18_out), .in1(Reg_E), .out(multiplexer_19_out), .sel(decoder_7_out14));
  Multiplexer #(.width(8), .enable("false")) multiplexer_20 (
    .in0(multiplexer_19_out), .in1(Reg_F), .out(multiplexer_20_out), .sel(decoder_7_out15));
  Decoder #(.select(4), .disabled(0)) decoder_6 (
    .out0(decoder_6_out0), .out1(decoder_6_out1), .out2(decoder_6_out2), .out3(decoder_6_out3),
    .out4(decoder_6_out4), .out5(decoder_6_out5), .out6(decoder_6_out6), .out7(decoder_6_out7),
    .out8(decoder_6_out8), .out9(decoder_6_out9), .out10(decoder_6_out10), .out11(decoder_6_out11),
    .out12(decoder_6_out12), .out13(decoder_6_out13), .out14(decoder_6_out14), .out15(decoder_6_out15),
    .sel(multiplexer_21_out), .en(or_37_out));
  Multiplexer #(.width(4), .enable("false")) multiplexer_21 (
    .in0(multiplexer_76_out_2), .in1(multiplexer_76_out[7:4]), .out(multiplexer_21_out), .sel(or_39_out));
  Decoder #(.select(4), .disabled(0)) decoder_7 (
    .out0(decoder_7_out0), .out1(decoder_7_out1), .out2(decoder_7_out2), .out3(decoder_7_out3),
    .out4(decoder_7_out4), .out5(decoder_7_out5), .out6(decoder_7_out6), .out7(decoder_7_out7),
    .out8(decoder_7_out8), .out9(decoder_7_out9), .out10(decoder_7_out10), .out11(decoder_7_out11),
    .out12(decoder_7_out12), .out13(decoder_7_out13), .out14(decoder_7_out14), .out15(decoder_7_out15),
    .sel(multiplexer_22_out), .en(or_7_out));
  Multiplexer #(.width(4), .enable("false")) multiplexer_22 (
    .in0(multiplexer_76_out[7:4]), .in1(multiplexer_76_out_2), .out(multiplexer_22_out), .sel(_3_out));
  Decoder #(.select(4), .disabled(0)) decoder_8 (
    .out0(decoder_8_out0), .out1(decoder_8_out1), .out2(decoder_8_out2), .out3(decoder_8_out3),
    .out4(decoder_8_out4), .out5(decoder_8_out5), .out6(decoder_8_out6), .out7(decoder_8_out7),
    .out8(decoder_8_out8), .out9(decoder_8_out9), .out10(decoder_8_out10), .out11(decoder_8_out11),
    .out12(decoder_8_out12), .out13(decoder_8_out13), .out14(decoder_8_out14), .out15(decoder_8_out15),
    .sel(multiplexer_23_out), .en(or_8_out));
  Multiplexer #(.width(4), .enable("false")) multiplexer_23 (
    .in0(multiplexer_76_out[3:0]), .in1(4'b0000), .out(multiplexer_23_out), .sel(1'b0));
  Decoder #(.select(4), .disabled(0)) decoder_9 (
    .out0(decoder_9_out0), .out1(decoder_9_out1), .out2(decoder_9_out2), .out3(decoder_9_out3),
    .out4(decoder_9_out4), .out5(decoder_9_out5), .out6(decoder_9_out6), .out7(decoder_9_out7),
    .out8(decoder_9_out8), .out9(decoder_9_out9), .out10(decoder_9_out10), .out11(decoder_9_out11),
    .out12(decoder_9_out12), .out13(decoder_9_out13), .out14(decoder_9_out14), .out15(decoder_9_out15),
    .sel(multiplexer_24_out), .en(or_70_out));
  Multiplexer #(.width(4), .enable("false")) multiplexer_24 (
    .in0(multiplexer_76_out_2), .in1(multiplexer_76_out[7:4]), .out(multiplexer_24_out), .sel(f0_out));
  Decoder #(.select(4), .disabled(0)) decoder_10 (
    .out0(decoder_10_out0), .out1(decoder_10_out1), .out2(decoder_10_out2), .out3(decoder_10_out3),
    .out4(decoder_10_out4), .out5(decoder_10_out5), .out6(decoder_10_out6), .out7(decoder_10_out7),
    .out8(decoder_10_out8), .out9(decoder_10_out9), .out10(decoder_10_out10), .out11(decoder_10_out11),
    .out12(decoder_10_out12), .out13(decoder_10_out13), .out14(decoder_10_out14), .out15(decoder_10_out15),
    .sel(multiplexer_25_out), .en(or_52_out));
  Multiplexer #(.width(4), .enable("false")) multiplexer_25 (
    .in0(multiplexer_76_out[3:0]), .in1(4'b0000), .out(multiplexer_25_out), .sel(1'b0));
  Decoder #(.select(4), .disabled(0)) decoder_11 (
    .out0(decoder_11_out0), .out1(decoder_11_out1), .out2(decoder_11_out2), .out3(decoder_11_out3),
    .out4(decoder_11_out4), .out5(decoder_11_out5), .out6(decoder_11_out6), .out7(decoder_11_out7),
    .out8(decoder_11_out8), .out9(decoder_11_out9), .out10(decoder_11_out10), .out11(decoder_11_out11),
    .out12(decoder_11_out12), .out13(decoder_11_out13), .out14(decoder_11_out14), .out15(decoder_11_out15),
    .sel(multiplexer_26_out), .en(or_22_out));
  Multiplexer #(.width(4), .enable("false")) multiplexer_26 (
    .in0(multiplexer_76_out[7:4]), .in1(4'b0000), .out(multiplexer_26_out), .sel(1'b0));
  and _0 (_0_out, decoder_5_out0, decoder_14_out5);
  and _1 (_1_out, decoder_5_out1, decoder_14_out5);
  and _20 (_20_out, decoder_3_out0, decoder_14_out5);
  and _21 (_21_out, decoder_3_out1, decoder_14_out5);
  and _22 (_22_out, decoder_3_out2, decoder_14_out5);
  and _23 (_23_out, decoder_3_out3, decoder_14_out5);
  and _24 (_24_out, decoder_3_out4, decoder_14_out5);
  and _25 (_25_out, decoder_3_out5, decoder_14_out5);
  and _26 (_26_out, decoder_3_out6, decoder_14_out5);
  and _27 (_27_out, decoder_3_out7, decoder_14_out5);
  and _28 (_28_out, decoder_3_out8, decoder_14_out5);
  and _29 (_29_out, decoder_3_out9, decoder_14_out5);
  and _2a (_2a_out, decoder_3_out10, decoder_14_out5);
  and _2b (_2b_out, decoder_3_out11, decoder_14_out5);
  and _3 (_3_out, decoder_5_out3, decoder_14_out5);
  and _4 (_4_out, decoder_5_out4, decoder_14_out5);
  and _5 (_5_out, decoder_5_out5, decoder_14_out5);
  and _6 (_6_out, decoder_5_out6, decoder_14_out5);
  and _7 (_7_out, decoder_5_out7, decoder_14_out5);
  and _8 (_8_out, decoder_5_out8, decoder_14_out5);
  and _9 (_9_out, decoder_5_out9, decoder_14_out5);
  and a (a_out, decoder_5_out10, decoder_14_out5);
  and b (b_out, decoder_5_out11, decoder_14_out5);
  and c (c_out, decoder_5_out12, decoder_14_out5);
  and d (d_out, decoder_5_out13, decoder_14_out5);
  and e (e_out, decoder_5_out14, decoder_14_out5);
  and f0 (f0_out, decoder_4_out0, decoder_14_out5);
  and and_5 (and_5_out, decoder_4_out0, decoder_14_out4);
  and f1 (f1_out, decoder_4_out1, decoder_14_out5);
  and and_6 (and_6_out, decoder_4_out1, decoder_14_out4);
  and fe (fe_out, decoder_4_out14, decoder_14_out5);
  and fffe (fffe_out, decoder_1_out14, decoder_14_out5);
  and ffff (ffff_out, decoder_1_out15, decoder_14_out5);
  Multiplexer #(.width(8), .enable("false")) multiplexer_27 (
    .in0({8{1'b0}}), .in1(Reg_0), .out(multiplexer_27_out), .sel(decoder_8_out0));
  Multiplexer #(.width(8), .enable("false")) multiplexer_28 (
    .in0(multiplexer_27_out), .in1(Reg_1), .out(multiplexer_28_out), .sel(decoder_8_out1));
  Multiplexer #(.width(8), .enable("false")) multiplexer_29 (
    .in0(multiplexer_28_out), .in1(Reg_2), .out(multiplexer_29_out), .sel(decoder_8_out2));
  Multiplexer #(.width(8), .enable("false")) multiplexer_30 (
    .in0(multiplexer_29_out), .in1(Reg_3), .out(multiplexer_30_out), .sel(decoder_8_out3));
  Multiplexer #(.width(8), .enable("false")) multiplexer_31 (
    .in0(multiplexer_30_out), .in1(Reg_4), .out(multiplexer_31_out), .sel(decoder_8_out4));
  Multiplexer #(.width(8), .enable("false")) multiplexer_32 (
    .in0(multiplexer_31_out), .in1(Reg_5), .out(multiplexer_32_out), .sel(decoder_8_out5));
  Multiplexer #(.width(8), .enable("false")) multiplexer_33 (
    .in0(multiplexer_32_out), .in1(Reg_6), .out(multiplexer_33_out), .sel(decoder_8_out6));
  Multiplexer #(.width(8), .enable("false")) multiplexer_34 (
    .in0(multiplexer_33_out), .in1(Reg_7), .out(multiplexer_34_out), .sel(decoder_8_out7));
  Multiplexer #(.width(8), .enable("false")) multiplexer_35 (
    .in0(multiplexer_34_out), .in1(Reg_8), .out(multiplexer_35_out), .sel(decoder_8_out8));
  Multiplexer #(.width(8), .enable("false")) multiplexer_36 (
    .in0(multiplexer_35_out), .in1(Reg_9), .out(multiplexer_36_out), .sel(decoder_8_out9));
  Multiplexer #(.width(8), .enable("false")) multiplexer_37 (
    .in0(multiplexer_36_out), .in1(Reg_A), .out(multiplexer_37_out), .sel(decoder_8_out10));
  Multiplexer #(.width(8), .enable("false")) multiplexer_38 (
    .in0(multiplexer_37_out), .in1(Reg_B), .out(multiplexer_38_out), .sel(decoder_8_out11));
  Multiplexer #(.width(8), .enable("false")) multiplexer_39 (
    .in0(multiplexer_38_out), .in1(Reg_C), .out(multiplexer_39_out), .sel(decoder_8_out12));
  Multiplexer #(.width(8), .enable("false")) multiplexer_40 (
    .in0(multiplexer_39_out), .in1(Reg_D), .out(multiplexer_40_out), .sel(decoder_8_out13));
  Multiplexer #(.width(8), .enable("false")) multiplexer_41 (
    .in0(multiplexer_40_out), .in1(Reg_E), .out(multiplexer_41_out), .sel(decoder_8_out14));
  Multiplexer #(.width(8), .enable("false")) multiplexer_42 (
    .in0(multiplexer_41_out), .in1(Reg_F), .out(multiplexer_42_out), .sel(decoder_8_out15));
  or or_7 (or_7_out, _0_out, or_38_out);
  or or_8 (or_8_out, _1_out, or_9_out);
  or or_9 (or_9_out, _20_out, or_10_out);
  or or_10 (or_10_out, _21_out, or_11_out);
  or or_11 (or_11_out, _22_out, or_12_out);
  or or_12 (or_12_out, _23_out, or_13_out);
  or or_13 (or_13_out, _24_out, or_14_out);
  or or_14 (or_14_out, _25_out, or_15_out);
  or or_15 (or_15_out, _26_out, or_16_out);
  or or_16 (or_16_out, _27_out, or_20_out);
  or or_17 (or_17_out, _28_out, or_18_out);
  or or_18 (or_18_out, _29_out, or_19_out);
  or or_19 (or_19_out, _2a_out, or_50_out);
  or or_20 (or_20_out, _2b_out, 1'b0);
  or or_21 (or_21_out, _3_out, or_79_out);
  or or_22 (or_22_out, _4_out, or_23_out);
  or or_23 (or_23_out, _5_out, 1'b0);
  or or_24 (or_24_out, _6_out, or_25_out);
  or or_25 (or_25_out, _7_out, or_27_out);
  or or_26 (or_26_out, _8_out, and_6_out);
  or or_27 (or_27_out, _9_out, or_28_out);
  or or_28 (or_28_out, a_out, or_29_out);
  or or_29 (or_29_out, b_out, or_30_out);
  or or_30 (or_30_out, c_out, or_31_out);
  or or_31 (or_31_out, d_out, e_out);
  or or_32 (or_32_out, f0_out, or_33_out);
  or or_33 (or_33_out, and_5_out, or_34_out);
  or or_34 (or_34_out, f1_out, and_6_out);
  or or_35 (or_35_out, and_6_out, undriven_33);
  or or_36 (or_36_out, fe_out, undriven_34);
  Multiplexer #(.width(8), .enable("false")) multiplexer_43 (
    .in0({8{1'b0}}), .in1(Reg_0), .out(multiplexer_43_out), .sel(decoder_9_out0));
  Multiplexer #(.width(8), .enable("false")) multiplexer_44 (
    .in0(multiplexer_43_out), .in1(Reg_1), .out(multiplexer_44_out), .sel(decoder_9_out1));
  Multiplexer #(.width(8), .enable("false")) multiplexer_45 (
    .in0(multiplexer_44_out), .in1(Reg_2), .out(multiplexer_45_out), .sel(decoder_9_out2));
  Multiplexer #(.width(8), .enable("false")) multiplexer_46 (
    .in0(multiplexer_45_out), .in1(Reg_3), .out(multiplexer_46_out), .sel(decoder_9_out3));
  Multiplexer #(.width(8), .enable("false")) multiplexer_47 (
    .in0(multiplexer_46_out), .in1(Reg_4), .out(multiplexer_47_out), .sel(decoder_9_out4));
  Multiplexer #(.width(8), .enable("false")) multiplexer_48 (
    .in0(multiplexer_47_out), .in1(Reg_5), .out(multiplexer_48_out), .sel(decoder_9_out5));
  Multiplexer #(.width(8), .enable("false")) multiplexer_49 (
    .in0(multiplexer_48_out), .in1(Reg_6), .out(multiplexer_49_out), .sel(or_93_out));
  Multiplexer #(.width(8), .enable("false")) multiplexer_50 (
    .in0(multiplexer_49_out), .in1(Reg_7), .out(multiplexer_50_out), .sel(decoder_9_out7));
  Multiplexer #(.width(8), .enable("false")) multiplexer_51 (
    .in0(multiplexer_50_out), .in1(Reg_8), .out(multiplexer_51_out), .sel(decoder_9_out8));
  Multiplexer #(.width(8), .enable("false")) multiplexer_52 (
    .in0(multiplexer_51_out), .in1(Reg_9), .out(multiplexer_52_out), .sel(decoder_9_out9));
  Multiplexer #(.width(8), .enable("false")) multiplexer_53 (
    .in0(multiplexer_52_out), .in1(Reg_A), .out(multiplexer_53_out), .sel(decoder_9_out10));
  Multiplexer #(.width(8), .enable("false")) multiplexer_54 (
    .in0(multiplexer_53_out), .in1(Reg_B), .out(multiplexer_54_out), .sel(decoder_9_out11));
  Multiplexer #(.width(8), .enable("false")) multiplexer_55 (
    .in0(multiplexer_54_out), .in1(Reg_C), .out(multiplexer_55_out), .sel(decoder_9_out12));
  Multiplexer #(.width(8), .enable("false")) multiplexer_56 (
    .in0(multiplexer_55_out), .in1(Reg_D), .out(multiplexer_56_out), .sel(decoder_9_out13));
  Multiplexer #(.width(8), .enable("false")) multiplexer_57 (
    .in0(multiplexer_56_out), .in1(Reg_E), .out(multiplexer_57_out), .sel(decoder_9_out14));
  Multiplexer #(.width(8), .enable("false")) multiplexer_58 (
    .in0(multiplexer_57_out), .in1(Reg_F), .out(multiplexer_58_out), .sel(decoder_9_out15));
  Register #(.width(12)) u_PC (.D(multiplexer_97_out), .en(or_106_out), .Q(PC), .clk(clock_1_out), .clr(or_124_out));
  Register #(.width(16)) Ins_Acc (
    .D(multiplexer_196_out), .en(decoder_14_out1), .Q(Instruc), .clk(clock_1_out));  // open: clr
  or or_37 (or_37_out, _0_out, or_61_out);
  or or_38 (or_38_out, _1_out, or_42_out);
  or or_39 (or_39_out, _20_out, or_40_out);
  or or_40 (or_40_out, _21_out, or_41_out);
  or or_41 (or_41_out, _22_out, or_65_out);
  or or_42 (or_42_out, _23_out, or_44_out);
  or or_43 (or_43_out, _24_out, or_67_out);
  or or_44 (or_44_out, _25_out, or_45_out);
  or or_45 (or_45_out, _26_out, or_46_out);
  or or_46 (or_46_out, _27_out, or_51_out);
  or or_47 (or_47_out, _28_out, or_48_out);
  or or_48 (or_48_out, _29_out, or_49_out);
  or or_49 (or_49_out, _2a_out, or_68_out);
  or or_50 (or_50_out, _2b_out, and_6_out);
  or or_51 (or_51_out, _3_out, 1'b0);
  or or_52 (or_52_out, _4_out, or_53_out);
  or or_53 (or_53_out, _5_out, 1'b0);
  or or_54 (or_54_out, _6_out, _7_out);
  or or_55 (or_55_out, _9_out, and_6_out);
  or or_56 (or_56_out, a_out, f0_out);
  or or_57 (or_57_out, b_out, or_58_out);
  or or_58 (or_58_out, c_out, or_73_out);
  and and_7 (and_7_out, d_out, nand_5_out);
  and and_8 (and_8_out, e_out, Carry_q[7]);
  or or_59 (or_59_out, and_5_out, f1_out);
  or or_60 (or_60_out, fe_out, undriven_35);
  Multiplexer #(.width(8), .enable("false")) multiplexer_59 (
    .in0({8{1'b0}}), .in1(Reg_0), .out(multiplexer_59_out), .sel(decoder_10_out0));
  Multiplexer #(.width(8), .enable("false")) multiplexer_60 (
    .in0(multiplexer_59_out), .in1(Reg_1), .out(multiplexer_60_out), .sel(decoder_10_out1));
  Multiplexer #(.width(8), .enable("false")) multiplexer_61 (
    .in0(multiplexer_60_out), .in1(Reg_2), .out(multiplexer_61_out), .sel(decoder_10_out2));
  Multiplexer #(.width(8), .enable("false")) multiplexer_62 (
    .in0(multiplexer_61_out), .in1(Reg_3), .out(multiplexer_62_out), .sel(decoder_10_out3));
  Multiplexer #(.width(8), .enable("false")) multiplexer_63 (
    .in0(multiplexer_62_out), .in1(Reg_4), .out(multiplexer_63_out), .sel(decoder_10_out4));
  Multiplexer #(.width(8), .enable("false")) multiplexer_64 (
    .in0(multiplexer_63_out), .in1(Reg_5), .out(multiplexer_64_out), .sel(decoder_10_out5));
  Multiplexer #(.width(8), .enable("false")) multiplexer_65 (
    .in0(multiplexer_64_out), .in1(Reg_6), .out(multiplexer_65_out), .sel(decoder_10_out6));
  Multiplexer #(.width(8), .enable("false")) multiplexer_66 (
    .in0(multiplexer_65_out), .in1(Reg_7), .out(multiplexer_66_out), .sel(or_94_out));
  Multiplexer #(.width(8), .enable("false")) multiplexer_67 (
    .in0(multiplexer_66_out), .in1(Reg_8), .out(multiplexer_67_out), .sel(decoder_10_out8));
  Multiplexer #(.width(8), .enable("false")) multiplexer_68 (
    .in0(multiplexer_67_out), .in1(Reg_9), .out(multiplexer_68_out), .sel(decoder_10_out9));
  Multiplexer #(.width(8), .enable("false")) multiplexer_69 (
    .in0(multiplexer_68_out), .in1(Reg_A), .out(multiplexer_69_out), .sel(decoder_10_out10));
  Multiplexer #(.width(8), .enable("false")) multiplexer_70 (
    .in0(multiplexer_69_out), .in1(Reg_B), .out(multiplexer_70_out), .sel(decoder_10_out11));
  Multiplexer #(.width(8), .enable("false")) multiplexer_71 (
    .in0(multiplexer_70_out), .in1(Reg_C), .out(multiplexer_71_out), .sel(decoder_10_out12));
  Multiplexer #(.width(8), .enable("false")) multiplexer_72 (
    .in0(multiplexer_71_out), .in1(Reg_D), .out(multiplexer_72_out), .sel(decoder_10_out13));
  Multiplexer #(.width(8), .enable("false")) multiplexer_73 (
    .in0(multiplexer_72_out), .in1(Reg_E), .out(multiplexer_73_out), .sel(decoder_10_out14));
  Multiplexer #(.width(8), .enable("false")) multiplexer_74 (
    .in0(multiplexer_73_out), .in1(Reg_F), .out(multiplexer_74_out), .sel(decoder_10_out15));
  Multiplexer #(.width(12), .enable("false")) multiplexer_75 (
    .in0({12{1'b0}}), .in1(PC), .out(multiplexer_75_out), .sel(decoder_14_out1));
  Multiplexer #(.width(16), .enable("false")) multiplexer_76 (
    .in0({16{1'b0}}), .in1(Instruc), .out({multiplexer_76_out_3, multiplexer_76_out_2, multiplexer_76_out}),
    .sel(or_122_out));
  or or_61 (or_61_out, _1_out, or_62_out);
  or or_62 (or_62_out, _20_out, or_63_out);
  or or_63 (or_63_out, _21_out, or_64_out);
  or or_64 (or_64_out, _22_out, or_77_out);
  or or_65 (or_65_out, _23_out, or_43_out);
  or or_66 (or_66_out, _24_out, or_78_out);
  or or_67 (or_67_out, _25_out, or_17_out);
  or or_68 (or_68_out, _2b_out, or_21_out);
  or or_69 (or_69_out, _4_out, or_71_out);
  or or_70 (or_70_out, _5_out, f0_out);
  or or_71 (or_71_out, _6_out, or_55_out);
  or or_72 (or_72_out, _7_out, a_out);
  or or_73 (or_73_out, and_7_out, or_74_out);
  or or_74 (or_74_out, and_8_out, fffe_out);
  or or_75 (or_75_out, and_5_out, f1_out);
  or or_76 (or_76_out, fe_out, undriven_36);
  Multiplexer #(.width(12), .enable("false")) multiplexer_77 (
    .in0({12{1'b0}}), .in1(PC), .out({multiplexer_77_out_2, multiplexer_77_out}), .sel(or_105_out));
  Multiplexer #(.width(16), .enable("false")) multiplexer_78 (
    .in0({16{1'b0}}), .in1(Instruc), .out(multiplexer_78_out), .sel(or_24_out));
  Multiplexer #(.width(8), .enable("false")) multiplexer_79 (
    .in0(Adr_In[7:0]), .in1(Reg_0), .out(multiplexer_79_out), .sel(decoder_11_out0));
  Multiplexer #(.width(8), .enable("false")) multiplexer_80 (
    .in0({4'b0000, Adr_In[11:8]}), .in1(Reg_1), .out(multiplexer_80_out), .sel(decoder_11_out0));
  Multiplexer #(.width(8), .enable("false")) multiplexer_81 (
    .in0(multiplexer_79_out), .in1(Reg_2), .out(multiplexer_81_out), .sel(decoder_11_out2));
  Multiplexer #(.width(8), .enable("false")) multiplexer_82 (
    .in0(multiplexer_80_out), .in1(Reg_3), .out(multiplexer_82_out), .sel(decoder_11_out2));
  Multiplexer #(.width(8), .enable("false")) multiplexer_83 (
    .in0(multiplexer_81_out), .in1(Reg_4), .out(multiplexer_83_out), .sel(decoder_11_out4));
  Multiplexer #(.width(8), .enable("false")) multiplexer_84 (
    .in0(multiplexer_82_out), .in1(Reg_5), .out(multiplexer_84_out), .sel(decoder_11_out4));
  Multiplexer #(.width(8), .enable("false")) multiplexer_85 (
    .in0(multiplexer_83_out), .in1(Reg_6), .out(multiplexer_85_out), .sel(decoder_11_out6));
  Multiplexer #(.width(8), .enable("false")) multiplexer_86 (
    .in0(multiplexer_84_out), .in1(Reg_7), .out(multiplexer_86_out), .sel(decoder_11_out6));
  Multiplexer #(.width(8), .enable("false")) multiplexer_87 (
    .in0(multiplexer_85_out), .in1(Reg_8), .out(multiplexer_87_out), .sel(decoder_11_out8));
  Multiplexer #(.width(8), .enable("false")) multiplexer_88 (
    .in0(multiplexer_86_out), .in1(Reg_9), .out(multiplexer_88_out), .sel(decoder_11_out8));
  Multiplexer #(.width(8), .enable("false")) multiplexer_89 (
    .in0(multiplexer_87_out), .in1(Reg_A), .out(multiplexer_89_out), .sel(or_95_out));
  Multiplexer #(.width(8), .enable("false")) multiplexer_90 (
    .in0(multiplexer_88_out), .in1(Reg_B), .out(multiplexer_90_out), .sel(or_95_out));
  Multiplexer #(.width(8), .enable("false")) multiplexer_91 (
    .in0(multiplexer_89_out), .in1(Reg_C), .out(multiplexer_91_out), .sel(or_96_out));
  Multiplexer #(.width(8), .enable("false")) multiplexer_92 (
    .in0(multiplexer_90_out), .in1(Reg_D), .out(multiplexer_92_out), .sel(or_96_out));
  Multiplexer #(.width(8), .enable("false")) multiplexer_93 (
    .in0(multiplexer_91_out), .in1(Reg_E), .out(multiplexer_93_out), .sel(decoder_11_out14));
  Multiplexer #(.width(8), .enable("false")) multiplexer_94 (
    .in0(multiplexer_92_out), .in1(Reg_F), .out(multiplexer_94_out), .sel(decoder_11_out14));
  or or_77 (or_77_out, _23_out, or_66_out);
  or or_78 (or_78_out, _25_out, or_47_out);
  or or_79 (or_79_out, _4_out, or_26_out);
  or or_80 (or_80_out, _5_out, or_82_out);
  or or_81 (or_81_out, _6_out, _9_out);
  or or_82 (or_82_out, _7_out, or_56_out);
  Multiplexer #(.width(12), .enable("false")) multiplexer_95 (
    .in0({12{1'b0}}), .in1(PC), .out(multiplexer_95_out), .sel(or_110_out));
  Multiplexer #(.width(16), .enable("false")) multiplexer_96 (
    .in0({16{1'b0}}), .in1(Instruc), .out(multiplexer_96_out), .sel(_8_out));
  Multiplexer #(.width(12), .enable("false")) multiplexer_97 (
    .in0(or_104_out), .in1(adder_1_out), .out(multiplexer_97_out), .sel(or_110_out));
  or or_83 (or_83_out, decoder_6_out15, 1'b0);
  Multiplexer #(.width(12), .enable("false")) multiplexer_98 (
    .in0(12'h2), .in1(12'hffe), .out(multiplexer_98_out), .sel(decoder_12_out6));
  Multiplexer #(.width(16), .enable("false")) multiplexer_99 (
    .in0({16{1'b0}}), .in1(Instruc), .out(multiplexer_99_out), .sel(_3_out));
  or or_84 (or_84_out, decoder_6_out13, c_out);
  or or_85 (or_85_out, decoder_6_out14, 1'b0);
  Adder #(.width(12)) adder_1 (.a(multiplexer_98_out), .b(multiplexer_95_out), .out(adder_1_out));  // open: cin, cout
  or or_86 (or_86_out, decoder_6_out11, or_75_out);
  or or_87 (or_87_out, decoder_6_out12, c_out);
  or or_88 (or_88_out, decoder_6_out10, or_75_out);
  or or_89 (or_89_out, decoder_6_out9, 1'b0);
  Button button_1 (.out(button_1_out));
  or or_90 (or_90_out, decoder_6_out8, 1'b0);
  or or_91 (or_91_out, decoder_6_out6, or_81_out);
  LED led_5 (.in(register_1_q[1]));
  LED led_6 (.in(register_1_q[6]));
  LED led_7 (.in(register_1_q[6]));
  LED led_8 (.in(register_1_q[6]));
  LED led_9 (.in(register_1_q[7]));
  LED led_10 (.in(register_1_q[5]));
  LED led_11 (.in(register_1_q[5]));
  LED led_12 (.in(register_1_q[5]));
  LED led_13 (.in(register_1_q[4]));
  LED led_14 (.in(d_ff_6_q));
  LED led_15 (.in(register_1_q[1]));
  LED led_16 (.in(register_1_q[1]));
  LED led_17 (.in(register_1_q[2]));
  LED led_18 (.in(register_1_q[2]));
  LED led_19 (.in(register_1_q[2]));
  LED led_20 (.in(register_1_q[7]));
  LED led_21 (.in(register_1_q[7]));
  LED led_22 (.in(register_1_q[3]));
  LED led_23 (.in(register_1_q[3]));
  LED led_24 (.in(register_1_q[3]));
  LED led_25 (.in(register_1_q[4]));
  LED led_26 (.in(register_1_q[4]));
  Register register_1 (.D(register_4_q), .en(or_126_out), .Q(register_1_q), .clk(d_ff_3_q));  // open: clr
  or or_92 (or_92_out, decoder_7_out6, d_out);
  LED led_27 (.in(register_2_q[1]));
  LED led_28 (.in(register_2_q[1]));
  LED led_29 (.in(register_2_q[1]));
  LED led_30 (.in(register_2_q[6]));
  LED led_31 (.in(register_2_q[6]));
  LED led_32 (.in(register_2_q[7]));
  LED led_33 (.in(register_2_q[6]));
  LED led_34 (.in(register_2_q[7]));
  LED led_35 (.in(register_2_q[7]));
  LED led_36 (.in(register_2_q[5]));
  LED led_37 (.in(register_2_q[5]));
  LED led_38 (.in(register_2_q[5]));
  LED led_39 (.in(register_2_q[4]));
  LED led_40 (.in(register_2_q[4]));
  LED led_41 (.in(register_2_q[4]));
  Register register_2 (.D(register_3_q), .en(or_126_out), .Q(register_2_q), .clk(d_ff_3_q));  // open: clr
  LED led_42 (.in(register_2_q[2]));
  LED led_43 (.in(register_2_q[2]));
  LED led_44 (.in(register_2_q[2]));
  LED led_45 (.in(register_2_q[3]));
  LED led_46 (.in(register_2_q[3]));
  LED led_47 (.in(register_2_q[3]));
  LED led_48 (.in(register_4_q[1]));
  LED led_49 (.in(register_4_q[1]));
  LED led_50 (.in(register_4_q[1]));
  LED led_51 (.in(register_4_q[2]));
  LED led_52 (.in(register_4_q[6]));
  LED led_53 (.in(register_4_q[6]));
  LED led_54 (.in(register_4_q[2]));
  LED led_55 (.in(register_4_q[7]));
  LED led_56 (.in(register_4_q[7]));
  LED led_57 (.in(register_4_q[7]));
  LED led_58 (.in(register_4_q[6]));
  LED led_59 (.in(register_4_q[2]));
  LED led_60 (.in(register_4_q[3]));
  LED led_61 (.in(register_4_q[5]));
  LED led_62 (.in(register_4_q[3]));
  LED led_63 (.in(register_4_q[5]));
  LED led_64 (.in(register_4_q[3]));
  LED led_65 (.in(register_4_q[5]));
  LED led_66 (.in(register_4_q[4]));
  LED led_67 (.in(register_4_q[4]));
  LED led_68 (.in(register_4_q[4]));
  LED led_69 (.in(register_3_q[1]));
  LED led_70 (.in(register_3_q[1]));
  LED led_71 (.in(register_3_q[6]));
  LED led_72 (.in(register_3_q[6]));
  LED led_73 (.in(register_3_q[7]));
  LED led_74 (.in(register_3_q[7]));
  LED led_75 (.in(register_3_q[6]));
  LED led_76 (.in(register_3_q[5]));
  LED led_77 (.in(register_3_q[5]));
  LED led_78 (.in(register_3_q[5]));
  LED led_79 (.in(register_3_q[4]));
  LED led_80 (.in(register_3_q[4]));
  Register register_3 (.D(register_6_q), .en(or_126_out), .Q(register_3_q), .clk(d_ff_3_q));  // open: clr
  Register register_4 (.D(register_5_q), .en(or_126_out), .Q(register_4_q), .clk(d_ff_3_q));  // open: clr
  LED led_81 (.in(register_3_q[1]));
  LED led_82 (.in(register_3_q[2]));
  LED led_83 (.in(register_3_q[2]));
  LED led_84 (.in(register_3_q[2]));
  LED led_85 (.in(register_3_q[7]));
  LED led_86 (.in(register_3_q[3]));
  LED led_87 (.in(register_3_q[3]));
  LED led_88 (.in(register_3_q[3]));
  LED led_89 (.in(register_3_q[4]));
  or or_93 (or_93_out, decoder_9_out6, or_72_out);
  LED led_90 (.in(register_5_q[1]));
  LED led_91 (.in(register_5_q[1]));
  LED led_92 (.in(register_5_q[1]));
  LED led_93 (.in(register_5_q[6]));
  LED led_94 (.in(register_5_q[6]));
  LED led_95 (.in(register_5_q[7]));
  LED led_96 (.in(register_5_q[7]));
  LED led_97 (.in(register_5_q[7]));
  LED led_98 (.in(register_5_q[6]));
  LED led_99 (.in(register_5_q[5]));
  LED led_100 (.in(register_5_q[5]));
  LED led_101 (.in(register_5_q[5]));
  LED led_102 (.in(register_5_q[4]));
  LED led_103 (.in(register_5_q[4]));
  LED led_104 (.in(register_5_q[4]));
  LED led_105 (.in(register_6_q[1]));
  LED led_106 (.in(register_6_q[6]));
  LED led_107 (.in(register_5_q[2]));
  LED led_108 (.in(register_6_q[6]));
  LED led_109 (.in(register_5_q[2]));
  LED led_110 (.in(register_6_q[6]));
  LED led_111 (.in(register_6_q[7]));
  LED led_112 (.in(register_5_q[2]));
  LED led_113 (.in(register_5_q[3]));
  LED led_114 (.in(register_6_q[5]));
  LED led_115 (.in(register_6_q[5]));
  LED led_116 (.in(register_5_q[3]));
  LED led_117 (.in(register_5_q[3]));
  LED led_118 (.in(register_6_q[5]));
  LED led_119 (.in(register_6_q[4]));
  Register register_5 (.D(register_7_q), .en(or_126_out), .Q(register_5_q), .clk(d_ff_3_q));  // open: clr
  or or_94 (or_94_out, decoder_10_out7, or_54_out);
  LED led_120 (.in(register_6_q[1]));
  LED led_121 (.in(register_6_q[1]));
  LED led_122 (.in(register_6_q[2]));
  LED led_123 (.in(register_6_q[2]));
  LED led_124 (.in(register_6_q[2]));
  LED led_125 (.in(register_6_q[7]));
  LED led_126 (.in(register_6_q[7]));
  LED led_127 (.in(register_6_q[3]));
  LED led_128 (.in(register_6_q[3]));
  LED led_129 (.in(register_6_q[3]));
  LED led_130 (.in(register_6_q[4]));
  LED led_131 (.in(register_6_q[4]));
  Register register_6 (.D(register_8_q), .en(or_126_out), .Q(register_6_q), .clk(d_ff_3_q));  // open: clr
  or or_95 (or_95_out, decoder_11_out10, or_32_out);
  LED led_132 (.in(register_7_q[1]));
  LED led_133 (.in(register_7_q[1]));
  LED led_134 (.in(register_7_q[6]));
  LED led_135 (.in(register_7_q[6]));
  LED led_136 (.in(register_7_q[7]));
  LED led_137 (.in(register_7_q[7]));
  LED led_138 (.in(register_7_q[6]));
  LED led_139 (.in(register_7_q[5]));
  LED led_140 (.in(register_7_q[5]));
  LED led_141 (.in(register_7_q[5]));
  LED led_142 (.in(register_7_q[4]));
  LED led_143 (.in(register_7_q[4]));
  or or_96 (or_96_out, decoder_11_out12, fffe_out);
  LED led_144 (.in(register_7_q[1]));
  LED led_145 (.in(register_7_q[2]));
  LED led_146 (.in(register_7_q[2]));
  LED led_147 (.in(register_7_q[2]));
  LED led_148 (.in(register_7_q[7]));
  LED led_149 (.in(register_7_q[3]));
  LED led_150 (.in(register_7_q[3]));
  LED led_151 (.in(register_7_q[3]));
  LED led_152 (.in(register_7_q[4]));
  Register register_7 (.D(register_9_q), .en(or_126_out), .Q(register_7_q), .clk(d_ff_3_q));  // open: clr
  or or_97 (or_97_out, multiplexer_20_out[7], multiplexer_20_out[6], multiplexer_20_out[5], multiplexer_20_out[4], multiplexer_20_out[3], multiplexer_20_out[2], multiplexer_20_out[1], multiplexer_20_out[0]);
  Multiplexer #(.width(8), .enable("false")) multiplexer_100 (
    .in0(multiplexer_42_out), .in1(multiplexer_99_out[7:0]), .out(multiplexer_100_out), .sel(_3_out));
  LED led_153 (.in(register_8_q[1]));
  LED led_154 (.in(register_8_q[1]));
  LED led_155 (.in(register_8_q[1]));
  LED led_156 (.in(register_8_q[6]));
  LED led_157 (.in(register_8_q[2]));
  LED led_158 (.in(register_8_q[6]));
  LED led_159 (.in(register_8_q[2]));
  LED led_160 (.in(register_8_q[7]));
  LED led_161 (.in(register_8_q[7]));
  LED led_162 (.in(register_8_q[7]));
  LED led_163 (.in(register_8_q[2]));
  LED led_164 (.in(register_8_q[6]));
  LED led_165 (.in(register_8_q[3]));
  LED led_166 (.in(register_8_q[5]));
  LED led_167 (.in(register_8_q[3]));
  LED led_168 (.in(register_8_q[5]));
  LED led_169 (.in(register_8_q[3]));
  LED led_170 (.in(register_8_q[5]));
  LED led_171 (.in(register_8_q[4]));
  LED led_172 (.in(register_8_q[4]));
  LED led_173 (.in(register_8_q[4]));
  Register register_8 (.D(register_10_q), .en(or_126_out), .Q(register_8_q), .clk(d_ff_3_q));  // open: clr
  Adder adder_2 (
    .a(multiplexer_20_out), .b(multiplexer_100_out), .out(adder_2_out), .cin(_20_out), .cout(adder_2_cout));
  assign not_1_out = ~multiplexer_100_out;  // NOT_Gate not_1, 8 bits wide
  assign xor_1_out = multiplexer_20_out ^ multiplexer_100_out;  // XOR_Gate xor_1, 8 bits wide
  Adder adder_3 (.a(multiplexer_20_out), .b(not_1_out), .out(adder_3_out), .cin(_25_out));  // open: cout
  Multiplier multiplier_1 (
    .a(multiplexer_20_out), .b(multiplexer_100_out), .out(multiplier_1_out), .cout(multiplier_1_cout));  // open: cin
  Divider divider_1 (
    .a(multiplexer_20_out), .b(multiplexer_100_out), .out(divider_1_out), .rem(divider_1_rem));  // open: upper
  LED led_174 (.in(register_9_q[1]));
  LED led_175 (.in(register_9_q[6]));
  LED led_176 (.in(register_9_q[6]));
  LED led_177 (.in(register_9_q[6]));
  LED led_178 (.in(register_9_q[7]));
  LED led_179 (.in(register_9_q[5]));
  LED led_180 (.in(register_9_q[5]));
  LED led_181 (.in(register_9_q[5]));
  LED led_182 (.in(register_9_q[4]));
  nand nand_5 (nand_5_out, or_97_out, or_97_out);
  Multiplexer #(.enable("false")) multiplexer_101 (
    .in0(adder_2_cout), .in1(multiplexer_100_out[7]), .out(multiplexer_101_out), .sel(_22_out));
  or or_98 (or_98_out, multiplexer_101_out, multiplexer_102_out);
  LED led_183 (.in(register_9_q[1]));
  LED led_184 (.in(register_9_q[1]));
  LED led_185 (.in(register_9_q[2]));
  LED led_186 (.in(register_9_q[2]));
  LED led_187 (.in(register_9_q[7]));
  LED led_188 (.in(register_9_q[2]));
  LED led_189 (.in(register_9_q[7]));
  LED led_190 (.in(register_9_q[3]));
  LED led_191 (.in(register_9_q[3]));
  LED led_192 (.in(register_9_q[3]));
  LED led_193 (.in(register_9_q[4]));
  LED led_194 (.in(register_9_q[4]));
  Register register_9 (.D(register_12_q), .en(or_126_out), .Q(register_9_q), .clk(d_ff_3_q));  // open: clr
  Multiplexer #(.enable("false")) multiplexer_102 (
    .in0(1'b0), .in1(multiplexer_100_out[0]), .out(multiplexer_102_out), .sel(_24_out));
  Multiplexer #(.width(8), .enable("false")) multiplexer_103 (
    .in0(multiplier_1_cout), .in1(divider_1_rem), .out(multiplexer_103_out), .sel(_27_out));
  Multiplexer #(.width(8), .enable("false")) multiplexer_104 (
    .in0(multiplier_1_out), .in1(divider_1_out), .out(multiplexer_104_out), .sel(_27_out));
  LED led_195 (.in(register_10_q[1]));
  LED led_196 (.in(register_10_q[1]));
  LED led_197 (.in(register_10_q[1]));
  LED led_198 (.in(register_10_q[6]));
  LED led_199 (.in(register_10_q[6]));
  LED led_200 (.in(register_10_q[7]));
  LED led_201 (.in(register_10_q[7]));
  LED led_202 (.in(register_10_q[6]));
  LED led_203 (.in(register_10_q[7]));
  LED led_204 (.in(register_10_q[5]));
  LED led_205 (.in(register_10_q[5]));
  LED led_206 (.in(register_10_q[5]));
  LED led_207 (.in(register_10_q[4]));
  LED led_208 (.in(register_10_q[4]));
  LED led_209 (.in(register_10_q[4]));
  Register register_10 (.D(register_11_q), .en(or_126_out), .Q(register_10_q), .clk(d_ff_3_q));  // open: clr
  LED led_210 (.in(register_10_q[2]));
  LED led_211 (.in(register_10_q[2]));
  LED led_212 (.in(register_10_q[2]));
  LED led_213 (.in(register_10_q[3]));
  LED led_214 (.in(register_10_q[3]));
  LED led_215 (.in(register_10_q[3]));
  LED led_216 (.in(register_12_q[1]));
  LED led_217 (.in(register_12_q[1]));
  LED led_218 (.in(register_12_q[1]));
  LED led_219 (.in(register_12_q[6]));
  LED led_220 (.in(register_12_q[2]));
  LED led_221 (.in(register_12_q[2]));
  LED led_222 (.in(register_12_q[6]));
  LED led_223 (.in(register_12_q[7]));
  LED led_224 (.in(register_12_q[7]));
  LED led_225 (.in(register_12_q[7]));
  LED led_226 (.in(register_12_q[2]));
  LED led_227 (.in(register_12_q[6]));
  LED led_228 (.in(register_12_q[3]));
  LED led_229 (.in(register_12_q[5]));
  LED led_230 (.in(register_12_q[3]));
  LED led_231 (.in(register_12_q[5]));
  LED led_232 (.in(register_12_q[5]));
  LED led_233 (.in(register_12_q[3]));
  LED led_234 (.in(register_12_q[4]));
  LED led_235 (.in(register_12_q[4]));
  LED led_236 (.in(register_12_q[4]));
  or or_99 (or_99_out, _1_out, _3_out, _20_out);
  or or_100 (or_100_out, _20_out, _24_out, _3_out, _22_out, _1_out);
  or or_101 (or_101_out, _26_out, _27_out);
  LED led_237 (.in(register_11_q[1]));
  LED led_238 (.in(register_11_q[1]));
  LED led_239 (.in(register_11_q[6]));
  LED led_240 (.in(register_11_q[6]));
  LED led_241 (.in(register_11_q[7]));
  LED led_242 (.in(register_11_q[6]));
  LED led_243 (.in(register_11_q[7]));
  LED led_244 (.in(register_11_q[5]));
  LED led_245 (.in(register_11_q[5]));
  LED led_246 (.in(register_11_q[5]));
  LED led_247 (.in(register_11_q[4]));
  LED led_248 (.in(register_11_q[4]));
  Register register_11 (.D(register_14_q), .en(or_126_out), .Q(register_11_q), .clk(d_ff_3_q));  // open: clr
  Register register_12 (.D(register_13_q), .en(or_126_out), .Q(register_12_q), .clk(d_ff_3_q));  // open: clr
  Multiplexer #(.width(8), .enable("false")) multiplexer_105 (
    .in0({8{1'b0}}), .in1({multiplexer_100_out[6:0], 1'b0}), .out(multiplexer_105_out), .sel(_22_out));
  Multiplexer #(.width(8), .enable("false")) multiplexer_106 (
    .in0(multiplexer_105_out), .in1({1'b0, multiplexer_100_out[7:1]}), .out(multiplexer_106_out),
    .sel(_24_out));
  Multiplexer #(.width(8), .enable("false")) multiplexer_107 (
    .in0(multiplexer_106_out), .in1(multiplexer_20_out), .out(multiplexer_107_out), .sel(_0_out));
  Multiplexer #(.width(8), .enable("false")) multiplexer_108 (
    .in0(multiplexer_107_out), .in1(adder_2_out), .out(multiplexer_108_out), .sel(or_99_out));
  Multiplexer #(.width(8), .enable("false")) multiplexer_109 (
    .in0(multiplexer_108_out), .in1(not_1_out), .out(multiplexer_109_out), .sel(_21_out));
  Multiplexer #(.width(8), .enable("false")) multiplexer_110 (
    .in0(multiplexer_109_out), .in1(xor_1_out), .out(multiplexer_110_out), .sel(_23_out));
  Multiplexer #(.width(8), .enable("false")) multiplexer_111 (
    .in0(multiplexer_110_out), .in1(adder_3_out), .out(multiplexer_111_out), .sel(_25_out));
  Multiplexer #(.width(8), .enable("false")) multiplexer_112 (
    .in0(multiplexer_111_out), .in1({8{Carry_q[7]}}), .out(multiplexer_112_out), .sel(_2a_out));
  Multiplexer #(.width(8), .enable("false")) multiplexer_113 (
    .in0(multiplexer_112_out), .in1({8{multiplexer_100_out[7]}}), .out(multiplexer_113_out), .sel(_2b_out));
  D_Flip_Flop #(.trigger("falling")) Carry (
    .clk(decoder_14_out5), .D(or_98_out), .Q(Carry_q[7]), .en(or_100_out));  // open: Qn, preset, reset
  Multiplexer #(.width(8), .enable("false")) multiplexer_114 (
    .in0(multiplexer_113_out), .in1(Hi_q), .out(multiplexer_114_out), .sel(_28_out));
  Register Hi (.D(multiplexer_103_out), .en(or_101_out), .Q(Hi_q), .clk(clock_1_out));  // open: clr
  Multiplexer #(.width(8), .enable("false")) multiplexer_115 (
    .in0(multiplexer_114_out), .in1(Lo_q), .out(multiplexer_115_out), .sel(_29_out));
  Register Lo (.D(multiplexer_104_out), .en(or_101_out), .Q(Lo_q), .clk(clock_1_out));  // open: clr
  LED led_249 (.in(register_11_q[1]));
  LED led_250 (.in(register_11_q[2]));
  LED led_251 (.in(register_11_q[2]));
  LED led_252 (.in(register_11_q[2]));
  LED led_253 (.in(register_11_q[7]));
  LED led_254 (.in(register_11_q[3]));
  LED led_255 (.in(register_11_q[3]));
  LED led_256 (.in(register_11_q[3]));
  LED led_257 (.in(register_11_q[4]));
  LED led_258 (.in(register_13_q[1]));
  LED led_259 (.in(register_13_q[1]));
  LED led_260 (.in(register_13_q[1]));
  LED led_261 (.in(register_13_q[6]));
  LED led_262 (.in(register_13_q[6]));
  LED led_263 (.in(register_13_q[7]));
  LED led_264 (.in(register_13_q[7]));
  LED led_265 (.in(register_13_q[7]));
  LED led_266 (.in(register_13_q[6]));
  LED led_267 (.in(register_13_q[5]));
  LED led_268 (.in(register_13_q[5]));
  LED led_269 (.in(register_13_q[5]));
  LED led_270 (.in(register_13_q[4]));
  LED led_271 (.in(register_13_q[4]));
  LED led_272 (.in(register_13_q[4]));
  LED led_273 (.in(register_14_q[1]));
  LED led_274 (.in(register_14_q[6]));
  LED led_275 (.in(register_13_q[2]));
  LED led_276 (.in(register_14_q[6]));
  LED led_277 (.in(register_13_q[2]));
  LED led_278 (.in(register_14_q[7]));
  LED led_279 (.in(register_14_q[6]));
  LED led_280 (.in(register_13_q[2]));
  LED led_281 (.in(register_13_q[3]));
  LED led_282 (.in(register_14_q[5]));
  LED led_283 (.in(register_14_q[5]));
  LED led_284 (.in(register_13_q[3]));
  LED led_285 (.in(register_14_q[5]));
  LED led_286 (.in(register_13_q[3]));
  LED led_287 (.in(register_14_q[4]));
  Register register_13 (.D(register_15_q), .en(or_126_out), .Q(register_13_q), .clk(d_ff_3_q));  // open: clr
  LED led_288 (.in(register_14_q[1]));
  LED led_289 (.in(register_14_q[1]));
  LED led_290 (.in(register_14_q[2]));
  LED led_291 (.in(register_14_q[2]));
  LED led_292 (.in(register_14_q[7]));
  LED led_293 (.in(register_14_q[2]));
  LED led_294 (.in(register_14_q[7]));
  LED led_295 (.in(register_14_q[3]));
  LED led_296 (.in(register_14_q[3]));
  LED led_297 (.in(register_14_q[3]));
  LED led_298 (.in(register_14_q[4]));
  LED led_299 (.in(register_14_q[4]));
  Register register_14 (.D(register_16_q), .en(or_126_out), .Q(register_14_q), .clk(d_ff_3_q));  // open: clr
  LED led_300 (.in(register_15_q[1]));
  LED led_301 (.in(register_15_q[1]));
  LED led_302 (.in(register_15_q[6]));
  LED led_303 (.in(register_15_q[6]));
  LED led_304 (.in(register_15_q[7]));
  LED led_305 (.in(register_15_q[7]));
  LED led_306 (.in(register_15_q[6]));
  LED led_307 (.in(register_15_q[5]));
  LED led_308 (.in(register_15_q[5]));
  LED led_309 (.in(register_15_q[5]));
  LED led_310 (.in(register_15_q[4]));
  LED led_311 (.in(register_15_q[4]));
  LED led_312 (.in(register_15_q[1]));
  LED led_313 (.in(register_15_q[2]));
  LED led_314 (.in(register_15_q[2]));
  LED led_315 (.in(register_15_q[7]));
  LED led_316 (.in(register_15_q[2]));
  LED led_317 (.in(register_15_q[3]));
  LED led_318 (.in(register_15_q[3]));
  LED led_319 (.in(register_15_q[3]));
  LED led_320 (.in(register_15_q[4]));
  Register register_15 (.D(multiplexer_135_out), .en(or_126_out), .Q(register_15_q), .clk(d_ff_3_q));  // open: clr
  LED led_321 (.in(register_16_q[1]));
  LED led_322 (.in(register_16_q[1]));
  LED led_323 (.in(register_16_q[1]));
  LED led_324 (.in(register_16_q[6]));
  LED led_325 (.in(register_16_q[2]));
  LED led_326 (.in(register_16_q[2]));
  LED led_327 (.in(register_16_q[6]));
  LED led_328 (.in(register_16_q[7]));
  LED led_329 (.in(register_16_q[6]));
  LED led_330 (.in(register_16_q[7]));
  LED led_331 (.in(register_16_q[7]));
  LED led_332 (.in(register_16_q[2]));
  LED led_333 (.in(register_16_q[3]));
  LED led_334 (.in(register_16_q[5]));
  LED led_335 (.in(register_16_q[3]));
  LED led_336 (.in(register_16_q[5]));
  LED led_337 (.in(register_16_q[3]));
  LED led_338 (.in(register_16_q[5]));
  LED led_339 (.in(register_16_q[4]));
  LED led_340 (.in(register_16_q[4]));
  LED led_341 (.in(register_16_q[4]));
  Register register_16 (.D(multiplexer_136_out), .en(or_126_out), .Q(register_16_q), .clk(d_ff_3_q));  // open: clr
  assign or_102_out = {multiplexer_94_out[3:0], multiplexer_93_out} | multiplexer_75_out;  // OR_Gate or_102, 12 bits wide
  assign or_103_out = or_102_out | multiplexer_78_out[11:0];  // OR_Gate or_103, 12 bits wide
  D_Flip_Flop d_ff_3 (
    .clk(clock_1_out), .D(or_5_out), .Q(d_ff_3_q), .en(or_5_out), .reset(or_6_out));  // open: Qn, preset
  assign or_104_out = multiplexer_120_out | or_103_out;  // OR_Gate or_104, 12 bits wide
  Multiplexer #(.width(12), .enable("false")) multiplexer_116 (
    .in0({12{1'b0}}), .in1(12'hef2), .out(multiplexer_116_out), .sel(or_107_out));
  Multiplexer #(.width(12), .enable("false")) multiplexer_117 (
    .in0(multiplexer_116_out), .in1(12'hef3), .out(multiplexer_117_out), .sel(or_111_out));
  Multiplexer #(.width(12), .enable("false")) multiplexer_118 (
    .in0(multiplexer_117_out), .in1(12'hef0), .out(multiplexer_118_out), .sel(or_112_out));
  Multiplexer #(.width(12), .enable("false")) multiplexer_119 (
    .in0(multiplexer_118_out), .in1(12'hef1), .out(multiplexer_119_out), .sel(or_108_out));
  Multiplexer #(.width(12), .enable("false")) multiplexer_120 (
    .in0(multiplexer_119_out), .in1(12'hef4), .out(multiplexer_120_out), .sel(or_113_out));
  Multiplexer #(.width(8), .enable("false")) multiplexer_121 (
    .in0({8{1'b0}}), .in1(8'h3), .out(multiplexer_121_out), .sel(button_1_out));
  Register #(.trigger("high")) Exc_Code (
    .D(multiplexer_121_out), .en(button_1_out), .Q(Exc_Code_q), .clk(button_1_out), .clr(decoder_13_out15));
  Register Exc_Data (
    .D({in_1, in_2, in_3, Keyboard_IN, in_5, in_6, in_7, in_8}), .en(button_1_out), .Q(Exc_Data_q),
    .clk(button_1_out), .clr(decoder_13_out15));
  Multiplexer #(.width(8), .enable("false")) multiplexer_122 (
    .in0({8{1'b0}}), .in1({4'b1011, multiplexer_77_out_2}), .out(multiplexer_122_out), .sel(or_107_out));
  Multiplexer #(.width(8), .enable("false")) multiplexer_123 (
    .in0(multiplexer_122_out), .in1(multiplexer_77_out), .out(multiplexer_123_out), .sel(or_111_out));
  Multiplexer #(.width(8), .enable("false")) multiplexer_124 (
    .in0(multiplexer_123_out), .in1(Exc_Code_q), .out(multiplexer_124_out), .sel(or_112_out));
  Multiplexer #(.width(8), .enable("false")) multiplexer_125 (
    .in0(multiplexer_124_out), .in1(Exc_Data_q), .out(multiplexer_125_out), .sel(or_108_out));
  or or_105 (or_105_out, or_114_out, c_out);
  or or_106 (or_106_out, decoder_12_out6, or_116_out);
  or or_107 (or_107_out, decoder_13_out3, decoder_13_out2);
  or or_108 (or_108_out, decoder_13_out12, decoder_13_out11);
  or or_109 (or_109_out, or_115_out, or_80_out);
  and and_9 (and_9_out, d_ff_17_q, decoder_14_out5);
  and and_10 (and_10_out, ~d_ff_17_q, decoder_12_out14);  // AND_Gate
  or or_110 (or_110_out, decoder_12_out6, decoder_14_out1);
  or or_111 (or_111_out, decoder_13_out5, decoder_13_out6);
  or or_112 (or_112_out, decoder_13_out8, decoder_13_out9);
  or or_113 (or_113_out, decoder_13_out13, decoder_13_out14);
  or or_114 (or_114_out, decoder_13_out2, decoder_13_out3, decoder_13_out5, decoder_13_out6);
  or or_115 (or_115_out, decoder_13_out3, decoder_13_out6, decoder_13_out9, decoder_13_out12);
  or or_116 (or_116_out, decoder_13_out14, or_118_out);
  D_Flip_Flop d_ff_4 (
    .clk(clock_1_out), .D(and_9_out), .Q(d_ff_4_q), .Qn(d_ff_4_qn), .en(and_9_out), .reset(and_10_out));  // open: preset
  D_Flip_Flop d_ff_5 (
    .clk(clock_1_out), .D(and_9_out), .Q(d_ff_5_q), .Qn(d_ff_5_qn), .en(and_9_out), .reset(decoder_12_out14));  // open: preset
  Decoder #(.select(4), .disabled(0), .enable("false")) decoder_12 (
    .out0(decoder_12_out0), .out1(decoder_12_out1), .out2(decoder_12_out2), .out3(decoder_12_out3),
    .out4(decoder_12_out4), .out5(decoder_12_out5), .out6(decoder_12_out6), .out7(decoder_12_out7),
    .out8(decoder_12_out8), .out9(decoder_12_out9), .out10(decoder_12_out10), .out11(decoder_12_out11),
    .out12(decoder_12_out12), .out13(decoder_12_out13), .out14(decoder_12_out14), .out15(decoder_12_out15),
    .sel(demultiplexer_1_out1));
  Decoder #(.select(4), .disabled(0), .enable("false")) decoder_13 (
    .out0(decoder_13_out0), .out1(decoder_13_out1), .out2(decoder_13_out2), .out3(decoder_13_out3),
    .out4(decoder_13_out4), .out5(decoder_13_out5), .out6(decoder_13_out6), .out7(decoder_13_out7),
    .out8(decoder_13_out8), .out9(decoder_13_out9), .out10(decoder_13_out10), .out11(decoder_13_out11),
    .out12(decoder_13_out12), .out13(decoder_13_out13), .out14(decoder_13_out14), .out15(decoder_13_out15),
    .sel(demultiplexer_1_out0));
  D_Flip_Flop d_ff_6 (
    .clk(clock_1_out), .D(and_12_out), .Q(d_ff_6_q), .en(and_12_out), .reset(and_11_out));  // open: Qn, preset
  and and_11 (and_11_out, and_18_out, decoder_14_out5);
  Demultiplexer #(.width(4), .enable("false")) demultiplexer_1 (
    .out0(demultiplexer_1_out0), .out1(demultiplexer_1_out1), .in(demultiplexer_2_out1), .sel(or_121_out));
  or or_117 (or_117_out, or_5_out, decoder_15_out1);
  and and_12 (and_12_out, button_1_out, ~d_ff_6_q);  // AND_Gate
  or or_118 (or_118_out, decoder_14_out1, or_57_out);
  and and_13 (and_13_out, clock_1_out, decoder_14_out1);
  D_Flip_Flop d_ff_7 (
    .clk(clock_1_out), .D(and_12_out), .Q(d_ff_7_q), .en(and_12_out), .reset(decoder_13_out1));  // open: Qn, preset
  or or_119 (or_119_out, On_out, decoder_13_out15);
  Multiplexer #(.width(16), .disabled(0), .enable("false")) multiplexer_126 (
    .in0(16'hff), .in1(16'hfff), .out(multiplexer_126_out), .sel(in_9));
  D_Flip_Flop d_ff_8 (
    .clk(clock_1_out), .D(On_2_out), .Q(d_ff_8_q), .Qn(d_ff_8_qn), .en(undriven_37), .reset(undriven_38));  // open: preset
  Register #(.width(16)) register_17 (
    .D(adder_4_out), .en(decoder_15_out2), .Q(out_20), .clk(clock_1_out), .clr(and_14_out));
  D_Flip_Flop d_ff_9 (
    .clk(and_13_out), .D(d_ff_7_q), .Q(d_ff_9_q), .Qn(d_ff_9_qn), .en(d_ff_7_q), .reset(or_119_out));  // open: preset
  Multiplexer #(.width(16), .enable("false")) multiplexer_127 (
    .in0({16{1'b0}}), .in1(out_20), .out(multiplexer_127_out), .sel(or_123_out));
  or or_120 (or_120_out, d_ff_4_q, d_ff_9_q);
  or or_121 (or_121_out, d_ff_9_qn, d_ff_4_q);
  D_Flip_Flop d_ff_10 (
    .clk(clock_1_out), .D(d_ff_8_q), .Q(d_ff_10_q), .Qn(d_ff_10_qn), .en(d_ff_8_q), .reset(and_14_out));  // open: preset
  Decoder #(.select(4), .disabled(0), .enable("false")) decoder_14 (
    .out0(decoder_14_out0), .out1(decoder_14_out1), .out2(decoder_14_out2), .out3(decoder_14_out3),
    .out4(decoder_14_out4), .out5(decoder_14_out5), .out6(decoder_14_out6), .out7(decoder_14_out7),
    .out8(decoder_14_out8), .out9(decoder_14_out9), .out10(decoder_14_out10), .out11(decoder_14_out11),
    .out12(decoder_14_out12), .out13(decoder_14_out13), .out14(decoder_14_out14), .out15(decoder_14_out15),
    .sel(demultiplexer_2_out0));
  or or_122 (or_122_out, decoder_14_out4, decoder_14_out5);
  Register #(.width(2)) register_18 (
    .D(adder_5_out), .en(d_ff_10_q), .Q(register_18_q), .clk(clock_1_out), .clr(and_14_out));
  Decoder #(.select(2), .disabled(0)) decoder_15 (
    .out0(decoder_15_out0), .out1(decoder_15_out1), .out2(decoder_15_out2), .out3(decoder_15_out3),
    .sel(register_18_q), .en(d_ff_10_q));
  or or_123 (or_123_out, decoder_15_out1, decoder_15_out2);
  and and_14 (and_14_out, decoder_15_out2, nand_6_out);
  Multiplexer #(.width(16), .enable("false")) multiplexer_128 (
    .in0({16{1'b0}}), .in1(out_20), .out(multiplexer_128_out), .sel(decoder_15_out2));
  Demultiplexer #(.width(4), .enable("false")) demultiplexer_2 (
    .out0(demultiplexer_2_out0), .out1(demultiplexer_2_out1), .in(register_19_q), .sel(or_120_out));
  Multiplexer #(.width(2), .disabled(0), .enable("false")) multiplexer_129 (
    .in0(2'b00), .in1(2'b10), .out(multiplexer_129_out), .sel(decoder_15_out2));
  nand nand_6 (nand_6_out, or_125_out, or_125_out);
  Adder #(.width(16)) adder_4 (
    .a({16{1'b0}}), .b(multiplexer_128_out), .out(adder_4_out), .cin(decoder_15_out2));  // open: cout
  D_Flip_Flop d_ff_11 (.clk(clock_1_out), .D(On_out), .Q(d_ff_11_q));  // open: Qn, preset, en, reset
  or or_124 (or_124_out, Off_out, ffff_out);
  Multiplexer #(.width(4), .enable("false")) multiplexer_130 (
    .in0(4'b0000), .in1(4'b0011), .out(multiplexer_130_out), .sel(decoder_14_out1));
  Multiplexer #(.width(4), .enable("false")) multiplexer_131 (
    .in0(multiplexer_130_out), .in1(4'b0010), .out(multiplexer_131_out), .sel(and_15_out));
  and and_15 (and_15_out, multiplexer_196_out[12], multiplexer_196_out[13], multiplexer_196_out[14], multiplexer_196_out[15], decoder_14_out1);
  Adder #(.width(2)) adder_5 (.a(multiplexer_129_out), .b(register_18_q), .out(adder_5_out), .cin(1'b1));  // open: cout
  or or_125 (or_125_out, xor_2_out[0], xor_2_out[1], xor_2_out[2], xor_2_out[3], xor_2_out[4], xor_2_out[5], xor_2_out[6], xor_2_out[7], xor_2_out[8], xor_2_out[9], xor_2_out[10], xor_2_out[11], xor_2_out[12], xor_2_out[13], xor_2_out[14], xor_2_out[15]);
  D_Flip_Flop d_ff_12 (
    .clk(clock_1_out), .D(d_ff_11_q), .Q(d_ff_12_q), .en(d_ff_11_q), .reset(or_124_out));  // open: Qn, preset
  Multiplexer #(.width(4), .enable("false")) multiplexer_132 (
    .in0(multiplexer_131_out), .in1(4'b1011), .out(multiplexer_132_out), .sel(decoder_14_out5));
  and and_16 (and_16_out, adder_7_out[11], adder_7_out[10], adder_7_out[9], adder_7_out[7], adder_7_out[6], adder_7_out[5], adder_7_out[4], adder_7_out[1]);
  and and_17 (and_17_out, ~adder_7_out[8], adder_7_out[3], adder_7_out[2]);  // AND_Gate
  Adder #(.width(4)) adder_6 (.a(multiplexer_132_out), .b(register_19_q), .out(adder_6_out), .cin(1'b1));  // open: cout
  assign xor_2_out = multiplexer_126_out ^ multiplexer_127_out;  // XOR_Gate xor_2, 16 bits wide
  RAM #(.addrWidth(16), .bus("separate")) ram_1 (
    .addr(multiplexer_127_out), .data(ram_1_data), .str(1'b0), .clk(clock_1_out), .ld(or_123_out));  // open: din, sel, clr
  or or_126 (or_126_out, and_20_out, or_133_out[0]);
  and and_18 (and_18_out, ~adder_7_out[2], ~adder_7_out[3], ~adder_7_out[0], and_16_out);  // AND_Gate
  and and_19 (or_133_out[0], ~adder_7_out[0], and_17_out, and_16_out);  // AND_Gate
  and and_20 (and_20_out, and_16_out, adder_7_out[0], and_17_out);
  Register #(.width(4)) register_19 (
    .D(adder_6_out), .en(d_ff_12_q), .Q(register_19_q), .clk(clock_1_out), .clr(or_124_out));
  Multiplexer #(.width(8), .enable("false")) multiplexer_133 (
    .in0({8{1'b0}}), .in1(ram_1_data), .out(multiplexer_133_out), .sel(or_123_out));
  assign or_127_out = multiplexer_58_out | multiplexer_125_out;  // OR_Gate or_127, 8 bits wide
  assign Read_Ram = multiplexer_180_out | or_132_out;  // OR_Gate or_128, 8 bits wide
  assign or_129_out = Data_In | or_130_out;  // OR_Gate or_129, 8 bits wide
  assign or_130_out = multiplexer_133_out | or_127_out;  // OR_Gate or_130, 8 bits wide
  assign {or_131_out[11:4], or_131_out_2, or_131_out[0]} = multiplexer_127_out[11:0] | adder_7_out;  // OR_Gate or_131, 12 bits wide
  assign or_132_out = multiplexer_115_out | multiplexer_96_out[7:0];  // OR_Gate or_132, 8 bits wide
  or or_133 (or_133_out[1], decoder_16_out0, decoder_16_out2, decoder_16_out3, decoder_16_out5, decoder_16_out6, decoder_16_out7, decoder_16_out8, decoder_16_out9, decoder_16_out10, decoder_16_out12, decoder_16_out14, decoder_16_out15);
  or or_134 (or_133_out[3], decoder_16_out0, decoder_16_out1, decoder_16_out3, decoder_16_out4, decoder_16_out5, decoder_16_out6, decoder_16_out7, decoder_16_out8, decoder_16_out9, decoder_16_out10, decoder_16_out11, decoder_16_out13);
  or or_135 (or_133_out[5], decoder_16_out0, decoder_16_out2, decoder_16_out6, decoder_16_out8, decoder_16_out10, decoder_16_out11, decoder_16_out12, decoder_16_out13, decoder_16_out14, decoder_16_out15);
  or or_136 (or_133_out[7], decoder_16_out2, decoder_16_out3, decoder_16_out4, decoder_16_out5, decoder_16_out6, decoder_16_out8, decoder_16_out9, decoder_16_out10, decoder_16_out11, decoder_16_out13, decoder_16_out14, decoder_16_out15);
  Multiplexer #(.width(12), .enable("false")) multiplexer_134 (
    .in0({4'b0000, multiplexer_74_out}), .in1({12{1'b1}}), .out(multiplexer_134_out), .sel(and_5_out));
  Multiplexer #(.width(8), .enable("false")) multiplexer_135 (
    .in0(or_127_out), .in1(or_133_out), .out(multiplexer_135_out), .sel(or_133_out[0]));
  Decoder #(.select(4), .disabled(0)) decoder_16 (
    .out0(decoder_16_out0), .out1(decoder_16_out1), .out2(decoder_16_out2), .out3(decoder_16_out3),
    .out4(decoder_16_out4), .out5(decoder_16_out5), .out6(decoder_16_out6), .out7(decoder_16_out7),
    .out8(decoder_16_out8), .out9(decoder_16_out9), .out10(decoder_16_out10), .out11(decoder_16_out11),
    .out12(decoder_16_out12), .out13(decoder_16_out13), .out14(decoder_16_out14), .out15(decoder_16_out15),
    .sel(or_127_out[7:4]), .en(or_133_out[0]));
  Adder #(.width(12)) adder_7 (.a(or_104_out), .b(multiplexer_134_out), .out(adder_7_out), .cin(f1_out));  // open: cout
  or or_137 (or_133_out[2], decoder_16_out0, decoder_16_out1, decoder_16_out2, decoder_16_out3, decoder_16_out4, decoder_16_out7, decoder_16_out8, decoder_16_out9, decoder_16_out10, decoder_16_out13);
  or or_138 (or_133_out[4], decoder_16_out0, decoder_16_out2, decoder_16_out3, decoder_16_out5, decoder_16_out6, decoder_16_out8, decoder_16_out9, decoder_16_out11, decoder_16_out12, decoder_16_out13, decoder_16_out14);
  or or_139 (or_133_out[6], decoder_16_out0, decoder_16_out4, decoder_16_out5, decoder_16_out6, decoder_16_out8, decoder_16_out9, decoder_16_out10, decoder_16_out11, decoder_16_out12, decoder_16_out14, decoder_16_out15);
  or or_140 (or_140_out[1], decoder_17_out0, decoder_17_out2, decoder_17_out3, decoder_17_out5, decoder_17_out6, decoder_17_out7, decoder_17_out8, decoder_17_out9, decoder_17_out10, decoder_17_out12, decoder_17_out14, decoder_17_out15);
  or or_141 (or_140_out[3], decoder_17_out0, decoder_17_out1, decoder_17_out3, decoder_17_out4, decoder_17_out5, decoder_17_out6, decoder_17_out7, decoder_17_out8, decoder_17_out9, decoder_17_out10, decoder_17_out11, decoder_17_out13);
  or or_142 (or_140_out[5], decoder_17_out0, decoder_17_out2, decoder_17_out6, decoder_17_out8, decoder_17_out10, decoder_17_out11, decoder_17_out12, decoder_17_out13, decoder_17_out14, decoder_17_out15);
  or or_143 (or_140_out[7], decoder_17_out2, decoder_17_out3, decoder_17_out4, decoder_17_out5, decoder_17_out6, decoder_17_out8, decoder_17_out9, decoder_17_out10, decoder_17_out11, decoder_17_out13, decoder_17_out14, decoder_17_out15);
  Multiplexer #(.width(8), .enable("false")) multiplexer_136 (
    .in0({8{1'b0}}), .in1({or_140_out, or_133_out[0]}), .out(multiplexer_136_out), .sel(or_133_out[0]));
  Decoder #(.select(4), .disabled(0)) decoder_17 (
    .out0(decoder_17_out0), .out1(decoder_17_out1), .out2(decoder_17_out2), .out3(decoder_17_out3),
    .out4(decoder_17_out4), .out5(decoder_17_out5), .out6(decoder_17_out6), .out7(decoder_17_out7),
    .out8(decoder_17_out8), .out9(decoder_17_out9), .out10(decoder_17_out10), .out11(decoder_17_out11),
    .out12(decoder_17_out12), .out13(decoder_17_out13), .out14(decoder_17_out14), .out15(decoder_17_out15),
    .sel(or_127_out[3:0]), .en(or_133_out[0]));
  or or_144 (or_140_out[2], decoder_17_out0, decoder_17_out1, decoder_17_out2, decoder_17_out3, decoder_17_out4, decoder_17_out7, decoder_17_out8, decoder_17_out9, decoder_17_out10, decoder_17_out13);
  or or_145 (or_140_out[4], decoder_17_out0, decoder_17_out2, decoder_17_out3, decoder_17_out5, decoder_17_out6, decoder_17_out8, decoder_17_out9, decoder_17_out11, decoder_17_out12, decoder_17_out13, decoder_17_out14);
  or or_146 (or_140_out[6], decoder_17_out0, decoder_17_out4, decoder_17_out5, decoder_17_out6, decoder_17_out8, decoder_17_out9, decoder_17_out10, decoder_17_out11, decoder_17_out12, decoder_17_out14, decoder_17_out15);
  or or_147 (or_147_out, or_117_out, or_6_out);
  Multiplexer #(.width(12), .enable("false")) multiplexer_137 (
    .in0({register_20_q, 4'b0000}), .in1({or_131_out[11:4], or_131_out_2, or_131_out[0]}),
    .out({multiplexer_137_out_2, multiplexer_137_out}), .sel(or_147_out));
  or or_148 (or_148_out, or_117_out, decoder_18_out2);
  and and_21 (and_21_out, or_149_out, or_150_out, or_151_out, or_152_out);
  Multiplexer #(.enable("false")) multiplexer_138 (
    .in0(decoder_14_out1), .in1(1'b0), .out(multiplexer_138_out), .sel(d_ff_17_q));
  Multiplexer #(.width(8), .enable("false")) multiplexer_139 (
    .in0(or_131_out[11:4]), .in1(register_20_q), .out(multiplexer_139_out), .sel(d_ff_17_q));
  D_Flip_Flop d_ff_13 (
    .clk(clock_1_out), .D(decoder_25_out0), .Q(d_ff_13_q), .Qn(d_ff_13_qn), .en(decoder_25_out0),
    .reset(and_22_out));  // open: preset
  and and_22 (and_22_out, or_148_out, and_26_out);
  D_Flip_Flop d_ff_14 (
    .clk(clock_1_out), .D(decoder_25_out1), .Q(d_ff_14_q), .Qn(d_ff_14_qn), .en(decoder_25_out1),
    .reset(and_23_out));  // open: preset
  and and_23 (and_23_out, or_148_out, and_27_out);
  D_Flip_Flop d_ff_15 (
    .clk(clock_1_out), .D(decoder_25_out2), .Q(d_ff_15_q), .Qn(d_ff_15_qn), .en(decoder_25_out2),
    .reset(and_24_out));  // open: preset
  and and_24 (and_24_out, or_148_out, and_28_out);
  D_Flip_Flop d_ff_16 (
    .clk(clock_1_out), .D(decoder_25_out3), .Q(d_ff_16_q), .Qn(d_ff_16_qn), .en(decoder_25_out3),
    .reset(and_25_out));  // open: preset
  and and_25 (and_25_out, or_148_out, and_29_out);
  D_Flip_Flop d_ff_17 (
    .clk(clock_1_out), .D(and_21_out), .Q(d_ff_17_q), .en(decoder_14_out1), .reset(decoder_18_out4));  // open: Qn, preset
  Register #(.trigger("high")) register_20 (
    .D(or_131_out[11:4]), .en(and_21_out), .Q(register_20_q), .clk(decoder_14_out1), .clr(decoder_18_out4));
  Counter #(.width(32), .max('hffffffff)) counter_1 (
    .count(and_21_out), .clk(decoder_14_out1), .clr(On_out));  // open: load, D, Q, carry
  or or_149 (or_149_out, or_153_out, d_ff_13_qn);
  or or_150 (or_150_out, or_154_out, d_ff_14_qn);
  or or_151 (or_151_out, or_155_out, d_ff_15_qn);
  or or_152 (or_152_out, or_156_out, d_ff_16_qn);
  Register #(.width(4)) register_21 (
    .D(adder_8_out), .en(d_ff_17_q), .Q(register_21_q), .clk(clock_1_out), .clr(decoder_18_out4));
  Register register_22 (
    .D(multiplexer_139_out), .en(decoder_25_out0), .Q(register_22_q), .clk(clock_1_out));  // open: clr
  Register register_23 (
    .D(multiplexer_139_out), .en(decoder_25_out1), .Q(register_23_q), .clk(clock_1_out));  // open: clr
  Register register_24 (
    .D(multiplexer_139_out), .en(decoder_25_out2), .Q(register_24_q), .clk(clock_1_out));  // open: clr
  Register register_25 (
    .D(multiplexer_139_out), .en(decoder_25_out3), .Q(register_25_q), .clk(clock_1_out));  // open: clr
  RAM #(.addrWidth(12), .bus("separate")) ram_2 (
    .addr({multiplexer_137_out_2, multiplexer_137_out}), .din(or_129_out), .data(ram_2_data),
    .str(or_117_out), .clk(clock_1_out), .ld(or_6_out));  // open: sel, clr
  Adder #(.width(4)) adder_8 (.a(register_21_q), .b(4'b0000), .out(adder_8_out), .cin(1'b1));  // open: cout
  Decoder #(.select(4), .enable("false")) decoder_18 (
    .out0(decoder_18_out0), .out1(decoder_18_out1), .out2(decoder_18_out2), .out3(decoder_18_out3),
    .out4(decoder_18_out4), .out5(decoder_18_out5), .out6(decoder_18_out6), .out7(decoder_18_out7),
    .out8(decoder_18_out8), .out9(decoder_18_out9), .out10(decoder_18_out10), .out11(decoder_18_out11),
    .out12(decoder_18_out12), .out13(decoder_18_out13), .out14(decoder_18_out14), .out15(decoder_18_out15),
    .sel(register_21_q));
  assign xor_3_out = register_22_q ^ multiplexer_139_out;  // XOR_Gate xor_3, 8 bits wide
  Decoder #(.select(3), .enable("false")) decoder_19 (
    .out0(decoder_19_out0), .out1(decoder_19_out1), .out2(decoder_19_out2), .out3(decoder_19_out3),
    .out4(decoder_19_out4), .out5(decoder_19_out5), .out6(decoder_19_out6), .out7(decoder_19_out7),
    .sel(or_131_out_2));
  assign xor_4_out = register_23_q ^ multiplexer_139_out;  // XOR_Gate xor_4, 8 bits wide
  Decoder #(.select(3), .enable("false")) decoder_20 (
    .out0(decoder_20_out0), .out1(decoder_20_out1), .out2(decoder_20_out2), .out3(decoder_20_out3),
    .out4(decoder_20_out4), .out5(decoder_20_out5), .out6(decoder_20_out6), .out7(decoder_20_out7),
    .sel(or_131_out_2));
  assign xor_5_out = register_24_q ^ multiplexer_139_out;  // XOR_Gate xor_5, 8 bits wide
  Decoder #(.select(3), .enable("false")) decoder_21 (
    .out0(decoder_21_out0), .out1(decoder_21_out1), .out2(decoder_21_out2), .out3(decoder_21_out3),
    .out4(decoder_21_out4), .out5(decoder_21_out5), .out6(decoder_21_out6), .out7(decoder_21_out7),
    .sel(or_131_out_2));
  assign xor_6_out = register_25_q ^ multiplexer_139_out;  // XOR_Gate xor_6, 8 bits wide
  Decoder #(.select(3), .enable("false")) decoder_22 (
    .out0(decoder_22_out0), .out1(decoder_22_out1), .out2(decoder_22_out2), .out3(decoder_22_out3),
    .out4(decoder_22_out4), .out5(decoder_22_out5), .out6(decoder_22_out6), .out7(decoder_22_out7),
    .sel(or_131_out_2));
  Multiplexer #(.width(8), .enable("false")) multiplexer_140 (
    .in0({8{1'b0}}), .in1(ram_2_data), .out(multiplexer_140_out), .sel(or_6_out));
  or or_153 (or_153_out, xor_3_out[0], xor_3_out[1], xor_3_out[2], xor_3_out[3], xor_3_out[4], xor_3_out[5], xor_3_out[6], xor_3_out[7]);
  and and_26 (and_26_out, ~or_153_out, d_ff_13_q);  // AND_Gate
  or or_154 (or_154_out, xor_4_out[0], xor_4_out[1], xor_4_out[2], xor_4_out[3], xor_4_out[4], xor_4_out[5], xor_4_out[6], xor_4_out[7]);
  and and_27 (and_27_out, ~or_154_out, d_ff_14_q);  // AND_Gate
  or or_155 (or_155_out, xor_5_out[0], xor_5_out[1], xor_5_out[2], xor_5_out[3], xor_5_out[4], xor_5_out[5], xor_5_out[6], xor_5_out[7]);
  and and_28 (and_28_out, ~or_155_out, d_ff_15_q);  // AND_Gate
  or or_156 (or_156_out, xor_6_out[0], xor_6_out[1], xor_6_out[2], xor_6_out[3], xor_6_out[4], xor_6_out[5], xor_6_out[6], xor_6_out[7]);
  and and_29 (and_29_out, ~or_156_out, d_ff_16_q);  // AND_Gate
  Register #(.width(2)) register_26 (
    .D(adder_9_out), .en(decoder_18_out1), .Q(register_26_q), .clk(clock_1_out));  // open: clr
  and and_30 (and_30_out, clock_1_out, decoder_24_out0);
  and and_31 (and_31_out, clock_1_out, decoder_24_out1);
  and and_32 (and_32_out, clock_1_out, decoder_24_out2);
  and and_33 (and_33_out, clock_1_out, decoder_24_out3);
  Multiplexer #(.width(2), .enable("false")) multiplexer_141 (
    .in0(register_26_q), .in1(2'b11), .out(multiplexer_141_out), .sel(d_ff_16_qn));
  Multiplexer #(.width(2), .enable("false")) multiplexer_142 (
    .in0(multiplexer_141_out), .in1(2'b10), .out(multiplexer_142_out), .sel(d_ff_15_qn));
  Multiplexer #(.width(2), .enable("false")) multiplexer_143 (
    .in0(multiplexer_142_out), .in1(2'b01), .out(multiplexer_143_out), .sel(d_ff_14_qn));
  Multiplexer #(.width(2), .enable("false")) multiplexer_144 (
    .in0(multiplexer_143_out), .in1(2'b00), .out(multiplexer_144_out), .sel(d_ff_13_qn));
  Register #(.width(16), .trigger("falling")) register_27 (
    .D(multiplexer_185_out_2), .en(and_30_out), .Q(register_27_q), .clk(or_148_out));  // open: clr
  and and_34 (and_34_out, and_26_out, decoder_19_out0, multiplexer_138_out);
  Register #(.width(16), .trigger("falling")) register_28 (
    .D(multiplexer_185_out_2), .en(and_31_out), .Q(register_28_q), .clk(or_148_out));  // open: clr
  and and_35 (and_35_out, and_27_out, decoder_20_out0, multiplexer_138_out);
  Register #(.width(16), .trigger("falling")) register_29 (
    .D(multiplexer_185_out_2), .en(and_32_out), .Q(register_29_q), .clk(or_148_out));  // open: clr
  and and_36 (and_36_out, and_28_out, decoder_21_out0, multiplexer_138_out);
  Register #(.width(16), .trigger("falling")) register_30 (
    .D(multiplexer_185_out_2), .en(and_33_out), .Q(register_30_q), .clk(or_148_out));  // open: clr
  and and_37 (and_37_out, and_29_out, decoder_22_out0, multiplexer_138_out);
  Adder #(.width(2)) adder_9 (.a(register_26_q), .b(2'b00), .out(adder_9_out), .cin(1'b1));  // open: cout
  Multiplexer #(.width(16), .enable("false")) multiplexer_145 (
    .in0({16{1'b0}}), .in1(register_27_q), .out(multiplexer_145_out), .sel(and_34_out));
  Multiplexer #(.width(16), .enable("false")) multiplexer_146 (
    .in0(multiplexer_145_out), .in1(register_28_q), .out(multiplexer_146_out), .sel(and_35_out));
  Multiplexer #(.width(16), .enable("false")) multiplexer_147 (
    .in0(multiplexer_146_out), .in1(register_29_q), .out(multiplexer_147_out), .sel(and_36_out));
  Multiplexer #(.width(16), .enable("false")) multiplexer_148 (
    .in0(multiplexer_147_out), .in1(register_30_q), .out(multiplexer_148_out), .sel(and_37_out));
  Decoder #(.select(4), .enable("false")) decoder_23 (
    .out0(decoder_23_out0), .out1(decoder_23_out1), .out2(decoder_23_out2), .out3(decoder_23_out3),
    .out4(decoder_23_out4), .out5(decoder_23_out5), .out6(decoder_23_out6), .out7(decoder_23_out7),
    .out8(decoder_23_out8), .out9(decoder_23_out9), .out10(decoder_23_out10), .out11(decoder_23_out11),
    .out12(decoder_23_out12), .out13(decoder_23_out13), .out14(decoder_23_out14), .out15(decoder_23_out15),
    .sel(multiplexer_137_out));
  Decoder #(.select(2), .disabled(0)) decoder_24 (
    .out0(decoder_24_out0), .out1(decoder_24_out1), .out2(decoder_24_out2), .out3(decoder_24_out3),
    .sel(multiplexer_144_out), .en(d_ff_17_q));
  Register #(.width(16), .trigger("falling")) register_31 (
    .D(multiplexer_185_out), .en(and_38_out), .Q(register_31_q), .clk(or_148_out));  // open: clr
  and and_38 (and_38_out, clock_1_out, decoder_24_out0);
  Register #(.width(16), .trigger("falling")) register_32 (
    .D(multiplexer_185_out), .en(and_39_out), .Q(register_32_q), .clk(or_148_out));  // open: clr
  and and_39 (and_39_out, clock_1_out, decoder_24_out1);
  Register #(.width(16), .trigger("falling")) register_33 (
    .D(multiplexer_185_out), .en(and_40_out), .Q(register_33_q), .clk(or_148_out));  // open: clr
  and and_40 (and_40_out, clock_1_out, decoder_24_out2);
  Register #(.width(16), .trigger("falling")) register_34 (
    .D(multiplexer_185_out), .en(and_41_out), .Q(register_34_q), .clk(or_148_out));  // open: clr
  and and_41 (and_41_out, clock_1_out, decoder_24_out3);
  Decoder #(.select(2), .disabled(0)) decoder_25 (
    .out0(decoder_25_out0), .out1(decoder_25_out1), .out2(decoder_25_out2), .out3(decoder_25_out3),
    .sel(multiplexer_144_out), .en(decoder_18_out3));
  Multiplexer #(.width(16), .enable("false")) multiplexer_149 (
    .in0(multiplexer_148_out), .in1(register_31_q), .out(multiplexer_149_out), .sel(and_42_out));
  and and_42 (and_42_out, and_26_out, decoder_19_out1, multiplexer_138_out);
  Multiplexer #(.width(16), .enable("false")) multiplexer_150 (
    .in0(multiplexer_149_out), .in1(register_32_q), .out(multiplexer_150_out), .sel(and_43_out));
  and and_43 (and_43_out, and_27_out, decoder_20_out1, multiplexer_138_out);
  Multiplexer #(.width(16), .enable("false")) multiplexer_151 (
    .in0(multiplexer_150_out), .in1(register_33_q), .out(multiplexer_151_out), .sel(and_44_out));
  and and_44 (and_44_out, and_28_out, decoder_21_out1, multiplexer_138_out);
  Multiplexer #(.width(16), .enable("false")) multiplexer_152 (
    .in0(multiplexer_151_out), .in1(register_34_q), .out(multiplexer_152_out), .sel(and_45_out));
  and and_45 (and_45_out, and_29_out, decoder_22_out1, multiplexer_138_out);
  or or_157 (or_157_out, decoder_18_out2, or_6_out);
  or or_158 (or_158_out, decoder_18_out2, decoder_23_out2);
  or or_159 (or_159_out, decoder_18_out2, decoder_23_out4);
  or or_160 (or_160_out, decoder_18_out2, decoder_23_out6);
  or or_161 (or_161_out, decoder_18_out2, decoder_23_out8);
  or or_162 (or_162_out, decoder_18_out2, decoder_23_out10);
  or or_163 (or_163_out, decoder_18_out2, decoder_23_out12);
  or or_164 (or_164_out, decoder_18_out2, decoder_23_out14);
  and and_46 (and_46_out, clock_1_out, decoder_24_out0);
  and and_47 (and_47_out, clock_1_out, decoder_24_out1);
  and and_48 (and_48_out, clock_1_out, decoder_24_out2);
  and and_49 (and_49_out, clock_1_out, decoder_24_out3);
  Multiplexer #(.width(16), .enable("false")) multiplexer_153 (
    .in0(multiplexer_152_out), .in1(register_35_q), .out(multiplexer_153_out), .sel(and_50_out));
  Register #(.width(16), .trigger("falling")) register_35 (
    .D(multiplexer_186_out_2), .en(and_46_out), .Q(register_35_q), .clk(or_148_out));  // open: clr
  and and_50 (and_50_out, and_26_out, decoder_19_out2, multiplexer_138_out);
  Multiplexer #(.width(16), .enable("false")) multiplexer_154 (
    .in0(multiplexer_153_out), .in1(register_36_q), .out(multiplexer_154_out), .sel(and_51_out));
  Register #(.width(16), .trigger("falling")) register_36 (
    .D(multiplexer_186_out_2), .en(and_47_out), .Q(register_36_q), .clk(or_148_out));  // open: clr
  and and_51 (and_51_out, and_27_out, decoder_20_out2, multiplexer_138_out);
  Multiplexer #(.width(16), .enable("false")) multiplexer_155 (
    .in0(multiplexer_154_out), .in1(register_37_q), .out(multiplexer_155_out), .sel(and_52_out));
  Register #(.width(16), .trigger("falling")) register_37 (
    .D(multiplexer_186_out_2), .en(and_48_out), .Q(register_37_q), .clk(or_148_out));  // open: clr
  and and_52 (and_52_out, and_28_out, decoder_21_out2, multiplexer_138_out);
  Multiplexer #(.width(16), .enable("false")) multiplexer_156 (
    .in0(multiplexer_155_out), .in1(register_38_q), .out(multiplexer_156_out), .sel(and_53_out));
  Register #(.width(16), .trigger("falling")) register_38 (
    .D(multiplexer_186_out_2), .en(and_49_out), .Q(register_38_q), .clk(or_148_out));  // open: clr
  and and_53 (and_53_out, and_29_out, decoder_22_out2, multiplexer_138_out);
  and and_54 (and_54_out, clock_1_out, decoder_24_out0);
  and and_55 (and_55_out, clock_1_out, decoder_24_out1);
  and and_56 (and_56_out, clock_1_out, decoder_24_out2);
  and and_57 (and_57_out, clock_1_out, decoder_24_out3);
  RAM #(.bus("separate")) ram_3 (
    .addr(multiplexer_137_out_2), .din(or_129_out), .data(ram_3_data), .str(or_117_out),
    .sel(decoder_23_out0), .clk(clock_1_out), .ld(or_157_out));  // open: clr
  and and_58 (and_58_out, decoder_23_out0, or_157_out);
  RAM #(.bus("separate")) ram_4 (
    .addr(multiplexer_137_out_2), .din(or_129_out), .data(ram_4_data), .str(or_117_out), .sel(or_158_out),
    .clk(clock_1_out), .ld(or_157_out));  // open: clr
  and and_59 (and_59_out, or_158_out, or_157_out);
  RAM #(.bus("separate")) ram_5 (
    .addr(multiplexer_137_out_2), .din(or_129_out), .data(ram_5_data), .str(or_117_out), .sel(or_159_out),
    .clk(clock_1_out), .ld(or_157_out));  // open: clr
  and and_60 (and_60_out, or_159_out, or_157_out);
  RAM #(.bus("separate")) ram_6 (
    .addr(multiplexer_137_out_2), .din(or_129_out), .data(ram_6_data), .str(or_117_out), .sel(or_160_out),
    .clk(clock_1_out), .ld(or_157_out));  // open: clr
  and and_61 (and_61_out, or_160_out, or_157_out);
  RAM #(.bus("separate")) ram_7 (
    .addr(multiplexer_137_out_2), .din(or_129_out), .data(ram_7_data), .str(or_117_out), .sel(or_161_out),
    .clk(clock_1_out), .ld(or_157_out));  // open: clr
  and and_62 (and_62_out, or_161_out, or_157_out);
  RAM #(.bus("separate")) ram_8 (
    .addr(multiplexer_137_out_2), .din(or_129_out), .data(ram_8_data), .str(or_117_out), .sel(or_162_out),
    .clk(clock_1_out), .ld(or_157_out));  // open: clr
  and and_63 (and_63_out, or_162_out, or_157_out);
  RAM #(.bus("separate")) ram_9 (
    .addr(multiplexer_137_out_2), .din(or_129_out), .data(ram_9_data), .str(or_117_out), .sel(or_163_out),
    .clk(clock_1_out), .ld(or_157_out));  // open: clr
  and and_64 (and_64_out, or_163_out, or_157_out);
  RAM #(.bus("separate")) ram_10 (
    .addr(multiplexer_137_out_2), .din(or_129_out), .data(ram_10_data), .str(or_117_out), .sel(or_164_out),
    .clk(clock_1_out), .ld(or_157_out));  // open: clr
  and and_65 (and_65_out, or_164_out, or_157_out);
  Register #(.width(16), .trigger("falling")) register_39 (
    .D(multiplexer_186_out), .en(and_54_out), .Q(register_39_q), .clk(or_148_out));  // open: clr
  Register #(.width(16), .trigger("falling")) register_40 (
    .D(multiplexer_186_out), .en(and_55_out), .Q(register_40_q), .clk(or_148_out));  // open: clr
  Register #(.width(16), .trigger("falling")) register_41 (
    .D(multiplexer_186_out), .en(and_56_out), .Q(register_41_q), .clk(or_148_out));  // open: clr
  Register #(.width(16), .trigger("falling")) register_42 (
    .D(multiplexer_186_out), .en(and_57_out), .Q(register_42_q), .clk(or_148_out));  // open: clr
  Multiplexer #(.width(8), .enable("false")) multiplexer_157 (
    .in0({8{1'b0}}), .in1(ram_3_data), .out(multiplexer_157_out), .sel(and_58_out));
  Multiplexer #(.width(8), .enable("false")) multiplexer_158 (
    .in0(multiplexer_157_out), .in1(ram_4_data), .out(multiplexer_158_out), .sel(and_59_out));
  Multiplexer #(.width(8), .enable("false")) multiplexer_159 (
    .in0(multiplexer_158_out), .in1(ram_5_data), .out(multiplexer_159_out), .sel(and_60_out));
  Multiplexer #(.width(8), .enable("false")) multiplexer_160 (
    .in0(multiplexer_159_out), .in1(ram_6_data), .out(multiplexer_160_out), .sel(and_61_out));
  Multiplexer #(.width(8), .enable("false")) multiplexer_161 (
    .in0(multiplexer_160_out), .in1(ram_7_data), .out(multiplexer_161_out), .sel(and_62_out));
  Multiplexer #(.width(8), .enable("false")) multiplexer_162 (
    .in0(multiplexer_161_out), .in1(ram_8_data), .out(multiplexer_162_out), .sel(and_63_out));
  Multiplexer #(.width(8), .enable("false")) multiplexer_163 (
    .in0(multiplexer_162_out), .in1(ram_9_data), .out(multiplexer_163_out), .sel(and_64_out));
  Multiplexer #(.width(8), .enable("false")) multiplexer_164 (
    .in0(multiplexer_163_out), .in1(ram_10_data), .out(multiplexer_164_out), .sel(and_65_out));
  Multiplexer #(.width(16), .enable("false")) multiplexer_165 (
    .in0(multiplexer_156_out), .in1(register_39_q), .out(multiplexer_165_out), .sel(and_66_out));
  and and_66 (and_66_out, and_26_out, decoder_19_out3, multiplexer_138_out);
  Multiplexer #(.width(16), .enable("false")) multiplexer_166 (
    .in0(multiplexer_165_out), .in1(register_40_q), .out(multiplexer_166_out), .sel(and_67_out));
  and and_67 (and_67_out, and_27_out, decoder_20_out3, multiplexer_138_out);
  Multiplexer #(.width(16), .enable("false")) multiplexer_167 (
    .in0(multiplexer_166_out), .in1(register_41_q), .out(multiplexer_167_out), .sel(and_68_out));
  and and_68 (and_68_out, and_28_out, decoder_21_out3, multiplexer_138_out);
  Multiplexer #(.width(16), .enable("false")) multiplexer_168 (
    .in0(multiplexer_167_out), .in1(register_42_q), .out(multiplexer_168_out), .sel(and_69_out));
  and and_69 (and_69_out, and_29_out, decoder_22_out3, multiplexer_138_out);
  or or_165 (or_165_out, decoder_18_out2, or_6_out);
  Register #(.width(16), .trigger("falling")) register_43 (
    .D(multiplexer_187_out_2), .en(and_70_out), .Q(register_43_q), .clk(or_148_out));  // open: clr
  and and_70 (and_70_out, clock_1_out, decoder_24_out0);
  Register #(.width(16), .trigger("falling")) register_44 (
    .D(multiplexer_187_out_2), .en(and_71_out), .Q(register_44_q), .clk(or_148_out));  // open: clr
  and and_71 (and_71_out, clock_1_out, decoder_24_out1);
  Register #(.width(16), .trigger("falling")) register_45 (
    .D(multiplexer_187_out_2), .en(and_72_out), .Q(register_45_q), .clk(or_148_out));  // open: clr
  and and_72 (and_72_out, clock_1_out, decoder_24_out2);
  Register #(.width(16), .trigger("falling")) register_46 (
    .D(multiplexer_187_out_2), .en(and_73_out), .Q(register_46_q), .clk(or_148_out));  // open: clr
  and and_73 (and_73_out, clock_1_out, decoder_24_out3);
  or or_166 (or_166_out, decoder_18_out2, decoder_23_out1);
  or or_167 (or_167_out, decoder_18_out2, decoder_23_out3);
  or or_168 (or_168_out, decoder_18_out2, decoder_23_out5);
  or or_169 (or_169_out, decoder_18_out2, decoder_23_out7);
  or or_170 (or_170_out, decoder_18_out2, decoder_23_out9);
  or or_171 (or_171_out, decoder_18_out2, decoder_23_out11);
  or or_172 (or_172_out, decoder_18_out2, decoder_23_out13);
  or or_173 (or_173_out, decoder_18_out2, decoder_23_out15);
  Multiplexer #(.width(16), .enable("false")) multiplexer_169 (
    .in0(multiplexer_168_out), .in1(register_43_q), .out(multiplexer_169_out), .sel(and_74_out));
  and and_74 (and_74_out, and_26_out, decoder_19_out4, multiplexer_138_out);
  Multiplexer #(.width(16), .enable("false")) multiplexer_170 (
    .in0(multiplexer_169_out), .in1(register_44_q), .out(multiplexer_170_out), .sel(and_75_out));
  and and_75 (and_75_out, and_27_out, decoder_20_out4, multiplexer_138_out);
  Multiplexer #(.width(16), .enable("false")) multiplexer_171 (
    .in0(multiplexer_170_out), .in1(register_45_q), .out(multiplexer_171_out), .sel(and_76_out));
  and and_76 (and_76_out, and_28_out, decoder_21_out4, multiplexer_138_out);
  Multiplexer #(.width(16), .enable("false")) multiplexer_172 (
    .in0(multiplexer_171_out), .in1(register_46_q), .out(multiplexer_172_out), .sel(and_77_out));
  and and_77 (and_77_out, and_29_out, decoder_22_out4, multiplexer_138_out);
  RAM #(.bus("separate")) ram_11 (
    .addr(multiplexer_137_out_2), .din(or_129_out), .data(ram_11_data), .str(or_117_out), .sel(or_166_out),
    .clk(clock_1_out), .ld(or_165_out));  // open: clr
  RAM #(.bus("separate")) ram_12 (
    .addr(multiplexer_137_out_2), .din(or_129_out), .data(ram_12_data), .str(or_117_out), .sel(or_167_out),
    .clk(clock_1_out), .ld(or_165_out));  // open: clr
  RAM #(.bus("separate")) ram_13 (
    .addr(multiplexer_137_out_2), .din(or_129_out), .data(ram_13_data), .str(or_117_out), .sel(or_168_out),
    .clk(clock_1_out), .ld(or_165_out));  // open: clr
  RAM #(.bus("separate")) ram_14 (
    .addr(multiplexer_137_out_2), .din(or_129_out), .data(ram_14_data), .str(or_117_out), .sel(or_169_out),
    .clk(clock_1_out), .ld(or_165_out));  // open: clr
  RAM #(.bus("separate")) ram_15 (
    .addr(multiplexer_137_out_2), .din(or_129_out), .data(ram_15_data), .str(or_117_out), .sel(or_170_out),
    .clk(clock_1_out), .ld(or_165_out));  // open: clr
  RAM #(.bus("separate")) ram_16 (
    .addr(multiplexer_137_out_2), .din(or_129_out), .data(ram_16_data), .str(or_117_out), .sel(or_171_out),
    .clk(clock_1_out), .ld(or_165_out));  // open: clr
  RAM #(.bus("separate")) ram_17 (
    .addr(multiplexer_137_out_2), .din(or_129_out), .data(ram_17_data), .str(or_117_out), .sel(or_172_out),
    .clk(clock_1_out), .ld(or_165_out));  // open: clr
  RAM #(.bus("separate")) ram_18 (
    .addr(multiplexer_137_out_2), .din(or_129_out), .data(ram_18_data), .str(or_117_out), .sel(or_173_out),
    .clk(clock_1_out), .ld(or_165_out));  // open: clr
  and and_78 (and_78_out, clock_1_out, decoder_24_out0);
  and and_79 (and_79_out, clock_1_out, decoder_24_out1);
  and and_80 (and_80_out, clock_1_out, decoder_24_out2);
  and and_81 (and_81_out, clock_1_out, decoder_24_out3);
  Multiplexer #(.width(8), .enable("false")) multiplexer_173 (
    .in0(multiplexer_164_out), .in1(ram_11_data), .out(multiplexer_173_out), .sel(and_82_out));
  and and_82 (and_82_out, or_166_out, or_165_out);
  Multiplexer #(.width(8), .enable("false")) multiplexer_174 (
    .in0(multiplexer_173_out), .in1(ram_12_data), .out(multiplexer_174_out), .sel(and_83_out));
  and and_83 (and_83_out, or_167_out, or_165_out);
  Multiplexer #(.width(8), .enable("false")) multiplexer_175 (
    .in0(multiplexer_174_out), .in1(ram_13_data), .out(multiplexer_175_out), .sel(and_84_out));
  and and_84 (and_84_out, or_168_out, or_165_out);
  Multiplexer #(.width(8), .enable("false")) multiplexer_176 (
    .in0(multiplexer_175_out), .in1(ram_14_data), .out(multiplexer_176_out), .sel(and_85_out));
  and and_85 (and_85_out, or_169_out, or_165_out);
  Multiplexer #(.width(8), .enable("false")) multiplexer_177 (
    .in0(multiplexer_176_out), .in1(ram_15_data), .out(multiplexer_177_out), .sel(and_86_out));
  and and_86 (and_86_out, or_170_out, or_165_out);
  Multiplexer #(.width(8), .enable("false")) multiplexer_178 (
    .in0(multiplexer_177_out), .in1(ram_16_data), .out(multiplexer_178_out), .sel(and_87_out));
  and and_87 (and_87_out, or_171_out, or_165_out);
  Multiplexer #(.width(8), .enable("false")) multiplexer_179 (
    .in0(multiplexer_178_out), .in1(ram_17_data), .out(multiplexer_179_out), .sel(and_88_out));
  and and_88 (and_88_out, or_172_out, or_165_out);
  Multiplexer #(.width(8), .enable("false")) multiplexer_180 (
    .in0(multiplexer_179_out), .in1(ram_18_data), .out(multiplexer_180_out), .sel(and_89_out));
  and and_89 (and_89_out, or_173_out, or_165_out);
  Register #(.width(16), .trigger("falling")) register_47 (
    .D(multiplexer_187_out), .en(and_78_out), .Q(register_47_q), .clk(or_148_out));  // open: clr
  and and_90 (and_90_out, and_26_out, decoder_19_out5, multiplexer_138_out);
  Register #(.width(16), .trigger("falling")) register_48 (
    .D(multiplexer_187_out), .en(and_79_out), .Q(register_48_q), .clk(or_148_out));  // open: clr
  and and_91 (and_91_out, and_27_out, decoder_20_out5, multiplexer_138_out);
  Register #(.width(16), .trigger("falling")) register_49 (
    .D(multiplexer_187_out), .en(and_80_out), .Q(register_49_q), .clk(or_148_out));  // open: clr
  and and_92 (and_92_out, and_28_out, decoder_21_out5, multiplexer_138_out);
  Register #(.width(16), .trigger("falling")) register_50 (
    .D(multiplexer_187_out), .en(and_81_out), .Q(register_50_q), .clk(or_148_out));  // open: clr
  and and_93 (and_93_out, and_29_out, decoder_22_out5, multiplexer_138_out);
  Multiplexer #(.width(16), .enable("false")) multiplexer_181 (
    .in0(multiplexer_172_out), .in1(register_47_q), .out(multiplexer_181_out), .sel(and_90_out));
  Multiplexer #(.width(16), .enable("false")) multiplexer_182 (
    .in0(multiplexer_181_out), .in1(register_48_q), .out(multiplexer_182_out), .sel(and_91_out));
  Multiplexer #(.width(16), .enable("false")) multiplexer_183 (
    .in0(multiplexer_182_out), .in1(register_49_q), .out(multiplexer_183_out), .sel(and_92_out));
  Multiplexer #(.width(16), .enable("false")) multiplexer_184 (
    .in0(multiplexer_183_out), .in1(register_50_q), .out(multiplexer_184_out), .sel(and_93_out));
  Multiplexer #(.width(32), .enable("false")) multiplexer_185 (
    .in0({32{1'b0}}), .in1({ram_3_data, ram_11_data, ram_4_data, ram_12_data}),
    .out({multiplexer_185_out_2, multiplexer_185_out}), .sel(decoder_18_out2));
  Multiplexer #(.width(32), .enable("false")) multiplexer_186 (
    .in0({32{1'b0}}), .in1({ram_5_data, ram_13_data, ram_6_data, ram_14_data}),
    .out({multiplexer_186_out_2, multiplexer_186_out}), .sel(decoder_18_out2));
  Multiplexer #(.width(32), .enable("false")) multiplexer_187 (
    .in0({32{1'b0}}), .in1({ram_7_data, ram_15_data, ram_8_data, ram_16_data}),
    .out({multiplexer_187_out_2, multiplexer_187_out}), .sel(decoder_18_out2));
  Multiplexer #(.width(32), .enable("false")) multiplexer_188 (
    .in0({32{1'b0}}), .in1({ram_9_data, ram_17_data, ram_10_data, ram_18_data}),
    .out({multiplexer_188_out_2, multiplexer_188_out}), .sel(decoder_18_out2));
  Register #(.width(16), .trigger("falling")) register_51 (
    .D(multiplexer_188_out_2), .en(and_94_out), .Q(register_51_q), .clk(or_148_out));  // open: clr
  and and_94 (and_94_out, clock_1_out, decoder_24_out0);
  Register #(.width(16), .trigger("falling")) register_52 (
    .D(multiplexer_188_out_2), .en(and_95_out), .Q(register_52_q), .clk(or_148_out));  // open: clr
  and and_95 (and_95_out, clock_1_out, decoder_24_out1);
  Register #(.width(16), .trigger("falling")) register_53 (
    .D(multiplexer_188_out_2), .en(and_96_out), .Q(register_53_q), .clk(or_148_out));  // open: clr
  and and_96 (and_96_out, clock_1_out, decoder_24_out2);
  Register #(.width(16), .trigger("falling")) register_54 (
    .D(multiplexer_188_out_2), .en(and_97_out), .Q(register_54_q), .clk(or_148_out));  // open: clr
  and and_97 (and_97_out, clock_1_out, decoder_24_out3);
  Multiplexer #(.width(16), .enable("false")) multiplexer_189 (
    .in0(multiplexer_184_out), .in1(register_51_q), .out(multiplexer_189_out), .sel(and_98_out));
  and and_98 (and_98_out, and_26_out, decoder_19_out6, multiplexer_138_out);
  Multiplexer #(.width(16), .enable("false")) multiplexer_190 (
    .in0(multiplexer_189_out), .in1(register_52_q), .out(multiplexer_190_out), .sel(and_99_out));
  and and_99 (and_99_out, and_27_out, decoder_20_out6, multiplexer_138_out);
  Multiplexer #(.width(16), .enable("false")) multiplexer_191 (
    .in0(multiplexer_190_out), .in1(register_53_q), .out(multiplexer_191_out), .sel(and_100_out));
  and and_100 (and_100_out, and_28_out, decoder_21_out6, multiplexer_138_out);
  Multiplexer #(.width(16), .enable("false")) multiplexer_192 (
    .in0(multiplexer_191_out), .in1(register_54_q), .out(multiplexer_192_out), .sel(and_101_out));
  and and_101 (and_101_out, and_29_out, decoder_22_out6, multiplexer_138_out);
  Register #(.width(16), .trigger("falling")) register_55 (
    .D(multiplexer_188_out), .en(and_102_out), .Q(register_55_q), .clk(or_148_out));  // open: clr
  and and_102 (and_102_out, clock_1_out, decoder_24_out0);
  Register #(.width(16), .trigger("falling")) register_56 (
    .D(multiplexer_188_out), .en(and_103_out), .Q(register_56_q), .clk(or_148_out));  // open: clr
  and and_103 (and_103_out, clock_1_out, decoder_24_out1);
  Register #(.width(16), .trigger("falling")) register_57 (
    .D(multiplexer_188_out), .en(and_104_out), .Q(register_57_q), .clk(or_148_out));  // open: clr
  and and_104 (and_104_out, clock_1_out, decoder_24_out2);
  Register #(.width(16), .trigger("falling")) register_58 (
    .D(multiplexer_188_out), .en(and_105_out), .Q(register_58_q), .clk(or_148_out));  // open: clr
  and and_105 (and_105_out, clock_1_out, decoder_24_out3);
  Multiplexer #(.width(16), .enable("false")) multiplexer_193 (
    .in0(multiplexer_192_out), .in1(register_55_q), .out(multiplexer_193_out), .sel(and_106_out));
  and and_106 (and_106_out, and_26_out, decoder_19_out7, multiplexer_138_out);
  Multiplexer #(.width(16), .enable("false")) multiplexer_194 (
    .in0(multiplexer_193_out), .in1(register_56_q), .out(multiplexer_194_out), .sel(and_107_out));
  and and_107 (and_107_out, and_27_out, decoder_20_out7, multiplexer_138_out);
  Multiplexer #(.width(16), .enable("false")) multiplexer_195 (
    .in0(multiplexer_194_out), .in1(register_57_q), .out(multiplexer_195_out), .sel(and_108_out));
  and and_108 (and_108_out, and_28_out, decoder_21_out7, multiplexer_138_out);
  Multiplexer #(.width(16), .enable("false")) multiplexer_196 (
    .in0(multiplexer_195_out), .in1(register_58_q), .out(multiplexer_196_out), .sel(and_109_out));
  and and_109 (and_109_out, and_29_out, decoder_22_out7, multiplexer_138_out);

  // Notes on the sheet:
  //   4011B Quad 2 Inputs NAND
  //   4013B Dual D-tipe flip-flop
  //   Clock
  //   Loader 256
  //   Loader 4K
  //   0x00
  //   00x0
  //   WReg 0x00
  //   WReg 00x0
  //   R00x0 alu1
  //   R0x00 alu1
  //   R000x alu2
  //   R0x00 to Ram
  //   R00x0 to Ram
  //   R000x adr alu
  //   R00x0 adr alu
  //   Enter
  //   ALU
  //   Pc hi Adr ef2
  //   Pc lo  Adr ef3
  //   Exc code Adr ef0
  //   Exc data Adr ef1
  //   Adr ef4
  //   R Pc
  //   W Ram
  //   W Pc
  //   R PC
  //   R PC+1
  //   W Pc
  //   W Acc
  //   R RAM 16
  //   Adr ALU
  //   Write Ram efe=write on screen decoded, write eff=7 segment code direct on screen
  //   Read to Ins and ins Ext
  //   Interrupt
  //   Main ON
  //   Data from Main ram
  //   1=miss 0=hit
  //   Miss Counter
  //   1=empty 0=with data
  //   Read Main mem
endmodule
