// Logisim project Cache 4by16.circ as structural Verilog: 1 circuit, main circuit main
module main (
  input  [11:0] in_1,
  input  in_2,
  input  in_3,
  input  in_4,
  input  in_5,
  input  [11:0] in_6,
  input  [31:0] in_7,
  input  [7:0] in_8,
  input  in_9,
  input  Ram_Read,
  input  [15:0] in_11,
  input  Interrupt,
  input  in_13,
  output [31:0] out_14,
  output [31:0] out_15,
  output [7:0] out_16
);

  wire and_1_out, and_2_out, and_3_out, and_4_out, and_5_out, and_6_out, and_7_out, and_8_out, and_9_out,
       and_10_out, and_11_out, and_12_out, and_13_out, and_14_out, and_15_out, and_16_out, and_17_out,
       and_18_out, and_19_out, and_20_out, and_21_out, and_22_out, and_23_out, and_24_out, and_25_out,
       and_26_out, and_27_out, and_28_out, and_29_out, and_30_out, and_31_out, and_32_out, and_33_out,
       and_34_out, and_35_out, and_36_out, and_37_out, and_38_out, and_39_out, and_40_out, and_41_out,
       and_42_out, and_43_out, and_44_out, and_45_out, and_46_out, and_47_out, and_48_out, and_49_out,
       and_50_out, and_51_out, and_52_out, and_53_out, and_54_out, and_55_out, and_56_out, and_57_out,
       and_58_out, and_59_out, and_60_out, and_61_out, and_62_out, and_63_out, and_64_out, and_65_out,
       and_66_out, and_67_out, and_68_out, and_69_out, and_70_out, and_71_out, and_72_out, and_73_out,
       and_74_out, and_75_out, and_76_out, and_77_out, and_78_out, and_79_out, and_80_out, and_81_out,
       and_82_out, and_83_out, and_84_out, and_85_out, and_86_out, and_87_out, and_88_out, and_89_out,
       button_1_out, d_ff_1_q, d_ff_1_qn, d_ff_2_q, d_ff_2_qn, d_ff_3_q, d_ff_3_qn, d_ff_4_q, d_ff_4_qn,
       d_ff_5_q, decoder_1_out0, decoder_1_out1, decoder_1_out3, decoder_1_out4, decoder_1_out5,
       decoder_1_out6, decoder_1_out7, decoder_1_out8, decoder_1_out9, decoder_1_out10, decoder_1_out11,
       decoder_1_out12, decoder_1_out13, decoder_1_out14, decoder_1_out15, decoder_2_out0, decoder_2_out1,
       decoder_2_out2, decoder_2_out3, decoder_2_out4, decoder_2_out5, decoder_2_out6, decoder_2_out7,
       decoder_3_out0, decoder_3_out1, decoder_3_out2, decoder_3_out3, decoder_3_out4, decoder_3_out5,
       decoder_3_out6, decoder_3_out7, decoder_4_out0, decoder_4_out1, decoder_4_out2, decoder_4_out3,
       decoder_4_out4, decoder_4_out5, decoder_4_out6, decoder_4_out7, decoder_5_out0, decoder_5_out1,
       decoder_5_out2, decoder_5_out3, decoder_5_out4, decoder_5_out5, decoder_5_out6, decoder_5_out7,
       decoder_6_out0, decoder_6_out1, decoder_6_out2, decoder_6_out3, decoder_6_out4, decoder_6_out5,
       decoder_6_out6, decoder_6_out7, decoder_6_out8, decoder_6_out9, decoder_6_out10, decoder_6_out11,
       decoder_6_out12, decoder_6_out13, decoder_6_out14, decoder_6_out15, decoder_7_out0, decoder_7_out1,
       decoder_7_out2, decoder_7_out3, decoder_8_out0, decoder_8_out1, decoder_8_out2, decoder_8_out3,
       multiplexer_2_out, or_1_out, or_2_out, or_3_out, or_4_out, or_5_out, or_6_out, or_7_out, or_8_out,
       or_9_out, or_10_out, or_11_out, or_12_out, or_13_out, or_14_out, or_15_out, or_16_out, or_17_out,
       or_18_out, or_19_out, or_20_out, or_21_out, or_22_out, or_23_out, or_24_out, or_25_out, or_26_out,
       or_27_out, undriven_2;
  wire [1:0] adder_2_out, multiplexer_6_out, multiplexer_7_out, multiplexer_8_out, multiplexer_9_out,
       register_7_q;
  wire [3:0] adder_1_out, register_6_q;
  wire [7:0] multiplexer_3_out, multiplexer_4_out, multiplexer_5_out, multiplexer_18_out, multiplexer_19_out,
       multiplexer_20_out, multiplexer_21_out, multiplexer_22_out, multiplexer_23_out, multiplexer_24_out,
       multiplexer_25_out, multiplexer_34_out, multiplexer_35_out, multiplexer_36_out, multiplexer_37_out,
       multiplexer_38_out, multiplexer_39_out, multiplexer_40_out, ram_1_data, ram_2_data, ram_3_data,
       ram_4_data, ram_5_data, ram_6_data, ram_7_data, ram_8_data, ram_9_data, ram_10_data, ram_11_data,
       ram_12_data, ram_13_data, ram_14_data, ram_15_data, ram_16_data, ram_17_data, ram_18_data,
       register_2_q, register_3_q, register_4_q, register_5_q, undriven, xor_1_out, xor_2_out, xor_3_out,
       xor_4_out;
  wire [11:4] register_1_q;
  wire [15:0] multiplexer_10_out, multiplexer_11_out, multiplexer_12_out, multiplexer_13_out,
       multiplexer_14_out, multiplexer_15_out, multiplexer_16_out, multiplexer_17_out, multiplexer_26_out,
       multiplexer_27_out, multiplexer_28_out, multiplexer_29_out, multiplexer_30_out, multiplexer_31_out,
       multiplexer_32_out, multiplexer_33_out, multiplexer_42_out, multiplexer_43_out, multiplexer_44_out,
       multiplexer_45_out, multiplexer_50_out, multiplexer_51_out, multiplexer_52_out, multiplexer_53_out,
       multiplexer_54_out, multiplexer_55_out, multiplexer_56_out, multiplexer_57_out, multiplexer_58_out,
       multiplexer_59_out, multiplexer_60_out, register_8_q, register_9_q, register_10_q, register_11_q,
       register_12_q, register_13_q, register_14_q, register_15_q, register_16_q, register_17_q,
       register_18_q, register_19_q, register_20_q, register_21_q, register_22_q, register_23_q,
       register_24_q, register_25_q, register_26_q, register_27_q, register_28_q, register_29_q,
       register_30_q, register_31_q, register_32_q, register_33_q, register_34_q, register_35_q,
       register_36_q, register_37_q, register_38_q, register_39_q;
  wire [31:0] multiplexer_48_out, multiplexer_49_out;

  Button button_1 (.out(button_1_out));
  Clock clock_1 (.out(in_2));
  Multiplexer #(.width(12), .enable("false")) multiplexer_1 (
    .in0({register_1_q, 4'b0000}), .in1(in_6), .out(in_1), .sel(or_1_out));
  or or_1 (or_1_out, in_3, in_4);
  RAM #(.addrWidth(12), .bus("separate")) ram_1 (
    .addr(in_1), .din(in_8), .data(ram_1_data), .str(in_3), .clk(in_2), .ld(undriven_2));  // open: sel, clr
  and and_1 (and_1_out, or_3_out, or_4_out, or_5_out, or_6_out);
  Multiplexer #(.enable("false")) multiplexer_2 (.in0(Interrupt), .in1(1'b0), .out(multiplexer_2_out), .sel(d_ff_5_q));
  or or_2 (or_2_out, in_3, in_5);
  Multiplexer #(.width(8), .enable("false")) multiplexer_3 (
    .in0({8{1'b0}}), .in1(ram_1_data), .out(multiplexer_3_out), .sel(undriven_2));
  Multiplexer #(.width(8), .enable("false")) multiplexer_4 (
    .in0(in_6[11:4]), .in1(register_1_q), .out(multiplexer_4_out), .sel(d_ff_5_q));
  D_Flip_Flop d_ff_1 (
    .clk(in_2), .D(decoder_8_out0), .Q(d_ff_1_q), .Qn(d_ff_1_qn), .en(decoder_8_out0), .reset(and_2_out));  // open: preset
  and and_2 (and_2_out, or_2_out, and_6_out);
  D_Flip_Flop d_ff_2 (
    .clk(in_2), .D(decoder_8_out1), .Q(d_ff_2_q), .Qn(d_ff_2_qn), .en(decoder_8_out1), .reset(and_3_out));  // open: preset
  and and_3 (and_3_out, or_2_out, and_7_out);
  D_Flip_Flop d_ff_3 (
    .clk(in_2), .D(decoder_8_out2), .Q(d_ff_3_q), .Qn(d_ff_3_qn), .en(decoder_8_out2), .reset(and_4_out));  // open: preset
  and and_4 (and_4_out, or_2_out, and_8_out);
  D_Flip_Flop d_ff_4 (
    .clk(in_2), .D(decoder_8_out3), .Q(d_ff_4_q), .Qn(d_ff_4_qn), .en(decoder_8_out3), .reset(and_5_out));  // open: preset
  and and_5 (and_5_out, or_2_out, and_9_out);
  RAM #(.addrWidth(12), .bus("separate")) ram_2 (
    .addr(in_1), .din(undriven), .data(ram_2_data), .str(in_3), .clk(in_2), .ld(in_4));  // open: sel, clr
  D_Flip_Flop d_ff_5 (
    .clk(in_2), .D(and_1_out), .Q(d_ff_5_q), .en(Interrupt), .reset(decoder_1_out4));  // open: Qn, preset
  Register register_1 (.D(in_6[11:4]), .en(and_1_out), .Q(register_1_q), .clk(Interrupt), .clr(decoder_1_out4));
  Counter #(.width(32), .max('hffffffff)) counter_1 (
    .count(and_1_out), .clk(Interrupt), .clr(button_1_out));  // open: load, D, Q, carry
  or or_3 (or_3_out, or_7_out, d_ff_1_qn);
  or or_4 (or_4_out, or_8_out, d_ff_2_qn);
  or or_5 (or_5_out, or_9_out, d_ff_3_qn);
  or or_6 (or_6_out, or_10_out, d_ff_4_qn);
  Multiplexer #(.width(8), .enable("false")) multiplexer_5 (
    .in0({8{1'b0}}), .in1(ram_2_data), .out(multiplexer_5_out), .sel(in_4));
  Register register_2 (.D(multiplexer_4_out), .en(decoder_8_out0), .Q(register_2_q), .clk(in_2));  // open: clr
  Register register_3 (.D(multiplexer_4_out), .en(decoder_8_out1), .Q(register_3_q), .clk(in_2));  // open: clr
  Register register_4 (.D(multiplexer_4_out), .en(decoder_8_out2), .Q(register_4_q), .clk(in_2));  // open: clr
  Register register_5 (.D(multiplexer_4_out), .en(decoder_8_out3), .Q(register_5_q), .clk(in_2));  // open: clr
  Register #(.width(4)) register_6 (.D(adder_1_out), .en(d_ff_5_q), .Q(register_6_q), .clk(in_2), .clr(decoder_1_out4));
  Decoder #(.select(4), .enable("false")) decoder_1 (
    .out0(decoder_1_out0), .out1(decoder_1_out1), .out2(in_5), .out3(decoder_1_out3), .out4(decoder_1_out4),
    .out5(decoder_1_out5), .out6(decoder_1_out6), .out7(decoder_1_out7), .out8(decoder_1_out8),
    .out9(decoder_1_out9), .out10(decoder_1_out10), .out11(decoder_1_out11), .out12(decoder_1_out12),
    .out13(decoder_1_out13), .out14(decoder_1_out14), .out15(decoder_1_out15), .sel(register_6_q));
  assign xor_1_out = register_2_q ^ multiplexer_4_out;  // XOR_Gate xor_1, 8 bits wide
  Decoder #(.select(3), .enable("false")) decoder_2 (
    .out0(decoder_2_out0), .out1(decoder_2_out1), .out2(decoder_2_out2), .out3(decoder_2_out3),
    .out4(decoder_2_out4), .out5(decoder_2_out5), .out6(decoder_2_out6), .out7(decoder_2_out7),
    .sel(in_6[3:1]));
  assign xor_2_out = register_3_q ^ multiplexer_4_out;  // XOR_Gate xor_2, 8 bits wide
  Decoder #(.select(3), .enable("false")) decoder_3 (
    .out0(decoder_3_out0), .out1(decoder_3_out1), .out2(decoder_3_out2), .out3(decoder_3_out3),
    .out4(decoder_3_out4), .out5(decoder_3_out5), .out6(decoder_3_out6), .out7(decoder_3_out7),
    .sel(in_6[3:1]));
  assign xor_3_out = register_4_q ^ multiplexer_4_out;  // XOR_Gate xor_3, 8 bits wide
  Decoder #(.select(3), .enable("false")) decoder_4 (
    .out0(decoder_4_out0), .out1(decoder_4_out1), .out2(decoder_4_out2), .out3(decoder_4_out3),
    .out4(decoder_4_out4), .out5(decoder_4_out5), .out6(decoder_4_out6), .out7(decoder_4_out7),
    .sel(in_6[3:1]));
  assign xor_4_out = register_5_q ^ multiplexer_4_out;  // XOR_Gate xor_4, 8 bits wide
  Decoder #(.select(3), .enable("false")) decoder_5 (
    .out0(decoder_5_out0), .out1(decoder_5_out1), .out2(decoder_5_out2), .out3(decoder_5_out3),
    .out4(decoder_5_out4), .out5(decoder_5_out5), .out6(decoder_5_out6), .out7(decoder_5_out7),
    .sel(in_6[3:1]));
  Adder #(.width(4)) adder_1 (.a(register_6_q), .b(4'b0000), .out(adder_1_out), .cin(1'b1));  // open: cout
  or or_7 (or_7_out, xor_1_out[0], xor_1_out[1], xor_1_out[2], xor_1_out[3], xor_1_out[4], xor_1_out[5], xor_1_out[6], xor_1_out[7]);
  or or_8 (or_8_out, xor_2_out[0], xor_2_out[1], xor_2_out[2], xor_2_out[3], xor_2_out[4], xor_2_out[5], xor_2_out[6], xor_2_out[7]);
  or or_9 (or_9_out, xor_3_out[0], xor_3_out[1], xor_3_out[2], xor_3_out[3], xor_3_out[4], xor_3_out[5], xor_3_out[6], xor_3_out[7]);
  or or_10 (or_10_out, xor_4_out[0], xor_4_out[1], xor_4_out[2], xor_4_out[3], xor_4_out[4], xor_4_out[5], xor_4_out[6], xor_4_out[7]);
  Decoder #(.select(4), .enable("false")) decoder_6 (
    .out0(decoder_6_out0), .out1(decoder_6_out1), .out2(decoder_6_out2), .out3(decoder_6_out3),
    .out4(decoder_6_out4), .out5(decoder_6_out5), .out6(decoder_6_out6), .out7(decoder_6_out7),
    .out8(decoder_6_out8), .out9(decoder_6_out9), .out10(decoder_6_out10), .out11(decoder_6_out11),
    .out12(decoder_6_out12), .out13(decoder_6_out13), .out14(decoder_6_out14), .out15(decoder_6_out15),
    .sel(in_1[3:0]));
  and and_6 (and_6_out, ~or_7_out, d_ff_1_q);  // AND_Gate
  and and_7 (and_7_out, ~or_8_out, d_ff_2_q);  // AND_Gate
  and and_8 (and_8_out, ~or_9_out, d_ff_3_q);  // AND_Gate
  and and_9 (and_9_out, ~or_10_out, d_ff_4_q);  // AND_Gate
  Register #(.width(2)) register_7 (.D(adder_2_out), .en(decoder_1_out1), .Q(register_7_q), .clk(in_2));  // open: clr
  Register #(.width(16), .trigger("falling")) register_8 (
    .D(in_7[31:16]), .en(and_10_out), .Q(register_8_q), .clk(or_2_out));  // open: clr
  and and_10 (and_10_out, in_2, decoder_7_out0);
  Register #(.width(16), .trigger("falling")) register_9 (
    .D(in_7[31:16]), .en(and_11_out), .Q(register_9_q), .clk(or_2_out));  // open: clr
  and and_11 (and_11_out, in_2, decoder_7_out1);
  Register #(.width(16), .trigger("falling")) register_10 (
    .D(in_7[31:16]), .en(and_12_out), .Q(register_10_q), .clk(or_2_out));  // open: clr
  and and_12 (and_12_out, in_2, decoder_7_out2);
  Register #(.width(16), .trigger("falling")) register_11 (
    .D(in_7[31:16]), .en(and_13_out), .Q(register_11_q), .clk(or_2_out));  // open: clr
  and and_13 (and_13_out, in_2, decoder_7_out3);
  Multiplexer #(.width(2), .enable("false")) multiplexer_6 (
    .in0(register_7_q), .in1(2'b11), .out(multiplexer_6_out), .sel(d_ff_4_qn));
  Multiplexer #(.width(2), .enable("false")) multiplexer_7 (
    .in0(multiplexer_6_out), .in1(2'b10), .out(multiplexer_7_out), .sel(d_ff_3_qn));
  Multiplexer #(.width(2), .enable("false")) multiplexer_8 (
    .in0(multiplexer_7_out), .in1(2'b01), .out(multiplexer_8_out), .sel(d_ff_2_qn));
  Multiplexer #(.width(2), .enable("false")) multiplexer_9 (
    .in0(multiplexer_8_out), .in1(2'b00), .out(multiplexer_9_out), .sel(d_ff_1_qn));
  Adder #(.width(2)) adder_2 (.a(register_7_q), .b(2'b00), .out(adder_2_out), .cin(1'b1));  // open: cout
  Multiplexer #(.width(16), .enable("false")) multiplexer_10 (
    .in0({16{1'b0}}), .in1(register_8_q), .out(multiplexer_10_out), .sel(and_14_out));
  and and_14 (and_14_out, and_6_out, decoder_2_out0, multiplexer_2_out);
  Multiplexer #(.width(16), .enable("false")) multiplexer_11 (
    .in0(multiplexer_10_out), .in1(register_9_q), .out(multiplexer_11_out), .sel(and_15_out));
  and and_15 (and_15_out, and_7_out, decoder_3_out0, multiplexer_2_out);
  Multiplexer #(.width(16), .enable("false")) multiplexer_12 (
    .in0(multiplexer_11_out), .in1(register_10_q), .out(multiplexer_12_out), .sel(and_16_out));
  and and_16 (and_16_out, and_8_out, decoder_4_out0, multiplexer_2_out);
  Multiplexer #(.width(16), .enable("false")) multiplexer_13 (
    .in0(multiplexer_12_out), .in1(register_11_q), .out(multiplexer_13_out), .sel(and_17_out));
  and and_17 (and_17_out, and_9_out, decoder_5_out0, multiplexer_2_out);
  or or_11 (or_11_out, in_5, in_4);
  or or_12 (or_12_out, in_5, decoder_6_out2);
  or or_13 (or_13_out, in_5, decoder_6_out4);
  or or_14 (or_14_out, in_5, decoder_6_out6);
  or or_15 (or_15_out, in_5, decoder_6_out8);
  or or_16 (or_16_out, in_5, decoder_6_out10);
  or or_17 (or_17_out, in_5, decoder_6_out12);
  or or_18 (or_18_out, in_5, decoder_6_out14);
  Decoder #(.select(2), .disabled(0)) decoder_7 (
    .out0(decoder_7_out0), .out1(decoder_7_out1), .out2(decoder_7_out2), .out3(decoder_7_out3),
    .sel(multiplexer_9_out), .en(d_ff_5_q));
  and and_18 (and_18_out, in_2, decoder_7_out0);
  and and_19 (and_19_out, in_2, decoder_7_out1);
  and and_20 (and_20_out, in_2, decoder_7_out2);
  and and_21 (and_21_out, in_2, decoder_7_out3);
  Register #(.width(16), .trigger("falling")) register_12 (
    .D(in_7[15:0]), .en(and_18_out), .Q(register_12_q), .clk(or_2_out));  // open: clr
  and and_22 (and_22_out, and_6_out, decoder_2_out1, multiplexer_2_out);
  Register #(.width(16), .trigger("falling")) register_13 (
    .D(in_7[15:0]), .en(and_19_out), .Q(register_13_q), .clk(or_2_out));  // open: clr
  and and_23 (and_23_out, and_7_out, decoder_3_out1, multiplexer_2_out);
  Register #(.width(16), .trigger("falling")) register_14 (
    .D(in_7[15:0]), .en(and_20_out), .Q(register_14_q), .clk(or_2_out));  // open: clr
  and and_24 (and_24_out, and_8_out, decoder_4_out1, multiplexer_2_out);
  Register #(.width(16), .trigger("falling")) register_15 (
    .D(in_7[15:0]), .en(and_21_out), .Q(register_15_q), .clk(or_2_out));  // open: clr
  and and_25 (and_25_out, and_9_out, decoder_5_out1, multiplexer_2_out);
  Decoder #(.select(2), .disabled(0)) decoder_8 (
    .out0(decoder_8_out0), .out1(decoder_8_out1), .out2(decoder_8_out2), .out3(decoder_8_out3),
    .sel(multiplexer_9_out), .en(decoder_1_out3));
  Multiplexer #(.width(16), .enable("false")) multiplexer_14 (
    .in0(multiplexer_13_out), .in1(register_12_q), .out(multiplexer_14_out), .sel(and_22_out));
  Multiplexer #(.width(16), .enable("false")) multiplexer_15 (
    .in0(multiplexer_14_out), .in1(register_13_q), .out(multiplexer_15_out), .sel(and_23_out));
  Multiplexer #(.width(16), .enable("false")) multiplexer_16 (
    .in0(multiplexer_15_out), .in1(register_14_q), .out(multiplexer_16_out), .sel(and_24_out));
  Multiplexer #(.width(16), .enable("false")) multiplexer_17 (
    .in0(multiplexer_16_out), .in1(register_15_q), .out(multiplexer_17_out), .sel(and_25_out));
  RAM #(.bus("separate")) ram_3 (
    .addr(in_1[11:4]), .din(undriven), .data(ram_3_data), .str(in_3), .sel(decoder_6_out0), .clk(in_2),
    .ld(or_11_out));  // open: clr
  and and_26 (and_26_out, decoder_6_out0, or_11_out);
  RAM #(.bus("separate")) ram_4 (
    .addr(in_1[11:4]), .din(undriven), .data(ram_4_data), .str(in_3), .sel(or_12_out), .clk(in_2),
    .ld(or_11_out));  // open: clr
  and and_27 (and_27_out, or_12_out, or_11_out);
  RAM #(.bus("separate")) ram_5 (
    .addr(in_1[11:4]), .din(undriven), .data(ram_5_data), .str(in_3), .sel(or_13_out), .clk(in_2),
    .ld(or_11_out));  // open: clr
  and and_28 (and_28_out, or_13_out, or_11_out);
  RAM #(.bus("separate")) ram_6 (
    .addr(in_1[11:4]), .din(undriven), .data(ram_6_data), .str(in_3), .sel(or_14_out), .clk(in_2),
    .ld(or_11_out));  // open: clr
  and and_29 (and_29_out, or_14_out, or_11_out);
  RAM #(.bus("separate")) ram_7 (
    .addr(in_1[11:4]), .din(undriven), .data(ram_7_data), .str(in_3), .sel(or_15_out), .clk(in_2),
    .ld(or_11_out));  // open: clr
  and and_30 (and_30_out, or_15_out, or_11_out);
  RAM #(.bus("separate")) ram_8 (
    .addr(in_1[11:4]), .din(undriven), .data(ram_8_data), .str(in_3), .sel(or_16_out), .clk(in_2),
    .ld(or_11_out));  // open: clr
  and and_31 (and_31_out, or_16_out, or_11_out);
  RAM #(.bus("separate")) ram_9 (
    .addr(in_1[11:4]), .din(undriven), .data(ram_9_data), .str(in_3), .sel(or_17_out), .clk(in_2),
    .ld(or_11_out));  // open: clr
  and and_32 (and_32_out, or_17_out, or_11_out);
  RAM #(.bus("separate")) ram_10 (
    .addr(in_1[11:4]), .din(undriven), .data(ram_10_data), .str(in_3), .sel(or_18_out), .clk(in_2),
    .ld(or_11_out));  // open: clr
  and and_33 (and_33_out, or_18_out, or_11_out);
  Register #(.width(16), .trigger("falling")) register_16 (
    .D(out_15[31:16]), .en(and_34_out), .Q(register_16_q), .clk(or_2_out));  // open: clr
  and and_34 (and_34_out, in_2, decoder_7_out0);
  Register #(.width(16), .trigger("falling")) register_17 (
    .D(out_15[31:16]), .en(and_35_out), .Q(register_17_q), .clk(or_2_out));  // open: clr
  and and_35 (and_35_out, in_2, decoder_7_out1);
  Register #(.width(16), .trigger("falling")) register_18 (
    .D(out_15[31:16]), .en(and_36_out), .Q(register_18_q), .clk(or_2_out));  // open: clr
  and and_36 (and_36_out, in_2, decoder_7_out2);
  Register #(.width(16), .trigger("falling")) register_19 (
    .D(out_15[31:16]), .en(and_37_out), .Q(register_19_q), .clk(or_2_out));  // open: clr
  and and_37 (and_37_out, in_2, decoder_7_out3);
  Multiplexer #(.width(8), .enable("false")) multiplexer_18 (
    .in0({8{1'b0}}), .in1(ram_3_data), .out(multiplexer_18_out), .sel(and_26_out));
  Multiplexer #(.width(8), .enable("false")) multiplexer_19 (
    .in0(multiplexer_18_out), .in1(ram_4_data), .out(multiplexer_19_out), .sel(and_27_out));
  Multiplexer #(.width(8), .enable("false")) multiplexer_20 (
    .in0(multiplexer_19_out), .in1(ram_5_data), .out(multiplexer_20_out), .sel(and_28_out));
  Multiplexer #(.width(8), .enable("false")) multiplexer_21 (
    .in0(multiplexer_20_out), .in1(ram_6_data), .out(multiplexer_21_out), .sel(and_29_out));
  Multiplexer #(.width(8), .enable("false")) multiplexer_22 (
    .in0(multiplexer_21_out), .in1(ram_7_data), .out(multiplexer_22_out), .sel(and_30_out));
  Multiplexer #(.width(8), .enable("false")) multiplexer_23 (
    .in0(multiplexer_22_out), .in1(ram_8_data), .out(multiplexer_23_out), .sel(and_31_out));
  Multiplexer #(.width(8), .enable("false")) multiplexer_24 (
    .in0(multiplexer_23_out), .in1(ram_9_data), .out(multiplexer_24_out), .sel(and_32_out));
  Multiplexer #(.width(8), .enable("false")) multiplexer_25 (
    .in0(multiplexer_24_out), .in1(ram_10_data), .out(multiplexer_25_out), .sel(and_33_out));
  Multiplexer #(.width(16), .enable("false")) multiplexer_26 (
    .in0(multiplexer_17_out), .in1(register_16_q), .out(multiplexer_26_out), .sel(and_38_out));
  and and_38 (and_38_out, and_6_out, decoder_2_out2, multiplexer_2_out);
  Multiplexer #(.width(16), .enable("false")) multiplexer_27 (
    .in0(multiplexer_26_out), .in1(register_17_q), .out(multiplexer_27_out), .sel(and_39_out));
  and and_39 (and_39_out, and_7_out, decoder_3_out2, multiplexer_2_out);
  Multiplexer #(.width(16), .enable("false")) multiplexer_28 (
    .in0(multiplexer_27_out), .in1(register_18_q), .out(multiplexer_28_out), .sel(and_40_out));
  and and_40 (and_40_out, and_8_out, decoder_4_out2, multiplexer_2_out);
  Multiplexer #(.width(16), .enable("false")) multiplexer_29 (
    .in0(multiplexer_28_out), .in1(register_19_q), .out(multiplexer_29_out), .sel(and_41_out));
  and and_41 (and_41_out, and_9_out, decoder_5_out2, multiplexer_2_out);
  or or_19 (or_19_out, in_5, in_4);
  Register #(.width(16), .trigger("falling")) register_20 (
    .D(out_15[15:0]), .en(and_42_out), .Q(register_20_q), .clk(or_2_out));  // open: clr
  and and_42 (and_42_out, in_2, decoder_7_out0);
  Register #(.width(16), .trigger("falling")) register_21 (
    .D(out_15[15:0]), .en(and_43_out), .Q(register_21_q), .clk(or_2_out));  // open: clr
  and and_43 (and_43_out, in_2, decoder_7_out1);
  Register #(.width(16), .trigger("falling")) register_22 (
    .D(out_15[15:0]), .en(and_44_out), .Q(register_22_q), .clk(or_2_out));  // open: clr
  and and_44 (and_44_out, in_2, decoder_7_out2);
  Register #(.width(16), .trigger("falling")) register_23 (
    .D(out_15[15:0]), .en(and_45_out), .Q(register_23_q), .clk(or_2_out));  // open: clr
  and and_45 (and_45_out, in_2, decoder_7_out3);
  or or_20 (or_20_out, in_5, decoder_6_out1);
  or or_21 (or_21_out, in_5, decoder_6_out3);
  or or_22 (or_22_out, in_5, decoder_6_out5);
  or or_23 (or_23_out, in_5, decoder_6_out7);
  or or_24 (or_24_out, in_5, decoder_6_out9);
  or or_25 (or_25_out, in_5, decoder_6_out11);
  or or_26 (or_26_out, in_5, decoder_6_out13);
  or or_27 (or_27_out, in_5, decoder_6_out15);
  Multiplexer #(.width(16), .enable("false")) multiplexer_30 (
    .in0(multiplexer_29_out), .in1(register_20_q), .out(multiplexer_30_out), .sel(and_46_out));
  and and_46 (and_46_out, and_6_out, decoder_2_out3, multiplexer_2_out);
  Multiplexer #(.width(16), .enable("false")) multiplexer_31 (
    .in0(multiplexer_30_out), .in1(register_21_q), .out(multiplexer_31_out), .sel(and_47_out));
  and and_47 (and_47_out, and_7_out, decoder_3_out3, multiplexer_2_out);
  Multiplexer #(.width(16), .enable("false")) multiplexer_32 (
    .in0(multiplexer_31_out), .in1(register_22_q), .out(multiplexer_32_out), .sel(and_48_out));
  and and_48 (and_48_out, and_8_out, decoder_4_out3, multiplexer_2_out);
  Multiplexer #(.width(16), .enable("false")) multiplexer_33 (
    .in0(multiplexer_32_out), .in1(register_23_q), .out(multiplexer_33_out), .sel(and_49_out));
  and and_49 (and_49_out, and_9_out, decoder_5_out3, multiplexer_2_out);
  RAM #(.bus("separate")) ram_11 (
    .addr(in_1[11:4]), .din(undriven), .data(ram_11_data), .str(in_3), .sel(or_20_out), .clk(in_2),
    .ld(or_19_out));  // open: clr
  and and_50 (and_50_out, or_20_out, or_19_out);
  RAM #(.bus("separate")) ram_12 (
    .addr(in_1[11:4]), .din(undriven), .data(ram_12_data), .str(in_3), .sel(or_21_out), .clk(in_2),
    .ld(or_19_out));  // open: clr
  and and_51 (and_51_out, or_21_out, or_19_out);
  RAM #(.bus("separate")) ram_13 (
    .addr(in_1[11:4]), .din(undriven), .data(ram_13_data), .str(in_3), .sel(or_22_out), .clk(in_2),
    .ld(or_19_out));  // open: clr
  and and_52 (and_52_out, or_22_out, or_19_out);
  RAM #(.bus("separate")) ram_14 (
    .addr(in_1[11:4]), .din(undriven), .data(ram_14_data), .str(in_3), .sel(or_23_out), .clk(in_2),
    .ld(or_19_out));  // open: clr
  and and_53 (and_53_out, or_23_out, or_19_out);
  RAM #(.bus("separate")) ram_15 (
    .addr(in_1[11:4]), .din(undriven), .data(ram_15_data), .str(in_3), .sel(or_24_out), .clk(in_2),
    .ld(or_19_out));  // open: clr
  and and_54 (and_54_out, or_24_out, or_19_out);
  RAM #(.bus("separate")) ram_16 (
    .addr(in_1[11:4]), .din(undriven), .data(ram_16_data), .str(in_3), .sel(or_25_out), .clk(in_2),
    .ld(or_19_out));  // open: clr
  and and_55 (and_55_out, or_25_out, or_19_out);
  RAM #(.bus("separate")) ram_17 (
    .addr(in_1[11:4]), .din(undriven), .data(ram_17_data), .str(in_3), .sel(or_26_out), .clk(in_2),
    .ld(or_19_out));  // open: clr
  and and_56 (and_56_out, or_26_out, or_19_out);
  RAM #(.bus("separate")) ram_18 (
    .addr(in_1[11:4]), .din(undriven), .data(ram_18_data), .str(in_3), .sel(or_27_out), .clk(in_2),
    .ld(or_19_out));  // open: clr
  and and_57 (and_57_out, or_27_out, or_19_out);
  and and_58 (and_58_out, in_2, decoder_7_out0);
  and and_59 (and_59_out, in_2, decoder_7_out1);
  and and_60 (and_60_out, in_2, decoder_7_out2);
  and and_61 (and_61_out, in_2, decoder_7_out3);
  Multiplexer #(.width(8), .enable("false")) multiplexer_34 (
    .in0(multiplexer_25_out), .in1(ram_11_data), .out(multiplexer_34_out), .sel(and_50_out));
  Multiplexer #(.width(8), .enable("false")) multiplexer_35 (
    .in0(multiplexer_34_out), .in1(ram_12_data), .out(multiplexer_35_out), .sel(and_51_out));
  Multiplexer #(.width(8), .enable("false")) multiplexer_36 (
    .in0(multiplexer_35_out), .in1(ram_13_data), .out(multiplexer_36_out), .sel(and_52_out));
  Multiplexer #(.width(8), .enable("false")) multiplexer_37 (
    .in0(multiplexer_36_out), .in1(ram_14_data), .out(multiplexer_37_out), .sel(and_53_out));
  Multiplexer #(.width(8), .enable("false")) multiplexer_38 (
    .in0(multiplexer_37_out), .in1(ram_15_data), .out(multiplexer_38_out), .sel(and_54_out));
  Multiplexer #(.width(8), .enable("false")) multiplexer_39 (
    .in0(multiplexer_38_out), .in1(ram_16_data), .out(multiplexer_39_out), .sel(and_55_out));
  Multiplexer #(.width(8), .enable("false")) multiplexer_40 (
    .in0(multiplexer_39_out), .in1(ram_17_data), .out(multiplexer_40_out), .sel(and_56_out));
  Multiplexer #(.width(8), .enable("false")) multiplexer_41 (
    .in0(multiplexer_40_out), .in1(ram_18_data), .out(out_16), .sel(and_57_out));
  Register #(.width(16), .trigger("falling")) register_24 (
    .D(multiplexer_48_out[31:16]), .en(and_58_out), .Q(register_24_q), .clk(or_2_out));  // open: clr
  and and_62 (and_62_out, and_6_out, decoder_2_out4, multiplexer_2_out);
  Register #(.width(16), .trigger("falling")) register_25 (
    .D(multiplexer_48_out[31:16]), .en(and_59_out), .Q(register_25_q), .clk(or_2_out));  // open: clr
  and and_63 (and_63_out, and_7_out, decoder_3_out4, multiplexer_2_out);
  Register #(.width(16), .trigger("falling")) register_26 (
    .D(multiplexer_48_out[31:16]), .en(and_60_out), .Q(register_26_q), .clk(or_2_out));  // open: clr
  and and_64 (and_64_out, and_8_out, decoder_4_out4, multiplexer_2_out);
  Register #(.width(16), .trigger("falling")) register_27 (
    .D(multiplexer_48_out[31:16]), .en(and_61_out), .Q(register_27_q), .clk(or_2_out));  // open: clr
  and and_65 (and_65_out, and_9_out, decoder_5_out4, multiplexer_2_out);
  Multiplexer #(.width(16), .enable("false")) multiplexer_42 (
    .in0(multiplexer_33_out), .in1(register_24_q), .out(multiplexer_42_out), .sel(and_62_out));
  Multiplexer #(.width(16), .enable("false")) multiplexer_43 (
    .in0(multiplexer_42_out), .in1(register_25_q), .out(multiplexer_43_out), .sel(and_63_out));
  Multiplexer #(.width(16), .enable("false")) multiplexer_44 (
    .in0(multiplexer_43_out), .in1(register_26_q), .out(multiplexer_44_out), .sel(and_64_out));
  Multiplexer #(.width(16), .enable("false")) multiplexer_45 (
    .in0(multiplexer_44_out), .in1(register_27_q), .out(multiplexer_45_out), .sel(and_65_out));
  Multiplexer #(.width(32), .enable("false")) multiplexer_46 (
    .in0({32{1'b0}}), .in1({ram_3_data, ram_11_data, ram_4_data, ram_12_data}), .out(in_7), .sel(in_5));
  Multiplexer #(.width(32), .enable("false")) multiplexer_47 (
    .in0({32{1'b0}}), .in1({ram_5_data, ram_13_data, ram_6_data, ram_14_data}), .out(out_15), .sel(in_5));
  Multiplexer #(.width(32), .enable("false")) multiplexer_48 (
    .in0({32{1'b0}}), .in1({ram_7_data, ram_15_data, ram_8_data, ram_16_data}), .out(multiplexer_48_out),
    .sel(in_5));
  Multiplexer #(.width(32), .enable("false")) multiplexer_49 (
    .in0({32{1'b0}}), .in1({ram_9_data, ram_17_data, ram_10_data, ram_18_data}), .out(multiplexer_49_out),
    .sel(in_5));
  Register #(.width(16), .trigger("falling")) register_28 (
    .D(multiplexer_48_out[15:0]), .en(and_66_out), .Q(register_28_q), .clk(or_2_out));  // open: clr
  and and_66 (and_66_out, in_2, decoder_7_out0);
  Register #(.width(16), .trigger("falling")) register_29 (
    .D(multiplexer_48_out[15:0]), .en(and_67_out), .Q(register_29_q), .clk(or_2_out));  // open: clr
  and and_67 (and_67_out, in_2, decoder_7_out1);
  Register #(.width(16), .trigger("falling")) register_30 (
    .D(multiplexer_48_out[15:0]), .en(and_68_out), .Q(register_30_q), .clk(or_2_out));  // open: clr
  and and_68 (and_68_out, in_2, decoder_7_out2);
  Register #(.width(16), .trigger("falling")) register_31 (
    .D(multiplexer_48_out[15:0]), .en(and_69_out), .Q(register_31_q), .clk(or_2_out));  // open: clr
  and and_69 (and_69_out, in_2, decoder_7_out3);
  Multiplexer #(.width(16), .enable("false")) multiplexer_50 (
    .in0(multiplexer_45_out), .in1(register_28_q), .out(multiplexer_50_out), .sel(and_70_out));
  and and_70 (and_70_out, and_6_out, decoder_2_out5, multiplexer_2_out);
  Multiplexer #(.width(16), .enable("false")) multiplexer_51 (
    .in0(multiplexer_50_out), .in1(register_29_q), .out(multiplexer_51_out), .sel(and_71_out));
  and and_71 (and_71_out, and_7_out, decoder_3_out5, multiplexer_2_out);
  Multiplexer #(.width(16), .enable("false")) multiplexer_52 (
    .in0(multiplexer_51_out), .in1(register_30_q), .out(multiplexer_52_out), .sel(and_72_out));
  and and_72 (and_72_out, and_8_out, decoder_4_out5, multiplexer_2_out);
  Multiplexer #(.width(16), .enable("false")) multiplexer_53 (
    .in0(multiplexer_52_out), .in1(register_31_q), .out(multiplexer_53_out), .sel(and_73_out));
  and and_73 (and_73_out, and_9_out, decoder_5_out5, multiplexer_2_out);
  and and_74 (and_74_out, in_2, decoder_7_out0);
  and and_75 (and_75_out, in_2, decoder_7_out1);
  and and_76 (and_76_out, in_2, decoder_7_out2);
  and and_77 (and_77_out, in_2, decoder_7_out3);
  Multiplexer #(.width(16), .enable("false")) multiplexer_54 (
    .in0(multiplexer_53_out), .in1(register_32_q), .out(multiplexer_54_out), .sel(and_78_out));
  Register #(.width(16), .trigger("falling")) register_32 (
    .D(multiplexer_49_out[31:16]), .en(and_74_out), .Q(register_32_q), .clk(or_2_out));  // open: clr
  and and_78 (and_78_out, and_6_out, decoder_2_out6, multiplexer_2_out);
  Multiplexer #(.width(16), .enable("false")) multiplexer_55 (
    .in0(multiplexer_54_out), .in1(register_33_q), .out(multiplexer_55_out), .sel(and_79_out));
  Register #(.width(16), .trigger("falling")) register_33 (
    .D(multiplexer_49_out[31:16]), .en(and_75_out), .Q(register_33_q), .clk(or_2_out));  // open: clr
  and and_79 (and_79_out, and_7_out, decoder_3_out6, multiplexer_2_out);
  Multiplexer #(.width(16), .enable("false")) multiplexer_56 (
    .in0(multiplexer_55_out), .in1(register_34_q), .out(multiplexer_56_out), .sel(and_80_out));
  Register #(.width(16), .trigger("falling")) register_34 (
    .D(multiplexer_49_out[31:16]), .en(and_76_out), .Q(register_34_q), .clk(or_2_out));  // open: clr
  and and_80 (and_80_out, and_8_out, decoder_4_out6, multiplexer_2_out);
  Multiplexer #(.width(16), .enable("false")) multiplexer_57 (
    .in0(multiplexer_56_out), .in1(register_35_q), .out(multiplexer_57_out), .sel(and_81_out));
  Register #(.width(16), .trigger("falling")) register_35 (
    .D(multiplexer_49_out[31:16]), .en(and_77_out), .Q(register_35_q), .clk(or_2_out));  // open: clr
  and and_81 (and_81_out, and_9_out, decoder_5_out6, multiplexer_2_out);
  and and_82 (and_82_out, in_2, decoder_7_out0);
  and and_83 (and_83_out, in_2, decoder_7_out1);
  and and_84 (and_84_out, in_2, decoder_7_out2);
  and and_85 (and_85_out, in_2, decoder_7_out3);
  Register #(.width(16), .trigger("falling")) register_36 (
    .D(multiplexer_49_out[15:0]), .en(and_82_out), .Q(register_36_q), .clk(or_2_out));  // open: clr
  Register #(.width(16), .trigger("falling")) register_37 (
    .D(multiplexer_49_out[15:0]), .en(and_83_out), .Q(register_37_q), .clk(or_2_out));  // open: clr
  Register #(.width(16), .trigger("falling")) register_38 (
    .D(multiplexer_49_out[15:0]), .en(and_84_out), .Q(register_38_q), .clk(or_2_out));  // open: clr
  Register #(.width(16), .trigger("falling")) register_39 (
    .D(multiplexer_49_out[15:0]), .en(and_85_out), .Q(register_39_q), .clk(or_2_out));  // open: clr
  Multiplexer #(.width(16), .enable("false")) multiplexer_58 (
    .in0(multiplexer_57_out), .in1(register_36_q), .out(multiplexer_58_out), .sel(and_86_out));
  and and_86 (and_86_out, and_6_out, decoder_2_out7, multiplexer_2_out);
  Multiplexer #(.width(16), .enable("false")) multiplexer_59 (
    .in0(multiplexer_58_out), .in1(register_37_q), .out(multiplexer_59_out), .sel(and_87_out));
  and and_87 (and_87_out, and_7_out, decoder_3_out7, multiplexer_2_out);
  Multiplexer #(.width(16), .enable("false")) multiplexer_60 (
    .in0(multiplexer_59_out), .in1(register_38_q), .out(multiplexer_60_out), .sel(and_88_out));
  and and_88 (and_88_out, and_8_out, decoder_4_out7, multiplexer_2_out);
  Multiplexer #(.width(16), .enable("false")) multiplexer_61 (
    .in0(multiplexer_60_out), .in1(register_39_q), .out(in_11), .sel(and_89_out));
  and and_89 (and_89_out, and_9_out, decoder_5_out7, multiplexer_2_out);

  assign in_9 = in_3;
  assign out_14 = in_7;
  assign Ram_Read = in_4;

  // Notes on the sheet:
  //   Read to Ins and ins Ext
  //   Main ON
  //   Data from Main ram
  //   1=miss 0=hit
  //   Miss Counter
  //   1=empty 0=with data
  //   Read Main mem
endmodule
