// Logisim project Cache 4by8.circ as structural Verilog: 1 circuit, main circuit main
module main (
  input  [11:0] in_1,
  input  [31:0] in_2,
  input  [7:0] in_3,
  input  in_4,
  input  Ram_Read,
  input  Interrupt,
  input  in_7,
  output [15:0] out_8
);

  wire and_1_out, and_2_out, and_3_out, and_4_out, and_5_out, and_6_out, and_7_out, and_8_out, and_9_out,
       and_10_out, and_11_out, and_12_out, and_13_out, and_14_out, and_15_out, and_16_out, and_17_out,
       and_18_out, and_19_out, and_20_out, and_21_out, and_22_out, and_23_out, and_24_out, and_25_out,
       and_26_out, and_27_out, and_28_out, and_29_out, and_30_out, and_31_out, and_32_out, and_33_out,
       and_34_out, and_35_out, and_36_out, and_37_out, and_38_out, and_39_out, and_40_out, and_41_out,
       button_1_out, clock_1_out, d_ff_1_q, d_ff_2_q, d_ff_2_qn, d_ff_3_q, d_ff_3_qn, d_ff_4_q, d_ff_4_qn,
       d_ff_5_q, d_ff_5_qn, decoder_1_out0, decoder_1_out1, decoder_1_out2, decoder_1_out3, decoder_1_out4,
       decoder_1_out5, decoder_1_out6, decoder_1_out7, decoder_1_out8, decoder_1_out9, decoder_1_out10,
       decoder_1_out11, decoder_1_out12, decoder_1_out13, decoder_1_out14, decoder_1_out15, decoder_2_out0,
       decoder_2_out1, decoder_2_out2, decoder_2_out3, decoder_3_out0, decoder_3_out1, decoder_3_out2,
       decoder_3_out3, decoder_4_out0, decoder_4_out1, decoder_4_out2, decoder_4_out3, decoder_5_out0,
       decoder_5_out1, decoder_5_out2, decoder_5_out3, decoder_6_out0, decoder_6_out1, decoder_6_out2,
       decoder_6_out3, decoder_7_out0, decoder_7_out1, decoder_7_out2, decoder_7_out3, multiplexer_2_out,
       or_1_out, or_2_out, or_3_out, or_4_out, or_5_out, or_6_out, or_7_out, or_8_out, or_9_out, or_10_out,
       undriven_3, undriven_4, undriven_8, undriven_9, undriven_10, undriven_11;
  wire [1:0] adder_2_out, multiplexer_6_out, multiplexer_7_out, multiplexer_8_out, multiplexer_9_out,
       register_7_q;
  wire [2:0] undriven;
  wire [3:0] adder_1_out, register_2_q;
  wire [7:0] multiplexer_4_out, multiplexer_5_out, ram_1_data, ram_2_data;
  wire [8:0] multiplexer_3_out, register_3_q, register_4_q, register_5_q, register_6_q, undriven_2,
       xor_1_out, xor_2_out, xor_3_out, xor_4_out;
  wire [11:0] multiplexer_1_out, undriven_7;
  wire [11:3] register_1_q;
  wire [15:0] multiplexer_10_out, multiplexer_11_out, multiplexer_12_out, multiplexer_13_out,
       multiplexer_14_out, multiplexer_15_out, multiplexer_16_out, multiplexer_17_out, multiplexer_18_out,
       multiplexer_19_out, multiplexer_20_out, multiplexer_21_out, multiplexer_22_out, multiplexer_23_out,
       multiplexer_24_out, register_8_q, register_9_q, register_10_q, register_11_q, register_12_q,
       register_13_q, register_14_q, register_15_q, register_16_q, register_17_q, register_18_q,
       register_19_q, register_20_q, register_21_q, register_22_q, register_23_q;
  wire [31:0] undriven_5, undriven_6;

  Button button_1 (.out(button_1_out));
  Clock clock_1 (.out(clock_1_out));
  Multiplexer #(.width(12), .enable("false")) multiplexer_1 (
    .in0({register_1_q, 3'b000}), .in1({undriven_2, undriven}), .out(multiplexer_1_out), .sel(or_1_out));
  or or_1 (or_1_out, undriven_4, undriven_3);
  or or_2 (or_2_out, undriven_4, decoder_1_out2);
  RAM #(.addrWidth(12), .bus("separate")) ram_1 (
    .addr(undriven_7), .din(in_3), .data(ram_1_data), .str(in_4), .clk(clock_1_out), .ld(undriven_8));  // open: sel, clr
  and and_1 (and_1_out, or_3_out, or_4_out, or_5_out, or_6_out);
  Multiplexer #(.enable("false")) multiplexer_2 (
    .in0(undriven_10), .in1(1'b0), .out(multiplexer_2_out), .sel(d_ff_1_q));
  Multiplexer #(.width(9), .enable("false")) multiplexer_3 (
    .in0(undriven_2), .in1(register_1_q), .out(multiplexer_3_out), .sel(d_ff_1_q));
  and and_2 (and_2_out, or_2_out, and_6_out);
  and and_3 (and_3_out, or_2_out, and_7_out);
  and and_4 (and_4_out, or_2_out, and_8_out);
  and and_5 (and_5_out, or_2_out, and_9_out);
  Multiplexer #(.width(8), .enable("false")) multiplexer_4 (
    .in0({8{1'b0}}), .in1(ram_1_data), .out(multiplexer_4_out), .sel(undriven_8));
  D_Flip_Flop d_ff_1 (
    .clk(undriven_9), .D(and_1_out), .Q(d_ff_1_q), .en(undriven_10), .reset(decoder_1_out4));  // open: Qn, preset
  Register #(.width(9)) register_1 (
    .D(undriven_2), .en(and_1_out), .Q(register_1_q), .clk(undriven_10), .clr(decoder_1_out4));
  Counter #(.width(32), .max('hffffffff)) counter_1 (
    .count(and_1_out), .clk(undriven_10), .clr(undriven_11));  // open: load, D, Q, carry
  D_Flip_Flop d_ff_2 (
    .clk(undriven_9), .D(decoder_7_out0), .Q(d_ff_2_q), .Qn(d_ff_2_qn), .en(decoder_7_out0), .reset(and_2_out));  // open: preset
  D_Flip_Flop d_ff_3 (
    .clk(undriven_9), .D(decoder_7_out1), .Q(d_ff_3_q), .Qn(d_ff_3_qn), .en(decoder_7_out1), .reset(and_3_out));  // open: preset
  D_Flip_Flop d_ff_4 (
    .clk(undriven_9), .D(decoder_7_out2), .Q(d_ff_4_q), .Qn(d_ff_4_qn), .en(decoder_7_out2), .reset(and_4_out));  // open: preset
  D_Flip_Flop d_ff_5 (
    .clk(undriven_9), .D(decoder_7_out3), .Q(d_ff_5_q), .Qn(d_ff_5_qn), .en(decoder_7_out3), .reset(and_5_out));  // open: preset
  RAM #(.addrWidth(12), .bus("separate")) ram_2 (
    .addr(undriven_7), .din(in_3), .data(ram_2_data), .str(in_4), .clk(clock_1_out), .ld(Ram_Read));  // open: sel, clr
  or or_3 (or_3_out, or_7_out, d_ff_2_qn);
  or or_4 (or_4_out, or_8_out, d_ff_3_qn);
  or or_5 (or_5_out, or_9_out, d_ff_4_qn);
  or or_6 (or_6_out, or_10_out, d_ff_5_qn);
  Multiplexer #(.width(8), .enable("false")) multiplexer_5 (
    .in0({8{1'b0}}), .in1(ram_2_data), .out(multiplexer_5_out), .sel(Ram_Read));
  Register #(.width(4)) register_2 (
    .D(adder_1_out), .en(d_ff_1_q), .Q(register_2_q), .clk(undriven_9), .clr(decoder_1_out4));
  Register #(.width(9)) register_3 (
    .D(multiplexer_3_out), .en(decoder_7_out0), .Q(register_3_q), .clk(undriven_9));  // open: clr
  Register #(.width(9)) register_4 (
    .D(multiplexer_3_out), .en(decoder_7_out1), .Q(register_4_q), .clk(undriven_9));  // open: clr
  Register #(.width(9)) register_5 (
    .D(multiplexer_3_out), .en(decoder_7_out2), .Q(register_5_q), .clk(undriven_9));  // open: clr
  Register #(.width(9)) register_6 (
    .D(multiplexer_3_out), .en(decoder_7_out3), .Q(register_6_q), .clk(undriven_9));  // open: clr
  Decoder #(.select(4), .enable("false")) decoder_1 (
    .out0(decoder_1_out0), .out1(decoder_1_out1), .out2(decoder_1_out2), .out3(decoder_1_out3),
    .out4(decoder_1_out4), .out5(decoder_1_out5), .out6(decoder_1_out6), .out7(decoder_1_out7),
    .out8(decoder_1_out8), .out9(decoder_1_out9), .out10(decoder_1_out10), .out11(decoder_1_out11),
    .out12(decoder_1_out12), .out13(decoder_1_out13), .out14(decoder_1_out14), .out15(decoder_1_out15),
    .sel(register_2_q));
  assign xor_1_out = register_3_q ^ multiplexer_3_out;  // XOR_Gate xor_1, 9 bits wide
  Decoder #(.select(2), .enable("false")) decoder_2 (
    .out0(decoder_2_out0), .out1(decoder_2_out1), .out2(decoder_2_out2), .out3(decoder_2_out3),
    .sel(undriven[2:1]));
  assign xor_2_out = register_4_q ^ multiplexer_3_out;  // XOR_Gate xor_2, 9 bits wide
  Decoder #(.select(2), .enable("false")) decoder_3 (
    .out0(decoder_3_out0), .out1(decoder_3_out1), .out2(decoder_3_out2), .out3(decoder_3_out3),
    .sel(undriven[2:1]));
  assign xor_3_out = register_5_q ^ multiplexer_3_out;  // XOR_Gate xor_3, 9 bits wide
  Decoder #(.select(2), .enable("false")) decoder_4 (
    .out0(decoder_4_out0), .out1(decoder_4_out1), .out2(decoder_4_out2), .out3(decoder_4_out3),
    .sel(undriven[2:1]));
  assign xor_4_out = register_6_q ^ multiplexer_3_out;  // XOR_Gate xor_4, 9 bits wide
  Decoder #(.select(2), .enable("false")) decoder_5 (
    .out0(decoder_5_out0), .out1(decoder_5_out1), .out2(decoder_5_out2), .out3(decoder_5_out3),
    .sel(undriven[2:1]));
  Adder #(.width(4)) adder_1 (.a(register_2_q), .b(4'b0000), .out(adder_1_out), .cin(1'b1));  // open: cout
  or or_7 (or_7_out, xor_1_out[0], xor_1_out[1], xor_1_out[2], xor_1_out[3], xor_1_out[4], xor_1_out[5], xor_1_out[6], xor_1_out[7], xor_1_out[8]);
  or or_8 (or_8_out, xor_2_out[0], xor_2_out[1], xor_2_out[2], xor_2_out[3], xor_2_out[4], xor_2_out[5], xor_2_out[6], xor_2_out[7], xor_2_out[8]);
  or or_9 (or_9_out, xor_3_out[0], xor_3_out[1], xor_3_out[2], xor_3_out[3], xor_3_out[4], xor_3_out[5], xor_3_out[6], xor_3_out[7], xor_3_out[8]);
  or or_10 (or_10_out, xor_4_out[0], xor_4_out[1], xor_4_out[2], xor_4_out[3], xor_4_out[4], xor_4_out[5], xor_4_out[6], xor_4_out[7], xor_4_out[8]);
  and and_6 (and_6_out, ~or_7_out, d_ff_2_q);  // AND_Gate
  and and_7 (and_7_out, ~or_8_out, d_ff_3_q);  // AND_Gate
  and and_8 (and_8_out, ~or_9_out, d_ff_4_q);  // AND_Gate
  and and_9 (and_9_out, ~or_10_out, d_ff_5_q);  // AND_Gate
  Register #(.width(2)) register_7 (
    .D(adder_2_out), .en(decoder_1_out1), .Q(register_7_q), .clk(undriven_9));  // open: clr
  Register #(.width(16), .trigger("falling")) register_8 (
    .D(undriven_5[31:16]), .en(and_10_out), .Q(register_8_q), .clk(or_2_out));  // open: clr
  and and_10 (and_10_out, undriven_9, decoder_6_out0);
  Register #(.width(16), .trigger("falling")) register_9 (
    .D(undriven_5[31:16]), .en(and_11_out), .Q(register_9_q), .clk(or_2_out));  // open: clr
  and and_11 (and_11_out, undriven_9, decoder_6_out1);
  Register #(.width(16), .trigger("falling")) register_10 (
    .D(undriven_5[31:16]), .en(and_12_out), .Q(register_10_q), .clk(or_2_out));  // open: clr
  and and_12 (and_12_out, undriven_9, decoder_6_out2);
  Register #(.width(16), .trigger("falling")) register_11 (
    .D(undriven_5[31:16]), .en(and_13_out), .Q(register_11_q), .clk(or_2_out));  // open: clr
  and and_13 (and_13_out, undriven_9, decoder_6_out3);
  Multiplexer #(.width(2), .enable("false")) multiplexer_6 (
    .in0(register_7_q), .in1(2'b11), .out(multiplexer_6_out), .sel(d_ff_5_qn));
  Multiplexer #(.width(2), .enable("false")) multiplexer_7 (
    .in0(multiplexer_6_out), .in1(2'b10), .out(multiplexer_7_out), .sel(d_ff_4_qn));
  Multiplexer #(.width(2), .enable("false")) multiplexer_8 (
    .in0(multiplexer_7_out), .in1(2'b01), .out(multiplexer_8_out), .sel(d_ff_3_qn));
  Multiplexer #(.width(2), .enable("false")) multiplexer_9 (
    .in0(multiplexer_8_out), .in1(2'b00), .out(multiplexer_9_out), .sel(d_ff_2_qn));
  Adder #(.width(2)) adder_2 (.a(register_7_q), .b(2'b00), .out(adder_2_out), .cin(1'b1));  // open: cout
  Multiplexer #(.width(16), .enable("false")) multiplexer_10 (
    .in0({16{1'b0}}), .in1(register_8_q), .out(multiplexer_10_out), .sel(and_14_out));
  and and_14 (and_14_out, and_6_out, decoder_2_out0, multiplexer_2_out);
  Multiplexer #(.width(16), .enable("false")) multiplexer_11 (
    .in0(multiplexer_10_out), .in1(register_9_q), .out(multiplexer_11_out), .sel(and_15_out));
  and and_15 (and_15_out, and_7_out, decoder_3_out0, multiplexer_2_out);
  Multiplexer #(.width(16), .enable("false")) multiplexer_12 (
    .in0(multiplexer_11_out), .in1(register_10_q), .out(multiplexer_12_out), .sel(and_16_out));
  and and_16 (and_16_out, and_8_out, decoder_4_out0, multiplexer_2_out);
  Multiplexer #(.width(16), .enable("false")) multiplexer_13 (
    .in0(multiplexer_12_out), .in1(register_11_q), .out(multiplexer_13_out), .sel(and_17_out));
  and and_17 (and_17_out, and_9_out, decoder_5_out0, multiplexer_2_out);
  Decoder #(.select(2), .disabled(0)) decoder_6 (
    .out0(decoder_6_out0), .out1(decoder_6_out1), .out2(decoder_6_out2), .out3(decoder_6_out3),
    .sel(multiplexer_9_out), .en(d_ff_1_q));
  Register #(.width(16), .trigger("falling")) register_12 (
    .D(undriven_5[15:0]), .en(and_18_out), .Q(register_12_q), .clk(or_2_out));  // open: clr
  and and_18 (and_18_out, undriven_9, decoder_6_out0);
  Register #(.width(16), .trigger("falling")) register_13 (
    .D(undriven_5[15:0]), .en(and_19_out), .Q(register_13_q), .clk(or_2_out));  // open: clr
  and and_19 (and_19_out, undriven_9, decoder_6_out1);
  Register #(.width(16), .trigger("falling")) register_14 (
    .D(undriven_5[15:0]), .en(and_20_out), .Q(register_14_q), .clk(or_2_out));  // open: clr
  and and_20 (and_20_out, undriven_9, decoder_6_out2);
  Register #(.width(16), .trigger("falling")) register_15 (
    .D(undriven_5[15:0]), .en(and_21_out), .Q(register_15_q), .clk(or_2_out));  // open: clr
  and and_21 (and_21_out, undriven_9, decoder_6_out3);
  Decoder #(.select(2), .disabled(0)) decoder_7 (
    .out0(decoder_7_out0), .out1(decoder_7_out1), .out2(decoder_7_out2), .out3(decoder_7_out3),
    .sel(multiplexer_9_out), .en(decoder_1_out3));
  Multiplexer #(.width(16), .enable("false")) multiplexer_14 (
    .in0(multiplexer_13_out), .in1(register_12_q), .out(multiplexer_14_out), .sel(and_22_out));
  and and_22 (and_22_out, and_6_out, decoder_2_out1, multiplexer_2_out);
  Multiplexer #(.width(16), .enable("false")) multiplexer_15 (
    .in0(multiplexer_14_out), .in1(register_13_q), .out(multiplexer_15_out), .sel(and_23_out));
  and and_23 (and_23_out, and_7_out, decoder_3_out1, multiplexer_2_out);
  Multiplexer #(.width(16), .enable("false")) multiplexer_16 (
    .in0(multiplexer_15_out), .in1(register_14_q), .out(multiplexer_16_out), .sel(and_24_out));
  and and_24 (and_24_out, and_8_out, decoder_4_out1, multiplexer_2_out);
  Multiplexer #(.width(16), .enable("false")) multiplexer_17 (
    .in0(multiplexer_16_out), .in1(register_15_q), .out(multiplexer_17_out), .sel(and_25_out));
  and and_25 (and_25_out, and_9_out, decoder_5_out1, multiplexer_2_out);
  and and_26 (and_26_out, undriven_9, decoder_6_out0);
  and and_27 (and_27_out, undriven_9, decoder_6_out1);
  and and_28 (and_28_out, undriven_9, decoder_6_out2);
  and and_29 (and_29_out, undriven_9, decoder_6_out3);
  Register #(.width(16), .trigger("falling")) register_16 (
    .D(undriven_6[31:16]), .en(and_26_out), .Q(register_16_q), .clk(or_2_out));  // open: clr
  and and_30 (and_30_out, and_6_out, decoder_2_out2, multiplexer_2_out);
  Register #(.width(16), .trigger("falling")) register_17 (
    .D(undriven_6[31:16]), .en(and_27_out), .Q(register_17_q), .clk(or_2_out));  // open: clr
  and and_31 (and_31_out, and_7_out, decoder_3_out2, multiplexer_2_out);
  Register #(.width(16), .trigger("falling")) register_18 (
    .D(undriven_6[31:16]), .en(and_28_out), .Q(register_18_q), .clk(or_2_out));  // open: clr
  and and_32 (and_32_out, and_8_out, decoder_4_out2, multiplexer_2_out);
  Register #(.width(16), .trigger("falling")) register_19 (
    .D(undriven_6[31:16]), .en(and_29_out), .Q(register_19_q), .clk(or_2_out));  // open: clr
  and and_33 (and_33_out, and_9_out, decoder_5_out2, multiplexer_2_out);
  Multiplexer #(.width(16), .enable("false")) multiplexer_18 (
    .in0(multiplexer_17_out), .in1(register_16_q), .out(multiplexer_18_out), .sel(and_30_out));
  Multiplexer #(.width(16), .enable("false")) multiplexer_19 (
    .in0(multiplexer_18_out), .in1(register_17_q), .out(multiplexer_19_out), .sel(and_31_out));
  Multiplexer #(.width(16), .enable("false")) multiplexer_20 (
    .in0(multiplexer_19_out), .in1(register_18_q), .out(multiplexer_20_out), .sel(and_32_out));
  Multiplexer #(.width(16), .enable("false")) multiplexer_21 (
    .in0(multiplexer_20_out), .in1(register_19_q), .out(multiplexer_21_out), .sel(and_33_out));
  Register #(.width(16), .trigger("falling")) register_20 (
    .D(undriven_6[15:0]), .en(and_34_out), .Q(register_20_q), .clk(or_2_out));  // open: clr
  and and_34 (and_34_out, undriven_9, decoder_6_out0);
  Register #(.width(16), .trigger("falling")) register_21 (
    .D(undriven_6[15:0]), .en(and_35_out), .Q(register_21_q), .clk(or_2_out));  // open: clr
  and and_35 (and_35_out, undriven_9, decoder_6_out1);
  Register #(.width(16), .trigger("falling")) register_22 (
    .D(undriven_6[15:0]), .en(and_36_out), .Q(register_22_q), .clk(or_2_out));  // open: clr
  and and_36 (and_36_out, undriven_9, decoder_6_out2);
  Register #(.width(16), .trigger("falling")) register_23 (
    .D(undriven_6[15:0]), .en(and_37_out), .Q(register_23_q), .clk(or_2_out));  // open: clr
  and and_37 (and_37_out, undriven_9, decoder_6_out3);
  Multiplexer #(.width(16), .enable("false")) multiplexer_22 (
    .in0(multiplexer_21_out), .in1(register_20_q), .out(multiplexer_22_out), .sel(and_38_out));
  and and_38 (and_38_out, and_6_out, decoder_2_out3, multiplexer_2_out);
  Multiplexer #(.width(16), .enable("false")) multiplexer_23 (
    .in0(multiplexer_22_out), .in1(register_21_q), .out(multiplexer_23_out), .sel(and_39_out));
  and and_39 (and_39_out, and_7_out, decoder_3_out3, multiplexer_2_out);
  Multiplexer #(.width(16), .enable("false")) multiplexer_24 (
    .in0(multiplexer_23_out), .in1(register_22_q), .out(multiplexer_24_out), .sel(and_40_out));
  and and_40 (and_40_out, and_8_out, decoder_4_out3, multiplexer_2_out);
  Multiplexer #(.width(16), .enable("false")) multiplexer_25 (
    .in0(multiplexer_24_out), .in1(register_23_q), .out(out_8), .sel(and_41_out));
  and and_41 (and_41_out, and_9_out, decoder_5_out3, multiplexer_2_out);

  // Notes on the sheet:
  //   Read to Ins and ins Ext
  //   Main ON
  //   Data from Main ram
  //   1=miss 0=hit
  //   Miss Counter
  //   1=empty 0=with data
  //   Read Main mem
endmodule
