// Logisim project 8.3.1 MMU.circ as structural Verilog: 1 circuit, main circuit main
module main (
  input  in_1,
  input  in_2,
  input  in_3,
  input  Keyboard_IN,
  input  in_5,
  input  in_6,
  input  in_7,
  input  in_8,
  input  in_9,
  input  [7:0] Data_In,
  input  [11:0] Adr_In,
  input  Write_Ram,
  input  in_13,
  output [11:0] PC,
  output [15:0] Instruc,
  output [7:0] Reg_0,
  output [7:0] Reg_1,
  output [7:0] Reg_2,
  output [7:0] Reg_3,
  output [15:0] out_20,
  output [7:0] Reg_4,
  output [7:0] Reg_5,
  output [7:0] Reg_6,
  output [7:0] Reg_7,
  output [7:0] Read_Ram,
  output [7:0] Reg_8,
  output [7:0] Reg_9,
  output [7:0] Reg_A,
  output [7:0] Reg_B,
  output [7:0] Reg_C,
  output [7:0] Reg_D,
  output [7:0] Reg_E,
  output [7:0] Reg_F
);

  wire _0_out, _1_out, _2a_out, _2b_out, _3_out, _4_out, _5_out, _6_out, _7_out, _8_out, _9_out, _20_out,
       _21_out, _22_out, _23_out, _24_out, _25_out, _26_out, _27_out, _28_out, _29_out, a_out, adder_2_cout,
       and_1_out, and_2_out, and_3_out, and_4_out, and_5_out, and_6_out, and_7_out, and_8_out, and_9_out,
       and_10_out, and_11_out, and_12_out, and_13_out, and_14_out, and_15_out, and_16_out, and_18_out,
       and_19_out, and_20_out, and_21_out, and_22_out, and_23_out, and_24_out, and_25_out, and_26_out,
       and_27_out, and_28_out, and_29_out, and_30_out, and_31_out, and_32_out, and_33_out, and_34_out,
       and_35_out, and_36_out, and_37_out, and_38_out, and_39_out, and_40_out, and_41_out, and_42_out,
       and_43_out, and_44_out, and_45_out, and_46_out, b_out, button_1_out, c_out, clock_1_out, d_ff_1_q,
       d_ff_1_qn, d_ff_2_q, d_ff_2_qn, d_ff_3_q, d_ff_4_q, d_ff_4_qn, d_ff_5_q, d_ff_5_qn, d_ff_6_q,
       d_ff_7_q, d_ff_8_q, d_ff_8_qn, d_ff_9_q, d_ff_9_qn, d_ff_10_q, d_ff_10_qn, d_ff_11_q, d_ff_12_q,
       d_out, decoder_1_out0, decoder_1_out1, decoder_1_out2, decoder_1_out3, decoder_1_out4, decoder_1_out5,
       decoder_1_out6, decoder_1_out7, decoder_1_out8, decoder_1_out9, decoder_1_out10, decoder_1_out11,
       decoder_1_out12, decoder_1_out13, decoder_1_out14, decoder_1_out15, decoder_2_out0, decoder_2_out1,
       decoder_2_out2, decoder_2_out3, decoder_2_out4, decoder_2_out5, decoder_2_out6, decoder_2_out7,
       decoder_2_out8, decoder_2_out9, decoder_2_out10, decoder_2_out11, decoder_2_out12, decoder_2_out13,
       decoder_2_out14, decoder_2_out15, decoder_3_out0, decoder_3_out1, decoder_3_out2, decoder_3_out3,
       decoder_3_out4, decoder_3_out5, decoder_3_out6, decoder_3_out7, decoder_3_out8, decoder_3_out9,
       decoder_3_out10, decoder_3_out11, decoder_3_out12, decoder_3_out13, decoder_3_out14, decoder_3_out15,
       decoder_4_out0, decoder_4_out1, decoder_4_out2, decoder_4_out3, decoder_4_out4, decoder_4_out5,
       decoder_4_out6, decoder_4_out7, decoder_4_out8, decoder_4_out9, decoder_4_out10, decoder_4_out11,
       decoder_4_out12, decoder_4_out13, decoder_4_out14, decoder_4_out15, decoder_5_out0, decoder_5_out1,
       decoder_5_out2, decoder_5_out3, decoder_5_out4, decoder_5_out5, decoder_5_out6, decoder_5_out7,
       decoder_5_out8, decoder_5_out9, decoder_5_out10, decoder_5_out11, decoder_5_out12, decoder_5_out13,
       decoder_5_out14, decoder_5_out15, decoder_6_out0, decoder_6_out1, decoder_6_out2, decoder_6_out3,
       decoder_6_out4, decoder_6_out5, decoder_6_out6, decoder_6_out7, decoder_6_out8, decoder_6_out9,
       decoder_6_out10, decoder_6_out11, decoder_6_out12, decoder_6_out13, decoder_6_out14, decoder_6_out15,
       decoder_7_out0, decoder_7_out1, decoder_7_out2, decoder_7_out3, decoder_7_out4, decoder_7_out5,
       decoder_7_out6, decoder_7_out7, decoder_7_out8, decoder_7_out9, decoder_7_out10, decoder_7_out11,
       decoder_7_out12, decoder_7_out13, decoder_7_out14, decoder_7_out15, decoder_8_out0, decoder_8_out1,
       decoder_8_out2, decoder_8_out3, decoder_8_out4, decoder_8_out5, decoder_8_out6, decoder_8_out7,
       decoder_8_out8, decoder_8_out9, decoder_8_out10, decoder_8_out11, decoder_8_out12, decoder_8_out13,
       decoder_8_out14, decoder_8_out15, decoder_9_out0, decoder_9_out1, decoder_9_out2, decoder_9_out3,
       decoder_9_out4, decoder_9_out5, decoder_9_out6, decoder_9_out7, decoder_9_out8, decoder_9_out9,
       decoder_9_out10, decoder_9_out11, decoder_9_out12, decoder_9_out13, decoder_9_out14, decoder_9_out15,
       decoder_10_out0, decoder_10_out1, decoder_10_out2, decoder_10_out3, decoder_10_out4, decoder_10_out5,
       decoder_10_out6, decoder_10_out7, decoder_10_out8, decoder_10_out9, decoder_10_out10,
       decoder_10_out11, decoder_10_out12, decoder_10_out13, decoder_10_out14, decoder_10_out15,
       decoder_11_out0, decoder_11_out1, decoder_11_out2, decoder_11_out3, decoder_11_out4, decoder_11_out5,
       decoder_11_out6, decoder_11_out7, decoder_11_out8, decoder_11_out9, decoder_11_out10,
       decoder_11_out11, decoder_11_out12, decoder_11_out13, decoder_11_out14, decoder_11_out15,
       decoder_12_out0, decoder_12_out1, decoder_12_out2, decoder_12_out3, decoder_12_out4, decoder_12_out5,
       decoder_12_out6, decoder_12_out7, decoder_12_out8, decoder_12_out9, decoder_12_out10,
       decoder_12_out11, decoder_12_out12, decoder_12_out13, decoder_12_out14, decoder_12_out15,
       decoder_13_out0, decoder_13_out1, decoder_13_out2, decoder_13_out3, decoder_13_out4, decoder_13_out5,
       decoder_13_out6, decoder_13_out7, decoder_13_out8, decoder_13_out9, decoder_13_out10,
       decoder_13_out11, decoder_13_out12, decoder_13_out13, decoder_13_out14, decoder_13_out15,
       decoder_14_out0, decoder_14_out1, decoder_14_out2, decoder_14_out3, decoder_14_out4, decoder_14_out5,
       decoder_14_out6, decoder_14_out7, decoder_14_out8, decoder_14_out9, decoder_14_out10,
       decoder_14_out11, decoder_14_out12, decoder_14_out13, decoder_14_out14, decoder_14_out15,
       decoder_15_out0, decoder_15_out1, decoder_15_out2, decoder_15_out3, decoder_16_out0, decoder_16_out1,
       decoder_16_out2, decoder_16_out3, decoder_16_out4, decoder_16_out5, decoder_16_out6, decoder_16_out7,
       decoder_16_out8, decoder_16_out9, decoder_16_out10, decoder_16_out11, decoder_16_out12,
       decoder_16_out13, decoder_16_out14, decoder_16_out15, decoder_17_out0, decoder_17_out1,
       decoder_17_out2, decoder_17_out3, decoder_17_out4, decoder_17_out5, decoder_17_out6, decoder_17_out7,
       decoder_17_out8, decoder_17_out9, decoder_17_out10, decoder_17_out11, decoder_17_out12,
       decoder_17_out13, decoder_17_out14, decoder_17_out15, decoder_18_out3, decoder_18_out4,
       decoder_18_out5, decoder_18_out6, e_out, f0_out, f1_out, fe_out, fffe_out, ffff_out,
       multiplexer_43_out, multiplexer_101_out, multiplexer_102_out, multiplexer_137_out,
       multiplexer_138_out, multiplexer_139_out, multiplexer_144_out, multiplexer_145_out,
       multiplexer_146_out, nand_1_out, nand_2_out, nand_3_out, nand_4_out, nand_5_out, nand_6_out,
       not_2_out, Off_out, On_2_out, On_out, or_1_out, or_2_out, or_3_out, or_4_out, or_5_out, or_6_out,
       or_7_out, or_8_out, or_9_out, or_10_out, or_11_out, or_12_out, or_13_out, or_14_out, or_15_out,
       or_16_out, or_17_out, or_18_out, or_19_out, or_20_out, or_21_out, or_22_out, or_23_out, or_24_out,
       or_25_out, or_26_out, or_27_out, or_28_out, or_29_out, or_30_out, or_31_out, or_32_out, or_33_out,
       or_34_out, or_35_out, or_36_out, or_37_out, or_38_out, or_39_out, or_40_out, or_41_out, or_42_out,
       or_43_out, or_44_out, or_45_out, or_46_out, or_47_out, or_48_out, or_49_out, or_50_out, or_51_out,
       or_52_out, or_53_out, or_54_out, or_55_out, or_56_out, or_57_out, or_58_out, or_59_out, or_60_out,
       or_61_out, or_62_out, or_63_out, or_64_out, or_65_out, or_66_out, or_67_out, or_68_out, or_69_out,
       or_70_out, or_71_out, or_72_out, or_73_out, or_74_out, or_75_out, or_76_out, or_77_out, or_78_out,
       or_79_out, or_80_out, or_81_out, or_82_out, or_83_out, or_84_out, or_85_out, or_86_out, or_87_out,
       or_88_out, or_89_out, or_90_out, or_91_out, or_92_out, or_93_out, or_94_out, or_95_out, or_96_out,
       or_97_out, or_98_out, or_99_out, or_100_out, or_101_out, or_105_out, or_107_out, or_108_out,
       or_109_out, or_110_out, or_111_out, or_112_out, or_113_out, or_114_out, or_115_out, or_116_out,
       or_117_out, or_118_out, or_119_out, or_120_out, or_121_out, or_122_out, or_123_out, or_124_out,
       or_125_out, or_145_out, or_146_out, or_148_out, or_150_out, or_151_out, or_153_out, or_154_out,
       or_155_out, or_156_out, or_157_out, or_158_out, register_22_q, register_25_q, register_28_q, undriven,
       undriven_2, undriven_3, undriven_4, undriven_5, undriven_6, undriven_7, undriven_8, undriven_9,
       undriven_10, undriven_11, undriven_12, undriven_13, undriven_14, undriven_15, undriven_16,
       undriven_17, undriven_18, undriven_19, undriven_20, undriven_21, undriven_22, undriven_23,
       undriven_24, undriven_25, undriven_26, undriven_27, undriven_28, undriven_29, undriven_30,
       undriven_31, undriven_32, undriven_33, undriven_34, undriven_35, undriven_36, undriven_37,
       undriven_38, undriven_39, undriven_40;
  wire [1:0] adder_6_out, multiplexer_131_out, register_18_q;
  wire [2:0] adder_10_out, multiplexer_156_out, register_30_q;
  wire [3:0] adder_7_out, demultiplexer_1_out0, demultiplexer_1_out1, demultiplexer_2_out0,
       demultiplexer_2_out1, multiplexer_21_out, multiplexer_22_out, multiplexer_23_out, multiplexer_24_out,
       multiplexer_25_out, multiplexer_26_out, multiplexer_77_out_2, multiplexer_77_out_3,
       multiplexer_78_out_2, multiplexer_123_out, multiplexer_129_out_2, multiplexer_132_out,
       multiplexer_133_out, multiplexer_134_out, register_19_q;
  wire [5:0] adder_8_out_2, adder_9_out, multiplexer_140_out, multiplexer_154_out, multiplexer_155_out,
       register_29_q;
  wire [7:0] adder_2_out, adder_3_out, and_17_out, divider_1_out, divider_1_rem, Exc_Code_q, Exc_Data_q,
       Hi_q, Lo_q, multiplexer_1_out, multiplexer_2_out, multiplexer_3_out, multiplexer_4_out,
       multiplexer_5_out, multiplexer_6_out, multiplexer_7_out, multiplexer_8_out, multiplexer_9_out,
       multiplexer_10_out, multiplexer_11_out, multiplexer_12_out, multiplexer_13_out, multiplexer_14_out,
       multiplexer_15_out, multiplexer_16_out, multiplexer_17_out, multiplexer_18_out, multiplexer_19_out,
       multiplexer_20_out, multiplexer_27_out, multiplexer_28_out, multiplexer_29_out, multiplexer_30_out,
       multiplexer_31_out, multiplexer_32_out, multiplexer_33_out, multiplexer_34_out, multiplexer_35_out,
       multiplexer_36_out, multiplexer_37_out, multiplexer_38_out, multiplexer_39_out, multiplexer_40_out,
       multiplexer_41_out, multiplexer_42_out, multiplexer_44_out, multiplexer_45_out, multiplexer_46_out,
       multiplexer_47_out, multiplexer_48_out, multiplexer_49_out, multiplexer_50_out, multiplexer_51_out,
       multiplexer_52_out, multiplexer_53_out, multiplexer_54_out, multiplexer_55_out, multiplexer_56_out,
       multiplexer_57_out, multiplexer_58_out, multiplexer_59_out, multiplexer_60_out, multiplexer_61_out,
       multiplexer_62_out, multiplexer_63_out, multiplexer_64_out, multiplexer_65_out, multiplexer_66_out,
       multiplexer_67_out, multiplexer_68_out, multiplexer_69_out, multiplexer_70_out, multiplexer_71_out,
       multiplexer_72_out, multiplexer_73_out, multiplexer_74_out, multiplexer_75_out, multiplexer_77_out,
       multiplexer_78_out, multiplexer_80_out, multiplexer_81_out, multiplexer_82_out, multiplexer_83_out,
       multiplexer_84_out, multiplexer_85_out, multiplexer_86_out, multiplexer_87_out, multiplexer_88_out,
       multiplexer_89_out, multiplexer_90_out, multiplexer_91_out, multiplexer_92_out, multiplexer_93_out,
       multiplexer_94_out, multiplexer_95_out, multiplexer_100_out, multiplexer_103_out, multiplexer_104_out,
       multiplexer_105_out, multiplexer_106_out, multiplexer_107_out, multiplexer_108_out,
       multiplexer_109_out, multiplexer_110_out, multiplexer_111_out, multiplexer_112_out,
       multiplexer_113_out, multiplexer_114_out, multiplexer_115_out, multiplexer_116_out,
       multiplexer_122_out, multiplexer_123_out_2, multiplexer_124_out, multiplexer_125_out,
       multiplexer_126_out, multiplexer_127_out, multiplexer_135_out, multiplexer_141_out,
       multiplexer_149_out, multiplexer_152_out, multiplexer_157_out, multiplexer_158_out, multiplier_1_cout,
       multiplier_1_out, not_1_out, or_106_out, or_126_out, or_128_out, or_129_out, or_130_out, or_152_out,
       ram_1_data, ram_2_data, ram_3_data, ram_4_data, ram_5_data, ram_6_data, register_1_q, register_2_q,
       register_3_q, register_4_q, register_5_q, register_6_q, register_7_q, register_8_q, register_9_q,
       register_10_q, register_11_q, register_12_q, register_13_q, register_14_q, register_15_q,
       register_16_q, register_20_q, register_21_q, register_23_q, register_24_q, register_26_q,
       register_27_q, xor_1_out;
  wire [7:1] or_131_out;
  wire [7:7] Carry_q;
  wire [11:0] adder_1_out, adder_4_out, multiplexer_76_out, multiplexer_96_out, multiplexer_98_out,
       multiplexer_117_out, multiplexer_118_out, multiplexer_119_out, multiplexer_120_out,
       multiplexer_121_out, multiplexer_129_out, multiplexer_136_out, multiplexer_143_out,
       multiplexer_150_out, multiplexer_151_out, or_102_out, or_103_out, or_104_out, or_147_out, or_149_out;
  wire [11:6] adder_8_out;
  wire [13:0] multiplexer_147_out, multiplexer_148_out;
  wire [15:0] adder_5_out, multiplexer_79_out, multiplexer_97_out, multiplexer_99_out, multiplexer_128_out,
       multiplexer_130_out, multiplexer_142_out, multiplexer_153_out, xor_2_out;

  nand nand_1 (nand_1_out, undriven_16, undriven_9);
  nand nand_2 (nand_2_out, undriven_5, undriven);
  nand nand_3 (nand_3_out, undriven_2, undriven_6);
  nand nand_4 (nand_4_out, undriven_10, undriven_11);
  or or_1 (or_1_out, undriven_7, undriven_3);
  or or_2 (or_2_out, undriven_12, undriven_13);
  or or_3 (or_3_out, undriven_4, undriven_8);
  or or_4 (or_4_out, undriven_14, undriven_15);
  D_Flip_Flop d_ff_1 (
    .clk(undriven_21), .D(undriven_17), .Q(d_ff_1_q), .Qn(d_ff_1_qn), .en(undriven_18), .reset(undriven_24));  // open: preset
  and and_1 (and_1_out, undriven_22, undriven_19);
  and and_2 (and_2_out, undriven_20, undriven_23);
  D_Flip_Flop d_ff_2 (
    .clk(undriven_27), .D(undriven_25), .Q(d_ff_2_q), .Qn(d_ff_2_qn), .en(undriven_26), .reset(undriven_32));  // open: preset
  and and_3 (and_3_out, undriven_28, undriven_29);
  and and_4 (and_4_out, undriven_30, undriven_31);
  Multiplexer #(.width(8), .disabled(0), .enable("false")) multiplexer_1 (
    .in0(Read_Ram), .in1({adder_8_out[7:6], adder_8_out_2}), .out(multiplexer_1_out), .sel(or_59_out));
  Multiplexer #(.width(8), .disabled(0), .enable("false")) multiplexer_2 (
    .in0(Read_Ram), .in1({4'b0000, adder_8_out[11:8]}), .out(multiplexer_2_out), .sel(or_59_out));
  Multiplexer #(.width(8), .disabled(0), .enable("false")) multiplexer_3 (
    .in0(multiplexer_1_out), .in1(multiplexer_78_out), .out(multiplexer_3_out), .sel(c_out));
  Multiplexer #(.width(8), .disabled(0), .enable("false")) multiplexer_4 (
    .in0(multiplexer_2_out), .in1({4'b0000, multiplexer_78_out_2}), .out(multiplexer_4_out), .sel(c_out));
  LED led_1 (.in(register_19_q[2]));
  LED led_2 (.in(register_19_q[3]));
  Button On (.out(On_out));
  Clock clock_1 (.out(clock_1_out));
  Button Off (.out(Off_out));
  Counter #(.width(32), .max('hffffffff)) Clocks (
    .count(d_ff_12_q), .clk(clock_1_out), .clr(On_out));  // open: load, D, Q, carry
  Counter #(.width(32), .max('hffffffff)) u_Instruc (
    .count(decoder_14_out1), .clk(clock_1_out), .clr(On_out));  // open: load, D, Q, carry
  LED led_3 (.in(register_19_q[1]));
  LED led_4 (.in(register_19_q[0]));
  Decoder #(.select(4), .disabled(0)) decoder_1 (
    .out0(decoder_1_out0), .out1(decoder_1_out1), .out2(decoder_1_out2), .out3(decoder_1_out3),
    .out4(decoder_1_out4), .out5(decoder_1_out5), .out6(decoder_1_out6), .out7(decoder_1_out7),
    .out8(decoder_1_out8), .out9(decoder_1_out9), .out10(decoder_1_out10), .out11(decoder_1_out11),
    .out12(decoder_1_out12), .out13(decoder_1_out13), .out14(decoder_1_out14), .out15(decoder_1_out15),
    .sel(multiplexer_77_out[3:0]), .en(decoder_2_out15));
  Button On_2 (.out(On_2_out));
  or or_5 (or_5_out, Write_Ram, or_80_out);
  Decoder #(.select(4), .disabled(0)) decoder_2 (
    .out0(decoder_2_out0), .out1(decoder_2_out1), .out2(decoder_2_out2), .out3(decoder_2_out3),
    .out4(decoder_2_out4), .out5(decoder_2_out5), .out6(decoder_2_out6), .out7(decoder_2_out7),
    .out8(decoder_2_out8), .out9(decoder_2_out9), .out10(decoder_2_out10), .out11(decoder_2_out11),
    .out12(decoder_2_out12), .out13(decoder_2_out13), .out14(decoder_2_out14), .out15(decoder_2_out15),
    .sel(multiplexer_77_out[7:4]), .en(decoder_4_out15));
  or or_6 (or_6_out, in_13, or_69_out);
  Decoder #(.select(4), .disabled(0)) decoder_3 (
    .out0(decoder_3_out0), .out1(decoder_3_out1), .out2(decoder_3_out2), .out3(decoder_3_out3),
    .out4(decoder_3_out4), .out5(decoder_3_out5), .out6(decoder_3_out6), .out7(decoder_3_out7),
    .out8(decoder_3_out8), .out9(decoder_3_out9), .out10(decoder_3_out10), .out11(decoder_3_out11),
    .out12(decoder_3_out12), .out13(decoder_3_out13), .out14(decoder_3_out14), .out15(decoder_3_out15),
    .sel(multiplexer_77_out_2), .en(decoder_5_out2));
  Decoder #(.select(4), .disabled(0)) decoder_4 (
    .out0(decoder_4_out0), .out1(decoder_4_out1), .out2(decoder_4_out2), .out3(decoder_4_out3),
    .out4(decoder_4_out4), .out5(decoder_4_out5), .out6(decoder_4_out6), .out7(decoder_4_out7),
    .out8(decoder_4_out8), .out9(decoder_4_out9), .out10(decoder_4_out10), .out11(decoder_4_out11),
    .out12(decoder_4_out12), .out13(decoder_4_out13), .out14(decoder_4_out14), .out15(decoder_4_out15),
    .sel(multiplexer_77_out_2), .en(decoder_5_out15));
  Decoder #(.select(4), .disabled(0), .enable("false")) decoder_5 (
    .out0(decoder_5_out0), .out1(decoder_5_out1), .out2(decoder_5_out2), .out3(decoder_5_out3),
    .out4(decoder_5_out4), .out5(decoder_5_out5), .out6(decoder_5_out6), .out7(decoder_5_out7),
    .out8(decoder_5_out8), .out9(decoder_5_out9), .out10(decoder_5_out10), .out11(decoder_5_out11),
    .out12(decoder_5_out12), .out13(decoder_5_out13), .out14(decoder_5_out14), .out15(decoder_5_out15),
    .sel(multiplexer_77_out_3));
  Register u_Reg_0 (.D(multiplexer_3_out), .en(decoder_6_out0), .Q(Reg_0), .clk(clock_1_out));  // open: clr
  Register u_Reg_1 (.D(multiplexer_4_out), .en(decoder_6_out1), .Q(Reg_1), .clk(clock_1_out));  // open: clr
  Register u_Reg_2 (.D(multiplexer_3_out), .en(decoder_6_out2), .Q(Reg_2), .clk(clock_1_out));  // open: clr
  Register u_Reg_3 (.D(multiplexer_4_out), .en(decoder_6_out3), .Q(Reg_3), .clk(clock_1_out));  // open: clr
  Register u_Reg_4 (.D(multiplexer_3_out), .en(decoder_6_out4), .Q(Reg_4), .clk(clock_1_out));  // open: clr
  Register u_Reg_5 (.D(multiplexer_4_out), .en(decoder_6_out5), .Q(Reg_5), .clk(clock_1_out));  // open: clr
  Register u_Reg_6 (.D(multiplexer_3_out), .en(or_90_out), .Q(Reg_6), .clk(clock_1_out));  // open: clr
  Register u_Reg_7 (.D(multiplexer_4_out), .en(decoder_6_out7), .Q(Reg_7), .clk(clock_1_out));  // open: clr
  Register u_Reg_8 (.D(multiplexer_3_out), .en(or_91_out), .Q(Reg_8), .clk(clock_1_out));  // open: clr
  Register u_Reg_9 (.D(multiplexer_4_out), .en(or_89_out), .Q(Reg_9), .clk(clock_1_out));  // open: clr
  Register u_Reg_A (.D(multiplexer_3_out), .en(or_88_out), .Q(Reg_A), .clk(clock_1_out));  // open: clr
  Register u_Reg_B (.D(multiplexer_4_out), .en(or_87_out), .Q(Reg_B), .clk(clock_1_out));  // open: clr
  Register u_Reg_C (.D(multiplexer_3_out), .en(or_86_out), .Q(Reg_C), .clk(clock_1_out));  // open: clr
  Register u_Reg_D (.D(multiplexer_4_out), .en(or_84_out), .Q(Reg_D), .clk(clock_1_out));  // open: clr
  Register u_Reg_E (.D(multiplexer_3_out), .en(or_85_out), .Q(Reg_E), .clk(clock_1_out));  // open: clr
  Register u_Reg_F (.D(multiplexer_4_out), .en(or_83_out), .Q(Reg_F), .clk(clock_1_out));  // open: clr
  Multiplexer #(.width(8), .enable("false")) multiplexer_5 (
    .in0({8{1'b0}}), .in1(Reg_0), .out(multiplexer_5_out), .sel(decoder_7_out0));
  Multiplexer #(.width(8), .enable("false")) multiplexer_6 (
    .in0(multiplexer_5_out), .in1(Reg_1), .out(multiplexer_6_out), .sel(decoder_7_out1));
  Multiplexer #(.width(8), .enable("false")) multiplexer_7 (
    .in0(multiplexer_6_out), .in1(Reg_2), .out(multiplexer_7_out), .sel(decoder_7_out2));
  Multiplexer #(.width(8), .enable("false")) multiplexer_8 (
    .in0(multiplexer_7_out), .in1(Reg_3), .out(multiplexer_8_out), .sel(decoder_7_out3));
  Multiplexer #(.width(8), .enable("false")) multiplexer_9 (
    .in0(multiplexer_8_out), .in1(Reg_4), .out(multiplexer_9_out), .sel(decoder_7_out4));
  Multiplexer #(.width(8), .enable("false")) multiplexer_10 (
    .in0(multiplexer_9_out), .in1(Reg_5), .out(multiplexer_10_out), .sel(decoder_7_out5));
  Multiplexer #(.width(8), .enable("false")) multiplexer_11 (
    .in0(multiplexer_10_out), .in1(Reg_6), .out(multiplexer_11_out), .sel(or_92_out));
  Multiplexer #(.width(8), .enable("false")) multiplexer_12 (
    .in0(multiplexer_11_out), .in1(Reg_7), .out(multiplexer_12_out), .sel(decoder_7_out7));
  Multiplexer #(.width(8), .enable("false")) multiplexer_13 (
    .in0(multiplexer_12_out), .in1(Reg_8), .out(multiplexer_13_out), .sel(decoder_7_out8));
  Multiplexer #(.width(8), .enable("false")) multiplexer_14 (
    .in0(multiplexer_13_out), .in1(Reg_9), .out(multiplexer_14_out), .sel(decoder_7_out9));
  Multiplexer #(.width(8), .enable("false")) multiplexer_15 (
    .in0(multiplexer_14_out), .in1(Reg_A), .out(multiplexer_15_out), .sel(decoder_7_out10));
  Multiplexer #(.width(8), .enable("false")) multiplexer_16 (
    .in0(multiplexer_15_out), .in1(Reg_B), .out(multiplexer_16_out), .sel(decoder_7_out11));
  Multiplexer #(.width(8), .enable("false")) multiplexer_17 (
    .in0(multiplexer_16_out), .in1(Reg_C), .out(multiplexer_17_out), .sel(decoder_7_out12));
  Multiplexer #(.width(8), .enable("false")) multiplexer_18 (
    .in0(multiplexer_17_out), .in1(Reg_D), .out(multiplexer_18_out), .sel(decoder_7_out13));
  Multiplexer #(.width(8), .enable("false")) multiplexer_19 (
    .in0(multiplexer_18_out), .in1(Reg_E), .out(multiplexer_19_out), .sel(decoder_7_out14));
  Multiplexer #(.width(8), .enable("false")) multiplexer_20 (
    .in0(multiplexer_19_out), .in1(Reg_F), .out(multiplexer_20_out), .sel(decoder_7_out15));
  Decoder #(.select(4), .disabled(0)) decoder_6 (
    .out0(decoder_6_out0), .out1(decoder_6_out1), .out2(decoder_6_out2), .out3(decoder_6_out3),
    .out4(decoder_6_out4), .out5(decoder_6_out5), .out6(decoder_6_out6), .out7(decoder_6_out7),
    .out8(decoder_6_out8), .out9(decoder_6_out9), .out10(decoder_6_out10), .out11(decoder_6_out11),
    .out12(decoder_6_out12), .out13(decoder_6_out13), .out14(decoder_6_out14), .out15(decoder_6_out15),
    .sel(multiplexer_21_out), .en(or_37_out));
  Multiplexer #(.width(4), .enable("false")) multiplexer_21 (
    .in0(multiplexer_77_out_2), .in1(multiplexer_77_out[7:4]), .out(multiplexer_21_out), .sel(or_39_out));
  Decoder #(.select(4), .disabled(0)) decoder_7 (
    .out0(decoder_7_out0), .out1(decoder_7_out1), .out2(decoder_7_out2), .out3(decoder_7_out3),
    .out4(decoder_7_out4), .out5(decoder_7_out5), .out6(decoder_7_out6), .out7(decoder_7_out7),
    .out8(decoder_7_out8), .out9(decoder_7_out9), .out10(decoder_7_out10), .out11(decoder_7_out11),
    .out12(decoder_7_out12), .out13(decoder_7_out13), .out14(decoder_7_out14), .out15(decoder_7_out15),
    .sel(multiplexer_22_out), .en(or_7_out));
  Multiplexer #(.width(4), .enable("false")) multiplexer_22 (
    .in0(multiplexer_77_out[7:4]), .in1(multiplexer_77_out_2), .out(multiplexer_22_out), .sel(_3_out));
  Decoder #(.select(4), .disabled(0)) decoder_8 (
    .out0(decoder_8_out0), .out1(decoder_8_out1), .out2(decoder_8_out2), .out3(decoder_8_out3),
    .out4(decoder_8_out4), .out5(decoder_8_out5), .out6(decoder_8_out6), .out7(decoder_8_out7),
    .out8(decoder_8_out8), .out9(decoder_8_out9), .out10(decoder_8_out10), .out11(decoder_8_out11),
    .out12(decoder_8_out12), .out13(decoder_8_out13), .out14(decoder_8_out14), .out15(decoder_8_out15),
    .sel(multiplexer_23_out), .en(or_8_out));
  Multiplexer #(.width(4), .enable("false")) multiplexer_23 (
    .in0(multiplexer_77_out[3:0]), .in1(4'b0000), .out(multiplexer_23_out), .sel(1'b0));
  Decoder #(.select(4), .disabled(0)) decoder_9 (
    .out0(decoder_9_out0), .out1(decoder_9_out1), .out2(decoder_9_out2), .out3(decoder_9_out3),
    .out4(decoder_9_out4), .out5(decoder_9_out5), .out6(decoder_9_out6), .out7(decoder_9_out7),
    .out8(decoder_9_out8), .out9(decoder_9_out9), .out10(decoder_9_out10), .out11(decoder_9_out11),
    .out12(decoder_9_out12), .out13(decoder_9_out13), .out14(decoder_9_out14), .out15(decoder_9_out15),
    .sel(multiplexer_24_out), .en(or_70_out));
  Multiplexer #(.width(4), .enable("false")) multiplexer_24 (
    .in0(multiplexer_77_out_2), .in1(multiplexer_77_out[7:4]), .out(multiplexer_24_out), .sel(f0_out));
  Decoder #(.select(4), .disabled(0)) decoder_10 (
    .out0(decoder_10_out0), .out1(decoder_10_out1), .out2(decoder_10_out2), .out3(decoder_10_out3),
    .out4(decoder_10_out4), .out5(decoder_10_out5), .out6(decoder_10_out6), .out7(decoder_10_out7),
    .out8(decoder_10_out8), .out9(decoder_10_out9), .out10(decoder_10_out10), .out11(decoder_10_out11),
    .out12(decoder_10_out12), .out13(decoder_10_out13), .out14(decoder_10_out14), .out15(decoder_10_out15),
    .sel(multiplexer_25_out), .en(or_52_out));
  Multiplexer #(.width(4), .enable("false")) multiplexer_25 (
    .in0(multiplexer_77_out[3:0]), .in1(4'b0000), .out(multiplexer_25_out), .sel(1'b0));
  Decoder #(.select(4), .disabled(0)) decoder_11 (
    .out0(decoder_11_out0), .out1(decoder_11_out1), .out2(decoder_11_out2), .out3(decoder_11_out3),
    .out4(decoder_11_out4), .out5(decoder_11_out5), .out6(decoder_11_out6), .out7(decoder_11_out7),
    .out8(decoder_11_out8), .out9(decoder_11_out9), .out10(decoder_11_out10), .out11(decoder_11_out11),
    .out12(decoder_11_out12), .out13(decoder_11_out13), .out14(decoder_11_out14), .out15(decoder_11_out15),
    .sel(multiplexer_26_out), .en(or_22_out));
  Multiplexer #(.width(4), .enable("false")) multiplexer_26 (
    .in0(multiplexer_77_out[7:4]), .in1(4'b0000), .out(multiplexer_26_out), .sel(1'b0));
  and _0 (_0_out, decoder_5_out0, decoder_14_out5);
  and _1 (_1_out, decoder_5_out1, decoder_14_out5);
  and _20 (_20_out, decoder_3_out0, decoder_14_out5);
  and _21 (_21_out, decoder_3_out1, decoder_14_out5);
  and _22 (_22_out, decoder_3_out2, decoder_14_out5);
  and _23 (_23_out, decoder_3_out3, decoder_14_out5);
  and _24 (_24_out, decoder_3_out4, decoder_14_out5);
  and _25 (_25_out, decoder_3_out5, decoder_14_out5);
  and _26 (_26_out, decoder_3_out6, decoder_14_out5);
  and _27 (_27_out, decoder_3_out7, decoder_14_out5);
  and _28 (_28_out, decoder_3_out8, decoder_14_out5);
  and _29 (_29_out, decoder_3_out9, decoder_14_out5);
  and _2a (_2a_out, decoder_3_out10, decoder_14_out5);
  and _2b (_2b_out, decoder_3_out11, decoder_14_out5);
  and _3 (_3_out, decoder_5_out3, decoder_14_out5);
  and _4 (_4_out, decoder_5_out4, decoder_14_out5);
  and _5 (_5_out, decoder_5_out5, decoder_14_out5);
  and _6 (_6_out, decoder_5_out6, decoder_14_out5);
  and _7 (_7_out, decoder_5_out7, decoder_14_out5);
  and _8 (_8_out, decoder_5_out8, decoder_14_out5);
  and _9 (_9_out, decoder_5_out9, decoder_14_out5);
  and a (a_out, decoder_5_out10, decoder_14_out5);
  and b (b_out, decoder_5_out11, decoder_14_out5);
  and c (c_out, decoder_5_out12, decoder_14_out5);
  and d (d_out, decoder_5_out13, decoder_14_out5);
  and e (e_out, decoder_5_out14, decoder_14_out5);
  and f0 (f0_out, decoder_4_out0, decoder_14_out5);
  and and_5 (and_5_out, decoder_4_out0, decoder_14_out4);
  and f1 (f1_out, decoder_4_out1, decoder_14_out5);
  and and_6 (and_6_out, decoder_4_out1, decoder_14_out4);
  and fe (fe_out, decoder_4_out14, decoder_14_out5);
  and fffe (fffe_out, decoder_1_out14, decoder_14_out5);
  and ffff (ffff_out, decoder_1_out15, decoder_14_out5);
  Multiplexer #(.width(8), .enable("false")) multiplexer_27 (
    .in0({8{1'b0}}), .in1(Reg_0), .out(multiplexer_27_out), .sel(decoder_8_out0));
  Multiplexer #(.width(8), .enable("false")) multiplexer_28 (
    .in0(multiplexer_27_out), .in1(Reg_1), .out(multiplexer_28_out), .sel(decoder_8_out1));
  Multiplexer #(.width(8), .enable("false")) multiplexer_29 (
    .in0(multiplexer_28_out), .in1(Reg_2), .out(multiplexer_29_out), .sel(decoder_8_out2));
  Multiplexer #(.width(8), .enable("false")) multiplexer_30 (
    .in0(multiplexer_29_out), .in1(Reg_3), .out(multiplexer_30_out), .sel(decoder_8_out3));
  Multiplexer #(.width(8), .enable("false")) multiplexer_31 (
    .in0(multiplexer_30_out), .in1(Reg_4), .out(multiplexer_31_out), .sel(decoder_8_out4));
  Multiplexer #(.width(8), .enable("false")) multiplexer_32 (
    .in0(multiplexer_31_out), .in1(Reg_5), .out(multiplexer_32_out), .sel(decoder_8_out5));
  Multiplexer #(.width(8), .enable("false")) multiplexer_33 (
    .in0(multiplexer_32_out), .in1(Reg_6), .out(multiplexer_33_out), .sel(decoder_8_out6));
  Multiplexer #(.width(8), .enable("false")) multiplexer_34 (
    .in0(multiplexer_33_out), .in1(Reg_7), .out(multiplexer_34_out), .sel(decoder_8_out7));
  Multiplexer #(.width(8), .enable("false")) multiplexer_35 (
    .in0(multiplexer_34_out), .in1(Reg_8), .out(multiplexer_35_out), .sel(decoder_8_out8));
  Multiplexer #(.width(8), .enable("false")) multiplexer_36 (
    .in0(multiplexer_35_out), .in1(Reg_9), .out(multiplexer_36_out), .sel(decoder_8_out9));
  Multiplexer #(.width(8), .enable("false")) multiplexer_37 (
    .in0(multiplexer_36_out), .in1(Reg_A), .out(multiplexer_37_out), .sel(decoder_8_out10));
  Multiplexer #(.width(8), .enable("false")) multiplexer_38 (
    .in0(multiplexer_37_out), .in1(Reg_B), .out(multiplexer_38_out), .sel(decoder_8_out11));
  Multiplexer #(.width(8), .enable("false")) multiplexer_39 (
    .in0(multiplexer_38_out), .in1(Reg_C), .out(multiplexer_39_out), .sel(decoder_8_out12));
  Multiplexer #(.width(8), .enable("false")) multiplexer_40 (
    .in0(multiplexer_39_out), .in1(Reg_D), .out(multiplexer_40_out), .sel(decoder_8_out13));
  Multiplexer #(.width(8), .enable("false")) multiplexer_41 (
    .in0(multiplexer_40_out), .in1(Reg_E), .out(multiplexer_41_out), .sel(decoder_8_out14));
  Multiplexer #(.width(8), .enable("false")) multiplexer_42 (
    .in0(multiplexer_41_out), .in1(Reg_F), .out(multiplexer_42_out), .sel(decoder_8_out15));
  Multiplexer #(.disabled(0), .enable("false")) multiplexer_43 (
    .in0(or_116_out), .in1(1'b0), .out(multiplexer_43_out), .sel(register_22_q));
  or or_7 (or_7_out, _0_out, or_38_out);
  or or_8 (or_8_out, _1_out, or_9_out);
  or or_9 (or_9_out, _20_out, or_10_out);
  or or_10 (or_10_out, _21_out, or_11_out);
  or or_11 (or_11_out, _22_out, or_12_out);
  or or_12 (or_12_out, _23_out, or_13_out);
  or or_13 (or_13_out, _24_out, or_14_out);
  or or_14 (or_14_out, _25_out, or_15_out);
  or or_15 (or_15_out, _26_out, or_16_out);
  or or_16 (or_16_out, _27_out, or_20_out);
  or or_17 (or_17_out, _28_out, or_18_out);
  or or_18 (or_18_out, _29_out, or_19_out);
  or or_19 (or_19_out, _2a_out, or_50_out);
  or or_20 (or_20_out, _2b_out, 1'b0);
  or or_21 (or_21_out, _3_out, or_79_out);
  or or_22 (or_22_out, _4_out, or_23_out);
  or or_23 (or_23_out, _5_out, 1'b0);
  or or_24 (or_24_out, _6_out, or_25_out);
  or or_25 (or_25_out, _7_out, or_27_out);
  or or_26 (or_26_out, _8_out, and_6_out);
  or or_27 (or_27_out, _9_out, or_28_out);
  or or_28 (or_28_out, a_out, or_29_out);
  or or_29 (or_29_out, b_out, or_30_out);
  or or_30 (or_30_out, c_out, or_31_out);
  or or_31 (or_31_out, d_out, e_out);
  or or_32 (or_32_out, f0_out, or_33_out);
  or or_33 (or_33_out, and_5_out, or_34_out);
  or or_34 (or_34_out, f1_out, and_6_out);
  or or_35 (or_35_out, and_6_out, undriven_33);
  or or_36 (or_36_out, fe_out, undriven_34);
  Multiplexer #(.width(8), .enable("false")) multiplexer_44 (
    .in0({8{1'b0}}), .in1(Reg_0), .out(multiplexer_44_out), .sel(decoder_9_out0));
  Multiplexer #(.width(8), .enable("false")) multiplexer_45 (
    .in0(multiplexer_44_out), .in1(Reg_1), .out(multiplexer_45_out), .sel(decoder_9_out1));
  Multiplexer #(.width(8), .enable("false")) multiplexer_46 (
    .in0(multiplexer_45_out), .in1(Reg_2), .out(multiplexer_46_out), .sel(decoder_9_out2));
  Multiplexer #(.width(8), .enable("false")) multiplexer_47 (
    .in0(multiplexer_46_out), .in1(Reg_3), .out(multiplexer_47_out), .sel(decoder_9_out3));
  Multiplexer #(.width(8), .enable("false")) multiplexer_48 (
    .in0(multiplexer_47_out), .in1(Reg_4), .out(multiplexer_48_out), .sel(decoder_9_out4));
  Multiplexer #(.width(8), .enable("false")) multiplexer_49 (
    .in0(multiplexer_48_out), .in1(Reg_5), .out(multiplexer_49_out), .sel(decoder_9_out5));
  Multiplexer #(.width(8), .enable("false")) multiplexer_50 (
    .in0(multiplexer_49_out), .in1(Reg_6), .out(multiplexer_50_out), .sel(or_93_out));
  Multiplexer #(.width(8), .enable("false")) multiplexer_51 (
    .in0(multiplexer_50_out), .in1(Reg_7), .out(multiplexer_51_out), .sel(decoder_9_out7));
  Multiplexer #(.width(8), .enable("false")) multiplexer_52 (
    .in0(multiplexer_51_out), .in1(Reg_8), .out(multiplexer_52_out), .sel(decoder_9_out8));
  Multiplexer #(.width(8), .enable("false")) multiplexer_53 (
    .in0(multiplexer_52_out), .in1(Reg_9), .out(multiplexer_53_out), .sel(decoder_9_out9));
  Multiplexer #(.width(8), .enable("false")) multiplexer_54 (
    .in0(multiplexer_53_out), .in1(Reg_A), .out(multiplexer_54_out), .sel(decoder_9_out10));
  Multiplexer #(.width(8), .enable("false")) multiplexer_55 (
    .in0(multiplexer_54_out), .in1(Reg_B), .out(multiplexer_55_out), .sel(decoder_9_out11));
  Multiplexer #(.width(8), .enable("false")) multiplexer_56 (
    .in0(multiplexer_55_out), .in1(Reg_C), .out(multiplexer_56_out), .sel(decoder_9_out12));
  Multiplexer #(.width(8), .enable("false")) multiplexer_57 (
    .in0(multiplexer_56_out), .in1(Reg_D), .out(multiplexer_57_out), .sel(decoder_9_out13));
  Multiplexer #(.width(8), .enable("false")) multiplexer_58 (
    .in0(multiplexer_57_out), .in1(Reg_E), .out(multiplexer_58_out), .sel(decoder_9_out14));
  Multiplexer #(.width(8), .enable("false")) multiplexer_59 (
    .in0(multiplexer_58_out), .in1(Reg_F), .out(multiplexer_59_out), .sel(decoder_9_out15));
  Register #(.width(12)) u_PC (
    .D(multiplexer_98_out), .en(multiplexer_43_out), .Q(PC), .clk(clock_1_out), .clr(or_124_out));
  Register #(.width(16)) Ins_Acc (
    .D(multiplexer_142_out), .en(decoder_14_out1), .Q(Instruc), .clk(clock_1_out));  // open: clr
  or or_37 (or_37_out, _0_out, or_61_out);
  or or_38 (or_38_out, _1_out, or_42_out);
  or or_39 (or_39_out, _20_out, or_40_out);
  or or_40 (or_40_out, _21_out, or_41_out);
  or or_41 (or_41_out, _22_out, or_65_out);
  or or_42 (or_42_out, _23_out, or_44_out);
  or or_43 (or_43_out, _24_out, or_67_out);
  or or_44 (or_44_out, _25_out, or_45_out);
  or or_45 (or_45_out, _26_out, or_46_out);
  or or_46 (or_46_out, _27_out, or_51_out);
  or or_47 (or_47_out, _28_out, or_48_out);
  or or_48 (or_48_out, _29_out, or_49_out);
  or or_49 (or_49_out, _2a_out, or_68_out);
  or or_50 (or_50_out, _2b_out, and_6_out);
  or or_51 (or_51_out, _3_out, 1'b0);
  or or_52 (or_52_out, _4_out, or_53_out);
  or or_53 (or_53_out, _5_out, 1'b0);
  or or_54 (or_54_out, _6_out, _7_out);
  or or_55 (or_55_out, _9_out, and_6_out);
  or or_56 (or_56_out, a_out, f0_out);
  or or_57 (or_57_out, b_out, or_58_out);
  or or_58 (or_58_out, c_out, or_73_out);
  and and_7 (and_7_out, d_out, nand_5_out);
  and and_8 (and_8_out, e_out, Carry_q[7]);
  or or_59 (or_59_out, and_5_out, f1_out);
  or or_60 (or_60_out, fe_out, undriven_35);
  Multiplexer #(.width(8), .enable("false")) multiplexer_60 (
    .in0({8{1'b0}}), .in1(Reg_0), .out(multiplexer_60_out), .sel(decoder_10_out0));
  Multiplexer #(.width(8), .enable("false")) multiplexer_61 (
    .in0(multiplexer_60_out), .in1(Reg_1), .out(multiplexer_61_out), .sel(decoder_10_out1));
  Multiplexer #(.width(8), .enable("false")) multiplexer_62 (
    .in0(multiplexer_61_out), .in1(Reg_2), .out(multiplexer_62_out), .sel(decoder_10_out2));
  Multiplexer #(.width(8), .enable("false")) multiplexer_63 (
    .in0(multiplexer_62_out), .in1(Reg_3), .out(multiplexer_63_out), .sel(decoder_10_out3));
  Multiplexer #(.width(8), .enable("false")) multiplexer_64 (
    .in0(multiplexer_63_out), .in1(Reg_4), .out(multiplexer_64_out), .sel(decoder_10_out4));
  Multiplexer #(.width(8), .enable("false")) multiplexer_65 (
    .in0(multiplexer_64_out), .in1(Reg_5), .out(multiplexer_65_out), .sel(decoder_10_out5));
  Multiplexer #(.width(8), .enable("false")) multiplexer_66 (
    .in0(multiplexer_65_out), .in1(Reg_6), .out(multiplexer_66_out), .sel(decoder_10_out6));
  Multiplexer #(.width(8), .enable("false")) multiplexer_67 (
    .in0(multiplexer_66_out), .in1(Reg_7), .out(multiplexer_67_out), .sel(or_94_out));
  Multiplexer #(.width(8), .enable("false")) multiplexer_68 (
    .in0(multiplexer_67_out), .in1(Reg_8), .out(multiplexer_68_out), .sel(decoder_10_out8));
  Multiplexer #(.width(8), .enable("false")) multiplexer_69 (
    .in0(multiplexer_68_out), .in1(Reg_9), .out(multiplexer_69_out), .sel(decoder_10_out9));
  Multiplexer #(.width(8), .enable("false")) multiplexer_70 (
    .in0(multiplexer_69_out), .in1(Reg_A), .out(multiplexer_70_out), .sel(decoder_10_out10));
  Multiplexer #(.width(8), .enable("false")) multiplexer_71 (
    .in0(multiplexer_70_out), .in1(Reg_B), .out(multiplexer_71_out), .sel(decoder_10_out11));
  Multiplexer #(.width(8), .enable("false")) multiplexer_72 (
    .in0(multiplexer_71_out), .in1(Reg_C), .out(multiplexer_72_out), .sel(decoder_10_out12));
  Multiplexer #(.width(8), .enable("false")) multiplexer_73 (
    .in0(multiplexer_72_out), .in1(Reg_D), .out(multiplexer_73_out), .sel(decoder_10_out13));
  Multiplexer #(.width(8), .enable("false")) multiplexer_74 (
    .in0(multiplexer_73_out), .in1(Reg_E), .out(multiplexer_74_out), .sel(decoder_10_out14));
  Multiplexer #(.width(8), .enable("false")) multiplexer_75 (
    .in0(multiplexer_74_out), .in1(Reg_F), .out(multiplexer_75_out), .sel(decoder_10_out15));
  Multiplexer #(.width(12), .enable("false")) multiplexer_76 (
    .in0({12{1'b0}}), .in1(PC), .out(multiplexer_76_out), .sel(decoder_14_out1));
  Multiplexer #(.width(16), .enable("false")) multiplexer_77 (
    .in0({16{1'b0}}), .in1(Instruc), .out({multiplexer_77_out_3, multiplexer_77_out_2, multiplexer_77_out}),
    .sel(or_122_out));
  or or_61 (or_61_out, _1_out, or_62_out);
  or or_62 (or_62_out, _20_out, or_63_out);
  or or_63 (or_63_out, _21_out, or_64_out);
  or or_64 (or_64_out, _22_out, or_77_out);
  or or_65 (or_65_out, _23_out, or_43_out);
  or or_66 (or_66_out, _24_out, or_78_out);
  or or_67 (or_67_out, _25_out, or_17_out);
  or or_68 (or_68_out, _2b_out, or_21_out);
  or or_69 (or_69_out, _4_out, or_71_out);
  or or_70 (or_70_out, _5_out, f0_out);
  or or_71 (or_71_out, _6_out, or_55_out);
  or or_72 (or_72_out, _7_out, a_out);
  or or_73 (or_73_out, and_7_out, or_74_out);
  or or_74 (or_74_out, and_8_out, fffe_out);
  or or_75 (or_75_out, and_5_out, f1_out);
  or or_76 (or_76_out, fe_out, undriven_36);
  Multiplexer #(.width(12), .enable("false")) multiplexer_78 (
    .in0({12{1'b0}}), .in1(PC), .out({multiplexer_78_out_2, multiplexer_78_out}), .sel(or_107_out));
  Multiplexer #(.width(16), .enable("false")) multiplexer_79 (
    .in0({16{1'b0}}), .in1(Instruc), .out(multiplexer_79_out), .sel(or_24_out));
  Multiplexer #(.width(8), .enable("false")) multiplexer_80 (
    .in0(Adr_In[7:0]), .in1(Reg_0), .out(multiplexer_80_out), .sel(decoder_11_out0));
  Multiplexer #(.width(8), .enable("false")) multiplexer_81 (
    .in0({4'b0000, Adr_In[11:8]}), .in1(Reg_1), .out(multiplexer_81_out), .sel(decoder_11_out0));
  Multiplexer #(.width(8), .enable("false")) multiplexer_82 (
    .in0(multiplexer_80_out), .in1(Reg_2), .out(multiplexer_82_out), .sel(decoder_11_out2));
  Multiplexer #(.width(8), .enable("false")) multiplexer_83 (
    .in0(multiplexer_81_out), .in1(Reg_3), .out(multiplexer_83_out), .sel(decoder_11_out2));
  Multiplexer #(.width(8), .enable("false")) multiplexer_84 (
    .in0(multiplexer_82_out), .in1(Reg_4), .out(multiplexer_84_out), .sel(decoder_11_out4));
  Multiplexer #(.width(8), .enable("false")) multiplexer_85 (
    .in0(multiplexer_83_out), .in1(Reg_5), .out(multiplexer_85_out), .sel(decoder_11_out4));
  Multiplexer #(.width(8), .enable("false")) multiplexer_86 (
    .in0(multiplexer_84_out), .in1(Reg_6), .out(multiplexer_86_out), .sel(decoder_11_out6));
  Multiplexer #(.width(8), .enable("false")) multiplexer_87 (
    .in0(multiplexer_85_out), .in1(Reg_7), .out(multiplexer_87_out), .sel(decoder_11_out6));
  Multiplexer #(.width(8), .enable("false")) multiplexer_88 (
    .in0(multiplexer_86_out), .in1(Reg_8), .out(multiplexer_88_out), .sel(decoder_11_out8));
  Multiplexer #(.width(8), .enable("false")) multiplexer_89 (
    .in0(multiplexer_87_out), .in1(Reg_9), .out(multiplexer_89_out), .sel(decoder_11_out8));
  Multiplexer #(.width(8), .enable("false")) multiplexer_90 (
    .in0(multiplexer_88_out), .in1(Reg_A), .out(multiplexer_90_out), .sel(or_95_out));
  Multiplexer #(.width(8), .enable("false")) multiplexer_91 (
    .in0(multiplexer_89_out), .in1(Reg_B), .out(multiplexer_91_out), .sel(or_95_out));
  Multiplexer #(.width(8), .enable("false")) multiplexer_92 (
    .in0(multiplexer_90_out), .in1(Reg_C), .out(multiplexer_92_out), .sel(or_96_out));
  Multiplexer #(.width(8), .enable("false")) multiplexer_93 (
    .in0(multiplexer_91_out), .in1(Reg_D), .out(multiplexer_93_out), .sel(or_96_out));
  Multiplexer #(.width(8), .enable("false")) multiplexer_94 (
    .in0(multiplexer_92_out), .in1(Reg_E), .out(multiplexer_94_out), .sel(decoder_11_out14));
  Multiplexer #(.width(8), .enable("false")) multiplexer_95 (
    .in0(multiplexer_93_out), .in1(Reg_F), .out(multiplexer_95_out), .sel(decoder_11_out14));
  or or_77 (or_77_out, _23_out, or_66_out);
  or or_78 (or_78_out, _25_out, or_47_out);
  or or_79 (or_79_out, _4_out, or_26_out);
  or or_80 (or_80_out, _5_out, or_82_out);
  or or_81 (or_81_out, _6_out, _9_out);
  or or_82 (or_82_out, _7_out, or_56_out);
  Multiplexer #(.width(12), .enable("false")) multiplexer_96 (
    .in0({12{1'b0}}), .in1(PC), .out(multiplexer_96_out), .sel(decoder_14_out1));
  Multiplexer #(.width(16), .enable("false")) multiplexer_97 (
    .in0({16{1'b0}}), .in1(Instruc), .out(multiplexer_97_out), .sel(_8_out));
  Multiplexer #(.width(12), .enable("false")) multiplexer_98 (
    .in0(or_104_out), .in1(adder_1_out), .out(multiplexer_98_out), .sel(decoder_14_out1));
  Adder #(.width(12)) adder_1 (.a(12'h2), .b(multiplexer_96_out), .out(adder_1_out));  // open: cin, cout
  or or_83 (or_83_out, decoder_6_out15, 1'b0);
  Multiplexer #(.width(16), .enable("false")) multiplexer_99 (
    .in0({16{1'b0}}), .in1(Instruc), .out(multiplexer_99_out), .sel(_3_out));
  or or_84 (or_84_out, decoder_6_out13, c_out);
  or or_85 (or_85_out, decoder_6_out14, 1'b0);
  or or_86 (or_86_out, decoder_6_out12, c_out);
  or or_87 (or_87_out, decoder_6_out11, or_75_out);
  or or_88 (or_88_out, decoder_6_out10, or_75_out);
  or or_89 (or_89_out, decoder_6_out9, 1'b0);
  Button button_1 (.out(button_1_out));
  or or_90 (or_90_out, decoder_6_out6, or_81_out);
  or or_91 (or_91_out, decoder_6_out8, 1'b0);
  LED led_5 (.in(register_1_q[1]));
  LED led_6 (.in(register_1_q[6]));
  LED led_7 (.in(register_1_q[6]));
  LED led_8 (.in(register_1_q[6]));
  LED led_9 (.in(register_1_q[7]));
  LED led_10 (.in(register_1_q[5]));
  LED led_11 (.in(register_1_q[5]));
  LED led_12 (.in(register_1_q[5]));
  LED led_13 (.in(register_1_q[4]));
  LED led_14 (.in(d_ff_6_q));
  LED led_15 (.in(register_1_q[1]));
  LED led_16 (.in(register_1_q[1]));
  LED led_17 (.in(register_1_q[2]));
  LED led_18 (.in(register_1_q[2]));
  LED led_19 (.in(register_1_q[7]));
  LED led_20 (.in(register_1_q[7]));
  LED led_21 (.in(register_1_q[2]));
  LED led_22 (.in(register_1_q[3]));
  LED led_23 (.in(register_1_q[3]));
  LED led_24 (.in(register_1_q[3]));
  LED led_25 (.in(register_1_q[4]));
  LED led_26 (.in(register_1_q[4]));
  Register register_1 (.D(register_3_q), .en(and_17_out[0]), .Q(register_1_q), .clk(d_ff_3_q));  // open: clr
  or or_92 (or_92_out, decoder_7_out6, d_out);
  LED led_27 (.in(register_2_q[1]));
  LED led_28 (.in(register_2_q[1]));
  LED led_29 (.in(register_2_q[1]));
  LED led_30 (.in(register_2_q[6]));
  LED led_31 (.in(register_2_q[6]));
  LED led_32 (.in(register_2_q[7]));
  LED led_33 (.in(register_2_q[6]));
  LED led_34 (.in(register_2_q[7]));
  LED led_35 (.in(register_2_q[7]));
  LED led_36 (.in(register_2_q[5]));
  LED led_37 (.in(register_2_q[5]));
  LED led_38 (.in(register_2_q[5]));
  LED led_39 (.in(register_2_q[4]));
  LED led_40 (.in(register_2_q[4]));
  LED led_41 (.in(register_2_q[4]));
  Register register_2 (.D(register_4_q), .en(and_17_out[0]), .Q(register_2_q), .clk(d_ff_3_q));  // open: clr
  LED led_42 (.in(register_2_q[2]));
  LED led_43 (.in(register_2_q[2]));
  LED led_44 (.in(register_2_q[2]));
  LED led_45 (.in(register_2_q[3]));
  LED led_46 (.in(register_2_q[3]));
  LED led_47 (.in(register_2_q[3]));
  LED led_48 (.in(register_3_q[1]));
  LED led_49 (.in(register_3_q[1]));
  LED led_50 (.in(register_3_q[1]));
  LED led_51 (.in(register_3_q[6]));
  LED led_52 (.in(register_3_q[2]));
  LED led_53 (.in(register_3_q[6]));
  LED led_54 (.in(register_3_q[2]));
  LED led_55 (.in(register_3_q[7]));
  LED led_56 (.in(register_3_q[2]));
  LED led_57 (.in(register_3_q[7]));
  LED led_58 (.in(register_3_q[7]));
  LED led_59 (.in(register_3_q[6]));
  LED led_60 (.in(register_3_q[5]));
  LED led_61 (.in(register_3_q[3]));
  LED led_62 (.in(register_3_q[3]));
  LED led_63 (.in(register_3_q[5]));
  LED led_64 (.in(register_3_q[3]));
  LED led_65 (.in(register_3_q[5]));
  LED led_66 (.in(register_3_q[4]));
  LED led_67 (.in(register_3_q[4]));
  LED led_68 (.in(register_3_q[4]));
  LED led_69 (.in(register_4_q[1]));
  LED led_70 (.in(register_4_q[1]));
  LED led_71 (.in(register_4_q[6]));
  LED led_72 (.in(register_4_q[6]));
  LED led_73 (.in(register_4_q[7]));
  LED led_74 (.in(register_4_q[7]));
  LED led_75 (.in(register_4_q[6]));
  LED led_76 (.in(register_4_q[5]));
  LED led_77 (.in(register_4_q[5]));
  LED led_78 (.in(register_4_q[5]));
  LED led_79 (.in(register_4_q[4]));
  LED led_80 (.in(register_4_q[4]));
  Register register_3 (.D(register_5_q), .en(and_17_out[0]), .Q(register_3_q), .clk(d_ff_3_q));  // open: clr
  Register register_4 (.D(register_6_q), .en(and_17_out[0]), .Q(register_4_q), .clk(d_ff_3_q));  // open: clr
  LED led_81 (.in(register_4_q[1]));
  LED led_82 (.in(register_4_q[2]));
  LED led_83 (.in(register_4_q[2]));
  LED led_84 (.in(register_4_q[2]));
  LED led_85 (.in(register_4_q[7]));
  LED led_86 (.in(register_4_q[3]));
  LED led_87 (.in(register_4_q[3]));
  LED led_88 (.in(register_4_q[3]));
  LED led_89 (.in(register_4_q[4]));
  or or_93 (or_93_out, decoder_9_out6, or_72_out);
  LED led_90 (.in(register_5_q[1]));
  LED led_91 (.in(register_5_q[1]));
  LED led_92 (.in(register_5_q[1]));
  LED led_93 (.in(register_5_q[6]));
  LED led_94 (.in(register_5_q[6]));
  LED led_95 (.in(register_5_q[7]));
  LED led_96 (.in(register_5_q[7]));
  LED led_97 (.in(register_5_q[6]));
  LED led_98 (.in(register_5_q[7]));
  LED led_99 (.in(register_5_q[5]));
  LED led_100 (.in(register_5_q[5]));
  LED led_101 (.in(register_5_q[5]));
  LED led_102 (.in(register_5_q[4]));
  LED led_103 (.in(register_5_q[4]));
  LED led_104 (.in(register_5_q[4]));
  LED led_105 (.in(register_6_q[1]));
  LED led_106 (.in(register_6_q[6]));
  LED led_107 (.in(register_5_q[2]));
  LED led_108 (.in(register_6_q[6]));
  LED led_109 (.in(register_5_q[2]));
  LED led_110 (.in(register_6_q[7]));
  LED led_111 (.in(register_6_q[6]));
  LED led_112 (.in(register_5_q[2]));
  LED led_113 (.in(register_6_q[5]));
  LED led_114 (.in(register_5_q[3]));
  LED led_115 (.in(register_5_q[3]));
  LED led_116 (.in(register_6_q[5]));
  LED led_117 (.in(register_6_q[5]));
  LED led_118 (.in(register_5_q[3]));
  LED led_119 (.in(register_6_q[4]));
  Register register_5 (.D(register_7_q), .en(and_17_out[0]), .Q(register_5_q), .clk(d_ff_3_q));  // open: clr
  or or_94 (or_94_out, decoder_10_out7, or_54_out);
  LED led_120 (.in(register_6_q[1]));
  LED led_121 (.in(register_6_q[1]));
  LED led_122 (.in(register_6_q[2]));
  LED led_123 (.in(register_6_q[2]));
  LED led_124 (.in(register_6_q[7]));
  LED led_125 (.in(register_6_q[2]));
  LED led_126 (.in(register_6_q[7]));
  LED led_127 (.in(register_6_q[3]));
  LED led_128 (.in(register_6_q[3]));
  LED led_129 (.in(register_6_q[3]));
  LED led_130 (.in(register_6_q[4]));
  LED led_131 (.in(register_6_q[4]));
  Register register_6 (.D(register_8_q), .en(and_17_out[0]), .Q(register_6_q), .clk(d_ff_3_q));  // open: clr
  or or_95 (or_95_out, decoder_11_out10, or_32_out);
  LED led_132 (.in(register_7_q[1]));
  LED led_133 (.in(register_7_q[1]));
  LED led_134 (.in(register_7_q[6]));
  LED led_135 (.in(register_7_q[6]));
  LED led_136 (.in(register_7_q[7]));
  LED led_137 (.in(register_7_q[7]));
  LED led_138 (.in(register_7_q[6]));
  LED led_139 (.in(register_7_q[5]));
  LED led_140 (.in(register_7_q[5]));
  LED led_141 (.in(register_7_q[5]));
  LED led_142 (.in(register_7_q[4]));
  LED led_143 (.in(register_7_q[4]));
  or or_96 (or_96_out, decoder_11_out12, fffe_out);
  LED led_144 (.in(register_7_q[1]));
  LED led_145 (.in(register_7_q[2]));
  LED led_146 (.in(register_7_q[2]));
  LED led_147 (.in(register_7_q[2]));
  LED led_148 (.in(register_7_q[7]));
  LED led_149 (.in(register_7_q[3]));
  LED led_150 (.in(register_7_q[3]));
  LED led_151 (.in(register_7_q[3]));
  LED led_152 (.in(register_7_q[4]));
  Register register_7 (.D(register_9_q), .en(and_17_out[0]), .Q(register_7_q), .clk(d_ff_3_q));  // open: clr
  or or_97 (or_97_out, multiplexer_20_out[7], multiplexer_20_out[6], multiplexer_20_out[5], multiplexer_20_out[4], multiplexer_20_out[3], multiplexer_20_out[2], multiplexer_20_out[1], multiplexer_20_out[0]);
  Multiplexer #(.width(8), .enable("false")) multiplexer_100 (
    .in0(multiplexer_42_out), .in1(multiplexer_99_out[7:0]), .out(multiplexer_100_out), .sel(_3_out));
  LED led_153 (.in(register_8_q[1]));
  LED led_154 (.in(register_8_q[1]));
  LED led_155 (.in(register_8_q[1]));
  LED led_156 (.in(register_8_q[6]));
  LED led_157 (.in(register_8_q[2]));
  LED led_158 (.in(register_8_q[6]));
  LED led_159 (.in(register_8_q[2]));
  LED led_160 (.in(register_8_q[6]));
  LED led_161 (.in(register_8_q[7]));
  LED led_162 (.in(register_8_q[2]));
  LED led_163 (.in(register_8_q[7]));
  LED led_164 (.in(register_8_q[7]));
  LED led_165 (.in(register_8_q[5]));
  LED led_166 (.in(register_8_q[3]));
  LED led_167 (.in(register_8_q[3]));
  LED led_168 (.in(register_8_q[5]));
  LED led_169 (.in(register_8_q[5]));
  LED led_170 (.in(register_8_q[3]));
  LED led_171 (.in(register_8_q[4]));
  LED led_172 (.in(register_8_q[4]));
  LED led_173 (.in(register_8_q[4]));
  Register register_8 (.D(register_10_q), .en(and_17_out[0]), .Q(register_8_q), .clk(d_ff_3_q));  // open: clr
  Adder adder_2 (
    .a(multiplexer_20_out), .b(multiplexer_100_out), .out(adder_2_out), .cin(_20_out), .cout(adder_2_cout));
  assign not_1_out = ~multiplexer_100_out;  // NOT_Gate not_1, 8 bits wide
  assign xor_1_out = multiplexer_20_out ^ multiplexer_100_out;  // XOR_Gate xor_1, 8 bits wide
  Adder adder_3 (.a(multiplexer_20_out), .b(not_1_out), .out(adder_3_out), .cin(_25_out));  // open: cout
  Multiplier multiplier_1 (
    .a(multiplexer_20_out), .b(multiplexer_100_out), .out(multiplier_1_out), .cout(multiplier_1_cout));  // open: cin
  Divider divider_1 (
    .a(multiplexer_20_out), .b(multiplexer_100_out), .out(divider_1_out), .rem(divider_1_rem));  // open: upper
  LED led_174 (.in(register_9_q[1]));
  LED led_175 (.in(register_9_q[6]));
  LED led_176 (.in(register_9_q[6]));
  LED led_177 (.in(register_9_q[6]));
  LED led_178 (.in(register_9_q[7]));
  LED led_179 (.in(register_9_q[5]));
  LED led_180 (.in(register_9_q[5]));
  LED led_181 (.in(register_9_q[5]));
  LED led_182 (.in(register_9_q[4]));
  nand nand_5 (nand_5_out, or_97_out, or_97_out);
  Multiplexer #(.enable("false")) multiplexer_101 (
    .in0(adder_2_cout), .in1(multiplexer_100_out[7]), .out(multiplexer_101_out), .sel(_22_out));
  or or_98 (or_98_out, multiplexer_101_out, multiplexer_102_out);
  LED led_183 (.in(register_9_q[1]));
  LED led_184 (.in(register_9_q[1]));
  LED led_185 (.in(register_9_q[2]));
  LED led_186 (.in(register_9_q[2]));
  LED led_187 (.in(register_9_q[7]));
  LED led_188 (.in(register_9_q[2]));
  LED led_189 (.in(register_9_q[7]));
  LED led_190 (.in(register_9_q[3]));
  LED led_191 (.in(register_9_q[3]));
  LED led_192 (.in(register_9_q[3]));
  LED led_193 (.in(register_9_q[4]));
  LED led_194 (.in(register_9_q[4]));
  Register register_9 (.D(register_12_q), .en(and_17_out[0]), .Q(register_9_q), .clk(d_ff_3_q));  // open: clr
  Multiplexer #(.enable("false")) multiplexer_102 (
    .in0(1'b0), .in1(multiplexer_100_out[0]), .out(multiplexer_102_out), .sel(_24_out));
  Multiplexer #(.width(8), .enable("false")) multiplexer_103 (
    .in0(multiplier_1_cout), .in1(divider_1_rem), .out(multiplexer_103_out), .sel(_27_out));
  Multiplexer #(.width(8), .enable("false")) multiplexer_104 (
    .in0(multiplier_1_out), .in1(divider_1_out), .out(multiplexer_104_out), .sel(_27_out));
  LED led_195 (.in(register_10_q[1]));
  LED led_196 (.in(register_10_q[1]));
  LED led_197 (.in(register_10_q[1]));
  LED led_198 (.in(register_10_q[6]));
  LED led_199 (.in(register_10_q[6]));
  LED led_200 (.in(register_10_q[7]));
  LED led_201 (.in(register_10_q[6]));
  LED led_202 (.in(register_10_q[7]));
  LED led_203 (.in(register_10_q[7]));
  LED led_204 (.in(register_10_q[5]));
  LED led_205 (.in(register_10_q[5]));
  LED led_206 (.in(register_10_q[5]));
  LED led_207 (.in(register_10_q[4]));
  LED led_208 (.in(register_10_q[4]));
  LED led_209 (.in(register_10_q[4]));
  Register register_10 (.D(register_11_q), .en(and_17_out[0]), .Q(register_10_q), .clk(d_ff_3_q));  // open: clr
  LED led_210 (.in(register_10_q[2]));
  LED led_211 (.in(register_10_q[2]));
  LED led_212 (.in(register_10_q[2]));
  LED led_213 (.in(register_10_q[3]));
  LED led_214 (.in(register_10_q[3]));
  LED led_215 (.in(register_10_q[3]));
  LED led_216 (.in(register_12_q[1]));
  LED led_217 (.in(register_12_q[1]));
  LED led_218 (.in(register_12_q[1]));
  LED led_219 (.in(register_12_q[6]));
  LED led_220 (.in(register_12_q[2]));
  LED led_221 (.in(register_12_q[6]));
  LED led_222 (.in(register_12_q[2]));
  LED led_223 (.in(register_12_q[2]));
  LED led_224 (.in(register_12_q[6]));
  LED led_225 (.in(register_12_q[7]));
  LED led_226 (.in(register_12_q[7]));
  LED led_227 (.in(register_12_q[7]));
  LED led_228 (.in(register_12_q[5]));
  LED led_229 (.in(register_12_q[3]));
  LED led_230 (.in(register_12_q[3]));
  LED led_231 (.in(register_12_q[5]));
  LED led_232 (.in(register_12_q[5]));
  LED led_233 (.in(register_12_q[3]));
  LED led_234 (.in(register_12_q[4]));
  LED led_235 (.in(register_12_q[4]));
  LED led_236 (.in(register_12_q[4]));
  or or_99 (or_99_out, _1_out, _3_out, _20_out);
  or or_100 (or_100_out, _20_out, _24_out, _3_out, _22_out, _1_out);
  or or_101 (or_101_out, _26_out, _27_out);
  LED led_237 (.in(register_11_q[1]));
  LED led_238 (.in(register_11_q[1]));
  LED led_239 (.in(register_11_q[6]));
  LED led_240 (.in(register_11_q[6]));
  LED led_241 (.in(register_11_q[6]));
  LED led_242 (.in(register_11_q[7]));
  LED led_243 (.in(register_11_q[7]));
  LED led_244 (.in(register_11_q[5]));
  LED led_245 (.in(register_11_q[5]));
  LED led_246 (.in(register_11_q[5]));
  LED led_247 (.in(register_11_q[4]));
  LED led_248 (.in(register_11_q[4]));
  Register register_11 (.D(register_14_q), .en(and_17_out[0]), .Q(register_11_q), .clk(d_ff_3_q));  // open: clr
  Register register_12 (.D(register_13_q), .en(and_17_out[0]), .Q(register_12_q), .clk(d_ff_3_q));  // open: clr
  Multiplexer #(.width(8), .enable("false")) multiplexer_105 (
    .in0({8{1'b0}}), .in1({multiplexer_100_out[6:0], 1'b0}), .out(multiplexer_105_out), .sel(_22_out));
  Multiplexer #(.width(8), .enable("false")) multiplexer_106 (
    .in0(multiplexer_105_out), .in1({1'b0, multiplexer_100_out[7:1]}), .out(multiplexer_106_out),
    .sel(_24_out));
  Multiplexer #(.width(8), .enable("false")) multiplexer_107 (
    .in0(multiplexer_106_out), .in1(multiplexer_20_out), .out(multiplexer_107_out), .sel(_0_out));
  Multiplexer #(.width(8), .enable("false")) multiplexer_108 (
    .in0(multiplexer_107_out), .in1(adder_2_out), .out(multiplexer_108_out), .sel(or_99_out));
  Multiplexer #(.width(8), .enable("false")) multiplexer_109 (
    .in0(multiplexer_108_out), .in1(not_1_out), .out(multiplexer_109_out), .sel(_21_out));
  Multiplexer #(.width(8), .enable("false")) multiplexer_110 (
    .in0(multiplexer_109_out), .in1(xor_1_out), .out(multiplexer_110_out), .sel(_23_out));
  Multiplexer #(.width(8), .enable("false")) multiplexer_111 (
    .in0(multiplexer_110_out), .in1(adder_3_out), .out(multiplexer_111_out), .sel(_25_out));
  Multiplexer #(.width(8), .enable("false")) multiplexer_112 (
    .in0(multiplexer_111_out), .in1({8{Carry_q[7]}}), .out(multiplexer_112_out), .sel(_2a_out));
  Multiplexer #(.width(8), .enable("false")) multiplexer_113 (
    .in0(multiplexer_112_out), .in1({8{multiplexer_100_out[7]}}), .out(multiplexer_113_out), .sel(_2b_out));
  D_Flip_Flop #(.trigger("falling")) Carry (
    .clk(decoder_14_out5), .D(or_98_out), .Q(Carry_q[7]), .en(or_100_out));  // open: Qn, preset, reset
  Multiplexer #(.width(8), .enable("false")) multiplexer_114 (
    .in0(multiplexer_113_out), .in1(Hi_q), .out(multiplexer_114_out), .sel(_28_out));
  Register Hi (.D(multiplexer_103_out), .en(or_101_out), .Q(Hi_q), .clk(clock_1_out));  // open: clr
  Multiplexer #(.width(8), .enable("false")) multiplexer_115 (
    .in0(multiplexer_114_out), .in1(Lo_q), .out(multiplexer_115_out), .sel(_29_out));
  Register Lo (.D(multiplexer_104_out), .en(or_101_out), .Q(Lo_q), .clk(clock_1_out));  // open: clr
  LED led_249 (.in(register_11_q[1]));
  LED led_250 (.in(register_11_q[2]));
  LED led_251 (.in(register_11_q[2]));
  LED led_252 (.in(register_11_q[7]));
  LED led_253 (.in(register_11_q[2]));
  LED led_254 (.in(register_11_q[3]));
  LED led_255 (.in(register_11_q[3]));
  LED led_256 (.in(register_11_q[3]));
  LED led_257 (.in(register_11_q[4]));
  LED led_258 (.in(register_13_q[1]));
  LED led_259 (.in(register_13_q[1]));
  LED led_260 (.in(register_13_q[1]));
  LED led_261 (.in(register_13_q[6]));
  LED led_262 (.in(register_13_q[6]));
  LED led_263 (.in(register_13_q[6]));
  LED led_264 (.in(register_13_q[7]));
  LED led_265 (.in(register_13_q[7]));
  LED led_266 (.in(register_13_q[7]));
  LED led_267 (.in(register_13_q[5]));
  LED led_268 (.in(register_13_q[5]));
  LED led_269 (.in(register_13_q[5]));
  LED led_270 (.in(register_13_q[4]));
  LED led_271 (.in(register_13_q[4]));
  LED led_272 (.in(register_13_q[4]));
  LED led_273 (.in(register_14_q[1]));
  LED led_274 (.in(register_13_q[2]));
  LED led_275 (.in(register_14_q[6]));
  LED led_276 (.in(register_14_q[6]));
  LED led_277 (.in(register_13_q[2]));
  LED led_278 (.in(register_14_q[6]));
  LED led_279 (.in(register_13_q[2]));
  LED led_280 (.in(register_14_q[7]));
  LED led_281 (.in(register_13_q[3]));
  LED led_282 (.in(register_14_q[5]));
  LED led_283 (.in(register_14_q[5]));
  LED led_284 (.in(register_13_q[3]));
  LED led_285 (.in(register_14_q[5]));
  LED led_286 (.in(register_13_q[3]));
  LED led_287 (.in(register_14_q[4]));
  Register register_13 (.D(register_15_q), .en(and_17_out[0]), .Q(register_13_q), .clk(d_ff_3_q));  // open: clr
  LED led_288 (.in(register_14_q[1]));
  LED led_289 (.in(register_14_q[1]));
  LED led_290 (.in(register_14_q[2]));
  LED led_291 (.in(register_14_q[2]));
  LED led_292 (.in(register_14_q[2]));
  LED led_293 (.in(register_14_q[7]));
  LED led_294 (.in(register_14_q[7]));
  LED led_295 (.in(register_14_q[3]));
  LED led_296 (.in(register_14_q[3]));
  LED led_297 (.in(register_14_q[3]));
  LED led_298 (.in(register_14_q[4]));
  LED led_299 (.in(register_14_q[4]));
  Register register_14 (.D(register_16_q), .en(and_17_out[0]), .Q(register_14_q), .clk(d_ff_3_q));  // open: clr
  LED led_300 (.in(register_15_q[1]));
  LED led_301 (.in(register_15_q[1]));
  LED led_302 (.in(register_15_q[6]));
  LED led_303 (.in(register_15_q[6]));
  LED led_304 (.in(register_15_q[7]));
  LED led_305 (.in(register_15_q[6]));
  LED led_306 (.in(register_15_q[7]));
  LED led_307 (.in(register_15_q[5]));
  LED led_308 (.in(register_15_q[5]));
  LED led_309 (.in(register_15_q[5]));
  LED led_310 (.in(register_15_q[4]));
  LED led_311 (.in(register_15_q[4]));
  LED led_312 (.in(register_15_q[1]));
  LED led_313 (.in(register_15_q[2]));
  LED led_314 (.in(register_15_q[2]));
  LED led_315 (.in(register_15_q[2]));
  LED led_316 (.in(register_15_q[7]));
  LED led_317 (.in(register_15_q[3]));
  LED led_318 (.in(register_15_q[3]));
  LED led_319 (.in(register_15_q[3]));
  LED led_320 (.in(register_15_q[4]));
  Register register_15 (
    .D({or_131_out, and_17_out[0]}), .en(and_17_out[0]), .Q(register_15_q), .clk(d_ff_3_q));  // open: clr
  LED led_321 (.in(register_16_q[1]));
  LED led_322 (.in(register_16_q[1]));
  LED led_323 (.in(register_16_q[1]));
  LED led_324 (.in(register_16_q[6]));
  LED led_325 (.in(register_16_q[2]));
  LED led_326 (.in(register_16_q[6]));
  LED led_327 (.in(register_16_q[2]));
  LED led_328 (.in(register_16_q[7]));
  LED led_329 (.in(register_16_q[7]));
  LED led_330 (.in(register_16_q[6]));
  LED led_331 (.in(register_16_q[7]));
  LED led_332 (.in(register_16_q[2]));
  LED led_333 (.in(register_16_q[5]));
  LED led_334 (.in(register_16_q[3]));
  LED led_335 (.in(register_16_q[3]));
  LED led_336 (.in(register_16_q[5]));
  LED led_337 (.in(register_16_q[5]));
  LED led_338 (.in(register_16_q[3]));
  LED led_339 (.in(register_16_q[4]));
  LED led_340 (.in(register_16_q[4]));
  LED led_341 (.in(register_16_q[4]));
  Register register_16 (.D(and_17_out), .en(and_17_out[0]), .Q(register_16_q), .clk(d_ff_3_q));  // open: clr
  assign or_102_out = {multiplexer_95_out[3:0], multiplexer_94_out} | multiplexer_76_out;  // OR_Gate or_102, 12 bits wide
  assign or_103_out = or_102_out | multiplexer_79_out[11:0];  // OR_Gate or_103, 12 bits wide
  Multiplexer #(.width(8), .enable("false")) multiplexer_116 (
    .in0({8{1'b0}}), .in1(8'h3), .out(multiplexer_116_out), .sel(button_1_out));
  D_Flip_Flop d_ff_3 (
    .clk(clock_1_out), .D(or_5_out), .Q(d_ff_3_q), .en(or_5_out), .reset(or_6_out));  // open: Qn, preset
  assign or_104_out = multiplexer_121_out | or_103_out;  // OR_Gate or_104, 12 bits wide
  Multiplexer #(.width(12), .enable("false")) multiplexer_117 (
    .in0({12{1'b0}}), .in1(12'hf02), .out(multiplexer_117_out), .sel(or_108_out));
  Multiplexer #(.width(12), .enable("false")) multiplexer_118 (
    .in0(multiplexer_117_out), .in1(12'hf03), .out(multiplexer_118_out), .sel(or_111_out));
  Multiplexer #(.width(12), .enable("false")) multiplexer_119 (
    .in0(multiplexer_118_out), .in1(12'hf00), .out(multiplexer_119_out), .sel(or_112_out));
  Multiplexer #(.width(12), .enable("false")) multiplexer_120 (
    .in0(multiplexer_119_out), .in1(12'hf01), .out(multiplexer_120_out), .sel(or_109_out));
  Multiplexer #(.width(12), .enable("false")) multiplexer_121 (
    .in0(multiplexer_120_out), .in1(12'hf04), .out(multiplexer_121_out), .sel(or_113_out));
  Multiplexer #(.width(8), .enable("false")) multiplexer_122 (
    .in0(multiplexer_116_out), .in1(8'h8), .out(multiplexer_122_out), .sel(register_22_q));
  or or_105 (or_105_out, register_22_q, button_1_out);
  assign or_106_out = register_21_q | {in_1, in_2, in_3, Keyboard_IN, in_5, in_6, in_7, in_8};  // OR_Gate or_106, 8 bits wide
  Adder #(.width(12)) adder_4 (
    .a(12'hffe), .b({multiplexer_78_out_2, multiplexer_78_out}), .out(adder_4_out));  // open: cin, cout
  Register #(.trigger("high")) Exc_Code (
    .D(multiplexer_122_out), .en(or_105_out), .Q(Exc_Code_q), .clk(or_105_out), .clr(decoder_13_out15));
  Register Exc_Data (.D(or_106_out), .en(or_105_out), .Q(Exc_Data_q), .clk(or_105_out), .clr(decoder_13_out15));
  Multiplexer #(.width(12), .enable("false")) multiplexer_123 (
    .in0({multiplexer_78_out_2, multiplexer_78_out}), .in1(adder_4_out),
    .out({multiplexer_123_out, multiplexer_123_out_2}), .sel(and_9_out));
  Multiplexer #(.width(8), .enable("false")) multiplexer_124 (
    .in0({8{1'b0}}), .in1({4'b1011, multiplexer_123_out}), .out(multiplexer_124_out), .sel(or_108_out));
  Multiplexer #(.width(8), .enable("false")) multiplexer_125 (
    .in0(multiplexer_124_out), .in1(multiplexer_123_out_2), .out(multiplexer_125_out), .sel(or_111_out));
  Multiplexer #(.width(8), .enable("false")) multiplexer_126 (
    .in0(multiplexer_125_out), .in1(Exc_Code_q), .out(multiplexer_126_out), .sel(or_112_out));
  Multiplexer #(.width(8), .enable("false")) multiplexer_127 (
    .in0(multiplexer_126_out), .in1(Exc_Data_q), .out(multiplexer_127_out), .sel(or_109_out));
  and and_9 (and_9_out, ~Exc_Code_q[7], ~Exc_Code_q[6], ~Exc_Code_q[5], ~Exc_Code_q[4], Exc_Code_q[3], ~Exc_Code_q[2], ~Exc_Code_q[1], ~Exc_Code_q[0]);  // AND_Gate
  or or_107 (or_107_out, or_114_out, c_out);
  or or_108 (or_108_out, decoder_13_out3, decoder_13_out2);
  or or_109 (or_109_out, decoder_13_out12, decoder_13_out11);
  or or_110 (or_110_out, undriven_37, undriven_38);
  and and_10 (and_10_out, or_156_out, decoder_14_out5);
  and and_11 (and_11_out, ~or_156_out, decoder_12_out14);  // AND_Gate
  or or_111 (or_111_out, decoder_13_out5, decoder_13_out6);
  or or_112 (or_112_out, decoder_13_out8, decoder_13_out9);
  or or_113 (or_113_out, decoder_13_out13, decoder_13_out14);
  or or_114 (or_114_out, decoder_13_out2, decoder_13_out3, decoder_13_out5, decoder_13_out6);
  or or_115 (or_115_out, decoder_13_out3, decoder_13_out6, decoder_13_out9, decoder_13_out12);
  or or_116 (or_116_out, decoder_13_out14, or_118_out);
  D_Flip_Flop d_ff_4 (
    .clk(clock_1_out), .D(and_10_out), .Q(d_ff_4_q), .Qn(d_ff_4_qn), .en(and_10_out), .reset(and_11_out));  // open: preset
  D_Flip_Flop d_ff_5 (
    .clk(clock_1_out), .D(and_10_out), .Q(d_ff_5_q), .Qn(d_ff_5_qn), .en(and_10_out), .reset(decoder_12_out14));  // open: preset
  Decoder #(.select(4), .disabled(0), .enable("false")) decoder_12 (
    .out0(decoder_12_out0), .out1(decoder_12_out1), .out2(decoder_12_out2), .out3(decoder_12_out3),
    .out4(decoder_12_out4), .out5(decoder_12_out5), .out6(decoder_12_out6), .out7(decoder_12_out7),
    .out8(decoder_12_out8), .out9(decoder_12_out9), .out10(decoder_12_out10), .out11(decoder_12_out11),
    .out12(decoder_12_out12), .out13(decoder_12_out13), .out14(decoder_12_out14), .out15(decoder_12_out15),
    .sel(demultiplexer_1_out1));
  Decoder #(.select(4), .disabled(0), .enable("false")) decoder_13 (
    .out0(decoder_13_out0), .out1(decoder_13_out1), .out2(decoder_13_out2), .out3(decoder_13_out3),
    .out4(decoder_13_out4), .out5(decoder_13_out5), .out6(decoder_13_out6), .out7(decoder_13_out7),
    .out8(decoder_13_out8), .out9(decoder_13_out9), .out10(decoder_13_out10), .out11(decoder_13_out11),
    .out12(decoder_13_out12), .out13(decoder_13_out13), .out14(decoder_13_out14), .out15(decoder_13_out15),
    .sel(demultiplexer_1_out0));
  D_Flip_Flop d_ff_6 (
    .clk(clock_1_out), .D(and_13_out), .Q(d_ff_6_q), .en(and_13_out), .reset(and_12_out));  // open: Qn, preset
  and and_12 (and_12_out, and_32_out, decoder_14_out5);
  Demultiplexer #(.width(4), .enable("false")) demultiplexer_1 (
    .out0(demultiplexer_1_out0), .out1(demultiplexer_1_out1), .in(demultiplexer_2_out1), .sel(or_121_out));
  or or_117 (or_117_out, button_1_out, register_22_q);
  and and_13 (and_13_out, or_117_out, ~d_ff_6_q);  // AND_Gate
  or or_118 (or_118_out, decoder_14_out1, or_57_out);
  and and_14 (and_14_out, decoder_14_out1, clock_1_out);
  D_Flip_Flop d_ff_7 (
    .clk(clock_1_out), .D(and_13_out), .Q(d_ff_7_q), .en(and_13_out), .reset(decoder_13_out1));  // open: Qn, preset
  or or_119 (or_119_out, On_out, decoder_13_out15);
  Multiplexer #(.width(16), .disabled(0), .enable("false")) multiplexer_128 (
    .in0(16'hff), .in1(16'hfdf), .out(multiplexer_128_out), .sel(in_9));
  D_Flip_Flop d_ff_8 (
    .clk(clock_1_out), .D(On_2_out), .Q(d_ff_8_q), .Qn(d_ff_8_qn), .en(undriven_39), .reset(undriven_40));  // open: preset
  Register #(.width(16)) register_17 (
    .D(adder_5_out), .en(decoder_15_out2), .Q(out_20), .clk(clock_1_out), .clr(and_15_out));
  D_Flip_Flop d_ff_9 (
    .clk(and_14_out), .D(d_ff_7_q), .Q(d_ff_9_q), .Qn(d_ff_9_qn), .en(d_ff_7_q), .reset(or_119_out));  // open: preset
  Multiplexer #(.width(16), .enable("false")) multiplexer_129 (
    .in0({16{1'b0}}), .in1(out_20), .out({multiplexer_129_out_2, multiplexer_129_out}), .sel(or_123_out));
  or or_120 (or_120_out, d_ff_4_q, d_ff_9_q);
  or or_121 (or_121_out, d_ff_9_qn, d_ff_4_q);
  D_Flip_Flop d_ff_10 (
    .clk(clock_1_out), .D(d_ff_8_q), .Q(d_ff_10_q), .Qn(d_ff_10_qn), .en(d_ff_8_q), .reset(and_15_out));  // open: preset
  Decoder #(.select(4), .disabled(0), .enable("false")) decoder_14 (
    .out0(decoder_14_out0), .out1(decoder_14_out1), .out2(decoder_14_out2), .out3(decoder_14_out3),
    .out4(decoder_14_out4), .out5(decoder_14_out5), .out6(decoder_14_out6), .out7(decoder_14_out7),
    .out8(decoder_14_out8), .out9(decoder_14_out9), .out10(decoder_14_out10), .out11(decoder_14_out11),
    .out12(decoder_14_out12), .out13(decoder_14_out13), .out14(decoder_14_out14), .out15(decoder_14_out15),
    .sel(demultiplexer_2_out0));
  or or_122 (or_122_out, decoder_14_out4, decoder_14_out5);
  Register #(.width(2)) register_18 (
    .D(adder_6_out), .en(d_ff_10_q), .Q(register_18_q), .clk(clock_1_out), .clr(and_15_out));
  Decoder #(.select(2), .disabled(0)) decoder_15 (
    .out0(decoder_15_out0), .out1(decoder_15_out1), .out2(decoder_15_out2), .out3(decoder_15_out3),
    .sel(register_18_q), .en(d_ff_10_q));
  or or_123 (or_123_out, decoder_15_out1, decoder_15_out2);
  and and_15 (and_15_out, decoder_15_out2, nand_6_out);
  Multiplexer #(.width(16), .enable("false")) multiplexer_130 (
    .in0({16{1'b0}}), .in1(out_20), .out(multiplexer_130_out), .sel(decoder_15_out2));
  Demultiplexer #(.width(4), .enable("false")) demultiplexer_2 (
    .out0(demultiplexer_2_out0), .out1(demultiplexer_2_out1), .in(register_19_q), .sel(or_120_out));
  Multiplexer #(.width(2), .disabled(0), .enable("false")) multiplexer_131 (
    .in0(2'b00), .in1(2'b10), .out(multiplexer_131_out), .sel(decoder_15_out2));
  nand nand_6 (nand_6_out, or_125_out, or_125_out);
  Adder #(.width(16)) adder_5 (
    .a({16{1'b0}}), .b(multiplexer_130_out), .out(adder_5_out), .cin(decoder_15_out2));  // open: cout
  D_Flip_Flop d_ff_11 (.clk(clock_1_out), .D(On_out), .Q(d_ff_11_q));  // open: Qn, preset, en, reset
  or or_124 (or_124_out, Off_out, ffff_out);
  Multiplexer #(.width(4), .enable("false")) multiplexer_132 (
    .in0(4'b0000), .in1(4'b0011), .out(multiplexer_132_out), .sel(decoder_14_out1));
  Multiplexer #(.width(4), .enable("false")) multiplexer_133 (
    .in0(multiplexer_132_out), .in1(4'b0010), .out(multiplexer_133_out), .sel(and_16_out));
  and and_16 (and_16_out, multiplexer_142_out[12], multiplexer_142_out[13], multiplexer_142_out[14], multiplexer_142_out[15], decoder_14_out1);
  Adder #(.width(2)) adder_6 (.a(multiplexer_131_out), .b(register_18_q), .out(adder_6_out), .cin(1'b1));  // open: cout
  or or_125 (or_125_out, xor_2_out[0], xor_2_out[1], xor_2_out[2], xor_2_out[3], xor_2_out[4], xor_2_out[5], xor_2_out[6], xor_2_out[7], xor_2_out[8], xor_2_out[9], xor_2_out[10], xor_2_out[11], xor_2_out[12], xor_2_out[13], xor_2_out[14], xor_2_out[15]);
  D_Flip_Flop d_ff_12 (
    .clk(clock_1_out), .D(d_ff_11_q), .Q(d_ff_12_q), .en(d_ff_11_q), .reset(or_124_out));  // open: Qn, preset
  Multiplexer #(.width(4), .enable("false")) multiplexer_134 (
    .in0(multiplexer_133_out), .in1(4'b1011), .out(multiplexer_134_out), .sel(decoder_14_out5));
  and and_17 (and_17_out[0], adder_8_out[11], adder_8_out[10], adder_8_out[9], adder_8_out[8], adder_8_out[7], adder_8_out[6], adder_8_out_2[5], adder_8_out_2[4], adder_8_out_2[3], adder_8_out_2[2], adder_8_out_2[1], ~adder_8_out_2[0]);  // AND_Gate
  Adder #(.width(4)) adder_7 (.a(multiplexer_134_out), .b(register_19_q), .out(adder_7_out), .cin(1'b1));  // open: cout
  assign xor_2_out = multiplexer_128_out ^ {multiplexer_129_out_2, multiplexer_129_out};  // XOR_Gate xor_2, 16 bits wide
  RAM #(.addrWidth(16), .bus("separate")) ram_1 (
    .addr({multiplexer_129_out_2, multiplexer_129_out}), .data(ram_1_data), .str(1'b0), .clk(clock_1_out),
    .ld(or_123_out));  // open: din, sel, clr
  Register #(.width(4)) register_19 (
    .D(adder_7_out), .en(d_ff_12_q), .Q(register_19_q), .clk(clock_1_out), .clr(or_124_out));
  Multiplexer #(.width(8), .enable("false")) multiplexer_135 (
    .in0({8{1'b0}}), .in1(ram_1_data), .out(multiplexer_135_out), .sel(or_123_out));
  assign or_126_out = multiplexer_59_out | multiplexer_127_out;  // OR_Gate or_126, 8 bits wide
  assign Read_Ram = multiplexer_152_out | or_130_out;  // OR_Gate or_127, 8 bits wide
  assign or_128_out = Data_In | or_129_out;  // OR_Gate or_128, 8 bits wide
  assign or_129_out = multiplexer_135_out | or_126_out;  // OR_Gate or_129, 8 bits wide
  assign or_130_out = multiplexer_115_out | multiplexer_97_out[7:0];  // OR_Gate or_130, 8 bits wide
  or or_131 (or_131_out[1], decoder_16_out0, decoder_16_out2, decoder_16_out3, decoder_16_out5, decoder_16_out6, decoder_16_out7, decoder_16_out8, decoder_16_out9, decoder_16_out10, decoder_16_out12, decoder_16_out14, decoder_16_out15);
  or or_132 (or_131_out[3], decoder_16_out0, decoder_16_out1, decoder_16_out3, decoder_16_out4, decoder_16_out5, decoder_16_out6, decoder_16_out7, decoder_16_out8, decoder_16_out9, decoder_16_out10, decoder_16_out11, decoder_16_out13);
  or or_133 (or_131_out[5], decoder_16_out0, decoder_16_out2, decoder_16_out6, decoder_16_out8, decoder_16_out10, decoder_16_out11, decoder_16_out12, decoder_16_out13, decoder_16_out14, decoder_16_out15);
  or or_134 (or_131_out[7], decoder_16_out2, decoder_16_out3, decoder_16_out4, decoder_16_out5, decoder_16_out6, decoder_16_out8, decoder_16_out9, decoder_16_out10, decoder_16_out11, decoder_16_out13, decoder_16_out14, decoder_16_out15);
  Decoder #(.select(4), .disabled(0)) decoder_16 (
    .out0(decoder_16_out0), .out1(decoder_16_out1), .out2(decoder_16_out2), .out3(decoder_16_out3),
    .out4(decoder_16_out4), .out5(decoder_16_out5), .out6(decoder_16_out6), .out7(decoder_16_out7),
    .out8(decoder_16_out8), .out9(decoder_16_out9), .out10(decoder_16_out10), .out11(decoder_16_out11),
    .out12(decoder_16_out12), .out13(decoder_16_out13), .out14(decoder_16_out14), .out15(decoder_16_out15),
    .sel(or_126_out[7:4]), .en(and_17_out[0]));
  Multiplexer #(.width(12), .enable("false")) multiplexer_136 (
    .in0({4'b0000, multiplexer_75_out}), .in1({12{1'b1}}), .out(multiplexer_136_out),
    .sel(multiplexer_137_out));
  Multiplexer #(.disabled(0), .enable("false")) multiplexer_137 (
    .in0(and_5_out), .in1(1'b0), .out(multiplexer_137_out), .sel(register_22_q));
  Multiplexer #(.disabled(0), .enable("false")) multiplexer_138 (
    .in0(f1_out), .in1(1'b0), .out(multiplexer_138_out), .sel(register_22_q));
  Adder #(.width(12)) adder_8 (
    .a(or_104_out), .b(multiplexer_136_out), .out({adder_8_out, adder_8_out_2}), .cin(multiplexer_138_out));  // open: cout
  or or_135 (or_131_out[2], decoder_16_out0, decoder_16_out1, decoder_16_out2, decoder_16_out3, decoder_16_out4, decoder_16_out7, decoder_16_out8, decoder_16_out9, decoder_16_out10, decoder_16_out13);
  or or_136 (or_131_out[4], decoder_16_out0, decoder_16_out2, decoder_16_out3, decoder_16_out5, decoder_16_out6, decoder_16_out8, decoder_16_out9, decoder_16_out11, decoder_16_out12, decoder_16_out13, decoder_16_out14);
  or or_137 (or_131_out[6], decoder_16_out0, decoder_16_out4, decoder_16_out5, decoder_16_out6, decoder_16_out8, decoder_16_out9, decoder_16_out10, decoder_16_out11, decoder_16_out12, decoder_16_out14, decoder_16_out15);
  or or_138 (and_17_out[1], decoder_17_out0, decoder_17_out2, decoder_17_out3, decoder_17_out5, decoder_17_out6, decoder_17_out7, decoder_17_out8, decoder_17_out9, decoder_17_out10, decoder_17_out12, decoder_17_out14, decoder_17_out15);
  or or_139 (and_17_out[3], decoder_17_out0, decoder_17_out1, decoder_17_out3, decoder_17_out4, decoder_17_out5, decoder_17_out6, decoder_17_out7, decoder_17_out8, decoder_17_out9, decoder_17_out10, decoder_17_out11, decoder_17_out13);
  or or_140 (and_17_out[5], decoder_17_out0, decoder_17_out2, decoder_17_out6, decoder_17_out8, decoder_17_out10, decoder_17_out11, decoder_17_out12, decoder_17_out13, decoder_17_out14, decoder_17_out15);
  or or_141 (and_17_out[7], decoder_17_out2, decoder_17_out3, decoder_17_out4, decoder_17_out5, decoder_17_out6, decoder_17_out8, decoder_17_out9, decoder_17_out10, decoder_17_out11, decoder_17_out13, decoder_17_out14, decoder_17_out15);
  Decoder #(.select(4), .disabled(0)) decoder_17 (
    .out0(decoder_17_out0), .out1(decoder_17_out1), .out2(decoder_17_out2), .out3(decoder_17_out3),
    .out4(decoder_17_out4), .out5(decoder_17_out5), .out6(decoder_17_out6), .out7(decoder_17_out7),
    .out8(decoder_17_out8), .out9(decoder_17_out9), .out10(decoder_17_out10), .out11(decoder_17_out11),
    .out12(decoder_17_out12), .out13(decoder_17_out13), .out14(decoder_17_out14), .out15(decoder_17_out15),
    .sel(or_126_out[3:0]), .en(and_17_out[0]));
  or or_142 (and_17_out[2], decoder_17_out0, decoder_17_out1, decoder_17_out2, decoder_17_out3, decoder_17_out4, decoder_17_out7, decoder_17_out8, decoder_17_out9, decoder_17_out10, decoder_17_out13);
  or or_143 (and_17_out[4], decoder_17_out0, decoder_17_out2, decoder_17_out3, decoder_17_out5, decoder_17_out6, decoder_17_out8, decoder_17_out9, decoder_17_out11, decoder_17_out12, decoder_17_out13, decoder_17_out14);
  or or_144 (and_17_out[6], decoder_17_out0, decoder_17_out4, decoder_17_out5, decoder_17_out6, decoder_17_out8, decoder_17_out9, decoder_17_out10, decoder_17_out11, decoder_17_out12, decoder_17_out14, decoder_17_out15);
  Register register_20 (.D(or_128_out), .en(and_22_out), .Q(register_20_q), .clk(clock_1_out));  // open: clr
  or or_145 (or_145_out, multiplexer_146_out, or_115_out, decoder_15_out1);
  or or_146 (or_146_out, or_5_out, or_6_out, decoder_14_out1);
  Multiplexer #(.disabled(0), .enable("false")) multiplexer_139 (
    .in0(or_145_out), .in1(1'b0), .out(multiplexer_139_out), .sel(and_23_out));
  Multiplexer #(.width(6), .disabled(0), .enable("false")) multiplexer_140 (
    .in0(adder_8_out), .in1(register_20_q[5:0]), .out(multiplexer_140_out), .sel(and_23_out));
  and and_18 (and_18_out, ~adder_8_out_2[4], adder_8_out_2[5], adder_8_out[6], adder_8_out[7], adder_8_out[8], adder_8_out[9], adder_8_out[10], adder_8_out[11]);  // AND_Gate
  and and_19 (and_19_out, adder_8_out_2[0], ~adder_8_out_2[1], ~adder_8_out_2[2], adder_8_out_2[3]);  // AND_Gate
  and and_20 (and_20_out, ~adder_8_out_2[0], adder_8_out_2[1], ~adder_8_out_2[2], adder_8_out_2[3]);  // AND_Gate
  and and_21 (and_21_out, adder_8_out_2[0], adder_8_out_2[1], ~adder_8_out_2[2], adder_8_out_2[3]);  // AND_Gate
  and and_22 (and_22_out, and_18_out, and_19_out, or_5_out);
  and and_23 (and_23_out, and_18_out, and_20_out, or_5_out);
  and and_24 (and_24_out, and_18_out, and_21_out, or_5_out);
  RAM #(.addrWidth(6), .bus("separate")) ram_2 (
    .addr(multiplexer_140_out), .din(or_128_out), .data(ram_2_data), .str(and_23_out), .clk(clock_1_out),
    .ld(or_146_out), .clr(and_24_out));  // open: sel
  Register register_21 (
    .D({2'b00, multiplexer_140_out}), .en(or_146_out), .Q(register_21_q), .clk(clock_1_out));  // open: clr
  Multiplexer #(.width(8), .enable("false")) multiplexer_141 (
    .in0({8{1'b0}}), .in1(ram_2_data), .out(multiplexer_141_out), .sel(or_146_out));
  Multiplexer #(.width(16), .disabled(0), .enable("false")) multiplexer_142 (
    .in0(multiplexer_153_out), .in1({16{1'b0}}), .out(multiplexer_142_out), .sel(or_148_out));
  Multiplexer #(.width(12), .disabled(0), .enable("false")) multiplexer_143 (
    .in0({12{1'b0}}), .in1({multiplexer_141_out[5:0], adder_8_out_2}), .out(multiplexer_143_out),
    .sel(multiplexer_141_out[7]));
  Counter #(.width(32), .max('hffffffff)) counter_1 (
    .count(register_22_q), .clk(register_22_q));  // open: load, D, Q, carry, clr
  and and_25 (and_25_out, ~multiplexer_141_out[7], or_146_out);  // AND_Gate
  Register #(.width(1)) register_22 (
    .D(and_25_out), .en(clock_1_out), .Q(register_22_q), .clk(clock_1_out));  // open: clr
  assign or_147_out = multiplexer_129_out | multiplexer_121_out | multiplexer_143_out;  // OR_Gate or_147, 12 bits wide
  or or_148 (or_148_out, register_22_q, and_25_out);
  Multiplexer #(.disabled(0), .enable("false")) multiplexer_144 (
    .in0(decoder_14_out1), .in1(1'b0), .out(multiplexer_144_out), .sel(or_148_out));
  and and_26 (and_26_out, and_25_out, or_5_out);
  Multiplexer #(.disabled(0), .enable("false")) multiplexer_145 (
    .in0(or_6_out), .in1(1'b0), .out(multiplexer_145_out), .sel(or_148_out));
  Multiplexer #(.disabled(0), .enable("false")) multiplexer_146 (
    .in0(or_5_out), .in1(1'b0), .out(multiplexer_146_out), .sel(and_26_out));
  and and_27 (and_27_out, ~or_147_out[4], or_147_out[5], or_147_out[6], or_147_out[7], or_147_out[8], or_147_out[9], or_147_out[10], or_147_out[11]);  // AND_Gate
  and and_28 (and_28_out, ~or_147_out[0], ~or_147_out[1], ~or_147_out[2], ~or_147_out[3]);  // AND_Gate
  and and_29 (and_29_out, or_147_out[0], ~or_147_out[1], ~or_147_out[2], ~or_147_out[3]);  // AND_Gate
  and and_30 (and_30_out, ~or_147_out[0], or_147_out[1], ~or_147_out[2], ~or_147_out[3]);  // AND_Gate
  and and_31 (and_31_out, or_147_out[0], or_147_out[1], ~or_147_out[2], ~or_147_out[3]);  // AND_Gate
  assign or_149_out = or_147_out | multiplexer_151_out;  // OR_Gate or_149, 12 bits wide
  or or_150 (or_150_out, multiplexer_139_out, and_42_out);
  or or_151 (or_151_out, multiplexer_145_out, and_41_out);
  assign or_152_out = or_128_out | multiplexer_158_out;  // OR_Gate or_152, 8 bits wide
  and and_32 (and_32_out, ~or_147_out[0], or_147_out[1], ~or_147_out[2], ~or_147_out[3], ~or_147_out[4], ~or_147_out[5], ~or_147_out[6], ~or_147_out[7], or_147_out[8], or_147_out[9], or_147_out[10], or_147_out[11]);  // AND_Gate
  and and_33 (and_33_out, and_27_out, and_28_out, multiplexer_139_out);
  and and_34 (and_34_out, and_27_out, and_29_out, multiplexer_139_out);
  and and_35 (and_35_out, and_27_out, and_30_out, multiplexer_139_out);
  and and_36 (and_36_out, and_27_out, and_31_out, multiplexer_139_out);
  Register register_23 (.D(or_128_out), .en(and_33_out), .Q(register_23_q), .clk(clock_1_out));  // open: clr
  Register register_24 (.D(or_128_out), .en(and_34_out), .Q(register_24_q), .clk(clock_1_out));  // open: clr
  Register #(.width(1)) register_25 (
    .D(and_34_out), .en(and_34_out), .Q(register_25_q), .clk(clock_1_out), .clr(and_45_out));
  Register register_26 (.D(or_128_out), .en(and_35_out), .Q(register_26_q), .clk(clock_1_out));  // open: clr
  Register register_27 (.D(or_128_out), .en(and_36_out), .Q(register_27_q), .clk(clock_1_out));  // open: clr
  Register #(.width(1)) register_28 (
    .D(and_36_out), .en(and_36_out), .Q(register_28_q), .clk(clock_1_out), .clr(and_45_out));
  or or_153 (or_153_out, multiplexer_144_out, or_151_out);
  Multiplexer #(.width(14), .disabled(0), .enable("false")) multiplexer_147 (
    .in0({14{1'b0}}), .in1({register_23_q, multiplexer_154_out}), .out(multiplexer_147_out), .sel(and_37_out));
  and and_37 (and_37_out, register_25_q, or_157_out);
  not not_2 (not_2_out, or_149_out[0]);
  Multiplexer #(.width(14), .disabled(0), .enable("false")) multiplexer_148 (
    .in0(multiplexer_147_out), .in1({register_27_q, multiplexer_154_out}), .out(multiplexer_148_out),
    .sel(and_38_out));
  and and_38 (and_38_out, register_28_q, or_157_out);
  RAM #(.addrWidth(11), .bus("separate")) ram_3 (
    .addr(or_149_out[11:1]), .din(or_152_out), .data(ram_3_data), .str(or_150_out), .sel(not_2_out),
    .clk(clock_1_out), .ld(or_153_out));  // open: clr
  and and_39 (and_39_out, not_2_out, or_153_out);
  Multiplexer #(.width(8), .enable("false")) multiplexer_149 (
    .in0({8{1'b0}}), .in1(ram_3_data), .out(multiplexer_149_out), .sel(and_39_out));
  Multiplexer #(.width(12), .disabled(0), .enable("false")) multiplexer_150 (
    .in0({12{1'b0}}), .in1({register_24_q[5:0], multiplexer_154_out}), .out(multiplexer_150_out),
    .sel(and_37_out));
  Multiplexer #(.width(12), .disabled(0), .enable("false")) multiplexer_151 (
    .in0(multiplexer_150_out), .in1({register_26_q[5:0], multiplexer_154_out}), .out(multiplexer_151_out),
    .sel(and_38_out));
  or or_154 (or_154_out, multiplexer_144_out, or_151_out);
  or or_155 (or_155_out, multiplexer_144_out, or_149_out[0]);
  and and_40 (and_40_out, register_25_q, or_157_out);
  and and_41 (and_41_out, register_28_q, or_157_out);
  and and_42 (and_42_out, register_25_q, decoder_18_out3);
  RAM #(.addrWidth(11), .bus("separate")) ram_4 (
    .addr(or_149_out[11:1]), .din(or_152_out), .data(ram_4_data), .str(or_150_out), .sel(or_155_out),
    .clk(clock_1_out), .ld(or_154_out));  // open: clr
  and and_43 (and_43_out, or_155_out, or_154_out);
  and and_44 (and_44_out, register_28_q, decoder_18_out3);
  Multiplexer #(.width(8), .enable("false")) multiplexer_152 (
    .in0(multiplexer_149_out), .in1(ram_4_data), .out(multiplexer_152_out), .sel(and_43_out));
  or or_156 (or_156_out, register_25_q, register_28_q);
  Counter #(.width(32), .max('hffffffff)) counter_2 (
    .count(or_156_out), .clk(clock_1_out));  // open: load, D, Q, carry, clr
  Counter #(.width(32), .max('hffffffff)) counter_3 (
    .count(or_156_out), .clk(or_156_out));  // open: load, D, Q, carry, clr
  Multiplexer #(.width(16), .enable("false")) multiplexer_153 (
    .in0({16{1'b0}}), .in1({ram_3_data, ram_4_data}), .out(multiplexer_153_out), .sel(multiplexer_144_out));
  Register #(.width(6)) register_29 (
    .D(adder_9_out), .en(decoder_18_out4), .Q(register_29_q), .clk(clock_1_out), .clr(and_45_out));
  Multiplexer #(.width(6), .enable("false")) multiplexer_154 (
    .in0({6{1'b0}}), .in1(register_29_q), .out(multiplexer_154_out), .sel(or_157_out));
  Register #(.width(3)) register_30 (
    .D(adder_10_out), .en(or_156_out), .Q(register_30_q), .clk(clock_1_out), .clr(and_45_out));
  Decoder #(.select(3), .disabled(0)) decoder_18 (
    .out3(decoder_18_out3), .out4(decoder_18_out4), .out5(decoder_18_out5), .out6(decoder_18_out6),
    .sel(register_30_q), .en(or_156_out));  // open: out0, out1, out2, out7
  or or_157 (or_157_out, decoder_18_out3, decoder_18_out4);
  or or_158 (or_158_out, decoder_18_out4, decoder_18_out4);
  and and_45 (and_45_out, decoder_18_out4, and_46_out);
  Multiplexer #(.width(6), .enable("false")) multiplexer_155 (
    .in0({6{1'b0}}), .in1(register_29_q), .out(multiplexer_155_out), .sel(or_158_out));
  RAM #(.addrWidth(12), .bus("separate")) ram_5 (
    .addr(or_149_out), .din(or_152_out), .data(ram_5_data), .str(or_150_out), .clk(clock_1_out),
    .ld(or_151_out));  // open: sel, clr
  Multiplexer #(.width(3), .disabled(0), .enable("false")) multiplexer_156 (
    .in0(3'b000), .in1(3'b110), .out(multiplexer_156_out), .sel(decoder_18_out4));
  Adder #(.width(6)) adder_9 (
    .a({6{1'b0}}), .b(multiplexer_155_out), .out(adder_9_out), .cin(or_158_out));  // open: cout
  Multiplexer #(.width(8), .enable("false")) multiplexer_157 (
    .in0({8{1'b0}}), .in1(ram_5_data), .out(multiplexer_157_out), .sel(or_151_out));
  Adder #(.width(3)) adder_10 (
    .a(multiplexer_156_out), .b(register_30_q), .out(adder_10_out), .cin(1'b1));  // open: cout
  and and_46 (and_46_out, multiplexer_154_out[0], multiplexer_154_out[1], multiplexer_154_out[2], multiplexer_154_out[3], multiplexer_154_out[4], multiplexer_154_out[5]);
  RAM #(.addrWidth(14), .bus("separate")) ram_6 (
    .addr(multiplexer_148_out), .din(multiplexer_152_out), .data(ram_6_data), .str(and_44_out),
    .clk(clock_1_out), .ld(and_40_out));  // open: sel, clr
  Multiplexer #(.width(8), .enable("false")) multiplexer_158 (
    .in0({8{1'b0}}), .in1(ram_6_data), .out(multiplexer_158_out), .sel(and_40_out));

  // Notes on the sheet:
  //   4011B Quad 2 Inputs NAND
  //   4013B Dual D-tipe flip-flop
  //   Clock
  //   Loader 256
  //   Loader 4K
  //   0x00
  //   00x0
  //   WReg 0x00
  //   WReg 00x0
  //   R00x0 alu1
  //   R0x00 alu1
  //   R000x alu2
  //   R0x00 to Ram
  //   R00x0 to Ram
  //   R000x adr alu
  //   R00x0 adr alu
  //   Enter
  //   ALU
  //   Save actual RA not +2
  //   Pc hi Adr f02
  //   Pc lo  Adr f03
  //   Exc code Adr f00
  //   Exc data Adr f01
  //   Adr f04
  //   R Pc
  //   W Ram
  //   W Pc
  //   R PC
  //   R PC+1
  //   W Pc
  //   W Acc
  //   Loading stops at fdf to avoid engaging the DMA
  //   R RAM 16
  //   Adr ALU
  //   Write Ram ffe=write on screen decoded
  //   MMU/ Page Table
  //   TLB fe9 set adr in MMU to write, fea write, feb Cls
  //   Interrupting Data flow to prevent next inst done twice
  //   Gen Interrupt Preventer reset f02
  //   To fix
  //   included from loader
  //   It activates on all W Ram
  //   DMA control
  //   HD Adr
  //   Ram Adr
  //   The interrupt when writing fe1 or fe3 stops the driver execution after the next instruction in executed
  //   R HD
  //   R Ram
  //   W Ram
  //   W HD
  //   16Kb HD 64 bites/page 256 pages
  //   HD
endmodule
