// Logisim project 4000 Chips.circ as structural Verilog: 6 circuits, main circuit main
module main (
  input  in_1,
  input  in_2,
  input  in_3,
  input  in_4,
  input  in_5,
  input  in_6,
  input  in_7,
  input  in_8,
  input  in_9,
  input  in_10,
  input  in_11,
  input  in_12,
  input  in_13,
  input  in_14,
  input  in_15,
  input  in_16,
  input  in_17,
  input  in_18,
  input  in_19,
  input  in_20,
  input  in_21,
  input  in_22,
  input  in_23,
  output out_24,
  output out_25,
  output out_26,
  output out_27,
  output out_28,
  output out_29,
  output out_30,
  output out_31,
  output out_32,
  output out_33,
  output out_34,
  output out_35,
  output out_36,
  output out_37,
  output out_38,
  output out_39
);

  wire and_1_out, and_2_out, and_3_out, and_4_out, and_5_out, and_6_out, and_7_out, and_8_out, and_9_out,
       and_10_out, and_11_out, and_12_out, and_13_out, and_14_out, and_15_out, and_16_out, d_ff_1_q,
       d_ff_1_qn, d_ff_2_q, d_ff_2_qn, d_ff_3_q, d_ff_3_qn, d_ff_4_q, d_ff_4_qn, d_ff_5_q, d_ff_5_qn,
       d_ff_6_q, d_ff_6_qn, d_ff_7_q, d_ff_7_qn, d_ff_8_q, d_ff_8_qn, nand_1_out, nand_2_out, nand_3_out,
       nand_4_out, nand_5_out, nand_6_out, nand_7_out, nand_8_out, nand_9_out, nand_10_out, nand_11_out,
       nand_12_out, nand_13_out, nand_14_out, nand_15_out, nand_16_out, or_1_out, or_2_out, or_3_out,
       or_4_out, or_5_out, or_6_out, or_7_out, or_8_out, undriven, undriven_2, undriven_3, undriven_4,
       undriven_5, undriven_6, undriven_7, undriven_8, undriven_9, undriven_10, undriven_11, undriven_12,
       undriven_13, undriven_14, undriven_15, undriven_16, undriven_17, undriven_18, undriven_19,
       undriven_20, undriven_21, undriven_22, undriven_23, undriven_24, undriven_25, undriven_26,
       undriven_27, undriven_28, undriven_29, undriven_30, undriven_31, undriven_32, undriven_33,
       undriven_34, undriven_35, undriven_36, undriven_37, undriven_38, undriven_39, undriven_40,
       undriven_41, undriven_42, undriven_43, undriven_44, undriven_45, undriven_46, undriven_47,
       undriven_48, undriven_49, undriven_50, undriven_51, undriven_52, undriven_53, undriven_54,
       undriven_55, undriven_56, undriven_57, undriven_58, undriven_59, undriven_60, undriven_61,
       undriven_62, undriven_63, undriven_64, undriven_65, undriven_66, undriven_67, undriven_68,
       undriven_69, undriven_70, undriven_71, undriven_72, undriven_73, undriven_74, undriven_75,
       undriven_76, undriven_77, undriven_78, undriven_79, undriven_80, undriven_81, undriven_82,
       undriven_83, undriven_84, undriven_85, undriven_86, undriven_87, undriven_88, undriven_89,
       undriven_90, undriven_91, undriven_92;

  _4051_8_Bits_2_channel_Multiplex u_4051_8_bits_2_channel_multiplex_1 ();  // open: in_1, in_2, in_3, in_4, in_5, in_6, in_7, in_8, in_9, in_10, in_11, in_12, in_13, in_14, in_15, in_16, in_17, out_18, out_19, out_20, out_21, out_22, out_23, out_24, out_25
  _4097_Dual_2to4_Decoder u_4097_dual_2to4_decoder_1 ();  // open: in_1, in_2, in_3, in_4, in_5, in_6, out_7, out_8, out_9, out_10, out_11, out_12, out_13, out_14
  _8016B_16_Bites_Ram_NAND u_8016b_16_bites_ram_nand_1 ();  // open: in_1, in_2, in_3, in_4, in_21, in_22, in_23, in_24, in_5, in_6, in_7, in_8, in_9, in_10, in_11, in_12, in_13, in_14, in_15, in_16, in_17, in_18, in_19, in_20, out_25, out_26, out_27, out_28, out_29, out_30, out_31, out_32, out_33, out_34, out_35, out_36, out_37, out_38, out_39, out_40
  _8256B_256_Bites_Ram_Lc u_8256b_256_bites_ram_lc_1 ();  // open: in_1, in_2, in_3, in_4, in_5, in_6, in_7, out_8
  nand nand_1 (nand_1_out, undriven_7, undriven);
  nand nand_2 (nand_2_out, undriven_2, undriven_8);
  nand nand_3 (nand_3_out, undriven_9, undriven_3);
  nand nand_4 (nand_4_out, undriven_4, undriven_10);
  nand nand_5 (nand_5_out, undriven_11, undriven_5);
  nand nand_6 (nand_6_out, undriven_6, undriven_12);
  nand nand_7 (nand_7_out, undriven_21, undriven_24);
  nand nand_8 (nand_8_out, undriven_13, undriven_14);
  nand nand_9 (nand_9_out, undriven_22, undriven_15);
  nand nand_10 (nand_10_out, undriven_16, undriven_17);
  nand nand_11 (nand_11_out, undriven_23, undriven_18);
  nand nand_12 (nand_12_out, undriven_19, undriven_20);
  V096_96_Bites_32By24_Video_Buffer v096_96_bites_32by24_video_buffer_1 ();  // open: out_8, out_9, out_10, out_11, out_12, out_13, out_14, out_15, out_16, out_17, out_18, out_19, out_20, out_21, out_22, out_23, out_24, out_25, out_26, out_27, out_28, out_29, out_30, out_31, in_1, in_2, in_3, in_4, in_5, in_6, in_7
  D_Flip_Flop d_ff_1 (
    .clk(undriven_29), .D(undriven_25), .Q(d_ff_1_q), .Qn(d_ff_1_qn), .en(undriven_33), .reset(undriven_35));  // open: preset
  D_Flip_Flop d_ff_2 (
    .clk(undriven_30), .D(undriven_26), .Q(d_ff_2_q), .Qn(d_ff_2_qn), .en(undriven_34), .reset(undriven_36));  // open: preset
  D_Flip_Flop d_ff_3 (
    .clk(undriven_31), .D(undriven_27), .Q(d_ff_3_q), .Qn(d_ff_3_qn), .en(undriven_28), .reset(undriven_32));  // open: preset
  D_Flip_Flop d_ff_4 (
    .clk(undriven_42), .D(undriven_39), .Q(d_ff_4_q), .Qn(d_ff_4_qn), .en(undriven_46), .reset(undriven_43));  // open: preset
  D_Flip_Flop d_ff_5 (
    .clk(undriven_40), .D(undriven_37), .Q(d_ff_5_q), .Qn(d_ff_5_qn), .en(undriven_44), .reset(undriven_47));  // open: preset
  D_Flip_Flop d_ff_6 (
    .clk(undriven_41), .D(undriven_38), .Q(d_ff_6_q), .Qn(d_ff_6_qn), .en(undriven_45), .reset(undriven_48));  // open: preset
  Decoder #(.select(2), .disabled(0)) decoder_1 (
    .out0(out_24), .out1(out_25), .out2(out_26), .out3(out_27), .sel({in_2, in_3}), .en(in_1));
  or or_1 (or_1_out, undriven_53, undriven_50);
  or or_2 (or_2_out, undriven_58, undriven_55);
  or or_3 (or_3_out, undriven_56, undriven_57);
  or or_4 (or_4_out, undriven_51, undriven_54);
  and and_1 (and_1_out, ~undriven_52, ~undriven_49);  // AND_Gate
  and and_2 (and_2_out, and_1_out, undriven_59);
  and and_3 (and_3_out, undriven_59, and_4_out);
  and and_4 (and_4_out, undriven_52, ~undriven_49);  // AND_Gate
  and and_5 (and_5_out, and_6_out, undriven_59);
  and and_6 (and_6_out, ~undriven_52, undriven_49);  // AND_Gate
  and and_7 (and_7_out, undriven_59, and_8_out);
  and and_8 (and_8_out, undriven_52, undriven_49);
  Decoder #(.select(2), .disabled(0)) decoder_2 (
    .out0(out_28), .out1(out_29), .out2(out_30), .out3(out_31), .sel({in_5, in_6}), .en(in_4));
  Multiplexer #(.width(8), .enable("false")) multiplexer_1 (
    .in0({in_7, in_8, in_9, in_10, in_11, in_12, in_13, in_14}),
    .in1({in_15, in_16, in_17, in_18, in_19, in_20, in_21, in_22}),
    .out({out_32, out_33, out_34, out_35, out_36, out_37, out_38, out_39}), .sel(in_23));
  and and_9 (and_9_out, undriven_83, undriven_75);
  and and_10 (and_10_out, undriven_66, undriven_60);
  and and_11 (and_11_out, undriven_76, undriven_77);
  and and_12 (and_12_out, undriven_61, undriven_67);
  nand nand_13 (nand_13_out, undriven_68, undriven_62);
  nand nand_14 (nand_14_out, undriven_78, undriven_79);
  nand nand_15 (nand_15_out, undriven_63, undriven_69);
  nand nand_16 (nand_16_out, undriven_80, undriven_81);
  D_Flip_Flop d_ff_7 (
    .clk(undriven_70), .D(undriven_64), .Q(d_ff_7_q), .Qn(d_ff_7_qn), .en(undriven_65), .reset(undriven_71));  // open: preset
  D_Flip_Flop d_ff_8 (
    .clk(undriven_73), .D(undriven_72), .Q(d_ff_8_q), .Qn(d_ff_8_qn), .en(undriven_82), .reset(undriven_74));  // open: preset
  and and_13 (and_13_out, undriven_84, undriven_87);
  and and_14 (and_14_out, undriven_87, undriven_85);
  and and_15 (and_15_out, undriven_86, undriven_87);
  and and_16 (and_16_out, undriven_87, undriven_88);
  or or_5 (or_5_out, and_13_out, undriven_89);
  or or_6 (or_6_out, undriven_90, and_14_out);
  or or_7 (or_7_out, and_15_out, undriven_91);
  or or_8 (or_8_out, undriven_92, and_16_out);

  // Notes on the sheet:
  //   4011B Quad 2 Inputs NAND
  //   4013B Dual D-tipe flip-flop
endmodule

module _4051_8_Bits_2_channel_Multiplex (
  input  in_1,
  input  in_2,
  input  in_3,
  input  in_4,
  input  in_5,
  input  in_6,
  input  in_7,
  input  in_8,
  input  in_9,
  input  in_10,
  input  in_11,
  input  in_12,
  input  in_13,
  input  in_14,
  input  in_15,
  input  in_16,
  input  in_17,
  output out_18,
  output out_19,
  output out_20,
  output out_21,
  output out_22,
  output out_23,
  output out_24,
  output out_25
);

  Multiplexer #(.width(8), .enable("false")) multiplexer_1 (
    .in0({in_1, in_2, in_3, in_4, in_5, in_6, in_7, in_8}),
    .in1({in_9, in_10, in_11, in_12, in_13, in_14, in_15, in_16}),
    .out({out_18, out_19, out_20, out_21, out_22, out_23, out_24, out_25}), .sel(in_17));
endmodule

module _4097_Dual_2to4_Decoder (
  input  in_1,
  input  in_2,
  input  in_3,
  input  in_4,
  input  in_5,
  input  in_6,
  output out_7,
  output out_8,
  output out_9,
  output out_10,
  output out_11,
  output out_12,
  output out_13,
  output out_14
);

  Decoder #(.select(2), .disabled(0)) decoder_1 (
    .out0(out_7), .out1(out_8), .out2(out_9), .out3(out_10), .sel({in_2, in_3}), .en(in_1));
  Decoder #(.select(2), .disabled(0)) decoder_2 (
    .out0(out_11), .out1(out_12), .out2(out_13), .out3(out_14), .sel({in_5, in_6}), .en(in_4));
endmodule

module _8016B_16_Bites_Ram_NAND (
  input  in_1,
  input  in_2,
  input  in_3,
  input  in_4,
  input  in_5,
  input  in_6,
  input  in_7,
  input  in_8,
  input  in_9,
  input  in_10,
  input  in_11,
  input  in_12,
  input  in_13,
  input  in_14,
  input  in_15,
  input  in_16,
  input  in_17,
  input  in_18,
  input  in_19,
  input  in_20,
  input  in_21,
  input  in_22,
  input  in_23,
  input  in_24,
  output out_25,
  output out_26,
  output out_27,
  output out_28,
  output out_29,
  output out_30,
  output out_31,
  output out_32,
  output out_33,
  output out_34,
  output out_35,
  output out_36,
  output out_37,
  output out_38,
  output out_39,
  output out_40
);

  wire and_1_out, and_2_out, and_3_out, and_4_out, and_5_out, and_6_out, and_7_out, and_8_out, and_9_out,
       and_10_out, and_11_out, and_12_out, and_13_out, and_14_out, and_15_out, and_16_out, and_17_out,
       and_18_out, and_19_out, and_20_out, and_21_out, and_22_out, and_23_out, and_24_out, and_25_out,
       and_26_out, and_27_out, and_28_out, and_29_out, and_30_out, and_31_out, and_32_out, and_33_out,
       and_34_out, and_35_out, and_36_out, and_37_out, and_38_out, and_39_out, and_40_out, and_41_out,
       and_42_out, and_43_out, and_44_out, and_45_out, and_46_out, and_47_out, and_48_out, and_49_out,
       and_50_out, and_51_out, and_52_out, and_53_out, and_54_out, and_55_out, and_56_out, and_57_out,
       and_58_out, and_59_out, and_60_out, and_61_out, and_62_out, and_63_out, and_64_out, and_65_out,
       and_66_out, and_67_out, and_68_out, and_69_out, and_70_out, and_71_out, and_72_out, and_73_out,
       and_74_out, and_75_out, and_76_out, and_77_out, and_78_out, and_79_out, and_80_out, and_81_out,
       and_82_out, and_83_out, and_84_out, and_85_out, and_86_out, and_87_out, and_88_out, and_89_out,
       and_90_out, and_91_out, and_92_out, and_93_out, and_94_out, and_95_out, and_96_out, and_97_out,
       and_98_out, and_99_out, and_100_out, and_101_out, and_102_out, and_103_out, and_104_out, and_105_out,
       and_106_out, and_107_out, and_108_out, and_109_out, and_110_out, and_111_out, and_112_out,
       and_113_out, and_114_out, and_115_out, and_116_out, and_117_out, and_118_out, and_119_out,
       and_120_out, and_121_out, and_122_out, and_123_out, and_124_out, and_125_out, and_126_out,
       and_127_out, and_128_out, and_129_out, and_130_out, and_131_out, and_132_out, and_133_out,
       and_134_out, and_135_out, and_136_out, and_137_out, and_138_out, and_139_out, and_140_out,
       and_141_out, and_142_out, and_143_out, and_144_out, and_145_out, and_146_out, and_147_out,
       and_148_out, and_149_out, and_150_out, and_151_out, and_152_out, and_153_out, and_154_out,
       and_155_out, and_156_out, and_157_out, and_158_out, and_159_out, and_160_out, and_161_out,
       and_162_out, and_163_out, and_164_out, and_165_out, and_166_out, and_167_out, and_168_out, d_ff_1_q,
       d_ff_1_qn, d_ff_2_q, d_ff_2_qn, d_ff_3_q, d_ff_3_qn, d_ff_4_q, d_ff_4_qn, d_ff_5_q, d_ff_5_qn,
       d_ff_6_q, d_ff_6_qn, d_ff_7_q, d_ff_7_qn, d_ff_8_q, d_ff_8_qn, d_ff_9_q, d_ff_9_qn, d_ff_10_q,
       d_ff_10_qn, d_ff_11_q, d_ff_11_qn, d_ff_12_q, d_ff_12_qn, d_ff_13_q, d_ff_13_qn, d_ff_14_q,
       d_ff_14_qn, d_ff_15_q, d_ff_15_qn, d_ff_16_q, d_ff_16_qn, d_ff_17_q, d_ff_17_qn, d_ff_18_q,
       d_ff_18_qn, d_ff_19_q, d_ff_19_qn, d_ff_20_q, d_ff_20_qn, d_ff_21_q, d_ff_21_qn, d_ff_22_q,
       d_ff_22_qn, d_ff_23_q, d_ff_23_qn, d_ff_24_q, d_ff_24_qn, d_ff_25_q, d_ff_25_qn, d_ff_26_q,
       d_ff_26_qn, d_ff_27_q, d_ff_27_qn, d_ff_28_q, d_ff_28_qn, d_ff_29_q, d_ff_29_qn, d_ff_30_q,
       d_ff_30_qn, d_ff_31_q, d_ff_31_qn, d_ff_32_q, d_ff_32_qn, d_ff_33_q, d_ff_33_qn, d_ff_34_q,
       d_ff_34_qn, d_ff_35_q, d_ff_35_qn, d_ff_36_q, d_ff_36_qn, d_ff_37_q, d_ff_37_qn, d_ff_38_q,
       d_ff_38_qn, d_ff_39_q, d_ff_39_qn, d_ff_40_q, d_ff_40_qn, d_ff_41_q, d_ff_41_qn, d_ff_42_q,
       d_ff_42_qn, d_ff_43_q, d_ff_43_qn, d_ff_44_q, d_ff_44_qn, d_ff_45_q, d_ff_45_qn, d_ff_46_q,
       d_ff_46_qn, d_ff_47_q, d_ff_47_qn, d_ff_48_q, d_ff_48_qn, d_ff_49_q, d_ff_49_qn, d_ff_50_q,
       d_ff_50_qn, d_ff_51_q, d_ff_51_qn, d_ff_52_q, d_ff_52_qn, d_ff_53_q, d_ff_53_qn, d_ff_54_q,
       d_ff_54_qn, d_ff_55_q, d_ff_55_qn, d_ff_56_q, d_ff_56_qn, d_ff_57_q, d_ff_57_qn, d_ff_58_q,
       d_ff_58_qn, d_ff_59_q, d_ff_59_qn, d_ff_60_q, d_ff_60_qn, d_ff_61_q, d_ff_61_qn, d_ff_62_q,
       d_ff_62_qn, d_ff_63_q, d_ff_63_qn, d_ff_64_q, d_ff_64_qn, d_ff_65_q, d_ff_65_qn, d_ff_66_q,
       d_ff_66_qn, d_ff_67_q, d_ff_67_qn, d_ff_68_q, d_ff_68_qn, d_ff_69_q, d_ff_69_qn, d_ff_70_q,
       d_ff_70_qn, d_ff_71_q, d_ff_71_qn, d_ff_72_q, d_ff_72_qn, d_ff_73_q, d_ff_73_qn, d_ff_74_q,
       d_ff_74_qn, d_ff_75_q, d_ff_75_qn, d_ff_76_q, d_ff_76_qn, d_ff_77_q, d_ff_77_qn, d_ff_78_q,
       d_ff_78_qn, d_ff_79_q, d_ff_79_qn, d_ff_80_q, d_ff_80_qn, d_ff_81_q, d_ff_81_qn, d_ff_82_q,
       d_ff_82_qn, d_ff_83_q, d_ff_83_qn, d_ff_84_q, d_ff_84_qn, d_ff_85_q, d_ff_85_qn, d_ff_86_q,
       d_ff_86_qn, d_ff_87_q, d_ff_87_qn, d_ff_88_q, d_ff_88_qn, d_ff_89_q, d_ff_89_qn, d_ff_90_q,
       d_ff_90_qn, d_ff_91_q, d_ff_91_qn, d_ff_92_q, d_ff_92_qn, d_ff_93_q, d_ff_93_qn, d_ff_94_q,
       d_ff_94_qn, d_ff_95_q, d_ff_95_qn, d_ff_96_q, d_ff_96_qn, d_ff_97_q, d_ff_97_qn, d_ff_98_q,
       d_ff_98_qn, d_ff_99_q, d_ff_99_qn, d_ff_100_q, d_ff_100_qn, d_ff_101_q, d_ff_101_qn, d_ff_102_q,
       d_ff_102_qn, d_ff_103_q, d_ff_103_qn, d_ff_104_q, d_ff_104_qn, d_ff_105_q, d_ff_105_qn, d_ff_106_q,
       d_ff_106_qn, d_ff_107_q, d_ff_107_qn, d_ff_108_q, d_ff_108_qn, d_ff_109_q, d_ff_109_qn, d_ff_110_q,
       d_ff_110_qn, d_ff_111_q, d_ff_111_qn, d_ff_112_q, d_ff_112_qn, d_ff_113_q, d_ff_113_qn, d_ff_114_q,
       d_ff_114_qn, d_ff_115_q, d_ff_115_qn, d_ff_116_q, d_ff_116_qn, d_ff_117_q, d_ff_117_qn, d_ff_118_q,
       d_ff_118_qn, d_ff_119_q, d_ff_119_qn, d_ff_120_q, d_ff_120_qn, d_ff_121_q, d_ff_121_qn, d_ff_122_q,
       d_ff_122_qn, d_ff_123_q, d_ff_123_qn, d_ff_124_q, d_ff_124_qn, d_ff_125_q, d_ff_125_qn, d_ff_126_q,
       d_ff_126_qn, d_ff_127_q, d_ff_127_qn, d_ff_128_q, d_ff_128_qn, nand_1_out, nand_2_out, nand_3_out,
       nand_4_out, nand_5_out, nand_6_out, nand_7_out, nand_8_out, nand_9_out, nand_10_out, nand_11_out,
       nand_12_out, nand_13_out, nand_14_out, nand_15_out, nand_16_out, nand_17_out, nand_18_out,
       nand_19_out, nand_20_out, nand_21_out, nand_22_out, nand_23_out, nand_24_out, nand_25_out,
       nand_26_out, nand_27_out, nand_28_out, nand_29_out, nand_30_out, nand_31_out, nand_32_out,
       nand_33_out, nand_34_out, nand_35_out, nand_36_out, nand_37_out, nand_38_out, nand_39_out,
       nand_40_out, nand_41_out, nand_42_out, nand_43_out, nand_44_out, nand_45_out, nand_46_out,
       nand_47_out, nand_48_out, nand_49_out, nand_50_out, nand_51_out, nand_52_out, nand_53_out,
       nand_54_out, nand_55_out, nand_56_out, nand_57_out, nand_58_out, nand_59_out, nand_60_out,
       nand_61_out, nand_62_out, nand_63_out, nand_64_out, or_1_out, or_2_out, or_3_out, or_4_out, or_5_out,
       or_6_out, or_7_out, or_8_out, or_9_out, or_10_out, or_11_out, or_12_out, or_13_out, or_14_out,
       or_15_out, or_16_out, or_17_out, or_18_out, or_19_out, or_20_out, or_21_out, or_22_out, or_23_out,
       or_24_out, or_25_out, or_26_out, or_27_out, or_28_out, or_29_out, or_30_out, or_33_out, or_34_out,
       or_35_out, or_36_out, or_37_out, or_38_out, or_39_out, or_40_out, or_41_out, or_42_out, or_43_out,
       or_44_out, or_45_out, or_46_out, or_47_out, or_48_out, or_49_out, or_50_out, or_51_out, or_52_out,
       or_53_out, or_54_out, or_55_out, or_56_out, or_57_out, or_58_out, or_59_out, or_60_out, or_61_out,
       or_62_out, or_65_out, or_66_out, or_67_out, or_68_out, or_69_out, or_70_out, or_71_out, or_72_out,
       or_73_out, or_74_out, or_75_out, or_76_out, or_77_out, or_78_out, or_79_out, or_80_out, or_81_out,
       or_82_out, or_83_out, or_84_out, or_85_out, or_86_out, or_87_out, or_88_out, or_89_out, or_90_out,
       or_91_out, or_92_out, or_93_out, or_94_out, or_97_out, or_98_out, or_99_out, or_100_out, or_101_out,
       or_102_out, or_103_out, or_104_out, or_105_out, or_106_out, or_107_out, or_108_out, or_109_out,
       or_110_out, or_111_out, or_112_out, or_113_out, or_114_out, or_115_out, or_116_out, or_117_out,
       or_118_out, or_119_out, or_120_out, or_121_out, or_122_out, or_123_out, or_124_out, or_125_out,
       or_126_out, undriven, undriven_2, undriven_3, undriven_4, undriven_5, undriven_6, undriven_7,
       undriven_8, undriven_9, undriven_10, undriven_11, undriven_12, undriven_13, undriven_14, undriven_15,
       undriven_16, undriven_17, undriven_18, undriven_19, undriven_20, undriven_21, undriven_22,
       undriven_23, undriven_24, undriven_25, undriven_26, undriven_27, undriven_28, undriven_29,
       undriven_30, undriven_31, undriven_32, undriven_33, undriven_34, undriven_35, undriven_36,
       undriven_37, undriven_38, undriven_39, undriven_40, undriven_41, undriven_42, undriven_43,
       undriven_44, undriven_45, undriven_46, undriven_47, undriven_48, undriven_49, undriven_50,
       undriven_51, undriven_52, undriven_53, undriven_54, undriven_55, undriven_56, undriven_57,
       undriven_58, undriven_59, undriven_60, undriven_61, undriven_62, undriven_63, undriven_64,
       undriven_65, undriven_66, undriven_67, undriven_68, undriven_69, undriven_70, undriven_71,
       undriven_72, undriven_73, undriven_74, undriven_75, undriven_76, undriven_77, undriven_78,
       undriven_79, undriven_80, undriven_81, undriven_82, undriven_83, undriven_84, undriven_85,
       undriven_86, undriven_87, undriven_88, undriven_89, undriven_90, undriven_91, undriven_92,
       undriven_93, undriven_94, undriven_95, undriven_96, undriven_97, undriven_98, undriven_99,
       undriven_100, undriven_101, undriven_102, undriven_103, undriven_104, undriven_105, undriven_106,
       undriven_107, undriven_108, undriven_109, undriven_110, undriven_111, undriven_112, undriven_113,
       undriven_114, undriven_115, undriven_116, undriven_117, undriven_118, undriven_119, undriven_120,
       undriven_121, undriven_122, undriven_123, undriven_124, undriven_125, undriven_126, undriven_127,
       undriven_128;

  and and_1 (and_1_out, ~in_1, ~in_2);  // AND_Gate
  and and_2 (and_2_out, in_1, ~in_2);  // AND_Gate
  and and_3 (and_3_out, ~in_1, in_2);  // AND_Gate
  and and_4 (and_4_out, in_1, in_2);
  and and_5 (and_5_out, ~in_3, ~in_4);  // AND_Gate
  and and_6 (and_6_out, in_3, ~in_4);  // AND_Gate
  and and_7 (and_7_out, ~in_3, in_4);  // AND_Gate
  and and_8 (and_8_out, in_3, in_4);
  and and_9 (and_9_out, ~in_1, ~in_2);  // AND_Gate
  and and_10 (and_10_out, in_1, ~in_2);  // AND_Gate
  and and_11 (and_11_out, ~in_1, in_2);  // AND_Gate
  and and_12 (and_12_out, in_1, in_2);
  and and_13 (and_13_out, ~in_1, ~in_2);  // AND_Gate
  and and_14 (and_14_out, in_1, ~in_2);  // AND_Gate
  and and_15 (and_15_out, ~in_1, in_2);  // AND_Gate
  and and_16 (and_16_out, in_1, in_2);
  and and_17 (and_17_out, ~in_1, ~in_2);  // AND_Gate
  and and_18 (and_18_out, in_1, ~in_2);  // AND_Gate
  and and_19 (and_19_out, ~in_1, in_2);  // AND_Gate
  and and_20 (and_20_out, in_1, in_2);
  and and_21 (and_21_out, and_1_out, and_25_out);
  and and_22 (and_22_out, and_25_out, and_2_out);
  and and_23 (and_23_out, and_3_out, and_25_out);
  and and_24 (and_24_out, and_25_out, and_4_out);
  and and_25 (and_25_out, and_5_out, in_24);
  and and_26 (and_26_out, in_24, and_6_out);
  and and_27 (and_27_out, and_7_out, in_24);
  and and_28 (and_28_out, in_24, and_8_out);
  and and_29 (and_29_out, and_9_out, and_26_out);
  and and_30 (and_30_out, and_26_out, and_10_out);
  and and_31 (and_31_out, and_11_out, and_26_out);
  and and_32 (and_32_out, and_26_out, and_12_out);
  and and_33 (and_33_out, and_13_out, and_27_out);
  and and_34 (and_34_out, and_27_out, and_14_out);
  and and_35 (and_35_out, and_15_out, and_27_out);
  and and_36 (and_36_out, and_27_out, and_16_out);
  and and_37 (and_37_out, and_17_out, and_28_out);
  and and_38 (and_38_out, and_28_out, and_18_out);
  and and_39 (and_39_out, and_19_out, and_28_out);
  and and_40 (and_40_out, and_28_out, and_20_out);
  nand nand_1 (nand_1_out, in_22, and_21_out);
  nand nand_2 (nand_2_out, and_21_out, in_23);
  nand nand_3 (nand_3_out, in_22, and_22_out);
  nand nand_4 (nand_4_out, and_22_out, in_23);
  nand nand_5 (nand_5_out, in_22, and_23_out);
  nand nand_6 (nand_6_out, and_23_out, in_23);
  nand nand_7 (nand_7_out, in_22, and_24_out);
  nand nand_8 (nand_8_out, and_24_out, in_23);
  nand nand_9 (nand_9_out, in_22, and_29_out);
  nand nand_10 (nand_10_out, and_29_out, in_23);
  nand nand_11 (nand_11_out, in_22, and_30_out);
  nand nand_12 (nand_12_out, and_30_out, in_23);
  nand nand_13 (nand_13_out, in_22, and_31_out);
  nand nand_14 (nand_14_out, and_31_out, in_23);
  nand nand_15 (nand_15_out, in_22, and_32_out);
  nand nand_16 (nand_16_out, and_32_out, in_23);
  nand nand_17 (nand_17_out, in_22, and_33_out);
  nand nand_18 (nand_18_out, and_33_out, in_23);
  nand nand_19 (nand_19_out, in_22, and_34_out);
  nand nand_20 (nand_20_out, and_34_out, in_23);
  nand nand_21 (nand_21_out, in_22, and_35_out);
  nand nand_22 (nand_22_out, and_35_out, in_23);
  nand nand_23 (nand_23_out, in_22, and_36_out);
  nand nand_24 (nand_24_out, and_36_out, in_23);
  nand nand_25 (nand_25_out, in_22, and_37_out);
  nand nand_26 (nand_26_out, and_37_out, in_23);
  nand nand_27 (nand_27_out, in_22, and_38_out);
  nand nand_28 (nand_28_out, and_38_out, in_23);
  nand nand_29 (nand_29_out, in_22, and_39_out);
  nand nand_30 (nand_30_out, and_39_out, in_23);
  nand nand_31 (nand_31_out, in_22, and_40_out);
  nand nand_32 (nand_32_out, and_40_out, in_23);
  nand nand_33 (nand_33_out, nand_1_out, nand_1_out);
  nand nand_34 (nand_34_out, nand_2_out, nand_2_out);
  nand nand_35 (nand_35_out, nand_3_out, nand_3_out);
  nand nand_36 (nand_36_out, nand_4_out, nand_4_out);
  nand nand_37 (nand_37_out, nand_5_out, nand_5_out);
  nand nand_38 (nand_38_out, nand_6_out, nand_6_out);
  nand nand_39 (nand_39_out, nand_7_out, nand_7_out);
  nand nand_40 (nand_40_out, nand_8_out, nand_8_out);
  nand nand_41 (nand_41_out, nand_9_out, nand_9_out);
  nand nand_42 (nand_42_out, nand_10_out, nand_10_out);
  nand nand_43 (nand_43_out, nand_11_out, nand_11_out);
  nand nand_44 (nand_44_out, nand_12_out, nand_12_out);
  nand nand_45 (nand_45_out, nand_13_out, nand_13_out);
  nand nand_46 (nand_46_out, nand_14_out, nand_14_out);
  nand nand_47 (nand_47_out, nand_15_out, nand_15_out);
  nand nand_48 (nand_48_out, nand_16_out, nand_16_out);
  nand nand_49 (nand_49_out, nand_17_out, nand_17_out);
  nand nand_50 (nand_50_out, nand_18_out, nand_18_out);
  nand nand_51 (nand_51_out, nand_19_out, nand_19_out);
  nand nand_52 (nand_52_out, nand_20_out, nand_20_out);
  nand nand_53 (nand_53_out, nand_21_out, nand_21_out);
  nand nand_54 (nand_54_out, nand_22_out, nand_22_out);
  nand nand_55 (nand_55_out, nand_23_out, nand_23_out);
  nand nand_56 (nand_56_out, nand_24_out, nand_24_out);
  nand nand_57 (nand_57_out, nand_25_out, nand_25_out);
  nand nand_58 (nand_58_out, nand_26_out, nand_26_out);
  nand nand_59 (nand_59_out, nand_27_out, nand_27_out);
  nand nand_60 (nand_60_out, nand_28_out, nand_28_out);
  nand nand_61 (nand_61_out, nand_29_out, nand_29_out);
  nand nand_62 (nand_62_out, nand_30_out, nand_30_out);
  nand nand_63 (nand_63_out, nand_31_out, nand_31_out);
  nand nand_64 (nand_64_out, nand_32_out, nand_32_out);
  D_Flip_Flop d_ff_1 (
    .clk(in_21), .D(in_5), .Q(d_ff_1_q), .Qn(d_ff_1_qn), .en(nand_33_out), .reset(undriven_8));  // open: preset
  D_Flip_Flop d_ff_2 (
    .clk(in_21), .D(in_5), .Q(d_ff_2_q), .Qn(d_ff_2_qn), .en(nand_35_out), .reset(undriven_9));  // open: preset
  D_Flip_Flop d_ff_3 (
    .clk(in_21), .D(in_5), .Q(d_ff_3_q), .Qn(d_ff_3_qn), .en(nand_37_out), .reset(undriven_10));  // open: preset
  D_Flip_Flop d_ff_4 (
    .clk(in_21), .D(in_5), .Q(d_ff_4_q), .Qn(d_ff_4_qn), .en(nand_39_out), .reset(undriven));  // open: preset
  D_Flip_Flop d_ff_5 (
    .clk(in_21), .D(in_5), .Q(d_ff_5_q), .Qn(d_ff_5_qn), .en(nand_41_out), .reset(undriven_2));  // open: preset
  D_Flip_Flop d_ff_6 (
    .clk(in_21), .D(in_5), .Q(d_ff_6_q), .Qn(d_ff_6_qn), .en(nand_43_out), .reset(undriven_11));  // open: preset
  D_Flip_Flop d_ff_7 (
    .clk(in_21), .D(in_5), .Q(d_ff_7_q), .Qn(d_ff_7_qn), .en(nand_45_out), .reset(undriven_3));  // open: preset
  D_Flip_Flop d_ff_8 (
    .clk(in_21), .D(in_5), .Q(d_ff_8_q), .Qn(d_ff_8_qn), .en(nand_47_out), .reset(undriven_12));  // open: preset
  D_Flip_Flop d_ff_9 (
    .clk(in_21), .D(in_5), .Q(d_ff_9_q), .Qn(d_ff_9_qn), .en(nand_49_out), .reset(undriven_4));  // open: preset
  D_Flip_Flop d_ff_10 (
    .clk(in_21), .D(in_5), .Q(d_ff_10_q), .Qn(d_ff_10_qn), .en(nand_51_out), .reset(undriven_5));  // open: preset
  D_Flip_Flop d_ff_11 (
    .clk(in_21), .D(in_5), .Q(d_ff_11_q), .Qn(d_ff_11_qn), .en(nand_53_out), .reset(undriven_6));  // open: preset
  D_Flip_Flop d_ff_12 (
    .clk(in_21), .D(in_5), .Q(d_ff_12_q), .Qn(d_ff_12_qn), .en(nand_55_out), .reset(undriven_13));  // open: preset
  D_Flip_Flop d_ff_13 (
    .clk(in_21), .D(in_5), .Q(d_ff_13_q), .Qn(d_ff_13_qn), .en(nand_57_out), .reset(undriven_14));  // open: preset
  D_Flip_Flop d_ff_14 (
    .clk(in_21), .D(in_5), .Q(d_ff_14_q), .Qn(d_ff_14_qn), .en(nand_59_out), .reset(undriven_15));  // open: preset
  D_Flip_Flop d_ff_15 (
    .clk(in_21), .D(in_5), .Q(d_ff_15_q), .Qn(d_ff_15_qn), .en(nand_61_out), .reset(undriven_16));  // open: preset
  D_Flip_Flop d_ff_16 (
    .clk(in_21), .D(in_5), .Q(d_ff_16_q), .Qn(d_ff_16_qn), .en(nand_63_out), .reset(undriven_7));  // open: preset
  D_Flip_Flop d_ff_17 (
    .clk(in_21), .D(in_6), .Q(d_ff_17_q), .Qn(d_ff_17_qn), .en(nand_33_out), .reset(undriven_25));  // open: preset
  D_Flip_Flop d_ff_18 (
    .clk(in_21), .D(in_6), .Q(d_ff_18_q), .Qn(d_ff_18_qn), .en(nand_35_out), .reset(undriven_17));  // open: preset
  D_Flip_Flop d_ff_19 (
    .clk(in_21), .D(in_6), .Q(d_ff_19_q), .Qn(d_ff_19_qn), .en(nand_37_out), .reset(undriven_18));  // open: preset
  D_Flip_Flop d_ff_20 (
    .clk(in_21), .D(in_6), .Q(d_ff_20_q), .Qn(d_ff_20_qn), .en(nand_39_out), .reset(undriven_26));  // open: preset
  D_Flip_Flop d_ff_21 (
    .clk(in_21), .D(in_6), .Q(d_ff_21_q), .Qn(d_ff_21_qn), .en(nand_41_out), .reset(undriven_27));  // open: preset
  D_Flip_Flop d_ff_22 (
    .clk(in_21), .D(in_6), .Q(d_ff_22_q), .Qn(d_ff_22_qn), .en(nand_43_out), .reset(undriven_19));  // open: preset
  D_Flip_Flop d_ff_23 (
    .clk(in_21), .D(in_6), .Q(d_ff_23_q), .Qn(d_ff_23_qn), .en(nand_45_out), .reset(undriven_28));  // open: preset
  D_Flip_Flop d_ff_24 (
    .clk(in_21), .D(in_6), .Q(d_ff_24_q), .Qn(d_ff_24_qn), .en(nand_47_out), .reset(undriven_20));  // open: preset
  D_Flip_Flop d_ff_25 (
    .clk(in_21), .D(in_6), .Q(d_ff_25_q), .Qn(d_ff_25_qn), .en(nand_49_out), .reset(undriven_21));  // open: preset
  D_Flip_Flop d_ff_26 (
    .clk(in_21), .D(in_6), .Q(d_ff_26_q), .Qn(d_ff_26_qn), .en(nand_51_out), .reset(undriven_29));  // open: preset
  D_Flip_Flop d_ff_27 (
    .clk(in_21), .D(in_6), .Q(d_ff_27_q), .Qn(d_ff_27_qn), .en(nand_53_out), .reset(undriven_22));  // open: preset
  D_Flip_Flop d_ff_28 (
    .clk(in_21), .D(in_6), .Q(d_ff_28_q), .Qn(d_ff_28_qn), .en(nand_55_out), .reset(undriven_30));  // open: preset
  D_Flip_Flop d_ff_29 (
    .clk(in_21), .D(in_6), .Q(d_ff_29_q), .Qn(d_ff_29_qn), .en(nand_57_out), .reset(undriven_31));  // open: preset
  D_Flip_Flop d_ff_30 (
    .clk(in_21), .D(in_6), .Q(d_ff_30_q), .Qn(d_ff_30_qn), .en(nand_59_out), .reset(undriven_23));  // open: preset
  D_Flip_Flop d_ff_31 (
    .clk(in_21), .D(in_6), .Q(d_ff_31_q), .Qn(d_ff_31_qn), .en(nand_61_out), .reset(undriven_24));  // open: preset
  D_Flip_Flop d_ff_32 (
    .clk(in_21), .D(in_6), .Q(d_ff_32_q), .Qn(d_ff_32_qn), .en(nand_63_out), .reset(undriven_32));  // open: preset
  D_Flip_Flop d_ff_33 (
    .clk(in_21), .D(in_7), .Q(d_ff_33_q), .Qn(d_ff_33_qn), .en(nand_33_out), .reset(undriven_33));  // open: preset
  D_Flip_Flop d_ff_34 (
    .clk(in_21), .D(in_7), .Q(d_ff_34_q), .Qn(d_ff_34_qn), .en(nand_35_out), .reset(undriven_42));  // open: preset
  D_Flip_Flop d_ff_35 (
    .clk(in_21), .D(in_7), .Q(d_ff_35_q), .Qn(d_ff_35_qn), .en(nand_37_out), .reset(undriven_34));  // open: preset
  D_Flip_Flop d_ff_36 (
    .clk(in_21), .D(in_7), .Q(d_ff_36_q), .Qn(d_ff_36_qn), .en(nand_39_out), .reset(undriven_35));  // open: preset
  D_Flip_Flop d_ff_37 (
    .clk(in_21), .D(in_7), .Q(d_ff_37_q), .Qn(d_ff_37_qn), .en(nand_41_out), .reset(undriven_43));  // open: preset
  D_Flip_Flop d_ff_38 (
    .clk(in_21), .D(in_7), .Q(d_ff_38_q), .Qn(d_ff_38_qn), .en(nand_43_out), .reset(undriven_36));  // open: preset
  D_Flip_Flop d_ff_39 (
    .clk(in_21), .D(in_7), .Q(d_ff_39_q), .Qn(d_ff_39_qn), .en(nand_45_out), .reset(undriven_37));  // open: preset
  D_Flip_Flop d_ff_40 (
    .clk(in_21), .D(in_7), .Q(d_ff_40_q), .Qn(d_ff_40_qn), .en(nand_47_out), .reset(undriven_44));  // open: preset
  D_Flip_Flop d_ff_41 (
    .clk(in_21), .D(in_7), .Q(d_ff_41_q), .Qn(d_ff_41_qn), .en(nand_49_out), .reset(undriven_45));  // open: preset
  D_Flip_Flop d_ff_42 (
    .clk(in_21), .D(in_7), .Q(d_ff_42_q), .Qn(d_ff_42_qn), .en(nand_51_out), .reset(undriven_38));  // open: preset
  D_Flip_Flop d_ff_43 (
    .clk(in_21), .D(in_7), .Q(d_ff_43_q), .Qn(d_ff_43_qn), .en(nand_53_out), .reset(undriven_46));  // open: preset
  D_Flip_Flop d_ff_44 (
    .clk(in_21), .D(in_7), .Q(d_ff_44_q), .Qn(d_ff_44_qn), .en(nand_55_out), .reset(undriven_47));  // open: preset
  D_Flip_Flop d_ff_45 (
    .clk(in_21), .D(in_7), .Q(d_ff_45_q), .Qn(d_ff_45_qn), .en(nand_57_out), .reset(undriven_39));  // open: preset
  D_Flip_Flop d_ff_46 (
    .clk(in_21), .D(in_7), .Q(d_ff_46_q), .Qn(d_ff_46_qn), .en(nand_59_out), .reset(undriven_48));  // open: preset
  D_Flip_Flop d_ff_47 (
    .clk(in_21), .D(in_7), .Q(d_ff_47_q), .Qn(d_ff_47_qn), .en(nand_61_out), .reset(undriven_40));  // open: preset
  D_Flip_Flop d_ff_48 (
    .clk(in_21), .D(in_7), .Q(d_ff_48_q), .Qn(d_ff_48_qn), .en(nand_63_out), .reset(undriven_41));  // open: preset
  D_Flip_Flop d_ff_49 (
    .clk(in_21), .D(in_8), .Q(d_ff_49_q), .Qn(d_ff_49_qn), .en(nand_33_out), .reset(undriven_58));  // open: preset
  D_Flip_Flop d_ff_50 (
    .clk(in_21), .D(in_8), .Q(d_ff_50_q), .Qn(d_ff_50_qn), .en(nand_35_out), .reset(undriven_49));  // open: preset
  D_Flip_Flop d_ff_51 (
    .clk(in_21), .D(in_8), .Q(d_ff_51_q), .Qn(d_ff_51_qn), .en(nand_37_out), .reset(undriven_59));  // open: preset
  D_Flip_Flop d_ff_52 (
    .clk(in_21), .D(in_8), .Q(d_ff_52_q), .Qn(d_ff_52_qn), .en(nand_39_out), .reset(undriven_50));  // open: preset
  D_Flip_Flop d_ff_53 (
    .clk(in_21), .D(in_8), .Q(d_ff_53_q), .Qn(d_ff_53_qn), .en(nand_41_out), .reset(undriven_51));  // open: preset
  D_Flip_Flop d_ff_54 (
    .clk(in_21), .D(in_8), .Q(d_ff_54_q), .Qn(d_ff_54_qn), .en(nand_43_out), .reset(undriven_52));  // open: preset
  D_Flip_Flop d_ff_55 (
    .clk(in_21), .D(in_8), .Q(d_ff_55_q), .Qn(d_ff_55_qn), .en(nand_45_out), .reset(undriven_60));  // open: preset
  D_Flip_Flop d_ff_56 (
    .clk(in_21), .D(in_8), .Q(d_ff_56_q), .Qn(d_ff_56_qn), .en(nand_47_out), .reset(undriven_53));  // open: preset
  D_Flip_Flop d_ff_57 (
    .clk(in_21), .D(in_8), .Q(d_ff_57_q), .Qn(d_ff_57_qn), .en(nand_49_out), .reset(undriven_54));  // open: preset
  D_Flip_Flop d_ff_58 (
    .clk(in_21), .D(in_8), .Q(d_ff_58_q), .Qn(d_ff_58_qn), .en(nand_51_out), .reset(undriven_61));  // open: preset
  D_Flip_Flop d_ff_59 (
    .clk(in_21), .D(in_8), .Q(d_ff_59_q), .Qn(d_ff_59_qn), .en(nand_53_out), .reset(undriven_55));  // open: preset
  D_Flip_Flop d_ff_60 (
    .clk(in_21), .D(in_8), .Q(d_ff_60_q), .Qn(d_ff_60_qn), .en(nand_55_out), .reset(undriven_62));  // open: preset
  D_Flip_Flop d_ff_61 (
    .clk(in_21), .D(in_8), .Q(d_ff_61_q), .Qn(d_ff_61_qn), .en(nand_57_out), .reset(undriven_63));  // open: preset
  D_Flip_Flop d_ff_62 (
    .clk(in_21), .D(in_8), .Q(d_ff_62_q), .Qn(d_ff_62_qn), .en(nand_59_out), .reset(undriven_56));  // open: preset
  D_Flip_Flop d_ff_63 (
    .clk(in_21), .D(in_8), .Q(d_ff_63_q), .Qn(d_ff_63_qn), .en(nand_61_out), .reset(undriven_64));  // open: preset
  D_Flip_Flop d_ff_64 (
    .clk(in_21), .D(in_8), .Q(d_ff_64_q), .Qn(d_ff_64_qn), .en(nand_63_out), .reset(undriven_57));  // open: preset
  D_Flip_Flop d_ff_65 (
    .clk(in_21), .D(in_9), .Q(d_ff_65_q), .Qn(d_ff_65_qn), .en(nand_33_out), .reset(undriven_65));  // open: preset
  D_Flip_Flop d_ff_66 (
    .clk(in_21), .D(in_9), .Q(d_ff_66_q), .Qn(d_ff_66_qn), .en(nand_35_out), .reset(undriven_73));  // open: preset
  D_Flip_Flop d_ff_67 (
    .clk(in_21), .D(in_9), .Q(d_ff_67_q), .Qn(d_ff_67_qn), .en(nand_37_out), .reset(undriven_74));  // open: preset
  D_Flip_Flop d_ff_68 (
    .clk(in_21), .D(in_9), .Q(d_ff_68_q), .Qn(d_ff_68_qn), .en(nand_39_out), .reset(undriven_66));  // open: preset
  D_Flip_Flop d_ff_69 (
    .clk(in_21), .D(in_9), .Q(d_ff_69_q), .Qn(d_ff_69_qn), .en(nand_41_out), .reset(undriven_75));  // open: preset
  D_Flip_Flop d_ff_70 (
    .clk(in_21), .D(in_9), .Q(d_ff_70_q), .Qn(d_ff_70_qn), .en(nand_43_out), .reset(undriven_67));  // open: preset
  D_Flip_Flop d_ff_71 (
    .clk(in_21), .D(in_9), .Q(d_ff_71_q), .Qn(d_ff_71_qn), .en(nand_45_out), .reset(undriven_68));  // open: preset
  D_Flip_Flop d_ff_72 (
    .clk(in_21), .D(in_9), .Q(d_ff_72_q), .Qn(d_ff_72_qn), .en(nand_47_out), .reset(undriven_69));  // open: preset
  D_Flip_Flop d_ff_73 (
    .clk(in_21), .D(in_9), .Q(d_ff_73_q), .Qn(d_ff_73_qn), .en(nand_49_out), .reset(undriven_76));  // open: preset
  D_Flip_Flop d_ff_74 (
    .clk(in_21), .D(in_9), .Q(d_ff_74_q), .Qn(d_ff_74_qn), .en(nand_51_out), .reset(undriven_77));  // open: preset
  D_Flip_Flop d_ff_75 (
    .clk(in_21), .D(in_9), .Q(d_ff_75_q), .Qn(d_ff_75_qn), .en(nand_53_out), .reset(undriven_78));  // open: preset
  D_Flip_Flop d_ff_76 (
    .clk(in_21), .D(in_9), .Q(d_ff_76_q), .Qn(d_ff_76_qn), .en(nand_55_out), .reset(undriven_70));  // open: preset
  D_Flip_Flop d_ff_77 (
    .clk(in_21), .D(in_9), .Q(d_ff_77_q), .Qn(d_ff_77_qn), .en(nand_57_out), .reset(undriven_71));  // open: preset
  D_Flip_Flop d_ff_78 (
    .clk(in_21), .D(in_9), .Q(d_ff_78_q), .Qn(d_ff_78_qn), .en(nand_59_out), .reset(undriven_79));  // open: preset
  D_Flip_Flop d_ff_79 (
    .clk(in_21), .D(in_9), .Q(d_ff_79_q), .Qn(d_ff_79_qn), .en(nand_61_out), .reset(undriven_72));  // open: preset
  D_Flip_Flop d_ff_80 (
    .clk(in_21), .D(in_9), .Q(d_ff_80_q), .Qn(d_ff_80_qn), .en(nand_63_out), .reset(undriven_80));  // open: preset
  D_Flip_Flop d_ff_81 (
    .clk(in_21), .D(in_10), .Q(d_ff_81_q), .Qn(d_ff_81_qn), .en(nand_33_out), .reset(undriven_89));  // open: preset
  D_Flip_Flop d_ff_82 (
    .clk(in_21), .D(in_10), .Q(d_ff_82_q), .Qn(d_ff_82_qn), .en(nand_35_out), .reset(undriven_81));  // open: preset
  D_Flip_Flop d_ff_83 (
    .clk(in_21), .D(in_10), .Q(d_ff_83_q), .Qn(d_ff_83_qn), .en(nand_37_out), .reset(undriven_82));  // open: preset
  D_Flip_Flop d_ff_84 (
    .clk(in_21), .D(in_10), .Q(d_ff_84_q), .Qn(d_ff_84_qn), .en(nand_39_out), .reset(undriven_90));  // open: preset
  D_Flip_Flop d_ff_85 (
    .clk(in_21), .D(in_10), .Q(d_ff_85_q), .Qn(d_ff_85_qn), .en(nand_41_out), .reset(undriven_83));  // open: preset
  D_Flip_Flop d_ff_86 (
    .clk(in_21), .D(in_10), .Q(d_ff_86_q), .Qn(d_ff_86_qn), .en(nand_43_out), .reset(undriven_91));  // open: preset
  D_Flip_Flop d_ff_87 (
    .clk(in_21), .D(in_10), .Q(d_ff_87_q), .Qn(d_ff_87_qn), .en(nand_45_out), .reset(undriven_84));  // open: preset
  D_Flip_Flop d_ff_88 (
    .clk(in_21), .D(in_10), .Q(d_ff_88_q), .Qn(d_ff_88_qn), .en(nand_47_out), .reset(undriven_85));  // open: preset
  D_Flip_Flop d_ff_89 (
    .clk(in_21), .D(in_10), .Q(d_ff_89_q), .Qn(d_ff_89_qn), .en(nand_49_out), .reset(undriven_92));  // open: preset
  D_Flip_Flop d_ff_90 (
    .clk(in_21), .D(in_10), .Q(d_ff_90_q), .Qn(d_ff_90_qn), .en(nand_51_out), .reset(undriven_86));  // open: preset
  D_Flip_Flop d_ff_91 (
    .clk(in_21), .D(in_10), .Q(d_ff_91_q), .Qn(d_ff_91_qn), .en(nand_53_out), .reset(undriven_93));  // open: preset
  D_Flip_Flop d_ff_92 (
    .clk(in_21), .D(in_10), .Q(d_ff_92_q), .Qn(d_ff_92_qn), .en(nand_55_out), .reset(undriven_94));  // open: preset
  D_Flip_Flop d_ff_93 (
    .clk(in_21), .D(in_10), .Q(d_ff_93_q), .Qn(d_ff_93_qn), .en(nand_57_out), .reset(undriven_87));  // open: preset
  D_Flip_Flop d_ff_94 (
    .clk(in_21), .D(in_10), .Q(d_ff_94_q), .Qn(d_ff_94_qn), .en(nand_59_out), .reset(undriven_88));  // open: preset
  D_Flip_Flop d_ff_95 (
    .clk(in_21), .D(in_10), .Q(d_ff_95_q), .Qn(d_ff_95_qn), .en(nand_61_out), .reset(undriven_95));  // open: preset
  D_Flip_Flop d_ff_96 (
    .clk(in_21), .D(in_10), .Q(d_ff_96_q), .Qn(d_ff_96_qn), .en(nand_63_out), .reset(undriven_96));  // open: preset
  D_Flip_Flop d_ff_97 (
    .clk(in_21), .D(in_11), .Q(d_ff_97_q), .Qn(d_ff_97_qn), .en(nand_33_out), .reset(undriven_105));  // open: preset
  D_Flip_Flop d_ff_98 (
    .clk(in_21), .D(in_11), .Q(d_ff_98_q), .Qn(d_ff_98_qn), .en(nand_35_out), .reset(undriven_106));  // open: preset
  D_Flip_Flop d_ff_99 (
    .clk(in_21), .D(in_11), .Q(d_ff_99_q), .Qn(d_ff_99_qn), .en(nand_37_out), .reset(undriven_97));  // open: preset
  D_Flip_Flop d_ff_100 (
    .clk(in_21), .D(in_11), .Q(d_ff_100_q), .Qn(d_ff_100_qn), .en(nand_39_out), .reset(undriven_98));  // open: preset
  D_Flip_Flop d_ff_101 (
    .clk(in_21), .D(in_11), .Q(d_ff_101_q), .Qn(d_ff_101_qn), .en(nand_41_out), .reset(undriven_107));  // open: preset
  D_Flip_Flop d_ff_102 (
    .clk(in_21), .D(in_11), .Q(d_ff_102_q), .Qn(d_ff_102_qn), .en(nand_43_out), .reset(undriven_99));  // open: preset
  D_Flip_Flop d_ff_103 (
    .clk(in_21), .D(in_11), .Q(d_ff_103_q), .Qn(d_ff_103_qn), .en(nand_45_out), .reset(undriven_100));  // open: preset
  D_Flip_Flop d_ff_104 (
    .clk(in_21), .D(in_11), .Q(d_ff_104_q), .Qn(d_ff_104_qn), .en(nand_47_out), .reset(undriven_108));  // open: preset
  D_Flip_Flop d_ff_105 (
    .clk(in_21), .D(in_11), .Q(d_ff_105_q), .Qn(d_ff_105_qn), .en(nand_49_out), .reset(undriven_101));  // open: preset
  D_Flip_Flop d_ff_106 (
    .clk(in_21), .D(in_11), .Q(d_ff_106_q), .Qn(d_ff_106_qn), .en(nand_51_out), .reset(undriven_102));  // open: preset
  D_Flip_Flop d_ff_107 (
    .clk(in_21), .D(in_11), .Q(d_ff_107_q), .Qn(d_ff_107_qn), .en(nand_53_out), .reset(undriven_109));  // open: preset
  D_Flip_Flop d_ff_108 (
    .clk(in_21), .D(in_11), .Q(d_ff_108_q), .Qn(d_ff_108_qn), .en(nand_55_out), .reset(undriven_103));  // open: preset
  D_Flip_Flop d_ff_109 (
    .clk(in_21), .D(in_11), .Q(d_ff_109_q), .Qn(d_ff_109_qn), .en(nand_57_out), .reset(undriven_110));  // open: preset
  D_Flip_Flop d_ff_110 (
    .clk(in_21), .D(in_11), .Q(d_ff_110_q), .Qn(d_ff_110_qn), .en(nand_59_out), .reset(undriven_111));  // open: preset
  D_Flip_Flop d_ff_111 (
    .clk(in_21), .D(in_11), .Q(d_ff_111_q), .Qn(d_ff_111_qn), .en(nand_61_out), .reset(undriven_112));  // open: preset
  D_Flip_Flop d_ff_112 (
    .clk(in_21), .D(in_11), .Q(d_ff_112_q), .Qn(d_ff_112_qn), .en(nand_63_out), .reset(undriven_104));  // open: preset
  D_Flip_Flop d_ff_113 (
    .clk(in_21), .D(in_12), .Q(d_ff_113_q), .Qn(d_ff_113_qn), .en(nand_33_out), .reset(undriven_113));  // open: preset
  D_Flip_Flop d_ff_114 (
    .clk(in_21), .D(in_12), .Q(d_ff_114_q), .Qn(d_ff_114_qn), .en(nand_35_out), .reset(undriven_114));  // open: preset
  D_Flip_Flop d_ff_115 (
    .clk(in_21), .D(in_12), .Q(d_ff_115_q), .Qn(d_ff_115_qn), .en(nand_37_out), .reset(undriven_123));  // open: preset
  D_Flip_Flop d_ff_116 (
    .clk(in_21), .D(in_12), .Q(d_ff_116_q), .Qn(d_ff_116_qn), .en(nand_39_out), .reset(undriven_115));  // open: preset
  D_Flip_Flop d_ff_117 (
    .clk(in_21), .D(in_12), .Q(d_ff_117_q), .Qn(d_ff_117_qn), .en(nand_41_out), .reset(undriven_124));  // open: preset
  D_Flip_Flop d_ff_118 (
    .clk(in_21), .D(in_12), .Q(d_ff_118_q), .Qn(d_ff_118_qn), .en(nand_43_out), .reset(undriven_125));  // open: preset
  D_Flip_Flop d_ff_119 (
    .clk(in_21), .D(in_12), .Q(d_ff_119_q), .Qn(d_ff_119_qn), .en(nand_45_out), .reset(undriven_116));  // open: preset
  D_Flip_Flop d_ff_120 (
    .clk(in_21), .D(in_12), .Q(d_ff_120_q), .Qn(d_ff_120_qn), .en(nand_47_out), .reset(undriven_117));  // open: preset
  D_Flip_Flop d_ff_121 (
    .clk(in_21), .D(in_12), .Q(d_ff_121_q), .Qn(d_ff_121_qn), .en(nand_49_out), .reset(undriven_126));  // open: preset
  D_Flip_Flop d_ff_122 (
    .clk(in_21), .D(in_12), .Q(d_ff_122_q), .Qn(d_ff_122_qn), .en(nand_51_out), .reset(undriven_118));  // open: preset
  D_Flip_Flop d_ff_123 (
    .clk(in_21), .D(in_12), .Q(d_ff_123_q), .Qn(d_ff_123_qn), .en(nand_53_out), .reset(undriven_119));  // open: preset
  D_Flip_Flop d_ff_124 (
    .clk(in_21), .D(in_12), .Q(d_ff_124_q), .Qn(d_ff_124_qn), .en(nand_55_out), .reset(undriven_127));  // open: preset
  D_Flip_Flop d_ff_125 (
    .clk(in_21), .D(in_12), .Q(d_ff_125_q), .Qn(d_ff_125_qn), .en(nand_57_out), .reset(undriven_120));  // open: preset
  D_Flip_Flop d_ff_126 (
    .clk(in_21), .D(in_12), .Q(d_ff_126_q), .Qn(d_ff_126_qn), .en(nand_59_out), .reset(undriven_128));  // open: preset
  D_Flip_Flop d_ff_127 (
    .clk(in_21), .D(in_12), .Q(d_ff_127_q), .Qn(d_ff_127_qn), .en(nand_61_out), .reset(undriven_121));  // open: preset
  D_Flip_Flop d_ff_128 (
    .clk(in_21), .D(in_12), .Q(d_ff_128_q), .Qn(d_ff_128_qn), .en(nand_63_out), .reset(undriven_122));  // open: preset
  and and_41 (and_41_out, d_ff_65_q, nand_34_out);
  and and_42 (and_42_out, nand_34_out, d_ff_49_q);
  and and_43 (and_43_out, d_ff_66_q, nand_36_out);
  and and_44 (and_44_out, nand_36_out, d_ff_50_q);
  and and_45 (and_45_out, d_ff_67_q, nand_38_out);
  and and_46 (and_46_out, nand_38_out, d_ff_51_q);
  and and_47 (and_47_out, d_ff_68_q, nand_40_out);
  and and_48 (and_48_out, nand_40_out, d_ff_52_q);
  and and_49 (and_49_out, d_ff_69_q, nand_42_out);
  and and_50 (and_50_out, nand_42_out, d_ff_53_q);
  and and_51 (and_51_out, d_ff_70_q, nand_44_out);
  and and_52 (and_52_out, nand_44_out, d_ff_54_q);
  and and_53 (and_53_out, d_ff_71_q, nand_46_out);
  and and_54 (and_54_out, nand_46_out, d_ff_55_q);
  and and_55 (and_55_out, d_ff_72_q, nand_48_out);
  and and_56 (and_56_out, nand_48_out, d_ff_56_q);
  and and_57 (and_57_out, d_ff_73_q, nand_50_out);
  and and_58 (and_58_out, nand_50_out, d_ff_57_q);
  and and_59 (and_59_out, d_ff_74_q, nand_52_out);
  and and_60 (and_60_out, nand_52_out, d_ff_58_q);
  and and_61 (and_61_out, d_ff_75_q, nand_54_out);
  and and_62 (and_62_out, nand_54_out, d_ff_59_q);
  and and_63 (and_63_out, d_ff_76_q, nand_56_out);
  and and_64 (and_64_out, nand_56_out, d_ff_60_q);
  and and_65 (and_65_out, d_ff_77_q, nand_58_out);
  and and_66 (and_66_out, nand_58_out, d_ff_61_q);
  and and_67 (and_67_out, d_ff_78_q, nand_60_out);
  and and_68 (and_68_out, nand_60_out, d_ff_62_q);
  and and_69 (and_69_out, d_ff_79_q, nand_62_out);
  and and_70 (and_70_out, nand_62_out, d_ff_63_q);
  and and_71 (and_71_out, d_ff_80_q, nand_64_out);
  and and_72 (and_72_out, nand_64_out, d_ff_64_q);
  and and_73 (and_73_out, d_ff_81_q, nand_34_out);
  and and_74 (and_74_out, nand_34_out, d_ff_33_q);
  and and_75 (and_75_out, d_ff_82_q, nand_36_out);
  and and_76 (and_76_out, nand_36_out, d_ff_34_q);
  and and_77 (and_77_out, d_ff_83_q, nand_38_out);
  and and_78 (and_78_out, nand_38_out, d_ff_35_q);
  and and_79 (and_79_out, d_ff_84_q, nand_40_out);
  and and_80 (and_80_out, nand_40_out, d_ff_36_q);
  and and_81 (and_81_out, d_ff_85_q, nand_42_out);
  and and_82 (and_82_out, nand_42_out, d_ff_37_q);
  and and_83 (and_83_out, d_ff_86_q, nand_44_out);
  and and_84 (and_84_out, nand_44_out, d_ff_38_q);
  and and_85 (and_85_out, d_ff_87_q, nand_46_out);
  and and_86 (and_86_out, nand_46_out, d_ff_39_q);
  and and_87 (and_87_out, d_ff_88_q, nand_48_out);
  and and_88 (and_88_out, nand_48_out, d_ff_40_q);
  and and_89 (and_89_out, d_ff_89_q, nand_50_out);
  and and_90 (and_90_out, nand_50_out, d_ff_41_q);
  and and_91 (and_91_out, d_ff_90_q, nand_52_out);
  and and_92 (and_92_out, nand_52_out, d_ff_42_q);
  and and_93 (and_93_out, d_ff_91_q, nand_54_out);
  and and_94 (and_94_out, nand_54_out, d_ff_43_q);
  and and_95 (and_95_out, d_ff_92_q, nand_56_out);
  and and_96 (and_96_out, nand_56_out, d_ff_44_q);
  and and_97 (and_97_out, d_ff_93_q, nand_58_out);
  and and_98 (and_98_out, nand_58_out, d_ff_45_q);
  and and_99 (and_99_out, d_ff_94_q, nand_60_out);
  and and_100 (and_100_out, nand_60_out, d_ff_46_q);
  and and_101 (and_101_out, d_ff_95_q, nand_62_out);
  and and_102 (and_102_out, nand_62_out, d_ff_47_q);
  and and_103 (and_103_out, d_ff_96_q, nand_64_out);
  and and_104 (and_104_out, nand_64_out, d_ff_48_q);
  and and_105 (and_105_out, d_ff_97_q, nand_34_out);
  and and_106 (and_106_out, nand_34_out, d_ff_17_q);
  and and_107 (and_107_out, d_ff_98_q, nand_36_out);
  and and_108 (and_108_out, nand_36_out, d_ff_18_q);
  and and_109 (and_109_out, d_ff_99_q, nand_38_out);
  and and_110 (and_110_out, nand_38_out, d_ff_19_q);
  and and_111 (and_111_out, d_ff_100_q, nand_40_out);
  and and_112 (and_112_out, nand_40_out, d_ff_20_q);
  and and_113 (and_113_out, d_ff_101_q, nand_42_out);
  and and_114 (and_114_out, nand_42_out, d_ff_21_q);
  and and_115 (and_115_out, d_ff_102_q, nand_44_out);
  and and_116 (and_116_out, nand_44_out, d_ff_22_q);
  and and_117 (and_117_out, d_ff_103_q, nand_46_out);
  and and_118 (and_118_out, nand_46_out, d_ff_23_q);
  and and_119 (and_119_out, d_ff_104_q, nand_48_out);
  and and_120 (and_120_out, nand_48_out, d_ff_24_q);
  and and_121 (and_121_out, d_ff_105_q, nand_50_out);
  and and_122 (and_122_out, nand_50_out, d_ff_25_q);
  and and_123 (and_123_out, d_ff_106_q, nand_52_out);
  and and_124 (and_124_out, nand_52_out, d_ff_26_q);
  and and_125 (and_125_out, d_ff_107_q, nand_54_out);
  and and_126 (and_126_out, nand_54_out, d_ff_27_q);
  and and_127 (and_127_out, d_ff_108_q, nand_56_out);
  and and_128 (and_128_out, nand_56_out, d_ff_28_q);
  and and_129 (and_129_out, d_ff_109_q, nand_58_out);
  and and_130 (and_130_out, nand_58_out, d_ff_29_q);
  and and_131 (and_131_out, d_ff_110_q, nand_60_out);
  and and_132 (and_132_out, nand_60_out, d_ff_30_q);
  and and_133 (and_133_out, d_ff_111_q, nand_62_out);
  and and_134 (and_134_out, nand_62_out, d_ff_31_q);
  and and_135 (and_135_out, d_ff_112_q, nand_64_out);
  and and_136 (and_136_out, nand_64_out, d_ff_32_q);
  and and_137 (and_137_out, d_ff_113_q, nand_34_out);
  and and_138 (and_138_out, nand_34_out, d_ff_1_q);
  and and_139 (and_139_out, d_ff_114_q, nand_36_out);
  and and_140 (and_140_out, nand_36_out, d_ff_2_q);
  and and_141 (and_141_out, d_ff_115_q, nand_38_out);
  and and_142 (and_142_out, nand_38_out, d_ff_3_q);
  and and_143 (and_143_out, d_ff_116_q, nand_40_out);
  and and_144 (and_144_out, nand_40_out, d_ff_4_q);
  and and_145 (and_145_out, d_ff_117_q, nand_42_out);
  and and_146 (and_146_out, nand_42_out, d_ff_5_q);
  and and_147 (and_147_out, d_ff_118_q, nand_44_out);
  and and_148 (and_148_out, nand_44_out, d_ff_6_q);
  and and_149 (and_149_out, d_ff_119_q, nand_46_out);
  and and_150 (and_150_out, nand_46_out, d_ff_7_q);
  and and_151 (and_151_out, d_ff_120_q, nand_48_out);
  and and_152 (and_152_out, nand_48_out, d_ff_8_q);
  and and_153 (and_153_out, d_ff_121_q, nand_50_out);
  and and_154 (and_154_out, nand_50_out, d_ff_9_q);
  and and_155 (and_155_out, d_ff_122_q, nand_52_out);
  and and_156 (and_156_out, nand_52_out, d_ff_10_q);
  and and_157 (and_157_out, d_ff_123_q, nand_54_out);
  and and_158 (and_158_out, nand_54_out, d_ff_11_q);
  and and_159 (and_159_out, d_ff_124_q, nand_56_out);
  and and_160 (and_160_out, nand_56_out, d_ff_12_q);
  and and_161 (and_161_out, d_ff_125_q, nand_58_out);
  and and_162 (and_162_out, nand_58_out, d_ff_13_q);
  and and_163 (and_163_out, d_ff_126_q, nand_60_out);
  and and_164 (and_164_out, nand_60_out, d_ff_14_q);
  and and_165 (and_165_out, d_ff_127_q, nand_62_out);
  and and_166 (and_166_out, nand_62_out, d_ff_15_q);
  and and_167 (and_167_out, d_ff_128_q, nand_64_out);
  and and_168 (and_168_out, nand_64_out, d_ff_16_q);
  or or_1 (or_1_out, and_41_out, in_17);
  or or_2 (or_2_out, in_16, and_42_out);
  or or_3 (or_3_out, and_43_out, or_1_out);
  or or_4 (or_4_out, or_2_out, and_44_out);
  or or_5 (or_5_out, and_45_out, or_3_out);
  or or_6 (or_6_out, or_4_out, and_46_out);
  or or_7 (or_7_out, and_47_out, or_5_out);
  or or_8 (or_8_out, or_6_out, and_48_out);
  or or_9 (or_9_out, and_49_out, or_7_out);
  or or_10 (or_10_out, or_8_out, and_50_out);
  or or_11 (or_11_out, and_51_out, or_9_out);
  or or_12 (or_12_out, or_10_out, and_52_out);
  or or_13 (or_13_out, and_53_out, or_11_out);
  or or_14 (or_14_out, or_12_out, and_54_out);
  or or_15 (or_15_out, and_55_out, or_13_out);
  or or_16 (or_16_out, or_14_out, and_56_out);
  or or_17 (or_17_out, and_57_out, or_15_out);
  or or_18 (or_18_out, or_16_out, and_58_out);
  or or_19 (or_19_out, and_59_out, or_17_out);
  or or_20 (or_20_out, or_18_out, and_60_out);
  or or_21 (or_21_out, and_61_out, or_19_out);
  or or_22 (or_22_out, or_20_out, and_62_out);
  or or_23 (or_23_out, and_63_out, or_21_out);
  or or_24 (or_24_out, or_22_out, and_64_out);
  or or_25 (or_25_out, and_65_out, or_23_out);
  or or_26 (or_26_out, or_24_out, and_66_out);
  or or_27 (or_27_out, and_67_out, or_25_out);
  or or_28 (or_28_out, or_26_out, and_68_out);
  or or_29 (or_29_out, and_69_out, or_27_out);
  or or_30 (or_30_out, or_28_out, and_70_out);
  or or_31 (out_37, and_71_out, or_29_out);
  or or_32 (out_36, or_30_out, and_72_out);
  or or_33 (or_33_out, and_73_out, in_18);
  or or_34 (or_34_out, in_15, and_74_out);
  or or_35 (or_35_out, and_75_out, or_33_out);
  or or_36 (or_36_out, or_34_out, and_76_out);
  or or_37 (or_37_out, and_77_out, or_35_out);
  or or_38 (or_38_out, or_36_out, and_78_out);
  or or_39 (or_39_out, and_79_out, or_37_out);
  or or_40 (or_40_out, or_38_out, and_80_out);
  or or_41 (or_41_out, and_81_out, or_39_out);
  or or_42 (or_42_out, or_40_out, and_82_out);
  or or_43 (or_43_out, and_83_out, or_41_out);
  or or_44 (or_44_out, or_42_out, and_84_out);
  or or_45 (or_45_out, and_85_out, or_43_out);
  or or_46 (or_46_out, or_44_out, and_86_out);
  or or_47 (or_47_out, and_87_out, or_45_out);
  or or_48 (or_48_out, or_46_out, and_88_out);
  or or_49 (or_49_out, and_89_out, or_47_out);
  or or_50 (or_50_out, or_48_out, and_90_out);
  or or_51 (or_51_out, and_91_out, or_49_out);
  or or_52 (or_52_out, or_50_out, and_92_out);
  or or_53 (or_53_out, and_93_out, or_51_out);
  or or_54 (or_54_out, or_52_out, and_94_out);
  or or_55 (or_55_out, and_95_out, or_53_out);
  or or_56 (or_56_out, or_54_out, and_96_out);
  or or_57 (or_57_out, and_97_out, or_55_out);
  or or_58 (or_58_out, or_56_out, and_98_out);
  or or_59 (or_59_out, and_99_out, or_57_out);
  or or_60 (or_60_out, or_58_out, and_100_out);
  or or_61 (or_61_out, and_101_out, or_59_out);
  or or_62 (or_62_out, or_60_out, and_102_out);
  or or_63 (out_38, and_103_out, or_61_out);
  or or_64 (out_35, or_62_out, and_104_out);
  or or_65 (or_65_out, and_105_out, in_19);
  or or_66 (or_66_out, in_14, and_106_out);
  or or_67 (or_67_out, and_107_out, or_65_out);
  or or_68 (or_68_out, or_66_out, and_108_out);
  or or_69 (or_69_out, and_109_out, or_67_out);
  or or_70 (or_70_out, or_68_out, and_110_out);
  or or_71 (or_71_out, and_111_out, or_69_out);
  or or_72 (or_72_out, or_70_out, and_112_out);
  or or_73 (or_73_out, and_113_out, or_71_out);
  or or_74 (or_74_out, or_72_out, and_114_out);
  or or_75 (or_75_out, and_115_out, or_73_out);
  or or_76 (or_76_out, or_74_out, and_116_out);
  or or_77 (or_77_out, and_117_out, or_75_out);
  or or_78 (or_78_out, or_76_out, and_118_out);
  or or_79 (or_79_out, and_119_out, or_77_out);
  or or_80 (or_80_out, or_78_out, and_120_out);
  or or_81 (or_81_out, and_121_out, or_79_out);
  or or_82 (or_82_out, or_80_out, and_122_out);
  or or_83 (or_83_out, and_123_out, or_81_out);
  or or_84 (or_84_out, or_82_out, and_124_out);
  or or_85 (or_85_out, and_125_out, or_83_out);
  or or_86 (or_86_out, or_84_out, and_126_out);
  or or_87 (or_87_out, and_127_out, or_85_out);
  or or_88 (or_88_out, or_86_out, and_128_out);
  or or_89 (or_89_out, and_129_out, or_87_out);
  or or_90 (or_90_out, or_88_out, and_130_out);
  or or_91 (or_91_out, and_131_out, or_89_out);
  or or_92 (or_92_out, or_90_out, and_132_out);
  or or_93 (or_93_out, and_133_out, or_91_out);
  or or_94 (or_94_out, or_92_out, and_134_out);
  or or_95 (out_39, and_135_out, or_93_out);
  or or_96 (out_34, or_94_out, and_136_out);
  or or_97 (or_97_out, and_137_out, in_20);
  or or_98 (or_98_out, in_13, and_138_out);
  or or_99 (or_99_out, and_139_out, or_97_out);
  or or_100 (or_100_out, or_98_out, and_140_out);
  or or_101 (or_101_out, and_141_out, or_99_out);
  or or_102 (or_102_out, or_100_out, and_142_out);
  or or_103 (or_103_out, and_143_out, or_101_out);
  or or_104 (or_104_out, or_102_out, and_144_out);
  or or_105 (or_105_out, and_145_out, or_103_out);
  or or_106 (or_106_out, or_104_out, and_146_out);
  or or_107 (or_107_out, and_147_out, or_105_out);
  or or_108 (or_108_out, or_106_out, and_148_out);
  or or_109 (or_109_out, and_149_out, or_107_out);
  or or_110 (or_110_out, or_108_out, and_150_out);
  or or_111 (or_111_out, and_151_out, or_109_out);
  or or_112 (or_112_out, or_110_out, and_152_out);
  or or_113 (or_113_out, and_153_out, or_111_out);
  or or_114 (or_114_out, or_112_out, and_154_out);
  or or_115 (or_115_out, and_155_out, or_113_out);
  or or_116 (or_116_out, or_114_out, and_156_out);
  or or_117 (or_117_out, and_157_out, or_115_out);
  or or_118 (or_118_out, or_116_out, and_158_out);
  or or_119 (or_119_out, and_159_out, or_117_out);
  or or_120 (or_120_out, or_118_out, and_160_out);
  or or_121 (or_121_out, and_161_out, or_119_out);
  or or_122 (or_122_out, or_120_out, and_162_out);
  or or_123 (or_123_out, and_163_out, or_121_out);
  or or_124 (or_124_out, or_122_out, and_164_out);
  or or_125 (or_125_out, and_165_out, or_123_out);
  or or_126 (or_126_out, or_124_out, and_166_out);
  or or_127 (out_40, and_167_out, or_125_out);
  or or_128 (out_33, or_126_out, and_168_out);

  assign out_25 = in_5;
  assign out_26 = in_6;
  assign out_27 = in_7;
  assign out_28 = in_8;
  assign out_29 = in_9;
  assign out_30 = in_10;
  assign out_31 = in_11;
  assign out_32 = in_12;

  // Notes on the sheet:
  //   R
  //   W
endmodule

module _8256B_256_Bites_Ram_Lc (
  input  [7:0] in_1,
  input  [7:0] in_2,
  input  [7:0] in_3,
  input  in_4,
  input  in_5,
  input  in_6,
  input  in_7,
  output [7:0] out_8
);

  wire [7:0] ram_1_data;

  RAM #(.bus("separate")) ram_1 (
    .addr(in_3), .din(in_1), .data(ram_1_data), .str(in_5), .sel(in_7), .clk(in_4), .ld(in_6));  // open: clr
  Multiplexer #(.width(8), .enable("false")) multiplexer_1 (.in0(in_2), .in1(ram_1_data), .out(out_8), .sel(in_7));
endmodule

module V096_96_Bites_32By24_Video_Buffer (
  input  in_1,
  input  [1:0] in_2,
  input  [1:0] in_3,
  input  [2:0] in_4,
  input  [7:0] in_5,
  input  in_6,
  input  in_7,
  output [31:0] out_8,
  output [31:0] out_9,
  output [31:0] out_10,
  output [31:0] out_11,
  output [31:0] out_12,
  output [31:0] out_13,
  output [31:0] out_14,
  output [31:0] out_15,
  output [31:0] out_16,
  output [31:0] out_17,
  output [31:0] out_18,
  output [31:0] out_19,
  output [31:0] out_20,
  output [31:0] out_21,
  output [31:0] out_22,
  output [31:0] out_23,
  output [31:0] out_24,
  output [31:0] out_25,
  output [31:0] out_26,
  output [31:0] out_27,
  output [31:0] out_28,
  output [31:0] out_29,
  output [31:0] out_30,
  output [31:0] out_31
);

  wire decoder_1_out0, decoder_1_out1, decoder_1_out2, decoder_1_out3, decoder_2_out1, decoder_2_out2,
       decoder_2_out3, decoder_2_out4, decoder_2_out5, decoder_2_out6, decoder_3_out0, decoder_3_out1,
       decoder_3_out2, decoder_3_out3, decoder_4_out1, decoder_4_out2, decoder_4_out3, decoder_4_out4,
       decoder_4_out5, decoder_4_out6, decoder_5_out0, decoder_5_out1, decoder_5_out2, decoder_5_out3,
       decoder_6_out1, decoder_6_out2, decoder_6_out3, decoder_6_out4, decoder_6_out5, decoder_6_out6,
       decoder_7_out0, decoder_7_out1, decoder_7_out2, decoder_7_out3, decoder_8_out1, decoder_8_out2,
       decoder_8_out3, decoder_8_out4, decoder_8_out5, decoder_8_out6, decoder_9_out0, decoder_9_out1,
       decoder_9_out2, decoder_9_out3, decoder_10_out1, decoder_10_out2, decoder_10_out3, decoder_10_out4,
       decoder_10_out5, decoder_10_out6, decoder_11_out1, decoder_11_out2, decoder_11_out3, decoder_11_out4,
       decoder_11_out5, decoder_11_out6, decoder_12_out1, decoder_12_out2, decoder_12_out3, decoder_12_out4,
       decoder_12_out5, decoder_12_out6, decoder_13_out1, decoder_13_out2, decoder_13_out3, decoder_13_out4,
       decoder_13_out5, decoder_13_out6, decoder_14_out1, decoder_14_out2, decoder_14_out3, decoder_14_out4,
       decoder_14_out5, decoder_14_out6, decoder_15_out1, decoder_15_out2, decoder_15_out3, decoder_15_out4,
       decoder_15_out5, decoder_15_out6, decoder_16_out1, decoder_16_out2, decoder_16_out3, decoder_16_out4,
       decoder_16_out5, decoder_16_out6, decoder_17_out1, decoder_17_out2, decoder_17_out3, decoder_17_out4,
       decoder_17_out5, decoder_17_out6, decoder_18_out1, decoder_18_out2, decoder_18_out3, decoder_18_out4,
       decoder_18_out5, decoder_18_out6, decoder_19_out1, decoder_19_out2, decoder_19_out3, decoder_19_out4,
       decoder_19_out5, decoder_19_out6, decoder_20_out1, decoder_20_out2, decoder_20_out3, decoder_20_out4,
       decoder_20_out5, decoder_20_out6, decoder_21_out1, decoder_21_out2, decoder_21_out3, decoder_21_out4,
       decoder_21_out5, decoder_21_out6;

  Decoder #(.select(2), .disabled(0)) decoder_1 (
    .out0(decoder_1_out0), .out1(decoder_1_out1), .out2(decoder_1_out2), .out3(decoder_1_out3), .sel(in_2),
    .en(in_1));
  Decoder #(.select(3), .disabled(0)) decoder_2 (
    .out1(decoder_2_out1), .out2(decoder_2_out2), .out3(decoder_2_out3), .out4(decoder_2_out4),
    .out5(decoder_2_out5), .out6(decoder_2_out6), .sel(in_4), .en(decoder_3_out0));  // open: out0, out7
  Decoder #(.select(2), .disabled(0)) decoder_3 (
    .out0(decoder_3_out0), .out1(decoder_3_out1), .out2(decoder_3_out2), .out3(decoder_3_out3), .sel(in_3),
    .en(decoder_1_out0));
  Decoder #(.select(3), .disabled(0)) decoder_4 (
    .out1(decoder_4_out1), .out2(decoder_4_out2), .out3(decoder_4_out3), .out4(decoder_4_out4),
    .out5(decoder_4_out5), .out6(decoder_4_out6), .sel(in_4), .en(decoder_5_out0));  // open: out0, out7
  Decoder #(.select(2), .disabled(0)) decoder_5 (
    .out0(decoder_5_out0), .out1(decoder_5_out1), .out2(decoder_5_out2), .out3(decoder_5_out3), .sel(in_3),
    .en(decoder_1_out1));
  Decoder #(.select(3), .disabled(0)) decoder_6 (
    .out1(decoder_6_out1), .out2(decoder_6_out2), .out3(decoder_6_out3), .out4(decoder_6_out4),
    .out5(decoder_6_out5), .out6(decoder_6_out6), .sel(in_4), .en(decoder_7_out0));  // open: out0, out7
  Decoder #(.select(2), .disabled(0)) decoder_7 (
    .out0(decoder_7_out0), .out1(decoder_7_out1), .out2(decoder_7_out2), .out3(decoder_7_out3), .sel(in_3),
    .en(decoder_1_out2));
  Decoder #(.select(3), .disabled(0)) decoder_8 (
    .out1(decoder_8_out1), .out2(decoder_8_out2), .out3(decoder_8_out3), .out4(decoder_8_out4),
    .out5(decoder_8_out5), .out6(decoder_8_out6), .sel(in_4), .en(decoder_9_out0));  // open: out0, out7
  Decoder #(.select(2), .disabled(0)) decoder_9 (
    .out0(decoder_9_out0), .out1(decoder_9_out1), .out2(decoder_9_out2), .out3(decoder_9_out3), .sel(in_3),
    .en(decoder_1_out3));
  Register register_1 (.D(in_5), .en(decoder_2_out1), .Q(out_8[31:24]), .clk(in_6), .clr(in_7));
  Register register_2 (.D(in_5), .en(decoder_2_out2), .Q(out_12[31:24]), .clk(in_6), .clr(in_7));
  Register register_3 (.D(in_5), .en(decoder_4_out1), .Q(out_8[23:16]), .clk(in_6), .clr(in_7));
  Register register_4 (.D(in_5), .en(decoder_4_out2), .Q(out_12[23:16]), .clk(in_6), .clr(in_7));
  Register register_5 (.D(in_5), .en(decoder_6_out1), .Q(out_8[15:8]), .clk(in_6), .clr(in_7));
  Register register_6 (.D(in_5), .en(decoder_6_out2), .Q(out_12[15:8]), .clk(in_6), .clr(in_7));
  Register register_7 (.D(in_5), .en(decoder_8_out1), .Q(out_8[7:0]), .clk(in_6), .clr(in_7));
  Register register_8 (.D(in_5), .en(decoder_8_out2), .Q(out_12[7:0]), .clk(in_6), .clr(in_7));
  Register register_9 (.D(in_5), .en(decoder_2_out3), .Q(out_16[31:24]), .clk(in_6), .clr(in_7));
  Register register_10 (.D(in_5), .en(decoder_2_out4), .Q(out_20[31:24]), .clk(in_6), .clr(in_7));
  Register register_11 (.D(in_5), .en(decoder_2_out5), .Q(out_24[31:24]), .clk(in_6), .clr(in_7));
  Register register_12 (.D(in_5), .en(decoder_4_out3), .Q(out_16[23:16]), .clk(in_6), .clr(in_7));
  Register register_13 (.D(in_5), .en(decoder_4_out4), .Q(out_20[23:16]), .clk(in_6), .clr(in_7));
  Register register_14 (.D(in_5), .en(decoder_4_out5), .Q(out_24[23:16]), .clk(in_6), .clr(in_7));
  Register register_15 (.D(in_5), .en(decoder_6_out3), .Q(out_16[15:8]), .clk(in_6), .clr(in_7));
  Register register_16 (.D(in_5), .en(decoder_6_out4), .Q(out_20[15:8]), .clk(in_6), .clr(in_7));
  Register register_17 (.D(in_5), .en(decoder_6_out5), .Q(out_24[15:8]), .clk(in_6), .clr(in_7));
  Register register_18 (.D(in_5), .en(decoder_8_out3), .Q(out_16[7:0]), .clk(in_6), .clr(in_7));
  Register register_19 (.D(in_5), .en(decoder_8_out4), .Q(out_20[7:0]), .clk(in_6), .clr(in_7));
  Register register_20 (.D(in_5), .en(decoder_8_out5), .Q(out_24[7:0]), .clk(in_6), .clr(in_7));
  Register register_21 (.D(in_5), .en(decoder_2_out6), .Q(out_28[31:24]), .clk(in_6), .clr(in_7));
  Register register_22 (.D(in_5), .en(decoder_4_out6), .Q(out_28[23:16]), .clk(in_6), .clr(in_7));
  Register register_23 (.D(in_5), .en(decoder_6_out6), .Q(out_28[15:8]), .clk(in_6), .clr(in_7));
  Register register_24 (.D(in_5), .en(decoder_8_out6), .Q(out_28[7:0]), .clk(in_6), .clr(in_7));
  Decoder #(.select(3), .disabled(0)) decoder_10 (
    .out1(decoder_10_out1), .out2(decoder_10_out2), .out3(decoder_10_out3), .out4(decoder_10_out4),
    .out5(decoder_10_out5), .out6(decoder_10_out6), .sel(in_4), .en(decoder_3_out1));  // open: out0, out7
  Decoder #(.select(3), .disabled(0)) decoder_11 (
    .out1(decoder_11_out1), .out2(decoder_11_out2), .out3(decoder_11_out3), .out4(decoder_11_out4),
    .out5(decoder_11_out5), .out6(decoder_11_out6), .sel(in_4), .en(decoder_5_out1));  // open: out0, out7
  Decoder #(.select(3), .disabled(0)) decoder_12 (
    .out1(decoder_12_out1), .out2(decoder_12_out2), .out3(decoder_12_out3), .out4(decoder_12_out4),
    .out5(decoder_12_out5), .out6(decoder_12_out6), .sel(in_4), .en(decoder_7_out1));  // open: out0, out7
  Decoder #(.select(3), .disabled(0)) decoder_13 (
    .out1(decoder_13_out1), .out2(decoder_13_out2), .out3(decoder_13_out3), .out4(decoder_13_out4),
    .out5(decoder_13_out5), .out6(decoder_13_out6), .sel(in_4), .en(decoder_9_out1));  // open: out0, out7
  Register register_25 (.D(in_5), .en(decoder_10_out1), .Q(out_9[31:24]), .clk(in_6), .clr(in_7));
  Register register_26 (.D(in_5), .en(decoder_10_out2), .Q(out_13[31:24]), .clk(in_6), .clr(in_7));
  Register register_27 (.D(in_5), .en(decoder_11_out1), .Q(out_9[23:16]), .clk(in_6), .clr(in_7));
  Register register_28 (.D(in_5), .en(decoder_11_out2), .Q(out_13[23:16]), .clk(in_6), .clr(in_7));
  Register register_29 (.D(in_5), .en(decoder_12_out1), .Q(out_9[15:8]), .clk(in_6), .clr(in_7));
  Register register_30 (.D(in_5), .en(decoder_12_out2), .Q(out_13[15:8]), .clk(in_6), .clr(in_7));
  Register register_31 (.D(in_5), .en(decoder_13_out1), .Q(out_9[7:0]), .clk(in_6), .clr(in_7));
  Register register_32 (.D(in_5), .en(decoder_13_out2), .Q(out_13[7:0]), .clk(in_6), .clr(in_7));
  Register register_33 (.D(in_5), .en(decoder_10_out3), .Q(out_17[31:24]), .clk(in_6), .clr(in_7));
  Register register_34 (.D(in_5), .en(decoder_10_out4), .Q(out_21[31:24]), .clk(in_6), .clr(in_7));
  Register register_35 (.D(in_5), .en(decoder_11_out3), .Q(out_17[23:16]), .clk(in_6), .clr(in_7));
  Register register_36 (.D(in_5), .en(decoder_11_out4), .Q(out_21[23:16]), .clk(in_6), .clr(in_7));
  Register register_37 (.D(in_5), .en(decoder_12_out3), .Q(out_17[15:8]), .clk(in_6), .clr(in_7));
  Register register_38 (.D(in_5), .en(decoder_12_out4), .Q(out_21[15:8]), .clk(in_6), .clr(in_7));
  Register register_39 (.D(in_5), .en(decoder_13_out3), .Q(out_17[7:0]), .clk(in_6), .clr(in_7));
  Register register_40 (.D(in_5), .en(decoder_13_out4), .Q(out_21[7:0]), .clk(in_6), .clr(in_7));
  Register register_41 (.D(in_5), .en(decoder_10_out5), .Q(out_25[31:24]), .clk(in_6), .clr(in_7));
  Register register_42 (.D(in_5), .en(decoder_10_out6), .Q(out_29[31:24]), .clk(in_6), .clr(in_7));
  Register register_43 (.D(in_5), .en(decoder_11_out5), .Q(out_25[23:16]), .clk(in_6), .clr(in_7));
  Register register_44 (.D(in_5), .en(decoder_11_out6), .Q(out_29[23:16]), .clk(in_6), .clr(in_7));
  Register register_45 (.D(in_5), .en(decoder_12_out5), .Q(out_25[15:8]), .clk(in_6), .clr(in_7));
  Register register_46 (.D(in_5), .en(decoder_12_out6), .Q(out_29[15:8]), .clk(in_6), .clr(in_7));
  Register register_47 (.D(in_5), .en(decoder_13_out5), .Q(out_25[7:0]), .clk(in_6), .clr(in_7));
  Register register_48 (.D(in_5), .en(decoder_13_out6), .Q(out_29[7:0]), .clk(in_6), .clr(in_7));
  Decoder #(.select(3), .disabled(0)) decoder_14 (
    .out1(decoder_14_out1), .out2(decoder_14_out2), .out3(decoder_14_out3), .out4(decoder_14_out4),
    .out5(decoder_14_out5), .out6(decoder_14_out6), .sel(in_4), .en(decoder_3_out2));  // open: out0, out7
  Decoder #(.select(3), .disabled(0)) decoder_15 (
    .out1(decoder_15_out1), .out2(decoder_15_out2), .out3(decoder_15_out3), .out4(decoder_15_out4),
    .out5(decoder_15_out5), .out6(decoder_15_out6), .sel(in_4), .en(decoder_5_out2));  // open: out0, out7
  Decoder #(.select(3), .disabled(0)) decoder_16 (
    .out1(decoder_16_out1), .out2(decoder_16_out2), .out3(decoder_16_out3), .out4(decoder_16_out4),
    .out5(decoder_16_out5), .out6(decoder_16_out6), .sel(in_4), .en(decoder_7_out2));  // open: out0, out7
  Decoder #(.select(3), .disabled(0)) decoder_17 (
    .out1(decoder_17_out1), .out2(decoder_17_out2), .out3(decoder_17_out3), .out4(decoder_17_out4),
    .out5(decoder_17_out5), .out6(decoder_17_out6), .sel(in_4), .en(decoder_9_out2));  // open: out0, out7
  Register register_49 (.D(in_5), .en(decoder_14_out1), .Q(out_10[31:24]), .clk(in_6), .clr(in_7));
  Register register_50 (.D(in_5), .en(decoder_15_out1), .Q(out_10[23:16]), .clk(in_6), .clr(in_7));
  Register register_51 (.D(in_5), .en(decoder_16_out1), .Q(out_10[15:8]), .clk(in_6), .clr(in_7));
  Register register_52 (.D(in_5), .en(decoder_17_out1), .Q(out_10[7:0]), .clk(in_6), .clr(in_7));
  Register register_53 (.D(in_5), .en(decoder_14_out2), .Q(out_14[31:24]), .clk(in_6), .clr(in_7));
  Register register_54 (.D(in_5), .en(decoder_14_out3), .Q(out_18[31:24]), .clk(in_6), .clr(in_7));
  Register register_55 (.D(in_5), .en(decoder_14_out4), .Q(out_22[31:24]), .clk(in_6), .clr(in_7));
  Register register_56 (.D(in_5), .en(decoder_15_out2), .Q(out_14[23:16]), .clk(in_6), .clr(in_7));
  Register register_57 (.D(in_5), .en(decoder_15_out3), .Q(out_18[23:16]), .clk(in_6), .clr(in_7));
  Register register_58 (.D(in_5), .en(decoder_15_out4), .Q(out_22[23:16]), .clk(in_6), .clr(in_7));
  Register register_59 (.D(in_5), .en(decoder_16_out2), .Q(out_14[15:8]), .clk(in_6), .clr(in_7));
  Register register_60 (.D(in_5), .en(decoder_16_out3), .Q(out_18[15:8]), .clk(in_6), .clr(in_7));
  Register register_61 (.D(in_5), .en(decoder_16_out4), .Q(out_22[15:8]), .clk(in_6), .clr(in_7));
  Register register_62 (.D(in_5), .en(decoder_17_out2), .Q(out_14[7:0]), .clk(in_6), .clr(in_7));
  Register register_63 (.D(in_5), .en(decoder_17_out3), .Q(out_18[7:0]), .clk(in_6), .clr(in_7));
  Register register_64 (.D(in_5), .en(decoder_17_out4), .Q(out_22[7:0]), .clk(in_6), .clr(in_7));
  Register register_65 (.D(in_5), .en(decoder_14_out5), .Q(out_26[31:24]), .clk(in_6), .clr(in_7));
  Register register_66 (.D(in_5), .en(decoder_14_out6), .Q(out_30[31:24]), .clk(in_6), .clr(in_7));
  Register register_67 (.D(in_5), .en(decoder_15_out5), .Q(out_26[23:16]), .clk(in_6), .clr(in_7));
  Register register_68 (.D(in_5), .en(decoder_15_out6), .Q(out_30[23:16]), .clk(in_6), .clr(in_7));
  Register register_69 (.D(in_5), .en(decoder_16_out5), .Q(out_26[15:8]), .clk(in_6), .clr(in_7));
  Register register_70 (.D(in_5), .en(decoder_16_out6), .Q(out_30[15:8]), .clk(in_6), .clr(in_7));
  Register register_71 (.D(in_5), .en(decoder_17_out5), .Q(out_26[7:0]), .clk(in_6), .clr(in_7));
  Register register_72 (.D(in_5), .en(decoder_17_out6), .Q(out_30[7:0]), .clk(in_6), .clr(in_7));
  Decoder #(.select(3), .disabled(0)) decoder_18 (
    .out1(decoder_18_out1), .out2(decoder_18_out2), .out3(decoder_18_out3), .out4(decoder_18_out4),
    .out5(decoder_18_out5), .out6(decoder_18_out6), .sel(in_4), .en(decoder_3_out3));  // open: out0, out7
  Decoder #(.select(3), .disabled(0)) decoder_19 (
    .out1(decoder_19_out1), .out2(decoder_19_out2), .out3(decoder_19_out3), .out4(decoder_19_out4),
    .out5(decoder_19_out5), .out6(decoder_19_out6), .sel(in_4), .en(decoder_5_out3));  // open: out0, out7
  Decoder #(.select(3), .disabled(0)) decoder_20 (
    .out1(decoder_20_out1), .out2(decoder_20_out2), .out3(decoder_20_out3), .out4(decoder_20_out4),
    .out5(decoder_20_out5), .out6(decoder_20_out6), .sel(in_4), .en(decoder_7_out3));  // open: out0, out7
  Decoder #(.select(3), .disabled(0)) decoder_21 (
    .out1(decoder_21_out1), .out2(decoder_21_out2), .out3(decoder_21_out3), .out4(decoder_21_out4),
    .out5(decoder_21_out5), .out6(decoder_21_out6), .sel(in_4), .en(decoder_9_out3));  // open: out0, out7
  Register register_73 (.D(in_5), .en(decoder_18_out1), .Q(out_11[31:24]), .clk(in_6), .clr(in_7));
  Register register_74 (.D(in_5), .en(decoder_19_out1), .Q(out_11[23:16]), .clk(in_6), .clr(in_7));
  Register register_75 (.D(in_5), .en(decoder_20_out1), .Q(out_11[15:8]), .clk(in_6), .clr(in_7));
  Register register_76 (.D(in_5), .en(decoder_21_out1), .Q(out_11[7:0]), .clk(in_6), .clr(in_7));
  Register register_77 (.D(in_5), .en(decoder_18_out2), .Q(out_15[31:24]), .clk(in_6), .clr(in_7));
  Register register_78 (.D(in_5), .en(decoder_18_out3), .Q(out_19[31:24]), .clk(in_6), .clr(in_7));
  Register register_79 (.D(in_5), .en(decoder_18_out4), .Q(out_23[31:24]), .clk(in_6), .clr(in_7));
  Register register_80 (.D(in_5), .en(decoder_19_out2), .Q(out_15[23:16]), .clk(in_6), .clr(in_7));
  Register register_81 (.D(in_5), .en(decoder_19_out3), .Q(out_19[23:16]), .clk(in_6), .clr(in_7));
  Register register_82 (.D(in_5), .en(decoder_19_out4), .Q(out_23[23:16]), .clk(in_6), .clr(in_7));
  Register register_83 (.D(in_5), .en(decoder_20_out2), .Q(out_15[15:8]), .clk(in_6), .clr(in_7));
  Register register_84 (.D(in_5), .en(decoder_20_out3), .Q(out_19[15:8]), .clk(in_6), .clr(in_7));
  Register register_85 (.D(in_5), .en(decoder_20_out4), .Q(out_23[15:8]), .clk(in_6), .clr(in_7));
  Register register_86 (.D(in_5), .en(decoder_21_out2), .Q(out_15[7:0]), .clk(in_6), .clr(in_7));
  Register register_87 (.D(in_5), .en(decoder_21_out3), .Q(out_19[7:0]), .clk(in_6), .clr(in_7));
  Register register_88 (.D(in_5), .en(decoder_21_out4), .Q(out_23[7:0]), .clk(in_6), .clr(in_7));
  Register register_89 (.D(in_5), .en(decoder_18_out5), .Q(out_27[31:24]), .clk(in_6), .clr(in_7));
  Register register_90 (.D(in_5), .en(decoder_18_out6), .Q(out_31[31:24]), .clk(in_6), .clr(in_7));
  Register register_91 (.D(in_5), .en(decoder_19_out5), .Q(out_27[23:16]), .clk(in_6), .clr(in_7));
  Register register_92 (.D(in_5), .en(decoder_19_out6), .Q(out_31[23:16]), .clk(in_6), .clr(in_7));
  Register register_93 (.D(in_5), .en(decoder_20_out5), .Q(out_27[15:8]), .clk(in_6), .clr(in_7));
  Register register_94 (.D(in_5), .en(decoder_20_out6), .Q(out_31[15:8]), .clk(in_6), .clr(in_7));
  Register register_95 (.D(in_5), .en(decoder_21_out5), .Q(out_27[7:0]), .clk(in_6), .clr(in_7));
  Register register_96 (.D(in_5), .en(decoder_21_out6), .Q(out_31[7:0]), .clk(in_6), .clr(in_7));

  // Notes on the sheet:
  //   Enable/Write
  //   Adr Y
  //   Adr X
  //   Adr Xc
  //   Data
  //   Clock
  //   Reset
endmodule
