// Logisim project 8.5.6 DMA.circ as structural Verilog: 9 circuits, main circuit main
module main (
  input  MMU_On,
  input  in_2,
  output [7:0] Data,
  output [15:0] out_4,
  output [15:0] Instruc,
  output [11:0] PC
);

  wire alu_1_out_8, alu_1_out_9, and_1_out, and_2_out, and_3_out, and_4_out, and_5_out, and_6_out, and_7_out,
       and_8_out, and_9_out, and_10_out, and_11_out, and_12_out, and_13_out, and_14_out, and_15_out,
       and_16_out, and_17_out, and_18_out, and_19_out, and_20_out, and_21_out, button_1_out, clock_1_out_13,
       clock_1_out_14, clock_1_out_15, clock_1_out_16, clock_1_out_17, clock_1_out_18, clock_1_out_19,
       clock_1_out_20, clock_1_out_21, clock_1_out_22, clock_1_out_24, clock_1_out_25, clock_1_out_26,
       clock_1_out_27, clock_1_out_28, clock_1_out_29, clock_1_out_30, clock_1_out_31, clock_1_out_32,
       clock_1_out_33, control_1_out_10, control_1_out_20, control_1_out_21, control_1_out_22,
       control_1_out_23, control_1_out_24, control_1_out_25, d_ff_1_q, d_ff_1_qn, d_ff_2_q, d_ff_2_qn,
       d_ff_3_q, d_ff_3_qn, d_ff_4_q, d_ff_4_qn, decoder_1_out0, decoder_1_out1, decoder_1_out2,
       decoder_1_out3, decoder_1_out4, decoder_2_out0, decoder_2_out1, decoder_2_out2, decoder_2_out3,
       decoder_2_out4, decoder_3_out0, decoder_3_out1, decoder_3_out2, decoder_3_out3, decoder_3_out4,
       decoder_4_out0, decoder_4_out1, decoder_4_out2, decoder_5_out0, decoder_5_out1, decoder_5_out2,
       decoder_5_out3, decoder_6_out0, decoder_6_out1, decoder_6_out2, decoder_6_out3, dma_1_out_7,
       dma_1_out_8, dma_1_out_9, dma_1_out_11, dma_1_out_12, kb_io_1_enable_io_mt, kb_io_1_out_11,
       kb_io_1_out_12, multiplexer_5_out, multiplexer_20_out, multiplexer_21_out, multiplexer_23_out,
       multiplexer_29_out, multiplexer_30_out, multiplexer_31_out, nand_1_out, nand_2_out, nand_3_out,
       nand_4_out, nand_5_out, not_1_out, Off_out, On_2_out, On_out, or_1_out, or_2_out, or_3_out, or_4_out,
       or_5_out, or_9_out, or_10_out, or_15_out, or_16_out, or_18_out, or_20_out, or_21_out, or_22_out,
       or_23_out, or_24_out, or_25_out, or_26_out, or_27_out, or_28_out, or_29_out, register_5_q, undriven,
       undriven_2, undriven_3, undriven_4, undriven_5, undriven_6, undriven_7, undriven_8, undriven_9,
       undriven_10, undriven_11, undriven_12, undriven_13, undriven_14, undriven_15, undriven_16,
       undriven_17, undriven_18, undriven_19, undriven_20, undriven_21, undriven_22, undriven_23,
       undriven_24, undriven_25, undriven_26, undriven_27, undriven_28, undriven_29, undriven_30,
       undriven_31, undriven_32, undriven_33, undriven_34, video_card_120_x_96_1__0,
       video_card_120_x_96_1_e_w;
  wire [1:0] adder_3_out, multiplexer_18_out, or_19_out, register_2_q, video_card_120_x_96_1_out_5,
       video_card_120_x_96_1_out_6, video_card_120_x_96_1_out_6_2;
  wire [2:0] control_1_out_18, video_card_120_x_96_1_out_5_2, video_card_120_x_96_1_out_5_3,
       video_card_120_x_96_1_out_7;
  wire [3:0] _0_out, _4_out, _8_out, c_out, multiplexer_8_out_2, video_card_120_x_96_1_out_6_3,
       video_card_120_x_96_1_out_7_3;
  wire [3:3] video_card_120_x_96_1_out_7_2;
  wire [4:0] control_1_out_17;
  wire [5:0] multiplexer_24_out;
  wire [7:0] alu_1_out_7, clock_1_out_12, control_1_out_16, multiplexer_1_out, multiplexer_2_out,
       multiplexer_3_out, multiplexer_4_out, multiplexer_8_out, multiplexer_19_out, multiplexer_25_out,
       multiplexer_28_out, multiplexer_32_out, multiplexer_33_out, multiplexer_34_out, multiplexer_35_out,
       multiplexer_36_out, multiplexer_38_out, multiplexer_39_out, multiplexer_40_out, multiplexer_42_out,
       or_11_out, or_12_out, or_13_out, or_14_out, ram_2_data, ram_3_data, ram_8_data, register_3_q,
       register_4_q, registers_1_out_10, registers_1_out_11, registers_1_out_12, registers_1_out_13,
       rom_1_data, video_card_120_x_96_1_out_8;
  wire [9:0] or_19_out_2;
  wire [11:0] adder_1_out, adder_4_out, clock_1_out_23, dma_1_out_6, dma_1_out_10, multiplexer_6_out,
       multiplexer_10_out, multiplexer_12_out, multiplexer_22_out, multiplexer_27_out, or_6_out, or_7_out,
       or_8_out, or_17_out;
  wire [14:0] control_1_out_19;
  wire [15:0] adder_2_out, control_1_out_11, control_1_out_12, control_1_out_13, control_1_out_14,
       control_1_out_15, multiplexer_7_out, multiplexer_9_out, multiplexer_11_out, multiplexer_13_out,
       multiplexer_15_out, multiplexer_16_out, multiplexer_17_out, multiplexer_26_out, multiplexer_37_out,
       multiplexer_41_out, registers_1_out_14, xor_1_out;
  wire [31:0] multiplexer_14_out, ram_1_data, ram_7_data, v096_96_bites_32by24_video_buffer_1_out_8,
       v096_96_bites_32by24_video_buffer_1_out_9, v096_96_bites_32by24_video_buffer_1_out_10,
       v096_96_bites_32by24_video_buffer_1_out_11, v096_96_bites_32by24_video_buffer_1_out_12,
       v096_96_bites_32by24_video_buffer_1_out_13, v096_96_bites_32by24_video_buffer_1_out_14,
       v096_96_bites_32by24_video_buffer_1_out_15, v096_96_bites_32by24_video_buffer_1_out_16,
       v096_96_bites_32by24_video_buffer_1_out_17, v096_96_bites_32by24_video_buffer_1_out_18,
       v096_96_bites_32by24_video_buffer_1_out_19, v096_96_bites_32by24_video_buffer_1_out_20,
       v096_96_bites_32by24_video_buffer_1_out_21, v096_96_bites_32by24_video_buffer_1_out_22,
       v096_96_bites_32by24_video_buffer_1_out_23, v096_96_bites_32by24_video_buffer_1_out_24,
       v096_96_bites_32by24_video_buffer_1_out_25, v096_96_bites_32by24_video_buffer_1_out_26,
       v096_96_bites_32by24_video_buffer_1_out_27, v096_96_bites_32by24_video_buffer_1_out_28,
       v096_96_bites_32by24_video_buffer_1_out_29, v096_96_bites_32by24_video_buffer_1_out_30,
       v096_96_bites_32by24_video_buffer_1_out_31, v096_96_bites_32by24_video_buffer_2_out_8,
       v096_96_bites_32by24_video_buffer_2_out_9, v096_96_bites_32by24_video_buffer_2_out_10,
       v096_96_bites_32by24_video_buffer_2_out_11, v096_96_bites_32by24_video_buffer_2_out_12,
       v096_96_bites_32by24_video_buffer_2_out_13, v096_96_bites_32by24_video_buffer_2_out_14,
       v096_96_bites_32by24_video_buffer_2_out_15, v096_96_bites_32by24_video_buffer_2_out_16,
       v096_96_bites_32by24_video_buffer_2_out_17, v096_96_bites_32by24_video_buffer_2_out_18,
       v096_96_bites_32by24_video_buffer_2_out_19, v096_96_bites_32by24_video_buffer_2_out_20,
       v096_96_bites_32by24_video_buffer_2_out_21, v096_96_bites_32by24_video_buffer_2_out_22,
       v096_96_bites_32by24_video_buffer_2_out_23, v096_96_bites_32by24_video_buffer_2_out_24,
       v096_96_bites_32by24_video_buffer_2_out_25, v096_96_bites_32by24_video_buffer_2_out_26,
       v096_96_bites_32by24_video_buffer_2_out_27, v096_96_bites_32by24_video_buffer_2_out_28,
       v096_96_bites_32by24_video_buffer_2_out_29, v096_96_bites_32by24_video_buffer_2_out_30,
       v096_96_bites_32by24_video_buffer_2_out_31, v096_96_bites_32by24_video_buffer_3_out_8,
       v096_96_bites_32by24_video_buffer_3_out_9, v096_96_bites_32by24_video_buffer_3_out_10,
       v096_96_bites_32by24_video_buffer_3_out_11, v096_96_bites_32by24_video_buffer_3_out_12,
       v096_96_bites_32by24_video_buffer_3_out_13, v096_96_bites_32by24_video_buffer_3_out_14,
       v096_96_bites_32by24_video_buffer_3_out_15, v096_96_bites_32by24_video_buffer_3_out_16,
       v096_96_bites_32by24_video_buffer_3_out_17, v096_96_bites_32by24_video_buffer_3_out_18,
       v096_96_bites_32by24_video_buffer_3_out_19, v096_96_bites_32by24_video_buffer_3_out_20,
       v096_96_bites_32by24_video_buffer_3_out_21, v096_96_bites_32by24_video_buffer_3_out_22,
       v096_96_bites_32by24_video_buffer_3_out_23, v096_96_bites_32by24_video_buffer_3_out_24,
       v096_96_bites_32by24_video_buffer_3_out_25, v096_96_bites_32by24_video_buffer_3_out_26,
       v096_96_bites_32by24_video_buffer_3_out_27, v096_96_bites_32by24_video_buffer_3_out_28,
       v096_96_bites_32by24_video_buffer_3_out_29, v096_96_bites_32by24_video_buffer_3_out_30,
       v096_96_bites_32by24_video_buffer_3_out_31, v096_96_bites_32by24_video_buffer_4_out_8,
       v096_96_bites_32by24_video_buffer_4_out_9, v096_96_bites_32by24_video_buffer_4_out_10,
       v096_96_bites_32by24_video_buffer_4_out_11, v096_96_bites_32by24_video_buffer_4_out_12,
       v096_96_bites_32by24_video_buffer_4_out_13, v096_96_bites_32by24_video_buffer_4_out_14,
       v096_96_bites_32by24_video_buffer_4_out_15, v096_96_bites_32by24_video_buffer_4_out_16,
       v096_96_bites_32by24_video_buffer_4_out_17, v096_96_bites_32by24_video_buffer_4_out_18,
       v096_96_bites_32by24_video_buffer_4_out_19, v096_96_bites_32by24_video_buffer_4_out_20,
       v096_96_bites_32by24_video_buffer_4_out_21, v096_96_bites_32by24_video_buffer_4_out_22,
       v096_96_bites_32by24_video_buffer_4_out_23, v096_96_bites_32by24_video_buffer_4_out_24,
       v096_96_bites_32by24_video_buffer_4_out_25, v096_96_bites_32by24_video_buffer_4_out_26,
       v096_96_bites_32by24_video_buffer_4_out_27, v096_96_bites_32by24_video_buffer_4_out_28,
       v096_96_bites_32by24_video_buffer_4_out_29, v096_96_bites_32by24_video_buffer_4_out_30,
       v096_96_bites_32by24_video_buffer_4_out_31, v096_96_bites_32by24_video_buffer_5_out_8,
       v096_96_bites_32by24_video_buffer_5_out_9, v096_96_bites_32by24_video_buffer_5_out_10,
       v096_96_bites_32by24_video_buffer_5_out_11, v096_96_bites_32by24_video_buffer_5_out_12,
       v096_96_bites_32by24_video_buffer_5_out_13, v096_96_bites_32by24_video_buffer_5_out_14,
       v096_96_bites_32by24_video_buffer_5_out_15, v096_96_bites_32by24_video_buffer_5_out_16,
       v096_96_bites_32by24_video_buffer_5_out_17, v096_96_bites_32by24_video_buffer_5_out_18,
       v096_96_bites_32by24_video_buffer_5_out_19, v096_96_bites_32by24_video_buffer_5_out_20,
       v096_96_bites_32by24_video_buffer_5_out_21, v096_96_bites_32by24_video_buffer_5_out_22,
       v096_96_bites_32by24_video_buffer_5_out_23, v096_96_bites_32by24_video_buffer_5_out_24,
       v096_96_bites_32by24_video_buffer_5_out_25, v096_96_bites_32by24_video_buffer_5_out_26,
       v096_96_bites_32by24_video_buffer_5_out_27, v096_96_bites_32by24_video_buffer_5_out_28,
       v096_96_bites_32by24_video_buffer_5_out_29, v096_96_bites_32by24_video_buffer_5_out_30,
       v096_96_bites_32by24_video_buffer_5_out_31, v096_96_bites_32by24_video_buffer_6_out_8,
       v096_96_bites_32by24_video_buffer_6_out_9, v096_96_bites_32by24_video_buffer_6_out_10,
       v096_96_bites_32by24_video_buffer_6_out_11, v096_96_bites_32by24_video_buffer_6_out_12,
       v096_96_bites_32by24_video_buffer_6_out_13, v096_96_bites_32by24_video_buffer_6_out_14,
       v096_96_bites_32by24_video_buffer_6_out_15, v096_96_bites_32by24_video_buffer_6_out_16,
       v096_96_bites_32by24_video_buffer_6_out_17, v096_96_bites_32by24_video_buffer_6_out_18,
       v096_96_bites_32by24_video_buffer_6_out_19, v096_96_bites_32by24_video_buffer_6_out_20,
       v096_96_bites_32by24_video_buffer_6_out_21, v096_96_bites_32by24_video_buffer_6_out_22,
       v096_96_bites_32by24_video_buffer_6_out_23, v096_96_bites_32by24_video_buffer_6_out_24,
       v096_96_bites_32by24_video_buffer_6_out_25, v096_96_bites_32by24_video_buffer_6_out_26,
       v096_96_bites_32by24_video_buffer_6_out_27, v096_96_bites_32by24_video_buffer_6_out_28,
       v096_96_bites_32by24_video_buffer_6_out_29, v096_96_bites_32by24_video_buffer_6_out_30,
       v096_96_bites_32by24_video_buffer_6_out_31, v096_96_bites_32by24_video_buffer_7_out_8,
       v096_96_bites_32by24_video_buffer_7_out_9, v096_96_bites_32by24_video_buffer_7_out_10,
       v096_96_bites_32by24_video_buffer_7_out_11, v096_96_bites_32by24_video_buffer_7_out_12,
       v096_96_bites_32by24_video_buffer_7_out_13, v096_96_bites_32by24_video_buffer_7_out_14,
       v096_96_bites_32by24_video_buffer_7_out_15, v096_96_bites_32by24_video_buffer_7_out_16,
       v096_96_bites_32by24_video_buffer_7_out_17, v096_96_bites_32by24_video_buffer_7_out_18,
       v096_96_bites_32by24_video_buffer_7_out_19, v096_96_bites_32by24_video_buffer_7_out_20,
       v096_96_bites_32by24_video_buffer_7_out_21, v096_96_bites_32by24_video_buffer_7_out_22,
       v096_96_bites_32by24_video_buffer_7_out_23, v096_96_bites_32by24_video_buffer_7_out_24,
       v096_96_bites_32by24_video_buffer_7_out_25, v096_96_bites_32by24_video_buffer_7_out_26,
       v096_96_bites_32by24_video_buffer_7_out_27, v096_96_bites_32by24_video_buffer_7_out_28,
       v096_96_bites_32by24_video_buffer_7_out_29, v096_96_bites_32by24_video_buffer_7_out_30,
       v096_96_bites_32by24_video_buffer_7_out_31, v096_96_bites_32by24_video_buffer_8_out_8,
       v096_96_bites_32by24_video_buffer_8_out_9, v096_96_bites_32by24_video_buffer_8_out_10,
       v096_96_bites_32by24_video_buffer_8_out_11, v096_96_bites_32by24_video_buffer_8_out_12,
       v096_96_bites_32by24_video_buffer_8_out_13, v096_96_bites_32by24_video_buffer_8_out_14,
       v096_96_bites_32by24_video_buffer_8_out_15, v096_96_bites_32by24_video_buffer_8_out_16,
       v096_96_bites_32by24_video_buffer_8_out_17, v096_96_bites_32by24_video_buffer_8_out_18,
       v096_96_bites_32by24_video_buffer_8_out_19, v096_96_bites_32by24_video_buffer_8_out_20,
       v096_96_bites_32by24_video_buffer_8_out_21, v096_96_bites_32by24_video_buffer_8_out_22,
       v096_96_bites_32by24_video_buffer_8_out_23, v096_96_bites_32by24_video_buffer_8_out_24,
       v096_96_bites_32by24_video_buffer_8_out_25, v096_96_bites_32by24_video_buffer_8_out_26,
       v096_96_bites_32by24_video_buffer_8_out_27, v096_96_bites_32by24_video_buffer_8_out_28,
       v096_96_bites_32by24_video_buffer_8_out_29, v096_96_bites_32by24_video_buffer_8_out_30,
       v096_96_bites_32by24_video_buffer_8_out_31, v096_96_bites_32by24_video_buffer_9_out_8,
       v096_96_bites_32by24_video_buffer_9_out_9, v096_96_bites_32by24_video_buffer_9_out_10,
       v096_96_bites_32by24_video_buffer_9_out_11, v096_96_bites_32by24_video_buffer_9_out_12,
       v096_96_bites_32by24_video_buffer_9_out_13, v096_96_bites_32by24_video_buffer_9_out_14,
       v096_96_bites_32by24_video_buffer_9_out_15, v096_96_bites_32by24_video_buffer_9_out_16,
       v096_96_bites_32by24_video_buffer_9_out_17, v096_96_bites_32by24_video_buffer_9_out_18,
       v096_96_bites_32by24_video_buffer_9_out_19, v096_96_bites_32by24_video_buffer_9_out_20,
       v096_96_bites_32by24_video_buffer_9_out_21, v096_96_bites_32by24_video_buffer_9_out_22,
       v096_96_bites_32by24_video_buffer_9_out_23, v096_96_bites_32by24_video_buffer_9_out_24,
       v096_96_bites_32by24_video_buffer_9_out_25, v096_96_bites_32by24_video_buffer_9_out_26,
       v096_96_bites_32by24_video_buffer_9_out_27, v096_96_bites_32by24_video_buffer_9_out_28,
       v096_96_bites_32by24_video_buffer_9_out_29, v096_96_bites_32by24_video_buffer_9_out_30,
       v096_96_bites_32by24_video_buffer_9_out_31, v096_96_bites_32by24_video_buffer_10_out_8,
       v096_96_bites_32by24_video_buffer_10_out_9, v096_96_bites_32by24_video_buffer_10_out_10,
       v096_96_bites_32by24_video_buffer_10_out_11, v096_96_bites_32by24_video_buffer_10_out_12,
       v096_96_bites_32by24_video_buffer_10_out_13, v096_96_bites_32by24_video_buffer_10_out_14,
       v096_96_bites_32by24_video_buffer_10_out_15, v096_96_bites_32by24_video_buffer_10_out_16,
       v096_96_bites_32by24_video_buffer_10_out_17, v096_96_bites_32by24_video_buffer_10_out_18,
       v096_96_bites_32by24_video_buffer_10_out_19, v096_96_bites_32by24_video_buffer_10_out_20,
       v096_96_bites_32by24_video_buffer_10_out_21, v096_96_bites_32by24_video_buffer_10_out_22,
       v096_96_bites_32by24_video_buffer_10_out_23, v096_96_bites_32by24_video_buffer_10_out_24,
       v096_96_bites_32by24_video_buffer_10_out_25, v096_96_bites_32by24_video_buffer_10_out_26,
       v096_96_bites_32by24_video_buffer_10_out_27, v096_96_bites_32by24_video_buffer_10_out_28,
       v096_96_bites_32by24_video_buffer_10_out_29, v096_96_bites_32by24_video_buffer_10_out_30,
       v096_96_bites_32by24_video_buffer_10_out_31, v096_96_bites_32by24_video_buffer_11_out_8,
       v096_96_bites_32by24_video_buffer_11_out_9, v096_96_bites_32by24_video_buffer_11_out_10,
       v096_96_bites_32by24_video_buffer_11_out_11, v096_96_bites_32by24_video_buffer_11_out_12,
       v096_96_bites_32by24_video_buffer_11_out_13, v096_96_bites_32by24_video_buffer_11_out_14,
       v096_96_bites_32by24_video_buffer_11_out_15, v096_96_bites_32by24_video_buffer_11_out_16,
       v096_96_bites_32by24_video_buffer_11_out_17, v096_96_bites_32by24_video_buffer_11_out_18,
       v096_96_bites_32by24_video_buffer_11_out_19, v096_96_bites_32by24_video_buffer_11_out_20,
       v096_96_bites_32by24_video_buffer_11_out_21, v096_96_bites_32by24_video_buffer_11_out_22,
       v096_96_bites_32by24_video_buffer_11_out_23, v096_96_bites_32by24_video_buffer_11_out_24,
       v096_96_bites_32by24_video_buffer_11_out_25, v096_96_bites_32by24_video_buffer_11_out_26,
       v096_96_bites_32by24_video_buffer_11_out_27, v096_96_bites_32by24_video_buffer_11_out_28,
       v096_96_bites_32by24_video_buffer_11_out_29, v096_96_bites_32by24_video_buffer_11_out_30,
       v096_96_bites_32by24_video_buffer_11_out_31, v096_96_bites_32by24_video_buffer_12_out_8,
       v096_96_bites_32by24_video_buffer_12_out_9, v096_96_bites_32by24_video_buffer_12_out_10,
       v096_96_bites_32by24_video_buffer_12_out_11, v096_96_bites_32by24_video_buffer_12_out_12,
       v096_96_bites_32by24_video_buffer_12_out_13, v096_96_bites_32by24_video_buffer_12_out_14,
       v096_96_bites_32by24_video_buffer_12_out_15, v096_96_bites_32by24_video_buffer_12_out_16,
       v096_96_bites_32by24_video_buffer_12_out_17, v096_96_bites_32by24_video_buffer_12_out_18,
       v096_96_bites_32by24_video_buffer_12_out_19, v096_96_bites_32by24_video_buffer_12_out_20,
       v096_96_bites_32by24_video_buffer_12_out_21, v096_96_bites_32by24_video_buffer_12_out_22,
       v096_96_bites_32by24_video_buffer_12_out_23, v096_96_bites_32by24_video_buffer_12_out_24,
       v096_96_bites_32by24_video_buffer_12_out_25, v096_96_bites_32by24_video_buffer_12_out_26,
       v096_96_bites_32by24_video_buffer_12_out_27, v096_96_bites_32by24_video_buffer_12_out_28,
       v096_96_bites_32by24_video_buffer_12_out_29, v096_96_bites_32by24_video_buffer_12_out_30,
       v096_96_bites_32by24_video_buffer_12_out_31, v096_96_bites_32by24_video_buffer_13_out_8,
       v096_96_bites_32by24_video_buffer_13_out_9, v096_96_bites_32by24_video_buffer_13_out_10,
       v096_96_bites_32by24_video_buffer_13_out_11, v096_96_bites_32by24_video_buffer_13_out_12,
       v096_96_bites_32by24_video_buffer_13_out_13, v096_96_bites_32by24_video_buffer_13_out_14,
       v096_96_bites_32by24_video_buffer_13_out_15, v096_96_bites_32by24_video_buffer_13_out_16,
       v096_96_bites_32by24_video_buffer_13_out_17, v096_96_bites_32by24_video_buffer_13_out_18,
       v096_96_bites_32by24_video_buffer_13_out_19, v096_96_bites_32by24_video_buffer_13_out_20,
       v096_96_bites_32by24_video_buffer_13_out_21, v096_96_bites_32by24_video_buffer_13_out_22,
       v096_96_bites_32by24_video_buffer_13_out_23, v096_96_bites_32by24_video_buffer_13_out_24,
       v096_96_bites_32by24_video_buffer_13_out_25, v096_96_bites_32by24_video_buffer_13_out_26,
       v096_96_bites_32by24_video_buffer_13_out_27, v096_96_bites_32by24_video_buffer_13_out_28,
       v096_96_bites_32by24_video_buffer_13_out_29, v096_96_bites_32by24_video_buffer_13_out_30,
       v096_96_bites_32by24_video_buffer_13_out_31, v096_96_bites_32by24_video_buffer_14_out_8,
       v096_96_bites_32by24_video_buffer_14_out_9, v096_96_bites_32by24_video_buffer_14_out_10,
       v096_96_bites_32by24_video_buffer_14_out_11, v096_96_bites_32by24_video_buffer_14_out_12,
       v096_96_bites_32by24_video_buffer_14_out_13, v096_96_bites_32by24_video_buffer_14_out_14,
       v096_96_bites_32by24_video_buffer_14_out_15, v096_96_bites_32by24_video_buffer_14_out_16,
       v096_96_bites_32by24_video_buffer_14_out_17, v096_96_bites_32by24_video_buffer_14_out_18,
       v096_96_bites_32by24_video_buffer_14_out_19, v096_96_bites_32by24_video_buffer_14_out_20,
       v096_96_bites_32by24_video_buffer_14_out_21, v096_96_bites_32by24_video_buffer_14_out_22,
       v096_96_bites_32by24_video_buffer_14_out_23, v096_96_bites_32by24_video_buffer_14_out_24,
       v096_96_bites_32by24_video_buffer_14_out_25, v096_96_bites_32by24_video_buffer_14_out_26,
       v096_96_bites_32by24_video_buffer_14_out_27, v096_96_bites_32by24_video_buffer_14_out_28,
       v096_96_bites_32by24_video_buffer_14_out_29, v096_96_bites_32by24_video_buffer_14_out_30,
       v096_96_bites_32by24_video_buffer_14_out_31, v096_96_bites_32by24_video_buffer_15_out_8,
       v096_96_bites_32by24_video_buffer_15_out_9, v096_96_bites_32by24_video_buffer_15_out_10,
       v096_96_bites_32by24_video_buffer_15_out_11, v096_96_bites_32by24_video_buffer_15_out_12,
       v096_96_bites_32by24_video_buffer_15_out_13, v096_96_bites_32by24_video_buffer_15_out_14,
       v096_96_bites_32by24_video_buffer_15_out_15, v096_96_bites_32by24_video_buffer_15_out_16,
       v096_96_bites_32by24_video_buffer_15_out_17, v096_96_bites_32by24_video_buffer_15_out_18,
       v096_96_bites_32by24_video_buffer_15_out_19, v096_96_bites_32by24_video_buffer_15_out_20,
       v096_96_bites_32by24_video_buffer_15_out_21, v096_96_bites_32by24_video_buffer_15_out_22,
       v096_96_bites_32by24_video_buffer_15_out_23, v096_96_bites_32by24_video_buffer_15_out_24,
       v096_96_bites_32by24_video_buffer_15_out_25, v096_96_bites_32by24_video_buffer_15_out_26,
       v096_96_bites_32by24_video_buffer_15_out_27, v096_96_bites_32by24_video_buffer_15_out_28,
       v096_96_bites_32by24_video_buffer_15_out_29, v096_96_bites_32by24_video_buffer_15_out_30,
       v096_96_bites_32by24_video_buffer_15_out_31;

  nand nand_1 (nand_1_out, undriven_15, undriven_9);
  nand nand_2 (nand_2_out, undriven_5, undriven);
  nand nand_3 (nand_3_out, undriven_10, undriven_11);
  nand nand_4 (nand_4_out, undriven_2, undriven_6);
  or or_1 (or_1_out, undriven_7, undriven_3);
  or or_2 (or_2_out, undriven_16, undriven_12);
  or or_3 (or_3_out, undriven_4, undriven_8);
  or or_4 (or_4_out, undriven_13, undriven_14);
  LED led_1 (.in(clock_1_out_16));
  LED led_2 (.in(clock_1_out_15));
  LED led_3 (.in(clock_1_out_17));
  Button On (.out(On_out));
  Button Off (.out(Off_out));
  Counter #(.width(32), .max('hffffffff)) Clocks (
    .count(clock_1_out_14), .clk(clock_1_out_25), .clr(On_out));  // open: load, D, Q, carry
  Counter #(.width(32), .max('hffffffff)) u_Instruc (
    .count(clock_1_out_13), .clk(clock_1_out_25), .clr(On_out));  // open: load, D, Q, carry
  LED led_4 (.in(clock_1_out_18));
  Button On_2 (.out(On_2_out));
  D_Flip_Flop d_ff_1 (
    .clk(undriven_21), .D(undriven_17), .Q(d_ff_1_q), .Qn(d_ff_1_qn), .en(undriven_18), .reset(undriven_24));  // open: preset
  and and_1 (and_1_out, undriven_22, undriven_19);
  and and_2 (and_2_out, undriven_20, undriven_23);
  D_Flip_Flop d_ff_2 (
    .clk(undriven_27), .D(undriven_25), .Q(d_ff_2_q), .Qn(d_ff_2_qn), .en(undriven_26), .reset(undriven_31));  // open: preset
  and and_3 (and_3_out, undriven_32, undriven_28);
  and and_4 (and_4_out, undriven_29, undriven_30);
  Button button_1 (.out(button_1_out));
  Multiplexer #(.width(8), .disabled(0), .enable("false")) multiplexer_1 (
    .in0(or_11_out), .in1(adder_4_out[7:0]), .out(multiplexer_1_out), .sel(control_1_out_24));
  Multiplexer #(.width(8), .disabled(0), .enable("false")) multiplexer_2 (
    .in0(or_11_out), .in1({4'b0000, adder_4_out[11:8]}), .out(multiplexer_2_out), .sel(control_1_out_24));
  or or_5 (or_5_out, button_1_out, On_out);
  Multiplexer #(.width(8), .disabled(0), .enable("false")) multiplexer_3 (
    .in0(multiplexer_1_out), .in1(multiplexer_8_out), .out(multiplexer_3_out), .sel(control_1_out_23));
  Multiplexer #(.width(8), .disabled(0), .enable("false")) multiplexer_4 (
    .in0(multiplexer_2_out), .in1({4'b0000, multiplexer_8_out_2}), .out(multiplexer_4_out),
    .sel(control_1_out_23));
  DotMatrix #(.matrixcols(24), .matrixrows(32)) dotmatrix_1 (
    .col0(v096_96_bites_32by24_video_buffer_1_out_8), .col1(v096_96_bites_32by24_video_buffer_1_out_12),
    .col2(v096_96_bites_32by24_video_buffer_1_out_16), .col3(v096_96_bites_32by24_video_buffer_1_out_20),
    .col4(v096_96_bites_32by24_video_buffer_1_out_24), .col5(v096_96_bites_32by24_video_buffer_1_out_28),
    .col6(v096_96_bites_32by24_video_buffer_1_out_9), .col7(v096_96_bites_32by24_video_buffer_1_out_13),
    .col8(v096_96_bites_32by24_video_buffer_1_out_17), .col9(v096_96_bites_32by24_video_buffer_1_out_21),
    .col10(v096_96_bites_32by24_video_buffer_1_out_25), .col11(v096_96_bites_32by24_video_buffer_1_out_29),
    .col12(v096_96_bites_32by24_video_buffer_1_out_10), .col13(v096_96_bites_32by24_video_buffer_1_out_14),
    .col14(v096_96_bites_32by24_video_buffer_1_out_18), .col15(v096_96_bites_32by24_video_buffer_1_out_22),
    .col16(v096_96_bites_32by24_video_buffer_1_out_26), .col17(v096_96_bites_32by24_video_buffer_1_out_30),
    .col18(v096_96_bites_32by24_video_buffer_1_out_11), .col19(v096_96_bites_32by24_video_buffer_1_out_15),
    .col20(v096_96_bites_32by24_video_buffer_1_out_19), .col21(v096_96_bites_32by24_video_buffer_1_out_23),
    .col22(v096_96_bites_32by24_video_buffer_1_out_27), .col23(v096_96_bites_32by24_video_buffer_1_out_31));
  DotMatrix #(.matrixcols(24), .matrixrows(32)) dotmatrix_2 (
    .col0(v096_96_bites_32by24_video_buffer_2_out_8), .col1(v096_96_bites_32by24_video_buffer_2_out_12),
    .col2(v096_96_bites_32by24_video_buffer_2_out_16), .col3(v096_96_bites_32by24_video_buffer_2_out_20),
    .col4(v096_96_bites_32by24_video_buffer_2_out_24), .col5(v096_96_bites_32by24_video_buffer_2_out_28),
    .col6(v096_96_bites_32by24_video_buffer_2_out_9), .col7(v096_96_bites_32by24_video_buffer_2_out_13),
    .col8(v096_96_bites_32by24_video_buffer_2_out_17), .col9(v096_96_bites_32by24_video_buffer_2_out_21),
    .col10(v096_96_bites_32by24_video_buffer_2_out_25), .col11(v096_96_bites_32by24_video_buffer_2_out_29),
    .col12(v096_96_bites_32by24_video_buffer_2_out_10), .col13(v096_96_bites_32by24_video_buffer_2_out_14),
    .col14(v096_96_bites_32by24_video_buffer_2_out_18), .col15(v096_96_bites_32by24_video_buffer_2_out_22),
    .col16(v096_96_bites_32by24_video_buffer_2_out_26), .col17(v096_96_bites_32by24_video_buffer_2_out_30),
    .col18(v096_96_bites_32by24_video_buffer_2_out_11), .col19(v096_96_bites_32by24_video_buffer_2_out_15),
    .col20(v096_96_bites_32by24_video_buffer_2_out_19), .col21(v096_96_bites_32by24_video_buffer_2_out_23),
    .col22(v096_96_bites_32by24_video_buffer_2_out_27), .col23(v096_96_bites_32by24_video_buffer_2_out_31));
  DotMatrix #(.matrixcols(24), .matrixrows(32)) dotmatrix_3 (
    .col0(v096_96_bites_32by24_video_buffer_3_out_8), .col1(v096_96_bites_32by24_video_buffer_3_out_12),
    .col2(v096_96_bites_32by24_video_buffer_3_out_16), .col3(v096_96_bites_32by24_video_buffer_3_out_20),
    .col4(v096_96_bites_32by24_video_buffer_3_out_24), .col5(v096_96_bites_32by24_video_buffer_3_out_28),
    .col6(v096_96_bites_32by24_video_buffer_3_out_9), .col7(v096_96_bites_32by24_video_buffer_3_out_13),
    .col8(v096_96_bites_32by24_video_buffer_3_out_17), .col9(v096_96_bites_32by24_video_buffer_3_out_21),
    .col10(v096_96_bites_32by24_video_buffer_3_out_25), .col11(v096_96_bites_32by24_video_buffer_3_out_29),
    .col12(v096_96_bites_32by24_video_buffer_3_out_10), .col13(v096_96_bites_32by24_video_buffer_3_out_14),
    .col14(v096_96_bites_32by24_video_buffer_3_out_18), .col15(v096_96_bites_32by24_video_buffer_3_out_22),
    .col16(v096_96_bites_32by24_video_buffer_3_out_26), .col17(v096_96_bites_32by24_video_buffer_3_out_30),
    .col18(v096_96_bites_32by24_video_buffer_3_out_11), .col19(v096_96_bites_32by24_video_buffer_3_out_15),
    .col20(v096_96_bites_32by24_video_buffer_3_out_19), .col21(v096_96_bites_32by24_video_buffer_3_out_23),
    .col22(v096_96_bites_32by24_video_buffer_3_out_27), .col23(v096_96_bites_32by24_video_buffer_3_out_31));
  Button _0 (.out(_0_out[0]));
  Button _1 (.out(_0_out[1]));
  Button _2 (.out(_0_out[2]));
  Button _3 (.out(_0_out[3]));
  V096_96_Bites_32By24_Video_Buffer v096_96_bites_32by24_video_buffer_1 (
    .out_8(v096_96_bites_32by24_video_buffer_1_out_8), .out_9(v096_96_bites_32by24_video_buffer_1_out_9),
    .out_10(v096_96_bites_32by24_video_buffer_1_out_10), .out_11(v096_96_bites_32by24_video_buffer_1_out_11),
    .out_12(v096_96_bites_32by24_video_buffer_1_out_12), .out_13(v096_96_bites_32by24_video_buffer_1_out_13),
    .out_14(v096_96_bites_32by24_video_buffer_1_out_14), .out_15(v096_96_bites_32by24_video_buffer_1_out_15),
    .out_16(v096_96_bites_32by24_video_buffer_1_out_16), .out_17(v096_96_bites_32by24_video_buffer_1_out_17),
    .out_18(v096_96_bites_32by24_video_buffer_1_out_18), .out_19(v096_96_bites_32by24_video_buffer_1_out_19),
    .out_20(v096_96_bites_32by24_video_buffer_1_out_20), .out_21(v096_96_bites_32by24_video_buffer_1_out_21),
    .out_22(v096_96_bites_32by24_video_buffer_1_out_22), .out_23(v096_96_bites_32by24_video_buffer_1_out_23),
    .out_24(v096_96_bites_32by24_video_buffer_1_out_24), .out_25(v096_96_bites_32by24_video_buffer_1_out_25),
    .out_26(v096_96_bites_32by24_video_buffer_1_out_26), .out_27(v096_96_bites_32by24_video_buffer_1_out_27),
    .out_28(v096_96_bites_32by24_video_buffer_1_out_28), .out_29(v096_96_bites_32by24_video_buffer_1_out_29),
    .out_30(v096_96_bites_32by24_video_buffer_1_out_30), .out_31(v096_96_bites_32by24_video_buffer_1_out_31),
    .in_1(decoder_1_out0), .in_2(video_card_120_x_96_1_out_6), .in_3(video_card_120_x_96_1_out_5),
    .in_4(video_card_120_x_96_1_out_7), .in_5(video_card_120_x_96_1_out_8), .in_6(clock_1_out_25),
    .in_7(video_card_120_x_96_1__0));
  V096_96_Bites_32By24_Video_Buffer v096_96_bites_32by24_video_buffer_2 (
    .out_8(v096_96_bites_32by24_video_buffer_2_out_8), .out_9(v096_96_bites_32by24_video_buffer_2_out_9),
    .out_10(v096_96_bites_32by24_video_buffer_2_out_10), .out_11(v096_96_bites_32by24_video_buffer_2_out_11),
    .out_12(v096_96_bites_32by24_video_buffer_2_out_12), .out_13(v096_96_bites_32by24_video_buffer_2_out_13),
    .out_14(v096_96_bites_32by24_video_buffer_2_out_14), .out_15(v096_96_bites_32by24_video_buffer_2_out_15),
    .out_16(v096_96_bites_32by24_video_buffer_2_out_16), .out_17(v096_96_bites_32by24_video_buffer_2_out_17),
    .out_18(v096_96_bites_32by24_video_buffer_2_out_18), .out_19(v096_96_bites_32by24_video_buffer_2_out_19),
    .out_20(v096_96_bites_32by24_video_buffer_2_out_20), .out_21(v096_96_bites_32by24_video_buffer_2_out_21),
    .out_22(v096_96_bites_32by24_video_buffer_2_out_22), .out_23(v096_96_bites_32by24_video_buffer_2_out_23),
    .out_24(v096_96_bites_32by24_video_buffer_2_out_24), .out_25(v096_96_bites_32by24_video_buffer_2_out_25),
    .out_26(v096_96_bites_32by24_video_buffer_2_out_26), .out_27(v096_96_bites_32by24_video_buffer_2_out_27),
    .out_28(v096_96_bites_32by24_video_buffer_2_out_28), .out_29(v096_96_bites_32by24_video_buffer_2_out_29),
    .out_30(v096_96_bites_32by24_video_buffer_2_out_30), .out_31(v096_96_bites_32by24_video_buffer_2_out_31),
    .in_1(decoder_2_out0), .in_2(video_card_120_x_96_1_out_6), .in_3(video_card_120_x_96_1_out_5),
    .in_4(video_card_120_x_96_1_out_7), .in_5(video_card_120_x_96_1_out_8), .in_6(clock_1_out_25),
    .in_7(video_card_120_x_96_1__0));
  V096_96_Bites_32By24_Video_Buffer v096_96_bites_32by24_video_buffer_3 (
    .out_8(v096_96_bites_32by24_video_buffer_3_out_8), .out_9(v096_96_bites_32by24_video_buffer_3_out_9),
    .out_10(v096_96_bites_32by24_video_buffer_3_out_10), .out_11(v096_96_bites_32by24_video_buffer_3_out_11),
    .out_12(v096_96_bites_32by24_video_buffer_3_out_12), .out_13(v096_96_bites_32by24_video_buffer_3_out_13),
    .out_14(v096_96_bites_32by24_video_buffer_3_out_14), .out_15(v096_96_bites_32by24_video_buffer_3_out_15),
    .out_16(v096_96_bites_32by24_video_buffer_3_out_16), .out_17(v096_96_bites_32by24_video_buffer_3_out_17),
    .out_18(v096_96_bites_32by24_video_buffer_3_out_18), .out_19(v096_96_bites_32by24_video_buffer_3_out_19),
    .out_20(v096_96_bites_32by24_video_buffer_3_out_20), .out_21(v096_96_bites_32by24_video_buffer_3_out_21),
    .out_22(v096_96_bites_32by24_video_buffer_3_out_22), .out_23(v096_96_bites_32by24_video_buffer_3_out_23),
    .out_24(v096_96_bites_32by24_video_buffer_3_out_24), .out_25(v096_96_bites_32by24_video_buffer_3_out_25),
    .out_26(v096_96_bites_32by24_video_buffer_3_out_26), .out_27(v096_96_bites_32by24_video_buffer_3_out_27),
    .out_28(v096_96_bites_32by24_video_buffer_3_out_28), .out_29(v096_96_bites_32by24_video_buffer_3_out_29),
    .out_30(v096_96_bites_32by24_video_buffer_3_out_30), .out_31(v096_96_bites_32by24_video_buffer_3_out_31),
    .in_1(decoder_3_out0), .in_2(video_card_120_x_96_1_out_6), .in_3(video_card_120_x_96_1_out_5),
    .in_4(video_card_120_x_96_1_out_7), .in_5(video_card_120_x_96_1_out_8), .in_6(clock_1_out_25),
    .in_7(video_card_120_x_96_1__0));
  Button _4 (.out(_4_out[0]));
  Button _5 (.out(_4_out[1]));
  Button _6 (.out(_4_out[2]));
  Button _7 (.out(_4_out[3]));
  Button _8 (.out(_8_out[0]));
  Button _9 (.out(_8_out[1]));
  Button a (.out(_8_out[2]));
  Button b (.out(_8_out[3]));
  DotMatrix #(.matrixcols(24), .matrixrows(32)) dotmatrix_4 (
    .col0(v096_96_bites_32by24_video_buffer_4_out_8), .col1(v096_96_bites_32by24_video_buffer_4_out_12),
    .col2(v096_96_bites_32by24_video_buffer_4_out_16), .col3(v096_96_bites_32by24_video_buffer_4_out_20),
    .col4(v096_96_bites_32by24_video_buffer_4_out_24), .col5(v096_96_bites_32by24_video_buffer_4_out_28),
    .col6(v096_96_bites_32by24_video_buffer_4_out_9), .col7(v096_96_bites_32by24_video_buffer_4_out_13),
    .col8(v096_96_bites_32by24_video_buffer_4_out_17), .col9(v096_96_bites_32by24_video_buffer_4_out_21),
    .col10(v096_96_bites_32by24_video_buffer_4_out_25), .col11(v096_96_bites_32by24_video_buffer_4_out_29),
    .col12(v096_96_bites_32by24_video_buffer_4_out_10), .col13(v096_96_bites_32by24_video_buffer_4_out_14),
    .col14(v096_96_bites_32by24_video_buffer_4_out_18), .col15(v096_96_bites_32by24_video_buffer_4_out_22),
    .col16(v096_96_bites_32by24_video_buffer_4_out_26), .col17(v096_96_bites_32by24_video_buffer_4_out_30),
    .col18(v096_96_bites_32by24_video_buffer_4_out_11), .col19(v096_96_bites_32by24_video_buffer_4_out_15),
    .col20(v096_96_bites_32by24_video_buffer_4_out_19), .col21(v096_96_bites_32by24_video_buffer_4_out_23),
    .col22(v096_96_bites_32by24_video_buffer_4_out_27), .col23(v096_96_bites_32by24_video_buffer_4_out_31));
  DotMatrix #(.matrixcols(24), .matrixrows(32)) dotmatrix_5 (
    .col0(v096_96_bites_32by24_video_buffer_5_out_8), .col1(v096_96_bites_32by24_video_buffer_5_out_12),
    .col2(v096_96_bites_32by24_video_buffer_5_out_16), .col3(v096_96_bites_32by24_video_buffer_5_out_20),
    .col4(v096_96_bites_32by24_video_buffer_5_out_24), .col5(v096_96_bites_32by24_video_buffer_5_out_28),
    .col6(v096_96_bites_32by24_video_buffer_5_out_9), .col7(v096_96_bites_32by24_video_buffer_5_out_13),
    .col8(v096_96_bites_32by24_video_buffer_5_out_17), .col9(v096_96_bites_32by24_video_buffer_5_out_21),
    .col10(v096_96_bites_32by24_video_buffer_5_out_25), .col11(v096_96_bites_32by24_video_buffer_5_out_29),
    .col12(v096_96_bites_32by24_video_buffer_5_out_10), .col13(v096_96_bites_32by24_video_buffer_5_out_14),
    .col14(v096_96_bites_32by24_video_buffer_5_out_18), .col15(v096_96_bites_32by24_video_buffer_5_out_22),
    .col16(v096_96_bites_32by24_video_buffer_5_out_26), .col17(v096_96_bites_32by24_video_buffer_5_out_30),
    .col18(v096_96_bites_32by24_video_buffer_5_out_11), .col19(v096_96_bites_32by24_video_buffer_5_out_15),
    .col20(v096_96_bites_32by24_video_buffer_5_out_19), .col21(v096_96_bites_32by24_video_buffer_5_out_23),
    .col22(v096_96_bites_32by24_video_buffer_5_out_27), .col23(v096_96_bites_32by24_video_buffer_5_out_31));
  DotMatrix #(.matrixcols(24), .matrixrows(32)) dotmatrix_6 (
    .col0(v096_96_bites_32by24_video_buffer_6_out_8), .col1(v096_96_bites_32by24_video_buffer_6_out_12),
    .col2(v096_96_bites_32by24_video_buffer_6_out_16), .col3(v096_96_bites_32by24_video_buffer_6_out_20),
    .col4(v096_96_bites_32by24_video_buffer_6_out_24), .col5(v096_96_bites_32by24_video_buffer_6_out_28),
    .col6(v096_96_bites_32by24_video_buffer_6_out_9), .col7(v096_96_bites_32by24_video_buffer_6_out_13),
    .col8(v096_96_bites_32by24_video_buffer_6_out_17), .col9(v096_96_bites_32by24_video_buffer_6_out_21),
    .col10(v096_96_bites_32by24_video_buffer_6_out_25), .col11(v096_96_bites_32by24_video_buffer_6_out_29),
    .col12(v096_96_bites_32by24_video_buffer_6_out_10), .col13(v096_96_bites_32by24_video_buffer_6_out_14),
    .col14(v096_96_bites_32by24_video_buffer_6_out_18), .col15(v096_96_bites_32by24_video_buffer_6_out_22),
    .col16(v096_96_bites_32by24_video_buffer_6_out_26), .col17(v096_96_bites_32by24_video_buffer_6_out_30),
    .col18(v096_96_bites_32by24_video_buffer_6_out_11), .col19(v096_96_bites_32by24_video_buffer_6_out_15),
    .col20(v096_96_bites_32by24_video_buffer_6_out_19), .col21(v096_96_bites_32by24_video_buffer_6_out_23),
    .col22(v096_96_bites_32by24_video_buffer_6_out_27), .col23(v096_96_bites_32by24_video_buffer_6_out_31));
  Button c (.out(c_out[0]));
  Button d (.out(c_out[1]));
  Button e (.out(c_out[2]));
  Button f (.out(c_out[3]));
  Multiplexer #(.disabled(0), .enable("false")) multiplexer_5 (
    .in0(control_1_out_17[4]), .in1(1'b0), .out(multiplexer_5_out), .sel(register_5_q));
  V096_96_Bites_32By24_Video_Buffer v096_96_bites_32by24_video_buffer_4 (
    .out_8(v096_96_bites_32by24_video_buffer_4_out_8), .out_9(v096_96_bites_32by24_video_buffer_4_out_9),
    .out_10(v096_96_bites_32by24_video_buffer_4_out_10), .out_11(v096_96_bites_32by24_video_buffer_4_out_11),
    .out_12(v096_96_bites_32by24_video_buffer_4_out_12), .out_13(v096_96_bites_32by24_video_buffer_4_out_13),
    .out_14(v096_96_bites_32by24_video_buffer_4_out_14), .out_15(v096_96_bites_32by24_video_buffer_4_out_15),
    .out_16(v096_96_bites_32by24_video_buffer_4_out_16), .out_17(v096_96_bites_32by24_video_buffer_4_out_17),
    .out_18(v096_96_bites_32by24_video_buffer_4_out_18), .out_19(v096_96_bites_32by24_video_buffer_4_out_19),
    .out_20(v096_96_bites_32by24_video_buffer_4_out_20), .out_21(v096_96_bites_32by24_video_buffer_4_out_21),
    .out_22(v096_96_bites_32by24_video_buffer_4_out_22), .out_23(v096_96_bites_32by24_video_buffer_4_out_23),
    .out_24(v096_96_bites_32by24_video_buffer_4_out_24), .out_25(v096_96_bites_32by24_video_buffer_4_out_25),
    .out_26(v096_96_bites_32by24_video_buffer_4_out_26), .out_27(v096_96_bites_32by24_video_buffer_4_out_27),
    .out_28(v096_96_bites_32by24_video_buffer_4_out_28), .out_29(v096_96_bites_32by24_video_buffer_4_out_29),
    .out_30(v096_96_bites_32by24_video_buffer_4_out_30), .out_31(v096_96_bites_32by24_video_buffer_4_out_31),
    .in_1(decoder_1_out1), .in_2(video_card_120_x_96_1_out_6), .in_3(video_card_120_x_96_1_out_5),
    .in_4(video_card_120_x_96_1_out_7), .in_5(video_card_120_x_96_1_out_8), .in_6(clock_1_out_25),
    .in_7(video_card_120_x_96_1__0));
  V096_96_Bites_32By24_Video_Buffer v096_96_bites_32by24_video_buffer_5 (
    .out_8(v096_96_bites_32by24_video_buffer_5_out_8), .out_9(v096_96_bites_32by24_video_buffer_5_out_9),
    .out_10(v096_96_bites_32by24_video_buffer_5_out_10), .out_11(v096_96_bites_32by24_video_buffer_5_out_11),
    .out_12(v096_96_bites_32by24_video_buffer_5_out_12), .out_13(v096_96_bites_32by24_video_buffer_5_out_13),
    .out_14(v096_96_bites_32by24_video_buffer_5_out_14), .out_15(v096_96_bites_32by24_video_buffer_5_out_15),
    .out_16(v096_96_bites_32by24_video_buffer_5_out_16), .out_17(v096_96_bites_32by24_video_buffer_5_out_17),
    .out_18(v096_96_bites_32by24_video_buffer_5_out_18), .out_19(v096_96_bites_32by24_video_buffer_5_out_19),
    .out_20(v096_96_bites_32by24_video_buffer_5_out_20), .out_21(v096_96_bites_32by24_video_buffer_5_out_21),
    .out_22(v096_96_bites_32by24_video_buffer_5_out_22), .out_23(v096_96_bites_32by24_video_buffer_5_out_23),
    .out_24(v096_96_bites_32by24_video_buffer_5_out_24), .out_25(v096_96_bites_32by24_video_buffer_5_out_25),
    .out_26(v096_96_bites_32by24_video_buffer_5_out_26), .out_27(v096_96_bites_32by24_video_buffer_5_out_27),
    .out_28(v096_96_bites_32by24_video_buffer_5_out_28), .out_29(v096_96_bites_32by24_video_buffer_5_out_29),
    .out_30(v096_96_bites_32by24_video_buffer_5_out_30), .out_31(v096_96_bites_32by24_video_buffer_5_out_31),
    .in_1(decoder_2_out1), .in_2(video_card_120_x_96_1_out_6), .in_3(video_card_120_x_96_1_out_5),
    .in_4(video_card_120_x_96_1_out_7), .in_5(video_card_120_x_96_1_out_8), .in_6(clock_1_out_25),
    .in_7(video_card_120_x_96_1__0));
  V096_96_Bites_32By24_Video_Buffer v096_96_bites_32by24_video_buffer_6 (
    .out_8(v096_96_bites_32by24_video_buffer_6_out_8), .out_9(v096_96_bites_32by24_video_buffer_6_out_9),
    .out_10(v096_96_bites_32by24_video_buffer_6_out_10), .out_11(v096_96_bites_32by24_video_buffer_6_out_11),
    .out_12(v096_96_bites_32by24_video_buffer_6_out_12), .out_13(v096_96_bites_32by24_video_buffer_6_out_13),
    .out_14(v096_96_bites_32by24_video_buffer_6_out_14), .out_15(v096_96_bites_32by24_video_buffer_6_out_15),
    .out_16(v096_96_bites_32by24_video_buffer_6_out_16), .out_17(v096_96_bites_32by24_video_buffer_6_out_17),
    .out_18(v096_96_bites_32by24_video_buffer_6_out_18), .out_19(v096_96_bites_32by24_video_buffer_6_out_19),
    .out_20(v096_96_bites_32by24_video_buffer_6_out_20), .out_21(v096_96_bites_32by24_video_buffer_6_out_21),
    .out_22(v096_96_bites_32by24_video_buffer_6_out_22), .out_23(v096_96_bites_32by24_video_buffer_6_out_23),
    .out_24(v096_96_bites_32by24_video_buffer_6_out_24), .out_25(v096_96_bites_32by24_video_buffer_6_out_25),
    .out_26(v096_96_bites_32by24_video_buffer_6_out_26), .out_27(v096_96_bites_32by24_video_buffer_6_out_27),
    .out_28(v096_96_bites_32by24_video_buffer_6_out_28), .out_29(v096_96_bites_32by24_video_buffer_6_out_29),
    .out_30(v096_96_bites_32by24_video_buffer_6_out_30), .out_31(v096_96_bites_32by24_video_buffer_6_out_31),
    .in_1(decoder_3_out1), .in_2(video_card_120_x_96_1_out_6), .in_3(video_card_120_x_96_1_out_5),
    .in_4(video_card_120_x_96_1_out_7), .in_5(video_card_120_x_96_1_out_8), .in_6(clock_1_out_25),
    .in_7(video_card_120_x_96_1__0));
  LED Int_Enabled (.in(kb_io_1_out_11));
  Register #(.width(12)) u_PC (
    .D(multiplexer_12_out), .en(multiplexer_5_out), .Q(PC), .clk(clock_1_out_25), .clr(control_1_out_17[3]));
  Register #(.width(16)) Ins_Acc (
    .D(multiplexer_26_out), .en(clock_1_out_32), .Q(Instruc), .clk(clock_1_out_25));  // open: clr
  Multiplexer #(.width(12), .enable("false")) multiplexer_6 (
    .in0({12{1'b0}}), .in1(PC), .out(multiplexer_6_out), .sel(control_1_out_17[2]));
  Multiplexer #(.width(16), .enable("false")) multiplexer_7 (
    .in0({16{1'b0}}), .in1(Instruc), .out(multiplexer_7_out), .sel(clock_1_out_33));
  DotMatrix #(.matrixcols(24), .matrixrows(32)) dotmatrix_7 (
    .col0(v096_96_bites_32by24_video_buffer_7_out_8), .col1(v096_96_bites_32by24_video_buffer_7_out_12),
    .col2(v096_96_bites_32by24_video_buffer_7_out_16), .col3(v096_96_bites_32by24_video_buffer_7_out_20),
    .col4(v096_96_bites_32by24_video_buffer_7_out_24), .col5(v096_96_bites_32by24_video_buffer_7_out_28),
    .col6(v096_96_bites_32by24_video_buffer_7_out_9), .col7(v096_96_bites_32by24_video_buffer_7_out_13),
    .col8(v096_96_bites_32by24_video_buffer_7_out_17), .col9(v096_96_bites_32by24_video_buffer_7_out_21),
    .col10(v096_96_bites_32by24_video_buffer_7_out_25), .col11(v096_96_bites_32by24_video_buffer_7_out_29),
    .col12(v096_96_bites_32by24_video_buffer_7_out_10), .col13(v096_96_bites_32by24_video_buffer_7_out_14),
    .col14(v096_96_bites_32by24_video_buffer_7_out_18), .col15(v096_96_bites_32by24_video_buffer_7_out_22),
    .col16(v096_96_bites_32by24_video_buffer_7_out_26), .col17(v096_96_bites_32by24_video_buffer_7_out_30),
    .col18(v096_96_bites_32by24_video_buffer_7_out_11), .col19(v096_96_bites_32by24_video_buffer_7_out_15),
    .col20(v096_96_bites_32by24_video_buffer_7_out_19), .col21(v096_96_bites_32by24_video_buffer_7_out_23),
    .col22(v096_96_bites_32by24_video_buffer_7_out_27), .col23(v096_96_bites_32by24_video_buffer_7_out_31));
  DotMatrix #(.matrixcols(24), .matrixrows(32)) dotmatrix_8 (
    .col0(v096_96_bites_32by24_video_buffer_8_out_8), .col1(v096_96_bites_32by24_video_buffer_8_out_12),
    .col2(v096_96_bites_32by24_video_buffer_8_out_16), .col3(v096_96_bites_32by24_video_buffer_8_out_20),
    .col4(v096_96_bites_32by24_video_buffer_8_out_24), .col5(v096_96_bites_32by24_video_buffer_8_out_28),
    .col6(v096_96_bites_32by24_video_buffer_8_out_9), .col7(v096_96_bites_32by24_video_buffer_8_out_13),
    .col8(v096_96_bites_32by24_video_buffer_8_out_17), .col9(v096_96_bites_32by24_video_buffer_8_out_21),
    .col10(v096_96_bites_32by24_video_buffer_8_out_25), .col11(v096_96_bites_32by24_video_buffer_8_out_29),
    .col12(v096_96_bites_32by24_video_buffer_8_out_10), .col13(v096_96_bites_32by24_video_buffer_8_out_14),
    .col14(v096_96_bites_32by24_video_buffer_8_out_18), .col15(v096_96_bites_32by24_video_buffer_8_out_22),
    .col16(v096_96_bites_32by24_video_buffer_8_out_26), .col17(v096_96_bites_32by24_video_buffer_8_out_30),
    .col18(v096_96_bites_32by24_video_buffer_8_out_11), .col19(v096_96_bites_32by24_video_buffer_8_out_15),
    .col20(v096_96_bites_32by24_video_buffer_8_out_19), .col21(v096_96_bites_32by24_video_buffer_8_out_23),
    .col22(v096_96_bites_32by24_video_buffer_8_out_27), .col23(v096_96_bites_32by24_video_buffer_8_out_31));
  DotMatrix #(.matrixcols(24), .matrixrows(32)) dotmatrix_9 (
    .col0(v096_96_bites_32by24_video_buffer_9_out_8), .col1(v096_96_bites_32by24_video_buffer_9_out_12),
    .col2(v096_96_bites_32by24_video_buffer_9_out_16), .col3(v096_96_bites_32by24_video_buffer_9_out_20),
    .col4(v096_96_bites_32by24_video_buffer_9_out_24), .col5(v096_96_bites_32by24_video_buffer_9_out_28),
    .col6(v096_96_bites_32by24_video_buffer_9_out_9), .col7(v096_96_bites_32by24_video_buffer_9_out_13),
    .col8(v096_96_bites_32by24_video_buffer_9_out_17), .col9(v096_96_bites_32by24_video_buffer_9_out_21),
    .col10(v096_96_bites_32by24_video_buffer_9_out_25), .col11(v096_96_bites_32by24_video_buffer_9_out_29),
    .col12(v096_96_bites_32by24_video_buffer_9_out_10), .col13(v096_96_bites_32by24_video_buffer_9_out_14),
    .col14(v096_96_bites_32by24_video_buffer_9_out_18), .col15(v096_96_bites_32by24_video_buffer_9_out_22),
    .col16(v096_96_bites_32by24_video_buffer_9_out_26), .col17(v096_96_bites_32by24_video_buffer_9_out_30),
    .col18(v096_96_bites_32by24_video_buffer_9_out_11), .col19(v096_96_bites_32by24_video_buffer_9_out_15),
    .col20(v096_96_bites_32by24_video_buffer_9_out_19), .col21(v096_96_bites_32by24_video_buffer_9_out_23),
    .col22(v096_96_bites_32by24_video_buffer_9_out_27), .col23(v096_96_bites_32by24_video_buffer_9_out_31));
  LED Int (.in(clock_1_out_20));
  Multiplexer #(.width(12), .enable("false")) multiplexer_8 (
    .in0({12{1'b0}}), .in1(PC), .out({multiplexer_8_out_2, multiplexer_8_out}), .sel(control_1_out_17[1]));
  Multiplexer #(.width(16), .enable("false")) multiplexer_9 (
    .in0({16{1'b0}}), .in1(Instruc), .out(multiplexer_9_out), .sel(control_1_out_18[2]));
  V096_96_Bites_32By24_Video_Buffer v096_96_bites_32by24_video_buffer_7 (
    .out_8(v096_96_bites_32by24_video_buffer_7_out_8), .out_9(v096_96_bites_32by24_video_buffer_7_out_9),
    .out_10(v096_96_bites_32by24_video_buffer_7_out_10), .out_11(v096_96_bites_32by24_video_buffer_7_out_11),
    .out_12(v096_96_bites_32by24_video_buffer_7_out_12), .out_13(v096_96_bites_32by24_video_buffer_7_out_13),
    .out_14(v096_96_bites_32by24_video_buffer_7_out_14), .out_15(v096_96_bites_32by24_video_buffer_7_out_15),
    .out_16(v096_96_bites_32by24_video_buffer_7_out_16), .out_17(v096_96_bites_32by24_video_buffer_7_out_17),
    .out_18(v096_96_bites_32by24_video_buffer_7_out_18), .out_19(v096_96_bites_32by24_video_buffer_7_out_19),
    .out_20(v096_96_bites_32by24_video_buffer_7_out_20), .out_21(v096_96_bites_32by24_video_buffer_7_out_21),
    .out_22(v096_96_bites_32by24_video_buffer_7_out_22), .out_23(v096_96_bites_32by24_video_buffer_7_out_23),
    .out_24(v096_96_bites_32by24_video_buffer_7_out_24), .out_25(v096_96_bites_32by24_video_buffer_7_out_25),
    .out_26(v096_96_bites_32by24_video_buffer_7_out_26), .out_27(v096_96_bites_32by24_video_buffer_7_out_27),
    .out_28(v096_96_bites_32by24_video_buffer_7_out_28), .out_29(v096_96_bites_32by24_video_buffer_7_out_29),
    .out_30(v096_96_bites_32by24_video_buffer_7_out_30), .out_31(v096_96_bites_32by24_video_buffer_7_out_31),
    .in_1(decoder_1_out2), .in_2(video_card_120_x_96_1_out_6), .in_3(video_card_120_x_96_1_out_5),
    .in_4(video_card_120_x_96_1_out_7), .in_5(video_card_120_x_96_1_out_8), .in_6(clock_1_out_25),
    .in_7(video_card_120_x_96_1__0));
  V096_96_Bites_32By24_Video_Buffer v096_96_bites_32by24_video_buffer_8 (
    .out_8(v096_96_bites_32by24_video_buffer_8_out_8), .out_9(v096_96_bites_32by24_video_buffer_8_out_9),
    .out_10(v096_96_bites_32by24_video_buffer_8_out_10), .out_11(v096_96_bites_32by24_video_buffer_8_out_11),
    .out_12(v096_96_bites_32by24_video_buffer_8_out_12), .out_13(v096_96_bites_32by24_video_buffer_8_out_13),
    .out_14(v096_96_bites_32by24_video_buffer_8_out_14), .out_15(v096_96_bites_32by24_video_buffer_8_out_15),
    .out_16(v096_96_bites_32by24_video_buffer_8_out_16), .out_17(v096_96_bites_32by24_video_buffer_8_out_17),
    .out_18(v096_96_bites_32by24_video_buffer_8_out_18), .out_19(v096_96_bites_32by24_video_buffer_8_out_19),
    .out_20(v096_96_bites_32by24_video_buffer_8_out_20), .out_21(v096_96_bites_32by24_video_buffer_8_out_21),
    .out_22(v096_96_bites_32by24_video_buffer_8_out_22), .out_23(v096_96_bites_32by24_video_buffer_8_out_23),
    .out_24(v096_96_bites_32by24_video_buffer_8_out_24), .out_25(v096_96_bites_32by24_video_buffer_8_out_25),
    .out_26(v096_96_bites_32by24_video_buffer_8_out_26), .out_27(v096_96_bites_32by24_video_buffer_8_out_27),
    .out_28(v096_96_bites_32by24_video_buffer_8_out_28), .out_29(v096_96_bites_32by24_video_buffer_8_out_29),
    .out_30(v096_96_bites_32by24_video_buffer_8_out_30), .out_31(v096_96_bites_32by24_video_buffer_8_out_31),
    .in_1(decoder_2_out2), .in_2(video_card_120_x_96_1_out_6), .in_3(video_card_120_x_96_1_out_5),
    .in_4(video_card_120_x_96_1_out_7), .in_5(video_card_120_x_96_1_out_8), .in_6(clock_1_out_25),
    .in_7(video_card_120_x_96_1__0));
  V096_96_Bites_32By24_Video_Buffer v096_96_bites_32by24_video_buffer_9 (
    .out_8(v096_96_bites_32by24_video_buffer_9_out_8), .out_9(v096_96_bites_32by24_video_buffer_9_out_9),
    .out_10(v096_96_bites_32by24_video_buffer_9_out_10), .out_11(v096_96_bites_32by24_video_buffer_9_out_11),
    .out_12(v096_96_bites_32by24_video_buffer_9_out_12), .out_13(v096_96_bites_32by24_video_buffer_9_out_13),
    .out_14(v096_96_bites_32by24_video_buffer_9_out_14), .out_15(v096_96_bites_32by24_video_buffer_9_out_15),
    .out_16(v096_96_bites_32by24_video_buffer_9_out_16), .out_17(v096_96_bites_32by24_video_buffer_9_out_17),
    .out_18(v096_96_bites_32by24_video_buffer_9_out_18), .out_19(v096_96_bites_32by24_video_buffer_9_out_19),
    .out_20(v096_96_bites_32by24_video_buffer_9_out_20), .out_21(v096_96_bites_32by24_video_buffer_9_out_21),
    .out_22(v096_96_bites_32by24_video_buffer_9_out_22), .out_23(v096_96_bites_32by24_video_buffer_9_out_23),
    .out_24(v096_96_bites_32by24_video_buffer_9_out_24), .out_25(v096_96_bites_32by24_video_buffer_9_out_25),
    .out_26(v096_96_bites_32by24_video_buffer_9_out_26), .out_27(v096_96_bites_32by24_video_buffer_9_out_27),
    .out_28(v096_96_bites_32by24_video_buffer_9_out_28), .out_29(v096_96_bites_32by24_video_buffer_9_out_29),
    .out_30(v096_96_bites_32by24_video_buffer_9_out_30), .out_31(v096_96_bites_32by24_video_buffer_9_out_31),
    .in_1(decoder_3_out2), .in_2(video_card_120_x_96_1_out_6), .in_3(video_card_120_x_96_1_out_5),
    .in_4(video_card_120_x_96_1_out_7), .in_5(video_card_120_x_96_1_out_8), .in_6(clock_1_out_25),
    .in_7(video_card_120_x_96_1__0));
  Multiplexer #(.width(12), .enable("false")) multiplexer_10 (
    .in0({12{1'b0}}), .in1(PC), .out(multiplexer_10_out), .sel(control_1_out_17[0]));
  Multiplexer #(.width(16), .enable("false")) multiplexer_11 (
    .in0({16{1'b0}}), .in1(Instruc), .out(multiplexer_11_out), .sel(control_1_out_18[1]));
  DotMatrix #(.matrixcols(24), .matrixrows(32)) dotmatrix_10 (
    .col0(v096_96_bites_32by24_video_buffer_10_out_8), .col1(v096_96_bites_32by24_video_buffer_10_out_12),
    .col2(v096_96_bites_32by24_video_buffer_10_out_16), .col3(v096_96_bites_32by24_video_buffer_10_out_20),
    .col4(v096_96_bites_32by24_video_buffer_10_out_24), .col5(v096_96_bites_32by24_video_buffer_10_out_28),
    .col6(v096_96_bites_32by24_video_buffer_10_out_9), .col7(v096_96_bites_32by24_video_buffer_10_out_13),
    .col8(v096_96_bites_32by24_video_buffer_10_out_17), .col9(v096_96_bites_32by24_video_buffer_10_out_21),
    .col10(v096_96_bites_32by24_video_buffer_10_out_25), .col11(v096_96_bites_32by24_video_buffer_10_out_29),
    .col12(v096_96_bites_32by24_video_buffer_10_out_10), .col13(v096_96_bites_32by24_video_buffer_10_out_14),
    .col14(v096_96_bites_32by24_video_buffer_10_out_18), .col15(v096_96_bites_32by24_video_buffer_10_out_22),
    .col16(v096_96_bites_32by24_video_buffer_10_out_26), .col17(v096_96_bites_32by24_video_buffer_10_out_30),
    .col18(v096_96_bites_32by24_video_buffer_10_out_11), .col19(v096_96_bites_32by24_video_buffer_10_out_15),
    .col20(v096_96_bites_32by24_video_buffer_10_out_19), .col21(v096_96_bites_32by24_video_buffer_10_out_23),
    .col22(v096_96_bites_32by24_video_buffer_10_out_27), .col23(v096_96_bites_32by24_video_buffer_10_out_31));
  DotMatrix #(.matrixcols(24), .matrixrows(32)) dotmatrix_11 (
    .col0(v096_96_bites_32by24_video_buffer_11_out_8), .col1(v096_96_bites_32by24_video_buffer_11_out_12),
    .col2(v096_96_bites_32by24_video_buffer_11_out_16), .col3(v096_96_bites_32by24_video_buffer_11_out_20),
    .col4(v096_96_bites_32by24_video_buffer_11_out_24), .col5(v096_96_bites_32by24_video_buffer_11_out_28),
    .col6(v096_96_bites_32by24_video_buffer_11_out_9), .col7(v096_96_bites_32by24_video_buffer_11_out_13),
    .col8(v096_96_bites_32by24_video_buffer_11_out_17), .col9(v096_96_bites_32by24_video_buffer_11_out_21),
    .col10(v096_96_bites_32by24_video_buffer_11_out_25), .col11(v096_96_bites_32by24_video_buffer_11_out_29),
    .col12(v096_96_bites_32by24_video_buffer_11_out_10), .col13(v096_96_bites_32by24_video_buffer_11_out_14),
    .col14(v096_96_bites_32by24_video_buffer_11_out_18), .col15(v096_96_bites_32by24_video_buffer_11_out_22),
    .col16(v096_96_bites_32by24_video_buffer_11_out_26), .col17(v096_96_bites_32by24_video_buffer_11_out_30),
    .col18(v096_96_bites_32by24_video_buffer_11_out_11), .col19(v096_96_bites_32by24_video_buffer_11_out_15),
    .col20(v096_96_bites_32by24_video_buffer_11_out_19), .col21(v096_96_bites_32by24_video_buffer_11_out_23),
    .col22(v096_96_bites_32by24_video_buffer_11_out_27), .col23(v096_96_bites_32by24_video_buffer_11_out_31));
  DotMatrix #(.matrixcols(24), .matrixrows(32)) dotmatrix_12 (
    .col0(v096_96_bites_32by24_video_buffer_12_out_8), .col1(v096_96_bites_32by24_video_buffer_12_out_12),
    .col2(v096_96_bites_32by24_video_buffer_12_out_16), .col3(v096_96_bites_32by24_video_buffer_12_out_20),
    .col4(v096_96_bites_32by24_video_buffer_12_out_24), .col5(v096_96_bites_32by24_video_buffer_12_out_28),
    .col6(v096_96_bites_32by24_video_buffer_12_out_9), .col7(v096_96_bites_32by24_video_buffer_12_out_13),
    .col8(v096_96_bites_32by24_video_buffer_12_out_17), .col9(v096_96_bites_32by24_video_buffer_12_out_21),
    .col10(v096_96_bites_32by24_video_buffer_12_out_25), .col11(v096_96_bites_32by24_video_buffer_12_out_29),
    .col12(v096_96_bites_32by24_video_buffer_12_out_10), .col13(v096_96_bites_32by24_video_buffer_12_out_14),
    .col14(v096_96_bites_32by24_video_buffer_12_out_18), .col15(v096_96_bites_32by24_video_buffer_12_out_22),
    .col16(v096_96_bites_32by24_video_buffer_12_out_26), .col17(v096_96_bites_32by24_video_buffer_12_out_30),
    .col18(v096_96_bites_32by24_video_buffer_12_out_11), .col19(v096_96_bites_32by24_video_buffer_12_out_15),
    .col20(v096_96_bites_32by24_video_buffer_12_out_19), .col21(v096_96_bites_32by24_video_buffer_12_out_23),
    .col22(v096_96_bites_32by24_video_buffer_12_out_27), .col23(v096_96_bites_32by24_video_buffer_12_out_31));
  KB_IO kb_io_1 (
    .in_1(adder_4_out), .C(clock_1_out_25), .W_Ram(control_1_out_21), .out_9(Data), .out_11(kb_io_1_out_11),
    .in_5(c_out), .in_6(_8_out), .in_7(_4_out), .in_8(_0_out), .Enable_IO_mt(kb_io_1_enable_io_mt),
    .IO_Int(clock_1_out_19), .out_12(kb_io_1_out_12));
  Registers registers_1 (
    .in_1(control_1_out_11), .in_2(control_1_out_12), .in_3(control_1_out_13), .in_4(control_1_out_14),
    .in_5(control_1_out_15), .in_6(control_1_out_16), .in_7(multiplexer_3_out), .in_8(multiplexer_4_out),
    .in_9(clock_1_out_25), .out_10(registers_1_out_10), .out_11(registers_1_out_11),
    .out_12(registers_1_out_12), .out_13(registers_1_out_13), .out_14(registers_1_out_14));
  Control control_1 (
    .out_16(control_1_out_16), .out_15(control_1_out_15), .out_14(control_1_out_14),
    .out_13(control_1_out_13), .out_12(control_1_out_12), .out_11(control_1_out_11),
    .out_21(control_1_out_21), .out_22(control_1_out_22), .out_23(control_1_out_23),
    .out_24(control_1_out_24), .in_3(multiplexer_7_out), .in_8(clock_1_out_30), .in_9(clock_1_out_31),
    .out_18(control_1_out_18), .out_10(control_1_out_10), .out_20(control_1_out_20),
    .out_19(control_1_out_19), .in_2(alu_1_out_8), .out_17(control_1_out_17), .in_7(clock_1_out_29),
    .in_6(clock_1_out_28), .in_5(clock_1_out_27), .in_4(clock_1_out_26), .out_25(control_1_out_25),
    .in_1(alu_1_out_9));
  Multiplexer #(.width(12), .enable("false")) multiplexer_12 (
    .in0(or_8_out), .in1(adder_1_out), .out(multiplexer_12_out), .sel(control_1_out_17[0]));
  Adder #(.width(12)) adder_1 (.a(12'h2), .b(multiplexer_10_out), .out(adder_1_out));  // open: cin, cout
  V096_96_Bites_32By24_Video_Buffer v096_96_bites_32by24_video_buffer_10 (
    .out_8(v096_96_bites_32by24_video_buffer_10_out_8), .out_9(v096_96_bites_32by24_video_buffer_10_out_9),
    .out_10(v096_96_bites_32by24_video_buffer_10_out_10),
    .out_11(v096_96_bites_32by24_video_buffer_10_out_11),
    .out_12(v096_96_bites_32by24_video_buffer_10_out_12),
    .out_13(v096_96_bites_32by24_video_buffer_10_out_13),
    .out_14(v096_96_bites_32by24_video_buffer_10_out_14),
    .out_15(v096_96_bites_32by24_video_buffer_10_out_15),
    .out_16(v096_96_bites_32by24_video_buffer_10_out_16),
    .out_17(v096_96_bites_32by24_video_buffer_10_out_17),
    .out_18(v096_96_bites_32by24_video_buffer_10_out_18),
    .out_19(v096_96_bites_32by24_video_buffer_10_out_19),
    .out_20(v096_96_bites_32by24_video_buffer_10_out_20),
    .out_21(v096_96_bites_32by24_video_buffer_10_out_21),
    .out_22(v096_96_bites_32by24_video_buffer_10_out_22),
    .out_23(v096_96_bites_32by24_video_buffer_10_out_23),
    .out_24(v096_96_bites_32by24_video_buffer_10_out_24),
    .out_25(v096_96_bites_32by24_video_buffer_10_out_25),
    .out_26(v096_96_bites_32by24_video_buffer_10_out_26),
    .out_27(v096_96_bites_32by24_video_buffer_10_out_27),
    .out_28(v096_96_bites_32by24_video_buffer_10_out_28),
    .out_29(v096_96_bites_32by24_video_buffer_10_out_29),
    .out_30(v096_96_bites_32by24_video_buffer_10_out_30),
    .out_31(v096_96_bites_32by24_video_buffer_10_out_31), .in_1(decoder_1_out3),
    .in_2(video_card_120_x_96_1_out_6), .in_3(video_card_120_x_96_1_out_5),
    .in_4(video_card_120_x_96_1_out_7), .in_5(video_card_120_x_96_1_out_8), .in_6(clock_1_out_25),
    .in_7(video_card_120_x_96_1__0));
  V096_96_Bites_32By24_Video_Buffer v096_96_bites_32by24_video_buffer_11 (
    .out_8(v096_96_bites_32by24_video_buffer_11_out_8), .out_9(v096_96_bites_32by24_video_buffer_11_out_9),
    .out_10(v096_96_bites_32by24_video_buffer_11_out_10),
    .out_11(v096_96_bites_32by24_video_buffer_11_out_11),
    .out_12(v096_96_bites_32by24_video_buffer_11_out_12),
    .out_13(v096_96_bites_32by24_video_buffer_11_out_13),
    .out_14(v096_96_bites_32by24_video_buffer_11_out_14),
    .out_15(v096_96_bites_32by24_video_buffer_11_out_15),
    .out_16(v096_96_bites_32by24_video_buffer_11_out_16),
    .out_17(v096_96_bites_32by24_video_buffer_11_out_17),
    .out_18(v096_96_bites_32by24_video_buffer_11_out_18),
    .out_19(v096_96_bites_32by24_video_buffer_11_out_19),
    .out_20(v096_96_bites_32by24_video_buffer_11_out_20),
    .out_21(v096_96_bites_32by24_video_buffer_11_out_21),
    .out_22(v096_96_bites_32by24_video_buffer_11_out_22),
    .out_23(v096_96_bites_32by24_video_buffer_11_out_23),
    .out_24(v096_96_bites_32by24_video_buffer_11_out_24),
    .out_25(v096_96_bites_32by24_video_buffer_11_out_25),
    .out_26(v096_96_bites_32by24_video_buffer_11_out_26),
    .out_27(v096_96_bites_32by24_video_buffer_11_out_27),
    .out_28(v096_96_bites_32by24_video_buffer_11_out_28),
    .out_29(v096_96_bites_32by24_video_buffer_11_out_29),
    .out_30(v096_96_bites_32by24_video_buffer_11_out_30),
    .out_31(v096_96_bites_32by24_video_buffer_11_out_31), .in_1(decoder_2_out3),
    .in_2(video_card_120_x_96_1_out_6), .in_3(video_card_120_x_96_1_out_5),
    .in_4(video_card_120_x_96_1_out_7), .in_5(video_card_120_x_96_1_out_8), .in_6(clock_1_out_25),
    .in_7(video_card_120_x_96_1__0));
  V096_96_Bites_32By24_Video_Buffer v096_96_bites_32by24_video_buffer_12 (
    .out_8(v096_96_bites_32by24_video_buffer_12_out_8), .out_9(v096_96_bites_32by24_video_buffer_12_out_9),
    .out_10(v096_96_bites_32by24_video_buffer_12_out_10),
    .out_11(v096_96_bites_32by24_video_buffer_12_out_11),
    .out_12(v096_96_bites_32by24_video_buffer_12_out_12),
    .out_13(v096_96_bites_32by24_video_buffer_12_out_13),
    .out_14(v096_96_bites_32by24_video_buffer_12_out_14),
    .out_15(v096_96_bites_32by24_video_buffer_12_out_15),
    .out_16(v096_96_bites_32by24_video_buffer_12_out_16),
    .out_17(v096_96_bites_32by24_video_buffer_12_out_17),
    .out_18(v096_96_bites_32by24_video_buffer_12_out_18),
    .out_19(v096_96_bites_32by24_video_buffer_12_out_19),
    .out_20(v096_96_bites_32by24_video_buffer_12_out_20),
    .out_21(v096_96_bites_32by24_video_buffer_12_out_21),
    .out_22(v096_96_bites_32by24_video_buffer_12_out_22),
    .out_23(v096_96_bites_32by24_video_buffer_12_out_23),
    .out_24(v096_96_bites_32by24_video_buffer_12_out_24),
    .out_25(v096_96_bites_32by24_video_buffer_12_out_25),
    .out_26(v096_96_bites_32by24_video_buffer_12_out_26),
    .out_27(v096_96_bites_32by24_video_buffer_12_out_27),
    .out_28(v096_96_bites_32by24_video_buffer_12_out_28),
    .out_29(v096_96_bites_32by24_video_buffer_12_out_29),
    .out_30(v096_96_bites_32by24_video_buffer_12_out_30),
    .out_31(v096_96_bites_32by24_video_buffer_12_out_31), .in_1(decoder_3_out3),
    .in_2(video_card_120_x_96_1_out_6), .in_3(video_card_120_x_96_1_out_5),
    .in_4(video_card_120_x_96_1_out_7), .in_5(video_card_120_x_96_1_out_8), .in_6(clock_1_out_25),
    .in_7(video_card_120_x_96_1__0));
  Multiplexer #(.width(16), .enable("false")) multiplexer_13 (
    .in0({16{1'b0}}), .in1(Instruc), .out(multiplexer_13_out), .sel(control_1_out_18[0]));
  assign or_6_out = registers_1_out_14[11:0] | multiplexer_6_out;  // OR_Gate or_6, 12 bits wide
  DotMatrix #(.matrixcols(24), .matrixrows(32)) dotmatrix_13 (
    .col0(v096_96_bites_32by24_video_buffer_13_out_8), .col1(v096_96_bites_32by24_video_buffer_13_out_12),
    .col2(v096_96_bites_32by24_video_buffer_13_out_16), .col3(v096_96_bites_32by24_video_buffer_13_out_20),
    .col4(v096_96_bites_32by24_video_buffer_13_out_24), .col5(v096_96_bites_32by24_video_buffer_13_out_28),
    .col6(v096_96_bites_32by24_video_buffer_13_out_9), .col7(v096_96_bites_32by24_video_buffer_13_out_13),
    .col8(v096_96_bites_32by24_video_buffer_13_out_17), .col9(v096_96_bites_32by24_video_buffer_13_out_21),
    .col10(v096_96_bites_32by24_video_buffer_13_out_25), .col11(v096_96_bites_32by24_video_buffer_13_out_29),
    .col12(v096_96_bites_32by24_video_buffer_13_out_10), .col13(v096_96_bites_32by24_video_buffer_13_out_14),
    .col14(v096_96_bites_32by24_video_buffer_13_out_18), .col15(v096_96_bites_32by24_video_buffer_13_out_22),
    .col16(v096_96_bites_32by24_video_buffer_13_out_26), .col17(v096_96_bites_32by24_video_buffer_13_out_30),
    .col18(v096_96_bites_32by24_video_buffer_13_out_11), .col19(v096_96_bites_32by24_video_buffer_13_out_15),
    .col20(v096_96_bites_32by24_video_buffer_13_out_19), .col21(v096_96_bites_32by24_video_buffer_13_out_23),
    .col22(v096_96_bites_32by24_video_buffer_13_out_27), .col23(v096_96_bites_32by24_video_buffer_13_out_31));
  DotMatrix #(.matrixcols(24), .matrixrows(32)) dotmatrix_14 (
    .col0(v096_96_bites_32by24_video_buffer_14_out_8), .col1(v096_96_bites_32by24_video_buffer_14_out_12),
    .col2(v096_96_bites_32by24_video_buffer_14_out_16), .col3(v096_96_bites_32by24_video_buffer_14_out_20),
    .col4(v096_96_bites_32by24_video_buffer_14_out_24), .col5(v096_96_bites_32by24_video_buffer_14_out_28),
    .col6(v096_96_bites_32by24_video_buffer_14_out_9), .col7(v096_96_bites_32by24_video_buffer_14_out_13),
    .col8(v096_96_bites_32by24_video_buffer_14_out_17), .col9(v096_96_bites_32by24_video_buffer_14_out_21),
    .col10(v096_96_bites_32by24_video_buffer_14_out_25), .col11(v096_96_bites_32by24_video_buffer_14_out_29),
    .col12(v096_96_bites_32by24_video_buffer_14_out_10), .col13(v096_96_bites_32by24_video_buffer_14_out_14),
    .col14(v096_96_bites_32by24_video_buffer_14_out_18), .col15(v096_96_bites_32by24_video_buffer_14_out_22),
    .col16(v096_96_bites_32by24_video_buffer_14_out_26), .col17(v096_96_bites_32by24_video_buffer_14_out_30),
    .col18(v096_96_bites_32by24_video_buffer_14_out_11), .col19(v096_96_bites_32by24_video_buffer_14_out_15),
    .col20(v096_96_bites_32by24_video_buffer_14_out_19), .col21(v096_96_bites_32by24_video_buffer_14_out_23),
    .col22(v096_96_bites_32by24_video_buffer_14_out_27), .col23(v096_96_bites_32by24_video_buffer_14_out_31));
  DotMatrix #(.matrixcols(24), .matrixrows(32)) dotmatrix_15 (
    .col0(v096_96_bites_32by24_video_buffer_15_out_8), .col1(v096_96_bites_32by24_video_buffer_15_out_12),
    .col2(v096_96_bites_32by24_video_buffer_15_out_16), .col3(v096_96_bites_32by24_video_buffer_15_out_20),
    .col4(v096_96_bites_32by24_video_buffer_15_out_24), .col5(v096_96_bites_32by24_video_buffer_15_out_28),
    .col6(v096_96_bites_32by24_video_buffer_15_out_9), .col7(v096_96_bites_32by24_video_buffer_15_out_13),
    .col8(v096_96_bites_32by24_video_buffer_15_out_17), .col9(v096_96_bites_32by24_video_buffer_15_out_21),
    .col10(v096_96_bites_32by24_video_buffer_15_out_25), .col11(v096_96_bites_32by24_video_buffer_15_out_29),
    .col12(v096_96_bites_32by24_video_buffer_15_out_10), .col13(v096_96_bites_32by24_video_buffer_15_out_14),
    .col14(v096_96_bites_32by24_video_buffer_15_out_18), .col15(v096_96_bites_32by24_video_buffer_15_out_22),
    .col16(v096_96_bites_32by24_video_buffer_15_out_26), .col17(v096_96_bites_32by24_video_buffer_15_out_30),
    .col18(v096_96_bites_32by24_video_buffer_15_out_11), .col19(v096_96_bites_32by24_video_buffer_15_out_15),
    .col20(v096_96_bites_32by24_video_buffer_15_out_19), .col21(v096_96_bites_32by24_video_buffer_15_out_23),
    .col22(v096_96_bites_32by24_video_buffer_15_out_27), .col23(v096_96_bites_32by24_video_buffer_15_out_31));
  V096_96_Bites_32By24_Video_Buffer v096_96_bites_32by24_video_buffer_13 (
    .out_8(v096_96_bites_32by24_video_buffer_13_out_8), .out_9(v096_96_bites_32by24_video_buffer_13_out_9),
    .out_10(v096_96_bites_32by24_video_buffer_13_out_10),
    .out_11(v096_96_bites_32by24_video_buffer_13_out_11),
    .out_12(v096_96_bites_32by24_video_buffer_13_out_12),
    .out_13(v096_96_bites_32by24_video_buffer_13_out_13),
    .out_14(v096_96_bites_32by24_video_buffer_13_out_14),
    .out_15(v096_96_bites_32by24_video_buffer_13_out_15),
    .out_16(v096_96_bites_32by24_video_buffer_13_out_16),
    .out_17(v096_96_bites_32by24_video_buffer_13_out_17),
    .out_18(v096_96_bites_32by24_video_buffer_13_out_18),
    .out_19(v096_96_bites_32by24_video_buffer_13_out_19),
    .out_20(v096_96_bites_32by24_video_buffer_13_out_20),
    .out_21(v096_96_bites_32by24_video_buffer_13_out_21),
    .out_22(v096_96_bites_32by24_video_buffer_13_out_22),
    .out_23(v096_96_bites_32by24_video_buffer_13_out_23),
    .out_24(v096_96_bites_32by24_video_buffer_13_out_24),
    .out_25(v096_96_bites_32by24_video_buffer_13_out_25),
    .out_26(v096_96_bites_32by24_video_buffer_13_out_26),
    .out_27(v096_96_bites_32by24_video_buffer_13_out_27),
    .out_28(v096_96_bites_32by24_video_buffer_13_out_28),
    .out_29(v096_96_bites_32by24_video_buffer_13_out_29),
    .out_30(v096_96_bites_32by24_video_buffer_13_out_30),
    .out_31(v096_96_bites_32by24_video_buffer_13_out_31), .in_1(decoder_1_out4),
    .in_2(video_card_120_x_96_1_out_6), .in_3(video_card_120_x_96_1_out_5),
    .in_4(video_card_120_x_96_1_out_7), .in_5(video_card_120_x_96_1_out_8), .in_6(clock_1_out_25),
    .in_7(video_card_120_x_96_1__0));
  V096_96_Bites_32By24_Video_Buffer v096_96_bites_32by24_video_buffer_14 (
    .out_8(v096_96_bites_32by24_video_buffer_14_out_8), .out_9(v096_96_bites_32by24_video_buffer_14_out_9),
    .out_10(v096_96_bites_32by24_video_buffer_14_out_10),
    .out_11(v096_96_bites_32by24_video_buffer_14_out_11),
    .out_12(v096_96_bites_32by24_video_buffer_14_out_12),
    .out_13(v096_96_bites_32by24_video_buffer_14_out_13),
    .out_14(v096_96_bites_32by24_video_buffer_14_out_14),
    .out_15(v096_96_bites_32by24_video_buffer_14_out_15),
    .out_16(v096_96_bites_32by24_video_buffer_14_out_16),
    .out_17(v096_96_bites_32by24_video_buffer_14_out_17),
    .out_18(v096_96_bites_32by24_video_buffer_14_out_18),
    .out_19(v096_96_bites_32by24_video_buffer_14_out_19),
    .out_20(v096_96_bites_32by24_video_buffer_14_out_20),
    .out_21(v096_96_bites_32by24_video_buffer_14_out_21),
    .out_22(v096_96_bites_32by24_video_buffer_14_out_22),
    .out_23(v096_96_bites_32by24_video_buffer_14_out_23),
    .out_24(v096_96_bites_32by24_video_buffer_14_out_24),
    .out_25(v096_96_bites_32by24_video_buffer_14_out_25),
    .out_26(v096_96_bites_32by24_video_buffer_14_out_26),
    .out_27(v096_96_bites_32by24_video_buffer_14_out_27),
    .out_28(v096_96_bites_32by24_video_buffer_14_out_28),
    .out_29(v096_96_bites_32by24_video_buffer_14_out_29),
    .out_30(v096_96_bites_32by24_video_buffer_14_out_30),
    .out_31(v096_96_bites_32by24_video_buffer_14_out_31), .in_1(decoder_2_out4),
    .in_2(video_card_120_x_96_1_out_6), .in_3(video_card_120_x_96_1_out_5),
    .in_4(video_card_120_x_96_1_out_7), .in_5(video_card_120_x_96_1_out_8), .in_6(clock_1_out_25),
    .in_7(video_card_120_x_96_1__0));
  V096_96_Bites_32By24_Video_Buffer v096_96_bites_32by24_video_buffer_15 (
    .out_8(v096_96_bites_32by24_video_buffer_15_out_8), .out_9(v096_96_bites_32by24_video_buffer_15_out_9),
    .out_10(v096_96_bites_32by24_video_buffer_15_out_10),
    .out_11(v096_96_bites_32by24_video_buffer_15_out_11),
    .out_12(v096_96_bites_32by24_video_buffer_15_out_12),
    .out_13(v096_96_bites_32by24_video_buffer_15_out_13),
    .out_14(v096_96_bites_32by24_video_buffer_15_out_14),
    .out_15(v096_96_bites_32by24_video_buffer_15_out_15),
    .out_16(v096_96_bites_32by24_video_buffer_15_out_16),
    .out_17(v096_96_bites_32by24_video_buffer_15_out_17),
    .out_18(v096_96_bites_32by24_video_buffer_15_out_18),
    .out_19(v096_96_bites_32by24_video_buffer_15_out_19),
    .out_20(v096_96_bites_32by24_video_buffer_15_out_20),
    .out_21(v096_96_bites_32by24_video_buffer_15_out_21),
    .out_22(v096_96_bites_32by24_video_buffer_15_out_22),
    .out_23(v096_96_bites_32by24_video_buffer_15_out_23),
    .out_24(v096_96_bites_32by24_video_buffer_15_out_24),
    .out_25(v096_96_bites_32by24_video_buffer_15_out_25),
    .out_26(v096_96_bites_32by24_video_buffer_15_out_26),
    .out_27(v096_96_bites_32by24_video_buffer_15_out_27),
    .out_28(v096_96_bites_32by24_video_buffer_15_out_28),
    .out_29(v096_96_bites_32by24_video_buffer_15_out_29),
    .out_30(v096_96_bites_32by24_video_buffer_15_out_30),
    .out_31(v096_96_bites_32by24_video_buffer_15_out_31), .in_1(decoder_3_out4),
    .in_2(video_card_120_x_96_1_out_6), .in_3(video_card_120_x_96_1_out_5),
    .in_4(video_card_120_x_96_1_out_7), .in_5(video_card_120_x_96_1_out_8), .in_6(clock_1_out_25),
    .in_7(video_card_120_x_96_1__0));
  ALU alu_1 (
    .in_4(control_1_out_19), .in_1(registers_1_out_10), .in_2(registers_1_out_11), .out_8(alu_1_out_8),
    .in_3(clock_1_out_25), .out_7(alu_1_out_7), .in_5(multiplexer_13_out[7:0]), .in_6(control_1_out_18[0]),
    .out_9(alu_1_out_9));
  Decoder #(.select(3), .disabled(0)) decoder_1 (
    .out0(decoder_1_out0), .out1(decoder_1_out1), .out2(decoder_1_out2), .out3(decoder_1_out3),
    .out4(decoder_1_out4), .sel(video_card_120_x_96_1_out_5_2), .en(decoder_4_out0));  // open: out5, out6, out7
  Decoder #(.select(3), .disabled(0)) decoder_2 (
    .out0(decoder_2_out0), .out1(decoder_2_out1), .out2(decoder_2_out2), .out3(decoder_2_out3),
    .out4(decoder_2_out4), .sel(video_card_120_x_96_1_out_5_2), .en(decoder_4_out1));  // open: out5, out6, out7
  Decoder #(.select(3), .disabled(0)) decoder_3 (
    .out0(decoder_3_out0), .out1(decoder_3_out1), .out2(decoder_3_out2), .out3(decoder_3_out3),
    .out4(decoder_3_out4), .sel(video_card_120_x_96_1_out_5_2), .en(decoder_4_out2));  // open: out5, out6, out7
  Decoder #(.select(2), .disabled(0)) decoder_4 (
    .out0(decoder_4_out0), .out1(decoder_4_out1), .out2(decoder_4_out2), .sel(video_card_120_x_96_1_out_6_2),
    .en(video_card_120_x_96_1_e_w));  // open: out3
  Video_Card_120_x_96 video_card_120_x_96_1 (
    .out_5({video_card_120_x_96_1_out_5_3, video_card_120_x_96_1_out_5_2, video_card_120_x_96_1_out_5}),
    .out_6({video_card_120_x_96_1_out_6_3, video_card_120_x_96_1_out_6_2, video_card_120_x_96_1_out_6}),
    .out_7({video_card_120_x_96_1_out_7_3, video_card_120_x_96_1_out_7_2[3], video_card_120_x_96_1_out_7}),
    .out_8(video_card_120_x_96_1_out_8), .E_W(video_card_120_x_96_1_e_w), ._0(video_card_120_x_96_1__0),
    .in_1(adder_4_out), .C(clock_1_out_25), .W_Ram(control_1_out_21), .in_4(or_14_out));
  Clock clock_1 (
    .out_31(clock_1_out_31), .out_27(clock_1_out_27), .out_28(clock_1_out_28), .out_29(clock_1_out_29),
    .out_30(clock_1_out_30), .out_25(clock_1_out_25), .in_11(control_1_out_25), .out_26(clock_1_out_26),
    .out_32(clock_1_out_32), .out_33(clock_1_out_33), .out_14(clock_1_out_14), .out_13(clock_1_out_13),
    .in_4(or_5_out), .in_3(Off_out), .out_15(clock_1_out_15), .out_16(clock_1_out_16),
    .out_17(clock_1_out_17), .out_18(clock_1_out_18), .in_5(kb_io_1_out_12), .out_19(clock_1_out_19),
    .in_6(kb_io_1_enable_io_mt), .out_20(clock_1_out_20), .in_2(Data), .out_22(clock_1_out_22),
    .in_7(multiplexer_26_out), .out_21(clock_1_out_21), .in_8(dma_1_out_9), .out_24(clock_1_out_24),
    .in_9(register_5_q), .in_10(register_4_q), .out_23(clock_1_out_23),
    .in_1({multiplexer_8_out_2, multiplexer_8_out}), .out_12(clock_1_out_12));
  RAM #(.addrWidth(12), .dataWidth(32), .bus("separate")) ram_1 (
    .addr(dma_1_out_6), .din(ram_7_data), .data(ram_1_data), .str(dma_1_out_8), .clk(clock_1_out_25),
    .ld(dma_1_out_7));  // open: sel, clr
  assign or_7_out = or_6_out | multiplexer_9_out[11:0];  // OR_Gate or_7, 12 bits wide
  assign or_8_out = clock_1_out_23 | or_7_out;  // OR_Gate or_8, 12 bits wide
  Multiplexer #(.width(32), .enable("false")) multiplexer_14 (
    .in0({32{1'b0}}), .in1(ram_1_data), .out(multiplexer_14_out), .sel(dma_1_out_7));
  Multiplexer #(.width(16), .disabled(0), .enable("false")) multiplexer_15 (
    .in0(16'hff), .in1(16'hfdf), .out(multiplexer_15_out), .sel(in_2));
  D_Flip_Flop d_ff_3 (
    .clk(clock_1_out_25), .D(On_2_out), .Q(d_ff_3_q), .Qn(d_ff_3_qn), .en(undriven_33), .reset(undriven_34));  // open: preset
  Register #(.width(16)) register_1 (
    .D(adder_2_out), .en(decoder_5_out2), .Q(out_4), .clk(clock_1_out_25), .clr(and_5_out));
  Multiplexer #(.width(16), .enable("false")) multiplexer_16 (
    .in0({16{1'b0}}), .in1(out_4), .out(multiplexer_16_out), .sel(or_9_out));
  D_Flip_Flop d_ff_4 (
    .clk(clock_1_out_25), .D(d_ff_3_q), .Q(d_ff_4_q), .Qn(d_ff_4_qn), .en(d_ff_3_q), .reset(and_5_out));  // open: preset
  Register #(.width(2)) register_2 (
    .D(adder_3_out), .en(d_ff_4_q), .Q(register_2_q), .clk(clock_1_out_25), .clr(and_5_out));
  Decoder #(.select(2), .disabled(0)) decoder_5 (
    .out0(decoder_5_out0), .out1(decoder_5_out1), .out2(decoder_5_out2), .out3(decoder_5_out3),
    .sel(register_2_q), .en(d_ff_4_q));
  or or_9 (or_9_out, decoder_5_out1, decoder_5_out2);
  and and_5 (and_5_out, decoder_5_out2, nand_5_out);
  Multiplexer #(.width(16), .enable("false")) multiplexer_17 (
    .in0({16{1'b0}}), .in1(out_4), .out(multiplexer_17_out), .sel(decoder_5_out2));
  Multiplexer #(.width(2), .disabled(0), .enable("false")) multiplexer_18 (
    .in0(2'b00), .in1(2'b10), .out(multiplexer_18_out), .sel(decoder_5_out2));
  nand nand_5 (nand_5_out, or_10_out, or_10_out);
  Adder #(.width(16)) adder_2 (
    .a({16{1'b0}}), .b(multiplexer_17_out), .out(adder_2_out), .cin(decoder_5_out2));  // open: cout
  Adder #(.width(2)) adder_3 (.a(multiplexer_18_out), .b(register_2_q), .out(adder_3_out), .cin(1'b1));  // open: cout
  or or_10 (or_10_out, xor_1_out[0], xor_1_out[1], xor_1_out[2], xor_1_out[3], xor_1_out[4], xor_1_out[5], xor_1_out[6], xor_1_out[7], xor_1_out[8], xor_1_out[9], xor_1_out[10], xor_1_out[11], xor_1_out[12], xor_1_out[13], xor_1_out[14], xor_1_out[15]);
  assign xor_1_out = multiplexer_15_out ^ multiplexer_16_out;  // XOR_Gate xor_1, 16 bits wide
  RAM #(.addrWidth(16), .bus("separate")) ram_2 (
    .addr(multiplexer_16_out), .data(ram_2_data), .str(1'b0), .clk(clock_1_out_25), .ld(or_9_out));  // open: din, sel, clr
  Multiplexer #(.width(8), .enable("false")) multiplexer_19 (
    .in0({8{1'b0}}), .in1(ram_2_data), .out(multiplexer_19_out), .sel(or_9_out));
  assign or_11_out = multiplexer_40_out | or_13_out;  // OR_Gate or_11, 8 bits wide
  assign or_12_out = registers_1_out_12 | clock_1_out_12;  // OR_Gate or_12, 8 bits wide
  assign or_13_out = alu_1_out_7 | multiplexer_11_out[7:0];  // OR_Gate or_13, 8 bits wide
  assign or_14_out = multiplexer_19_out | or_12_out;  // OR_Gate or_14, 8 bits wide
  and and_6 (and_6_out, button_1_out, clock_1_out_22);
  Multiplexer #(.disabled(0), .enable("false")) multiplexer_20 (
    .in0(control_1_out_10), .in1(1'b0), .out(multiplexer_20_out), .sel(register_5_q));
  Multiplexer #(.disabled(0), .enable("false")) multiplexer_21 (
    .in0(control_1_out_20), .in1(1'b0), .out(multiplexer_21_out), .sel(register_5_q));
  Multiplexer #(.width(12), .enable("false")) multiplexer_22 (
    .in0({4'b0000, registers_1_out_13}), .in1({12{1'b1}}), .out(multiplexer_22_out), .sel(multiplexer_20_out));
  Adder #(.width(12)) adder_4 (
    .a(or_8_out), .b(multiplexer_22_out), .out(adder_4_out), .cin(multiplexer_21_out));  // open: cout
  Register register_3 (.D(or_14_out), .en(and_11_out), .Q(register_3_q), .clk(clock_1_out_25));  // open: clr
  or or_15 (or_15_out, multiplexer_31_out, clock_1_out_24, decoder_5_out1);
  or or_16 (or_16_out, control_1_out_21, control_1_out_22, clock_1_out_21);
  Multiplexer #(.disabled(0), .enable("false")) multiplexer_23 (
    .in0(or_15_out), .in1(1'b0), .out(multiplexer_23_out), .sel(and_12_out));
  Multiplexer #(.width(6), .disabled(0), .enable("false")) multiplexer_24 (
    .in0(adder_4_out[11:6]), .in1(register_3_q[5:0]), .out(multiplexer_24_out), .sel(and_12_out));
  and and_7 (and_7_out, ~adder_4_out[4], adder_4_out[5], adder_4_out[6], adder_4_out[7], adder_4_out[8], adder_4_out[9], adder_4_out[10], adder_4_out[11]);  // AND_Gate
  and and_8 (and_8_out, adder_4_out[0], ~adder_4_out[1], ~adder_4_out[2], adder_4_out[3]);  // AND_Gate
  and and_9 (and_9_out, ~adder_4_out[0], adder_4_out[1], ~adder_4_out[2], adder_4_out[3]);  // AND_Gate
  and and_10 (and_10_out, adder_4_out[0], adder_4_out[1], ~adder_4_out[2], adder_4_out[3]);  // AND_Gate
  and and_11 (and_11_out, and_7_out, and_8_out, control_1_out_21);
  and and_12 (and_12_out, and_7_out, and_9_out, control_1_out_21);
  and and_13 (and_13_out, and_7_out, and_10_out, control_1_out_21);
  RAM #(.addrWidth(6), .bus("separate")) ram_3 (
    .addr(multiplexer_24_out), .din(or_14_out), .data(ram_3_data), .str(and_12_out), .clk(clock_1_out_25),
    .ld(or_16_out), .clr(and_13_out));  // open: sel
  Register register_4 (
    .D({2'b00, multiplexer_24_out}), .en(or_16_out), .Q(register_4_q), .clk(clock_1_out_25));  // open: clr
  Multiplexer #(.width(8), .enable("false")) multiplexer_25 (
    .in0({8{1'b0}}), .in1(multiplexer_28_out), .out(multiplexer_25_out), .sel(or_16_out));
  Multiplexer #(.width(16), .disabled(0), .enable("false")) multiplexer_26 (
    .in0(multiplexer_41_out), .in1({16{1'b0}}), .out(multiplexer_26_out), .sel(or_18_out));
  ROM #(.addrWidth(6)) rom_1 (.addr(multiplexer_24_out), .data(rom_1_data));  // open: sel
  Multiplexer #(.width(12), .disabled(0), .enable("false")) multiplexer_27 (
    .in0({12{1'b0}}), .in1({multiplexer_25_out[5:0], adder_4_out[5:0]}), .out(multiplexer_27_out),
    .sel(multiplexer_25_out[7]));
  Counter #(.width(32), .max('hffffffff)) counter_1 (
    .count(register_5_q), .clk(register_5_q));  // open: load, D, Q, carry, clr
  and and_14 (and_14_out, ~multiplexer_25_out[7], or_16_out);  // AND_Gate
  Register #(.width(1)) register_5 (
    .D(and_14_out), .en(clock_1_out_25), .Q(register_5_q), .clk(clock_1_out_25));  // open: clr
  Multiplexer #(.width(8), .enable("false")) multiplexer_28 (
    .in0(rom_1_data), .in1(ram_3_data), .out(multiplexer_28_out), .sel(MMU_On));
  assign or_17_out = multiplexer_16_out[11:0] | clock_1_out_23 | multiplexer_27_out;  // OR_Gate or_17, 12 bits wide
  Multiplexer #(.disabled(0), .enable("false")) multiplexer_29 (
    .in0(clock_1_out_21), .in1(1'b0), .out(multiplexer_29_out), .sel(or_18_out));
  or or_18 (or_18_out, register_5_q, and_14_out);
  and and_15 (and_15_out, and_14_out, control_1_out_21);
  Multiplexer #(.disabled(0), .enable("false")) multiplexer_30 (
    .in0(control_1_out_22), .in1(1'b0), .out(multiplexer_30_out), .sel(or_18_out));
  Multiplexer #(.disabled(0), .enable("false")) multiplexer_31 (
    .in0(control_1_out_21), .in1(1'b0), .out(multiplexer_31_out), .sel(and_15_out));
  DMA dma_1 (
    .in_3(and_6_out), .out_9(dma_1_out_9), .in_1(or_14_out), .in_4(multiplexer_23_out),
    .in_5(clock_1_out_25), .in_2(or_17_out), .out_6(dma_1_out_6), .out_7(dma_1_out_7), .out_8(dma_1_out_8),
    .out_10(dma_1_out_10), .out_11(dma_1_out_11), .out_12(dma_1_out_12));
  assign {or_19_out_2, or_19_out} = or_17_out | dma_1_out_10;  // OR_Gate or_19, 12 bits wide
  or or_20 (or_20_out, multiplexer_23_out, dma_1_out_11);
  or or_21 (or_21_out, dma_1_out_11, dma_1_out_12);
  Decoder #(.select(2), .enable("false")) decoder_6 (
    .out0(decoder_6_out0), .out1(decoder_6_out1), .out2(decoder_6_out2), .out3(decoder_6_out3),
    .sel(or_19_out));
  or or_22 (or_22_out, multiplexer_29_out, dma_1_out_12, multiplexer_30_out);
  not not_1 (not_1_out, or_19_out[1]);
  Multiplexer #(.width(8), .enable("false")) multiplexer_32 (
    .in0(or_14_out), .in1(multiplexer_14_out[31:24]), .out(multiplexer_32_out), .sel(dma_1_out_11));
  or or_23 (or_23_out, decoder_6_out0, or_21_out, and_17_out);
  and and_16 (and_16_out, or_19_out[1], multiplexer_29_out);
  and and_17 (and_17_out, not_1_out, multiplexer_29_out);
  RAM #(.addrWidth(10), .bus("separate")) ram_4 (
    .addr(or_19_out_2), .din(multiplexer_32_out), .data(ram_7_data[31:24]), .str(or_20_out), .sel(or_23_out),
    .clk(clock_1_out_25), .ld(or_22_out));  // open: clr
  and and_18 (and_18_out, or_23_out, or_22_out);
  Multiplexer #(.width(8), .enable("false")) multiplexer_33 (
    .in0({8{1'b0}}), .in1(ram_7_data[31:24]), .out(multiplexer_33_out), .sel(and_18_out));
  or or_24 (or_24_out, multiplexer_29_out, dma_1_out_12, multiplexer_30_out);
  Multiplexer #(.width(8), .enable("false")) multiplexer_34 (
    .in0(or_14_out), .in1(multiplexer_14_out[23:16]), .out(multiplexer_34_out), .sel(dma_1_out_11));
  or or_25 (or_25_out, decoder_6_out1, or_21_out, and_17_out);
  RAM #(.addrWidth(10), .bus("separate")) ram_5 (
    .addr(or_19_out_2), .din(multiplexer_34_out), .data(ram_7_data[23:16]), .str(or_20_out), .sel(or_25_out),
    .clk(clock_1_out_25), .ld(or_24_out));  // open: clr
  and and_19 (and_19_out, or_25_out, or_24_out);
  Multiplexer #(.width(8), .enable("false")) multiplexer_35 (
    .in0(multiplexer_33_out), .in1(ram_7_data[23:16]), .out(multiplexer_35_out), .sel(and_19_out));
  or or_26 (or_26_out, multiplexer_29_out, dma_1_out_12, multiplexer_30_out);
  Multiplexer #(.width(8), .enable("false")) multiplexer_36 (
    .in0(or_14_out), .in1(multiplexer_14_out[15:8]), .out(multiplexer_36_out), .sel(dma_1_out_11));
  or or_27 (or_27_out, decoder_6_out2, or_21_out, and_16_out);
  RAM #(.addrWidth(10), .bus("separate")) ram_6 (
    .addr(or_19_out_2), .din(multiplexer_36_out), .data(ram_7_data[15:8]), .str(or_20_out), .sel(or_27_out),
    .clk(clock_1_out_25), .ld(or_26_out));  // open: clr
  and and_20 (and_20_out, or_27_out, or_26_out);
  Multiplexer #(.width(16), .enable("false")) multiplexer_37 (
    .in0({16{1'b0}}), .in1(ram_7_data[31:16]), .out(multiplexer_37_out), .sel(and_17_out));
  Multiplexer #(.width(8), .enable("false")) multiplexer_38 (
    .in0(multiplexer_35_out), .in1(ram_7_data[15:8]), .out(multiplexer_38_out), .sel(and_20_out));
  or or_28 (or_28_out, multiplexer_29_out, dma_1_out_12, multiplexer_30_out);
  or or_29 (or_29_out, decoder_6_out3, or_21_out, and_16_out);
  Multiplexer #(.width(8), .enable("false")) multiplexer_39 (
    .in0(or_14_out), .in1(multiplexer_14_out[7:0]), .out(multiplexer_39_out), .sel(dma_1_out_11));
  RAM #(.addrWidth(10), .bus("separate")) ram_7 (
    .addr(or_19_out_2), .din(multiplexer_39_out), .data(ram_7_data[7:0]), .str(or_20_out), .sel(or_29_out),
    .clk(clock_1_out_25), .ld(or_28_out));  // open: clr
  and and_21 (and_21_out, or_29_out, or_28_out);
  Multiplexer #(.width(8), .enable("false")) multiplexer_40 (
    .in0(multiplexer_38_out), .in1(ram_7_data[7:0]), .out(multiplexer_40_out), .sel(and_21_out));
  Multiplexer #(.width(16), .enable("false")) multiplexer_41 (
    .in0(multiplexer_37_out), .in1(ram_7_data[15:0]), .out(multiplexer_41_out), .sel(and_16_out));
  RAM #(.addrWidth(12), .bus("separate")) ram_8 (
    .addr({or_19_out_2, or_19_out}), .din(multiplexer_32_out), .data(ram_8_data), .str(or_20_out),
    .clk(clock_1_out_25), .ld(multiplexer_30_out));  // open: sel, clr
  Multiplexer #(.width(8), .enable("false")) multiplexer_42 (
    .in0({8{1'b0}}), .in1(ram_8_data), .out(multiplexer_42_out), .sel(multiplexer_30_out));

  // Notes on the sheet:
  //   4011B Quad 2 Inputs NAND
  //   Clock
  //   Loader 256
  //   Loader 4K
  //   4013B Dual D-tipe flip-flop
  //   Boot From HD
  //   Keyboard IN
  //   16Kb HD 64 bites/page 256 pages
  //   HD
  //   Loading stops at fdf to avoid engaging the DMA
  //   Adr ALU
  //   TLB fe9 set adr in MMU to write, fea write, feb Cls
  //   MMU/ Page Table
  //   contents of rom_1 (hex, n*v repeats v):
  //   80 81 82 83 84 85 86 87 88 89 8a 8b 8c 8d 8e 8f 90 91 92 93 94 95 96 97 98 99 9a 9b 9c 9d 9e 9f a0
  //   a1 a2 a3 a4 a5 a6 a7 a8 a9 aa ab ac ad ae af b0 b1 b2 b3 b4 b5 b6 b7 b8 b9 ba bb bc bd be bf
  //   Interrupting Data flow to prevent next inst done twice
endmodule
module V096_96_Bites_32By24_Video_Buffer (
  input  in_1,
  input  [1:0] in_2,
  input  [1:0] in_3,
  input  [2:0] in_4,
  input  [7:0] in_5,
  input  in_6,
  input  in_7,
  output [31:0] out_8,
  output [31:0] out_9,
  output [31:0] out_10,
  output [31:0] out_11,
  output [31:0] out_12,
  output [31:0] out_13,
  output [31:0] out_14,
  output [31:0] out_15,
  output [31:0] out_16,
  output [31:0] out_17,
  output [31:0] out_18,
  output [31:0] out_19,
  output [31:0] out_20,
  output [31:0] out_21,
  output [31:0] out_22,
  output [31:0] out_23,
  output [31:0] out_24,
  output [31:0] out_25,
  output [31:0] out_26,
  output [31:0] out_27,
  output [31:0] out_28,
  output [31:0] out_29,
  output [31:0] out_30,
  output [31:0] out_31
);

  wire decoder_1_out0, decoder_1_out1, decoder_1_out2, decoder_1_out3, decoder_2_out1, decoder_2_out2,
       decoder_2_out3, decoder_2_out4, decoder_2_out5, decoder_2_out6, decoder_3_out0, decoder_3_out1,
       decoder_3_out2, decoder_3_out3, decoder_4_out1, decoder_4_out2, decoder_4_out3, decoder_4_out4,
       decoder_4_out5, decoder_4_out6, decoder_5_out0, decoder_5_out1, decoder_5_out2, decoder_5_out3,
       decoder_6_out1, decoder_6_out2, decoder_6_out3, decoder_6_out4, decoder_6_out5, decoder_6_out6,
       decoder_7_out0, decoder_7_out1, decoder_7_out2, decoder_7_out3, decoder_8_out1, decoder_8_out2,
       decoder_8_out3, decoder_8_out4, decoder_8_out5, decoder_8_out6, decoder_9_out0, decoder_9_out1,
       decoder_9_out2, decoder_9_out3, decoder_10_out1, decoder_10_out2, decoder_10_out3, decoder_10_out4,
       decoder_10_out5, decoder_10_out6, decoder_11_out1, decoder_11_out2, decoder_11_out3, decoder_11_out4,
       decoder_11_out5, decoder_11_out6, decoder_12_out1, decoder_12_out2, decoder_12_out3, decoder_12_out4,
       decoder_12_out5, decoder_12_out6, decoder_13_out1, decoder_13_out2, decoder_13_out3, decoder_13_out4,
       decoder_13_out5, decoder_13_out6, decoder_14_out1, decoder_14_out2, decoder_14_out3, decoder_14_out4,
       decoder_14_out5, decoder_14_out6, decoder_15_out1, decoder_15_out2, decoder_15_out3, decoder_15_out4,
       decoder_15_out5, decoder_15_out6, decoder_16_out1, decoder_16_out2, decoder_16_out3, decoder_16_out4,
       decoder_16_out5, decoder_16_out6, decoder_17_out1, decoder_17_out2, decoder_17_out3, decoder_17_out4,
       decoder_17_out5, decoder_17_out6, decoder_18_out1, decoder_18_out2, decoder_18_out3, decoder_18_out4,
       decoder_18_out5, decoder_18_out6, decoder_19_out1, decoder_19_out2, decoder_19_out3, decoder_19_out4,
       decoder_19_out5, decoder_19_out6, decoder_20_out1, decoder_20_out2, decoder_20_out3, decoder_20_out4,
       decoder_20_out5, decoder_20_out6, decoder_21_out1, decoder_21_out2, decoder_21_out3, decoder_21_out4,
       decoder_21_out5, decoder_21_out6;

  Decoder #(.select(2), .disabled(0)) decoder_1 (
    .out0(decoder_1_out0), .out1(decoder_1_out1), .out2(decoder_1_out2), .out3(decoder_1_out3), .sel(in_2),
    .en(in_1));
  Decoder #(.select(3), .disabled(0)) decoder_2 (
    .out1(decoder_2_out1), .out2(decoder_2_out2), .out3(decoder_2_out3), .out4(decoder_2_out4),
    .out5(decoder_2_out5), .out6(decoder_2_out6), .sel(in_4), .en(decoder_3_out0));  // open: out0, out7
  Decoder #(.select(2), .disabled(0)) decoder_3 (
    .out0(decoder_3_out0), .out1(decoder_3_out1), .out2(decoder_3_out2), .out3(decoder_3_out3), .sel(in_3),
    .en(decoder_1_out0));
  Decoder #(.select(3), .disabled(0)) decoder_4 (
    .out1(decoder_4_out1), .out2(decoder_4_out2), .out3(decoder_4_out3), .out4(decoder_4_out4),
    .out5(decoder_4_out5), .out6(decoder_4_out6), .sel(in_4), .en(decoder_5_out0));  // open: out0, out7
  Decoder #(.select(2), .disabled(0)) decoder_5 (
    .out0(decoder_5_out0), .out1(decoder_5_out1), .out2(decoder_5_out2), .out3(decoder_5_out3), .sel(in_3),
    .en(decoder_1_out1));
  Decoder #(.select(3), .disabled(0)) decoder_6 (
    .out1(decoder_6_out1), .out2(decoder_6_out2), .out3(decoder_6_out3), .out4(decoder_6_out4),
    .out5(decoder_6_out5), .out6(decoder_6_out6), .sel(in_4), .en(decoder_7_out0));  // open: out0, out7
  Decoder #(.select(2), .disabled(0)) decoder_7 (
    .out0(decoder_7_out0), .out1(decoder_7_out1), .out2(decoder_7_out2), .out3(decoder_7_out3), .sel(in_3),
    .en(decoder_1_out2));
  Decoder #(.select(3), .disabled(0)) decoder_8 (
    .out1(decoder_8_out1), .out2(decoder_8_out2), .out3(decoder_8_out3), .out4(decoder_8_out4),
    .out5(decoder_8_out5), .out6(decoder_8_out6), .sel(in_4), .en(decoder_9_out0));  // open: out0, out7
  Decoder #(.select(2), .disabled(0)) decoder_9 (
    .out0(decoder_9_out0), .out1(decoder_9_out1), .out2(decoder_9_out2), .out3(decoder_9_out3), .sel(in_3),
    .en(decoder_1_out3));
  Register register_1 (.D(in_5), .en(decoder_2_out1), .Q(out_8[31:24]), .clk(in_6), .clr(in_7));
  Register register_2 (.D(in_5), .en(decoder_2_out2), .Q(out_12[31:24]), .clk(in_6), .clr(in_7));
  Register register_3 (.D(in_5), .en(decoder_4_out1), .Q(out_8[23:16]), .clk(in_6), .clr(in_7));
  Register register_4 (.D(in_5), .en(decoder_4_out2), .Q(out_12[23:16]), .clk(in_6), .clr(in_7));
  Register register_5 (.D(in_5), .en(decoder_6_out1), .Q(out_8[15:8]), .clk(in_6), .clr(in_7));
  Register register_6 (.D(in_5), .en(decoder_6_out2), .Q(out_12[15:8]), .clk(in_6), .clr(in_7));
  Register register_7 (.D(in_5), .en(decoder_8_out1), .Q(out_8[7:0]), .clk(in_6), .clr(in_7));
  Register register_8 (.D(in_5), .en(decoder_8_out2), .Q(out_12[7:0]), .clk(in_6), .clr(in_7));
  Register register_9 (.D(in_5), .en(decoder_2_out3), .Q(out_16[31:24]), .clk(in_6), .clr(in_7));
  Register register_10 (.D(in_5), .en(decoder_2_out4), .Q(out_20[31:24]), .clk(in_6), .clr(in_7));
  Register register_11 (.D(in_5), .en(decoder_2_out5), .Q(out_24[31:24]), .clk(in_6), .clr(in_7));
  Register register_12 (.D(in_5), .en(decoder_4_out3), .Q(out_16[23:16]), .clk(in_6), .clr(in_7));
  Register register_13 (.D(in_5), .en(decoder_4_out4), .Q(out_20[23:16]), .clk(in_6), .clr(in_7));
  Register register_14 (.D(in_5), .en(decoder_4_out5), .Q(out_24[23:16]), .clk(in_6), .clr(in_7));
  Register register_15 (.D(in_5), .en(decoder_6_out3), .Q(out_16[15:8]), .clk(in_6), .clr(in_7));
  Register register_16 (.D(in_5), .en(decoder_6_out4), .Q(out_20[15:8]), .clk(in_6), .clr(in_7));
  Register register_17 (.D(in_5), .en(decoder_6_out5), .Q(out_24[15:8]), .clk(in_6), .clr(in_7));
  Register register_18 (.D(in_5), .en(decoder_8_out3), .Q(out_16[7:0]), .clk(in_6), .clr(in_7));
  Register register_19 (.D(in_5), .en(decoder_8_out4), .Q(out_20[7:0]), .clk(in_6), .clr(in_7));
  Register register_20 (.D(in_5), .en(decoder_8_out5), .Q(out_24[7:0]), .clk(in_6), .clr(in_7));
  Register register_21 (.D(in_5), .en(decoder_2_out6), .Q(out_28[31:24]), .clk(in_6), .clr(in_7));
  Register register_22 (.D(in_5), .en(decoder_4_out6), .Q(out_28[23:16]), .clk(in_6), .clr(in_7));
  Register register_23 (.D(in_5), .en(decoder_6_out6), .Q(out_28[15:8]), .clk(in_6), .clr(in_7));
  Register register_24 (.D(in_5), .en(decoder_8_out6), .Q(out_28[7:0]), .clk(in_6), .clr(in_7));
  Decoder #(.select(3), .disabled(0)) decoder_10 (
    .out1(decoder_10_out1), .out2(decoder_10_out2), .out3(decoder_10_out3), .out4(decoder_10_out4),
    .out5(decoder_10_out5), .out6(decoder_10_out6), .sel(in_4), .en(decoder_3_out1));  // open: out0, out7
  Decoder #(.select(3), .disabled(0)) decoder_11 (
    .out1(decoder_11_out1), .out2(decoder_11_out2), .out3(decoder_11_out3), .out4(decoder_11_out4),
    .out5(decoder_11_out5), .out6(decoder_11_out6), .sel(in_4), .en(decoder_5_out1));  // open: out0, out7
  Decoder #(.select(3), .disabled(0)) decoder_12 (
    .out1(decoder_12_out1), .out2(decoder_12_out2), .out3(decoder_12_out3), .out4(decoder_12_out4),
    .out5(decoder_12_out5), .out6(decoder_12_out6), .sel(in_4), .en(decoder_7_out1));  // open: out0, out7
  Decoder #(.select(3), .disabled(0)) decoder_13 (
    .out1(decoder_13_out1), .out2(decoder_13_out2), .out3(decoder_13_out3), .out4(decoder_13_out4),
    .out5(decoder_13_out5), .out6(decoder_13_out6), .sel(in_4), .en(decoder_9_out1));  // open: out0, out7
  Register register_25 (.D(in_5), .en(decoder_10_out1), .Q(out_9[31:24]), .clk(in_6), .clr(in_7));
  Register register_26 (.D(in_5), .en(decoder_10_out2), .Q(out_13[31:24]), .clk(in_6), .clr(in_7));
  Register register_27 (.D(in_5), .en(decoder_11_out1), .Q(out_9[23:16]), .clk(in_6), .clr(in_7));
  Register register_28 (.D(in_5), .en(decoder_11_out2), .Q(out_13[23:16]), .clk(in_6), .clr(in_7));
  Register register_29 (.D(in_5), .en(decoder_12_out1), .Q(out_9[15:8]), .clk(in_6), .clr(in_7));
  Register register_30 (.D(in_5), .en(decoder_12_out2), .Q(out_13[15:8]), .clk(in_6), .clr(in_7));
  Register register_31 (.D(in_5), .en(decoder_13_out1), .Q(out_9[7:0]), .clk(in_6), .clr(in_7));
  Register register_32 (.D(in_5), .en(decoder_13_out2), .Q(out_13[7:0]), .clk(in_6), .clr(in_7));
  Register register_33 (.D(in_5), .en(decoder_10_out3), .Q(out_17[31:24]), .clk(in_6), .clr(in_7));
  Register register_34 (.D(in_5), .en(decoder_10_out4), .Q(out_21[31:24]), .clk(in_6), .clr(in_7));
  Register register_35 (.D(in_5), .en(decoder_11_out3), .Q(out_17[23:16]), .clk(in_6), .clr(in_7));
  Register register_36 (.D(in_5), .en(decoder_11_out4), .Q(out_21[23:16]), .clk(in_6), .clr(in_7));
  Register register_37 (.D(in_5), .en(decoder_12_out3), .Q(out_17[15:8]), .clk(in_6), .clr(in_7));
  Register register_38 (.D(in_5), .en(decoder_12_out4), .Q(out_21[15:8]), .clk(in_6), .clr(in_7));
  Register register_39 (.D(in_5), .en(decoder_13_out3), .Q(out_17[7:0]), .clk(in_6), .clr(in_7));
  Register register_40 (.D(in_5), .en(decoder_13_out4), .Q(out_21[7:0]), .clk(in_6), .clr(in_7));
  Register register_41 (.D(in_5), .en(decoder_10_out5), .Q(out_25[31:24]), .clk(in_6), .clr(in_7));
  Register register_42 (.D(in_5), .en(decoder_10_out6), .Q(out_29[31:24]), .clk(in_6), .clr(in_7));
  Register register_43 (.D(in_5), .en(decoder_11_out5), .Q(out_25[23:16]), .clk(in_6), .clr(in_7));
  Register register_44 (.D(in_5), .en(decoder_11_out6), .Q(out_29[23:16]), .clk(in_6), .clr(in_7));
  Register register_45 (.D(in_5), .en(decoder_12_out5), .Q(out_25[15:8]), .clk(in_6), .clr(in_7));
  Register register_46 (.D(in_5), .en(decoder_12_out6), .Q(out_29[15:8]), .clk(in_6), .clr(in_7));
  Register register_47 (.D(in_5), .en(decoder_13_out5), .Q(out_25[7:0]), .clk(in_6), .clr(in_7));
  Register register_48 (.D(in_5), .en(decoder_13_out6), .Q(out_29[7:0]), .clk(in_6), .clr(in_7));
  Decoder #(.select(3), .disabled(0)) decoder_14 (
    .out1(decoder_14_out1), .out2(decoder_14_out2), .out3(decoder_14_out3), .out4(decoder_14_out4),
    .out5(decoder_14_out5), .out6(decoder_14_out6), .sel(in_4), .en(decoder_3_out2));  // open: out0, out7
  Decoder #(.select(3), .disabled(0)) decoder_15 (
    .out1(decoder_15_out1), .out2(decoder_15_out2), .out3(decoder_15_out3), .out4(decoder_15_out4),
    .out5(decoder_15_out5), .out6(decoder_15_out6), .sel(in_4), .en(decoder_5_out2));  // open: out0, out7
  Decoder #(.select(3), .disabled(0)) decoder_16 (
    .out1(decoder_16_out1), .out2(decoder_16_out2), .out3(decoder_16_out3), .out4(decoder_16_out4),
    .out5(decoder_16_out5), .out6(decoder_16_out6), .sel(in_4), .en(decoder_7_out2));  // open: out0, out7
  Decoder #(.select(3), .disabled(0)) decoder_17 (
    .out1(decoder_17_out1), .out2(decoder_17_out2), .out3(decoder_17_out3), .out4(decoder_17_out4),
    .out5(decoder_17_out5), .out6(decoder_17_out6), .sel(in_4), .en(decoder_9_out2));  // open: out0, out7
  Register register_49 (.D(in_5), .en(decoder_14_out1), .Q(out_10[31:24]), .clk(in_6), .clr(in_7));
  Register register_50 (.D(in_5), .en(decoder_15_out1), .Q(out_10[23:16]), .clk(in_6), .clr(in_7));
  Register register_51 (.D(in_5), .en(decoder_16_out1), .Q(out_10[15:8]), .clk(in_6), .clr(in_7));
  Register register_52 (.D(in_5), .en(decoder_17_out1), .Q(out_10[7:0]), .clk(in_6), .clr(in_7));
  Register register_53 (.D(in_5), .en(decoder_14_out2), .Q(out_14[31:24]), .clk(in_6), .clr(in_7));
  Register register_54 (.D(in_5), .en(decoder_14_out3), .Q(out_18[31:24]), .clk(in_6), .clr(in_7));
  Register register_55 (.D(in_5), .en(decoder_14_out4), .Q(out_22[31:24]), .clk(in_6), .clr(in_7));
  Register register_56 (.D(in_5), .en(decoder_15_out2), .Q(out_14[23:16]), .clk(in_6), .clr(in_7));
  Register register_57 (.D(in_5), .en(decoder_15_out3), .Q(out_18[23:16]), .clk(in_6), .clr(in_7));
  Register register_58 (.D(in_5), .en(decoder_15_out4), .Q(out_22[23:16]), .clk(in_6), .clr(in_7));
  Register register_59 (.D(in_5), .en(decoder_16_out2), .Q(out_14[15:8]), .clk(in_6), .clr(in_7));
  Register register_60 (.D(in_5), .en(decoder_16_out3), .Q(out_18[15:8]), .clk(in_6), .clr(in_7));
  Register register_61 (.D(in_5), .en(decoder_16_out4), .Q(out_22[15:8]), .clk(in_6), .clr(in_7));
  Register register_62 (.D(in_5), .en(decoder_17_out2), .Q(out_14[7:0]), .clk(in_6), .clr(in_7));
  Register register_63 (.D(in_5), .en(decoder_17_out3), .Q(out_18[7:0]), .clk(in_6), .clr(in_7));
  Register register_64 (.D(in_5), .en(decoder_17_out4), .Q(out_22[7:0]), .clk(in_6), .clr(in_7));
  Register register_65 (.D(in_5), .en(decoder_14_out5), .Q(out_26[31:24]), .clk(in_6), .clr(in_7));
  Register register_66 (.D(in_5), .en(decoder_14_out6), .Q(out_30[31:24]), .clk(in_6), .clr(in_7));
  Register register_67 (.D(in_5), .en(decoder_15_out5), .Q(out_26[23:16]), .clk(in_6), .clr(in_7));
  Register register_68 (.D(in_5), .en(decoder_15_out6), .Q(out_30[23:16]), .clk(in_6), .clr(in_7));
  Register register_69 (.D(in_5), .en(decoder_16_out5), .Q(out_26[15:8]), .clk(in_6), .clr(in_7));
  Register register_70 (.D(in_5), .en(decoder_16_out6), .Q(out_30[15:8]), .clk(in_6), .clr(in_7));
  Register register_71 (.D(in_5), .en(decoder_17_out5), .Q(out_26[7:0]), .clk(in_6), .clr(in_7));
  Register register_72 (.D(in_5), .en(decoder_17_out6), .Q(out_30[7:0]), .clk(in_6), .clr(in_7));
  Decoder #(.select(3), .disabled(0)) decoder_18 (
    .out1(decoder_18_out1), .out2(decoder_18_out2), .out3(decoder_18_out3), .out4(decoder_18_out4),
    .out5(decoder_18_out5), .out6(decoder_18_out6), .sel(in_4), .en(decoder_3_out3));  // open: out0, out7
  Decoder #(.select(3), .disabled(0)) decoder_19 (
    .out1(decoder_19_out1), .out2(decoder_19_out2), .out3(decoder_19_out3), .out4(decoder_19_out4),
    .out5(decoder_19_out5), .out6(decoder_19_out6), .sel(in_4), .en(decoder_5_out3));  // open: out0, out7
  Decoder #(.select(3), .disabled(0)) decoder_20 (
    .out1(decoder_20_out1), .out2(decoder_20_out2), .out3(decoder_20_out3), .out4(decoder_20_out4),
    .out5(decoder_20_out5), .out6(decoder_20_out6), .sel(in_4), .en(decoder_7_out3));  // open: out0, out7
  Decoder #(.select(3), .disabled(0)) decoder_21 (
    .out1(decoder_21_out1), .out2(decoder_21_out2), .out3(decoder_21_out3), .out4(decoder_21_out4),
    .out5(decoder_21_out5), .out6(decoder_21_out6), .sel(in_4), .en(decoder_9_out3));  // open: out0, out7
  Register register_73 (.D(in_5), .en(decoder_18_out1), .Q(out_11[31:24]), .clk(in_6), .clr(in_7));
  Register register_74 (.D(in_5), .en(decoder_19_out1), .Q(out_11[23:16]), .clk(in_6), .clr(in_7));
  Register register_75 (.D(in_5), .en(decoder_20_out1), .Q(out_11[15:8]), .clk(in_6), .clr(in_7));
  Register register_76 (.D(in_5), .en(decoder_21_out1), .Q(out_11[7:0]), .clk(in_6), .clr(in_7));
  Register register_77 (.D(in_5), .en(decoder_18_out2), .Q(out_15[31:24]), .clk(in_6), .clr(in_7));
  Register register_78 (.D(in_5), .en(decoder_18_out3), .Q(out_19[31:24]), .clk(in_6), .clr(in_7));
  Register register_79 (.D(in_5), .en(decoder_18_out4), .Q(out_23[31:24]), .clk(in_6), .clr(in_7));
  Register register_80 (.D(in_5), .en(decoder_19_out2), .Q(out_15[23:16]), .clk(in_6), .clr(in_7));
  Register register_81 (.D(in_5), .en(decoder_19_out3), .Q(out_19[23:16]), .clk(in_6), .clr(in_7));
  Register register_82 (.D(in_5), .en(decoder_19_out4), .Q(out_23[23:16]), .clk(in_6), .clr(in_7));
  Register register_83 (.D(in_5), .en(decoder_20_out2), .Q(out_15[15:8]), .clk(in_6), .clr(in_7));
  Register register_84 (.D(in_5), .en(decoder_20_out3), .Q(out_19[15:8]), .clk(in_6), .clr(in_7));
  Register register_85 (.D(in_5), .en(decoder_20_out4), .Q(out_23[15:8]), .clk(in_6), .clr(in_7));
  Register register_86 (.D(in_5), .en(decoder_21_out2), .Q(out_15[7:0]), .clk(in_6), .clr(in_7));
  Register register_87 (.D(in_5), .en(decoder_21_out3), .Q(out_19[7:0]), .clk(in_6), .clr(in_7));
  Register register_88 (.D(in_5), .en(decoder_21_out4), .Q(out_23[7:0]), .clk(in_6), .clr(in_7));
  Register register_89 (.D(in_5), .en(decoder_18_out5), .Q(out_27[31:24]), .clk(in_6), .clr(in_7));
  Register register_90 (.D(in_5), .en(decoder_18_out6), .Q(out_31[31:24]), .clk(in_6), .clr(in_7));
  Register register_91 (.D(in_5), .en(decoder_19_out5), .Q(out_27[23:16]), .clk(in_6), .clr(in_7));
  Register register_92 (.D(in_5), .en(decoder_19_out6), .Q(out_31[23:16]), .clk(in_6), .clr(in_7));
  Register register_93 (.D(in_5), .en(decoder_20_out5), .Q(out_27[15:8]), .clk(in_6), .clr(in_7));
  Register register_94 (.D(in_5), .en(decoder_20_out6), .Q(out_31[15:8]), .clk(in_6), .clr(in_7));
  Register register_95 (.D(in_5), .en(decoder_21_out5), .Q(out_27[7:0]), .clk(in_6), .clr(in_7));
  Register register_96 (.D(in_5), .en(decoder_21_out6), .Q(out_31[7:0]), .clk(in_6), .clr(in_7));

  // Notes on the sheet:
  //   Enable/Write
  //   Adr Y
  //   Adr X
  //   Adr Xc
  //   Data
  //   Clock
  //   Reset
endmodule

module Video_Card_120_x_96 (
  input  [11:0] in_1,
  input  C,
  input  W_Ram,
  input  [7:0] in_4,
  output [7:0] out_5,
  output [7:0] out_6,
  output [7:0] out_7,
  output [7:0] out_8,
  output E_W,
  output _0
);

  wire and_1_out, and_2_out, and_3_out, and_4_out, and_5_out, and_6_out, and_7_out, and_8_out, and_9_out,
       and_10_out, and_11_out, and_12_out, and_13_out, and_14_out, and_15_out, and_16_out, and_17_out,
       and_18_out, and_19_out, and_20_out, and_22_out, and_23_out, decoder_1_out2, decoder_1_out3,
       decoder_1_out4, decoder_1_out5, decoder_1_out6, decoder_1_out7, decoder_1_out8, decoder_1_out9,
       decoder_1_out10, decoder_1_out11, decoder_1_out12, decoder_1_out13, decoder_1_out14, decoder_1_out15,
       or_1_out, or_2_out, or_3_out, or_4_out, or_5_out, or_6_out, or_7_out, or_8_out, or_10_out, or_11_out,
       or_12_out, or_13_out, or_14_out, or_15_out, register_4_q;
  wire [3:0] adder_1_out, register_5_q;
  wire [7:0] multiplexer_1_out, multiplexer_2_out, multiplexer_3_out, multiplexer_4_out, multiplexer_5_out,
       multiplexer_6_out, multiplexer_8_out, multiplexer_9_out, multiplexer_10_out, multiplexer_11_out,
       multiplexer_12_out, register_3_q, rom_1_data, rom_2_data, rom_3_data, rom_4_data, rom_5_data,
       rom_6_data;

  and and_1 (and_1_out, in_1[4], in_1[5], in_1[6], in_1[7], in_1[8], in_1[9], in_1[10], in_1[11]);
  and and_2 (and_2_out, ~in_1[0], ~in_1[1], ~in_1[2], ~in_1[3]);  // AND_Gate
  and and_3 (and_3_out, in_1[0], ~in_1[1], ~in_1[2], ~in_1[3]);  // AND_Gate
  and and_4 (and_4_out, ~in_1[0], ~in_1[1], ~in_1[2], in_1[3]);  // AND_Gate
  and and_5 (and_5_out, ~in_1[0], in_1[1], ~in_1[2], ~in_1[3]);  // AND_Gate
  and and_6 (and_6_out, in_1[0], in_1[1], ~in_1[2], ~in_1[3]);  // AND_Gate
  and and_7 (and_7_out, ~in_1[0], ~in_1[1], in_1[2], ~in_1[3]);  // AND_Gate
  and and_8 (and_8_out, in_1[0], ~in_1[1], in_1[2], ~in_1[3]);  // AND_Gate
  and and_9 (and_9_out, ~in_1[0], in_1[1], in_1[2], ~in_1[3]);  // AND_Gate
  and and_10 (and_10_out, in_1[0], in_1[1], in_1[2], ~in_1[3]);  // AND_Gate
  and and_11 (and_11_out, in_1[0], in_1[1], in_1[2], in_1[3]);
  and and_12 (and_12_out, and_1_out, and_2_out, W_Ram);
  and and_13 (and_13_out, and_1_out, and_3_out, W_Ram);
  and and_14 (and_14_out, and_1_out, and_4_out, W_Ram);
  and and_15 (and_15_out, and_1_out, and_5_out);
  and and_16 (and_16_out, and_1_out, and_6_out);
  and and_17 (and_17_out, and_1_out, and_7_out);
  and and_18 (and_18_out, and_1_out, and_8_out);
  and and_19 (and_19_out, and_1_out, and_9_out);
  and and_20 (and_20_out, and_1_out, and_10_out);
  and and_21 (_0, and_1_out, and_11_out, W_Ram);
  Register register_1 (.D(in_4), .en(and_12_out), .Q(out_5), .clk(C));  // open: clr
  Register register_2 (.D(in_4), .en(and_13_out), .Q(out_6), .clk(C));  // open: clr
  Register register_3 (.D(in_4), .en(and_14_out), .Q(register_3_q), .clk(C));  // open: clr
  Register #(.width(1)) register_4 (.D(and_14_out), .en(and_14_out), .Q(register_4_q), .clk(C), .clr(decoder_1_out14));
  and and_22 (and_22_out, or_8_out, ~register_3_q[7], ~register_3_q[6], ~register_3_q[5], ~register_3_q[4], register_3_q[3], register_3_q[2], ~register_3_q[1], ~register_3_q[0]);  // AND_Gate
  Register #(.width(4)) register_5 (
    .D(adder_1_out), .en(register_4_q), .Q(register_5_q), .clk(C), .clr(decoder_1_out14));
  Decoder #(.select(4), .disabled(0)) decoder_1 (
    .out2(decoder_1_out2), .out3(decoder_1_out3), .out4(decoder_1_out4), .out5(decoder_1_out5),
    .out6(decoder_1_out6), .out7(decoder_1_out7), .out8(decoder_1_out8), .out9(decoder_1_out9),
    .out10(decoder_1_out10), .out11(decoder_1_out11), .out12(decoder_1_out12), .out13(decoder_1_out13),
    .out14(decoder_1_out14), .out15(decoder_1_out15), .sel(adder_1_out), .en(register_4_q));  // open: out0, out1
  or or_1 (or_1_out, and_20_out, and_19_out, and_18_out, and_17_out, and_16_out, and_15_out);
  Adder #(.width(4)) adder_1 (.a(4'b0000), .b(register_5_q), .out(adder_1_out), .cin(1'b1));  // open: cout
  and and_23 (and_23_out, W_Ram, or_1_out);
  or or_2 (or_2_out, decoder_1_out2, decoder_1_out3);
  or or_3 (or_3_out, decoder_1_out4, decoder_1_out5);
  or or_4 (or_4_out, decoder_1_out6, decoder_1_out7);
  or or_5 (or_5_out, decoder_1_out8, decoder_1_out9);
  or or_6 (or_6_out, decoder_1_out10, decoder_1_out11);
  or or_7 (or_7_out, decoder_1_out12, decoder_1_out13);
  or or_8 (or_8_out, decoder_1_out3, decoder_1_out5, decoder_1_out7, decoder_1_out9, decoder_1_out11, decoder_1_out13);
  or or_9 (E_W, and_23_out, or_8_out);
  ROM rom_1 (.addr(register_3_q), .data(rom_1_data), .sel(or_2_out));
  ROM rom_2 (.addr(register_3_q), .data(rom_2_data), .sel(or_3_out));
  ROM rom_3 (.addr(register_3_q), .data(rom_3_data), .sel(or_4_out));
  ROM rom_4 (.addr(register_3_q), .data(rom_4_data), .sel(or_5_out));
  ROM rom_5 (.addr(register_3_q), .data(rom_5_data), .sel(or_6_out));
  ROM rom_6 (.addr(register_3_q), .data(rom_6_data), .sel(or_7_out));
  Multiplexer #(.width(8), .disabled(0), .enable("false")) multiplexer_1 (
    .in0({8{1'b0}}), .in1(rom_1_data), .out(multiplexer_1_out), .sel(or_2_out));
  Multiplexer #(.width(8), .disabled(0), .enable("false")) multiplexer_2 (
    .in0(multiplexer_1_out), .in1(rom_2_data), .out(multiplexer_2_out), .sel(or_3_out));
  Multiplexer #(.width(8), .disabled(0), .enable("false")) multiplexer_3 (
    .in0(multiplexer_2_out), .in1(rom_3_data), .out(multiplexer_3_out), .sel(or_4_out));
  Multiplexer #(.width(8), .disabled(0), .enable("false")) multiplexer_4 (
    .in0(multiplexer_3_out), .in1(rom_4_data), .out(multiplexer_4_out), .sel(or_5_out));
  Multiplexer #(.width(8), .disabled(0), .enable("false")) multiplexer_5 (
    .in0(multiplexer_4_out), .in1(rom_5_data), .out(multiplexer_5_out), .sel(or_6_out));
  Multiplexer #(.width(8), .disabled(0), .enable("false")) multiplexer_6 (
    .in0(multiplexer_5_out), .in1(rom_6_data), .out(multiplexer_6_out), .sel(or_7_out));
  Multiplexer #(.width(8), .disabled(0), .enable("false")) multiplexer_7 (
    .in0(multiplexer_6_out), .in1(in_4), .out(out_8), .sel(or_1_out));
  or or_10 (or_10_out, or_2_out, and_15_out);
  or or_11 (or_11_out, or_3_out, and_16_out);
  or or_12 (or_12_out, or_4_out, and_17_out);
  or or_13 (or_13_out, or_5_out, and_18_out);
  or or_14 (or_14_out, or_6_out, and_19_out);
  or or_15 (or_15_out, or_7_out, and_20_out);
  Multiplexer #(.width(8), .disabled(0), .enable("false")) multiplexer_8 (
    .in0({8{1'b0}}), .in1(8'h1), .out(multiplexer_8_out), .sel(or_10_out));
  Multiplexer #(.width(8), .disabled(0), .enable("false")) multiplexer_9 (
    .in0(multiplexer_8_out), .in1(8'h2), .out(multiplexer_9_out), .sel(or_11_out));
  Multiplexer #(.width(8), .disabled(0), .enable("false")) multiplexer_10 (
    .in0(multiplexer_9_out), .in1(8'h3), .out(multiplexer_10_out), .sel(or_12_out));
  Multiplexer #(.width(8), .disabled(0), .enable("false")) multiplexer_11 (
    .in0(multiplexer_10_out), .in1(8'h4), .out(multiplexer_11_out), .sel(or_13_out));
  Multiplexer #(.width(8), .disabled(0), .enable("false")) multiplexer_12 (
    .in0(multiplexer_11_out), .in1(8'h5), .out(multiplexer_12_out), .sel(or_14_out));
  Multiplexer #(.width(8), .disabled(0), .enable("false")) multiplexer_13 (
    .in0(multiplexer_12_out), .in1(8'h6), .out(out_7), .sel(or_15_out));

  // Notes on the sheet:
  //   X
  //   Y
  //   Xc
  //   Data
  //   Adr
  //   Data
  //   contents of rom_1 (hex, n*v repeats v):
  //   35*0 14 0 19 32 4*0 8 0 8 0 1 3e 0 21 22 c 71 3e 40 36 30 0 0 8 0 0 30 3e 7f 7f 3e 7f 7f 7f 3e 7f 0
  //   2 6*7f 3e 7f 31 40 7e 70 7c 63 60 43 0 40 0 0 1 0 2 7f 6 6 e 3f 8 7f 0 2 7f 0 f f e 1f 8 f d 3e e e
  //   e 11 10 11 0 0 0 8 0 3e 0 21 22 c 71 3e 40 36 30 2 7f 6 6 e 3f 30*0 8 22 88 88 aa 0 8 14 8 8 14 14 0
  //   14 14 8 14 8 0 8 8 0 8 8 4*0 14 14 0 14 14 14 8 14 8 4*0 8 14 8 0 ff f ff 0 f0 16*0 15 1 1 1 0 0 8
  //   contents of rom_2 (hex, n*v repeats v):
  //   34*0 10 7f 3a 1a 4d 0 0 41 28 8 1 8 0 6 41 21 42 41 14 49 49 40 49 49 0 1 14 14 41 40 41 44 49 41 41
  //   49 48 41 8 41 41 8 1 20 10 41 48 41 48 49 40 1 c 3 14 10 45 7f 30 41 20 1 40 15 9 9 9 15 48 15 8 0 1
  //   4 0 8 8 11 14 14 4 15 11 1 1 1 a 8 13 8 0 41 10 0 41 21 42 41 14 49 49 40 49 49 15 9 9 9 15 48 30*0
  //   14 14 0 22 55 0 8 14 ff f 14 f7 ff 17 f4 f8 14 8 0 8 8 0 8 8 0 ff fc 1f f4 17 ff 14 f7 14 f8 14 f f8
  //   0 0 f ff 14 8 0 ff f ff 0 f0 16*0 15 11 45 11 3f 2 8
  //   contents of rom_3 (hex, n*v repeats v):
  //   33*0 7d 60 14 6b 4 45 70 3e 3e 70 3e 6 8 3 8 41 7f 45 49 24 49 49 43 49 49 36 36 22 14 22 45 49 44
  //   49 41 41 49 48 41 8 7f 7e 14 1 10 8 41 48 49 4c 49 7f 1 3 c 8 f 49 41 8 41 40 1 30 15 9 9 9 15 48 15
  //   8 2f 2e 1b 7f 7 8 11 14 14 4 15 0 1 2 2 4 7 15 36 77 36 8 0 41 7f 45 49 24 49 49 43 49 49 15 9 9 9
  //   15 48 30*0 2a 2a 22 88 aa ff ff ff 0 8 1f 0 0 10 4 8 fc f f8 f8 f ff 8 ff ff 0 4 10 4 10 0 14 0 f4 8
  //   17 8 8 fc 1f 8 8 ff f8 f ff f ff 0 f0 16*0 15 39 29 29 40 1 2a
  //   contents of rom_4 (hex, n*v repeats v):
  //   34*0 10 7f 2e b 22 0 41 0 28 8 0 8 0 30 41 1 49 49 7f 49 49 4c 49 49 0 0 41 14 14 48 55 44 49 41 41
  //   49 40 45 8 41 40 22 1 20 4 41 48 45 4a 49 40 1 c 3 14 10 51 41 6 7f 20 1 0 15 9 0 9 d 0 15 7 4*0 8 7
  //   e 8 f 8 16 0 e c 1 a 8 19 41 0 8 4 0 41 1 49 49 7f 49 49 4c 49 49 15 9 0 9 d 31*0 14 14 0 22 55 0 0
  //   0 ff f 0 ff ff 1f fc f8 0 0 6*8 14 ff f4 17 f4 17 f7 14 f7 14 f8 14 f f8 14 14 f ff 14 0 8 ff f 0 ff
  //   f0 16*0 15 11 11 45 20 7e 8
  //   contents of rom_5 (hex, n*v repeats v):
  //   34*0 60 14 0 13 5 4*0 8 0 8 0 40 3e 0 31 36 4 46 6 70 36 3e 0 0 0 14 8 30 38 7f 36 0 3e 0 0 26 7f 0
  //   0 41 0 7f 7f 7f 30 3e 31 46 40 7e 70 7c 63 60 61 0 1 0 0 1 0 f 6 0 7f 0 0 e 5*0 7 9*0 e 11 10 4*0 8
  //   0 3e 0 31 36 4 46 6 70 36 3e f 6 0 7f 32*0 22 8 88 88 aa 13*0 6*8 14 8 8*14 8 14 8 8 14 14 8 8 14 0
  //   8 ff f 0 ff f0 16*0 15 1 1 1 0 0 8
  //   contents of rom_6 (hex, n*v repeats v):
  //   177*0 22 55 13*0 6*8 14 8 8*14 8 14 8 8 14 14 8 8 14 0 8 ff f 0 ff f0
endmodule

module KB_IO (
  input  [11:0] in_1,
  input  C,
  input  W_Ram,
  input  IO_Int,
  input  [3:0] in_5,
  input  [3:0] in_6,
  input  [3:0] in_7,
  input  [3:0] in_8,
  output [7:0] out_9,
  output Enable_IO_mt,
  output out_11,
  output out_12
);

  wire and_3_out, and_4_out, and_5_out, and_6_out, and_7_out, d_ff_1_q, d_ff_1_qn, d_ff_2_q, d_ff_2_qn,
       d_ff_3_qn, d_ff_4_q, d_ff_4_qn, d_ff_5_q, d_ff_5_qn, d_ff_6_q, d_ff_6_qn, d_ff_7_q, d_ff_7_qn,
       d_ff_8_q, d_ff_8_qn, d_ff_9_q, d_ff_9_qn, d_ff_10_q, d_ff_10_qn, or_1_out, or_2_out, or_3_out,
       or_4_out, or_5_out, or_6_out, or_7_out, or_8_out, or_9_out, or_10_out, or_11_out, or_12_out,
       or_13_out, or_14_out, or_15_out, or_16_out, or_17_out, or_18_out, undriven, undriven_2, undriven_3;
  wire [3:0] multiplexer_1_out, multiplexer_2_out, multiplexer_3_out, multiplexer_4_out, multiplexer_5_out,
       multiplexer_6_out, multiplexer_7_out, multiplexer_8_out, multiplexer_9_out, multiplexer_10_out,
       multiplexer_11_out, multiplexer_12_out, multiplexer_13_out, multiplexer_14_out, multiplexer_15_out,
       multiplexer_16_out;

  Multiplexer #(.width(4), .disabled(0), .enable("false")) multiplexer_1 (
    .in0(4'b0000), .in1(4'b0000), .out(multiplexer_1_out), .sel(in_8[0]));
  Multiplexer #(.width(4), .disabled(0), .enable("false")) multiplexer_2 (
    .in0(multiplexer_1_out), .in1(4'b0001), .out(multiplexer_2_out), .sel(in_8[1]));
  Multiplexer #(.width(4), .disabled(0), .enable("false")) multiplexer_3 (
    .in0(multiplexer_2_out), .in1(4'b0010), .out(multiplexer_3_out), .sel(in_8[2]));
  Multiplexer #(.width(4), .disabled(0), .enable("false")) multiplexer_4 (
    .in0(multiplexer_3_out), .in1(4'b0011), .out(multiplexer_4_out), .sel(in_8[3]));
  Register #(.width(4), .trigger("high")) register_1 (
    .D(multiplexer_16_out), .en(or_18_out), .Q(out_9[3:0]), .clk(or_18_out));  // open: clr
  or or_1 (or_1_out, in_8[0], in_8[1]);
  or or_2 (or_2_out, or_1_out, in_8[2]);
  or or_3 (or_3_out, or_2_out, in_8[3]);
  Register #(.width(4)) register_2 (.D(out_9[3:0]), .en(or_18_out), .Q(out_9[7:4]), .clk(or_18_out));  // open: clr
  D_Flip_Flop d_ff_1 (
    .clk(C), .D(or_9_out), .Q(d_ff_1_q), .Qn(d_ff_1_qn), .en(undriven), .reset(undriven_3));  // open: preset
  D_Flip_Flop d_ff_2 (
    .clk(or_18_out), .D(or_18_out), .Q(d_ff_2_q), .Qn(d_ff_2_qn), .en(undriven_2), .reset(or_4_out));  // open: preset
  D_Flip_Flop d_ff_3 (
    .clk(C), .D(d_ff_1_q), .Q(out_11), .Qn(d_ff_3_qn), .en(d_ff_1_q), .reset(or_10_out));  // open: preset
  or or_4 (or_4_out, d_ff_1_q, or_10_out);
  D_Flip_Flop d_ff_4 (
    .clk(or_18_out), .D(d_ff_2_q), .Q(d_ff_4_q), .Qn(d_ff_4_qn), .en(d_ff_2_q), .reset(or_4_out));  // open: preset
  Multiplexer #(.width(4), .disabled(0), .enable("false")) multiplexer_5 (
    .in0(multiplexer_4_out), .in1(4'b0100), .out(multiplexer_5_out), .sel(in_7[0]));
  Multiplexer #(.width(4), .disabled(0), .enable("false")) multiplexer_6 (
    .in0(multiplexer_5_out), .in1(4'b0101), .out(multiplexer_6_out), .sel(in_7[1]));
  Multiplexer #(.width(4), .disabled(0), .enable("false")) multiplexer_7 (
    .in0(multiplexer_6_out), .in1(4'b0110), .out(multiplexer_7_out), .sel(in_7[2]));
  Multiplexer #(.width(4), .disabled(0), .enable("false")) multiplexer_8 (
    .in0(multiplexer_7_out), .in1(4'b0111), .out(multiplexer_8_out), .sel(in_7[3]));
  and and_1 (Enable_IO_mt, out_11, d_ff_6_q);
  D_Flip_Flop d_ff_5 (
    .clk(C), .D(d_ff_4_q), .Q(d_ff_5_q), .Qn(d_ff_5_qn), .en(d_ff_4_q), .reset(or_4_out));  // open: preset
  or or_5 (or_5_out, or_3_out, in_7[0]);
  or or_6 (or_6_out, or_5_out, in_7[1]);
  or or_7 (or_7_out, or_6_out, in_7[2]);
  or or_8 (or_8_out, or_7_out, in_7[3]);
  or or_9 (or_9_out, IO_Int, and_6_out);
  or or_10 (or_10_out, and_7_out, d_ff_10_q);
  D_Flip_Flop d_ff_6 (
    .clk(C), .D(d_ff_5_q), .Q(d_ff_6_q), .Qn(d_ff_6_qn), .en(d_ff_5_q), .reset(or_4_out));  // open: preset
  Multiplexer #(.width(4), .disabled(0), .enable("false")) multiplexer_9 (
    .in0(multiplexer_8_out), .in1(4'b1000), .out(multiplexer_9_out), .sel(in_6[0]));
  Multiplexer #(.width(4), .disabled(0), .enable("false")) multiplexer_10 (
    .in0(multiplexer_9_out), .in1(4'b1001), .out(multiplexer_10_out), .sel(in_6[1]));
  Multiplexer #(.width(4), .disabled(0), .enable("false")) multiplexer_11 (
    .in0(multiplexer_10_out), .in1(4'b1010), .out(multiplexer_11_out), .sel(in_6[2]));
  Multiplexer #(.width(4), .disabled(0), .enable("false")) multiplexer_12 (
    .in0(multiplexer_11_out), .in1(4'b1011), .out(multiplexer_12_out), .sel(in_6[3]));
  D_Flip_Flop d_ff_7 (
    .clk(C), .D(Enable_IO_mt), .Q(d_ff_7_q), .Qn(d_ff_7_qn), .en(Enable_IO_mt), .reset(or_4_out));  // open: preset
  or or_11 (or_11_out, or_8_out, in_6[0]);
  or or_12 (or_12_out, or_11_out, in_6[1]);
  or or_13 (or_13_out, or_12_out, in_6[2]);
  or or_14 (or_14_out, or_13_out, in_6[3]);
  D_Flip_Flop d_ff_8 (
    .clk(C), .D(d_ff_7_q), .Q(d_ff_8_q), .Qn(d_ff_8_qn), .en(d_ff_7_q), .reset(or_4_out));  // open: preset
  and and_2 (out_12, ~in_1[0], in_1[1], ~in_1[2], ~in_1[3], ~in_1[4], ~in_1[5], ~in_1[6], ~in_1[7], in_1[8], in_1[9], in_1[10], in_1[11]);  // AND_Gate
  Multiplexer #(.width(4), .disabled(0), .enable("false")) multiplexer_13 (
    .in0(multiplexer_12_out), .in1(4'b1100), .out(multiplexer_13_out), .sel(in_5[0]));
  or or_15 (or_15_out, or_14_out, in_5[0]);
  Multiplexer #(.width(4), .disabled(0), .enable("false")) multiplexer_14 (
    .in0(multiplexer_13_out), .in1(4'b1101), .out(multiplexer_14_out), .sel(in_5[1]));
  or or_16 (or_16_out, or_15_out, in_5[1]);
  Multiplexer #(.width(4), .disabled(0), .enable("false")) multiplexer_15 (
    .in0(multiplexer_14_out), .in1(4'b1110), .out(multiplexer_15_out), .sel(in_5[2]));
  or or_17 (or_17_out, or_16_out, in_5[2]);
  Multiplexer #(.width(4), .disabled(0), .enable("false")) multiplexer_16 (
    .in0(multiplexer_15_out), .in1(4'b1111), .out(multiplexer_16_out), .sel(in_5[3]));
  or or_18 (or_18_out, or_17_out, in_5[3]);
  and and_3 (and_3_out, ~in_1[0], ~in_1[1], in_1[2], in_1[3]);  // AND_Gate
  and and_4 (and_4_out, in_1[0], ~in_1[1], in_1[2], in_1[3]);  // AND_Gate
  and and_5 (and_5_out, in_1[4], in_1[5], in_1[6], in_1[7], in_1[8], in_1[9], in_1[10], in_1[11]);
  D_Flip_Flop d_ff_9 (
    .clk(C), .D(d_ff_8_q), .Q(d_ff_9_q), .Qn(d_ff_9_qn), .en(d_ff_8_q), .reset(or_4_out));  // open: preset
  and and_6 (and_6_out, and_5_out, and_3_out, W_Ram);
  and and_7 (and_7_out, and_5_out, and_4_out, W_Ram);
  D_Flip_Flop d_ff_10 (
    .clk(C), .D(d_ff_9_q), .Q(d_ff_10_q), .Qn(d_ff_10_qn), .en(d_ff_9_q), .reset(or_4_out));  // open: preset

  // Notes on the sheet:
  //   Data
  //   Int enabled
  //   Hex IN
  //   Enable IO Int
  //   Adr
  //   Disable
  //   Gen Interrupt Preventer reset f02
  //   Gen Interrupt Preventer reset f02
endmodule

module Registers (
  input  [15:0] in_1,
  input  [15:0] in_2,
  input  [15:0] in_3,
  input  [15:0] in_4,
  input  [15:0] in_5,
  input  [7:0] in_6,
  input  [7:0] in_7,
  input  [7:0] in_8,
  input  in_9,
  output [7:0] out_10,
  output [7:0] out_11,
  output [7:0] out_12,
  output [7:0] out_13,
  output [15:0] out_14
);

  wire [7:0] multiplexer_1_out, multiplexer_2_out, multiplexer_3_out, multiplexer_4_out, multiplexer_5_out,
       multiplexer_6_out, multiplexer_7_out, multiplexer_8_out, multiplexer_9_out, multiplexer_10_out,
       multiplexer_11_out, multiplexer_12_out, multiplexer_13_out, multiplexer_14_out, multiplexer_15_out,
       multiplexer_17_out, multiplexer_18_out, multiplexer_19_out, multiplexer_20_out, multiplexer_21_out,
       multiplexer_22_out, multiplexer_23_out, multiplexer_24_out, multiplexer_25_out, multiplexer_26_out,
       multiplexer_27_out, multiplexer_28_out, multiplexer_29_out, multiplexer_30_out, multiplexer_31_out,
       multiplexer_33_out, multiplexer_34_out, multiplexer_35_out, multiplexer_36_out, multiplexer_37_out,
       multiplexer_38_out, multiplexer_39_out, multiplexer_40_out, multiplexer_41_out, multiplexer_42_out,
       multiplexer_43_out, multiplexer_44_out, multiplexer_45_out, multiplexer_46_out, multiplexer_47_out,
       multiplexer_49_out, multiplexer_50_out, multiplexer_51_out, multiplexer_52_out, multiplexer_53_out,
       multiplexer_54_out, multiplexer_55_out, multiplexer_56_out, multiplexer_57_out, multiplexer_58_out,
       multiplexer_59_out, multiplexer_60_out, multiplexer_61_out, multiplexer_62_out, multiplexer_63_out,
       multiplexer_65_out, multiplexer_66_out, multiplexer_67_out, multiplexer_68_out, multiplexer_69_out,
       multiplexer_70_out, multiplexer_71_out, multiplexer_72_out, multiplexer_73_out, multiplexer_74_out,
       multiplexer_75_out, multiplexer_76_out, multiplexer_77_out, multiplexer_78_out, Reg_0_q, Reg_1_q,
       Reg_2_q, Reg_3_q, Reg_4_q, Reg_5_q, Reg_6_q, Reg_7_q, Reg_8_q, Reg_9_q, Reg_A_q, Reg_B_q, Reg_C_q,
       Reg_D_q, Reg_E_q, Reg_F_q;

  Register Reg_0 (.D(in_7), .en(in_1[0]), .Q(Reg_0_q), .clk(in_9));  // open: clr
  Register Reg_1 (.D(in_8), .en(in_1[1]), .Q(Reg_1_q), .clk(in_9));  // open: clr
  Register Reg_2 (.D(in_7), .en(in_1[2]), .Q(Reg_2_q), .clk(in_9));  // open: clr
  Register Reg_3 (.D(in_8), .en(in_1[3]), .Q(Reg_3_q), .clk(in_9));  // open: clr
  Register Reg_4 (.D(in_7), .en(in_1[4]), .Q(Reg_4_q), .clk(in_9));  // open: clr
  Register Reg_5 (.D(in_8), .en(in_1[5]), .Q(Reg_5_q), .clk(in_9));  // open: clr
  Register Reg_6 (.D(in_7), .en(in_1[6]), .Q(Reg_6_q), .clk(in_9));  // open: clr
  Register Reg_7 (.D(in_8), .en(in_1[7]), .Q(Reg_7_q), .clk(in_9));  // open: clr
  Register Reg_8 (.D(in_7), .en(in_1[8]), .Q(Reg_8_q), .clk(in_9));  // open: clr
  Register Reg_9 (.D(in_8), .en(in_1[9]), .Q(Reg_9_q), .clk(in_9));  // open: clr
  Register Reg_A (.D(in_7), .en(in_1[10]), .Q(Reg_A_q), .clk(in_9));  // open: clr
  Register Reg_B (.D(in_8), .en(in_1[11]), .Q(Reg_B_q), .clk(in_9));  // open: clr
  Register Reg_C (.D(in_7), .en(in_1[12]), .Q(Reg_C_q), .clk(in_9));  // open: clr
  Register Reg_D (.D(in_8), .en(in_1[13]), .Q(Reg_D_q), .clk(in_9));  // open: clr
  Register Reg_E (.D(in_7), .en(in_1[14]), .Q(Reg_E_q), .clk(in_9));  // open: clr
  Register Reg_F (.D(in_8), .en(in_1[15]), .Q(Reg_F_q), .clk(in_9));  // open: clr
  Multiplexer #(.width(8), .enable("false")) multiplexer_1 (
    .in0({8{1'b0}}), .in1(Reg_0_q), .out(multiplexer_1_out), .sel(in_2[0]));
  Multiplexer #(.width(8), .enable("false")) multiplexer_2 (
    .in0(multiplexer_1_out), .in1(Reg_1_q), .out(multiplexer_2_out), .sel(in_2[1]));
  Multiplexer #(.width(8), .enable("false")) multiplexer_3 (
    .in0(multiplexer_2_out), .in1(Reg_2_q), .out(multiplexer_3_out), .sel(in_2[2]));
  Multiplexer #(.width(8), .enable("false")) multiplexer_4 (
    .in0(multiplexer_3_out), .in1(Reg_3_q), .out(multiplexer_4_out), .sel(in_2[3]));
  Multiplexer #(.width(8), .enable("false")) multiplexer_5 (
    .in0(multiplexer_4_out), .in1(Reg_4_q), .out(multiplexer_5_out), .sel(in_2[4]));
  Multiplexer #(.width(8), .enable("false")) multiplexer_6 (
    .in0(multiplexer_5_out), .in1(Reg_5_q), .out(multiplexer_6_out), .sel(in_2[5]));
  Multiplexer #(.width(8), .enable("false")) multiplexer_7 (
    .in0(multiplexer_6_out), .in1(Reg_6_q), .out(multiplexer_7_out), .sel(in_2[6]));
  Multiplexer #(.width(8), .enable("false")) multiplexer_8 (
    .in0(multiplexer_7_out), .in1(Reg_7_q), .out(multiplexer_8_out), .sel(in_2[7]));
  Multiplexer #(.width(8), .enable("false")) multiplexer_9 (
    .in0(multiplexer_8_out), .in1(Reg_8_q), .out(multiplexer_9_out), .sel(in_2[8]));
  Multiplexer #(.width(8), .enable("false")) multiplexer_10 (
    .in0(multiplexer_9_out), .in1(Reg_9_q), .out(multiplexer_10_out), .sel(in_2[9]));
  Multiplexer #(.width(8), .enable("false")) multiplexer_11 (
    .in0(multiplexer_10_out), .in1(Reg_A_q), .out(multiplexer_11_out), .sel(in_2[10]));
  Multiplexer #(.width(8), .enable("false")) multiplexer_12 (
    .in0(multiplexer_11_out), .in1(Reg_B_q), .out(multiplexer_12_out), .sel(in_2[11]));
  Multiplexer #(.width(8), .enable("false")) multiplexer_13 (
    .in0(multiplexer_12_out), .in1(Reg_C_q), .out(multiplexer_13_out), .sel(in_2[12]));
  Multiplexer #(.width(8), .enable("false")) multiplexer_14 (
    .in0(multiplexer_13_out), .in1(Reg_D_q), .out(multiplexer_14_out), .sel(in_2[13]));
  Multiplexer #(.width(8), .enable("false")) multiplexer_15 (
    .in0(multiplexer_14_out), .in1(Reg_E_q), .out(multiplexer_15_out), .sel(in_2[14]));
  Multiplexer #(.width(8), .enable("false")) multiplexer_16 (
    .in0(multiplexer_15_out), .in1(Reg_F_q), .out(out_10), .sel(in_2[15]));
  Multiplexer #(.width(8), .enable("false")) multiplexer_17 (
    .in0({8{1'b0}}), .in1(Reg_0_q), .out(multiplexer_17_out), .sel(in_3[0]));
  Multiplexer #(.width(8), .enable("false")) multiplexer_18 (
    .in0(multiplexer_17_out), .in1(Reg_1_q), .out(multiplexer_18_out), .sel(in_3[1]));
  Multiplexer #(.width(8), .enable("false")) multiplexer_19 (
    .in0(multiplexer_18_out), .in1(Reg_2_q), .out(multiplexer_19_out), .sel(in_3[2]));
  Multiplexer #(.width(8), .enable("false")) multiplexer_20 (
    .in0(multiplexer_19_out), .in1(Reg_3_q), .out(multiplexer_20_out), .sel(in_3[3]));
  Multiplexer #(.width(8), .enable("false")) multiplexer_21 (
    .in0(multiplexer_20_out), .in1(Reg_4_q), .out(multiplexer_21_out), .sel(in_3[4]));
  Multiplexer #(.width(8), .enable("false")) multiplexer_22 (
    .in0(multiplexer_21_out), .in1(Reg_5_q), .out(multiplexer_22_out), .sel(in_3[5]));
  Multiplexer #(.width(8), .enable("false")) multiplexer_23 (
    .in0(multiplexer_22_out), .in1(Reg_6_q), .out(multiplexer_23_out), .sel(in_3[6]));
  Multiplexer #(.width(8), .enable("false")) multiplexer_24 (
    .in0(multiplexer_23_out), .in1(Reg_7_q), .out(multiplexer_24_out), .sel(in_3[7]));
  Multiplexer #(.width(8), .enable("false")) multiplexer_25 (
    .in0(multiplexer_24_out), .in1(Reg_8_q), .out(multiplexer_25_out), .sel(in_3[8]));
  Multiplexer #(.width(8), .enable("false")) multiplexer_26 (
    .in0(multiplexer_25_out), .in1(Reg_9_q), .out(multiplexer_26_out), .sel(in_3[9]));
  Multiplexer #(.width(8), .enable("false")) multiplexer_27 (
    .in0(multiplexer_26_out), .in1(Reg_A_q), .out(multiplexer_27_out), .sel(in_3[10]));
  Multiplexer #(.width(8), .enable("false")) multiplexer_28 (
    .in0(multiplexer_27_out), .in1(Reg_B_q), .out(multiplexer_28_out), .sel(in_3[11]));
  Multiplexer #(.width(8), .enable("false")) multiplexer_29 (
    .in0(multiplexer_28_out), .in1(Reg_C_q), .out(multiplexer_29_out), .sel(in_3[12]));
  Multiplexer #(.width(8), .enable("false")) multiplexer_30 (
    .in0(multiplexer_29_out), .in1(Reg_D_q), .out(multiplexer_30_out), .sel(in_3[13]));
  Multiplexer #(.width(8), .enable("false")) multiplexer_31 (
    .in0(multiplexer_30_out), .in1(Reg_E_q), .out(multiplexer_31_out), .sel(in_3[14]));
  Multiplexer #(.width(8), .enable("false")) multiplexer_32 (
    .in0(multiplexer_31_out), .in1(Reg_F_q), .out(out_11), .sel(in_3[15]));
  Multiplexer #(.width(8), .enable("false")) multiplexer_33 (
    .in0({8{1'b0}}), .in1(Reg_0_q), .out(multiplexer_33_out), .sel(in_4[0]));
  Multiplexer #(.width(8), .enable("false")) multiplexer_34 (
    .in0(multiplexer_33_out), .in1(Reg_1_q), .out(multiplexer_34_out), .sel(in_4[1]));
  Multiplexer #(.width(8), .enable("false")) multiplexer_35 (
    .in0(multiplexer_34_out), .in1(Reg_2_q), .out(multiplexer_35_out), .sel(in_4[2]));
  Multiplexer #(.width(8), .enable("false")) multiplexer_36 (
    .in0(multiplexer_35_out), .in1(Reg_3_q), .out(multiplexer_36_out), .sel(in_4[3]));
  Multiplexer #(.width(8), .enable("false")) multiplexer_37 (
    .in0(multiplexer_36_out), .in1(Reg_4_q), .out(multiplexer_37_out), .sel(in_4[4]));
  Multiplexer #(.width(8), .enable("false")) multiplexer_38 (
    .in0(multiplexer_37_out), .in1(Reg_5_q), .out(multiplexer_38_out), .sel(in_4[5]));
  Multiplexer #(.width(8), .enable("false")) multiplexer_39 (
    .in0(multiplexer_38_out), .in1(Reg_6_q), .out(multiplexer_39_out), .sel(in_4[6]));
  Multiplexer #(.width(8), .enable("false")) multiplexer_40 (
    .in0(multiplexer_39_out), .in1(Reg_7_q), .out(multiplexer_40_out), .sel(in_4[7]));
  Multiplexer #(.width(8), .enable("false")) multiplexer_41 (
    .in0(multiplexer_40_out), .in1(Reg_8_q), .out(multiplexer_41_out), .sel(in_4[8]));
  Multiplexer #(.width(8), .enable("false")) multiplexer_42 (
    .in0(multiplexer_41_out), .in1(Reg_9_q), .out(multiplexer_42_out), .sel(in_4[9]));
  Multiplexer #(.width(8), .enable("false")) multiplexer_43 (
    .in0(multiplexer_42_out), .in1(Reg_A_q), .out(multiplexer_43_out), .sel(in_4[10]));
  Multiplexer #(.width(8), .enable("false")) multiplexer_44 (
    .in0(multiplexer_43_out), .in1(Reg_B_q), .out(multiplexer_44_out), .sel(in_4[11]));
  Multiplexer #(.width(8), .enable("false")) multiplexer_45 (
    .in0(multiplexer_44_out), .in1(Reg_C_q), .out(multiplexer_45_out), .sel(in_4[12]));
  Multiplexer #(.width(8), .enable("false")) multiplexer_46 (
    .in0(multiplexer_45_out), .in1(Reg_D_q), .out(multiplexer_46_out), .sel(in_4[13]));
  Multiplexer #(.width(8), .enable("false")) multiplexer_47 (
    .in0(multiplexer_46_out), .in1(Reg_E_q), .out(multiplexer_47_out), .sel(in_4[14]));
  Multiplexer #(.width(8), .enable("false")) multiplexer_48 (
    .in0(multiplexer_47_out), .in1(Reg_F_q), .out(out_12), .sel(in_4[15]));
  Multiplexer #(.width(8), .enable("false")) multiplexer_49 (
    .in0({8{1'b0}}), .in1(Reg_0_q), .out(multiplexer_49_out), .sel(in_5[0]));
  Multiplexer #(.width(8), .enable("false")) multiplexer_50 (
    .in0(multiplexer_49_out), .in1(Reg_1_q), .out(multiplexer_50_out), .sel(in_5[1]));
  Multiplexer #(.width(8), .enable("false")) multiplexer_51 (
    .in0(multiplexer_50_out), .in1(Reg_2_q), .out(multiplexer_51_out), .sel(in_5[2]));
  Multiplexer #(.width(8), .enable("false")) multiplexer_52 (
    .in0(multiplexer_51_out), .in1(Reg_3_q), .out(multiplexer_52_out), .sel(in_5[3]));
  Multiplexer #(.width(8), .enable("false")) multiplexer_53 (
    .in0(multiplexer_52_out), .in1(Reg_4_q), .out(multiplexer_53_out), .sel(in_5[4]));
  Multiplexer #(.width(8), .enable("false")) multiplexer_54 (
    .in0(multiplexer_53_out), .in1(Reg_5_q), .out(multiplexer_54_out), .sel(in_5[5]));
  Multiplexer #(.width(8), .enable("false")) multiplexer_55 (
    .in0(multiplexer_54_out), .in1(Reg_6_q), .out(multiplexer_55_out), .sel(in_5[6]));
  Multiplexer #(.width(8), .enable("false")) multiplexer_56 (
    .in0(multiplexer_55_out), .in1(Reg_7_q), .out(multiplexer_56_out), .sel(in_5[7]));
  Multiplexer #(.width(8), .enable("false")) multiplexer_57 (
    .in0(multiplexer_56_out), .in1(Reg_8_q), .out(multiplexer_57_out), .sel(in_5[8]));
  Multiplexer #(.width(8), .enable("false")) multiplexer_58 (
    .in0(multiplexer_57_out), .in1(Reg_9_q), .out(multiplexer_58_out), .sel(in_5[9]));
  Multiplexer #(.width(8), .enable("false")) multiplexer_59 (
    .in0(multiplexer_58_out), .in1(Reg_A_q), .out(multiplexer_59_out), .sel(in_5[10]));
  Multiplexer #(.width(8), .enable("false")) multiplexer_60 (
    .in0(multiplexer_59_out), .in1(Reg_B_q), .out(multiplexer_60_out), .sel(in_5[11]));
  Multiplexer #(.width(8), .enable("false")) multiplexer_61 (
    .in0(multiplexer_60_out), .in1(Reg_C_q), .out(multiplexer_61_out), .sel(in_5[12]));
  Multiplexer #(.width(8), .enable("false")) multiplexer_62 (
    .in0(multiplexer_61_out), .in1(Reg_D_q), .out(multiplexer_62_out), .sel(in_5[13]));
  Multiplexer #(.width(8), .enable("false")) multiplexer_63 (
    .in0(multiplexer_62_out), .in1(Reg_E_q), .out(multiplexer_63_out), .sel(in_5[14]));
  Multiplexer #(.width(8), .enable("false")) multiplexer_64 (
    .in0(multiplexer_63_out), .in1(Reg_F_q), .out(out_13), .sel(in_5[15]));
  Multiplexer #(.width(8), .enable("false")) multiplexer_65 (
    .in0({8{1'b0}}), .in1(Reg_0_q), .out(multiplexer_65_out), .sel(in_6[0]));
  Multiplexer #(.width(8), .enable("false")) multiplexer_66 (
    .in0({8{1'b0}}), .in1(Reg_1_q), .out(multiplexer_66_out), .sel(in_6[0]));
  Multiplexer #(.width(8), .enable("false")) multiplexer_67 (
    .in0(multiplexer_65_out), .in1(Reg_2_q), .out(multiplexer_67_out), .sel(in_6[1]));
  Multiplexer #(.width(8), .enable("false")) multiplexer_68 (
    .in0(multiplexer_66_out), .in1(Reg_3_q), .out(multiplexer_68_out), .sel(in_6[1]));
  Multiplexer #(.width(8), .enable("false")) multiplexer_69 (
    .in0(multiplexer_67_out), .in1(Reg_4_q), .out(multiplexer_69_out), .sel(in_6[2]));
  Multiplexer #(.width(8), .enable("false")) multiplexer_70 (
    .in0(multiplexer_68_out), .in1(Reg_5_q), .out(multiplexer_70_out), .sel(in_6[2]));
  Multiplexer #(.width(8), .enable("false")) multiplexer_71 (
    .in0(multiplexer_69_out), .in1(Reg_6_q), .out(multiplexer_71_out), .sel(in_6[3]));
  Multiplexer #(.width(8), .enable("false")) multiplexer_72 (
    .in0(multiplexer_70_out), .in1(Reg_7_q), .out(multiplexer_72_out), .sel(in_6[3]));
  Multiplexer #(.width(8), .enable("false")) multiplexer_73 (
    .in0(multiplexer_71_out), .in1(Reg_8_q), .out(multiplexer_73_out), .sel(in_6[4]));
  Multiplexer #(.width(8), .enable("false")) multiplexer_74 (
    .in0(multiplexer_72_out), .in1(Reg_9_q), .out(multiplexer_74_out), .sel(in_6[4]));
  Multiplexer #(.width(8), .enable("false")) multiplexer_75 (
    .in0(multiplexer_73_out), .in1(Reg_A_q), .out(multiplexer_75_out), .sel(in_6[5]));
  Multiplexer #(.width(8), .enable("false")) multiplexer_76 (
    .in0(multiplexer_74_out), .in1(Reg_B_q), .out(multiplexer_76_out), .sel(in_6[5]));
  Multiplexer #(.width(8), .enable("false")) multiplexer_77 (
    .in0(multiplexer_75_out), .in1(Reg_C_q), .out(multiplexer_77_out), .sel(in_6[6]));
  Multiplexer #(.width(8), .enable("false")) multiplexer_78 (
    .in0(multiplexer_76_out), .in1(Reg_D_q), .out(multiplexer_78_out), .sel(in_6[6]));
  Multiplexer #(.width(8), .enable("false")) multiplexer_79 (
    .in0(multiplexer_77_out), .in1(Reg_E_q), .out(out_14[7:0]), .sel(in_6[7]));
  Multiplexer #(.width(8), .enable("false")) multiplexer_80 (
    .in0(multiplexer_78_out), .in1(Reg_F_q), .out(out_14[15:8]), .sel(in_6[7]));
endmodule

module Control (
  input  in_1,
  input  in_2,
  input  [15:0] in_3,
  input  in_4,
  input  in_5,
  input  in_6,
  input  in_7,
  input  in_8,
  input  in_9,
  output out_10,
  output [15:0] out_11,
  output [15:0] out_12,
  output [15:0] out_13,
  output [15:0] out_14,
  output [15:0] out_15,
  output [7:0] out_16,
  output [4:0] out_17,
  output [2:0] out_18,
  output [14:0] out_19,
  output out_20,
  output out_21,
  output out_22,
  output out_23,
  output out_24,
  output out_25
);

  wire _4_out, _5_out, _6_out, _7_out, _9_out, a_out, and_2_out, and_3_out, and_4_out, b_out, d_out,
       decoder_1_out0, decoder_1_out1, decoder_1_out2, decoder_1_out3, decoder_1_out4, decoder_1_out5,
       decoder_1_out6, decoder_1_out7, decoder_1_out8, decoder_1_out9, decoder_1_out10, decoder_1_out11,
       decoder_1_out12, decoder_1_out13, decoder_1_out14, decoder_1_out15, decoder_2_out0, decoder_2_out1,
       decoder_2_out2, decoder_2_out3, decoder_2_out4, decoder_2_out5, decoder_2_out6, decoder_2_out7,
       decoder_2_out8, decoder_2_out9, decoder_2_out10, decoder_2_out11, decoder_2_out12, decoder_2_out13,
       decoder_2_out14, decoder_2_out15, decoder_3_out0, decoder_3_out1, decoder_3_out2, decoder_3_out3,
       decoder_3_out4, decoder_3_out5, decoder_3_out6, decoder_3_out7, decoder_3_out8, decoder_3_out9,
       decoder_3_out10, decoder_3_out11, decoder_3_out12, decoder_3_out13, decoder_3_out14, decoder_3_out15,
       decoder_4_out0, decoder_4_out1, decoder_4_out2, decoder_4_out3, decoder_4_out4, decoder_4_out5,
       decoder_4_out6, decoder_4_out7, decoder_4_out8, decoder_4_out9, decoder_4_out10, decoder_4_out11,
       decoder_4_out12, decoder_4_out13, decoder_4_out14, decoder_4_out15, decoder_5_out0, decoder_5_out1,
       decoder_5_out2, decoder_5_out3, decoder_5_out4, decoder_5_out5, decoder_5_out6, decoder_5_out7,
       decoder_5_out8, decoder_5_out9, decoder_5_out10, decoder_5_out11, decoder_5_out12, decoder_5_out13,
       decoder_5_out14, decoder_5_out15, decoder_6_out6, decoder_6_out8, decoder_6_out9, decoder_6_out10,
       decoder_6_out11, decoder_6_out12, decoder_6_out13, decoder_6_out14, decoder_6_out15, decoder_7_out6,
       decoder_9_out6, decoder_10_out7, decoder_11_out1, decoder_11_out3, decoder_11_out5, decoder_11_out7,
       decoder_11_out9, decoder_11_out10, decoder_11_out11, decoder_11_out12, decoder_11_out13,
       decoder_11_out15, e_out, f0_out, fe_out, fffe_out, or_1_out, or_2_out, or_3_out, or_4_out, or_5_out,
       or_6_out, or_7_out, or_8_out, or_9_out, or_10_out, or_11_out, or_12_out, or_13_out, or_14_out,
       or_15_out, or_16_out, or_17_out, or_19_out, or_20_out, or_21_out, or_22_out, or_23_out, or_24_out,
       or_25_out, or_26_out, or_27_out, or_28_out, or_29_out, or_30_out, or_31_out, or_32_out, or_33_out,
       or_34_out, or_35_out, or_36_out, or_37_out, or_38_out, or_39_out, or_40_out, or_41_out, or_42_out,
       or_43_out, or_44_out, or_45_out, or_46_out, or_47_out, or_48_out, or_49_out, or_50_out, or_51_out,
       or_52_out, or_54_out, or_55_out, or_56_out, or_57_out, or_58_out, or_59_out, or_60_out, or_61_out,
       or_62_out, or_64_out, or_65_out, or_66_out, or_67_out, or_68_out, or_69_out, or_70_out, or_71_out,
       or_72_out, or_73_out, or_75_out, or_76_out, undriven, undriven_2, undriven_3, undriven_4;
  wire [3:0] multiplexer_1_out, multiplexer_2_out, multiplexer_3_out, multiplexer_4_out, multiplexer_5_out,
       multiplexer_6_out;

  Decoder #(.select(4), .disabled(0)) decoder_1 (
    .out0(decoder_1_out0), .out1(decoder_1_out1), .out2(decoder_1_out2), .out3(decoder_1_out3),
    .out4(decoder_1_out4), .out5(decoder_1_out5), .out6(decoder_1_out6), .out7(decoder_1_out7),
    .out8(decoder_1_out8), .out9(decoder_1_out9), .out10(decoder_1_out10), .out11(decoder_1_out11),
    .out12(decoder_1_out12), .out13(decoder_1_out13), .out14(decoder_1_out14), .out15(decoder_1_out15),
    .sel(in_3[3:0]), .en(decoder_2_out15));
  Decoder #(.select(4), .disabled(0)) decoder_2 (
    .out0(decoder_2_out0), .out1(decoder_2_out1), .out2(decoder_2_out2), .out3(decoder_2_out3),
    .out4(decoder_2_out4), .out5(decoder_2_out5), .out6(decoder_2_out6), .out7(decoder_2_out7),
    .out8(decoder_2_out8), .out9(decoder_2_out9), .out10(decoder_2_out10), .out11(decoder_2_out11),
    .out12(decoder_2_out12), .out13(decoder_2_out13), .out14(decoder_2_out14), .out15(decoder_2_out15),
    .sel(in_3[7:4]), .en(decoder_4_out15));
  Decoder #(.select(4), .disabled(0)) decoder_3 (
    .out0(decoder_3_out0), .out1(decoder_3_out1), .out2(decoder_3_out2), .out3(decoder_3_out3),
    .out4(decoder_3_out4), .out5(decoder_3_out5), .out6(decoder_3_out6), .out7(decoder_3_out7),
    .out8(decoder_3_out8), .out9(decoder_3_out9), .out10(decoder_3_out10), .out11(decoder_3_out11),
    .out12(decoder_3_out12), .out13(decoder_3_out13), .out14(decoder_3_out14), .out15(decoder_3_out15),
    .sel(in_3[11:8]), .en(decoder_5_out2));
  Decoder #(.select(4), .disabled(0)) decoder_4 (
    .out0(decoder_4_out0), .out1(decoder_4_out1), .out2(decoder_4_out2), .out3(decoder_4_out3),
    .out4(decoder_4_out4), .out5(decoder_4_out5), .out6(decoder_4_out6), .out7(decoder_4_out7),
    .out8(decoder_4_out8), .out9(decoder_4_out9), .out10(decoder_4_out10), .out11(decoder_4_out11),
    .out12(decoder_4_out12), .out13(decoder_4_out13), .out14(decoder_4_out14), .out15(decoder_4_out15),
    .sel(in_3[11:8]), .en(decoder_5_out15));
  Decoder #(.select(4), .disabled(0), .enable("false")) decoder_5 (
    .out0(decoder_5_out0), .out1(decoder_5_out1), .out2(decoder_5_out2), .out3(decoder_5_out3),
    .out4(decoder_5_out4), .out5(decoder_5_out5), .out6(decoder_5_out6), .out7(decoder_5_out7),
    .out8(decoder_5_out8), .out9(decoder_5_out9), .out10(decoder_5_out10), .out11(decoder_5_out11),
    .out12(decoder_5_out12), .out13(decoder_5_out13), .out14(decoder_5_out14), .out15(decoder_5_out15),
    .sel(in_3[15:12]));
  Multiplexer #(.width(4), .enable("false")) multiplexer_1 (
    .in0(in_3[11:8]), .in1(in_3[7:4]), .out(multiplexer_1_out), .sel(or_33_out));
  Multiplexer #(.width(4), .enable("false")) multiplexer_2 (
    .in0(in_3[7:4]), .in1(in_3[11:8]), .out(multiplexer_2_out), .sel(out_18[0]));
  Multiplexer #(.width(4), .enable("false")) multiplexer_3 (
    .in0(in_3[3:0]), .in1(4'b0000), .out(multiplexer_3_out), .sel(1'b0));
  Multiplexer #(.width(4), .enable("false")) multiplexer_4 (
    .in0(in_3[11:8]), .in1(in_3[7:4]), .out(multiplexer_4_out), .sel(f0_out));
  Multiplexer #(.width(4), .enable("false")) multiplexer_5 (
    .in0(in_3[3:0]), .in1(4'b0000), .out(multiplexer_5_out), .sel(1'b0));
  Multiplexer #(.width(4), .enable("false")) multiplexer_6 (
    .in0(in_3[7:4]), .in1(4'b0000), .out(multiplexer_6_out), .sel(1'b0));
  Decoder #(.select(4), .disabled(0)) decoder_6 (
    .out0(out_11[0]), .out1(out_11[1]), .out2(out_11[2]), .out3(out_11[3]), .out4(out_11[4]),
    .out5(out_11[5]), .out6(decoder_6_out6), .out7(out_11[7]), .out8(decoder_6_out8), .out9(decoder_6_out9),
    .out10(decoder_6_out10), .out11(decoder_6_out11), .out12(decoder_6_out12), .out13(decoder_6_out13),
    .out14(decoder_6_out14), .out15(decoder_6_out15), .sel(multiplexer_1_out), .en(or_31_out));
  Decoder #(.select(4), .disabled(0)) decoder_7 (
    .out0(out_12[0]), .out1(out_12[1]), .out2(out_12[2]), .out3(out_12[3]), .out4(out_12[4]),
    .out5(out_12[5]), .out6(decoder_7_out6), .out7(out_12[7]), .out8(out_12[8]), .out9(out_12[9]),
    .out10(out_12[10]), .out11(out_12[11]), .out12(out_12[12]), .out13(out_12[13]), .out14(out_12[14]),
    .out15(out_12[15]), .sel(multiplexer_2_out), .en(or_1_out));
  Decoder #(.select(4), .disabled(0)) decoder_8 (
    .out0(out_13[0]), .out1(out_13[1]), .out2(out_13[2]), .out3(out_13[3]), .out4(out_13[4]),
    .out5(out_13[5]), .out6(out_13[6]), .out7(out_13[7]), .out8(out_13[8]), .out9(out_13[9]),
    .out10(out_13[10]), .out11(out_13[11]), .out12(out_13[12]), .out13(out_13[13]), .out14(out_13[14]),
    .out15(out_13[15]), .sel(multiplexer_3_out), .en(or_2_out));
  Decoder #(.select(4), .disabled(0)) decoder_9 (
    .out0(out_14[0]), .out1(out_14[1]), .out2(out_14[2]), .out3(out_14[3]), .out4(out_14[4]),
    .out5(out_14[5]), .out6(decoder_9_out6), .out7(out_14[7]), .out8(out_14[8]), .out9(out_14[9]),
    .out10(out_14[10]), .out11(out_14[11]), .out12(out_14[12]), .out13(out_14[13]), .out14(out_14[14]),
    .out15(out_14[15]), .sel(multiplexer_4_out), .en(or_64_out));
  Decoder #(.select(4), .disabled(0)) decoder_10 (
    .out0(out_15[0]), .out1(out_15[1]), .out2(out_15[2]), .out3(out_15[3]), .out4(out_15[4]),
    .out5(out_15[5]), .out6(out_15[6]), .out7(decoder_10_out7), .out8(out_15[8]), .out9(out_15[9]),
    .out10(out_15[10]), .out11(out_15[11]), .out12(out_15[12]), .out13(out_15[13]), .out14(out_15[14]),
    .out15(out_15[15]), .sel(multiplexer_5_out), .en(or_46_out));
  Decoder #(.select(4), .disabled(0)) decoder_11 (
    .out0(out_16[0]), .out1(decoder_11_out1), .out2(out_16[1]), .out3(decoder_11_out3), .out4(out_16[2]),
    .out5(decoder_11_out5), .out6(out_16[3]), .out7(decoder_11_out7), .out8(out_16[4]),
    .out9(decoder_11_out9), .out10(decoder_11_out10), .out11(decoder_11_out11), .out12(decoder_11_out12),
    .out13(decoder_11_out13), .out14(out_16[7]), .out15(decoder_11_out15), .sel(multiplexer_6_out),
    .en(or_16_out));
  and _0 (out_19[1], decoder_5_out0, in_9);
  and _1 (out_19[14], decoder_5_out1, in_9);
  and _20 (out_19[0], decoder_3_out0, in_9);
  and _21 (out_19[13], decoder_3_out1, in_9);
  and _22 (out_19[12], decoder_3_out2, in_9);
  and _23 (out_19[11], decoder_3_out3, in_9);
  and _24 (out_19[10], decoder_3_out4, in_9);
  and _25 (out_19[9], decoder_3_out5, in_9);
  and _26 (out_19[8], decoder_3_out6, in_9);
  and _27 (out_19[7], decoder_3_out7, in_9);
  and _28 (out_19[6], decoder_3_out8, in_9);
  and _29 (out_19[5], decoder_3_out9, in_9);
  and _2a (out_19[4], decoder_3_out10, in_9);
  and _2b (out_19[3], decoder_3_out11, in_9);
  and _3 (out_18[0], decoder_5_out3, in_9);
  and _4 (_4_out, decoder_5_out4, in_9);
  and _5 (_5_out, decoder_5_out5, in_9);
  and _6 (_6_out, decoder_5_out6, in_9);
  and _7 (_7_out, decoder_5_out7, in_9);
  and _8 (out_18[1], decoder_5_out8, in_9);
  and _9 (_9_out, decoder_5_out9, in_9);
  and a (a_out, decoder_5_out10, in_9);
  and b (b_out, decoder_5_out11, in_9);
  and c (out_23, decoder_5_out12, in_9);
  and d (d_out, decoder_5_out13, in_9);
  and e (e_out, decoder_5_out14, in_9);
  and f0 (f0_out, decoder_4_out0, in_9);
  and and_1 (out_10, decoder_4_out0, in_8);
  and f1 (out_20, decoder_4_out1, in_9);
  and and_2 (and_2_out, decoder_4_out1, in_8);
  and fe (fe_out, decoder_4_out14, in_9);
  and fffe (fffe_out, decoder_1_out14, in_9);
  and ffff (out_25, decoder_1_out15, in_9);
  or or_1 (or_1_out, out_19[1], or_32_out);
  or or_2 (or_2_out, out_19[14], or_3_out);
  or or_3 (or_3_out, out_19[0], or_4_out);
  or or_4 (or_4_out, out_19[13], or_5_out);
  or or_5 (or_5_out, out_19[12], or_6_out);
  or or_6 (or_6_out, out_19[11], or_7_out);
  or or_7 (or_7_out, out_19[10], or_8_out);
  or or_8 (or_8_out, out_19[9], or_9_out);
  or or_9 (or_9_out, out_19[8], or_10_out);
  or or_10 (or_10_out, out_19[7], or_14_out);
  or or_11 (or_11_out, out_19[6], or_12_out);
  or or_12 (or_12_out, out_19[5], or_13_out);
  or or_13 (or_13_out, out_19[4], or_44_out);
  or or_14 (or_14_out, out_19[3], 1'b0);
  or or_15 (or_15_out, out_18[0], or_73_out);
  or or_16 (or_16_out, _4_out, or_17_out);
  or or_17 (or_17_out, _5_out, 1'b0);
  or or_18 (out_18[2], _6_out, or_19_out);
  or or_19 (or_19_out, _7_out, or_21_out);
  or or_20 (or_20_out, out_18[1], and_2_out);
  or or_21 (or_21_out, _9_out, or_22_out);
  or or_22 (or_22_out, a_out, or_23_out);
  or or_23 (or_23_out, b_out, or_24_out);
  or or_24 (or_24_out, out_23, or_25_out);
  or or_25 (or_25_out, d_out, e_out);
  or or_26 (or_26_out, f0_out, or_27_out);
  or or_27 (or_27_out, out_10, or_28_out);
  or or_28 (or_28_out, out_20, and_2_out);
  or or_29 (or_29_out, and_2_out, undriven);
  or or_30 (or_30_out, fe_out, undriven_2);
  or or_31 (or_31_out, out_19[1], or_55_out);
  or or_32 (or_32_out, out_19[14], or_36_out);
  or or_33 (or_33_out, out_19[0], or_34_out);
  or or_34 (or_34_out, out_19[13], or_35_out);
  or or_35 (or_35_out, out_19[12], or_59_out);
  or or_36 (or_36_out, out_19[11], or_38_out);
  or or_37 (or_37_out, out_19[10], or_61_out);
  or or_38 (or_38_out, out_19[9], or_39_out);
  or or_39 (or_39_out, out_19[8], or_40_out);
  or or_40 (or_40_out, out_19[7], or_45_out);
  or or_41 (or_41_out, out_19[6], or_42_out);
  or or_42 (or_42_out, out_19[5], or_43_out);
  or or_43 (or_43_out, out_19[4], or_62_out);
  or or_44 (or_44_out, out_19[3], and_2_out);
  or or_45 (or_45_out, out_18[0], 1'b0);
  or or_46 (or_46_out, _4_out, or_47_out);
  or or_47 (or_47_out, _5_out, 1'b0);
  or or_48 (or_48_out, _6_out, _7_out);
  or or_49 (or_49_out, _9_out, and_2_out);
  or or_50 (or_50_out, a_out, f0_out);
  or or_51 (or_51_out, b_out, or_52_out);
  or or_52 (or_52_out, out_23, or_67_out);
  and and_3 (and_3_out, d_out, in_2);
  and and_4 (and_4_out, e_out, in_1);
  or or_53 (out_24, out_10, out_20);
  or or_54 (or_54_out, fe_out, undriven_3);
  or or_55 (or_55_out, out_19[14], or_56_out);
  or or_56 (or_56_out, out_19[0], or_57_out);
  or or_57 (or_57_out, out_19[13], or_58_out);
  or or_58 (or_58_out, out_19[12], or_71_out);
  or or_59 (or_59_out, out_19[11], or_37_out);
  or or_60 (or_60_out, out_19[10], or_72_out);
  or or_61 (or_61_out, out_19[9], or_11_out);
  or or_62 (or_62_out, out_19[3], or_15_out);
  or or_63 (out_22, _4_out, or_65_out);
  or or_64 (or_64_out, _5_out, f0_out);
  or or_65 (or_65_out, _6_out, or_49_out);
  or or_66 (or_66_out, _7_out, a_out);
  or or_67 (or_67_out, and_3_out, or_68_out);
  or or_68 (or_68_out, and_4_out, fffe_out);
  or or_69 (or_69_out, out_10, out_20);
  or or_70 (or_70_out, fe_out, undriven_4);
  or or_71 (or_71_out, out_19[11], or_60_out);
  or or_72 (or_72_out, out_19[9], or_41_out);
  or or_73 (or_73_out, _4_out, or_20_out);
  or or_74 (out_21, _5_out, or_76_out);
  or or_75 (or_75_out, _6_out, _9_out);
  or or_76 (or_76_out, _7_out, or_50_out);
  or or_77 (out_11[15], decoder_6_out15, 1'b0);
  or or_78 (out_11[13], decoder_6_out13, out_23);
  or or_79 (out_11[14], decoder_6_out14, 1'b0);
  or or_80 (out_11[11], decoder_6_out11, or_69_out);
  or or_81 (out_11[12], decoder_6_out12, out_23);
  or or_82 (out_11[10], decoder_6_out10, or_69_out);
  or or_83 (out_11[9], decoder_6_out9, 1'b0);
  or or_84 (out_11[6], decoder_6_out6, or_75_out);
  or or_85 (out_11[8], decoder_6_out8, 1'b0);
  or or_86 (out_12[6], decoder_7_out6, d_out);
  or or_87 (out_14[6], decoder_9_out6, or_66_out);
  or or_88 (out_15[7], decoder_10_out7, or_48_out);
  or or_89 (out_16[5], decoder_11_out10, or_26_out);
  or or_90 (out_16[6], decoder_11_out12, fffe_out);
  or or_91 (out_17[3], out_25, in_4);
  or or_92 (out_17[1], out_23, in_5);
  or or_93 (out_17[4], or_51_out, in_7, in_6);

  assign {out_17[2], out_17[0]} = {2{in_7}};
  assign out_19[2] = in_9;

  // Notes on the sheet:
  //   0x00
  //   00x0
  //   WReg 0x00
  //   WReg 00x0
  //   R00x0 alu1
  //   R0x00 alu1
  //   R000x alu2
  //   R0x00 to Ram
  //   R00x0 to Ram
  //   R000x adr alu
  //   R00x0 adr alu
endmodule

module ALU (
  input  [7:0] in_1,
  input  [7:0] in_2,
  input  in_3,
  input  [14:0] in_4,
  input  [7:0] in_5,
  input  in_6,
  output [7:0] out_7,
  output out_8,
  output out_9
);

  wire adder_1_cout, multiplexer_2_out, multiplexer_3_out, or_1_out, or_2_out, or_3_out, or_4_out, or_5_out;
  wire [7:0] adder_1_out, adder_2_out, divider_1_out, divider_1_rem, Hi_q, Lo_q, multiplexer_1_out,
       multiplexer_4_out, multiplexer_5_out, multiplexer_6_out, multiplexer_7_out, multiplexer_8_out,
       multiplexer_9_out, multiplexer_10_out, multiplexer_11_out, multiplexer_12_out, multiplexer_13_out,
       multiplexer_14_out, multiplexer_15_out, multiplier_1_cout, multiplier_1_out, not_1_out, xor_1_out;

  or or_1 (or_1_out, in_1[7], in_1[6], in_1[5], in_1[4], in_1[3], in_1[2], in_1[1], in_1[0]);
  Multiplexer #(.width(8), .enable("false")) multiplexer_1 (
    .in0(in_2), .in1(in_5), .out(multiplexer_1_out), .sel(in_6));
  nand nand_1 (out_8, or_1_out, or_1_out);
  Adder adder_1 (.a(in_1), .b(multiplexer_1_out), .out(adder_1_out), .cin(in_4[0]), .cout(adder_1_cout));
  assign not_1_out = ~multiplexer_1_out;  // NOT_Gate not_1, 8 bits wide
  assign xor_1_out = in_1 ^ multiplexer_1_out;  // XOR_Gate xor_1, 8 bits wide
  Adder adder_2 (.a(in_1), .b(not_1_out), .out(adder_2_out), .cin(in_4[9]));  // open: cout
  Multiplier multiplier_1 (
    .a(in_1), .b(multiplexer_1_out), .out(multiplier_1_out), .cout(multiplier_1_cout));  // open: cin
  Divider divider_1 (.a(in_1), .b(multiplexer_1_out), .out(divider_1_out), .rem(divider_1_rem));  // open: upper
  Multiplexer #(.enable("false")) multiplexer_2 (
    .in0(1'b0), .in1(multiplexer_1_out[0]), .out(multiplexer_2_out), .sel(in_4[10]));
  Multiplexer #(.enable("false")) multiplexer_3 (
    .in0(adder_1_cout), .in1(multiplexer_1_out[7]), .out(multiplexer_3_out), .sel(in_4[12]));
  or or_2 (or_2_out, multiplexer_3_out, multiplexer_2_out);
  Multiplexer #(.width(8), .enable("false")) multiplexer_4 (
    .in0(multiplier_1_cout), .in1(divider_1_rem), .out(multiplexer_4_out), .sel(in_4[7]));
  Multiplexer #(.width(8), .enable("false")) multiplexer_5 (
    .in0(multiplier_1_out), .in1(divider_1_out), .out(multiplexer_5_out), .sel(in_4[7]));
  or or_3 (or_3_out, in_4[14], in_6, in_4[0]);
  or or_4 (or_4_out, in_4[0], in_4[10], in_6, in_4[12], in_4[14]);
  or or_5 (or_5_out, in_4[8], in_4[7]);
  Register Hi (.D(multiplexer_4_out), .en(or_5_out), .Q(Hi_q), .clk(in_3));  // open: clr
  Register Lo (.D(multiplexer_5_out), .en(or_5_out), .Q(Lo_q), .clk(in_3));  // open: clr
  Multiplexer #(.width(8), .enable("false")) multiplexer_6 (
    .in0({8{1'b0}}), .in1({multiplexer_1_out[6:0], 1'b0}), .out(multiplexer_6_out), .sel(in_4[12]));
  Multiplexer #(.width(8), .enable("false")) multiplexer_7 (
    .in0(multiplexer_6_out), .in1({1'b0, multiplexer_1_out[7:1]}), .out(multiplexer_7_out), .sel(in_4[10]));
  Multiplexer #(.width(8), .enable("false")) multiplexer_8 (
    .in0(multiplexer_7_out), .in1(in_1), .out(multiplexer_8_out), .sel(in_4[1]));
  Multiplexer #(.width(8), .enable("false")) multiplexer_9 (
    .in0(multiplexer_8_out), .in1(adder_1_out), .out(multiplexer_9_out), .sel(or_3_out));
  Multiplexer #(.width(8), .enable("false")) multiplexer_10 (
    .in0(multiplexer_9_out), .in1(not_1_out), .out(multiplexer_10_out), .sel(in_4[13]));
  Multiplexer #(.width(8), .enable("false")) multiplexer_11 (
    .in0(multiplexer_10_out), .in1(xor_1_out), .out(multiplexer_11_out), .sel(in_4[11]));
  Multiplexer #(.width(8), .enable("false")) multiplexer_12 (
    .in0(multiplexer_11_out), .in1(adder_2_out), .out(multiplexer_12_out), .sel(in_4[9]));
  Multiplexer #(.width(8), .enable("false")) multiplexer_13 (
    .in0(multiplexer_12_out), .in1({8{out_9}}), .out(multiplexer_13_out), .sel(in_4[4]));
  Multiplexer #(.width(8), .enable("false")) multiplexer_14 (
    .in0(multiplexer_13_out), .in1({8{multiplexer_1_out[7]}}), .out(multiplexer_14_out), .sel(in_4[3]));
  D_Flip_Flop #(.trigger("falling")) Carry (
    .clk(in_4[2]), .D(or_2_out), .Q(out_9), .en(or_4_out));  // open: Qn, preset, reset
  Multiplexer #(.width(8), .enable("false")) multiplexer_15 (
    .in0(multiplexer_14_out), .in1(Hi_q), .out(multiplexer_15_out), .sel(in_4[6]));
  Multiplexer #(.width(8), .enable("false")) multiplexer_16 (
    .in0(multiplexer_15_out), .in1(Lo_q), .out(out_7), .sel(in_4[5]));

  // Notes on the sheet:
  //   ALU
endmodule

module Clock (
  input  [11:0] in_1,
  input  [7:0] in_2,
  input  in_3,
  input  in_4,
  input  in_5,
  input  in_6,
  input  [15:0] in_7,
  input  in_8,
  input  in_9,
  input  [7:0] in_10,
  input  in_11,
  output [7:0] out_12,
  output out_13,
  output out_14,
  output out_15,
  output out_16,
  output out_17,
  output out_18,
  output out_19,
  output out_20,
  output out_21,
  output out_22,
  output [11:0] out_23,
  output out_24,
  output out_25,
  output out_26,
  output out_27,
  output out_28,
  output out_29,
  output out_30,
  output out_31,
  output out_32,
  output out_33
);

  wire and_1_out, and_2_out, and_3_out, and_4_out, and_5_out, and_6_out, and_7_out, d_ff_1_q, d_ff_1_qn,
       d_ff_2_q, d_ff_2_qn, d_ff_4_q, d_ff_5_q, d_ff_5_qn, decoder_1_out0, decoder_1_out1, decoder_1_out2,
       decoder_1_out3, decoder_1_out4, decoder_1_out5, decoder_1_out6, decoder_1_out7, decoder_1_out8,
       decoder_1_out9, decoder_1_out10, decoder_1_out11, decoder_1_out12, decoder_1_out13, decoder_1_out14,
       decoder_1_out15, decoder_2_out0, decoder_2_out1, decoder_2_out2, decoder_2_out3, decoder_2_out4,
       decoder_2_out5, decoder_2_out6, decoder_2_out7, decoder_2_out8, decoder_2_out9, decoder_2_out10,
       decoder_2_out11, decoder_2_out12, decoder_2_out13, decoder_3_out0, decoder_3_out2, decoder_3_out3,
       decoder_3_out6, decoder_3_out7, decoder_3_out8, decoder_3_out9, decoder_3_out10, decoder_3_out11,
       decoder_3_out12, decoder_3_out13, decoder_3_out14, decoder_3_out15, or_1_out, or_2_out, or_3_out,
       or_4_out, or_5_out, or_6_out, or_9_out, or_10_out, or_11_out, or_12_out;
  wire [3:0] adder_2_out, demultiplexer_1_out0, demultiplexer_1_out1, demultiplexer_2_out0,
       demultiplexer_2_out1, multiplexer_14_out, multiplexer_15_out, multiplexer_16_out, multiplexer_17_out;
  wire [7:0] Exc_Code_q, Exc_Data_q, multiplexer_1_out, multiplexer_7_out, multiplexer_8_out,
       multiplexer_10_out, multiplexer_11_out, multiplexer_12_out;
  wire [11:0] adder_1_out, multiplexer_2_out, multiplexer_3_out, multiplexer_4_out, multiplexer_5_out,
       multiplexer_9_out;

  Multiplexer #(.width(8), .enable("false")) multiplexer_1 (
    .in0({8{1'b0}}), .in1(8'h3), .out(multiplexer_1_out), .sel(in_6));
  Multiplexer #(.width(12), .enable("false")) multiplexer_2 (
    .in0({12{1'b0}}), .in1(12'hf02), .out(multiplexer_2_out), .sel(or_2_out));
  Multiplexer #(.width(12), .enable("false")) multiplexer_3 (
    .in0(multiplexer_2_out), .in1(12'hf03), .out(multiplexer_3_out), .sel(or_4_out));
  Multiplexer #(.width(12), .enable("false")) multiplexer_4 (
    .in0(multiplexer_3_out), .in1(12'hf00), .out(multiplexer_4_out), .sel(or_5_out));
  Multiplexer #(.width(12), .enable("false")) multiplexer_5 (
    .in0(multiplexer_4_out), .in1(12'hf01), .out(multiplexer_5_out), .sel(or_3_out));
  Multiplexer #(.width(12), .enable("false")) multiplexer_6 (
    .in0(multiplexer_5_out), .in1(12'hf04), .out(out_23), .sel(or_6_out));
  Multiplexer #(.width(8), .enable("false")) multiplexer_7 (
    .in0(multiplexer_1_out), .in1(8'h8), .out(multiplexer_7_out), .sel(in_9));
  or or_1 (or_1_out, in_9, in_6);
  Multiplexer #(.width(8), .enable("false")) multiplexer_8 (
    .in0(in_10), .in1(in_2), .out(multiplexer_8_out), .sel(in_6));
  Adder #(.width(12)) adder_1 (.a(12'hffe), .b(in_1), .out(adder_1_out));  // open: cin, cout
  Register #(.trigger("high")) Exc_Code (
    .D(multiplexer_7_out), .en(or_1_out), .Q(Exc_Code_q), .clk(or_1_out), .clr(out_19));
  Register #(.trigger("high")) Exc_Data (
    .D(multiplexer_8_out), .en(or_1_out), .Q(Exc_Data_q), .clk(or_1_out), .clr(out_19));
  Multiplexer #(.width(12), .enable("false")) multiplexer_9 (
    .in0(in_1), .in1(adder_1_out), .out(multiplexer_9_out), .sel(and_1_out));
  Multiplexer #(.width(8), .enable("false")) multiplexer_10 (
    .in0({8{1'b0}}), .in1({4'b1011, multiplexer_9_out[11:8]}), .out(multiplexer_10_out), .sel(or_2_out));
  Multiplexer #(.width(8), .enable("false")) multiplexer_11 (
    .in0(multiplexer_10_out), .in1(multiplexer_9_out[7:0]), .out(multiplexer_11_out), .sel(or_4_out));
  Multiplexer #(.width(8), .enable("false")) multiplexer_12 (
    .in0(multiplexer_11_out), .in1(Exc_Code_q), .out(multiplexer_12_out), .sel(or_5_out));
  Multiplexer #(.width(8), .enable("false")) multiplexer_13 (
    .in0(multiplexer_12_out), .in1(Exc_Data_q), .out(out_12), .sel(or_3_out));
  and and_1 (and_1_out, ~Exc_Code_q[7], ~Exc_Code_q[6], ~Exc_Code_q[5], ~Exc_Code_q[4], Exc_Code_q[3], ~Exc_Code_q[2], ~Exc_Code_q[1], ~Exc_Code_q[0]);  // AND_Gate
  or or_2 (or_2_out, decoder_2_out3, decoder_2_out2);
  or or_3 (or_3_out, decoder_2_out12, decoder_2_out11);
  and and_2 (and_2_out, in_8, out_31);
  and and_3 (and_3_out, ~in_8, decoder_1_out2);  // AND_Gate
  or or_4 (or_4_out, decoder_2_out5, decoder_2_out6);
  or or_5 (or_5_out, decoder_2_out8, decoder_2_out9);
  or or_6 (or_6_out, decoder_2_out13, out_28);
  or or_7 (out_27, decoder_2_out2, decoder_2_out3, decoder_2_out5, decoder_2_out6);
  or or_8 (out_24, decoder_2_out3, decoder_2_out6, decoder_2_out9, decoder_2_out12);
  D_Flip_Flop d_ff_1 (
    .clk(out_25), .D(and_2_out), .Q(d_ff_1_q), .Qn(d_ff_1_qn), .en(and_2_out), .reset(and_3_out));  // open: preset
  D_Flip_Flop d_ff_2 (
    .clk(out_25), .D(and_2_out), .Q(d_ff_2_q), .Qn(d_ff_2_qn), .en(and_2_out), .reset(decoder_1_out2));  // open: preset
  Decoder #(.select(4), .disabled(0), .enable("false")) decoder_1 (
    .out0(decoder_1_out0), .out1(decoder_1_out1), .out2(decoder_1_out2), .out3(decoder_1_out3),
    .out4(decoder_1_out4), .out5(decoder_1_out5), .out6(decoder_1_out6), .out7(decoder_1_out7),
    .out8(decoder_1_out8), .out9(decoder_1_out9), .out10(decoder_1_out10), .out11(decoder_1_out11),
    .out12(decoder_1_out12), .out13(decoder_1_out13), .out14(decoder_1_out14), .out15(decoder_1_out15),
    .sel(demultiplexer_1_out1));
  Decoder #(.select(4), .disabled(0), .enable("false")) decoder_2 (
    .out0(decoder_2_out0), .out1(decoder_2_out1), .out2(decoder_2_out2), .out3(decoder_2_out3),
    .out4(decoder_2_out4), .out5(decoder_2_out5), .out6(decoder_2_out6), .out7(decoder_2_out7),
    .out8(decoder_2_out8), .out9(decoder_2_out9), .out10(decoder_2_out10), .out11(decoder_2_out11),
    .out12(decoder_2_out12), .out13(decoder_2_out13), .out14(out_28), .out15(out_19),
    .sel(demultiplexer_1_out0));
  D_Flip_Flop d_ff_3 (.clk(out_25), .D(and_5_out), .Q(out_20), .en(and_5_out), .reset(and_4_out));  // open: Qn, preset
  and and_4 (and_4_out, in_5, out_31);
  Demultiplexer #(.width(4), .enable("false")) demultiplexer_1 (
    .out0(demultiplexer_1_out0), .out1(demultiplexer_1_out1), .in(demultiplexer_2_out1), .sel(or_12_out));
  or or_9 (or_9_out, in_6, in_9);
  and and_5 (and_5_out, or_9_out, ~out_20);  // AND_Gate
  and and_6 (and_6_out, out_13, out_25);
  D_Flip_Flop d_ff_4 (
    .clk(out_25), .D(and_5_out), .Q(d_ff_4_q), .en(and_5_out), .reset(decoder_2_out1));  // open: Qn, preset
  or or_10 (or_10_out, in_4, out_19);
  D_Flip_Flop d_ff_5 (
    .clk(and_6_out), .D(d_ff_4_q), .Q(d_ff_5_q), .Qn(d_ff_5_qn), .en(d_ff_4_q), .reset(or_10_out));  // open: preset
  or or_11 (or_11_out, d_ff_1_q, d_ff_5_q);
  or or_12 (or_12_out, d_ff_5_qn, d_ff_1_q);
  Decoder #(.select(4), .disabled(0), .enable("false")) decoder_3 (
    .out0(decoder_3_out0), .out1(out_13), .out2(decoder_3_out2), .out3(decoder_3_out3), .out4(out_30),
    .out5(out_31), .out6(decoder_3_out6), .out7(decoder_3_out7), .out8(decoder_3_out8),
    .out9(decoder_3_out9), .out10(decoder_3_out10), .out11(decoder_3_out11), .out12(decoder_3_out12),
    .out13(decoder_3_out13), .out14(decoder_3_out14), .out15(decoder_3_out15), .sel(demultiplexer_2_out0));
  or or_13 (out_33, out_30, out_31);
  Demultiplexer #(.width(4), .enable("false")) demultiplexer_2 (
    .out0(demultiplexer_2_out0), .out1(demultiplexer_2_out1), .in({out_15, out_16, out_17, out_18}),
    .sel(or_11_out));
  D_Flip_Flop d_ff_6 (.clk(out_25), .D(in_4), .Q(out_22));  // open: Qn, preset, en, reset
  or or_14 (out_26, in_3, in_11);
  Multiplexer #(.width(4), .enable("false")) multiplexer_14 (
    .in0(4'b0000), .in1(4'b0011), .out(multiplexer_14_out), .sel(out_13));
  Multiplexer #(.width(4), .enable("false")) multiplexer_15 (
    .in0(multiplexer_14_out), .in1(4'b0010), .out(multiplexer_15_out), .sel(and_7_out));
  and and_7 (and_7_out, in_7[12], in_7[13], in_7[14], in_7[15], out_13);
  D_Flip_Flop d_ff_7 (.clk(out_25), .D(out_22), .Q(out_14), .en(out_22), .reset(out_26));  // open: Qn, preset
  Multiplexer #(.width(4), .enable("false")) multiplexer_16 (
    .in0(multiplexer_15_out), .in1(4'b1011), .out(multiplexer_16_out), .sel(out_31));
  Clock_part clock_1 (.out(out_25));
  Multiplexer #(.width(4), .enable("false")) multiplexer_17 (
    .in0(multiplexer_16_out), .in1(4'b1110), .out(multiplexer_17_out), .sel(decoder_3_out2));
  Adder #(.width(4)) adder_2 (
    .a(multiplexer_17_out), .b({out_15, out_16, out_17, out_18}), .out(adder_2_out), .cin(1'b1));  // open: cout
  Register #(.width(4)) register_1 (
    .D(adder_2_out), .en(out_14), .Q({out_15, out_16, out_17, out_18}), .clk(out_25), .clr(out_26));

  assign out_21 = out_13;
  assign out_29 = out_13;
  assign out_32 = out_13;

  // Notes on the sheet:
  //   Save actual RA not +2
  //   Pc hi Adr f02
  //   Pc lo  Adr f03
  //   Exc code Adr f00
  //   Exc data Adr f01
  //   Adr f04
  //   R Pc
  //   W Ram
  //   W Pc
  //   R PC
  //   R PC+1
  //   W Pc
  //   W Acc
  //   R RAM 16
endmodule

module DMA (
  input  [7:0] in_1,
  input  [11:0] in_2,
  input  in_3,
  input  in_4,
  input  in_5,
  output [11:0] out_6,
  output out_7,
  output out_8,
  output out_9,
  output [11:0] out_10,
  output out_11,
  output out_12
);

  wire and_1_out, and_2_out, and_3_out, and_4_out, and_5_out, and_6_out, and_7_out, and_8_out, and_9_out,
       and_10_out, and_11_out, and_16_out, and_17_out, decoder_1_out3, decoder_1_out4, decoder_1_out5,
       decoder_1_out6, or_1_out, or_3_out, or_4_out, register_3_q, register_6_q;
  wire [2:0] adder_1_out, multiplexer_7_out, register_8_q;
  wire [3:0] adder_2_out, multiplexer_6_out, register_7_q;
  wire [7:0] register_1_q, register_2_q;
  wire [7:6] register_4_q;
  wire [11:0] multiplexer_1_out, multiplexer_3_out, multiplexer_5_out;
  wire [11:6] register_4_q_2;

  and and_1 (and_1_out, ~in_2[4], in_2[5], in_2[6], in_2[7], in_2[8], in_2[9], in_2[10], in_2[11]);  // AND_Gate
  and and_2 (and_2_out, ~in_2[0], ~in_2[1], ~in_2[2], ~in_2[3]);  // AND_Gate
  and and_3 (and_3_out, in_2[0], ~in_2[1], ~in_2[2], ~in_2[3]);  // AND_Gate
  and and_4 (and_4_out, ~in_2[0], in_2[1], ~in_2[2], ~in_2[3]);  // AND_Gate
  and and_5 (and_5_out, in_2[0], in_2[1], ~in_2[2], ~in_2[3]);  // AND_Gate
  and and_6 (and_6_out, and_1_out, and_2_out, in_4);
  and and_7 (and_7_out, and_1_out, and_3_out, in_4);
  and and_8 (and_8_out, and_1_out, and_4_out, in_4);
  and and_9 (and_9_out, and_1_out, and_5_out, in_4);
  or or_1 (or_1_out, and_7_out, in_3);
  Register register_1 (.D(in_1), .en(and_6_out), .Q(register_1_q), .clk(in_5));  // open: clr
  Register register_2 (.D(in_1), .en(and_7_out), .Q(register_2_q), .clk(in_5));  // open: clr
  Register #(.width(1)) register_3 (.D(or_1_out), .en(or_1_out), .Q(register_3_q), .clk(in_5), .clr(and_16_out));
  Register register_4 (.D(in_1), .en(and_8_out), .Q({register_4_q, register_4_q_2}), .clk(in_5));  // open: clr
  Register register_5 (.D(in_1), .en(and_9_out), .Q(multiplexer_5_out[11:4]), .clk(in_5));  // open: clr
  Register #(.width(1)) register_6 (.D(and_9_out), .en(and_9_out), .Q(register_6_q), .clk(in_5), .clr(and_16_out));
  Multiplexer #(.width(12), .disabled(0), .enable("false")) multiplexer_1 (
    .in0({12{1'b0}}), .in1({register_1_q, multiplexer_5_out[3:0]}), .out(multiplexer_1_out), .sel(and_10_out));
  and and_10 (and_10_out, register_3_q, or_3_out);
  and and_11 (and_11_out, register_6_q, or_3_out);
  Multiplexer #(.width(12), .disabled(0), .enable("false")) multiplexer_2 (
    .in0(multiplexer_1_out), .in1(multiplexer_5_out), .out(out_6), .sel(and_11_out));
  Multiplexer #(.width(12), .disabled(0), .enable("false")) multiplexer_3 (
    .in0({12{1'b0}}), .in1({register_2_q[5:0], multiplexer_5_out[3:0], 2'b00}), .out(multiplexer_3_out),
    .sel(and_10_out));
  Multiplexer #(.width(12), .disabled(0), .enable("false")) multiplexer_4 (
    .in0(multiplexer_3_out), .in1({register_4_q_2, multiplexer_5_out[3:0], 2'b00}), .out(out_10),
    .sel(and_11_out));
  and and_12 (out_7, register_3_q, or_3_out);
  and and_13 (out_11, register_3_q, decoder_1_out3);
  and and_14 (out_8, register_6_q, decoder_1_out3);
  and and_15 (out_12, register_6_q, or_3_out);
  or or_2 (out_9, register_3_q, register_6_q);
  Counter #(.width(32), .max('hffffffff)) counter_1 (.count(out_9), .clk(in_5));  // open: load, D, Q, carry, clr
  Counter #(.width(32), .max('hffffffff)) counter_2 (.count(out_9), .clk(out_9));  // open: load, D, Q, carry, clr
  Register #(.width(4)) register_7 (
    .D(adder_2_out), .en(decoder_1_out4), .Q(register_7_q), .clk(in_5), .clr(and_16_out));
  Register #(.width(3)) register_8 (.D(adder_1_out), .en(out_9), .Q(register_8_q), .clk(in_5), .clr(and_16_out));
  or or_3 (or_3_out, decoder_1_out3, decoder_1_out4);
  or or_4 (or_4_out, decoder_1_out4, decoder_1_out4);
  and and_16 (and_16_out, decoder_1_out4, and_17_out);
  Multiplexer #(.width(4), .enable("false")) multiplexer_5 (
    .in0(4'b0000), .in1(register_7_q), .out(multiplexer_5_out[3:0]), .sel(or_3_out));
  Decoder #(.select(3), .disabled(0)) decoder_1 (
    .out3(decoder_1_out3), .out4(decoder_1_out4), .out5(decoder_1_out5), .out6(decoder_1_out6),
    .sel(register_8_q), .en(out_9));  // open: out0, out1, out2, out7
  Multiplexer #(.width(4), .enable("false")) multiplexer_6 (
    .in0(4'b0000), .in1(register_7_q), .out(multiplexer_6_out), .sel(or_4_out));
  Multiplexer #(.width(3), .disabled(0), .enable("false")) multiplexer_7 (
    .in0(3'b000), .in1(3'b110), .out(multiplexer_7_out), .sel(decoder_1_out4));
  Adder #(.width(3)) adder_1 (.a(multiplexer_7_out), .b(register_8_q), .out(adder_1_out), .cin(1'b1));  // open: cout
  Adder #(.width(4)) adder_2 (.a(4'b0000), .b(multiplexer_6_out), .out(adder_2_out), .cin(or_4_out));  // open: cout
  and and_17 (and_17_out, multiplexer_5_out[0], multiplexer_5_out[1], multiplexer_5_out[2], multiplexer_5_out[3]);

  // Notes on the sheet:
  //   To fix
  //   It activates on all W Ram
  //   included from loader
  //   DMA control
  //   HD Adr
  //   Ram Adr
  //   R HD
  //   The interrupt when writing fe1 or fe3 stops the driver execution after the next instruction in executed
  //   W Ram
  //   R Ram
  //   W HD
endmodule
