// Logisim project 8.4.2 Boot From HD.circ as structural Verilog: 2 circuits, main circuit main
module main (
  input  in_1,
  input  in_2,
  input  in_3,
  input  Keyboard_IN,
  input  in_5,
  input  in_6,
  input  in_7,
  input  in_8,
  input  MMU_On,
  input  in_10,
  input  [7:0] Data_In,
  input  [11:0] Adr_In,
  input  Write_Ram,
  input  in_14,
  output [11:0] PC,
  output [15:0] Instruc,
  output [7:0] Reg_0,
  output [7:0] Reg_1,
  output [7:0] Reg_2,
  output [7:0] Reg_3,
  output [7:0] Data,
  output [15:0] out_22,
  output [7:0] Reg_4,
  output [7:0] Reg_5,
  output [7:0] Reg_6,
  output [7:0] Reg_7,
  output [7:0] Read_Ram,
  output [7:0] Reg_8,
  output [7:0] Reg_9,
  output [7:0] Reg_A,
  output [7:0] Reg_B,
  output [7:0] Reg_C,
  output [7:0] Reg_D,
  output [7:0] Reg_E,
  output [7:0] Reg_F
);

  wire _0_2_out, _1_2_out, _2a_out, _2b_out, _3_2_out, _4_out, _5_out, _6_out, _7_out, _8_out, _9_out,
       _20_out, _21_out, _22_out, _23_out, _24_out, _25_out, _26_out, _27_out, _28_out, _29_out, a_out,
       adder_2_cout, and_1_out, and_2_out, and_3_out, and_4_out, and_5_out, and_6_out, and_7_out, and_8_out,
       and_9_out, and_10_out, and_11_out, and_12_out, and_13_out, and_14_out, and_15_out, and_16_out,
       and_17_out, and_18_out, and_19_out, and_20_out, and_21_out, and_22_out, and_23_out, and_24_out,
       and_25_out, and_26_out, and_27_out, and_28_out, and_29_out, and_30_out, and_31_out, and_32_out,
       and_33_out, and_34_out, and_35_out, and_36_out, and_37_out, and_38_out, and_39_out, and_40_out,
       and_41_out, and_42_out, and_43_out, and_44_out, and_46_out, and_47_out, and_48_out, and_49_out,
       and_50_out, and_51_out, and_52_out, and_53_out, and_54_out, and_55_out, and_56_out, and_57_out,
       and_58_out, and_59_out, and_60_out, and_61_out, and_62_out, and_63_out, and_64_out, and_65_out,
       and_66_out, and_67_out, and_68_out, and_69_out, and_70_out, and_71_out, and_72_out, and_73_out,
       and_74_out, and_75_out, and_76_out, and_77_out, and_78_out, and_79_out, b_out, button_1_out,
       button_2_out, c_out, clock_1_out, d_ff_1_q, d_ff_1_qn, d_ff_2_q, d_ff_2_qn, d_ff_3_q, d_ff_3_qn,
       d_ff_4_q, d_ff_4_qn, d_ff_5_q, d_ff_5_qn, d_ff_6_q, d_ff_6_qn, d_ff_7_q, d_ff_7_qn, d_ff_8_q,
       d_ff_8_qn, d_ff_9_q, d_ff_9_qn, d_ff_10_q, d_ff_10_qn, d_ff_11_q, d_ff_11_qn, d_ff_12_q, d_ff_12_qn,
       d_ff_13_q, d_ff_13_qn, d_ff_14_q, d_ff_14_qn, d_ff_15_q, d_ff_16_q, d_ff_17_q, d_ff_17_qn, d_ff_18_q,
       d_ff_18_qn, d_ff_19_q, d_ff_19_qn, d_ff_20_q, d_ff_21_q, d_ff_22_q, d_out, decoder_1_out0,
       decoder_1_out1, decoder_1_out2, decoder_1_out3, decoder_1_out4, decoder_1_out5, decoder_1_out6,
       decoder_1_out7, decoder_1_out8, decoder_1_out9, decoder_1_out10, decoder_1_out11, decoder_1_out12,
       decoder_1_out13, decoder_1_out14, decoder_1_out15, decoder_2_out0, decoder_2_out1, decoder_2_out2,
       decoder_2_out3, decoder_2_out4, decoder_2_out5, decoder_2_out6, decoder_2_out7, decoder_2_out8,
       decoder_2_out9, decoder_2_out10, decoder_2_out11, decoder_2_out12, decoder_2_out13, decoder_2_out14,
       decoder_2_out15, decoder_3_out0, decoder_3_out1, decoder_3_out2, decoder_3_out3, decoder_3_out4,
       decoder_3_out5, decoder_3_out6, decoder_3_out7, decoder_3_out8, decoder_3_out9, decoder_3_out10,
       decoder_3_out11, decoder_3_out12, decoder_3_out13, decoder_3_out14, decoder_3_out15, decoder_4_out0,
       decoder_4_out1, decoder_4_out2, decoder_4_out3, decoder_4_out4, decoder_4_out5, decoder_4_out6,
       decoder_4_out7, decoder_4_out8, decoder_4_out9, decoder_4_out10, decoder_4_out11, decoder_4_out12,
       decoder_4_out13, decoder_4_out14, decoder_4_out15, decoder_5_out0, decoder_5_out1, decoder_5_out2,
       decoder_5_out3, decoder_5_out4, decoder_5_out5, decoder_5_out6, decoder_5_out7, decoder_5_out8,
       decoder_5_out9, decoder_5_out10, decoder_5_out11, decoder_5_out12, decoder_5_out13, decoder_5_out14,
       decoder_5_out15, decoder_6_out0, decoder_6_out1, decoder_6_out2, decoder_6_out3, decoder_6_out4,
       decoder_6_out5, decoder_6_out6, decoder_6_out7, decoder_6_out8, decoder_6_out9, decoder_6_out10,
       decoder_6_out11, decoder_6_out12, decoder_6_out13, decoder_6_out14, decoder_6_out15, decoder_7_out0,
       decoder_7_out1, decoder_7_out2, decoder_7_out3, decoder_7_out4, decoder_7_out5, decoder_7_out6,
       decoder_7_out7, decoder_7_out8, decoder_7_out9, decoder_7_out10, decoder_7_out11, decoder_7_out12,
       decoder_7_out13, decoder_7_out14, decoder_7_out15, decoder_8_out0, decoder_8_out1, decoder_8_out2,
       decoder_8_out3, decoder_8_out4, decoder_8_out5, decoder_8_out6, decoder_8_out7, decoder_8_out8,
       decoder_8_out9, decoder_8_out10, decoder_8_out11, decoder_8_out12, decoder_8_out13, decoder_8_out14,
       decoder_8_out15, decoder_9_out0, decoder_9_out1, decoder_9_out2, decoder_9_out3, decoder_9_out4,
       decoder_9_out5, decoder_9_out6, decoder_9_out7, decoder_9_out8, decoder_9_out9, decoder_9_out10,
       decoder_9_out11, decoder_9_out12, decoder_9_out13, decoder_9_out14, decoder_9_out15, decoder_10_out0,
       decoder_10_out1, decoder_10_out2, decoder_10_out3, decoder_10_out4, decoder_10_out5, decoder_10_out6,
       decoder_10_out7, decoder_10_out8, decoder_10_out9, decoder_10_out10, decoder_10_out11,
       decoder_10_out12, decoder_10_out13, decoder_10_out14, decoder_10_out15, decoder_11_out0,
       decoder_11_out1, decoder_11_out2, decoder_11_out3, decoder_11_out4, decoder_11_out5, decoder_11_out6,
       decoder_11_out7, decoder_11_out8, decoder_11_out9, decoder_11_out10, decoder_11_out11,
       decoder_11_out12, decoder_11_out13, decoder_11_out14, decoder_11_out15, decoder_12_out0,
       decoder_12_out1, decoder_12_out2, decoder_12_out3, decoder_12_out4, decoder_13_out0, decoder_13_out1,
       decoder_13_out2, decoder_13_out3, decoder_13_out4, decoder_14_out0, decoder_14_out1, decoder_14_out2,
       decoder_14_out3, decoder_14_out4, decoder_15_out0, decoder_15_out1, decoder_15_out2, decoder_16_out2,
       decoder_16_out3, decoder_16_out4, decoder_16_out5, decoder_16_out6, decoder_16_out7, decoder_16_out8,
       decoder_16_out9, decoder_16_out10, decoder_16_out11, decoder_16_out12, decoder_16_out13,
       decoder_16_out14, decoder_16_out15, decoder_17_out0, decoder_17_out1, decoder_17_out2,
       decoder_17_out3, decoder_17_out4, decoder_17_out5, decoder_17_out6, decoder_17_out7, decoder_17_out8,
       decoder_17_out9, decoder_17_out10, decoder_17_out11, decoder_17_out12, decoder_17_out13,
       decoder_17_out14, decoder_17_out15, decoder_18_out0, decoder_18_out1, decoder_18_out2,
       decoder_18_out3, decoder_18_out4, decoder_18_out5, decoder_18_out6, decoder_18_out7, decoder_18_out8,
       decoder_18_out9, decoder_18_out10, decoder_18_out11, decoder_18_out12, decoder_18_out13,
       decoder_18_out14, decoder_18_out15, decoder_19_out0, decoder_19_out1, decoder_19_out2,
       decoder_19_out3, decoder_19_out4, decoder_19_out5, decoder_19_out6, decoder_19_out7, decoder_19_out8,
       decoder_19_out9, decoder_19_out10, decoder_19_out11, decoder_19_out12, decoder_19_out13,
       decoder_19_out14, decoder_19_out15, decoder_20_out0, decoder_20_out1, decoder_20_out2,
       decoder_20_out3, decoder_21_out0, decoder_21_out1, decoder_21_out2, decoder_21_out3, decoder_21_out4,
       decoder_21_out5, decoder_21_out6, decoder_21_out7, decoder_21_out8, decoder_21_out9, decoder_21_out10,
       decoder_21_out11, decoder_21_out12, decoder_21_out13, decoder_21_out14, decoder_21_out15,
       decoder_22_out0, decoder_22_out1, decoder_22_out2, decoder_22_out3, decoder_22_out4, decoder_22_out5,
       decoder_22_out6, decoder_22_out7, decoder_22_out8, decoder_22_out9, decoder_22_out10,
       decoder_22_out11, decoder_22_out12, decoder_22_out13, decoder_22_out14, decoder_22_out15,
       decoder_23_out0, decoder_23_out1, decoder_23_out2, decoder_23_out3, decoder_24_out3, decoder_24_out4,
       decoder_24_out5, decoder_24_out6, e_out, f0_out, f1_out, fe_out, fffe_out, ffff_out,
       multiplexer_43_out, multiplexer_117_out, multiplexer_118_out, multiplexer_168_out,
       multiplexer_169_out, multiplexer_170_out, multiplexer_176_out, multiplexer_177_out,
       multiplexer_178_out, nand_1_out, nand_2_out, nand_3_out, nand_4_out, nand_5_out, nand_6_out,
       not_2_out, Off_out, On_2_out, On_out, or_1_out, or_2_out, or_3_out, or_4_out, or_5_out, or_6_out,
       or_7_out, or_8_out, or_9_out, or_10_out, or_11_out, or_12_out, or_13_out, or_14_out, or_15_out,
       or_16_out, or_17_out, or_18_out, or_19_out, or_20_out, or_21_out, or_22_out, or_23_out, or_24_out,
       or_25_out, or_26_out, or_27_out, or_28_out, or_29_out, or_30_out, or_31_out, or_32_out, or_33_out,
       or_34_out, or_35_out, or_36_out, or_37_out, or_38_out, or_39_out, or_40_out, or_41_out, or_42_out,
       or_43_out, or_44_out, or_45_out, or_46_out, or_47_out, or_48_out, or_49_out, or_50_out, or_51_out,
       or_52_out, or_53_out, or_54_out, or_55_out, or_56_out, or_57_out, or_58_out, or_59_out, or_60_out,
       or_61_out, or_62_out, or_63_out, or_64_out, or_65_out, or_66_out, or_67_out, or_68_out, or_69_out,
       or_70_out, or_71_out, or_72_out, or_73_out, or_74_out, or_75_out, or_76_out, or_77_out, or_78_out,
       or_79_out, or_80_out, or_81_out, or_82_out, or_83_out, or_84_out, or_85_out, or_86_out, or_87_out,
       or_88_out, or_89_out, or_90_out, or_91_out, or_92_out, or_93_out, or_94_out, or_95_out, or_96_out,
       or_97_out, or_98_out, or_99_out, or_100_out, or_101_out, or_102_out, or_103_out, or_104_out,
       or_105_out, or_106_out, or_107_out, or_108_out, or_109_out, or_110_out, or_111_out, or_112_out,
       or_113_out, or_114_out, or_115_out, or_116_out, or_117_out, or_118_out, or_119_out, or_120_out,
       or_121_out, or_122_out, or_123_out, or_124_out, or_125_out, or_126_out, or_127_out, or_128_out,
       or_129_out, or_130_out, or_131_out, or_132_out, or_133_out, or_134_out, or_135_out, or_139_out,
       or_140_out, or_141_out, or_142_out, or_143_out, or_144_out, or_145_out, or_146_out, or_147_out,
       or_148_out, or_149_out, or_150_out, or_151_out, or_152_out, or_153_out, or_154_out, or_155_out,
       or_156_out, or_157_out, or_158_out, or_178_out, or_179_out, or_181_out, or_183_out, or_184_out,
       or_185_out, or_186_out, or_187_out, or_188_out, or_189_out, or_190_out, or_191_out, or_192_out,
       or_193_out, or_194_out, or_195_out, or_196_out, register_6_q, register_29_q, register_32_q,
       register_35_q, undriven, undriven_2, undriven_3, undriven_4, undriven_5, undriven_6, undriven_7,
       undriven_8, undriven_9, undriven_10, undriven_11, undriven_12, undriven_13, undriven_14, undriven_15,
       undriven_16, undriven_17, undriven_18, undriven_19, undriven_20, undriven_21, undriven_22,
       undriven_23, undriven_24, undriven_25, undriven_26, undriven_27, undriven_28, undriven_29,
       undriven_30, undriven_31, undriven_32, undriven_33, undriven_34, undriven_35, undriven_36,
       undriven_37, undriven_38, undriven_39, undriven_40, undriven_41, undriven_42, undriven_43, undriven_44;
  wire [1:0] adder_7_out, multiplexer_161_out, register_3_q, register_4_q, register_4_q_2, register_21_q;
  wire [2:0] adder_11_out, multiplexer_144_out, multiplexer_193_out, register_3_q_2, register_3_q_3,
       register_37_q;
  wire [3:0] _0_out, _4_2_out, _8_2_out, adder_4_out, adder_8_out, adder_9_out_2, adder_10_out, c_2_out,
       demultiplexer_1_out0, demultiplexer_1_out1, demultiplexer_2_out0, demultiplexer_2_out1,
       multiplexer_21_out, multiplexer_22_out, multiplexer_23_out, multiplexer_24_out, multiplexer_25_out,
       multiplexer_26_out, multiplexer_77_out_2, multiplexer_77_out_3, multiplexer_78_out_2,
       multiplexer_100_out, multiplexer_101_out, multiplexer_102_out, multiplexer_103_out,
       multiplexer_104_out, multiplexer_105_out, multiplexer_106_out, multiplexer_107_out,
       multiplexer_108_out, multiplexer_109_out, multiplexer_110_out, multiplexer_111_out,
       multiplexer_112_out, multiplexer_113_out, multiplexer_114_out, multiplexer_115_out,
       multiplexer_144_out_3, multiplexer_153_out, multiplexer_159_out_2, multiplexer_162_out,
       multiplexer_163_out, multiplexer_164_out, multiplexer_165_out, multiplexer_189_out,
       multiplexer_191_out, register_4_q_3, register_7_q, register_24_q, register_36_q;
  wire [3:3] multiplexer_144_out_2;
  wire [5:0] adder_9_out_3, multiplexer_171_out;
  wire [7:0] adder_2_out, adder_3_out, and_45_out, divider_1_out, divider_1_rem, Exc_Code_q, Exc_Data_q,
       Hi_q, Lo_q, multiplexer_1_out, multiplexer_2_out, multiplexer_3_out, multiplexer_4_out,
       multiplexer_5_out, multiplexer_6_out, multiplexer_7_out, multiplexer_8_out, multiplexer_9_out,
       multiplexer_10_out, multiplexer_11_out, multiplexer_12_out, multiplexer_13_out, multiplexer_14_out,
       multiplexer_15_out, multiplexer_16_out, multiplexer_17_out, multiplexer_18_out, multiplexer_19_out,
       multiplexer_20_out, multiplexer_27_out, multiplexer_28_out, multiplexer_29_out, multiplexer_30_out,
       multiplexer_31_out, multiplexer_32_out, multiplexer_33_out, multiplexer_34_out, multiplexer_35_out,
       multiplexer_36_out, multiplexer_37_out, multiplexer_38_out, multiplexer_39_out, multiplexer_40_out,
       multiplexer_41_out, multiplexer_42_out, multiplexer_44_out, multiplexer_45_out, multiplexer_46_out,
       multiplexer_47_out, multiplexer_48_out, multiplexer_49_out, multiplexer_50_out, multiplexer_51_out,
       multiplexer_52_out, multiplexer_53_out, multiplexer_54_out, multiplexer_55_out, multiplexer_56_out,
       multiplexer_57_out, multiplexer_58_out, multiplexer_59_out, multiplexer_60_out, multiplexer_61_out,
       multiplexer_62_out, multiplexer_63_out, multiplexer_64_out, multiplexer_65_out, multiplexer_66_out,
       multiplexer_67_out, multiplexer_68_out, multiplexer_69_out, multiplexer_70_out, multiplexer_71_out,
       multiplexer_72_out, multiplexer_73_out, multiplexer_74_out, multiplexer_75_out, multiplexer_77_out,
       multiplexer_78_out, multiplexer_80_out, multiplexer_81_out, multiplexer_82_out, multiplexer_83_out,
       multiplexer_84_out, multiplexer_85_out, multiplexer_86_out, multiplexer_87_out, multiplexer_88_out,
       multiplexer_89_out, multiplexer_90_out, multiplexer_91_out, multiplexer_92_out, multiplexer_93_out,
       multiplexer_94_out, multiplexer_95_out, multiplexer_116_out, multiplexer_119_out, multiplexer_120_out,
       multiplexer_121_out, multiplexer_122_out, multiplexer_123_out, multiplexer_124_out,
       multiplexer_125_out, multiplexer_126_out, multiplexer_127_out, multiplexer_128_out,
       multiplexer_129_out, multiplexer_130_out, multiplexer_131_out, multiplexer_132_out,
       multiplexer_133_out, multiplexer_134_out, multiplexer_135_out, multiplexer_136_out,
       multiplexer_137_out, multiplexer_138_out, multiplexer_139_out, multiplexer_140_out,
       multiplexer_141_out, multiplexer_142_out, multiplexer_143_out, multiplexer_145_out,
       multiplexer_151_out, multiplexer_152_out, multiplexer_153_out_2, multiplexer_154_out,
       multiplexer_155_out, multiplexer_156_out, multiplexer_157_out, multiplexer_166_out,
       multiplexer_172_out, multiplexer_175_out, multiplexer_179_out, multiplexer_182_out,
       multiplexer_185_out, multiplexer_186_out, multiplexer_187_out, multiplexer_190_out,
       multiplexer_192_out, multiplexer_194_out, multiplexer_196_out, multiplexer_197_out,
       multiplexer_197_out_2, multiplexer_197_out_3, multiplexer_197_out_4, multiplier_1_cout,
       multiplier_1_out, not_1_out, or_159_out, or_161_out, or_162_out, or_163_out, ram_1_data, ram_2_data,
       ram_3_data, ram_4_data, ram_5_data, ram_6_data, ram_7_data, register_5_q, register_8_q, register_9_q,
       register_10_q, register_11_q, register_12_q, register_13_q, register_14_q, register_15_q,
       register_16_q, register_17_q, register_19_q, register_20_q, register_22_q, register_23_q,
       register_25_q, register_26_q, register_27_q, register_28_q, register_30_q, register_31_q,
       register_33_q, register_34_q, rom_1_data, rom_2_data, rom_3_data, rom_4_data, rom_5_data, rom_6_data,
       rom_7_data, xor_1_out;
  wire [7:1] or_164_out;
  wire [7:6] adder_9_out;
  wire [7:7] Carry_q;
  wire [11:0] adder_1_out, adder_5_out, multiplexer_76_out, multiplexer_96_out, multiplexer_98_out,
       multiplexer_146_out, multiplexer_147_out, multiplexer_148_out, multiplexer_149_out,
       multiplexer_150_out, multiplexer_159_out, multiplexer_167_out, multiplexer_174_out,
       multiplexer_180_out, multiplexer_181_out, multiplexer_183_out, multiplexer_184_out, or_136_out,
       or_137_out, or_138_out, or_180_out, or_182_out;
  wire [15:0] adder_6_out, multiplexer_79_out, multiplexer_97_out, multiplexer_99_out, multiplexer_158_out,
       multiplexer_160_out, multiplexer_173_out, multiplexer_188_out, multiplexer_195_out, xor_2_out;
  wire [31:0] ram_8_data, v096_96_bites_32by24_video_buffer_1_out_8,
       v096_96_bites_32by24_video_buffer_1_out_9, v096_96_bites_32by24_video_buffer_1_out_10,
       v096_96_bites_32by24_video_buffer_1_out_11, v096_96_bites_32by24_video_buffer_1_out_12,
       v096_96_bites_32by24_video_buffer_1_out_13, v096_96_bites_32by24_video_buffer_1_out_14,
       v096_96_bites_32by24_video_buffer_1_out_15, v096_96_bites_32by24_video_buffer_1_out_16,
       v096_96_bites_32by24_video_buffer_1_out_17, v096_96_bites_32by24_video_buffer_1_out_18,
       v096_96_bites_32by24_video_buffer_1_out_19, v096_96_bites_32by24_video_buffer_1_out_20,
       v096_96_bites_32by24_video_buffer_1_out_21, v096_96_bites_32by24_video_buffer_1_out_22,
       v096_96_bites_32by24_video_buffer_1_out_23, v096_96_bites_32by24_video_buffer_1_out_24,
       v096_96_bites_32by24_video_buffer_1_out_25, v096_96_bites_32by24_video_buffer_1_out_26,
       v096_96_bites_32by24_video_buffer_1_out_27, v096_96_bites_32by24_video_buffer_1_out_28,
       v096_96_bites_32by24_video_buffer_1_out_29, v096_96_bites_32by24_video_buffer_1_out_30,
       v096_96_bites_32by24_video_buffer_1_out_31, v096_96_bites_32by24_video_buffer_2_out_8,
       v096_96_bites_32by24_video_buffer_2_out_9, v096_96_bites_32by24_video_buffer_2_out_10,
       v096_96_bites_32by24_video_buffer_2_out_11, v096_96_bites_32by24_video_buffer_2_out_12,
       v096_96_bites_32by24_video_buffer_2_out_13, v096_96_bites_32by24_video_buffer_2_out_14,
       v096_96_bites_32by24_video_buffer_2_out_15, v096_96_bites_32by24_video_buffer_2_out_16,
       v096_96_bites_32by24_video_buffer_2_out_17, v096_96_bites_32by24_video_buffer_2_out_18,
       v096_96_bites_32by24_video_buffer_2_out_19, v096_96_bites_32by24_video_buffer_2_out_20,
       v096_96_bites_32by24_video_buffer_2_out_21, v096_96_bites_32by24_video_buffer_2_out_22,
       v096_96_bites_32by24_video_buffer_2_out_23, v096_96_bites_32by24_video_buffer_2_out_24,
       v096_96_bites_32by24_video_buffer_2_out_25, v096_96_bites_32by24_video_buffer_2_out_26,
       v096_96_bites_32by24_video_buffer_2_out_27, v096_96_bites_32by24_video_buffer_2_out_28,
       v096_96_bites_32by24_video_buffer_2_out_29, v096_96_bites_32by24_video_buffer_2_out_30,
       v096_96_bites_32by24_video_buffer_2_out_31, v096_96_bites_32by24_video_buffer_3_out_8,
       v096_96_bites_32by24_video_buffer_3_out_9, v096_96_bites_32by24_video_buffer_3_out_10,
       v096_96_bites_32by24_video_buffer_3_out_11, v096_96_bites_32by24_video_buffer_3_out_12,
       v096_96_bites_32by24_video_buffer_3_out_13, v096_96_bites_32by24_video_buffer_3_out_14,
       v096_96_bites_32by24_video_buffer_3_out_15, v096_96_bites_32by24_video_buffer_3_out_16,
       v096_96_bites_32by24_video_buffer_3_out_17, v096_96_bites_32by24_video_buffer_3_out_18,
       v096_96_bites_32by24_video_buffer_3_out_19, v096_96_bites_32by24_video_buffer_3_out_20,
       v096_96_bites_32by24_video_buffer_3_out_21, v096_96_bites_32by24_video_buffer_3_out_22,
       v096_96_bites_32by24_video_buffer_3_out_23, v096_96_bites_32by24_video_buffer_3_out_24,
       v096_96_bites_32by24_video_buffer_3_out_25, v096_96_bites_32by24_video_buffer_3_out_26,
       v096_96_bites_32by24_video_buffer_3_out_27, v096_96_bites_32by24_video_buffer_3_out_28,
       v096_96_bites_32by24_video_buffer_3_out_29, v096_96_bites_32by24_video_buffer_3_out_30,
       v096_96_bites_32by24_video_buffer_3_out_31, v096_96_bites_32by24_video_buffer_4_out_8,
       v096_96_bites_32by24_video_buffer_4_out_9, v096_96_bites_32by24_video_buffer_4_out_10,
       v096_96_bites_32by24_video_buffer_4_out_11, v096_96_bites_32by24_video_buffer_4_out_12,
       v096_96_bites_32by24_video_buffer_4_out_13, v096_96_bites_32by24_video_buffer_4_out_14,
       v096_96_bites_32by24_video_buffer_4_out_15, v096_96_bites_32by24_video_buffer_4_out_16,
       v096_96_bites_32by24_video_buffer_4_out_17, v096_96_bites_32by24_video_buffer_4_out_18,
       v096_96_bites_32by24_video_buffer_4_out_19, v096_96_bites_32by24_video_buffer_4_out_20,
       v096_96_bites_32by24_video_buffer_4_out_21, v096_96_bites_32by24_video_buffer_4_out_22,
       v096_96_bites_32by24_video_buffer_4_out_23, v096_96_bites_32by24_video_buffer_4_out_24,
       v096_96_bites_32by24_video_buffer_4_out_25, v096_96_bites_32by24_video_buffer_4_out_26,
       v096_96_bites_32by24_video_buffer_4_out_27, v096_96_bites_32by24_video_buffer_4_out_28,
       v096_96_bites_32by24_video_buffer_4_out_29, v096_96_bites_32by24_video_buffer_4_out_30,
       v096_96_bites_32by24_video_buffer_4_out_31, v096_96_bites_32by24_video_buffer_5_out_8,
       v096_96_bites_32by24_video_buffer_5_out_9, v096_96_bites_32by24_video_buffer_5_out_10,
       v096_96_bites_32by24_video_buffer_5_out_11, v096_96_bites_32by24_video_buffer_5_out_12,
       v096_96_bites_32by24_video_buffer_5_out_13, v096_96_bites_32by24_video_buffer_5_out_14,
       v096_96_bites_32by24_video_buffer_5_out_15, v096_96_bites_32by24_video_buffer_5_out_16,
       v096_96_bites_32by24_video_buffer_5_out_17, v096_96_bites_32by24_video_buffer_5_out_18,
       v096_96_bites_32by24_video_buffer_5_out_19, v096_96_bites_32by24_video_buffer_5_out_20,
       v096_96_bites_32by24_video_buffer_5_out_21, v096_96_bites_32by24_video_buffer_5_out_22,
       v096_96_bites_32by24_video_buffer_5_out_23, v096_96_bites_32by24_video_buffer_5_out_24,
       v096_96_bites_32by24_video_buffer_5_out_25, v096_96_bites_32by24_video_buffer_5_out_26,
       v096_96_bites_32by24_video_buffer_5_out_27, v096_96_bites_32by24_video_buffer_5_out_28,
       v096_96_bites_32by24_video_buffer_5_out_29, v096_96_bites_32by24_video_buffer_5_out_30,
       v096_96_bites_32by24_video_buffer_5_out_31, v096_96_bites_32by24_video_buffer_6_out_8,
       v096_96_bites_32by24_video_buffer_6_out_9, v096_96_bites_32by24_video_buffer_6_out_10,
       v096_96_bites_32by24_video_buffer_6_out_11, v096_96_bites_32by24_video_buffer_6_out_12,
       v096_96_bites_32by24_video_buffer_6_out_13, v096_96_bites_32by24_video_buffer_6_out_14,
       v096_96_bites_32by24_video_buffer_6_out_15, v096_96_bites_32by24_video_buffer_6_out_16,
       v096_96_bites_32by24_video_buffer_6_out_17, v096_96_bites_32by24_video_buffer_6_out_18,
       v096_96_bites_32by24_video_buffer_6_out_19, v096_96_bites_32by24_video_buffer_6_out_20,
       v096_96_bites_32by24_video_buffer_6_out_21, v096_96_bites_32by24_video_buffer_6_out_22,
       v096_96_bites_32by24_video_buffer_6_out_23, v096_96_bites_32by24_video_buffer_6_out_24,
       v096_96_bites_32by24_video_buffer_6_out_25, v096_96_bites_32by24_video_buffer_6_out_26,
       v096_96_bites_32by24_video_buffer_6_out_27, v096_96_bites_32by24_video_buffer_6_out_28,
       v096_96_bites_32by24_video_buffer_6_out_29, v096_96_bites_32by24_video_buffer_6_out_30,
       v096_96_bites_32by24_video_buffer_6_out_31, v096_96_bites_32by24_video_buffer_7_out_8,
       v096_96_bites_32by24_video_buffer_7_out_9, v096_96_bites_32by24_video_buffer_7_out_10,
       v096_96_bites_32by24_video_buffer_7_out_11, v096_96_bites_32by24_video_buffer_7_out_12,
       v096_96_bites_32by24_video_buffer_7_out_13, v096_96_bites_32by24_video_buffer_7_out_14,
       v096_96_bites_32by24_video_buffer_7_out_15, v096_96_bites_32by24_video_buffer_7_out_16,
       v096_96_bites_32by24_video_buffer_7_out_17, v096_96_bites_32by24_video_buffer_7_out_18,
       v096_96_bites_32by24_video_buffer_7_out_19, v096_96_bites_32by24_video_buffer_7_out_20,
       v096_96_bites_32by24_video_buffer_7_out_21, v096_96_bites_32by24_video_buffer_7_out_22,
       v096_96_bites_32by24_video_buffer_7_out_23, v096_96_bites_32by24_video_buffer_7_out_24,
       v096_96_bites_32by24_video_buffer_7_out_25, v096_96_bites_32by24_video_buffer_7_out_26,
       v096_96_bites_32by24_video_buffer_7_out_27, v096_96_bites_32by24_video_buffer_7_out_28,
       v096_96_bites_32by24_video_buffer_7_out_29, v096_96_bites_32by24_video_buffer_7_out_30,
       v096_96_bites_32by24_video_buffer_7_out_31, v096_96_bites_32by24_video_buffer_8_out_8,
       v096_96_bites_32by24_video_buffer_8_out_9, v096_96_bites_32by24_video_buffer_8_out_10,
       v096_96_bites_32by24_video_buffer_8_out_11, v096_96_bites_32by24_video_buffer_8_out_12,
       v096_96_bites_32by24_video_buffer_8_out_13, v096_96_bites_32by24_video_buffer_8_out_14,
       v096_96_bites_32by24_video_buffer_8_out_15, v096_96_bites_32by24_video_buffer_8_out_16,
       v096_96_bites_32by24_video_buffer_8_out_17, v096_96_bites_32by24_video_buffer_8_out_18,
       v096_96_bites_32by24_video_buffer_8_out_19, v096_96_bites_32by24_video_buffer_8_out_20,
       v096_96_bites_32by24_video_buffer_8_out_21, v096_96_bites_32by24_video_buffer_8_out_22,
       v096_96_bites_32by24_video_buffer_8_out_23, v096_96_bites_32by24_video_buffer_8_out_24,
       v096_96_bites_32by24_video_buffer_8_out_25, v096_96_bites_32by24_video_buffer_8_out_26,
       v096_96_bites_32by24_video_buffer_8_out_27, v096_96_bites_32by24_video_buffer_8_out_28,
       v096_96_bites_32by24_video_buffer_8_out_29, v096_96_bites_32by24_video_buffer_8_out_30,
       v096_96_bites_32by24_video_buffer_8_out_31, v096_96_bites_32by24_video_buffer_9_out_8,
       v096_96_bites_32by24_video_buffer_9_out_9, v096_96_bites_32by24_video_buffer_9_out_10,
       v096_96_bites_32by24_video_buffer_9_out_11, v096_96_bites_32by24_video_buffer_9_out_12,
       v096_96_bites_32by24_video_buffer_9_out_13, v096_96_bites_32by24_video_buffer_9_out_14,
       v096_96_bites_32by24_video_buffer_9_out_15, v096_96_bites_32by24_video_buffer_9_out_16,
       v096_96_bites_32by24_video_buffer_9_out_17, v096_96_bites_32by24_video_buffer_9_out_18,
       v096_96_bites_32by24_video_buffer_9_out_19, v096_96_bites_32by24_video_buffer_9_out_20,
       v096_96_bites_32by24_video_buffer_9_out_21, v096_96_bites_32by24_video_buffer_9_out_22,
       v096_96_bites_32by24_video_buffer_9_out_23, v096_96_bites_32by24_video_buffer_9_out_24,
       v096_96_bites_32by24_video_buffer_9_out_25, v096_96_bites_32by24_video_buffer_9_out_26,
       v096_96_bites_32by24_video_buffer_9_out_27, v096_96_bites_32by24_video_buffer_9_out_28,
       v096_96_bites_32by24_video_buffer_9_out_29, v096_96_bites_32by24_video_buffer_9_out_30,
       v096_96_bites_32by24_video_buffer_9_out_31, v096_96_bites_32by24_video_buffer_10_out_8,
       v096_96_bites_32by24_video_buffer_10_out_9, v096_96_bites_32by24_video_buffer_10_out_10,
       v096_96_bites_32by24_video_buffer_10_out_11, v096_96_bites_32by24_video_buffer_10_out_12,
       v096_96_bites_32by24_video_buffer_10_out_13, v096_96_bites_32by24_video_buffer_10_out_14,
       v096_96_bites_32by24_video_buffer_10_out_15, v096_96_bites_32by24_video_buffer_10_out_16,
       v096_96_bites_32by24_video_buffer_10_out_17, v096_96_bites_32by24_video_buffer_10_out_18,
       v096_96_bites_32by24_video_buffer_10_out_19, v096_96_bites_32by24_video_buffer_10_out_20,
       v096_96_bites_32by24_video_buffer_10_out_21, v096_96_bites_32by24_video_buffer_10_out_22,
       v096_96_bites_32by24_video_buffer_10_out_23, v096_96_bites_32by24_video_buffer_10_out_24,
       v096_96_bites_32by24_video_buffer_10_out_25, v096_96_bites_32by24_video_buffer_10_out_26,
       v096_96_bites_32by24_video_buffer_10_out_27, v096_96_bites_32by24_video_buffer_10_out_28,
       v096_96_bites_32by24_video_buffer_10_out_29, v096_96_bites_32by24_video_buffer_10_out_30,
       v096_96_bites_32by24_video_buffer_10_out_31, v096_96_bites_32by24_video_buffer_11_out_8,
       v096_96_bites_32by24_video_buffer_11_out_9, v096_96_bites_32by24_video_buffer_11_out_10,
       v096_96_bites_32by24_video_buffer_11_out_11, v096_96_bites_32by24_video_buffer_11_out_12,
       v096_96_bites_32by24_video_buffer_11_out_13, v096_96_bites_32by24_video_buffer_11_out_14,
       v096_96_bites_32by24_video_buffer_11_out_15, v096_96_bites_32by24_video_buffer_11_out_16,
       v096_96_bites_32by24_video_buffer_11_out_17, v096_96_bites_32by24_video_buffer_11_out_18,
       v096_96_bites_32by24_video_buffer_11_out_19, v096_96_bites_32by24_video_buffer_11_out_20,
       v096_96_bites_32by24_video_buffer_11_out_21, v096_96_bites_32by24_video_buffer_11_out_22,
       v096_96_bites_32by24_video_buffer_11_out_23, v096_96_bites_32by24_video_buffer_11_out_24,
       v096_96_bites_32by24_video_buffer_11_out_25, v096_96_bites_32by24_video_buffer_11_out_26,
       v096_96_bites_32by24_video_buffer_11_out_27, v096_96_bites_32by24_video_buffer_11_out_28,
       v096_96_bites_32by24_video_buffer_11_out_29, v096_96_bites_32by24_video_buffer_11_out_30,
       v096_96_bites_32by24_video_buffer_11_out_31, v096_96_bites_32by24_video_buffer_12_out_8,
       v096_96_bites_32by24_video_buffer_12_out_9, v096_96_bites_32by24_video_buffer_12_out_10,
       v096_96_bites_32by24_video_buffer_12_out_11, v096_96_bites_32by24_video_buffer_12_out_12,
       v096_96_bites_32by24_video_buffer_12_out_13, v096_96_bites_32by24_video_buffer_12_out_14,
       v096_96_bites_32by24_video_buffer_12_out_15, v096_96_bites_32by24_video_buffer_12_out_16,
       v096_96_bites_32by24_video_buffer_12_out_17, v096_96_bites_32by24_video_buffer_12_out_18,
       v096_96_bites_32by24_video_buffer_12_out_19, v096_96_bites_32by24_video_buffer_12_out_20,
       v096_96_bites_32by24_video_buffer_12_out_21, v096_96_bites_32by24_video_buffer_12_out_22,
       v096_96_bites_32by24_video_buffer_12_out_23, v096_96_bites_32by24_video_buffer_12_out_24,
       v096_96_bites_32by24_video_buffer_12_out_25, v096_96_bites_32by24_video_buffer_12_out_26,
       v096_96_bites_32by24_video_buffer_12_out_27, v096_96_bites_32by24_video_buffer_12_out_28,
       v096_96_bites_32by24_video_buffer_12_out_29, v096_96_bites_32by24_video_buffer_12_out_30,
       v096_96_bites_32by24_video_buffer_12_out_31, v096_96_bites_32by24_video_buffer_13_out_8,
       v096_96_bites_32by24_video_buffer_13_out_9, v096_96_bites_32by24_video_buffer_13_out_10,
       v096_96_bites_32by24_video_buffer_13_out_11, v096_96_bites_32by24_video_buffer_13_out_12,
       v096_96_bites_32by24_video_buffer_13_out_13, v096_96_bites_32by24_video_buffer_13_out_14,
       v096_96_bites_32by24_video_buffer_13_out_15, v096_96_bites_32by24_video_buffer_13_out_16,
       v096_96_bites_32by24_video_buffer_13_out_17, v096_96_bites_32by24_video_buffer_13_out_18,
       v096_96_bites_32by24_video_buffer_13_out_19, v096_96_bites_32by24_video_buffer_13_out_20,
       v096_96_bites_32by24_video_buffer_13_out_21, v096_96_bites_32by24_video_buffer_13_out_22,
       v096_96_bites_32by24_video_buffer_13_out_23, v096_96_bites_32by24_video_buffer_13_out_24,
       v096_96_bites_32by24_video_buffer_13_out_25, v096_96_bites_32by24_video_buffer_13_out_26,
       v096_96_bites_32by24_video_buffer_13_out_27, v096_96_bites_32by24_video_buffer_13_out_28,
       v096_96_bites_32by24_video_buffer_13_out_29, v096_96_bites_32by24_video_buffer_13_out_30,
       v096_96_bites_32by24_video_buffer_13_out_31, v096_96_bites_32by24_video_buffer_14_out_8,
       v096_96_bites_32by24_video_buffer_14_out_9, v096_96_bites_32by24_video_buffer_14_out_10,
       v096_96_bites_32by24_video_buffer_14_out_11, v096_96_bites_32by24_video_buffer_14_out_12,
       v096_96_bites_32by24_video_buffer_14_out_13, v096_96_bites_32by24_video_buffer_14_out_14,
       v096_96_bites_32by24_video_buffer_14_out_15, v096_96_bites_32by24_video_buffer_14_out_16,
       v096_96_bites_32by24_video_buffer_14_out_17, v096_96_bites_32by24_video_buffer_14_out_18,
       v096_96_bites_32by24_video_buffer_14_out_19, v096_96_bites_32by24_video_buffer_14_out_20,
       v096_96_bites_32by24_video_buffer_14_out_21, v096_96_bites_32by24_video_buffer_14_out_22,
       v096_96_bites_32by24_video_buffer_14_out_23, v096_96_bites_32by24_video_buffer_14_out_24,
       v096_96_bites_32by24_video_buffer_14_out_25, v096_96_bites_32by24_video_buffer_14_out_26,
       v096_96_bites_32by24_video_buffer_14_out_27, v096_96_bites_32by24_video_buffer_14_out_28,
       v096_96_bites_32by24_video_buffer_14_out_29, v096_96_bites_32by24_video_buffer_14_out_30,
       v096_96_bites_32by24_video_buffer_14_out_31, v096_96_bites_32by24_video_buffer_15_out_8,
       v096_96_bites_32by24_video_buffer_15_out_9, v096_96_bites_32by24_video_buffer_15_out_10,
       v096_96_bites_32by24_video_buffer_15_out_11, v096_96_bites_32by24_video_buffer_15_out_12,
       v096_96_bites_32by24_video_buffer_15_out_13, v096_96_bites_32by24_video_buffer_15_out_14,
       v096_96_bites_32by24_video_buffer_15_out_15, v096_96_bites_32by24_video_buffer_15_out_16,
       v096_96_bites_32by24_video_buffer_15_out_17, v096_96_bites_32by24_video_buffer_15_out_18,
       v096_96_bites_32by24_video_buffer_15_out_19, v096_96_bites_32by24_video_buffer_15_out_20,
       v096_96_bites_32by24_video_buffer_15_out_21, v096_96_bites_32by24_video_buffer_15_out_22,
       v096_96_bites_32by24_video_buffer_15_out_23, v096_96_bites_32by24_video_buffer_15_out_24,
       v096_96_bites_32by24_video_buffer_15_out_25, v096_96_bites_32by24_video_buffer_15_out_26,
       v096_96_bites_32by24_video_buffer_15_out_27, v096_96_bites_32by24_video_buffer_15_out_28,
       v096_96_bites_32by24_video_buffer_15_out_29, v096_96_bites_32by24_video_buffer_15_out_30,
       v096_96_bites_32by24_video_buffer_15_out_31;

  nand nand_1 (nand_1_out, undriven_16, undriven_9);
  nand nand_2 (nand_2_out, undriven_5, undriven);
  nand nand_3 (nand_3_out, undriven_2, undriven_6);
  nand nand_4 (nand_4_out, undriven_10, undriven_11);
  or or_1 (or_1_out, undriven_7, undriven_3);
  or or_2 (or_2_out, undriven_12, undriven_13);
  or or_3 (or_3_out, undriven_14, undriven_15);
  or or_4 (or_4_out, undriven_4, undriven_8);
  D_Flip_Flop d_ff_1 (
    .clk(undriven_21), .D(undriven_17), .Q(d_ff_1_q), .Qn(d_ff_1_qn), .en(undriven_18), .reset(undriven_24));  // open: preset
  and and_1 (and_1_out, undriven_22, undriven_19);
  and and_2 (and_2_out, undriven_20, undriven_23);
  D_Flip_Flop d_ff_2 (
    .clk(undriven_27), .D(undriven_25), .Q(d_ff_2_q), .Qn(d_ff_2_qn), .en(undriven_26), .reset(undriven_32));  // open: preset
  and and_3 (and_3_out, undriven_28, undriven_29);
  and and_4 (and_4_out, undriven_30, undriven_31);
  Multiplexer #(.width(8), .disabled(0), .enable("false")) multiplexer_1 (
    .in0(Read_Ram), .in1({adder_9_out, adder_9_out_3}), .out(multiplexer_1_out), .sel(or_60_out));
  Multiplexer #(.width(8), .disabled(0), .enable("false")) multiplexer_2 (
    .in0(Read_Ram), .in1({4'b0000, adder_9_out_2}), .out(multiplexer_2_out), .sel(or_60_out));
  Multiplexer #(.width(8), .disabled(0), .enable("false")) multiplexer_3 (
    .in0(multiplexer_1_out), .in1(multiplexer_78_out), .out(multiplexer_3_out), .sel(c_out));
  Multiplexer #(.width(8), .disabled(0), .enable("false")) multiplexer_4 (
    .in0(multiplexer_2_out), .in1({4'b0000, multiplexer_78_out_2}), .out(multiplexer_4_out), .sel(c_out));
  LED led_1 (.in(register_24_q[3]));
  LED led_2 (.in(register_24_q[2]));
  Button On (.out(On_out));
  Clock clock_1 (.out(clock_1_out));
  Button Off (.out(Off_out));
  Counter #(.width(32), .max('hffffffff)) Clocks (
    .count(d_ff_21_q), .clk(clock_1_out), .clr(On_out));  // open: load, D, Q, carry
  Counter #(.width(32), .max('hffffffff)) u_Instruc (
    .count(decoder_19_out1), .clk(clock_1_out), .clr(On_out));  // open: load, D, Q, carry
  LED led_3 (.in(register_24_q[0]));
  LED led_4 (.in(register_24_q[1]));
  Decoder #(.select(4), .disabled(0)) decoder_1 (
    .out0(decoder_1_out0), .out1(decoder_1_out1), .out2(decoder_1_out2), .out3(decoder_1_out3),
    .out4(decoder_1_out4), .out5(decoder_1_out5), .out6(decoder_1_out6), .out7(decoder_1_out7),
    .out8(decoder_1_out8), .out9(decoder_1_out9), .out10(decoder_1_out10), .out11(decoder_1_out11),
    .out12(decoder_1_out12), .out13(decoder_1_out13), .out14(decoder_1_out14), .out15(decoder_1_out15),
    .sel(multiplexer_77_out[3:0]), .en(decoder_2_out15));
  Button On_2 (.out(On_2_out));
  or or_5 (or_5_out, Write_Ram, or_81_out);
  Decoder #(.select(4), .disabled(0)) decoder_2 (
    .out0(decoder_2_out0), .out1(decoder_2_out1), .out2(decoder_2_out2), .out3(decoder_2_out3),
    .out4(decoder_2_out4), .out5(decoder_2_out5), .out6(decoder_2_out6), .out7(decoder_2_out7),
    .out8(decoder_2_out8), .out9(decoder_2_out9), .out10(decoder_2_out10), .out11(decoder_2_out11),
    .out12(decoder_2_out12), .out13(decoder_2_out13), .out14(decoder_2_out14), .out15(decoder_2_out15),
    .sel(multiplexer_77_out[7:4]), .en(decoder_4_out15));
  Button button_1 (.out(button_1_out));
  or or_6 (or_6_out, in_14, or_70_out);
  Decoder #(.select(4), .disabled(0)) decoder_3 (
    .out0(decoder_3_out0), .out1(decoder_3_out1), .out2(decoder_3_out2), .out3(decoder_3_out3),
    .out4(decoder_3_out4), .out5(decoder_3_out5), .out6(decoder_3_out6), .out7(decoder_3_out7),
    .out8(decoder_3_out8), .out9(decoder_3_out9), .out10(decoder_3_out10), .out11(decoder_3_out11),
    .out12(decoder_3_out12), .out13(decoder_3_out13), .out14(decoder_3_out14), .out15(decoder_3_out15),
    .sel(multiplexer_77_out_2), .en(decoder_5_out2));
  Decoder #(.select(4), .disabled(0)) decoder_4 (
    .out0(decoder_4_out0), .out1(decoder_4_out1), .out2(decoder_4_out2), .out3(decoder_4_out3),
    .out4(decoder_4_out4), .out5(decoder_4_out5), .out6(decoder_4_out6), .out7(decoder_4_out7),
    .out8(decoder_4_out8), .out9(decoder_4_out9), .out10(decoder_4_out10), .out11(decoder_4_out11),
    .out12(decoder_4_out12), .out13(decoder_4_out13), .out14(decoder_4_out14), .out15(decoder_4_out15),
    .sel(multiplexer_77_out_2), .en(decoder_5_out15));
  or or_7 (or_7_out, button_1_out, On_out);
  Decoder #(.select(4), .disabled(0), .enable("false")) decoder_5 (
    .out0(decoder_5_out0), .out1(decoder_5_out1), .out2(decoder_5_out2), .out3(decoder_5_out3),
    .out4(decoder_5_out4), .out5(decoder_5_out5), .out6(decoder_5_out6), .out7(decoder_5_out7),
    .out8(decoder_5_out8), .out9(decoder_5_out9), .out10(decoder_5_out10), .out11(decoder_5_out11),
    .out12(decoder_5_out12), .out13(decoder_5_out13), .out14(decoder_5_out14), .out15(decoder_5_out15),
    .sel(multiplexer_77_out_3));
  DotMatrix #(.matrixcols(24), .matrixrows(32)) dotmatrix_1 (
    .col0(v096_96_bites_32by24_video_buffer_1_out_8), .col1(v096_96_bites_32by24_video_buffer_1_out_12),
    .col2(v096_96_bites_32by24_video_buffer_1_out_16), .col3(v096_96_bites_32by24_video_buffer_1_out_20),
    .col4(v096_96_bites_32by24_video_buffer_1_out_24), .col5(v096_96_bites_32by24_video_buffer_1_out_28),
    .col6(v096_96_bites_32by24_video_buffer_1_out_9), .col7(v096_96_bites_32by24_video_buffer_1_out_13),
    .col8(v096_96_bites_32by24_video_buffer_1_out_17), .col9(v096_96_bites_32by24_video_buffer_1_out_21),
    .col10(v096_96_bites_32by24_video_buffer_1_out_25), .col11(v096_96_bites_32by24_video_buffer_1_out_29),
    .col12(v096_96_bites_32by24_video_buffer_1_out_10), .col13(v096_96_bites_32by24_video_buffer_1_out_14),
    .col14(v096_96_bites_32by24_video_buffer_1_out_18), .col15(v096_96_bites_32by24_video_buffer_1_out_22),
    .col16(v096_96_bites_32by24_video_buffer_1_out_26), .col17(v096_96_bites_32by24_video_buffer_1_out_30),
    .col18(v096_96_bites_32by24_video_buffer_1_out_11), .col19(v096_96_bites_32by24_video_buffer_1_out_15),
    .col20(v096_96_bites_32by24_video_buffer_1_out_19), .col21(v096_96_bites_32by24_video_buffer_1_out_23),
    .col22(v096_96_bites_32by24_video_buffer_1_out_27), .col23(v096_96_bites_32by24_video_buffer_1_out_31));
  DotMatrix #(.matrixcols(24), .matrixrows(32)) dotmatrix_2 (
    .col0(v096_96_bites_32by24_video_buffer_2_out_8), .col1(v096_96_bites_32by24_video_buffer_2_out_12),
    .col2(v096_96_bites_32by24_video_buffer_2_out_16), .col3(v096_96_bites_32by24_video_buffer_2_out_20),
    .col4(v096_96_bites_32by24_video_buffer_2_out_24), .col5(v096_96_bites_32by24_video_buffer_2_out_28),
    .col6(v096_96_bites_32by24_video_buffer_2_out_9), .col7(v096_96_bites_32by24_video_buffer_2_out_13),
    .col8(v096_96_bites_32by24_video_buffer_2_out_17), .col9(v096_96_bites_32by24_video_buffer_2_out_21),
    .col10(v096_96_bites_32by24_video_buffer_2_out_25), .col11(v096_96_bites_32by24_video_buffer_2_out_29),
    .col12(v096_96_bites_32by24_video_buffer_2_out_10), .col13(v096_96_bites_32by24_video_buffer_2_out_14),
    .col14(v096_96_bites_32by24_video_buffer_2_out_18), .col15(v096_96_bites_32by24_video_buffer_2_out_22),
    .col16(v096_96_bites_32by24_video_buffer_2_out_26), .col17(v096_96_bites_32by24_video_buffer_2_out_30),
    .col18(v096_96_bites_32by24_video_buffer_2_out_11), .col19(v096_96_bites_32by24_video_buffer_2_out_15),
    .col20(v096_96_bites_32by24_video_buffer_2_out_19), .col21(v096_96_bites_32by24_video_buffer_2_out_23),
    .col22(v096_96_bites_32by24_video_buffer_2_out_27), .col23(v096_96_bites_32by24_video_buffer_2_out_31));
  DotMatrix #(.matrixcols(24), .matrixrows(32)) dotmatrix_3 (
    .col0(v096_96_bites_32by24_video_buffer_3_out_8), .col1(v096_96_bites_32by24_video_buffer_3_out_12),
    .col2(v096_96_bites_32by24_video_buffer_3_out_16), .col3(v096_96_bites_32by24_video_buffer_3_out_20),
    .col4(v096_96_bites_32by24_video_buffer_3_out_24), .col5(v096_96_bites_32by24_video_buffer_3_out_28),
    .col6(v096_96_bites_32by24_video_buffer_3_out_9), .col7(v096_96_bites_32by24_video_buffer_3_out_13),
    .col8(v096_96_bites_32by24_video_buffer_3_out_17), .col9(v096_96_bites_32by24_video_buffer_3_out_21),
    .col10(v096_96_bites_32by24_video_buffer_3_out_25), .col11(v096_96_bites_32by24_video_buffer_3_out_29),
    .col12(v096_96_bites_32by24_video_buffer_3_out_10), .col13(v096_96_bites_32by24_video_buffer_3_out_14),
    .col14(v096_96_bites_32by24_video_buffer_3_out_18), .col15(v096_96_bites_32by24_video_buffer_3_out_22),
    .col16(v096_96_bites_32by24_video_buffer_3_out_26), .col17(v096_96_bites_32by24_video_buffer_3_out_30),
    .col18(v096_96_bites_32by24_video_buffer_3_out_11), .col19(v096_96_bites_32by24_video_buffer_3_out_15),
    .col20(v096_96_bites_32by24_video_buffer_3_out_19), .col21(v096_96_bites_32by24_video_buffer_3_out_23),
    .col22(v096_96_bites_32by24_video_buffer_3_out_27), .col23(v096_96_bites_32by24_video_buffer_3_out_31));
  Register u_Reg_0 (.D(multiplexer_3_out), .en(decoder_6_out0), .Q(Reg_0), .clk(clock_1_out));  // open: clr
  Register u_Reg_1 (.D(multiplexer_4_out), .en(decoder_6_out1), .Q(Reg_1), .clk(clock_1_out));  // open: clr
  Register u_Reg_2 (.D(multiplexer_3_out), .en(decoder_6_out2), .Q(Reg_2), .clk(clock_1_out));  // open: clr
  Register u_Reg_3 (.D(multiplexer_4_out), .en(decoder_6_out3), .Q(Reg_3), .clk(clock_1_out));  // open: clr
  Register u_Reg_4 (.D(multiplexer_3_out), .en(decoder_6_out4), .Q(Reg_4), .clk(clock_1_out));  // open: clr
  Register u_Reg_5 (.D(multiplexer_4_out), .en(decoder_6_out5), .Q(Reg_5), .clk(clock_1_out));  // open: clr
  Register u_Reg_6 (.D(multiplexer_3_out), .en(or_95_out), .Q(Reg_6), .clk(clock_1_out));  // open: clr
  Register u_Reg_7 (.D(multiplexer_4_out), .en(decoder_6_out7), .Q(Reg_7), .clk(clock_1_out));  // open: clr
  Register u_Reg_8 (.D(multiplexer_3_out), .en(or_94_out), .Q(Reg_8), .clk(clock_1_out));  // open: clr
  Register u_Reg_9 (.D(multiplexer_4_out), .en(or_92_out), .Q(Reg_9), .clk(clock_1_out));  // open: clr
  Register u_Reg_A (.D(multiplexer_3_out), .en(or_93_out), .Q(Reg_A), .clk(clock_1_out));  // open: clr
  Register u_Reg_B (.D(multiplexer_4_out), .en(or_87_out), .Q(Reg_B), .clk(clock_1_out));  // open: clr
  Register u_Reg_C (.D(multiplexer_3_out), .en(or_88_out), .Q(Reg_C), .clk(clock_1_out));  // open: clr
  Register u_Reg_D (.D(multiplexer_4_out), .en(or_86_out), .Q(Reg_D), .clk(clock_1_out));  // open: clr
  Register u_Reg_E (.D(multiplexer_3_out), .en(or_85_out), .Q(Reg_E), .clk(clock_1_out));  // open: clr
  Register u_Reg_F (.D(multiplexer_4_out), .en(or_84_out), .Q(Reg_F), .clk(clock_1_out));  // open: clr
  V096_96_Bites_32By24_Video_Buffer v096_96_bites_32by24_video_buffer_1 (
    .out_8(v096_96_bites_32by24_video_buffer_1_out_8), .out_9(v096_96_bites_32by24_video_buffer_1_out_9),
    .out_10(v096_96_bites_32by24_video_buffer_1_out_10), .out_11(v096_96_bites_32by24_video_buffer_1_out_11),
    .out_12(v096_96_bites_32by24_video_buffer_1_out_12), .out_13(v096_96_bites_32by24_video_buffer_1_out_13),
    .out_14(v096_96_bites_32by24_video_buffer_1_out_14), .out_15(v096_96_bites_32by24_video_buffer_1_out_15),
    .out_16(v096_96_bites_32by24_video_buffer_1_out_16), .out_17(v096_96_bites_32by24_video_buffer_1_out_17),
    .out_18(v096_96_bites_32by24_video_buffer_1_out_18), .out_19(v096_96_bites_32by24_video_buffer_1_out_19),
    .out_20(v096_96_bites_32by24_video_buffer_1_out_20), .out_21(v096_96_bites_32by24_video_buffer_1_out_21),
    .out_22(v096_96_bites_32by24_video_buffer_1_out_22), .out_23(v096_96_bites_32by24_video_buffer_1_out_23),
    .out_24(v096_96_bites_32by24_video_buffer_1_out_24), .out_25(v096_96_bites_32by24_video_buffer_1_out_25),
    .out_26(v096_96_bites_32by24_video_buffer_1_out_26), .out_27(v096_96_bites_32by24_video_buffer_1_out_27),
    .out_28(v096_96_bites_32by24_video_buffer_1_out_28), .out_29(v096_96_bites_32by24_video_buffer_1_out_29),
    .out_30(v096_96_bites_32by24_video_buffer_1_out_30), .out_31(v096_96_bites_32by24_video_buffer_1_out_31),
    .in_1(decoder_12_out0), .in_2(register_4_q), .in_3(register_3_q), .in_4(multiplexer_144_out),
    .in_5(multiplexer_138_out), .in_6(clock_1_out), .in_7(and_34_out));
  V096_96_Bites_32By24_Video_Buffer v096_96_bites_32by24_video_buffer_2 (
    .out_8(v096_96_bites_32by24_video_buffer_2_out_8), .out_9(v096_96_bites_32by24_video_buffer_2_out_9),
    .out_10(v096_96_bites_32by24_video_buffer_2_out_10), .out_11(v096_96_bites_32by24_video_buffer_2_out_11),
    .out_12(v096_96_bites_32by24_video_buffer_2_out_12), .out_13(v096_96_bites_32by24_video_buffer_2_out_13),
    .out_14(v096_96_bites_32by24_video_buffer_2_out_14), .out_15(v096_96_bites_32by24_video_buffer_2_out_15),
    .out_16(v096_96_bites_32by24_video_buffer_2_out_16), .out_17(v096_96_bites_32by24_video_buffer_2_out_17),
    .out_18(v096_96_bites_32by24_video_buffer_2_out_18), .out_19(v096_96_bites_32by24_video_buffer_2_out_19),
    .out_20(v096_96_bites_32by24_video_buffer_2_out_20), .out_21(v096_96_bites_32by24_video_buffer_2_out_21),
    .out_22(v096_96_bites_32by24_video_buffer_2_out_22), .out_23(v096_96_bites_32by24_video_buffer_2_out_23),
    .out_24(v096_96_bites_32by24_video_buffer_2_out_24), .out_25(v096_96_bites_32by24_video_buffer_2_out_25),
    .out_26(v096_96_bites_32by24_video_buffer_2_out_26), .out_27(v096_96_bites_32by24_video_buffer_2_out_27),
    .out_28(v096_96_bites_32by24_video_buffer_2_out_28), .out_29(v096_96_bites_32by24_video_buffer_2_out_29),
    .out_30(v096_96_bites_32by24_video_buffer_2_out_30), .out_31(v096_96_bites_32by24_video_buffer_2_out_31),
    .in_1(decoder_13_out0), .in_2(register_4_q), .in_3(register_3_q), .in_4(multiplexer_144_out),
    .in_5(multiplexer_138_out), .in_6(clock_1_out), .in_7(and_34_out));
  V096_96_Bites_32By24_Video_Buffer v096_96_bites_32by24_video_buffer_3 (
    .out_8(v096_96_bites_32by24_video_buffer_3_out_8), .out_9(v096_96_bites_32by24_video_buffer_3_out_9),
    .out_10(v096_96_bites_32by24_video_buffer_3_out_10), .out_11(v096_96_bites_32by24_video_buffer_3_out_11),
    .out_12(v096_96_bites_32by24_video_buffer_3_out_12), .out_13(v096_96_bites_32by24_video_buffer_3_out_13),
    .out_14(v096_96_bites_32by24_video_buffer_3_out_14), .out_15(v096_96_bites_32by24_video_buffer_3_out_15),
    .out_16(v096_96_bites_32by24_video_buffer_3_out_16), .out_17(v096_96_bites_32by24_video_buffer_3_out_17),
    .out_18(v096_96_bites_32by24_video_buffer_3_out_18), .out_19(v096_96_bites_32by24_video_buffer_3_out_19),
    .out_20(v096_96_bites_32by24_video_buffer_3_out_20), .out_21(v096_96_bites_32by24_video_buffer_3_out_21),
    .out_22(v096_96_bites_32by24_video_buffer_3_out_22), .out_23(v096_96_bites_32by24_video_buffer_3_out_23),
    .out_24(v096_96_bites_32by24_video_buffer_3_out_24), .out_25(v096_96_bites_32by24_video_buffer_3_out_25),
    .out_26(v096_96_bites_32by24_video_buffer_3_out_26), .out_27(v096_96_bites_32by24_video_buffer_3_out_27),
    .out_28(v096_96_bites_32by24_video_buffer_3_out_28), .out_29(v096_96_bites_32by24_video_buffer_3_out_29),
    .out_30(v096_96_bites_32by24_video_buffer_3_out_30), .out_31(v096_96_bites_32by24_video_buffer_3_out_31),
    .in_1(decoder_14_out0), .in_2(register_4_q), .in_3(register_3_q), .in_4(multiplexer_144_out),
    .in_5(multiplexer_138_out), .in_6(clock_1_out), .in_7(and_34_out));
  Button _0 (.out(_0_out[0]));
  Button _1 (.out(_0_out[1]));
  Button _2 (.out(_0_out[2]));
  Button _3 (.out(_0_out[3]));
  Multiplexer #(.width(8), .enable("false")) multiplexer_5 (
    .in0({8{1'b0}}), .in1(Reg_0), .out(multiplexer_5_out), .sel(decoder_7_out0));
  Multiplexer #(.width(8), .enable("false")) multiplexer_6 (
    .in0(multiplexer_5_out), .in1(Reg_1), .out(multiplexer_6_out), .sel(decoder_7_out1));
  Multiplexer #(.width(8), .enable("false")) multiplexer_7 (
    .in0(multiplexer_6_out), .in1(Reg_2), .out(multiplexer_7_out), .sel(decoder_7_out2));
  Multiplexer #(.width(8), .enable("false")) multiplexer_8 (
    .in0(multiplexer_7_out), .in1(Reg_3), .out(multiplexer_8_out), .sel(decoder_7_out3));
  Multiplexer #(.width(8), .enable("false")) multiplexer_9 (
    .in0(multiplexer_8_out), .in1(Reg_4), .out(multiplexer_9_out), .sel(decoder_7_out4));
  Multiplexer #(.width(8), .enable("false")) multiplexer_10 (
    .in0(multiplexer_9_out), .in1(Reg_5), .out(multiplexer_10_out), .sel(decoder_7_out5));
  Multiplexer #(.width(8), .enable("false")) multiplexer_11 (
    .in0(multiplexer_10_out), .in1(Reg_6), .out(multiplexer_11_out), .sel(or_101_out));
  Multiplexer #(.width(8), .enable("false")) multiplexer_12 (
    .in0(multiplexer_11_out), .in1(Reg_7), .out(multiplexer_12_out), .sel(decoder_7_out7));
  Multiplexer #(.width(8), .enable("false")) multiplexer_13 (
    .in0(multiplexer_12_out), .in1(Reg_8), .out(multiplexer_13_out), .sel(decoder_7_out8));
  Multiplexer #(.width(8), .enable("false")) multiplexer_14 (
    .in0(multiplexer_13_out), .in1(Reg_9), .out(multiplexer_14_out), .sel(decoder_7_out9));
  Multiplexer #(.width(8), .enable("false")) multiplexer_15 (
    .in0(multiplexer_14_out), .in1(Reg_A), .out(multiplexer_15_out), .sel(decoder_7_out10));
  Multiplexer #(.width(8), .enable("false")) multiplexer_16 (
    .in0(multiplexer_15_out), .in1(Reg_B), .out(multiplexer_16_out), .sel(decoder_7_out11));
  Multiplexer #(.width(8), .enable("false")) multiplexer_17 (
    .in0(multiplexer_16_out), .in1(Reg_C), .out(multiplexer_17_out), .sel(decoder_7_out12));
  Multiplexer #(.width(8), .enable("false")) multiplexer_18 (
    .in0(multiplexer_17_out), .in1(Reg_D), .out(multiplexer_18_out), .sel(decoder_7_out13));
  Multiplexer #(.width(8), .enable("false")) multiplexer_19 (
    .in0(multiplexer_18_out), .in1(Reg_E), .out(multiplexer_19_out), .sel(decoder_7_out14));
  Multiplexer #(.width(8), .enable("false")) multiplexer_20 (
    .in0(multiplexer_19_out), .in1(Reg_F), .out(multiplexer_20_out), .sel(decoder_7_out15));
  Decoder #(.select(4), .disabled(0)) decoder_6 (
    .out0(decoder_6_out0), .out1(decoder_6_out1), .out2(decoder_6_out2), .out3(decoder_6_out3),
    .out4(decoder_6_out4), .out5(decoder_6_out5), .out6(decoder_6_out6), .out7(decoder_6_out7),
    .out8(decoder_6_out8), .out9(decoder_6_out9), .out10(decoder_6_out10), .out11(decoder_6_out11),
    .out12(decoder_6_out12), .out13(decoder_6_out13), .out14(decoder_6_out14), .out15(decoder_6_out15),
    .sel(multiplexer_21_out), .en(or_38_out));
  Multiplexer #(.width(4), .enable("false")) multiplexer_21 (
    .in0(multiplexer_77_out_2), .in1(multiplexer_77_out[7:4]), .out(multiplexer_21_out), .sel(or_40_out));
  Decoder #(.select(4), .disabled(0)) decoder_7 (
    .out0(decoder_7_out0), .out1(decoder_7_out1), .out2(decoder_7_out2), .out3(decoder_7_out3),
    .out4(decoder_7_out4), .out5(decoder_7_out5), .out6(decoder_7_out6), .out7(decoder_7_out7),
    .out8(decoder_7_out8), .out9(decoder_7_out9), .out10(decoder_7_out10), .out11(decoder_7_out11),
    .out12(decoder_7_out12), .out13(decoder_7_out13), .out14(decoder_7_out14), .out15(decoder_7_out15),
    .sel(multiplexer_22_out), .en(or_8_out));
  Multiplexer #(.width(4), .enable("false")) multiplexer_22 (
    .in0(multiplexer_77_out[7:4]), .in1(multiplexer_77_out_2), .out(multiplexer_22_out), .sel(_3_2_out));
  Decoder #(.select(4), .disabled(0)) decoder_8 (
    .out0(decoder_8_out0), .out1(decoder_8_out1), .out2(decoder_8_out2), .out3(decoder_8_out3),
    .out4(decoder_8_out4), .out5(decoder_8_out5), .out6(decoder_8_out6), .out7(decoder_8_out7),
    .out8(decoder_8_out8), .out9(decoder_8_out9), .out10(decoder_8_out10), .out11(decoder_8_out11),
    .out12(decoder_8_out12), .out13(decoder_8_out13), .out14(decoder_8_out14), .out15(decoder_8_out15),
    .sel(multiplexer_23_out), .en(or_9_out));
  Multiplexer #(.width(4), .enable("false")) multiplexer_23 (
    .in0(multiplexer_77_out[3:0]), .in1(4'b0000), .out(multiplexer_23_out), .sel(1'b0));
  Decoder #(.select(4), .disabled(0)) decoder_9 (
    .out0(decoder_9_out0), .out1(decoder_9_out1), .out2(decoder_9_out2), .out3(decoder_9_out3),
    .out4(decoder_9_out4), .out5(decoder_9_out5), .out6(decoder_9_out6), .out7(decoder_9_out7),
    .out8(decoder_9_out8), .out9(decoder_9_out9), .out10(decoder_9_out10), .out11(decoder_9_out11),
    .out12(decoder_9_out12), .out13(decoder_9_out13), .out14(decoder_9_out14), .out15(decoder_9_out15),
    .sel(multiplexer_24_out), .en(or_71_out));
  Multiplexer #(.width(4), .enable("false")) multiplexer_24 (
    .in0(multiplexer_77_out_2), .in1(multiplexer_77_out[7:4]), .out(multiplexer_24_out), .sel(f0_out));
  Decoder #(.select(4), .disabled(0)) decoder_10 (
    .out0(decoder_10_out0), .out1(decoder_10_out1), .out2(decoder_10_out2), .out3(decoder_10_out3),
    .out4(decoder_10_out4), .out5(decoder_10_out5), .out6(decoder_10_out6), .out7(decoder_10_out7),
    .out8(decoder_10_out8), .out9(decoder_10_out9), .out10(decoder_10_out10), .out11(decoder_10_out11),
    .out12(decoder_10_out12), .out13(decoder_10_out13), .out14(decoder_10_out14), .out15(decoder_10_out15),
    .sel(multiplexer_25_out), .en(or_53_out));
  Multiplexer #(.width(4), .enable("false")) multiplexer_25 (
    .in0(multiplexer_77_out[3:0]), .in1(4'b0000), .out(multiplexer_25_out), .sel(1'b0));
  Decoder #(.select(4), .disabled(0)) decoder_11 (
    .out0(decoder_11_out0), .out1(decoder_11_out1), .out2(decoder_11_out2), .out3(decoder_11_out3),
    .out4(decoder_11_out4), .out5(decoder_11_out5), .out6(decoder_11_out6), .out7(decoder_11_out7),
    .out8(decoder_11_out8), .out9(decoder_11_out9), .out10(decoder_11_out10), .out11(decoder_11_out11),
    .out12(decoder_11_out12), .out13(decoder_11_out13), .out14(decoder_11_out14), .out15(decoder_11_out15),
    .sel(multiplexer_26_out), .en(or_23_out));
  Multiplexer #(.width(4), .enable("false")) multiplexer_26 (
    .in0(multiplexer_77_out[7:4]), .in1(4'b0000), .out(multiplexer_26_out), .sel(1'b0));
  and _0_2 (_0_2_out, decoder_5_out0, decoder_19_out5);
  and _1_2 (_1_2_out, decoder_5_out1, decoder_19_out5);
  and _20 (_20_out, decoder_3_out0, decoder_19_out5);
  and _21 (_21_out, decoder_3_out1, decoder_19_out5);
  and _22 (_22_out, decoder_3_out2, decoder_19_out5);
  and _23 (_23_out, decoder_3_out3, decoder_19_out5);
  and _24 (_24_out, decoder_3_out4, decoder_19_out5);
  and _25 (_25_out, decoder_3_out5, decoder_19_out5);
  and _26 (_26_out, decoder_3_out6, decoder_19_out5);
  and _27 (_27_out, decoder_3_out7, decoder_19_out5);
  and _28 (_28_out, decoder_3_out8, decoder_19_out5);
  and _29 (_29_out, decoder_3_out9, decoder_19_out5);
  and _2a (_2a_out, decoder_3_out10, decoder_19_out5);
  and _2b (_2b_out, decoder_3_out11, decoder_19_out5);
  and _3_2 (_3_2_out, decoder_5_out3, decoder_19_out5);
  and _4 (_4_out, decoder_5_out4, decoder_19_out5);
  and _5 (_5_out, decoder_5_out5, decoder_19_out5);
  and _6 (_6_out, decoder_5_out6, decoder_19_out5);
  and _7 (_7_out, decoder_5_out7, decoder_19_out5);
  and _8 (_8_out, decoder_5_out8, decoder_19_out5);
  and _9 (_9_out, decoder_5_out9, decoder_19_out5);
  and a (a_out, decoder_5_out10, decoder_19_out5);
  and b (b_out, decoder_5_out11, decoder_19_out5);
  and c (c_out, decoder_5_out12, decoder_19_out5);
  and d (d_out, decoder_5_out13, decoder_19_out5);
  and e (e_out, decoder_5_out14, decoder_19_out5);
  and f0 (f0_out, decoder_4_out0, decoder_19_out5);
  and and_5 (and_5_out, decoder_4_out0, decoder_19_out4);
  and f1 (f1_out, decoder_4_out1, decoder_19_out5);
  and and_6 (and_6_out, decoder_4_out1, decoder_19_out4);
  and fe (fe_out, decoder_4_out14, decoder_19_out5);
  and fffe (fffe_out, decoder_1_out14, decoder_19_out5);
  and ffff (ffff_out, decoder_1_out15, decoder_19_out5);
  Button _4_2 (.out(_4_2_out[0]));
  Button _5_2 (.out(_4_2_out[1]));
  Button _6_2 (.out(_4_2_out[2]));
  Button _7_2 (.out(_4_2_out[3]));
  DotMatrix #(.matrixcols(24), .matrixrows(32)) dotmatrix_4 (
    .col0(v096_96_bites_32by24_video_buffer_4_out_8), .col1(v096_96_bites_32by24_video_buffer_4_out_12),
    .col2(v096_96_bites_32by24_video_buffer_4_out_16), .col3(v096_96_bites_32by24_video_buffer_4_out_20),
    .col4(v096_96_bites_32by24_video_buffer_4_out_24), .col5(v096_96_bites_32by24_video_buffer_4_out_28),
    .col6(v096_96_bites_32by24_video_buffer_4_out_9), .col7(v096_96_bites_32by24_video_buffer_4_out_13),
    .col8(v096_96_bites_32by24_video_buffer_4_out_17), .col9(v096_96_bites_32by24_video_buffer_4_out_21),
    .col10(v096_96_bites_32by24_video_buffer_4_out_25), .col11(v096_96_bites_32by24_video_buffer_4_out_29),
    .col12(v096_96_bites_32by24_video_buffer_4_out_10), .col13(v096_96_bites_32by24_video_buffer_4_out_14),
    .col14(v096_96_bites_32by24_video_buffer_4_out_18), .col15(v096_96_bites_32by24_video_buffer_4_out_22),
    .col16(v096_96_bites_32by24_video_buffer_4_out_26), .col17(v096_96_bites_32by24_video_buffer_4_out_30),
    .col18(v096_96_bites_32by24_video_buffer_4_out_11), .col19(v096_96_bites_32by24_video_buffer_4_out_15),
    .col20(v096_96_bites_32by24_video_buffer_4_out_19), .col21(v096_96_bites_32by24_video_buffer_4_out_23),
    .col22(v096_96_bites_32by24_video_buffer_4_out_27), .col23(v096_96_bites_32by24_video_buffer_4_out_31));
  DotMatrix #(.matrixcols(24), .matrixrows(32)) dotmatrix_5 (
    .col0(v096_96_bites_32by24_video_buffer_5_out_8), .col1(v096_96_bites_32by24_video_buffer_5_out_12),
    .col2(v096_96_bites_32by24_video_buffer_5_out_16), .col3(v096_96_bites_32by24_video_buffer_5_out_20),
    .col4(v096_96_bites_32by24_video_buffer_5_out_24), .col5(v096_96_bites_32by24_video_buffer_5_out_28),
    .col6(v096_96_bites_32by24_video_buffer_5_out_9), .col7(v096_96_bites_32by24_video_buffer_5_out_13),
    .col8(v096_96_bites_32by24_video_buffer_5_out_17), .col9(v096_96_bites_32by24_video_buffer_5_out_21),
    .col10(v096_96_bites_32by24_video_buffer_5_out_25), .col11(v096_96_bites_32by24_video_buffer_5_out_29),
    .col12(v096_96_bites_32by24_video_buffer_5_out_10), .col13(v096_96_bites_32by24_video_buffer_5_out_14),
    .col14(v096_96_bites_32by24_video_buffer_5_out_18), .col15(v096_96_bites_32by24_video_buffer_5_out_22),
    .col16(v096_96_bites_32by24_video_buffer_5_out_26), .col17(v096_96_bites_32by24_video_buffer_5_out_30),
    .col18(v096_96_bites_32by24_video_buffer_5_out_11), .col19(v096_96_bites_32by24_video_buffer_5_out_15),
    .col20(v096_96_bites_32by24_video_buffer_5_out_19), .col21(v096_96_bites_32by24_video_buffer_5_out_23),
    .col22(v096_96_bites_32by24_video_buffer_5_out_27), .col23(v096_96_bites_32by24_video_buffer_5_out_31));
  DotMatrix #(.matrixcols(24), .matrixrows(32)) dotmatrix_6 (
    .col0(v096_96_bites_32by24_video_buffer_6_out_8), .col1(v096_96_bites_32by24_video_buffer_6_out_12),
    .col2(v096_96_bites_32by24_video_buffer_6_out_16), .col3(v096_96_bites_32by24_video_buffer_6_out_20),
    .col4(v096_96_bites_32by24_video_buffer_6_out_24), .col5(v096_96_bites_32by24_video_buffer_6_out_28),
    .col6(v096_96_bites_32by24_video_buffer_6_out_9), .col7(v096_96_bites_32by24_video_buffer_6_out_13),
    .col8(v096_96_bites_32by24_video_buffer_6_out_17), .col9(v096_96_bites_32by24_video_buffer_6_out_21),
    .col10(v096_96_bites_32by24_video_buffer_6_out_25), .col11(v096_96_bites_32by24_video_buffer_6_out_29),
    .col12(v096_96_bites_32by24_video_buffer_6_out_10), .col13(v096_96_bites_32by24_video_buffer_6_out_14),
    .col14(v096_96_bites_32by24_video_buffer_6_out_18), .col15(v096_96_bites_32by24_video_buffer_6_out_22),
    .col16(v096_96_bites_32by24_video_buffer_6_out_26), .col17(v096_96_bites_32by24_video_buffer_6_out_30),
    .col18(v096_96_bites_32by24_video_buffer_6_out_11), .col19(v096_96_bites_32by24_video_buffer_6_out_15),
    .col20(v096_96_bites_32by24_video_buffer_6_out_19), .col21(v096_96_bites_32by24_video_buffer_6_out_23),
    .col22(v096_96_bites_32by24_video_buffer_6_out_27), .col23(v096_96_bites_32by24_video_buffer_6_out_31));
  Button _8_2 (.out(_8_2_out[0]));
  Button _9_2 (.out(_8_2_out[1]));
  Button a_2 (.out(_8_2_out[2]));
  Button b_2 (.out(_8_2_out[3]));
  Multiplexer #(.width(8), .enable("false")) multiplexer_27 (
    .in0({8{1'b0}}), .in1(Reg_0), .out(multiplexer_27_out), .sel(decoder_8_out0));
  Multiplexer #(.width(8), .enable("false")) multiplexer_28 (
    .in0(multiplexer_27_out), .in1(Reg_1), .out(multiplexer_28_out), .sel(decoder_8_out1));
  Multiplexer #(.width(8), .enable("false")) multiplexer_29 (
    .in0(multiplexer_28_out), .in1(Reg_2), .out(multiplexer_29_out), .sel(decoder_8_out2));
  Multiplexer #(.width(8), .enable("false")) multiplexer_30 (
    .in0(multiplexer_29_out), .in1(Reg_3), .out(multiplexer_30_out), .sel(decoder_8_out3));
  Multiplexer #(.width(8), .enable("false")) multiplexer_31 (
    .in0(multiplexer_30_out), .in1(Reg_4), .out(multiplexer_31_out), .sel(decoder_8_out4));
  Multiplexer #(.width(8), .enable("false")) multiplexer_32 (
    .in0(multiplexer_31_out), .in1(Reg_5), .out(multiplexer_32_out), .sel(decoder_8_out5));
  Multiplexer #(.width(8), .enable("false")) multiplexer_33 (
    .in0(multiplexer_32_out), .in1(Reg_6), .out(multiplexer_33_out), .sel(decoder_8_out6));
  Multiplexer #(.width(8), .enable("false")) multiplexer_34 (
    .in0(multiplexer_33_out), .in1(Reg_7), .out(multiplexer_34_out), .sel(decoder_8_out7));
  Multiplexer #(.width(8), .enable("false")) multiplexer_35 (
    .in0(multiplexer_34_out), .in1(Reg_8), .out(multiplexer_35_out), .sel(decoder_8_out8));
  Multiplexer #(.width(8), .enable("false")) multiplexer_36 (
    .in0(multiplexer_35_out), .in1(Reg_9), .out(multiplexer_36_out), .sel(decoder_8_out9));
  Multiplexer #(.width(8), .enable("false")) multiplexer_37 (
    .in0(multiplexer_36_out), .in1(Reg_A), .out(multiplexer_37_out), .sel(decoder_8_out10));
  Multiplexer #(.width(8), .enable("false")) multiplexer_38 (
    .in0(multiplexer_37_out), .in1(Reg_B), .out(multiplexer_38_out), .sel(decoder_8_out11));
  Multiplexer #(.width(8), .enable("false")) multiplexer_39 (
    .in0(multiplexer_38_out), .in1(Reg_C), .out(multiplexer_39_out), .sel(decoder_8_out12));
  Multiplexer #(.width(8), .enable("false")) multiplexer_40 (
    .in0(multiplexer_39_out), .in1(Reg_D), .out(multiplexer_40_out), .sel(decoder_8_out13));
  Multiplexer #(.width(8), .enable("false")) multiplexer_41 (
    .in0(multiplexer_40_out), .in1(Reg_E), .out(multiplexer_41_out), .sel(decoder_8_out14));
  Multiplexer #(.width(8), .enable("false")) multiplexer_42 (
    .in0(multiplexer_41_out), .in1(Reg_F), .out(multiplexer_42_out), .sel(decoder_8_out15));
  Multiplexer #(.disabled(0), .enable("false")) multiplexer_43 (
    .in0(or_149_out), .in1(1'b0), .out(multiplexer_43_out), .sel(register_29_q));
  or or_8 (or_8_out, _0_2_out, or_39_out);
  or or_9 (or_9_out, _1_2_out, or_10_out);
  or or_10 (or_10_out, _20_out, or_11_out);
  or or_11 (or_11_out, _21_out, or_12_out);
  or or_12 (or_12_out, _22_out, or_13_out);
  or or_13 (or_13_out, _23_out, or_14_out);
  or or_14 (or_14_out, _24_out, or_15_out);
  or or_15 (or_15_out, _25_out, or_16_out);
  or or_16 (or_16_out, _26_out, or_17_out);
  or or_17 (or_17_out, _27_out, or_21_out);
  or or_18 (or_18_out, _28_out, or_19_out);
  or or_19 (or_19_out, _29_out, or_20_out);
  or or_20 (or_20_out, _2a_out, or_51_out);
  or or_21 (or_21_out, _2b_out, 1'b0);
  or or_22 (or_22_out, _3_2_out, or_80_out);
  or or_23 (or_23_out, _4_out, or_24_out);
  or or_24 (or_24_out, _5_out, 1'b0);
  or or_25 (or_25_out, _6_out, or_26_out);
  or or_26 (or_26_out, _7_out, or_28_out);
  or or_27 (or_27_out, _8_out, and_6_out);
  or or_28 (or_28_out, _9_out, or_29_out);
  or or_29 (or_29_out, a_out, or_30_out);
  or or_30 (or_30_out, b_out, or_31_out);
  or or_31 (or_31_out, c_out, or_32_out);
  or or_32 (or_32_out, d_out, e_out);
  or or_33 (or_33_out, f0_out, or_34_out);
  or or_34 (or_34_out, and_5_out, or_35_out);
  or or_35 (or_35_out, f1_out, and_6_out);
  or or_36 (or_36_out, and_6_out, undriven_33);
  or or_37 (or_37_out, fe_out, undriven_34);
  V096_96_Bites_32By24_Video_Buffer v096_96_bites_32by24_video_buffer_4 (
    .out_8(v096_96_bites_32by24_video_buffer_4_out_8), .out_9(v096_96_bites_32by24_video_buffer_4_out_9),
    .out_10(v096_96_bites_32by24_video_buffer_4_out_10), .out_11(v096_96_bites_32by24_video_buffer_4_out_11),
    .out_12(v096_96_bites_32by24_video_buffer_4_out_12), .out_13(v096_96_bites_32by24_video_buffer_4_out_13),
    .out_14(v096_96_bites_32by24_video_buffer_4_out_14), .out_15(v096_96_bites_32by24_video_buffer_4_out_15),
    .out_16(v096_96_bites_32by24_video_buffer_4_out_16), .out_17(v096_96_bites_32by24_video_buffer_4_out_17),
    .out_18(v096_96_bites_32by24_video_buffer_4_out_18), .out_19(v096_96_bites_32by24_video_buffer_4_out_19),
    .out_20(v096_96_bites_32by24_video_buffer_4_out_20), .out_21(v096_96_bites_32by24_video_buffer_4_out_21),
    .out_22(v096_96_bites_32by24_video_buffer_4_out_22), .out_23(v096_96_bites_32by24_video_buffer_4_out_23),
    .out_24(v096_96_bites_32by24_video_buffer_4_out_24), .out_25(v096_96_bites_32by24_video_buffer_4_out_25),
    .out_26(v096_96_bites_32by24_video_buffer_4_out_26), .out_27(v096_96_bites_32by24_video_buffer_4_out_27),
    .out_28(v096_96_bites_32by24_video_buffer_4_out_28), .out_29(v096_96_bites_32by24_video_buffer_4_out_29),
    .out_30(v096_96_bites_32by24_video_buffer_4_out_30), .out_31(v096_96_bites_32by24_video_buffer_4_out_31),
    .in_1(decoder_12_out1), .in_2(register_4_q), .in_3(register_3_q), .in_4(multiplexer_144_out),
    .in_5(multiplexer_138_out), .in_6(clock_1_out), .in_7(and_34_out));
  V096_96_Bites_32By24_Video_Buffer v096_96_bites_32by24_video_buffer_5 (
    .out_8(v096_96_bites_32by24_video_buffer_5_out_8), .out_9(v096_96_bites_32by24_video_buffer_5_out_9),
    .out_10(v096_96_bites_32by24_video_buffer_5_out_10), .out_11(v096_96_bites_32by24_video_buffer_5_out_11),
    .out_12(v096_96_bites_32by24_video_buffer_5_out_12), .out_13(v096_96_bites_32by24_video_buffer_5_out_13),
    .out_14(v096_96_bites_32by24_video_buffer_5_out_14), .out_15(v096_96_bites_32by24_video_buffer_5_out_15),
    .out_16(v096_96_bites_32by24_video_buffer_5_out_16), .out_17(v096_96_bites_32by24_video_buffer_5_out_17),
    .out_18(v096_96_bites_32by24_video_buffer_5_out_18), .out_19(v096_96_bites_32by24_video_buffer_5_out_19),
    .out_20(v096_96_bites_32by24_video_buffer_5_out_20), .out_21(v096_96_bites_32by24_video_buffer_5_out_21),
    .out_22(v096_96_bites_32by24_video_buffer_5_out_22), .out_23(v096_96_bites_32by24_video_buffer_5_out_23),
    .out_24(v096_96_bites_32by24_video_buffer_5_out_24), .out_25(v096_96_bites_32by24_video_buffer_5_out_25),
    .out_26(v096_96_bites_32by24_video_buffer_5_out_26), .out_27(v096_96_bites_32by24_video_buffer_5_out_27),
    .out_28(v096_96_bites_32by24_video_buffer_5_out_28), .out_29(v096_96_bites_32by24_video_buffer_5_out_29),
    .out_30(v096_96_bites_32by24_video_buffer_5_out_30), .out_31(v096_96_bites_32by24_video_buffer_5_out_31),
    .in_1(decoder_13_out1), .in_2(register_4_q), .in_3(register_3_q), .in_4(multiplexer_144_out),
    .in_5(multiplexer_138_out), .in_6(clock_1_out), .in_7(and_34_out));
  V096_96_Bites_32By24_Video_Buffer v096_96_bites_32by24_video_buffer_6 (
    .out_8(v096_96_bites_32by24_video_buffer_6_out_8), .out_9(v096_96_bites_32by24_video_buffer_6_out_9),
    .out_10(v096_96_bites_32by24_video_buffer_6_out_10), .out_11(v096_96_bites_32by24_video_buffer_6_out_11),
    .out_12(v096_96_bites_32by24_video_buffer_6_out_12), .out_13(v096_96_bites_32by24_video_buffer_6_out_13),
    .out_14(v096_96_bites_32by24_video_buffer_6_out_14), .out_15(v096_96_bites_32by24_video_buffer_6_out_15),
    .out_16(v096_96_bites_32by24_video_buffer_6_out_16), .out_17(v096_96_bites_32by24_video_buffer_6_out_17),
    .out_18(v096_96_bites_32by24_video_buffer_6_out_18), .out_19(v096_96_bites_32by24_video_buffer_6_out_19),
    .out_20(v096_96_bites_32by24_video_buffer_6_out_20), .out_21(v096_96_bites_32by24_video_buffer_6_out_21),
    .out_22(v096_96_bites_32by24_video_buffer_6_out_22), .out_23(v096_96_bites_32by24_video_buffer_6_out_23),
    .out_24(v096_96_bites_32by24_video_buffer_6_out_24), .out_25(v096_96_bites_32by24_video_buffer_6_out_25),
    .out_26(v096_96_bites_32by24_video_buffer_6_out_26), .out_27(v096_96_bites_32by24_video_buffer_6_out_27),
    .out_28(v096_96_bites_32by24_video_buffer_6_out_28), .out_29(v096_96_bites_32by24_video_buffer_6_out_29),
    .out_30(v096_96_bites_32by24_video_buffer_6_out_30), .out_31(v096_96_bites_32by24_video_buffer_6_out_31),
    .in_1(decoder_14_out1), .in_2(register_4_q), .in_3(register_3_q), .in_4(multiplexer_144_out),
    .in_5(multiplexer_138_out), .in_6(clock_1_out), .in_7(and_34_out));
  Button c_2 (.out(c_2_out[0]));
  Button d_2 (.out(c_2_out[1]));
  Button e_2 (.out(c_2_out[2]));
  Button f (.out(c_2_out[3]));
  Multiplexer #(.width(8), .enable("false")) multiplexer_44 (
    .in0({8{1'b0}}), .in1(Reg_0), .out(multiplexer_44_out), .sel(decoder_9_out0));
  Multiplexer #(.width(8), .enable("false")) multiplexer_45 (
    .in0(multiplexer_44_out), .in1(Reg_1), .out(multiplexer_45_out), .sel(decoder_9_out1));
  Multiplexer #(.width(8), .enable("false")) multiplexer_46 (
    .in0(multiplexer_45_out), .in1(Reg_2), .out(multiplexer_46_out), .sel(decoder_9_out2));
  Multiplexer #(.width(8), .enable("false")) multiplexer_47 (
    .in0(multiplexer_46_out), .in1(Reg_3), .out(multiplexer_47_out), .sel(decoder_9_out3));
  Multiplexer #(.width(8), .enable("false")) multiplexer_48 (
    .in0(multiplexer_47_out), .in1(Reg_4), .out(multiplexer_48_out), .sel(decoder_9_out4));
  Multiplexer #(.width(8), .enable("false")) multiplexer_49 (
    .in0(multiplexer_48_out), .in1(Reg_5), .out(multiplexer_49_out), .sel(decoder_9_out5));
  Multiplexer #(.width(8), .enable("false")) multiplexer_50 (
    .in0(multiplexer_49_out), .in1(Reg_6), .out(multiplexer_50_out), .sel(or_112_out));
  Multiplexer #(.width(8), .enable("false")) multiplexer_51 (
    .in0(multiplexer_50_out), .in1(Reg_7), .out(multiplexer_51_out), .sel(decoder_9_out7));
  Multiplexer #(.width(8), .enable("false")) multiplexer_52 (
    .in0(multiplexer_51_out), .in1(Reg_8), .out(multiplexer_52_out), .sel(decoder_9_out8));
  Multiplexer #(.width(8), .enable("false")) multiplexer_53 (
    .in0(multiplexer_52_out), .in1(Reg_9), .out(multiplexer_53_out), .sel(decoder_9_out9));
  Multiplexer #(.width(8), .enable("false")) multiplexer_54 (
    .in0(multiplexer_53_out), .in1(Reg_A), .out(multiplexer_54_out), .sel(decoder_9_out10));
  Multiplexer #(.width(8), .enable("false")) multiplexer_55 (
    .in0(multiplexer_54_out), .in1(Reg_B), .out(multiplexer_55_out), .sel(decoder_9_out11));
  Multiplexer #(.width(8), .enable("false")) multiplexer_56 (
    .in0(multiplexer_55_out), .in1(Reg_C), .out(multiplexer_56_out), .sel(decoder_9_out12));
  Multiplexer #(.width(8), .enable("false")) multiplexer_57 (
    .in0(multiplexer_56_out), .in1(Reg_D), .out(multiplexer_57_out), .sel(decoder_9_out13));
  Multiplexer #(.width(8), .enable("false")) multiplexer_58 (
    .in0(multiplexer_57_out), .in1(Reg_E), .out(multiplexer_58_out), .sel(decoder_9_out14));
  Multiplexer #(.width(8), .enable("false")) multiplexer_59 (
    .in0(multiplexer_58_out), .in1(Reg_F), .out(multiplexer_59_out), .sel(decoder_9_out15));
  Register #(.width(12)) u_PC (
    .D(multiplexer_98_out), .en(multiplexer_43_out), .Q(PC), .clk(clock_1_out), .clr(or_157_out));
  Register #(.width(16)) Ins_Acc (
    .D(multiplexer_173_out), .en(decoder_19_out1), .Q(Instruc), .clk(clock_1_out));  // open: clr
  or or_38 (or_38_out, _0_2_out, or_62_out);
  or or_39 (or_39_out, _1_2_out, or_43_out);
  or or_40 (or_40_out, _20_out, or_41_out);
  or or_41 (or_41_out, _21_out, or_42_out);
  or or_42 (or_42_out, _22_out, or_66_out);
  or or_43 (or_43_out, _23_out, or_45_out);
  or or_44 (or_44_out, _24_out, or_68_out);
  or or_45 (or_45_out, _25_out, or_46_out);
  or or_46 (or_46_out, _26_out, or_47_out);
  or or_47 (or_47_out, _27_out, or_52_out);
  or or_48 (or_48_out, _28_out, or_49_out);
  or or_49 (or_49_out, _29_out, or_50_out);
  or or_50 (or_50_out, _2a_out, or_69_out);
  or or_51 (or_51_out, _2b_out, and_6_out);
  or or_52 (or_52_out, _3_2_out, 1'b0);
  or or_53 (or_53_out, _4_out, or_54_out);
  or or_54 (or_54_out, _5_out, 1'b0);
  or or_55 (or_55_out, _6_out, _7_out);
  or or_56 (or_56_out, _9_out, and_6_out);
  or or_57 (or_57_out, a_out, f0_out);
  or or_58 (or_58_out, b_out, or_59_out);
  or or_59 (or_59_out, c_out, or_74_out);
  and and_7 (and_7_out, d_out, nand_5_out);
  and and_8 (and_8_out, e_out, Carry_q[7]);
  or or_60 (or_60_out, and_5_out, f1_out);
  or or_61 (or_61_out, fe_out, undriven_35);
  LED Int_Enabled (.in(d_ff_5_q));
  Multiplexer #(.width(8), .enable("false")) multiplexer_60 (
    .in0({8{1'b0}}), .in1(Reg_0), .out(multiplexer_60_out), .sel(decoder_10_out0));
  Multiplexer #(.width(8), .enable("false")) multiplexer_61 (
    .in0(multiplexer_60_out), .in1(Reg_1), .out(multiplexer_61_out), .sel(decoder_10_out1));
  Multiplexer #(.width(8), .enable("false")) multiplexer_62 (
    .in0(multiplexer_61_out), .in1(Reg_2), .out(multiplexer_62_out), .sel(decoder_10_out2));
  Multiplexer #(.width(8), .enable("false")) multiplexer_63 (
    .in0(multiplexer_62_out), .in1(Reg_3), .out(multiplexer_63_out), .sel(decoder_10_out3));
  Multiplexer #(.width(8), .enable("false")) multiplexer_64 (
    .in0(multiplexer_63_out), .in1(Reg_4), .out(multiplexer_64_out), .sel(decoder_10_out4));
  Multiplexer #(.width(8), .enable("false")) multiplexer_65 (
    .in0(multiplexer_64_out), .in1(Reg_5), .out(multiplexer_65_out), .sel(decoder_10_out5));
  Multiplexer #(.width(8), .enable("false")) multiplexer_66 (
    .in0(multiplexer_65_out), .in1(Reg_6), .out(multiplexer_66_out), .sel(decoder_10_out6));
  Multiplexer #(.width(8), .enable("false")) multiplexer_67 (
    .in0(multiplexer_66_out), .in1(Reg_7), .out(multiplexer_67_out), .sel(or_113_out));
  Multiplexer #(.width(8), .enable("false")) multiplexer_68 (
    .in0(multiplexer_67_out), .in1(Reg_8), .out(multiplexer_68_out), .sel(decoder_10_out8));
  Multiplexer #(.width(8), .enable("false")) multiplexer_69 (
    .in0(multiplexer_68_out), .in1(Reg_9), .out(multiplexer_69_out), .sel(decoder_10_out9));
  Multiplexer #(.width(8), .enable("false")) multiplexer_70 (
    .in0(multiplexer_69_out), .in1(Reg_A), .out(multiplexer_70_out), .sel(decoder_10_out10));
  Multiplexer #(.width(8), .enable("false")) multiplexer_71 (
    .in0(multiplexer_70_out), .in1(Reg_B), .out(multiplexer_71_out), .sel(decoder_10_out11));
  Multiplexer #(.width(8), .enable("false")) multiplexer_72 (
    .in0(multiplexer_71_out), .in1(Reg_C), .out(multiplexer_72_out), .sel(decoder_10_out12));
  Multiplexer #(.width(8), .enable("false")) multiplexer_73 (
    .in0(multiplexer_72_out), .in1(Reg_D), .out(multiplexer_73_out), .sel(decoder_10_out13));
  Multiplexer #(.width(8), .enable("false")) multiplexer_74 (
    .in0(multiplexer_73_out), .in1(Reg_E), .out(multiplexer_74_out), .sel(decoder_10_out14));
  Multiplexer #(.width(8), .enable("false")) multiplexer_75 (
    .in0(multiplexer_74_out), .in1(Reg_F), .out(multiplexer_75_out), .sel(decoder_10_out15));
  Multiplexer #(.width(12), .enable("false")) multiplexer_76 (
    .in0({12{1'b0}}), .in1(PC), .out(multiplexer_76_out), .sel(decoder_19_out1));
  Multiplexer #(.width(16), .enable("false")) multiplexer_77 (
    .in0({16{1'b0}}), .in1(Instruc), .out({multiplexer_77_out_3, multiplexer_77_out_2, multiplexer_77_out}),
    .sel(or_155_out));
  or or_62 (or_62_out, _1_2_out, or_63_out);
  or or_63 (or_63_out, _20_out, or_64_out);
  or or_64 (or_64_out, _21_out, or_65_out);
  or or_65 (or_65_out, _22_out, or_78_out);
  or or_66 (or_66_out, _23_out, or_44_out);
  or or_67 (or_67_out, _24_out, or_79_out);
  or or_68 (or_68_out, _25_out, or_18_out);
  or or_69 (or_69_out, _2b_out, or_22_out);
  or or_70 (or_70_out, _4_out, or_72_out);
  or or_71 (or_71_out, _5_out, f0_out);
  or or_72 (or_72_out, _6_out, or_56_out);
  or or_73 (or_73_out, _7_out, a_out);
  or or_74 (or_74_out, and_7_out, or_75_out);
  or or_75 (or_75_out, and_8_out, fffe_out);
  or or_76 (or_76_out, and_5_out, f1_out);
  or or_77 (or_77_out, fe_out, undriven_36);
  DotMatrix #(.matrixcols(24), .matrixrows(32)) dotmatrix_7 (
    .col0(v096_96_bites_32by24_video_buffer_7_out_8), .col1(v096_96_bites_32by24_video_buffer_7_out_12),
    .col2(v096_96_bites_32by24_video_buffer_7_out_16), .col3(v096_96_bites_32by24_video_buffer_7_out_20),
    .col4(v096_96_bites_32by24_video_buffer_7_out_24), .col5(v096_96_bites_32by24_video_buffer_7_out_28),
    .col6(v096_96_bites_32by24_video_buffer_7_out_9), .col7(v096_96_bites_32by24_video_buffer_7_out_13),
    .col8(v096_96_bites_32by24_video_buffer_7_out_17), .col9(v096_96_bites_32by24_video_buffer_7_out_21),
    .col10(v096_96_bites_32by24_video_buffer_7_out_25), .col11(v096_96_bites_32by24_video_buffer_7_out_29),
    .col12(v096_96_bites_32by24_video_buffer_7_out_10), .col13(v096_96_bites_32by24_video_buffer_7_out_14),
    .col14(v096_96_bites_32by24_video_buffer_7_out_18), .col15(v096_96_bites_32by24_video_buffer_7_out_22),
    .col16(v096_96_bites_32by24_video_buffer_7_out_26), .col17(v096_96_bites_32by24_video_buffer_7_out_30),
    .col18(v096_96_bites_32by24_video_buffer_7_out_11), .col19(v096_96_bites_32by24_video_buffer_7_out_15),
    .col20(v096_96_bites_32by24_video_buffer_7_out_19), .col21(v096_96_bites_32by24_video_buffer_7_out_23),
    .col22(v096_96_bites_32by24_video_buffer_7_out_27), .col23(v096_96_bites_32by24_video_buffer_7_out_31));
  DotMatrix #(.matrixcols(24), .matrixrows(32)) dotmatrix_8 (
    .col0(v096_96_bites_32by24_video_buffer_8_out_8), .col1(v096_96_bites_32by24_video_buffer_8_out_12),
    .col2(v096_96_bites_32by24_video_buffer_8_out_16), .col3(v096_96_bites_32by24_video_buffer_8_out_20),
    .col4(v096_96_bites_32by24_video_buffer_8_out_24), .col5(v096_96_bites_32by24_video_buffer_8_out_28),
    .col6(v096_96_bites_32by24_video_buffer_8_out_9), .col7(v096_96_bites_32by24_video_buffer_8_out_13),
    .col8(v096_96_bites_32by24_video_buffer_8_out_17), .col9(v096_96_bites_32by24_video_buffer_8_out_21),
    .col10(v096_96_bites_32by24_video_buffer_8_out_25), .col11(v096_96_bites_32by24_video_buffer_8_out_29),
    .col12(v096_96_bites_32by24_video_buffer_8_out_10), .col13(v096_96_bites_32by24_video_buffer_8_out_14),
    .col14(v096_96_bites_32by24_video_buffer_8_out_18), .col15(v096_96_bites_32by24_video_buffer_8_out_22),
    .col16(v096_96_bites_32by24_video_buffer_8_out_26), .col17(v096_96_bites_32by24_video_buffer_8_out_30),
    .col18(v096_96_bites_32by24_video_buffer_8_out_11), .col19(v096_96_bites_32by24_video_buffer_8_out_15),
    .col20(v096_96_bites_32by24_video_buffer_8_out_19), .col21(v096_96_bites_32by24_video_buffer_8_out_23),
    .col22(v096_96_bites_32by24_video_buffer_8_out_27), .col23(v096_96_bites_32by24_video_buffer_8_out_31));
  DotMatrix #(.matrixcols(24), .matrixrows(32)) dotmatrix_9 (
    .col0(v096_96_bites_32by24_video_buffer_9_out_8), .col1(v096_96_bites_32by24_video_buffer_9_out_12),
    .col2(v096_96_bites_32by24_video_buffer_9_out_16), .col3(v096_96_bites_32by24_video_buffer_9_out_20),
    .col4(v096_96_bites_32by24_video_buffer_9_out_24), .col5(v096_96_bites_32by24_video_buffer_9_out_28),
    .col6(v096_96_bites_32by24_video_buffer_9_out_9), .col7(v096_96_bites_32by24_video_buffer_9_out_13),
    .col8(v096_96_bites_32by24_video_buffer_9_out_17), .col9(v096_96_bites_32by24_video_buffer_9_out_21),
    .col10(v096_96_bites_32by24_video_buffer_9_out_25), .col11(v096_96_bites_32by24_video_buffer_9_out_29),
    .col12(v096_96_bites_32by24_video_buffer_9_out_10), .col13(v096_96_bites_32by24_video_buffer_9_out_14),
    .col14(v096_96_bites_32by24_video_buffer_9_out_18), .col15(v096_96_bites_32by24_video_buffer_9_out_22),
    .col16(v096_96_bites_32by24_video_buffer_9_out_26), .col17(v096_96_bites_32by24_video_buffer_9_out_30),
    .col18(v096_96_bites_32by24_video_buffer_9_out_11), .col19(v096_96_bites_32by24_video_buffer_9_out_15),
    .col20(v096_96_bites_32by24_video_buffer_9_out_19), .col21(v096_96_bites_32by24_video_buffer_9_out_23),
    .col22(v096_96_bites_32by24_video_buffer_9_out_27), .col23(v096_96_bites_32by24_video_buffer_9_out_31));
  Multiplexer #(.width(12), .enable("false")) multiplexer_78 (
    .in0({12{1'b0}}), .in1(PC), .out({multiplexer_78_out_2, multiplexer_78_out}), .sel(or_140_out));
  Multiplexer #(.width(16), .enable("false")) multiplexer_79 (
    .in0({16{1'b0}}), .in1(Instruc), .out(multiplexer_79_out), .sel(or_25_out));
  V096_96_Bites_32By24_Video_Buffer v096_96_bites_32by24_video_buffer_7 (
    .out_8(v096_96_bites_32by24_video_buffer_7_out_8), .out_9(v096_96_bites_32by24_video_buffer_7_out_9),
    .out_10(v096_96_bites_32by24_video_buffer_7_out_10), .out_11(v096_96_bites_32by24_video_buffer_7_out_11),
    .out_12(v096_96_bites_32by24_video_buffer_7_out_12), .out_13(v096_96_bites_32by24_video_buffer_7_out_13),
    .out_14(v096_96_bites_32by24_video_buffer_7_out_14), .out_15(v096_96_bites_32by24_video_buffer_7_out_15),
    .out_16(v096_96_bites_32by24_video_buffer_7_out_16), .out_17(v096_96_bites_32by24_video_buffer_7_out_17),
    .out_18(v096_96_bites_32by24_video_buffer_7_out_18), .out_19(v096_96_bites_32by24_video_buffer_7_out_19),
    .out_20(v096_96_bites_32by24_video_buffer_7_out_20), .out_21(v096_96_bites_32by24_video_buffer_7_out_21),
    .out_22(v096_96_bites_32by24_video_buffer_7_out_22), .out_23(v096_96_bites_32by24_video_buffer_7_out_23),
    .out_24(v096_96_bites_32by24_video_buffer_7_out_24), .out_25(v096_96_bites_32by24_video_buffer_7_out_25),
    .out_26(v096_96_bites_32by24_video_buffer_7_out_26), .out_27(v096_96_bites_32by24_video_buffer_7_out_27),
    .out_28(v096_96_bites_32by24_video_buffer_7_out_28), .out_29(v096_96_bites_32by24_video_buffer_7_out_29),
    .out_30(v096_96_bites_32by24_video_buffer_7_out_30), .out_31(v096_96_bites_32by24_video_buffer_7_out_31),
    .in_1(decoder_12_out2), .in_2(register_4_q), .in_3(register_3_q), .in_4(multiplexer_144_out),
    .in_5(multiplexer_138_out), .in_6(clock_1_out), .in_7(and_34_out));
  V096_96_Bites_32By24_Video_Buffer v096_96_bites_32by24_video_buffer_8 (
    .out_8(v096_96_bites_32by24_video_buffer_8_out_8), .out_9(v096_96_bites_32by24_video_buffer_8_out_9),
    .out_10(v096_96_bites_32by24_video_buffer_8_out_10), .out_11(v096_96_bites_32by24_video_buffer_8_out_11),
    .out_12(v096_96_bites_32by24_video_buffer_8_out_12), .out_13(v096_96_bites_32by24_video_buffer_8_out_13),
    .out_14(v096_96_bites_32by24_video_buffer_8_out_14), .out_15(v096_96_bites_32by24_video_buffer_8_out_15),
    .out_16(v096_96_bites_32by24_video_buffer_8_out_16), .out_17(v096_96_bites_32by24_video_buffer_8_out_17),
    .out_18(v096_96_bites_32by24_video_buffer_8_out_18), .out_19(v096_96_bites_32by24_video_buffer_8_out_19),
    .out_20(v096_96_bites_32by24_video_buffer_8_out_20), .out_21(v096_96_bites_32by24_video_buffer_8_out_21),
    .out_22(v096_96_bites_32by24_video_buffer_8_out_22), .out_23(v096_96_bites_32by24_video_buffer_8_out_23),
    .out_24(v096_96_bites_32by24_video_buffer_8_out_24), .out_25(v096_96_bites_32by24_video_buffer_8_out_25),
    .out_26(v096_96_bites_32by24_video_buffer_8_out_26), .out_27(v096_96_bites_32by24_video_buffer_8_out_27),
    .out_28(v096_96_bites_32by24_video_buffer_8_out_28), .out_29(v096_96_bites_32by24_video_buffer_8_out_29),
    .out_30(v096_96_bites_32by24_video_buffer_8_out_30), .out_31(v096_96_bites_32by24_video_buffer_8_out_31),
    .in_1(decoder_13_out2), .in_2(register_4_q), .in_3(register_3_q), .in_4(multiplexer_144_out),
    .in_5(multiplexer_138_out), .in_6(clock_1_out), .in_7(and_34_out));
  V096_96_Bites_32By24_Video_Buffer v096_96_bites_32by24_video_buffer_9 (
    .out_8(v096_96_bites_32by24_video_buffer_9_out_8), .out_9(v096_96_bites_32by24_video_buffer_9_out_9),
    .out_10(v096_96_bites_32by24_video_buffer_9_out_10), .out_11(v096_96_bites_32by24_video_buffer_9_out_11),
    .out_12(v096_96_bites_32by24_video_buffer_9_out_12), .out_13(v096_96_bites_32by24_video_buffer_9_out_13),
    .out_14(v096_96_bites_32by24_video_buffer_9_out_14), .out_15(v096_96_bites_32by24_video_buffer_9_out_15),
    .out_16(v096_96_bites_32by24_video_buffer_9_out_16), .out_17(v096_96_bites_32by24_video_buffer_9_out_17),
    .out_18(v096_96_bites_32by24_video_buffer_9_out_18), .out_19(v096_96_bites_32by24_video_buffer_9_out_19),
    .out_20(v096_96_bites_32by24_video_buffer_9_out_20), .out_21(v096_96_bites_32by24_video_buffer_9_out_21),
    .out_22(v096_96_bites_32by24_video_buffer_9_out_22), .out_23(v096_96_bites_32by24_video_buffer_9_out_23),
    .out_24(v096_96_bites_32by24_video_buffer_9_out_24), .out_25(v096_96_bites_32by24_video_buffer_9_out_25),
    .out_26(v096_96_bites_32by24_video_buffer_9_out_26), .out_27(v096_96_bites_32by24_video_buffer_9_out_27),
    .out_28(v096_96_bites_32by24_video_buffer_9_out_28), .out_29(v096_96_bites_32by24_video_buffer_9_out_29),
    .out_30(v096_96_bites_32by24_video_buffer_9_out_30), .out_31(v096_96_bites_32by24_video_buffer_9_out_31),
    .in_1(decoder_14_out2), .in_2(register_4_q), .in_3(register_3_q), .in_4(multiplexer_144_out),
    .in_5(multiplexer_138_out), .in_6(clock_1_out), .in_7(and_34_out));
  LED Int (.in(d_ff_15_q));
  Multiplexer #(.width(8), .enable("false")) multiplexer_80 (
    .in0(Adr_In[7:0]), .in1(Reg_0), .out(multiplexer_80_out), .sel(decoder_11_out0));
  Multiplexer #(.width(8), .enable("false")) multiplexer_81 (
    .in0({4'b0000, Adr_In[11:8]}), .in1(Reg_1), .out(multiplexer_81_out), .sel(decoder_11_out0));
  Multiplexer #(.width(8), .enable("false")) multiplexer_82 (
    .in0(multiplexer_80_out), .in1(Reg_2), .out(multiplexer_82_out), .sel(decoder_11_out2));
  Multiplexer #(.width(8), .enable("false")) multiplexer_83 (
    .in0(multiplexer_81_out), .in1(Reg_3), .out(multiplexer_83_out), .sel(decoder_11_out2));
  Multiplexer #(.width(8), .enable("false")) multiplexer_84 (
    .in0(multiplexer_82_out), .in1(Reg_4), .out(multiplexer_84_out), .sel(decoder_11_out4));
  Multiplexer #(.width(8), .enable("false")) multiplexer_85 (
    .in0(multiplexer_83_out), .in1(Reg_5), .out(multiplexer_85_out), .sel(decoder_11_out4));
  Multiplexer #(.width(8), .enable("false")) multiplexer_86 (
    .in0(multiplexer_84_out), .in1(Reg_6), .out(multiplexer_86_out), .sel(decoder_11_out6));
  Multiplexer #(.width(8), .enable("false")) multiplexer_87 (
    .in0(multiplexer_85_out), .in1(Reg_7), .out(multiplexer_87_out), .sel(decoder_11_out6));
  Multiplexer #(.width(8), .enable("false")) multiplexer_88 (
    .in0(multiplexer_86_out), .in1(Reg_8), .out(multiplexer_88_out), .sel(decoder_11_out8));
  Multiplexer #(.width(8), .enable("false")) multiplexer_89 (
    .in0(multiplexer_87_out), .in1(Reg_9), .out(multiplexer_89_out), .sel(decoder_11_out8));
  Multiplexer #(.width(8), .enable("false")) multiplexer_90 (
    .in0(multiplexer_88_out), .in1(Reg_A), .out(multiplexer_90_out), .sel(or_114_out));
  Multiplexer #(.width(8), .enable("false")) multiplexer_91 (
    .in0(multiplexer_89_out), .in1(Reg_B), .out(multiplexer_91_out), .sel(or_114_out));
  Multiplexer #(.width(8), .enable("false")) multiplexer_92 (
    .in0(multiplexer_90_out), .in1(Reg_C), .out(multiplexer_92_out), .sel(or_115_out));
  Multiplexer #(.width(8), .enable("false")) multiplexer_93 (
    .in0(multiplexer_91_out), .in1(Reg_D), .out(multiplexer_93_out), .sel(or_115_out));
  Multiplexer #(.width(8), .enable("false")) multiplexer_94 (
    .in0(multiplexer_92_out), .in1(Reg_E), .out(multiplexer_94_out), .sel(decoder_11_out14));
  Multiplexer #(.width(8), .enable("false")) multiplexer_95 (
    .in0(multiplexer_93_out), .in1(Reg_F), .out(multiplexer_95_out), .sel(decoder_11_out14));
  or or_78 (or_78_out, _23_out, or_67_out);
  or or_79 (or_79_out, _25_out, or_48_out);
  or or_80 (or_80_out, _4_out, or_27_out);
  or or_81 (or_81_out, _5_out, or_83_out);
  or or_82 (or_82_out, _6_out, _9_out);
  or or_83 (or_83_out, _7_out, or_57_out);
  Multiplexer #(.width(12), .enable("false")) multiplexer_96 (
    .in0({12{1'b0}}), .in1(PC), .out(multiplexer_96_out), .sel(decoder_19_out1));
  Multiplexer #(.width(16), .enable("false")) multiplexer_97 (
    .in0({16{1'b0}}), .in1(Instruc), .out(multiplexer_97_out), .sel(_8_out));
  DotMatrix #(.matrixcols(24), .matrixrows(32)) dotmatrix_10 (
    .col0(v096_96_bites_32by24_video_buffer_10_out_8), .col1(v096_96_bites_32by24_video_buffer_10_out_12),
    .col2(v096_96_bites_32by24_video_buffer_10_out_16), .col3(v096_96_bites_32by24_video_buffer_10_out_20),
    .col4(v096_96_bites_32by24_video_buffer_10_out_24), .col5(v096_96_bites_32by24_video_buffer_10_out_28),
    .col6(v096_96_bites_32by24_video_buffer_10_out_9), .col7(v096_96_bites_32by24_video_buffer_10_out_13),
    .col8(v096_96_bites_32by24_video_buffer_10_out_17), .col9(v096_96_bites_32by24_video_buffer_10_out_21),
    .col10(v096_96_bites_32by24_video_buffer_10_out_25), .col11(v096_96_bites_32by24_video_buffer_10_out_29),
    .col12(v096_96_bites_32by24_video_buffer_10_out_10), .col13(v096_96_bites_32by24_video_buffer_10_out_14),
    .col14(v096_96_bites_32by24_video_buffer_10_out_18), .col15(v096_96_bites_32by24_video_buffer_10_out_22),
    .col16(v096_96_bites_32by24_video_buffer_10_out_26), .col17(v096_96_bites_32by24_video_buffer_10_out_30),
    .col18(v096_96_bites_32by24_video_buffer_10_out_11), .col19(v096_96_bites_32by24_video_buffer_10_out_15),
    .col20(v096_96_bites_32by24_video_buffer_10_out_19), .col21(v096_96_bites_32by24_video_buffer_10_out_23),
    .col22(v096_96_bites_32by24_video_buffer_10_out_27), .col23(v096_96_bites_32by24_video_buffer_10_out_31));
  DotMatrix #(.matrixcols(24), .matrixrows(32)) dotmatrix_11 (
    .col0(v096_96_bites_32by24_video_buffer_11_out_8), .col1(v096_96_bites_32by24_video_buffer_11_out_12),
    .col2(v096_96_bites_32by24_video_buffer_11_out_16), .col3(v096_96_bites_32by24_video_buffer_11_out_20),
    .col4(v096_96_bites_32by24_video_buffer_11_out_24), .col5(v096_96_bites_32by24_video_buffer_11_out_28),
    .col6(v096_96_bites_32by24_video_buffer_11_out_9), .col7(v096_96_bites_32by24_video_buffer_11_out_13),
    .col8(v096_96_bites_32by24_video_buffer_11_out_17), .col9(v096_96_bites_32by24_video_buffer_11_out_21),
    .col10(v096_96_bites_32by24_video_buffer_11_out_25), .col11(v096_96_bites_32by24_video_buffer_11_out_29),
    .col12(v096_96_bites_32by24_video_buffer_11_out_10), .col13(v096_96_bites_32by24_video_buffer_11_out_14),
    .col14(v096_96_bites_32by24_video_buffer_11_out_18), .col15(v096_96_bites_32by24_video_buffer_11_out_22),
    .col16(v096_96_bites_32by24_video_buffer_11_out_26), .col17(v096_96_bites_32by24_video_buffer_11_out_30),
    .col18(v096_96_bites_32by24_video_buffer_11_out_11), .col19(v096_96_bites_32by24_video_buffer_11_out_15),
    .col20(v096_96_bites_32by24_video_buffer_11_out_19), .col21(v096_96_bites_32by24_video_buffer_11_out_23),
    .col22(v096_96_bites_32by24_video_buffer_11_out_27), .col23(v096_96_bites_32by24_video_buffer_11_out_31));
  DotMatrix #(.matrixcols(24), .matrixrows(32)) dotmatrix_12 (
    .col0(v096_96_bites_32by24_video_buffer_12_out_8), .col1(v096_96_bites_32by24_video_buffer_12_out_12),
    .col2(v096_96_bites_32by24_video_buffer_12_out_16), .col3(v096_96_bites_32by24_video_buffer_12_out_20),
    .col4(v096_96_bites_32by24_video_buffer_12_out_24), .col5(v096_96_bites_32by24_video_buffer_12_out_28),
    .col6(v096_96_bites_32by24_video_buffer_12_out_9), .col7(v096_96_bites_32by24_video_buffer_12_out_13),
    .col8(v096_96_bites_32by24_video_buffer_12_out_17), .col9(v096_96_bites_32by24_video_buffer_12_out_21),
    .col10(v096_96_bites_32by24_video_buffer_12_out_25), .col11(v096_96_bites_32by24_video_buffer_12_out_29),
    .col12(v096_96_bites_32by24_video_buffer_12_out_10), .col13(v096_96_bites_32by24_video_buffer_12_out_14),
    .col14(v096_96_bites_32by24_video_buffer_12_out_18), .col15(v096_96_bites_32by24_video_buffer_12_out_22),
    .col16(v096_96_bites_32by24_video_buffer_12_out_26), .col17(v096_96_bites_32by24_video_buffer_12_out_30),
    .col18(v096_96_bites_32by24_video_buffer_12_out_11), .col19(v096_96_bites_32by24_video_buffer_12_out_15),
    .col20(v096_96_bites_32by24_video_buffer_12_out_19), .col21(v096_96_bites_32by24_video_buffer_12_out_23),
    .col22(v096_96_bites_32by24_video_buffer_12_out_27), .col23(v096_96_bites_32by24_video_buffer_12_out_31));
  Multiplexer #(.width(12), .enable("false")) multiplexer_98 (
    .in0(or_138_out), .in1(adder_1_out), .out(multiplexer_98_out), .sel(decoder_19_out1));
  Adder #(.width(12)) adder_1 (.a(12'h2), .b(multiplexer_96_out), .out(adder_1_out));  // open: cin, cout
  or or_84 (or_84_out, decoder_6_out15, 1'b0);
  V096_96_Bites_32By24_Video_Buffer v096_96_bites_32by24_video_buffer_10 (
    .out_8(v096_96_bites_32by24_video_buffer_10_out_8), .out_9(v096_96_bites_32by24_video_buffer_10_out_9),
    .out_10(v096_96_bites_32by24_video_buffer_10_out_10),
    .out_11(v096_96_bites_32by24_video_buffer_10_out_11),
    .out_12(v096_96_bites_32by24_video_buffer_10_out_12),
    .out_13(v096_96_bites_32by24_video_buffer_10_out_13),
    .out_14(v096_96_bites_32by24_video_buffer_10_out_14),
    .out_15(v096_96_bites_32by24_video_buffer_10_out_15),
    .out_16(v096_96_bites_32by24_video_buffer_10_out_16),
    .out_17(v096_96_bites_32by24_video_buffer_10_out_17),
    .out_18(v096_96_bites_32by24_video_buffer_10_out_18),
    .out_19(v096_96_bites_32by24_video_buffer_10_out_19),
    .out_20(v096_96_bites_32by24_video_buffer_10_out_20),
    .out_21(v096_96_bites_32by24_video_buffer_10_out_21),
    .out_22(v096_96_bites_32by24_video_buffer_10_out_22),
    .out_23(v096_96_bites_32by24_video_buffer_10_out_23),
    .out_24(v096_96_bites_32by24_video_buffer_10_out_24),
    .out_25(v096_96_bites_32by24_video_buffer_10_out_25),
    .out_26(v096_96_bites_32by24_video_buffer_10_out_26),
    .out_27(v096_96_bites_32by24_video_buffer_10_out_27),
    .out_28(v096_96_bites_32by24_video_buffer_10_out_28),
    .out_29(v096_96_bites_32by24_video_buffer_10_out_29),
    .out_30(v096_96_bites_32by24_video_buffer_10_out_30),
    .out_31(v096_96_bites_32by24_video_buffer_10_out_31), .in_1(decoder_12_out3), .in_2(register_4_q),
    .in_3(register_3_q), .in_4(multiplexer_144_out), .in_5(multiplexer_138_out), .in_6(clock_1_out),
    .in_7(and_34_out));
  V096_96_Bites_32By24_Video_Buffer v096_96_bites_32by24_video_buffer_11 (
    .out_8(v096_96_bites_32by24_video_buffer_11_out_8), .out_9(v096_96_bites_32by24_video_buffer_11_out_9),
    .out_10(v096_96_bites_32by24_video_buffer_11_out_10),
    .out_11(v096_96_bites_32by24_video_buffer_11_out_11),
    .out_12(v096_96_bites_32by24_video_buffer_11_out_12),
    .out_13(v096_96_bites_32by24_video_buffer_11_out_13),
    .out_14(v096_96_bites_32by24_video_buffer_11_out_14),
    .out_15(v096_96_bites_32by24_video_buffer_11_out_15),
    .out_16(v096_96_bites_32by24_video_buffer_11_out_16),
    .out_17(v096_96_bites_32by24_video_buffer_11_out_17),
    .out_18(v096_96_bites_32by24_video_buffer_11_out_18),
    .out_19(v096_96_bites_32by24_video_buffer_11_out_19),
    .out_20(v096_96_bites_32by24_video_buffer_11_out_20),
    .out_21(v096_96_bites_32by24_video_buffer_11_out_21),
    .out_22(v096_96_bites_32by24_video_buffer_11_out_22),
    .out_23(v096_96_bites_32by24_video_buffer_11_out_23),
    .out_24(v096_96_bites_32by24_video_buffer_11_out_24),
    .out_25(v096_96_bites_32by24_video_buffer_11_out_25),
    .out_26(v096_96_bites_32by24_video_buffer_11_out_26),
    .out_27(v096_96_bites_32by24_video_buffer_11_out_27),
    .out_28(v096_96_bites_32by24_video_buffer_11_out_28),
    .out_29(v096_96_bites_32by24_video_buffer_11_out_29),
    .out_30(v096_96_bites_32by24_video_buffer_11_out_30),
    .out_31(v096_96_bites_32by24_video_buffer_11_out_31), .in_1(decoder_13_out3), .in_2(register_4_q),
    .in_3(register_3_q), .in_4(multiplexer_144_out), .in_5(multiplexer_138_out), .in_6(clock_1_out),
    .in_7(and_34_out));
  V096_96_Bites_32By24_Video_Buffer v096_96_bites_32by24_video_buffer_12 (
    .out_8(v096_96_bites_32by24_video_buffer_12_out_8), .out_9(v096_96_bites_32by24_video_buffer_12_out_9),
    .out_10(v096_96_bites_32by24_video_buffer_12_out_10),
    .out_11(v096_96_bites_32by24_video_buffer_12_out_11),
    .out_12(v096_96_bites_32by24_video_buffer_12_out_12),
    .out_13(v096_96_bites_32by24_video_buffer_12_out_13),
    .out_14(v096_96_bites_32by24_video_buffer_12_out_14),
    .out_15(v096_96_bites_32by24_video_buffer_12_out_15),
    .out_16(v096_96_bites_32by24_video_buffer_12_out_16),
    .out_17(v096_96_bites_32by24_video_buffer_12_out_17),
    .out_18(v096_96_bites_32by24_video_buffer_12_out_18),
    .out_19(v096_96_bites_32by24_video_buffer_12_out_19),
    .out_20(v096_96_bites_32by24_video_buffer_12_out_20),
    .out_21(v096_96_bites_32by24_video_buffer_12_out_21),
    .out_22(v096_96_bites_32by24_video_buffer_12_out_22),
    .out_23(v096_96_bites_32by24_video_buffer_12_out_23),
    .out_24(v096_96_bites_32by24_video_buffer_12_out_24),
    .out_25(v096_96_bites_32by24_video_buffer_12_out_25),
    .out_26(v096_96_bites_32by24_video_buffer_12_out_26),
    .out_27(v096_96_bites_32by24_video_buffer_12_out_27),
    .out_28(v096_96_bites_32by24_video_buffer_12_out_28),
    .out_29(v096_96_bites_32by24_video_buffer_12_out_29),
    .out_30(v096_96_bites_32by24_video_buffer_12_out_30),
    .out_31(v096_96_bites_32by24_video_buffer_12_out_31), .in_1(decoder_14_out3), .in_2(register_4_q),
    .in_3(register_3_q), .in_4(multiplexer_144_out), .in_5(multiplexer_138_out), .in_6(clock_1_out),
    .in_7(and_34_out));
  Multiplexer #(.width(16), .enable("false")) multiplexer_99 (
    .in0({16{1'b0}}), .in1(Instruc), .out(multiplexer_99_out), .sel(_3_2_out));
  or or_85 (or_85_out, decoder_6_out14, 1'b0);
  or or_86 (or_86_out, decoder_6_out13, c_out);
  Multiplexer #(.width(4), .disabled(0), .enable("false")) multiplexer_100 (
    .in0(4'b0000), .in1(4'b0000), .out(multiplexer_100_out), .sel(_0_out[0]));
  Multiplexer #(.width(4), .disabled(0), .enable("false")) multiplexer_101 (
    .in0(multiplexer_100_out), .in1(4'b0001), .out(multiplexer_101_out), .sel(_0_out[1]));
  Multiplexer #(.width(4), .disabled(0), .enable("false")) multiplexer_102 (
    .in0(multiplexer_101_out), .in1(4'b0010), .out(multiplexer_102_out), .sel(_0_out[2]));
  Multiplexer #(.width(4), .disabled(0), .enable("false")) multiplexer_103 (
    .in0(multiplexer_102_out), .in1(4'b0011), .out(multiplexer_103_out), .sel(_0_out[3]));
  or or_87 (or_87_out, decoder_6_out11, or_76_out);
  or or_88 (or_88_out, decoder_6_out12, c_out);
  DotMatrix #(.matrixcols(24), .matrixrows(32)) dotmatrix_13 (
    .col0(v096_96_bites_32by24_video_buffer_13_out_8), .col1(v096_96_bites_32by24_video_buffer_13_out_12),
    .col2(v096_96_bites_32by24_video_buffer_13_out_16), .col3(v096_96_bites_32by24_video_buffer_13_out_20),
    .col4(v096_96_bites_32by24_video_buffer_13_out_24), .col5(v096_96_bites_32by24_video_buffer_13_out_28),
    .col6(v096_96_bites_32by24_video_buffer_13_out_9), .col7(v096_96_bites_32by24_video_buffer_13_out_13),
    .col8(v096_96_bites_32by24_video_buffer_13_out_17), .col9(v096_96_bites_32by24_video_buffer_13_out_21),
    .col10(v096_96_bites_32by24_video_buffer_13_out_25), .col11(v096_96_bites_32by24_video_buffer_13_out_29),
    .col12(v096_96_bites_32by24_video_buffer_13_out_10), .col13(v096_96_bites_32by24_video_buffer_13_out_14),
    .col14(v096_96_bites_32by24_video_buffer_13_out_18), .col15(v096_96_bites_32by24_video_buffer_13_out_22),
    .col16(v096_96_bites_32by24_video_buffer_13_out_26), .col17(v096_96_bites_32by24_video_buffer_13_out_30),
    .col18(v096_96_bites_32by24_video_buffer_13_out_11), .col19(v096_96_bites_32by24_video_buffer_13_out_15),
    .col20(v096_96_bites_32by24_video_buffer_13_out_19), .col21(v096_96_bites_32by24_video_buffer_13_out_23),
    .col22(v096_96_bites_32by24_video_buffer_13_out_27), .col23(v096_96_bites_32by24_video_buffer_13_out_31));
  DotMatrix #(.matrixcols(24), .matrixrows(32)) dotmatrix_14 (
    .col0(v096_96_bites_32by24_video_buffer_14_out_8), .col1(v096_96_bites_32by24_video_buffer_14_out_12),
    .col2(v096_96_bites_32by24_video_buffer_14_out_16), .col3(v096_96_bites_32by24_video_buffer_14_out_20),
    .col4(v096_96_bites_32by24_video_buffer_14_out_24), .col5(v096_96_bites_32by24_video_buffer_14_out_28),
    .col6(v096_96_bites_32by24_video_buffer_14_out_9), .col7(v096_96_bites_32by24_video_buffer_14_out_13),
    .col8(v096_96_bites_32by24_video_buffer_14_out_17), .col9(v096_96_bites_32by24_video_buffer_14_out_21),
    .col10(v096_96_bites_32by24_video_buffer_14_out_25), .col11(v096_96_bites_32by24_video_buffer_14_out_29),
    .col12(v096_96_bites_32by24_video_buffer_14_out_10), .col13(v096_96_bites_32by24_video_buffer_14_out_14),
    .col14(v096_96_bites_32by24_video_buffer_14_out_18), .col15(v096_96_bites_32by24_video_buffer_14_out_22),
    .col16(v096_96_bites_32by24_video_buffer_14_out_26), .col17(v096_96_bites_32by24_video_buffer_14_out_30),
    .col18(v096_96_bites_32by24_video_buffer_14_out_11), .col19(v096_96_bites_32by24_video_buffer_14_out_15),
    .col20(v096_96_bites_32by24_video_buffer_14_out_19), .col21(v096_96_bites_32by24_video_buffer_14_out_23),
    .col22(v096_96_bites_32by24_video_buffer_14_out_27), .col23(v096_96_bites_32by24_video_buffer_14_out_31));
  DotMatrix #(.matrixcols(24), .matrixrows(32)) dotmatrix_15 (
    .col0(v096_96_bites_32by24_video_buffer_15_out_8), .col1(v096_96_bites_32by24_video_buffer_15_out_12),
    .col2(v096_96_bites_32by24_video_buffer_15_out_16), .col3(v096_96_bites_32by24_video_buffer_15_out_20),
    .col4(v096_96_bites_32by24_video_buffer_15_out_24), .col5(v096_96_bites_32by24_video_buffer_15_out_28),
    .col6(v096_96_bites_32by24_video_buffer_15_out_9), .col7(v096_96_bites_32by24_video_buffer_15_out_13),
    .col8(v096_96_bites_32by24_video_buffer_15_out_17), .col9(v096_96_bites_32by24_video_buffer_15_out_21),
    .col10(v096_96_bites_32by24_video_buffer_15_out_25), .col11(v096_96_bites_32by24_video_buffer_15_out_29),
    .col12(v096_96_bites_32by24_video_buffer_15_out_10), .col13(v096_96_bites_32by24_video_buffer_15_out_14),
    .col14(v096_96_bites_32by24_video_buffer_15_out_18), .col15(v096_96_bites_32by24_video_buffer_15_out_22),
    .col16(v096_96_bites_32by24_video_buffer_15_out_26), .col17(v096_96_bites_32by24_video_buffer_15_out_30),
    .col18(v096_96_bites_32by24_video_buffer_15_out_11), .col19(v096_96_bites_32by24_video_buffer_15_out_15),
    .col20(v096_96_bites_32by24_video_buffer_15_out_19), .col21(v096_96_bites_32by24_video_buffer_15_out_23),
    .col22(v096_96_bites_32by24_video_buffer_15_out_27), .col23(v096_96_bites_32by24_video_buffer_15_out_31));
  Register #(.width(4), .trigger("high")) register_1 (
    .D(multiplexer_115_out), .en(or_111_out), .Q(Data[3:0]), .clk(or_111_out));  // open: clr
  D_Flip_Flop d_ff_3 (
    .clk(clock_1_out), .D(or_107_out), .Q(d_ff_3_q), .Qn(d_ff_3_qn), .en(undriven_37), .reset(undriven_39));  // open: preset
  D_Flip_Flop d_ff_4 (
    .clk(or_111_out), .D(or_111_out), .Q(d_ff_4_q), .Qn(d_ff_4_qn), .en(undriven_38), .reset(or_96_out));  // open: preset
  or or_89 (or_89_out, _0_out[0], _0_out[1]);
  or or_90 (or_90_out, or_89_out, _0_out[2]);
  or or_91 (or_91_out, or_90_out, _0_out[3]);
  or or_92 (or_92_out, decoder_6_out9, 1'b0);
  or or_93 (or_93_out, decoder_6_out10, or_76_out);
  V096_96_Bites_32By24_Video_Buffer v096_96_bites_32by24_video_buffer_13 (
    .out_8(v096_96_bites_32by24_video_buffer_13_out_8), .out_9(v096_96_bites_32by24_video_buffer_13_out_9),
    .out_10(v096_96_bites_32by24_video_buffer_13_out_10),
    .out_11(v096_96_bites_32by24_video_buffer_13_out_11),
    .out_12(v096_96_bites_32by24_video_buffer_13_out_12),
    .out_13(v096_96_bites_32by24_video_buffer_13_out_13),
    .out_14(v096_96_bites_32by24_video_buffer_13_out_14),
    .out_15(v096_96_bites_32by24_video_buffer_13_out_15),
    .out_16(v096_96_bites_32by24_video_buffer_13_out_16),
    .out_17(v096_96_bites_32by24_video_buffer_13_out_17),
    .out_18(v096_96_bites_32by24_video_buffer_13_out_18),
    .out_19(v096_96_bites_32by24_video_buffer_13_out_19),
    .out_20(v096_96_bites_32by24_video_buffer_13_out_20),
    .out_21(v096_96_bites_32by24_video_buffer_13_out_21),
    .out_22(v096_96_bites_32by24_video_buffer_13_out_22),
    .out_23(v096_96_bites_32by24_video_buffer_13_out_23),
    .out_24(v096_96_bites_32by24_video_buffer_13_out_24),
    .out_25(v096_96_bites_32by24_video_buffer_13_out_25),
    .out_26(v096_96_bites_32by24_video_buffer_13_out_26),
    .out_27(v096_96_bites_32by24_video_buffer_13_out_27),
    .out_28(v096_96_bites_32by24_video_buffer_13_out_28),
    .out_29(v096_96_bites_32by24_video_buffer_13_out_29),
    .out_30(v096_96_bites_32by24_video_buffer_13_out_30),
    .out_31(v096_96_bites_32by24_video_buffer_13_out_31), .in_1(decoder_12_out4), .in_2(register_4_q),
    .in_3(register_3_q), .in_4(multiplexer_144_out), .in_5(multiplexer_138_out), .in_6(clock_1_out),
    .in_7(and_34_out));
  V096_96_Bites_32By24_Video_Buffer v096_96_bites_32by24_video_buffer_14 (
    .out_8(v096_96_bites_32by24_video_buffer_14_out_8), .out_9(v096_96_bites_32by24_video_buffer_14_out_9),
    .out_10(v096_96_bites_32by24_video_buffer_14_out_10),
    .out_11(v096_96_bites_32by24_video_buffer_14_out_11),
    .out_12(v096_96_bites_32by24_video_buffer_14_out_12),
    .out_13(v096_96_bites_32by24_video_buffer_14_out_13),
    .out_14(v096_96_bites_32by24_video_buffer_14_out_14),
    .out_15(v096_96_bites_32by24_video_buffer_14_out_15),
    .out_16(v096_96_bites_32by24_video_buffer_14_out_16),
    .out_17(v096_96_bites_32by24_video_buffer_14_out_17),
    .out_18(v096_96_bites_32by24_video_buffer_14_out_18),
    .out_19(v096_96_bites_32by24_video_buffer_14_out_19),
    .out_20(v096_96_bites_32by24_video_buffer_14_out_20),
    .out_21(v096_96_bites_32by24_video_buffer_14_out_21),
    .out_22(v096_96_bites_32by24_video_buffer_14_out_22),
    .out_23(v096_96_bites_32by24_video_buffer_14_out_23),
    .out_24(v096_96_bites_32by24_video_buffer_14_out_24),
    .out_25(v096_96_bites_32by24_video_buffer_14_out_25),
    .out_26(v096_96_bites_32by24_video_buffer_14_out_26),
    .out_27(v096_96_bites_32by24_video_buffer_14_out_27),
    .out_28(v096_96_bites_32by24_video_buffer_14_out_28),
    .out_29(v096_96_bites_32by24_video_buffer_14_out_29),
    .out_30(v096_96_bites_32by24_video_buffer_14_out_30),
    .out_31(v096_96_bites_32by24_video_buffer_14_out_31), .in_1(decoder_13_out4), .in_2(register_4_q),
    .in_3(register_3_q), .in_4(multiplexer_144_out), .in_5(multiplexer_138_out), .in_6(clock_1_out),
    .in_7(and_34_out));
  V096_96_Bites_32By24_Video_Buffer v096_96_bites_32by24_video_buffer_15 (
    .out_8(v096_96_bites_32by24_video_buffer_15_out_8), .out_9(v096_96_bites_32by24_video_buffer_15_out_9),
    .out_10(v096_96_bites_32by24_video_buffer_15_out_10),
    .out_11(v096_96_bites_32by24_video_buffer_15_out_11),
    .out_12(v096_96_bites_32by24_video_buffer_15_out_12),
    .out_13(v096_96_bites_32by24_video_buffer_15_out_13),
    .out_14(v096_96_bites_32by24_video_buffer_15_out_14),
    .out_15(v096_96_bites_32by24_video_buffer_15_out_15),
    .out_16(v096_96_bites_32by24_video_buffer_15_out_16),
    .out_17(v096_96_bites_32by24_video_buffer_15_out_17),
    .out_18(v096_96_bites_32by24_video_buffer_15_out_18),
    .out_19(v096_96_bites_32by24_video_buffer_15_out_19),
    .out_20(v096_96_bites_32by24_video_buffer_15_out_20),
    .out_21(v096_96_bites_32by24_video_buffer_15_out_21),
    .out_22(v096_96_bites_32by24_video_buffer_15_out_22),
    .out_23(v096_96_bites_32by24_video_buffer_15_out_23),
    .out_24(v096_96_bites_32by24_video_buffer_15_out_24),
    .out_25(v096_96_bites_32by24_video_buffer_15_out_25),
    .out_26(v096_96_bites_32by24_video_buffer_15_out_26),
    .out_27(v096_96_bites_32by24_video_buffer_15_out_27),
    .out_28(v096_96_bites_32by24_video_buffer_15_out_28),
    .out_29(v096_96_bites_32by24_video_buffer_15_out_29),
    .out_30(v096_96_bites_32by24_video_buffer_15_out_30),
    .out_31(v096_96_bites_32by24_video_buffer_15_out_31), .in_1(decoder_14_out4), .in_2(register_4_q),
    .in_3(register_3_q), .in_4(multiplexer_144_out), .in_5(multiplexer_138_out), .in_6(clock_1_out),
    .in_7(and_34_out));
  Register #(.width(4)) register_2 (.D(Data[3:0]), .en(or_111_out), .Q(Data[7:4]), .clk(or_111_out));  // open: clr
  or or_94 (or_94_out, decoder_6_out8, 1'b0);
  or or_95 (or_95_out, decoder_6_out6, or_82_out);
  Decoder #(.select(3), .disabled(0)) decoder_12 (
    .out0(decoder_12_out0), .out1(decoder_12_out1), .out2(decoder_12_out2), .out3(decoder_12_out3),
    .out4(decoder_12_out4), .sel(register_3_q_2), .en(decoder_15_out0));  // open: out5, out6, out7
  Decoder #(.select(3), .disabled(0)) decoder_13 (
    .out0(decoder_13_out0), .out1(decoder_13_out1), .out2(decoder_13_out2), .out3(decoder_13_out3),
    .out4(decoder_13_out4), .sel(register_3_q_2), .en(decoder_15_out1));  // open: out5, out6, out7
  Decoder #(.select(3), .disabled(0)) decoder_14 (
    .out0(decoder_14_out0), .out1(decoder_14_out1), .out2(decoder_14_out2), .out3(decoder_14_out3),
    .out4(decoder_14_out4), .sel(register_3_q_2), .en(decoder_15_out2));  // open: out5, out6, out7
  D_Flip_Flop d_ff_5 (
    .clk(clock_1_out), .D(d_ff_3_q), .Q(d_ff_5_q), .Qn(d_ff_5_qn), .en(d_ff_3_q), .reset(or_102_out));  // open: preset
  or or_96 (or_96_out, d_ff_3_q, or_102_out);
  D_Flip_Flop d_ff_6 (
    .clk(or_111_out), .D(d_ff_4_q), .Q(d_ff_6_q), .Qn(d_ff_6_qn), .en(d_ff_4_q), .reset(or_96_out));  // open: preset
  Multiplexer #(.width(4), .disabled(0), .enable("false")) multiplexer_104 (
    .in0(multiplexer_103_out), .in1(4'b0100), .out(multiplexer_104_out), .sel(_4_2_out[0]));
  Multiplexer #(.width(4), .disabled(0), .enable("false")) multiplexer_105 (
    .in0(multiplexer_104_out), .in1(4'b0101), .out(multiplexer_105_out), .sel(_4_2_out[1]));
  Multiplexer #(.width(4), .disabled(0), .enable("false")) multiplexer_106 (
    .in0(multiplexer_105_out), .in1(4'b0110), .out(multiplexer_106_out), .sel(_4_2_out[2]));
  Multiplexer #(.width(4), .disabled(0), .enable("false")) multiplexer_107 (
    .in0(multiplexer_106_out), .in1(4'b0111), .out(multiplexer_107_out), .sel(_4_2_out[3]));
  and and_9 (and_9_out, d_ff_5_q, d_ff_8_q);
  D_Flip_Flop d_ff_7 (
    .clk(clock_1_out), .D(d_ff_6_q), .Q(d_ff_7_q), .Qn(d_ff_7_qn), .en(d_ff_6_q), .reset(or_96_out));  // open: preset
  or or_97 (or_97_out, or_91_out, _4_2_out[0]);
  or or_98 (or_98_out, or_97_out, _4_2_out[1]);
  or or_99 (or_99_out, or_98_out, _4_2_out[2]);
  or or_100 (or_100_out, or_99_out, _4_2_out[3]);
  or or_101 (or_101_out, decoder_7_out6, d_out);
  Decoder #(.select(2), .disabled(0)) decoder_15 (
    .out0(decoder_15_out0), .out1(decoder_15_out1), .out2(decoder_15_out2), .sel(register_4_q_2),
    .en(or_126_out));  // open: out3
  or or_102 (or_102_out, and_24_out, d_ff_12_q);
  D_Flip_Flop d_ff_8 (
    .clk(clock_1_out), .D(d_ff_7_q), .Q(d_ff_8_q), .Qn(d_ff_8_qn), .en(d_ff_7_q), .reset(or_96_out));  // open: preset
  Multiplexer #(.width(4), .disabled(0), .enable("false")) multiplexer_108 (
    .in0(multiplexer_107_out), .in1(4'b1000), .out(multiplexer_108_out), .sel(_8_2_out[0]));
  Multiplexer #(.width(4), .disabled(0), .enable("false")) multiplexer_109 (
    .in0(multiplexer_108_out), .in1(4'b1001), .out(multiplexer_109_out), .sel(_8_2_out[1]));
  Multiplexer #(.width(4), .disabled(0), .enable("false")) multiplexer_110 (
    .in0(multiplexer_109_out), .in1(4'b1010), .out(multiplexer_110_out), .sel(_8_2_out[2]));
  Multiplexer #(.width(4), .disabled(0), .enable("false")) multiplexer_111 (
    .in0(multiplexer_110_out), .in1(4'b1011), .out(multiplexer_111_out), .sel(_8_2_out[3]));
  D_Flip_Flop d_ff_9 (
    .clk(clock_1_out), .D(and_9_out), .Q(d_ff_9_q), .Qn(d_ff_9_qn), .en(and_9_out), .reset(or_96_out));  // open: preset
  or or_103 (or_103_out, or_100_out, _8_2_out[0]);
  or or_104 (or_104_out, or_103_out, _8_2_out[1]);
  or or_105 (or_105_out, or_104_out, _8_2_out[2]);
  or or_106 (or_106_out, or_105_out, _8_2_out[3]);
  or or_107 (or_107_out, and_23_out, decoder_18_out15);
  D_Flip_Flop d_ff_10 (
    .clk(clock_1_out), .D(d_ff_9_q), .Q(d_ff_10_q), .Qn(d_ff_10_qn), .en(d_ff_9_q), .reset(or_96_out));  // open: preset
  Multiplexer #(.width(4), .disabled(0), .enable("false")) multiplexer_112 (
    .in0(multiplexer_111_out), .in1(4'b1100), .out(multiplexer_112_out), .sel(c_2_out[0]));
  or or_108 (or_108_out, or_106_out, c_2_out[0]);
  Multiplexer #(.width(4), .disabled(0), .enable("false")) multiplexer_113 (
    .in0(multiplexer_112_out), .in1(4'b1101), .out(multiplexer_113_out), .sel(c_2_out[1]));
  or or_109 (or_109_out, or_108_out, c_2_out[1]);
  Multiplexer #(.width(4), .disabled(0), .enable("false")) multiplexer_114 (
    .in0(multiplexer_113_out), .in1(4'b1110), .out(multiplexer_114_out), .sel(c_2_out[2]));
  or or_110 (or_110_out, or_109_out, c_2_out[2]);
  Multiplexer #(.width(4), .disabled(0), .enable("false")) multiplexer_115 (
    .in0(multiplexer_114_out), .in1(4'b1111), .out(multiplexer_115_out), .sel(c_2_out[3]));
  or or_111 (or_111_out, or_110_out, c_2_out[3]);
  or or_112 (or_112_out, decoder_9_out6, or_73_out);
  D_Flip_Flop d_ff_11 (
    .clk(clock_1_out), .D(d_ff_10_q), .Q(d_ff_11_q), .Qn(d_ff_11_qn), .en(d_ff_10_q), .reset(or_96_out));  // open: preset
  and and_10 (and_10_out, ~adder_9_out_3[0], ~adder_9_out_3[1], adder_9_out_3[2], adder_9_out_3[3]);  // AND_Gate
  and and_11 (and_11_out, adder_9_out_3[0], ~adder_9_out_3[1], adder_9_out_3[2], adder_9_out_3[3]);  // AND_Gate
  and and_12 (and_12_out, adder_9_out_3[4], adder_9_out_3[5], adder_9_out[6], adder_9_out[7], adder_9_out_2[0], adder_9_out_2[1], adder_9_out_2[2], adder_9_out_2[3]);
  and and_13 (and_13_out, ~adder_9_out_3[0], ~adder_9_out_3[1], ~adder_9_out_3[2], ~adder_9_out_3[3]);  // AND_Gate
  and and_14 (and_14_out, adder_9_out_3[0], ~adder_9_out_3[1], ~adder_9_out_3[2], ~adder_9_out_3[3]);  // AND_Gate
  and and_15 (and_15_out, ~adder_9_out_3[0], ~adder_9_out_3[1], ~adder_9_out_3[2], adder_9_out_3[3]);  // AND_Gate
  and and_16 (and_16_out, ~adder_9_out_3[0], adder_9_out_3[1], ~adder_9_out_3[2], ~adder_9_out_3[3]);  // AND_Gate
  and and_17 (and_17_out, adder_9_out_3[0], adder_9_out_3[1], ~adder_9_out_3[2], ~adder_9_out_3[3]);  // AND_Gate
  and and_18 (and_18_out, ~adder_9_out_3[0], ~adder_9_out_3[1], adder_9_out_3[2], ~adder_9_out_3[3]);  // AND_Gate
  and and_19 (and_19_out, adder_9_out_3[0], ~adder_9_out_3[1], adder_9_out_3[2], ~adder_9_out_3[3]);  // AND_Gate
  and and_20 (and_20_out, ~adder_9_out_3[0], adder_9_out_3[1], adder_9_out_3[2], ~adder_9_out_3[3]);  // AND_Gate
  and and_21 (and_21_out, adder_9_out_3[0], adder_9_out_3[1], adder_9_out_3[2], ~adder_9_out_3[3]);  // AND_Gate
  and and_22 (and_22_out, adder_9_out_3[0], adder_9_out_3[1], adder_9_out_3[2], adder_9_out_3[3]);
  D_Flip_Flop d_ff_12 (
    .clk(clock_1_out), .D(d_ff_11_q), .Q(d_ff_12_q), .Qn(d_ff_12_qn), .en(d_ff_11_q), .reset(or_96_out));  // open: preset
  or or_113 (or_113_out, decoder_10_out7, or_55_out);
  and and_23 (and_23_out, and_12_out, and_10_out, or_5_out);
  and and_24 (and_24_out, and_12_out, and_11_out, or_5_out);
  and and_25 (and_25_out, and_12_out, and_13_out, or_5_out);
  and and_26 (and_26_out, and_12_out, and_14_out, or_5_out);
  and and_27 (and_27_out, and_12_out, and_15_out, or_5_out);
  and and_28 (and_28_out, and_12_out, and_16_out);
  and and_29 (and_29_out, and_12_out, and_17_out);
  and and_30 (and_30_out, and_12_out, and_18_out);
  and and_31 (and_31_out, and_12_out, and_19_out);
  and and_32 (and_32_out, and_12_out, and_20_out);
  and and_33 (and_33_out, and_12_out, and_21_out);
  and and_34 (and_34_out, and_12_out, and_22_out, or_5_out);
  or or_114 (or_114_out, decoder_11_out10, or_33_out);
  Register register_3 (
    .D(or_161_out), .en(and_25_out), .Q({register_3_q_3, register_3_q_2, register_3_q}), .clk(clock_1_out));  // open: clr
  Register register_4 (
    .D(or_161_out), .en(and_26_out), .Q({register_4_q_3, register_4_q_2, register_4_q}), .clk(clock_1_out));  // open: clr
  Register register_5 (.D(or_161_out), .en(and_27_out), .Q(register_5_q), .clk(clock_1_out));  // open: clr
  Register #(.width(1)) register_6 (
    .D(and_27_out), .en(and_27_out), .Q(register_6_q), .clk(clock_1_out), .clr(decoder_16_out14));
  or or_115 (or_115_out, decoder_11_out12, fffe_out);
  and and_35 (and_35_out, or_125_out, ~register_5_q[7], ~register_5_q[6], ~register_5_q[5], ~register_5_q[4], register_5_q[3], register_5_q[2], ~register_5_q[1], ~register_5_q[0]);  // AND_Gate
  or or_116 (or_116_out, multiplexer_20_out[7], multiplexer_20_out[6], multiplexer_20_out[5], multiplexer_20_out[4], multiplexer_20_out[3], multiplexer_20_out[2], multiplexer_20_out[1], multiplexer_20_out[0]);
  Multiplexer #(.width(8), .enable("false")) multiplexer_116 (
    .in0(multiplexer_42_out), .in1(multiplexer_99_out[7:0]), .out(multiplexer_116_out), .sel(_3_2_out));
  Register #(.width(4)) register_7 (
    .D(adder_4_out), .en(register_6_q), .Q(register_7_q), .clk(clock_1_out), .clr(decoder_16_out14));
  Decoder #(.select(4), .disabled(0)) decoder_16 (
    .out2(decoder_16_out2), .out3(decoder_16_out3), .out4(decoder_16_out4), .out5(decoder_16_out5),
    .out6(decoder_16_out6), .out7(decoder_16_out7), .out8(decoder_16_out8), .out9(decoder_16_out9),
    .out10(decoder_16_out10), .out11(decoder_16_out11), .out12(decoder_16_out12), .out13(decoder_16_out13),
    .out14(decoder_16_out14), .out15(decoder_16_out15), .sel(adder_4_out), .en(register_6_q));  // open: out0, out1
  Adder adder_2 (
    .a(multiplexer_20_out), .b(multiplexer_116_out), .out(adder_2_out), .cin(_20_out), .cout(adder_2_cout));
  assign not_1_out = ~multiplexer_116_out;  // NOT_Gate not_1, 8 bits wide
  assign xor_1_out = multiplexer_20_out ^ multiplexer_116_out;  // XOR_Gate xor_1, 8 bits wide
  Adder adder_3 (.a(multiplexer_20_out), .b(not_1_out), .out(adder_3_out), .cin(_25_out));  // open: cout
  Multiplier multiplier_1 (
    .a(multiplexer_20_out), .b(multiplexer_116_out), .out(multiplier_1_out), .cout(multiplier_1_cout));  // open: cin
  Divider divider_1 (
    .a(multiplexer_20_out), .b(multiplexer_116_out), .out(divider_1_out), .rem(divider_1_rem));  // open: upper
  or or_117 (or_117_out, and_33_out, and_32_out, and_31_out, and_30_out, and_29_out, and_28_out);
  nand nand_5 (nand_5_out, or_116_out, or_116_out);
  Multiplexer #(.enable("false")) multiplexer_117 (
    .in0(adder_2_cout), .in1(multiplexer_116_out[7]), .out(multiplexer_117_out), .sel(_22_out));
  or or_118 (or_118_out, multiplexer_117_out, multiplexer_118_out);
  Adder #(.width(4)) adder_4 (.a(4'b0000), .b(register_7_q), .out(adder_4_out), .cin(1'b1));  // open: cout
  and and_36 (and_36_out, or_5_out, or_117_out);
  Multiplexer #(.enable("false")) multiplexer_118 (
    .in0(1'b0), .in1(multiplexer_116_out[0]), .out(multiplexer_118_out), .sel(_24_out));
  Multiplexer #(.width(8), .enable("false")) multiplexer_119 (
    .in0(multiplier_1_cout), .in1(divider_1_rem), .out(multiplexer_119_out), .sel(_27_out));
  Multiplexer #(.width(8), .enable("false")) multiplexer_120 (
    .in0(multiplier_1_out), .in1(divider_1_out), .out(multiplexer_120_out), .sel(_27_out));
  or or_119 (or_119_out, decoder_16_out2, decoder_16_out3);
  or or_120 (or_120_out, decoder_16_out4, decoder_16_out5);
  or or_121 (or_121_out, decoder_16_out6, decoder_16_out7);
  or or_122 (or_122_out, decoder_16_out8, decoder_16_out9);
  or or_123 (or_123_out, decoder_16_out10, decoder_16_out11);
  or or_124 (or_124_out, decoder_16_out12, decoder_16_out13);
  or or_125 (or_125_out, decoder_16_out3, decoder_16_out5, decoder_16_out7, decoder_16_out9, decoder_16_out11, decoder_16_out13);
  or or_126 (or_126_out, and_36_out, or_125_out);
  or or_127 (or_127_out, _1_2_out, _3_2_out, _20_out);
  or or_128 (or_128_out, _20_out, _24_out, _3_2_out, _22_out, _1_2_out);
  or or_129 (or_129_out, _26_out, _27_out);
  ROM rom_1 (.addr(register_5_q), .data(rom_1_data), .sel(or_119_out));
  ROM rom_2 (.addr(register_5_q), .data(rom_2_data), .sel(or_120_out));
  ROM rom_3 (.addr(register_5_q), .data(rom_3_data), .sel(or_121_out));
  ROM rom_4 (.addr(register_5_q), .data(rom_4_data), .sel(or_122_out));
  ROM rom_5 (.addr(register_5_q), .data(rom_5_data), .sel(or_123_out));
  ROM rom_6 (.addr(register_5_q), .data(rom_6_data), .sel(or_124_out));
  Multiplexer #(.width(8), .enable("false")) multiplexer_121 (
    .in0({8{1'b0}}), .in1({multiplexer_116_out[6:0], 1'b0}), .out(multiplexer_121_out), .sel(_22_out));
  Multiplexer #(.width(8), .enable("false")) multiplexer_122 (
    .in0(multiplexer_121_out), .in1({1'b0, multiplexer_116_out[7:1]}), .out(multiplexer_122_out),
    .sel(_24_out));
  Multiplexer #(.width(8), .enable("false")) multiplexer_123 (
    .in0(multiplexer_122_out), .in1(multiplexer_20_out), .out(multiplexer_123_out), .sel(_0_2_out));
  Multiplexer #(.width(8), .enable("false")) multiplexer_124 (
    .in0(multiplexer_123_out), .in1(adder_2_out), .out(multiplexer_124_out), .sel(or_127_out));
  Multiplexer #(.width(8), .enable("false")) multiplexer_125 (
    .in0(multiplexer_124_out), .in1(not_1_out), .out(multiplexer_125_out), .sel(_21_out));
  Multiplexer #(.width(8), .enable("false")) multiplexer_126 (
    .in0(multiplexer_125_out), .in1(xor_1_out), .out(multiplexer_126_out), .sel(_23_out));
  Multiplexer #(.width(8), .enable("false")) multiplexer_127 (
    .in0(multiplexer_126_out), .in1(adder_3_out), .out(multiplexer_127_out), .sel(_25_out));
  Multiplexer #(.width(8), .enable("false")) multiplexer_128 (
    .in0(multiplexer_127_out), .in1({8{Carry_q[7]}}), .out(multiplexer_128_out), .sel(_2a_out));
  Multiplexer #(.width(8), .enable("false")) multiplexer_129 (
    .in0(multiplexer_128_out), .in1({8{multiplexer_116_out[7]}}), .out(multiplexer_129_out), .sel(_2b_out));
  D_Flip_Flop #(.trigger("falling")) Carry (
    .clk(decoder_19_out5), .D(or_118_out), .Q(Carry_q[7]), .en(or_128_out));  // open: Qn, preset, reset
  Multiplexer #(.width(8), .enable("false")) multiplexer_130 (
    .in0(multiplexer_129_out), .in1(Hi_q), .out(multiplexer_130_out), .sel(_28_out));
  Register Hi (.D(multiplexer_119_out), .en(or_129_out), .Q(Hi_q), .clk(clock_1_out));  // open: clr
  Multiplexer #(.width(8), .enable("false")) multiplexer_131 (
    .in0(multiplexer_130_out), .in1(Lo_q), .out(multiplexer_131_out), .sel(_29_out));
  Register Lo (.D(multiplexer_120_out), .en(or_129_out), .Q(Lo_q), .clk(clock_1_out));  // open: clr
  Multiplexer #(.width(8), .disabled(0), .enable("false")) multiplexer_132 (
    .in0({8{1'b0}}), .in1(rom_1_data), .out(multiplexer_132_out), .sel(or_119_out));
  Multiplexer #(.width(8), .disabled(0), .enable("false")) multiplexer_133 (
    .in0(multiplexer_132_out), .in1(rom_2_data), .out(multiplexer_133_out), .sel(or_120_out));
  Multiplexer #(.width(8), .disabled(0), .enable("false")) multiplexer_134 (
    .in0(multiplexer_133_out), .in1(rom_3_data), .out(multiplexer_134_out), .sel(or_121_out));
  Multiplexer #(.width(8), .disabled(0), .enable("false")) multiplexer_135 (
    .in0(multiplexer_134_out), .in1(rom_4_data), .out(multiplexer_135_out), .sel(or_122_out));
  Multiplexer #(.width(8), .disabled(0), .enable("false")) multiplexer_136 (
    .in0(multiplexer_135_out), .in1(rom_5_data), .out(multiplexer_136_out), .sel(or_123_out));
  Multiplexer #(.width(8), .disabled(0), .enable("false")) multiplexer_137 (
    .in0(multiplexer_136_out), .in1(rom_6_data), .out(multiplexer_137_out), .sel(or_124_out));
  Multiplexer #(.width(8), .disabled(0), .enable("false")) multiplexer_138 (
    .in0(multiplexer_137_out), .in1(or_161_out), .out(multiplexer_138_out), .sel(or_117_out));
  or or_130 (or_130_out, or_119_out, and_28_out);
  or or_131 (or_131_out, or_120_out, and_29_out);
  or or_132 (or_132_out, or_121_out, and_30_out);
  or or_133 (or_133_out, or_122_out, and_31_out);
  or or_134 (or_134_out, or_123_out, and_32_out);
  or or_135 (or_135_out, or_124_out, and_33_out);
  Multiplexer #(.width(8), .disabled(0), .enable("false")) multiplexer_139 (
    .in0({8{1'b0}}), .in1(8'h1), .out(multiplexer_139_out), .sel(or_130_out));
  Multiplexer #(.width(8), .disabled(0), .enable("false")) multiplexer_140 (
    .in0(multiplexer_139_out), .in1(8'h2), .out(multiplexer_140_out), .sel(or_131_out));
  Multiplexer #(.width(8), .disabled(0), .enable("false")) multiplexer_141 (
    .in0(multiplexer_140_out), .in1(8'h3), .out(multiplexer_141_out), .sel(or_132_out));
  Multiplexer #(.width(8), .disabled(0), .enable("false")) multiplexer_142 (
    .in0(multiplexer_141_out), .in1(8'h4), .out(multiplexer_142_out), .sel(or_133_out));
  Multiplexer #(.width(8), .disabled(0), .enable("false")) multiplexer_143 (
    .in0(multiplexer_142_out), .in1(8'h5), .out(multiplexer_143_out), .sel(or_134_out));
  Multiplexer #(.width(8), .disabled(0), .enable("false")) multiplexer_144 (
    .in0(multiplexer_143_out), .in1(8'h6),
    .out({multiplexer_144_out_3, multiplexer_144_out_2[3], multiplexer_144_out}), .sel(or_135_out));
  assign or_136_out = {multiplexer_95_out[3:0], multiplexer_94_out} | multiplexer_76_out;  // OR_Gate or_136, 12 bits wide
  assign or_137_out = or_136_out | multiplexer_79_out[11:0];  // OR_Gate or_137, 12 bits wide
  Multiplexer #(.width(8), .enable("false")) multiplexer_145 (
    .in0({8{1'b0}}), .in1(8'h3), .out(multiplexer_145_out), .sel(and_9_out));
  LED led_5 (.in(register_9_q[1]));
  LED led_6 (.in(register_9_q[1]));
  LED led_7 (.in(register_9_q[1]));
  LED led_8 (.in(register_9_q[2]));
  LED led_9 (.in(register_9_q[6]));
  LED led_10 (.in(register_9_q[6]));
  LED led_11 (.in(register_9_q[2]));
  LED led_12 (.in(register_9_q[2]));
  LED led_13 (.in(register_9_q[7]));
  LED led_14 (.in(register_9_q[7]));
  LED led_15 (.in(register_9_q[7]));
  LED led_16 (.in(register_9_q[6]));
  LED led_17 (.in(register_9_q[5]));
  LED led_18 (.in(register_9_q[3]));
  LED led_19 (.in(register_9_q[3]));
  LED led_20 (.in(register_9_q[5]));
  LED led_21 (.in(register_9_q[3]));
  LED led_22 (.in(register_9_q[5]));
  LED led_23 (.in(register_9_q[4]));
  LED led_24 (.in(register_9_q[4]));
  LED led_25 (.in(register_9_q[4]));
  assign or_138_out = multiplexer_150_out | or_137_out;  // OR_Gate or_138, 12 bits wide
  Multiplexer #(.width(12), .enable("false")) multiplexer_146 (
    .in0({12{1'b0}}), .in1(12'hf02), .out(multiplexer_146_out), .sel(or_141_out));
  Multiplexer #(.width(12), .enable("false")) multiplexer_147 (
    .in0(multiplexer_146_out), .in1(12'hf03), .out(multiplexer_147_out), .sel(or_144_out));
  Multiplexer #(.width(12), .enable("false")) multiplexer_148 (
    .in0(multiplexer_147_out), .in1(12'hf00), .out(multiplexer_148_out), .sel(or_145_out));
  Multiplexer #(.width(12), .enable("false")) multiplexer_149 (
    .in0(multiplexer_148_out), .in1(12'hf01), .out(multiplexer_149_out), .sel(or_142_out));
  Multiplexer #(.width(12), .enable("false")) multiplexer_150 (
    .in0(multiplexer_149_out), .in1(12'hf04), .out(multiplexer_150_out), .sel(or_146_out));
  Multiplexer #(.width(8), .enable("false")) multiplexer_151 (
    .in0(multiplexer_145_out), .in1(8'h8), .out(multiplexer_151_out), .sel(register_29_q));
  or or_139 (or_139_out, register_29_q, and_9_out);
  Multiplexer #(.width(8), .enable("false")) multiplexer_152 (
    .in0(register_28_q), .in1(Data), .out(multiplexer_152_out), .sel(and_9_out));
  LED led_26 (.in(register_8_q[1]));
  LED led_27 (.in(register_8_q[1]));
  LED led_28 (.in(register_8_q[6]));
  LED led_29 (.in(register_8_q[6]));
  LED led_30 (.in(register_8_q[7]));
  LED led_31 (.in(register_8_q[6]));
  LED led_32 (.in(register_8_q[7]));
  LED led_33 (.in(register_8_q[5]));
  LED led_34 (.in(register_8_q[5]));
  LED led_35 (.in(register_8_q[5]));
  LED led_36 (.in(register_8_q[4]));
  LED led_37 (.in(register_8_q[4]));
  Register register_8 (.D(register_11_q), .en(and_45_out[0]), .Q(register_8_q), .clk(d_ff_22_q));  // open: clr
  Register register_9 (.D(register_10_q), .en(and_45_out[0]), .Q(register_9_q), .clk(d_ff_22_q));  // open: clr
  Adder #(.width(12)) adder_5 (
    .a(12'hffe), .b({multiplexer_78_out_2, multiplexer_78_out}), .out(adder_5_out));  // open: cin, cout
  Register #(.trigger("high")) Exc_Code (
    .D(multiplexer_151_out), .en(or_139_out), .Q(Exc_Code_q), .clk(or_139_out), .clr(decoder_18_out15));
  Register #(.trigger("high")) Exc_Data (
    .D(multiplexer_152_out), .en(or_139_out), .Q(Exc_Data_q), .clk(or_139_out), .clr(decoder_18_out15));
  LED led_38 (.in(register_8_q[1]));
  LED led_39 (.in(register_8_q[2]));
  LED led_40 (.in(register_8_q[2]));
  LED led_41 (.in(register_8_q[2]));
  LED led_42 (.in(register_8_q[7]));
  LED led_43 (.in(register_8_q[3]));
  LED led_44 (.in(register_8_q[3]));
  LED led_45 (.in(register_8_q[3]));
  LED led_46 (.in(register_8_q[4]));
  Multiplexer #(.width(12), .enable("false")) multiplexer_153 (
    .in0({multiplexer_78_out_2, multiplexer_78_out}), .in1(adder_5_out),
    .out({multiplexer_153_out, multiplexer_153_out_2}), .sel(and_37_out));
  Multiplexer #(.width(8), .enable("false")) multiplexer_154 (
    .in0({8{1'b0}}), .in1({4'b1011, multiplexer_153_out}), .out(multiplexer_154_out), .sel(or_141_out));
  Multiplexer #(.width(8), .enable("false")) multiplexer_155 (
    .in0(multiplexer_154_out), .in1(multiplexer_153_out_2), .out(multiplexer_155_out), .sel(or_144_out));
  Multiplexer #(.width(8), .enable("false")) multiplexer_156 (
    .in0(multiplexer_155_out), .in1(Exc_Code_q), .out(multiplexer_156_out), .sel(or_145_out));
  Multiplexer #(.width(8), .enable("false")) multiplexer_157 (
    .in0(multiplexer_156_out), .in1(Exc_Data_q), .out(multiplexer_157_out), .sel(or_142_out));
  LED led_47 (.in(register_10_q[1]));
  LED led_48 (.in(register_10_q[1]));
  LED led_49 (.in(register_10_q[1]));
  LED led_50 (.in(register_10_q[6]));
  LED led_51 (.in(register_10_q[6]));
  LED led_52 (.in(register_10_q[6]));
  LED led_53 (.in(register_10_q[7]));
  LED led_54 (.in(register_10_q[7]));
  LED led_55 (.in(register_10_q[7]));
  LED led_56 (.in(register_10_q[5]));
  LED led_57 (.in(register_10_q[5]));
  LED led_58 (.in(register_10_q[5]));
  LED led_59 (.in(register_10_q[4]));
  LED led_60 (.in(register_10_q[4]));
  LED led_61 (.in(register_10_q[4]));
  LED led_62 (.in(register_11_q[1]));
  LED led_63 (.in(register_10_q[2]));
  LED led_64 (.in(register_11_q[6]));
  LED led_65 (.in(register_10_q[2]));
  LED led_66 (.in(register_11_q[6]));
  LED led_67 (.in(register_11_q[7]));
  LED led_68 (.in(register_11_q[6]));
  LED led_69 (.in(register_10_q[2]));
  LED led_70 (.in(register_11_q[5]));
  LED led_71 (.in(register_10_q[3]));
  LED led_72 (.in(register_10_q[3]));
  LED led_73 (.in(register_11_q[5]));
  LED led_74 (.in(register_11_q[5]));
  LED led_75 (.in(register_10_q[3]));
  LED led_76 (.in(register_11_q[4]));
  Register register_10 (.D(register_12_q), .en(and_45_out[0]), .Q(register_10_q), .clk(d_ff_22_q));  // open: clr
  Button button_2 (.out(button_2_out));
  LED led_77 (.in(undriven_40));
  LED led_78 (.in(register_11_q[1]));
  LED led_79 (.in(register_11_q[1]));
  LED led_80 (.in(register_11_q[2]));
  LED led_81 (.in(register_11_q[2]));
  LED led_82 (.in(register_11_q[2]));
  LED led_83 (.in(register_11_q[7]));
  LED led_84 (.in(register_11_q[7]));
  LED led_85 (.in(register_11_q[3]));
  LED led_86 (.in(register_11_q[3]));
  LED led_87 (.in(register_11_q[3]));
  LED led_88 (.in(register_11_q[4]));
  LED led_89 (.in(register_11_q[4]));
  Register register_11 (.D(register_13_q), .en(and_45_out[0]), .Q(register_11_q), .clk(d_ff_22_q));  // open: clr
  and and_37 (and_37_out, ~Exc_Code_q[7], ~Exc_Code_q[6], ~Exc_Code_q[5], ~Exc_Code_q[4], Exc_Code_q[3], ~Exc_Code_q[2], ~Exc_Code_q[1], ~Exc_Code_q[0]);  // AND_Gate
  or or_140 (or_140_out, or_147_out, c_out);
  LED led_90 (.in(register_12_q[1]));
  LED led_91 (.in(register_12_q[1]));
  LED led_92 (.in(register_12_q[6]));
  LED led_93 (.in(register_12_q[6]));
  LED led_94 (.in(register_12_q[7]));
  LED led_95 (.in(register_12_q[6]));
  LED led_96 (.in(register_12_q[7]));
  LED led_97 (.in(register_12_q[5]));
  LED led_98 (.in(register_12_q[5]));
  LED led_99 (.in(register_12_q[5]));
  LED led_100 (.in(register_12_q[4]));
  LED led_101 (.in(register_12_q[4]));
  or or_141 (or_141_out, decoder_18_out3, decoder_18_out2);
  or or_142 (or_142_out, decoder_18_out12, decoder_18_out11);
  or or_143 (or_143_out, undriven_41, undriven_42);
  LED led_102 (.in(register_12_q[1]));
  LED led_103 (.in(register_12_q[2]));
  LED led_104 (.in(register_12_q[2]));
  LED led_105 (.in(register_12_q[7]));
  LED led_106 (.in(register_12_q[2]));
  LED led_107 (.in(register_12_q[3]));
  LED led_108 (.in(register_12_q[3]));
  LED led_109 (.in(register_12_q[3]));
  LED led_110 (.in(register_12_q[4]));
  Register register_12 (.D(register_14_q), .en(and_45_out[0]), .Q(register_12_q), .clk(d_ff_22_q));  // open: clr
  and and_38 (and_38_out, or_190_out, decoder_19_out5);
  and and_39 (and_39_out, ~or_190_out, decoder_17_out2);  // AND_Gate
  or or_144 (or_144_out, decoder_18_out5, decoder_18_out6);
  or or_145 (or_145_out, decoder_18_out8, decoder_18_out9);
  or or_146 (or_146_out, decoder_18_out13, decoder_18_out14);
  or or_147 (or_147_out, decoder_18_out2, decoder_18_out3, decoder_18_out5, decoder_18_out6);
  or or_148 (or_148_out, decoder_18_out3, decoder_18_out6, decoder_18_out9, decoder_18_out12);
  or or_149 (or_149_out, decoder_18_out14, or_151_out);
  LED led_111 (.in(register_13_q[1]));
  LED led_112 (.in(register_13_q[1]));
  LED led_113 (.in(register_13_q[1]));
  LED led_114 (.in(register_13_q[2]));
  LED led_115 (.in(register_13_q[6]));
  LED led_116 (.in(register_13_q[6]));
  LED led_117 (.in(register_13_q[2]));
  LED led_118 (.in(register_13_q[7]));
  LED led_119 (.in(register_13_q[7]));
  LED led_120 (.in(register_13_q[2]));
  LED led_121 (.in(register_13_q[6]));
  LED led_122 (.in(register_13_q[7]));
  LED led_123 (.in(register_13_q[5]));
  LED led_124 (.in(register_13_q[3]));
  LED led_125 (.in(register_13_q[3]));
  LED led_126 (.in(register_13_q[5]));
  LED led_127 (.in(register_13_q[5]));
  LED led_128 (.in(register_13_q[3]));
  LED led_129 (.in(register_13_q[4]));
  LED led_130 (.in(register_13_q[4]));
  LED led_131 (.in(register_13_q[4]));
  Register register_13 (.D(register_15_q), .en(and_45_out[0]), .Q(register_13_q), .clk(d_ff_22_q));  // open: clr
  D_Flip_Flop d_ff_13 (
    .clk(clock_1_out), .D(and_38_out), .Q(d_ff_13_q), .Qn(d_ff_13_qn), .en(and_38_out), .reset(and_39_out));  // open: preset
  LED led_132 (.in(register_14_q[1]));
  LED led_133 (.in(register_14_q[6]));
  LED led_134 (.in(register_14_q[6]));
  LED led_135 (.in(register_14_q[7]));
  LED led_136 (.in(register_14_q[6]));
  LED led_137 (.in(register_14_q[5]));
  LED led_138 (.in(register_14_q[5]));
  LED led_139 (.in(register_14_q[5]));
  LED led_140 (.in(register_14_q[4]));
  LED led_141 (.in(register_14_q[1]));
  LED led_142 (.in(register_14_q[1]));
  LED led_143 (.in(register_14_q[2]));
  LED led_144 (.in(register_14_q[2]));
  LED led_145 (.in(register_14_q[7]));
  LED led_146 (.in(register_14_q[2]));
  LED led_147 (.in(register_14_q[7]));
  LED led_148 (.in(register_14_q[3]));
  LED led_149 (.in(register_14_q[3]));
  LED led_150 (.in(register_14_q[3]));
  LED led_151 (.in(register_14_q[4]));
  LED led_152 (.in(register_14_q[4]));
  Register register_14 (.D(register_16_q), .en(and_45_out[0]), .Q(register_14_q), .clk(d_ff_22_q));  // open: clr
  D_Flip_Flop d_ff_14 (
    .clk(clock_1_out), .D(and_38_out), .Q(d_ff_14_q), .Qn(d_ff_14_qn), .en(and_38_out),
    .reset(decoder_17_out2));  // open: preset
  Decoder #(.select(4), .disabled(0), .enable("false")) decoder_17 (
    .out0(decoder_17_out0), .out1(decoder_17_out1), .out2(decoder_17_out2), .out3(decoder_17_out3),
    .out4(decoder_17_out4), .out5(decoder_17_out5), .out6(decoder_17_out6), .out7(decoder_17_out7),
    .out8(decoder_17_out8), .out9(decoder_17_out9), .out10(decoder_17_out10), .out11(decoder_17_out11),
    .out12(decoder_17_out12), .out13(decoder_17_out13), .out14(decoder_17_out14), .out15(decoder_17_out15),
    .sel(demultiplexer_1_out1));
  Decoder #(.select(4), .disabled(0), .enable("false")) decoder_18 (
    .out0(decoder_18_out0), .out1(decoder_18_out1), .out2(decoder_18_out2), .out3(decoder_18_out3),
    .out4(decoder_18_out4), .out5(decoder_18_out5), .out6(decoder_18_out6), .out7(decoder_18_out7),
    .out8(decoder_18_out8), .out9(decoder_18_out9), .out10(decoder_18_out10), .out11(decoder_18_out11),
    .out12(decoder_18_out12), .out13(decoder_18_out13), .out14(decoder_18_out14), .out15(decoder_18_out15),
    .sel(demultiplexer_1_out0));
  LED led_153 (.in(register_15_q[1]));
  LED led_154 (.in(register_15_q[1]));
  LED led_155 (.in(register_15_q[1]));
  LED led_156 (.in(register_15_q[6]));
  LED led_157 (.in(register_15_q[6]));
  LED led_158 (.in(register_15_q[7]));
  LED led_159 (.in(register_15_q[7]));
  LED led_160 (.in(register_15_q[6]));
  LED led_161 (.in(register_15_q[7]));
  LED led_162 (.in(register_15_q[5]));
  LED led_163 (.in(register_15_q[5]));
  LED led_164 (.in(register_15_q[5]));
  LED led_165 (.in(register_15_q[4]));
  LED led_166 (.in(register_15_q[4]));
  LED led_167 (.in(register_15_q[4]));
  Register register_15 (.D(register_17_q), .en(and_45_out[0]), .Q(register_15_q), .clk(d_ff_22_q));  // open: clr
  LED led_168 (.in(register_15_q[2]));
  LED led_169 (.in(register_15_q[2]));
  LED led_170 (.in(register_15_q[2]));
  LED led_171 (.in(register_15_q[3]));
  LED led_172 (.in(register_15_q[3]));
  LED led_173 (.in(register_15_q[3]));
  D_Flip_Flop d_ff_15 (
    .clk(clock_1_out), .D(and_41_out), .Q(d_ff_15_q), .en(and_41_out), .reset(and_40_out));  // open: Qn, preset
  and and_40 (and_40_out, and_46_out, decoder_19_out5);
  Demultiplexer #(.width(4), .enable("false")) demultiplexer_1 (
    .out0(demultiplexer_1_out0), .out1(demultiplexer_1_out1), .in(demultiplexer_2_out1), .sel(or_154_out));
  LED led_174 (.in(register_16_q[1]));
  LED led_175 (.in(register_16_q[1]));
  LED led_176 (.in(register_16_q[1]));
  LED led_177 (.in(register_16_q[2]));
  LED led_178 (.in(register_16_q[6]));
  LED led_179 (.in(register_16_q[2]));
  LED led_180 (.in(register_16_q[6]));
  LED led_181 (.in(register_16_q[7]));
  LED led_182 (.in(register_16_q[6]));
  LED led_183 (.in(register_16_q[7]));
  LED led_184 (.in(register_16_q[7]));
  LED led_185 (.in(register_16_q[2]));
  LED led_186 (.in(register_16_q[5]));
  LED led_187 (.in(register_16_q[3]));
  LED led_188 (.in(register_16_q[5]));
  LED led_189 (.in(register_16_q[3]));
  LED led_190 (.in(register_16_q[5]));
  LED led_191 (.in(register_16_q[3]));
  LED led_192 (.in(register_16_q[4]));
  LED led_193 (.in(register_16_q[4]));
  LED led_194 (.in(register_16_q[4]));
  or or_150 (or_150_out, and_9_out, register_29_q);
  and and_41 (and_41_out, or_150_out, ~d_ff_15_q);  // AND_Gate
  or or_151 (or_151_out, decoder_19_out1, or_58_out);
  LED led_195 (.in(register_17_q[1]));
  LED led_196 (.in(register_17_q[1]));
  LED led_197 (.in(register_17_q[6]));
  LED led_198 (.in(register_17_q[6]));
  LED led_199 (.in(register_17_q[6]));
  LED led_200 (.in(register_17_q[7]));
  LED led_201 (.in(register_17_q[7]));
  LED led_202 (.in(register_17_q[5]));
  LED led_203 (.in(register_17_q[5]));
  LED led_204 (.in(register_17_q[5]));
  LED led_205 (.in(register_17_q[4]));
  LED led_206 (.in(register_17_q[4]));
  Register register_16 (.D(register_19_q), .en(and_45_out[0]), .Q(register_16_q), .clk(d_ff_22_q));  // open: clr
  Register register_17 (.D(register_20_q), .en(and_45_out[0]), .Q(register_17_q), .clk(d_ff_22_q));  // open: clr
  and and_42 (and_42_out, decoder_19_out1, clock_1_out);
  D_Flip_Flop d_ff_16 (
    .clk(clock_1_out), .D(and_41_out), .Q(d_ff_16_q), .en(and_41_out), .reset(decoder_18_out1));  // open: Qn, preset
  or or_152 (or_152_out, or_7_out, decoder_18_out15);
  LED led_207 (.in(register_17_q[1]));
  LED led_208 (.in(register_17_q[2]));
  LED led_209 (.in(register_17_q[2]));
  LED led_210 (.in(register_17_q[7]));
  LED led_211 (.in(register_17_q[2]));
  LED led_212 (.in(register_17_q[3]));
  LED led_213 (.in(register_17_q[3]));
  LED led_214 (.in(register_17_q[3]));
  LED led_215 (.in(register_17_q[4]));
  Multiplexer #(.width(16), .disabled(0), .enable("false")) multiplexer_158 (
    .in0(16'hff), .in1(16'hfdf), .out(multiplexer_158_out), .sel(in_10));
  D_Flip_Flop d_ff_17 (
    .clk(clock_1_out), .D(On_2_out), .Q(d_ff_17_q), .Qn(d_ff_17_qn), .en(undriven_43), .reset(undriven_44));  // open: preset
  Register #(.width(16)) register_18 (
    .D(adder_6_out), .en(decoder_20_out2), .Q(out_22), .clk(clock_1_out), .clr(and_43_out));
  D_Flip_Flop d_ff_18 (
    .clk(and_42_out), .D(d_ff_16_q), .Q(d_ff_18_q), .Qn(d_ff_18_qn), .en(d_ff_16_q), .reset(or_152_out));  // open: preset
  LED led_216 (.in(register_19_q[1]));
  LED led_217 (.in(register_19_q[1]));
  LED led_218 (.in(register_19_q[1]));
  LED led_219 (.in(register_19_q[6]));
  LED led_220 (.in(register_19_q[6]));
  LED led_221 (.in(register_19_q[7]));
  LED led_222 (.in(register_19_q[6]));
  LED led_223 (.in(register_19_q[7]));
  LED led_224 (.in(register_19_q[7]));
  LED led_225 (.in(register_19_q[5]));
  LED led_226 (.in(register_19_q[5]));
  LED led_227 (.in(register_19_q[5]));
  LED led_228 (.in(register_19_q[4]));
  LED led_229 (.in(register_19_q[4]));
  LED led_230 (.in(register_19_q[4]));
  Multiplexer #(.width(16), .enable("false")) multiplexer_159 (
    .in0({16{1'b0}}), .in1(out_22), .out({multiplexer_159_out_2, multiplexer_159_out}), .sel(or_156_out));
  or or_153 (or_153_out, d_ff_13_q, d_ff_18_q);
  or or_154 (or_154_out, d_ff_18_qn, d_ff_13_q);
  LED led_231 (.in(register_20_q[1]));
  LED led_232 (.in(register_20_q[6]));
  LED led_233 (.in(register_19_q[2]));
  LED led_234 (.in(register_19_q[2]));
  LED led_235 (.in(register_20_q[6]));
  LED led_236 (.in(register_19_q[2]));
  LED led_237 (.in(register_20_q[6]));
  LED led_238 (.in(register_20_q[7]));
  LED led_239 (.in(register_20_q[5]));
  LED led_240 (.in(register_19_q[3]));
  LED led_241 (.in(register_20_q[5]));
  LED led_242 (.in(register_19_q[3]));
  LED led_243 (.in(register_19_q[3]));
  LED led_244 (.in(register_20_q[5]));
  LED led_245 (.in(register_20_q[4]));
  Register register_19 (.D(register_22_q), .en(and_45_out[0]), .Q(register_19_q), .clk(d_ff_22_q));  // open: clr
  D_Flip_Flop d_ff_19 (
    .clk(clock_1_out), .D(d_ff_17_q), .Q(d_ff_19_q), .Qn(d_ff_19_qn), .en(d_ff_17_q), .reset(and_43_out));  // open: preset
  Decoder #(.select(4), .disabled(0), .enable("false")) decoder_19 (
    .out0(decoder_19_out0), .out1(decoder_19_out1), .out2(decoder_19_out2), .out3(decoder_19_out3),
    .out4(decoder_19_out4), .out5(decoder_19_out5), .out6(decoder_19_out6), .out7(decoder_19_out7),
    .out8(decoder_19_out8), .out9(decoder_19_out9), .out10(decoder_19_out10), .out11(decoder_19_out11),
    .out12(decoder_19_out12), .out13(decoder_19_out13), .out14(decoder_19_out14), .out15(decoder_19_out15),
    .sel(demultiplexer_2_out0));
  or or_155 (or_155_out, decoder_19_out4, decoder_19_out5);
  LED led_246 (.in(register_20_q[1]));
  LED led_247 (.in(register_20_q[1]));
  LED led_248 (.in(register_20_q[2]));
  LED led_249 (.in(register_20_q[2]));
  LED led_250 (.in(register_20_q[7]));
  LED led_251 (.in(register_20_q[7]));
  LED led_252 (.in(register_20_q[2]));
  LED led_253 (.in(register_20_q[3]));
  LED led_254 (.in(register_20_q[3]));
  LED led_255 (.in(register_20_q[3]));
  LED led_256 (.in(register_20_q[4]));
  LED led_257 (.in(register_20_q[4]));
  Register register_20 (.D(register_23_q), .en(and_45_out[0]), .Q(register_20_q), .clk(d_ff_22_q));  // open: clr
  Register #(.width(2)) register_21 (
    .D(adder_7_out), .en(d_ff_19_q), .Q(register_21_q), .clk(clock_1_out), .clr(and_43_out));
  Decoder #(.select(2), .disabled(0)) decoder_20 (
    .out0(decoder_20_out0), .out1(decoder_20_out1), .out2(decoder_20_out2), .out3(decoder_20_out3),
    .sel(register_21_q), .en(d_ff_19_q));
  or or_156 (or_156_out, decoder_20_out1, decoder_20_out2);
  and and_43 (and_43_out, decoder_20_out2, nand_6_out);
  Multiplexer #(.width(16), .enable("false")) multiplexer_160 (
    .in0({16{1'b0}}), .in1(out_22), .out(multiplexer_160_out), .sel(decoder_20_out2));
  Demultiplexer #(.width(4), .enable("false")) demultiplexer_2 (
    .out0(demultiplexer_2_out0), .out1(demultiplexer_2_out1), .in(register_24_q), .sel(or_153_out));
  LED led_258 (.in(register_22_q[1]));
  LED led_259 (.in(register_22_q[1]));
  LED led_260 (.in(register_22_q[6]));
  LED led_261 (.in(register_22_q[6]));
  LED led_262 (.in(register_22_q[6]));
  LED led_263 (.in(register_22_q[7]));
  LED led_264 (.in(register_22_q[7]));
  LED led_265 (.in(register_22_q[5]));
  LED led_266 (.in(register_22_q[5]));
  LED led_267 (.in(register_22_q[5]));
  LED led_268 (.in(register_22_q[4]));
  LED led_269 (.in(register_22_q[4]));
  Multiplexer #(.width(2), .disabled(0), .enable("false")) multiplexer_161 (
    .in0(2'b00), .in1(2'b10), .out(multiplexer_161_out), .sel(decoder_20_out2));
  nand nand_6 (nand_6_out, or_158_out, or_158_out);
  Adder #(.width(16)) adder_6 (
    .a({16{1'b0}}), .b(multiplexer_160_out), .out(adder_6_out), .cin(decoder_20_out2));  // open: cout
  D_Flip_Flop d_ff_20 (.clk(clock_1_out), .D(or_7_out), .Q(d_ff_20_q));  // open: Qn, preset, en, reset
  or or_157 (or_157_out, Off_out, ffff_out);
  Multiplexer #(.width(4), .enable("false")) multiplexer_162 (
    .in0(4'b0000), .in1(4'b0011), .out(multiplexer_162_out), .sel(decoder_19_out1));
  Multiplexer #(.width(4), .enable("false")) multiplexer_163 (
    .in0(multiplexer_162_out), .in1(4'b0010), .out(multiplexer_163_out), .sel(and_44_out));
  and and_44 (and_44_out, multiplexer_173_out[12], multiplexer_173_out[13], multiplexer_173_out[14], multiplexer_173_out[15], decoder_19_out1);
  LED led_270 (.in(register_22_q[1]));
  LED led_271 (.in(register_22_q[2]));
  LED led_272 (.in(register_22_q[2]));
  LED led_273 (.in(register_22_q[7]));
  LED led_274 (.in(register_22_q[2]));
  LED led_275 (.in(register_22_q[3]));
  LED led_276 (.in(register_22_q[3]));
  LED led_277 (.in(register_22_q[3]));
  LED led_278 (.in(register_22_q[4]));
  Register register_22 (.D(register_25_q), .en(and_45_out[0]), .Q(register_22_q), .clk(d_ff_22_q));  // open: clr
  Adder #(.width(2)) adder_7 (.a(multiplexer_161_out), .b(register_21_q), .out(adder_7_out), .cin(1'b1));  // open: cout
  or or_158 (or_158_out, xor_2_out[0], xor_2_out[1], xor_2_out[2], xor_2_out[3], xor_2_out[4], xor_2_out[5], xor_2_out[6], xor_2_out[7], xor_2_out[8], xor_2_out[9], xor_2_out[10], xor_2_out[11], xor_2_out[12], xor_2_out[13], xor_2_out[14], xor_2_out[15]);
  D_Flip_Flop d_ff_21 (
    .clk(clock_1_out), .D(d_ff_20_q), .Q(d_ff_21_q), .en(d_ff_20_q), .reset(or_157_out));  // open: Qn, preset
  Multiplexer #(.width(4), .enable("false")) multiplexer_164 (
    .in0(multiplexer_163_out), .in1(4'b1011), .out(multiplexer_164_out), .sel(decoder_19_out5));
  LED led_279 (.in(register_23_q[1]));
  LED led_280 (.in(register_23_q[1]));
  LED led_281 (.in(register_23_q[1]));
  LED led_282 (.in(register_23_q[2]));
  LED led_283 (.in(register_23_q[6]));
  LED led_284 (.in(register_23_q[6]));
  LED led_285 (.in(register_23_q[2]));
  LED led_286 (.in(register_23_q[6]));
  LED led_287 (.in(register_23_q[2]));
  LED led_288 (.in(register_23_q[7]));
  LED led_289 (.in(register_23_q[7]));
  LED led_290 (.in(register_23_q[7]));
  LED led_291 (.in(register_23_q[5]));
  LED led_292 (.in(register_23_q[3]));
  LED led_293 (.in(register_23_q[3]));
  LED led_294 (.in(register_23_q[5]));
  LED led_295 (.in(register_23_q[3]));
  LED led_296 (.in(register_23_q[5]));
  LED led_297 (.in(register_23_q[4]));
  LED led_298 (.in(register_23_q[4]));
  LED led_299 (.in(register_23_q[4]));
  Register register_23 (.D(register_26_q), .en(and_45_out[0]), .Q(register_23_q), .clk(d_ff_22_q));  // open: clr
  and and_45 (and_45_out[0], adder_9_out_2[3], adder_9_out_2[2], adder_9_out_2[1], adder_9_out_2[0], adder_9_out[7], adder_9_out[6], adder_9_out_3[5], adder_9_out_3[4], adder_9_out_3[3], adder_9_out_3[2], adder_9_out_3[1], ~adder_9_out_3[0]);  // AND_Gate
  and and_46 (and_46_out, ~adder_9_out_3[0], adder_9_out_3[1], ~adder_9_out_3[2], ~adder_9_out_3[3], ~adder_9_out_3[4], ~adder_9_out_3[5], ~adder_9_out[6], ~adder_9_out[7], adder_9_out_2[0], adder_9_out_2[1], adder_9_out_2[2], adder_9_out_2[3]);  // AND_Gate
  Multiplexer #(.width(4), .enable("false")) multiplexer_165 (
    .in0(multiplexer_164_out), .in1(4'b1110), .out(multiplexer_165_out), .sel(decoder_19_out2));
  Adder #(.width(4)) adder_8 (.a(multiplexer_165_out), .b(register_24_q), .out(adder_8_out), .cin(1'b1));  // open: cout
  LED led_300 (.in(register_25_q[1]));
  LED led_301 (.in(register_25_q[6]));
  LED led_302 (.in(register_25_q[6]));
  LED led_303 (.in(register_25_q[7]));
  LED led_304 (.in(register_25_q[6]));
  LED led_305 (.in(register_25_q[5]));
  LED led_306 (.in(register_25_q[5]));
  LED led_307 (.in(register_25_q[5]));
  LED led_308 (.in(register_25_q[4]));
  assign xor_2_out = multiplexer_158_out ^ {multiplexer_159_out_2, multiplexer_159_out};  // XOR_Gate xor_2, 16 bits wide
  RAM #(.addrWidth(16), .bus("separate")) ram_1 (
    .addr({multiplexer_159_out_2, multiplexer_159_out}), .data(ram_1_data), .str(1'b0), .clk(clock_1_out),
    .ld(or_156_out));  // open: din, sel, clr
  Register #(.width(4)) register_24 (
    .D(adder_8_out), .en(d_ff_21_q), .Q(register_24_q), .clk(clock_1_out), .clr(or_157_out));
  LED led_309 (.in(register_25_q[1]));
  LED led_310 (.in(register_25_q[1]));
  LED led_311 (.in(register_25_q[2]));
  LED led_312 (.in(register_25_q[2]));
  LED led_313 (.in(register_25_q[2]));
  LED led_314 (.in(register_25_q[7]));
  LED led_315 (.in(register_25_q[7]));
  LED led_316 (.in(register_25_q[3]));
  LED led_317 (.in(register_25_q[3]));
  LED led_318 (.in(register_25_q[3]));
  LED led_319 (.in(register_25_q[4]));
  LED led_320 (.in(register_25_q[4]));
  Register register_25 (
    .D({or_164_out, and_45_out[0]}), .en(and_45_out[0]), .Q(register_25_q), .clk(d_ff_22_q));  // open: clr
  Multiplexer #(.width(8), .enable("false")) multiplexer_166 (
    .in0({8{1'b0}}), .in1(ram_1_data), .out(multiplexer_166_out), .sel(or_156_out));
  LED led_321 (.in(register_26_q[1]));
  LED led_322 (.in(register_26_q[1]));
  LED led_323 (.in(register_26_q[1]));
  LED led_324 (.in(register_26_q[6]));
  LED led_325 (.in(register_26_q[6]));
  LED led_326 (.in(register_26_q[6]));
  LED led_327 (.in(register_26_q[7]));
  LED led_328 (.in(register_26_q[7]));
  LED led_329 (.in(register_26_q[7]));
  LED led_330 (.in(register_26_q[5]));
  LED led_331 (.in(register_26_q[5]));
  LED led_332 (.in(register_26_q[5]));
  LED led_333 (.in(register_26_q[4]));
  LED led_334 (.in(register_26_q[4]));
  LED led_335 (.in(register_26_q[4]));
  Register register_26 (.D(and_45_out), .en(and_45_out[0]), .Q(register_26_q), .clk(d_ff_22_q));  // open: clr
  LED led_336 (.in(register_26_q[2]));
  LED led_337 (.in(register_26_q[2]));
  LED led_338 (.in(register_26_q[2]));
  LED led_339 (.in(register_26_q[3]));
  LED led_340 (.in(register_26_q[3]));
  LED led_341 (.in(register_26_q[3]));
  D_Flip_Flop d_ff_22 (
    .clk(clock_1_out), .D(or_5_out), .Q(d_ff_22_q), .en(or_5_out), .reset(or_6_out));  // open: Qn, preset
  assign or_159_out = multiplexer_59_out | multiplexer_157_out;  // OR_Gate or_159, 8 bits wide
  assign Read_Ram = multiplexer_194_out | or_163_out;  // OR_Gate or_160, 8 bits wide
  assign or_161_out = Data_In | or_162_out;  // OR_Gate or_161, 8 bits wide
  assign or_162_out = multiplexer_166_out | or_159_out;  // OR_Gate or_162, 8 bits wide
  assign or_163_out = multiplexer_131_out | multiplexer_97_out[7:0];  // OR_Gate or_163, 8 bits wide
  or or_164 (or_164_out[1], decoder_21_out0, decoder_21_out2, decoder_21_out3, decoder_21_out5, decoder_21_out6, decoder_21_out7, decoder_21_out8, decoder_21_out9, decoder_21_out10, decoder_21_out12, decoder_21_out14, decoder_21_out15);
  or or_165 (or_164_out[3], decoder_21_out0, decoder_21_out1, decoder_21_out3, decoder_21_out4, decoder_21_out5, decoder_21_out6, decoder_21_out7, decoder_21_out8, decoder_21_out9, decoder_21_out10, decoder_21_out11, decoder_21_out13);
  or or_166 (or_164_out[5], decoder_21_out0, decoder_21_out2, decoder_21_out6, decoder_21_out8, decoder_21_out10, decoder_21_out11, decoder_21_out12, decoder_21_out13, decoder_21_out14, decoder_21_out15);
  or or_167 (or_164_out[7], decoder_21_out2, decoder_21_out3, decoder_21_out4, decoder_21_out5, decoder_21_out6, decoder_21_out8, decoder_21_out9, decoder_21_out10, decoder_21_out11, decoder_21_out13, decoder_21_out14, decoder_21_out15);
  and and_47 (and_47_out, button_1_out, d_ff_20_q);
  Decoder #(.select(4), .disabled(0)) decoder_21 (
    .out0(decoder_21_out0), .out1(decoder_21_out1), .out2(decoder_21_out2), .out3(decoder_21_out3),
    .out4(decoder_21_out4), .out5(decoder_21_out5), .out6(decoder_21_out6), .out7(decoder_21_out7),
    .out8(decoder_21_out8), .out9(decoder_21_out9), .out10(decoder_21_out10), .out11(decoder_21_out11),
    .out12(decoder_21_out12), .out13(decoder_21_out13), .out14(decoder_21_out14), .out15(decoder_21_out15),
    .sel(or_159_out[7:4]), .en(and_45_out[0]));
  Multiplexer #(.width(12), .enable("false")) multiplexer_167 (
    .in0({4'b0000, multiplexer_75_out}), .in1({12{1'b1}}), .out(multiplexer_167_out),
    .sel(multiplexer_168_out));
  Multiplexer #(.disabled(0), .enable("false")) multiplexer_168 (
    .in0(and_5_out), .in1(1'b0), .out(multiplexer_168_out), .sel(register_29_q));
  Multiplexer #(.disabled(0), .enable("false")) multiplexer_169 (
    .in0(f1_out), .in1(1'b0), .out(multiplexer_169_out), .sel(register_29_q));
  Adder #(.width(12)) adder_9 (
    .a(or_138_out), .b(multiplexer_167_out), .out({adder_9_out_2, adder_9_out, adder_9_out_3}),
    .cin(multiplexer_169_out));  // open: cout
  or or_168 (or_164_out[2], decoder_21_out0, decoder_21_out1, decoder_21_out2, decoder_21_out3, decoder_21_out4, decoder_21_out7, decoder_21_out8, decoder_21_out9, decoder_21_out10, decoder_21_out13);
  or or_169 (or_164_out[4], decoder_21_out0, decoder_21_out2, decoder_21_out3, decoder_21_out5, decoder_21_out6, decoder_21_out8, decoder_21_out9, decoder_21_out11, decoder_21_out12, decoder_21_out13, decoder_21_out14);
  or or_170 (or_164_out[6], decoder_21_out0, decoder_21_out4, decoder_21_out5, decoder_21_out6, decoder_21_out8, decoder_21_out9, decoder_21_out10, decoder_21_out11, decoder_21_out12, decoder_21_out14, decoder_21_out15);
  or or_171 (and_45_out[1], decoder_22_out0, decoder_22_out2, decoder_22_out3, decoder_22_out5, decoder_22_out6, decoder_22_out7, decoder_22_out8, decoder_22_out9, decoder_22_out10, decoder_22_out12, decoder_22_out14, decoder_22_out15);
  or or_172 (and_45_out[3], decoder_22_out0, decoder_22_out1, decoder_22_out3, decoder_22_out4, decoder_22_out5, decoder_22_out6, decoder_22_out7, decoder_22_out8, decoder_22_out9, decoder_22_out10, decoder_22_out11, decoder_22_out13);
  or or_173 (and_45_out[5], decoder_22_out0, decoder_22_out2, decoder_22_out6, decoder_22_out8, decoder_22_out10, decoder_22_out11, decoder_22_out12, decoder_22_out13, decoder_22_out14, decoder_22_out15);
  or or_174 (and_45_out[7], decoder_22_out2, decoder_22_out3, decoder_22_out4, decoder_22_out5, decoder_22_out6, decoder_22_out8, decoder_22_out9, decoder_22_out10, decoder_22_out11, decoder_22_out13, decoder_22_out14, decoder_22_out15);
  Decoder #(.select(4), .disabled(0)) decoder_22 (
    .out0(decoder_22_out0), .out1(decoder_22_out1), .out2(decoder_22_out2), .out3(decoder_22_out3),
    .out4(decoder_22_out4), .out5(decoder_22_out5), .out6(decoder_22_out6), .out7(decoder_22_out7),
    .out8(decoder_22_out8), .out9(decoder_22_out9), .out10(decoder_22_out10), .out11(decoder_22_out11),
    .out12(decoder_22_out12), .out13(decoder_22_out13), .out14(decoder_22_out14), .out15(decoder_22_out15),
    .sel(or_159_out[3:0]), .en(and_45_out[0]));
  or or_175 (and_45_out[2], decoder_22_out0, decoder_22_out1, decoder_22_out2, decoder_22_out3, decoder_22_out4, decoder_22_out7, decoder_22_out8, decoder_22_out9, decoder_22_out10, decoder_22_out13);
  or or_176 (and_45_out[4], decoder_22_out0, decoder_22_out2, decoder_22_out3, decoder_22_out5, decoder_22_out6, decoder_22_out8, decoder_22_out9, decoder_22_out11, decoder_22_out12, decoder_22_out13, decoder_22_out14);
  or or_177 (and_45_out[6], decoder_22_out0, decoder_22_out4, decoder_22_out5, decoder_22_out6, decoder_22_out8, decoder_22_out9, decoder_22_out10, decoder_22_out11, decoder_22_out12, decoder_22_out14, decoder_22_out15);
  Register register_27 (.D(or_161_out), .en(and_52_out), .Q(register_27_q), .clk(clock_1_out));  // open: clr
  or or_178 (or_178_out, multiplexer_178_out, or_148_out, decoder_20_out1);
  or or_179 (or_179_out, or_5_out, or_6_out, decoder_19_out1);
  Multiplexer #(.disabled(0), .enable("false")) multiplexer_170 (
    .in0(or_178_out), .in1(1'b0), .out(multiplexer_170_out), .sel(and_53_out));
  Multiplexer #(.width(6), .disabled(0), .enable("false")) multiplexer_171 (
    .in0({adder_9_out_2, adder_9_out}), .in1(register_27_q[5:0]), .out(multiplexer_171_out), .sel(and_53_out));
  and and_48 (and_48_out, ~adder_9_out_3[4], adder_9_out_3[5], adder_9_out[6], adder_9_out[7], adder_9_out_2[0], adder_9_out_2[1], adder_9_out_2[2], adder_9_out_2[3]);  // AND_Gate
  and and_49 (and_49_out, adder_9_out_3[0], ~adder_9_out_3[1], ~adder_9_out_3[2], adder_9_out_3[3]);  // AND_Gate
  and and_50 (and_50_out, ~adder_9_out_3[0], adder_9_out_3[1], ~adder_9_out_3[2], adder_9_out_3[3]);  // AND_Gate
  and and_51 (and_51_out, adder_9_out_3[0], adder_9_out_3[1], ~adder_9_out_3[2], adder_9_out_3[3]);  // AND_Gate
  and and_52 (and_52_out, and_48_out, and_49_out, or_5_out);
  and and_53 (and_53_out, and_48_out, and_50_out, or_5_out);
  and and_54 (and_54_out, and_48_out, and_51_out, or_5_out);
  RAM #(.addrWidth(6), .bus("separate")) ram_2 (
    .addr(multiplexer_171_out), .din(or_161_out), .data(ram_2_data), .str(and_53_out), .clk(clock_1_out),
    .ld(or_179_out), .clr(and_54_out));  // open: sel
  Register register_28 (
    .D({2'b00, multiplexer_171_out}), .en(or_179_out), .Q(register_28_q), .clk(clock_1_out));  // open: clr
  Multiplexer #(.width(8), .enable("false")) multiplexer_172 (
    .in0({8{1'b0}}), .in1(multiplexer_175_out), .out(multiplexer_172_out), .sel(or_179_out));
  Multiplexer #(.width(16), .disabled(0), .enable("false")) multiplexer_173 (
    .in0(multiplexer_195_out), .in1({16{1'b0}}), .out(multiplexer_173_out), .sel(or_181_out));
  ROM #(.addrWidth(6)) rom_7 (.addr(multiplexer_171_out), .data(rom_7_data));  // open: sel
  Multiplexer #(.width(12), .disabled(0), .enable("false")) multiplexer_174 (
    .in0({12{1'b0}}), .in1({multiplexer_172_out[5:0], adder_9_out_3}), .out(multiplexer_174_out),
    .sel(multiplexer_172_out[7]));
  Counter #(.width(32), .max('hffffffff)) counter_1 (
    .count(register_29_q), .clk(register_29_q));  // open: load, D, Q, carry, clr
  and and_55 (and_55_out, ~multiplexer_172_out[7], or_179_out);  // AND_Gate
  Register #(.width(1)) register_29 (
    .D(and_55_out), .en(clock_1_out), .Q(register_29_q), .clk(clock_1_out));  // open: clr
  Multiplexer #(.width(8), .enable("false")) multiplexer_175 (
    .in0(rom_7_data), .in1(ram_2_data), .out(multiplexer_175_out), .sel(MMU_On));
  assign or_180_out = multiplexer_159_out | multiplexer_150_out | multiplexer_174_out;  // OR_Gate or_180, 12 bits wide
  or or_181 (or_181_out, register_29_q, and_55_out);
  Multiplexer #(.disabled(0), .enable("false")) multiplexer_176 (
    .in0(decoder_19_out1), .in1(1'b0), .out(multiplexer_176_out), .sel(or_181_out));
  and and_56 (and_56_out, and_55_out, or_5_out);
  Multiplexer #(.disabled(0), .enable("false")) multiplexer_177 (
    .in0(or_6_out), .in1(1'b0), .out(multiplexer_177_out), .sel(or_181_out));
  Multiplexer #(.disabled(0), .enable("false")) multiplexer_178 (
    .in0(or_5_out), .in1(1'b0), .out(multiplexer_178_out), .sel(and_56_out));
  and and_57 (and_57_out, ~or_180_out[4], or_180_out[5], or_180_out[6], or_180_out[7], or_180_out[8], or_180_out[9], or_180_out[10], or_180_out[11]);  // AND_Gate
  and and_58 (and_58_out, ~or_180_out[0], ~or_180_out[1], ~or_180_out[2], ~or_180_out[3]);  // AND_Gate
  and and_59 (and_59_out, or_180_out[0], ~or_180_out[1], ~or_180_out[2], ~or_180_out[3]);  // AND_Gate
  and and_60 (and_60_out, ~or_180_out[0], or_180_out[1], ~or_180_out[2], ~or_180_out[3]);  // AND_Gate
  and and_61 (and_61_out, or_180_out[0], or_180_out[1], ~or_180_out[2], ~or_180_out[3]);  // AND_Gate
  assign or_182_out = or_180_out | multiplexer_184_out;  // OR_Gate or_182, 12 bits wide
  or or_183 (or_183_out, multiplexer_170_out, and_73_out);
  and and_62 (and_62_out, and_57_out, and_58_out, multiplexer_170_out);
  and and_63 (and_63_out, and_57_out, and_59_out, multiplexer_170_out);
  and and_64 (and_64_out, and_57_out, and_60_out, multiplexer_170_out);
  and and_65 (and_65_out, and_57_out, and_61_out, multiplexer_170_out);
  or or_184 (or_184_out, and_63_out, and_47_out);
  Register register_30 (.D(or_161_out), .en(and_62_out), .Q(register_30_q), .clk(clock_1_out));  // open: clr
  Register register_31 (.D(or_161_out), .en(and_63_out), .Q(register_31_q), .clk(clock_1_out));  // open: clr
  Register #(.width(1)) register_32 (
    .D(or_184_out), .en(or_184_out), .Q(register_32_q), .clk(clock_1_out), .clr(and_77_out));
  Register register_33 (.D(or_161_out), .en(and_64_out), .Q(register_33_q), .clk(clock_1_out));  // open: clr
  Register register_34 (.D(or_161_out), .en(and_65_out), .Q(register_34_q), .clk(clock_1_out));  // open: clr
  Register #(.width(1)) register_35 (
    .D(and_65_out), .en(and_65_out), .Q(register_35_q), .clk(clock_1_out), .clr(and_77_out));
  Decoder #(.select(2), .enable("false")) decoder_23 (
    .out0(decoder_23_out0), .out1(decoder_23_out1), .out2(decoder_23_out2), .out3(decoder_23_out3),
    .sel(or_182_out[1:0]));
  or or_185 (or_185_out, multiplexer_176_out, and_72_out, multiplexer_177_out);
  or or_186 (or_186_out, and_73_out, and_72_out);
  not not_2 (not_2_out, or_182_out[1]);
  Multiplexer #(.width(8), .enable("false")) multiplexer_179 (
    .in0(or_161_out), .in1(multiplexer_197_out_4), .out(multiplexer_179_out), .sel(and_73_out));
  Multiplexer #(.width(12), .disabled(0), .enable("false")) multiplexer_180 (
    .in0({12{1'b0}}), .in1({register_30_q, multiplexer_189_out}), .out(multiplexer_180_out), .sel(and_66_out));
  and and_66 (and_66_out, register_32_q, or_193_out);
  or or_187 (or_187_out, decoder_23_out0, or_186_out, and_68_out);
  and and_67 (and_67_out, or_182_out[1], multiplexer_176_out);
  and and_68 (and_68_out, not_2_out, multiplexer_176_out);
  Multiplexer #(.width(12), .disabled(0), .enable("false")) multiplexer_181 (
    .in0(multiplexer_180_out), .in1({register_34_q, multiplexer_189_out}), .out(multiplexer_181_out),
    .sel(and_69_out));
  and and_69 (and_69_out, register_35_q, or_193_out);
  RAM #(.addrWidth(10), .bus("separate")) ram_3 (
    .addr(or_182_out[11:2]), .din(multiplexer_179_out), .data(ram_3_data), .str(or_183_out),
    .sel(or_187_out), .clk(clock_1_out), .ld(or_185_out));  // open: clr
  and and_70 (and_70_out, or_187_out, or_185_out);
  Multiplexer #(.width(8), .enable("false")) multiplexer_182 (
    .in0({8{1'b0}}), .in1(ram_3_data), .out(multiplexer_182_out), .sel(and_70_out));
  Multiplexer #(.width(12), .disabled(0), .enable("false")) multiplexer_183 (
    .in0({12{1'b0}}), .in1({register_31_q[5:0], multiplexer_189_out, 2'b00}), .out(multiplexer_183_out),
    .sel(and_66_out));
  Multiplexer #(.width(12), .disabled(0), .enable("false")) multiplexer_184 (
    .in0(multiplexer_183_out), .in1({register_33_q[5:0], multiplexer_189_out, 2'b00}),
    .out(multiplexer_184_out), .sel(and_69_out));
  or or_188 (or_188_out, multiplexer_176_out, and_72_out, multiplexer_177_out);
  and and_71 (and_71_out, register_32_q, or_193_out);
  or or_189 (or_189_out, decoder_23_out1, or_186_out, and_68_out);
  Multiplexer #(.width(8), .enable("false")) multiplexer_185 (
    .in0(or_161_out), .in1(multiplexer_197_out_3), .out(multiplexer_185_out), .sel(and_73_out));
  and and_72 (and_72_out, register_35_q, or_193_out);
  and and_73 (and_73_out, register_32_q, decoder_24_out3);
  RAM #(.addrWidth(10), .bus("separate")) ram_4 (
    .addr(or_182_out[11:2]), .din(multiplexer_185_out), .data(ram_4_data), .str(or_183_out),
    .sel(or_189_out), .clk(clock_1_out), .ld(or_188_out));  // open: clr
  and and_74 (and_74_out, or_189_out, or_188_out);
  and and_75 (and_75_out, register_35_q, decoder_24_out3);
  Multiplexer #(.width(8), .enable("false")) multiplexer_186 (
    .in0(multiplexer_182_out), .in1(ram_4_data), .out(multiplexer_186_out), .sel(and_74_out));
  or or_190 (or_190_out, register_32_q, register_35_q);
  or or_191 (or_191_out, multiplexer_176_out, and_72_out, multiplexer_177_out);
  Counter #(.width(32), .max('hffffffff)) counter_2 (
    .count(or_190_out), .clk(clock_1_out));  // open: load, D, Q, carry, clr
  Counter #(.width(32), .max('hffffffff)) counter_3 (
    .count(or_190_out), .clk(or_190_out));  // open: load, D, Q, carry, clr
  or or_192 (or_192_out, decoder_23_out2, or_186_out, and_67_out);
  Multiplexer #(.width(8), .enable("false")) multiplexer_187 (
    .in0(or_161_out), .in1(multiplexer_197_out_2), .out(multiplexer_187_out), .sel(and_73_out));
  Register #(.width(4)) register_36 (
    .D(adder_10_out), .en(decoder_24_out4), .Q(register_36_q), .clk(clock_1_out), .clr(and_77_out));
  RAM #(.addrWidth(10), .bus("separate")) ram_5 (
    .addr(or_182_out[11:2]), .din(multiplexer_187_out), .data(ram_5_data), .str(or_183_out),
    .sel(or_192_out), .clk(clock_1_out), .ld(or_191_out));  // open: clr
  and and_76 (and_76_out, or_192_out, or_191_out);
  Multiplexer #(.width(16), .enable("false")) multiplexer_188 (
    .in0({16{1'b0}}), .in1({ram_3_data, ram_4_data}), .out(multiplexer_188_out), .sel(and_68_out));
  Multiplexer #(.width(4), .enable("false")) multiplexer_189 (
    .in0(4'b0000), .in1(register_36_q), .out(multiplexer_189_out), .sel(or_193_out));
  Multiplexer #(.width(8), .enable("false")) multiplexer_190 (
    .in0(multiplexer_186_out), .in1(ram_5_data), .out(multiplexer_190_out), .sel(and_76_out));
  Register #(.width(3)) register_37 (
    .D(adder_11_out), .en(or_190_out), .Q(register_37_q), .clk(clock_1_out), .clr(and_77_out));
  Decoder #(.select(3), .disabled(0)) decoder_24 (
    .out3(decoder_24_out3), .out4(decoder_24_out4), .out5(decoder_24_out5), .out6(decoder_24_out6),
    .sel(register_37_q), .en(or_190_out));  // open: out0, out1, out2, out7
  or or_193 (or_193_out, decoder_24_out3, decoder_24_out4);
  or or_194 (or_194_out, decoder_24_out4, decoder_24_out4);
  and and_77 (and_77_out, decoder_24_out4, and_78_out);
  or or_195 (or_195_out, multiplexer_176_out, and_72_out, multiplexer_177_out);
  Multiplexer #(.width(4), .enable("false")) multiplexer_191 (
    .in0(4'b0000), .in1(register_36_q), .out(multiplexer_191_out), .sel(or_194_out));
  or or_196 (or_196_out, decoder_23_out3, or_186_out, and_67_out);
  Multiplexer #(.width(8), .enable("false")) multiplexer_192 (
    .in0(or_161_out), .in1(multiplexer_197_out), .out(multiplexer_192_out), .sel(and_73_out));
  Multiplexer #(.width(3), .disabled(0), .enable("false")) multiplexer_193 (
    .in0(3'b000), .in1(3'b110), .out(multiplexer_193_out), .sel(decoder_24_out4));
  Adder #(.width(4)) adder_10 (
    .a(4'b0000), .b(multiplexer_191_out), .out(adder_10_out), .cin(or_194_out));  // open: cout
  Adder #(.width(3)) adder_11 (
    .a(multiplexer_193_out), .b(register_37_q), .out(adder_11_out), .cin(1'b1));  // open: cout
  and and_78 (and_78_out, multiplexer_189_out[0], multiplexer_189_out[1], multiplexer_189_out[2], multiplexer_189_out[3]);
  Multiplexer #(.width(8), .enable("false")) multiplexer_194 (
    .in0(multiplexer_190_out), .in1(ram_6_data), .out(multiplexer_194_out), .sel(and_79_out));
  RAM #(.addrWidth(10), .bus("separate")) ram_6 (
    .addr(or_182_out[11:2]), .din(multiplexer_192_out), .data(ram_6_data), .str(or_183_out),
    .sel(or_196_out), .clk(clock_1_out), .ld(or_195_out));  // open: clr
  and and_79 (and_79_out, or_196_out, or_195_out);
  Multiplexer #(.width(16), .enable("false")) multiplexer_195 (
    .in0(multiplexer_188_out), .in1({ram_5_data, ram_6_data}), .out(multiplexer_195_out), .sel(and_67_out));
  RAM #(.addrWidth(12), .bus("separate")) ram_7 (
    .addr(or_182_out), .din(multiplexer_179_out), .data(ram_7_data), .str(or_183_out), .clk(clock_1_out),
    .ld(multiplexer_177_out));  // open: sel, clr
  Multiplexer #(.width(8), .enable("false")) multiplexer_196 (
    .in0({8{1'b0}}), .in1(ram_7_data), .out(multiplexer_196_out), .sel(multiplexer_177_out));
  RAM #(.addrWidth(12), .dataWidth(32), .bus("separate")) ram_8 (
    .addr(multiplexer_181_out), .din({ram_3_data, ram_4_data, ram_5_data, ram_6_data}), .data(ram_8_data),
    .str(and_75_out), .clk(clock_1_out), .ld(and_71_out));  // open: sel, clr
  Multiplexer #(.width(32), .enable("false")) multiplexer_197 (
    .in0({32{1'b0}}), .in1(ram_8_data),
    .out({multiplexer_197_out_4, multiplexer_197_out_3, multiplexer_197_out_2, multiplexer_197_out}),
    .sel(and_71_out));

  // Notes on the sheet:
  //   4011B Quad 2 Inputs NAND
  //   4013B Dual D-tipe flip-flop
  //   Clock
  //   Loader 256
  //   Loader 4K
  //   Boot From HD
  //   0x00
  //   00x0
  //   Keyboard IN
  //   WReg 0x00
  //   WReg 00x0
  //   R00x0 alu1
  //   R0x00 alu1
  //   R000x alu2
  //   R0x00 to Ram
  //   R00x0 to Ram
  //   R000x adr alu
  //   R00x0 adr alu
  //   Enable IO Int
  //   Disable
  //   ALU
  //   contents of rom_1 (hex, n*v repeats v):
  //   35*0 14 0 19 32 4*0 8 0 8 0 1 3e 0 21 22 c 71 3e 40 36 30 0 0 8 0 0 30 3e 7f 7f 3e 7f 7f 7f 3e 7f 0
  //   2 6*7f 3e 7f 31 40 7e 70 7c 63 60 43 0 40 0 0 1 0 2 7f 6 6 e 3f 8 7f 0 2 7f 0 f f e 1f 8 f d 3e e e
  //   e 11 10 11 0 0 0 8 0 3e 0 21 22 c 71 3e 40 36 30 2 7f 6 6 e 3f 30*0 8 22 88 88 aa 0 8 14 8 8 14 14 0
  //   14 14 8 14 8 0 8 8 0 8 8 4*0 14 14 0 14 14 14 8 14 8 4*0 8 14 8 0 ff f ff 0 f0 16*0 15 1 1 1 0 0 8
  //   contents of rom_2 (hex, n*v repeats v):
  //   34*0 10 7f 3a 1a 4d 0 0 41 28 8 1 8 0 6 41 21 42 41 14 49 49 40 49 49 0 1 14 14 41 40 41 44 49 41 41
  //   49 48 41 8 41 41 8 1 20 10 41 48 41 48 49 40 1 c 3 14 10 45 7f 30 41 20 1 40 15 9 9 9 15 48 15 8 0 1
  //   4 0 8 8 11 14 14 4 15 11 1 1 1 a 8 13 8 0 41 10 0 41 21 42 41 14 49 49 40 49 49 15 9 9 9 15 48 30*0
  //   14 14 0 22 55 0 8 14 ff f 14 f7 ff 17 f4 f8 14 8 0 8 8 0 8 8 0 ff fc 1f f4 17 ff 14 f7 14 f8 14 f f8
  //   0 0 f ff 14 8 0 ff f ff 0 f0 16*0 15 11 45 11 3f 2 8
  //   contents of rom_3 (hex, n*v repeats v):
  //   33*0 7d 60 14 6b 4 45 70 3e 3e 70 3e 6 8 3 8 41 7f 45 49 24 49 49 43 49 49 36 36 22 14 22 45 49 44
  //   49 41 41 49 48 41 8 7f 7e 14 1 10 8 41 48 49 4c 49 7f 1 3 c 8 f 49 41 8 41 40 1 30 15 9 9 9 15 48 15
  //   8 2f 2e 1b 7f 7 8 11 14 14 4 15 0 1 2 2 4 7 15 36 77 36 8 0 41 7f 45 49 24 49 49 43 49 49 15 9 9 9
  //   15 48 30*0 2a 2a 22 88 aa ff ff ff 0 8 1f 0 0 10 4 8 fc f f8 f8 f ff 8 ff ff 0 4 10 4 10 0 14 0 f4 8
  //   17 8 8 fc 1f 8 8 ff f8 f ff f ff 0 f0 16*0 15 39 29 29 40 1 2a
  //   contents of rom_4 (hex, n*v repeats v):
  //   34*0 10 7f 2e b 22 0 41 0 28 8 0 8 0 30 41 1 49 49 7f 49 49 4c 49 49 0 0 41 14 14 48 55 44 49 41 41
  //   49 40 45 8 41 40 22 1 20 4 41 48 45 4a 49 40 1 c 3 14 10 51 41 6 7f 20 1 0 15 9 0 9 d 0 15 7 4*0 8 7
  //   e 8 f 8 16 0 e c 1 a 8 19 41 0 8 4 0 41 1 49 49 7f 49 49 4c 49 49 15 9 0 9 d 31*0 14 14 0 22 55 0 0
  //   0 ff f 0 ff ff 1f fc f8 0 0 6*8 14 ff f4 17 f4 17 f7 14 f7 14 f8 14 f f8 14 14 f ff 14 0 8 ff f 0 ff
  //   f0 16*0 15 11 11 45 20 7e 8
  //   contents of rom_5 (hex, n*v repeats v):
  //   34*0 60 14 0 13 5 4*0 8 0 8 0 40 3e 0 31 36 4 46 6 70 36 3e 0 0 0 14 8 30 38 7f 36 0 3e 0 0 26 7f 0
  //   0 41 0 7f 7f 7f 30 3e 31 46 40 7e 70 7c 63 60 61 0 1 0 0 1 0 f 6 0 7f 0 0 e 5*0 7 9*0 e 11 10 4*0 8
  //   0 3e 0 31 36 4 46 6 70 36 3e f 6 0 7f 32*0 22 8 88 88 aa 13*0 6*8 14 8 8*14 8 14 8 8 14 14 8 8 14 0
  //   8 ff f 0 ff f0 16*0 15 1 1 1 0 0 8
  //   contents of rom_6 (hex, n*v repeats v):
  //   177*0 22 55 13*0 6*8 14 8 8*14 8 14 8 8 14 14 8 8 14 0 8 ff f 0 ff f0
  //   Save actual RA not +2
  //   Enter
  //   Pc hi Adr f02
  //   Pc lo  Adr f03
  //   Exc code Adr f00
  //   Exc data Adr f01
  //   Adr f04
  //   R Pc
  //   W Ram
  //   W Pc
  //   R PC
  //   R PC+1
  //   W Pc
  //   W Acc
  //   Loading stops at fdf to avoid engaging the DMA
  //   Gen Interrupt Preventer reset f02
  //   R RAM 16
  //   Adr ALU
  //   Write Ram ffe=write on screen decoded
  //   TLB fe9 set adr in MMU to write, fea write, feb Cls
  //   MMU/ Page Table
  //   contents of rom_7 (hex, n*v repeats v):
  //   80 81 82 83 84 85 86 87 88 89 8a 8b 8c 8d 8e 8f 90 91 92 93 94 95 96 97 98 99 9a 9b 9c 9d 9e 9f a0
  //   a1 a2 a3 a4 a5 a6 a7 a8 a9 aa ab ac ad ae af b0 b1 b2 b3 b4 b5 b6 b7 b8 b9 ba bb bc bd be bf
  //   Interrupting Data flow to prevent next inst done twice
  //   To fix
  //   included from loader
  //   It activates on all W Ram
  //   DMA control
  //   HD Adr
  //   Ram Adr
  //   The interrupt when writing fe1 or fe3 stops the driver execution after the next instruction in executed
  //   R HD
  //   R Ram
  //   W Ram
  //   W HD
  //   16Kb HD 64 bites/page 256 pages
  //   HD
endmodule

module V096_96_Bites_32By24_Video_Buffer (
  input  in_1,
  input  [1:0] in_2,
  input  [1:0] in_3,
  input  [2:0] in_4,
  input  [7:0] in_5,
  input  in_6,
  input  in_7,
  output [31:0] out_8,
  output [31:0] out_9,
  output [31:0] out_10,
  output [31:0] out_11,
  output [31:0] out_12,
  output [31:0] out_13,
  output [31:0] out_14,
  output [31:0] out_15,
  output [31:0] out_16,
  output [31:0] out_17,
  output [31:0] out_18,
  output [31:0] out_19,
  output [31:0] out_20,
  output [31:0] out_21,
  output [31:0] out_22,
  output [31:0] out_23,
  output [31:0] out_24,
  output [31:0] out_25,
  output [31:0] out_26,
  output [31:0] out_27,
  output [31:0] out_28,
  output [31:0] out_29,
  output [31:0] out_30,
  output [31:0] out_31
);

  wire decoder_1_out0, decoder_1_out1, decoder_1_out2, decoder_1_out3, decoder_2_out1, decoder_2_out2,
       decoder_2_out3, decoder_2_out4, decoder_2_out5, decoder_2_out6, decoder_3_out0, decoder_3_out1,
       decoder_3_out2, decoder_3_out3, decoder_4_out1, decoder_4_out2, decoder_4_out3, decoder_4_out4,
       decoder_4_out5, decoder_4_out6, decoder_5_out0, decoder_5_out1, decoder_5_out2, decoder_5_out3,
       decoder_6_out1, decoder_6_out2, decoder_6_out3, decoder_6_out4, decoder_6_out5, decoder_6_out6,
       decoder_7_out0, decoder_7_out1, decoder_7_out2, decoder_7_out3, decoder_8_out1, decoder_8_out2,
       decoder_8_out3, decoder_8_out4, decoder_8_out5, decoder_8_out6, decoder_9_out0, decoder_9_out1,
       decoder_9_out2, decoder_9_out3, decoder_10_out1, decoder_10_out2, decoder_10_out3, decoder_10_out4,
       decoder_10_out5, decoder_10_out6, decoder_11_out1, decoder_11_out2, decoder_11_out3, decoder_11_out4,
       decoder_11_out5, decoder_11_out6, decoder_12_out1, decoder_12_out2, decoder_12_out3, decoder_12_out4,
       decoder_12_out5, decoder_12_out6, decoder_13_out1, decoder_13_out2, decoder_13_out3, decoder_13_out4,
       decoder_13_out5, decoder_13_out6, decoder_14_out1, decoder_14_out2, decoder_14_out3, decoder_14_out4,
       decoder_14_out5, decoder_14_out6, decoder_15_out1, decoder_15_out2, decoder_15_out3, decoder_15_out4,
       decoder_15_out5, decoder_15_out6, decoder_16_out1, decoder_16_out2, decoder_16_out3, decoder_16_out4,
       decoder_16_out5, decoder_16_out6, decoder_17_out1, decoder_17_out2, decoder_17_out3, decoder_17_out4,
       decoder_17_out5, decoder_17_out6, decoder_18_out1, decoder_18_out2, decoder_18_out3, decoder_18_out4,
       decoder_18_out5, decoder_18_out6, decoder_19_out1, decoder_19_out2, decoder_19_out3, decoder_19_out4,
       decoder_19_out5, decoder_19_out6, decoder_20_out1, decoder_20_out2, decoder_20_out3, decoder_20_out4,
       decoder_20_out5, decoder_20_out6, decoder_21_out1, decoder_21_out2, decoder_21_out3, decoder_21_out4,
       decoder_21_out5, decoder_21_out6;

  Decoder #(.select(2), .disabled(0)) decoder_1 (
    .out0(decoder_1_out0), .out1(decoder_1_out1), .out2(decoder_1_out2), .out3(decoder_1_out3), .sel(in_2),
    .en(in_1));
  Decoder #(.select(3), .disabled(0)) decoder_2 (
    .out1(decoder_2_out1), .out2(decoder_2_out2), .out3(decoder_2_out3), .out4(decoder_2_out4),
    .out5(decoder_2_out5), .out6(decoder_2_out6), .sel(in_4), .en(decoder_3_out0));  // open: out0, out7
  Decoder #(.select(2), .disabled(0)) decoder_3 (
    .out0(decoder_3_out0), .out1(decoder_3_out1), .out2(decoder_3_out2), .out3(decoder_3_out3), .sel(in_3),
    .en(decoder_1_out0));
  Decoder #(.select(3), .disabled(0)) decoder_4 (
    .out1(decoder_4_out1), .out2(decoder_4_out2), .out3(decoder_4_out3), .out4(decoder_4_out4),
    .out5(decoder_4_out5), .out6(decoder_4_out6), .sel(in_4), .en(decoder_5_out0));  // open: out0, out7
  Decoder #(.select(2), .disabled(0)) decoder_5 (
    .out0(decoder_5_out0), .out1(decoder_5_out1), .out2(decoder_5_out2), .out3(decoder_5_out3), .sel(in_3),
    .en(decoder_1_out1));
  Decoder #(.select(3), .disabled(0)) decoder_6 (
    .out1(decoder_6_out1), .out2(decoder_6_out2), .out3(decoder_6_out3), .out4(decoder_6_out4),
    .out5(decoder_6_out5), .out6(decoder_6_out6), .sel(in_4), .en(decoder_7_out0));  // open: out0, out7
  Decoder #(.select(2), .disabled(0)) decoder_7 (
    .out0(decoder_7_out0), .out1(decoder_7_out1), .out2(decoder_7_out2), .out3(decoder_7_out3), .sel(in_3),
    .en(decoder_1_out2));
  Decoder #(.select(3), .disabled(0)) decoder_8 (
    .out1(decoder_8_out1), .out2(decoder_8_out2), .out3(decoder_8_out3), .out4(decoder_8_out4),
    .out5(decoder_8_out5), .out6(decoder_8_out6), .sel(in_4), .en(decoder_9_out0));  // open: out0, out7
  Decoder #(.select(2), .disabled(0)) decoder_9 (
    .out0(decoder_9_out0), .out1(decoder_9_out1), .out2(decoder_9_out2), .out3(decoder_9_out3), .sel(in_3),
    .en(decoder_1_out3));
  Register register_1 (.D(in_5), .en(decoder_2_out1), .Q(out_8[31:24]), .clk(in_6), .clr(in_7));
  Register register_2 (.D(in_5), .en(decoder_2_out2), .Q(out_12[31:24]), .clk(in_6), .clr(in_7));
  Register register_3 (.D(in_5), .en(decoder_4_out1), .Q(out_8[23:16]), .clk(in_6), .clr(in_7));
  Register register_4 (.D(in_5), .en(decoder_4_out2), .Q(out_12[23:16]), .clk(in_6), .clr(in_7));
  Register register_5 (.D(in_5), .en(decoder_6_out1), .Q(out_8[15:8]), .clk(in_6), .clr(in_7));
  Register register_6 (.D(in_5), .en(decoder_6_out2), .Q(out_12[15:8]), .clk(in_6), .clr(in_7));
  Register register_7 (.D(in_5), .en(decoder_8_out1), .Q(out_8[7:0]), .clk(in_6), .clr(in_7));
  Register register_8 (.D(in_5), .en(decoder_8_out2), .Q(out_12[7:0]), .clk(in_6), .clr(in_7));
  Register register_9 (.D(in_5), .en(decoder_2_out3), .Q(out_16[31:24]), .clk(in_6), .clr(in_7));
  Register register_10 (.D(in_5), .en(decoder_2_out4), .Q(out_20[31:24]), .clk(in_6), .clr(in_7));
  Register register_11 (.D(in_5), .en(decoder_2_out5), .Q(out_24[31:24]), .clk(in_6), .clr(in_7));
  Register register_12 (.D(in_5), .en(decoder_4_out3), .Q(out_16[23:16]), .clk(in_6), .clr(in_7));
  Register register_13 (.D(in_5), .en(decoder_4_out4), .Q(out_20[23:16]), .clk(in_6), .clr(in_7));
  Register register_14 (.D(in_5), .en(decoder_4_out5), .Q(out_24[23:16]), .clk(in_6), .clr(in_7));
  Register register_15 (.D(in_5), .en(decoder_6_out3), .Q(out_16[15:8]), .clk(in_6), .clr(in_7));
  Register register_16 (.D(in_5), .en(decoder_6_out4), .Q(out_20[15:8]), .clk(in_6), .clr(in_7));
  Register register_17 (.D(in_5), .en(decoder_6_out5), .Q(out_24[15:8]), .clk(in_6), .clr(in_7));
  Register register_18 (.D(in_5), .en(decoder_8_out3), .Q(out_16[7:0]), .clk(in_6), .clr(in_7));
  Register register_19 (.D(in_5), .en(decoder_8_out4), .Q(out_20[7:0]), .clk(in_6), .clr(in_7));
  Register register_20 (.D(in_5), .en(decoder_8_out5), .Q(out_24[7:0]), .clk(in_6), .clr(in_7));
  Register register_21 (.D(in_5), .en(decoder_2_out6), .Q(out_28[31:24]), .clk(in_6), .clr(in_7));
  Register register_22 (.D(in_5), .en(decoder_4_out6), .Q(out_28[23:16]), .clk(in_6), .clr(in_7));
  Register register_23 (.D(in_5), .en(decoder_6_out6), .Q(out_28[15:8]), .clk(in_6), .clr(in_7));
  Register register_24 (.D(in_5), .en(decoder_8_out6), .Q(out_28[7:0]), .clk(in_6), .clr(in_7));
  Decoder #(.select(3), .disabled(0)) decoder_10 (
    .out1(decoder_10_out1), .out2(decoder_10_out2), .out3(decoder_10_out3), .out4(decoder_10_out4),
    .out5(decoder_10_out5), .out6(decoder_10_out6), .sel(in_4), .en(decoder_3_out1));  // open: out0, out7
  Decoder #(.select(3), .disabled(0)) decoder_11 (
    .out1(decoder_11_out1), .out2(decoder_11_out2), .out3(decoder_11_out3), .out4(decoder_11_out4),
    .out5(decoder_11_out5), .out6(decoder_11_out6), .sel(in_4), .en(decoder_5_out1));  // open: out0, out7
  Decoder #(.select(3), .disabled(0)) decoder_12 (
    .out1(decoder_12_out1), .out2(decoder_12_out2), .out3(decoder_12_out3), .out4(decoder_12_out4),
    .out5(decoder_12_out5), .out6(decoder_12_out6), .sel(in_4), .en(decoder_7_out1));  // open: out0, out7
  Decoder #(.select(3), .disabled(0)) decoder_13 (
    .out1(decoder_13_out1), .out2(decoder_13_out2), .out3(decoder_13_out3), .out4(decoder_13_out4),
    .out5(decoder_13_out5), .out6(decoder_13_out6), .sel(in_4), .en(decoder_9_out1));  // open: out0, out7
  Register register_25 (.D(in_5), .en(decoder_10_out1), .Q(out_9[31:24]), .clk(in_6), .clr(in_7));
  Register register_26 (.D(in_5), .en(decoder_10_out2), .Q(out_13[31:24]), .clk(in_6), .clr(in_7));
  Register register_27 (.D(in_5), .en(decoder_11_out1), .Q(out_9[23:16]), .clk(in_6), .clr(in_7));
  Register register_28 (.D(in_5), .en(decoder_11_out2), .Q(out_13[23:16]), .clk(in_6), .clr(in_7));
  Register register_29 (.D(in_5), .en(decoder_12_out1), .Q(out_9[15:8]), .clk(in_6), .clr(in_7));
  Register register_30 (.D(in_5), .en(decoder_12_out2), .Q(out_13[15:8]), .clk(in_6), .clr(in_7));
  Register register_31 (.D(in_5), .en(decoder_13_out1), .Q(out_9[7:0]), .clk(in_6), .clr(in_7));
  Register register_32 (.D(in_5), .en(decoder_13_out2), .Q(out_13[7:0]), .clk(in_6), .clr(in_7));
  Register register_33 (.D(in_5), .en(decoder_10_out3), .Q(out_17[31:24]), .clk(in_6), .clr(in_7));
  Register register_34 (.D(in_5), .en(decoder_10_out4), .Q(out_21[31:24]), .clk(in_6), .clr(in_7));
  Register register_35 (.D(in_5), .en(decoder_11_out3), .Q(out_17[23:16]), .clk(in_6), .clr(in_7));
  Register register_36 (.D(in_5), .en(decoder_11_out4), .Q(out_21[23:16]), .clk(in_6), .clr(in_7));
  Register register_37 (.D(in_5), .en(decoder_12_out3), .Q(out_17[15:8]), .clk(in_6), .clr(in_7));
  Register register_38 (.D(in_5), .en(decoder_12_out4), .Q(out_21[15:8]), .clk(in_6), .clr(in_7));
  Register register_39 (.D(in_5), .en(decoder_13_out3), .Q(out_17[7:0]), .clk(in_6), .clr(in_7));
  Register register_40 (.D(in_5), .en(decoder_13_out4), .Q(out_21[7:0]), .clk(in_6), .clr(in_7));
  Register register_41 (.D(in_5), .en(decoder_10_out5), .Q(out_25[31:24]), .clk(in_6), .clr(in_7));
  Register register_42 (.D(in_5), .en(decoder_10_out6), .Q(out_29[31:24]), .clk(in_6), .clr(in_7));
  Register register_43 (.D(in_5), .en(decoder_11_out5), .Q(out_25[23:16]), .clk(in_6), .clr(in_7));
  Register register_44 (.D(in_5), .en(decoder_11_out6), .Q(out_29[23:16]), .clk(in_6), .clr(in_7));
  Register register_45 (.D(in_5), .en(decoder_12_out5), .Q(out_25[15:8]), .clk(in_6), .clr(in_7));
  Register register_46 (.D(in_5), .en(decoder_12_out6), .Q(out_29[15:8]), .clk(in_6), .clr(in_7));
  Register register_47 (.D(in_5), .en(decoder_13_out5), .Q(out_25[7:0]), .clk(in_6), .clr(in_7));
  Register register_48 (.D(in_5), .en(decoder_13_out6), .Q(out_29[7:0]), .clk(in_6), .clr(in_7));
  Decoder #(.select(3), .disabled(0)) decoder_14 (
    .out1(decoder_14_out1), .out2(decoder_14_out2), .out3(decoder_14_out3), .out4(decoder_14_out4),
    .out5(decoder_14_out5), .out6(decoder_14_out6), .sel(in_4), .en(decoder_3_out2));  // open: out0, out7
  Decoder #(.select(3), .disabled(0)) decoder_15 (
    .out1(decoder_15_out1), .out2(decoder_15_out2), .out3(decoder_15_out3), .out4(decoder_15_out4),
    .out5(decoder_15_out5), .out6(decoder_15_out6), .sel(in_4), .en(decoder_5_out2));  // open: out0, out7
  Decoder #(.select(3), .disabled(0)) decoder_16 (
    .out1(decoder_16_out1), .out2(decoder_16_out2), .out3(decoder_16_out3), .out4(decoder_16_out4),
    .out5(decoder_16_out5), .out6(decoder_16_out6), .sel(in_4), .en(decoder_7_out2));  // open: out0, out7
  Decoder #(.select(3), .disabled(0)) decoder_17 (
    .out1(decoder_17_out1), .out2(decoder_17_out2), .out3(decoder_17_out3), .out4(decoder_17_out4),
    .out5(decoder_17_out5), .out6(decoder_17_out6), .sel(in_4), .en(decoder_9_out2));  // open: out0, out7
  Register register_49 (.D(in_5), .en(decoder_14_out1), .Q(out_10[31:24]), .clk(in_6), .clr(in_7));
  Register register_50 (.D(in_5), .en(decoder_15_out1), .Q(out_10[23:16]), .clk(in_6), .clr(in_7));
  Register register_51 (.D(in_5), .en(decoder_16_out1), .Q(out_10[15:8]), .clk(in_6), .clr(in_7));
  Register register_52 (.D(in_5), .en(decoder_17_out1), .Q(out_10[7:0]), .clk(in_6), .clr(in_7));
  Register register_53 (.D(in_5), .en(decoder_14_out2), .Q(out_14[31:24]), .clk(in_6), .clr(in_7));
  Register register_54 (.D(in_5), .en(decoder_14_out3), .Q(out_18[31:24]), .clk(in_6), .clr(in_7));
  Register register_55 (.D(in_5), .en(decoder_14_out4), .Q(out_22[31:24]), .clk(in_6), .clr(in_7));
  Register register_56 (.D(in_5), .en(decoder_15_out2), .Q(out_14[23:16]), .clk(in_6), .clr(in_7));
  Register register_57 (.D(in_5), .en(decoder_15_out3), .Q(out_18[23:16]), .clk(in_6), .clr(in_7));
  Register register_58 (.D(in_5), .en(decoder_15_out4), .Q(out_22[23:16]), .clk(in_6), .clr(in_7));
  Register register_59 (.D(in_5), .en(decoder_16_out2), .Q(out_14[15:8]), .clk(in_6), .clr(in_7));
  Register register_60 (.D(in_5), .en(decoder_16_out3), .Q(out_18[15:8]), .clk(in_6), .clr(in_7));
  Register register_61 (.D(in_5), .en(decoder_16_out4), .Q(out_22[15:8]), .clk(in_6), .clr(in_7));
  Register register_62 (.D(in_5), .en(decoder_17_out2), .Q(out_14[7:0]), .clk(in_6), .clr(in_7));
  Register register_63 (.D(in_5), .en(decoder_17_out3), .Q(out_18[7:0]), .clk(in_6), .clr(in_7));
  Register register_64 (.D(in_5), .en(decoder_17_out4), .Q(out_22[7:0]), .clk(in_6), .clr(in_7));
  Register register_65 (.D(in_5), .en(decoder_14_out5), .Q(out_26[31:24]), .clk(in_6), .clr(in_7));
  Register register_66 (.D(in_5), .en(decoder_14_out6), .Q(out_30[31:24]), .clk(in_6), .clr(in_7));
  Register register_67 (.D(in_5), .en(decoder_15_out5), .Q(out_26[23:16]), .clk(in_6), .clr(in_7));
  Register register_68 (.D(in_5), .en(decoder_15_out6), .Q(out_30[23:16]), .clk(in_6), .clr(in_7));
  Register register_69 (.D(in_5), .en(decoder_16_out5), .Q(out_26[15:8]), .clk(in_6), .clr(in_7));
  Register register_70 (.D(in_5), .en(decoder_16_out6), .Q(out_30[15:8]), .clk(in_6), .clr(in_7));
  Register register_71 (.D(in_5), .en(decoder_17_out5), .Q(out_26[7:0]), .clk(in_6), .clr(in_7));
  Register register_72 (.D(in_5), .en(decoder_17_out6), .Q(out_30[7:0]), .clk(in_6), .clr(in_7));
  Decoder #(.select(3), .disabled(0)) decoder_18 (
    .out1(decoder_18_out1), .out2(decoder_18_out2), .out3(decoder_18_out3), .out4(decoder_18_out4),
    .out5(decoder_18_out5), .out6(decoder_18_out6), .sel(in_4), .en(decoder_3_out3));  // open: out0, out7
  Decoder #(.select(3), .disabled(0)) decoder_19 (
    .out1(decoder_19_out1), .out2(decoder_19_out2), .out3(decoder_19_out3), .out4(decoder_19_out4),
    .out5(decoder_19_out5), .out6(decoder_19_out6), .sel(in_4), .en(decoder_5_out3));  // open: out0, out7
  Decoder #(.select(3), .disabled(0)) decoder_20 (
    .out1(decoder_20_out1), .out2(decoder_20_out2), .out3(decoder_20_out3), .out4(decoder_20_out4),
    .out5(decoder_20_out5), .out6(decoder_20_out6), .sel(in_4), .en(decoder_7_out3));  // open: out0, out7
  Decoder #(.select(3), .disabled(0)) decoder_21 (
    .out1(decoder_21_out1), .out2(decoder_21_out2), .out3(decoder_21_out3), .out4(decoder_21_out4),
    .out5(decoder_21_out5), .out6(decoder_21_out6), .sel(in_4), .en(decoder_9_out3));  // open: out0, out7
  Register register_73 (.D(in_5), .en(decoder_18_out1), .Q(out_11[31:24]), .clk(in_6), .clr(in_7));
  Register register_74 (.D(in_5), .en(decoder_19_out1), .Q(out_11[23:16]), .clk(in_6), .clr(in_7));
  Register register_75 (.D(in_5), .en(decoder_20_out1), .Q(out_11[15:8]), .clk(in_6), .clr(in_7));
  Register register_76 (.D(in_5), .en(decoder_21_out1), .Q(out_11[7:0]), .clk(in_6), .clr(in_7));
  Register register_77 (.D(in_5), .en(decoder_18_out2), .Q(out_15[31:24]), .clk(in_6), .clr(in_7));
  Register register_78 (.D(in_5), .en(decoder_18_out3), .Q(out_19[31:24]), .clk(in_6), .clr(in_7));
  Register register_79 (.D(in_5), .en(decoder_18_out4), .Q(out_23[31:24]), .clk(in_6), .clr(in_7));
  Register register_80 (.D(in_5), .en(decoder_19_out2), .Q(out_15[23:16]), .clk(in_6), .clr(in_7));
  Register register_81 (.D(in_5), .en(decoder_19_out3), .Q(out_19[23:16]), .clk(in_6), .clr(in_7));
  Register register_82 (.D(in_5), .en(decoder_19_out4), .Q(out_23[23:16]), .clk(in_6), .clr(in_7));
  Register register_83 (.D(in_5), .en(decoder_20_out2), .Q(out_15[15:8]), .clk(in_6), .clr(in_7));
  Register register_84 (.D(in_5), .en(decoder_20_out3), .Q(out_19[15:8]), .clk(in_6), .clr(in_7));
  Register register_85 (.D(in_5), .en(decoder_20_out4), .Q(out_23[15:8]), .clk(in_6), .clr(in_7));
  Register register_86 (.D(in_5), .en(decoder_21_out2), .Q(out_15[7:0]), .clk(in_6), .clr(in_7));
  Register register_87 (.D(in_5), .en(decoder_21_out3), .Q(out_19[7:0]), .clk(in_6), .clr(in_7));
  Register register_88 (.D(in_5), .en(decoder_21_out4), .Q(out_23[7:0]), .clk(in_6), .clr(in_7));
  Register register_89 (.D(in_5), .en(decoder_18_out5), .Q(out_27[31:24]), .clk(in_6), .clr(in_7));
  Register register_90 (.D(in_5), .en(decoder_18_out6), .Q(out_31[31:24]), .clk(in_6), .clr(in_7));
  Register register_91 (.D(in_5), .en(decoder_19_out5), .Q(out_27[23:16]), .clk(in_6), .clr(in_7));
  Register register_92 (.D(in_5), .en(decoder_19_out6), .Q(out_31[23:16]), .clk(in_6), .clr(in_7));
  Register register_93 (.D(in_5), .en(decoder_20_out5), .Q(out_27[15:8]), .clk(in_6), .clr(in_7));
  Register register_94 (.D(in_5), .en(decoder_20_out6), .Q(out_31[15:8]), .clk(in_6), .clr(in_7));
  Register register_95 (.D(in_5), .en(decoder_21_out5), .Q(out_27[7:0]), .clk(in_6), .clr(in_7));
  Register register_96 (.D(in_5), .en(decoder_21_out6), .Q(out_31[7:0]), .clk(in_6), .clr(in_7));

  // Notes on the sheet:
  //   Enable/Write
  //   Adr Y
  //   Adr X
  //   Adr Xc
  //   Data
  //   Clock
  //   Reset
endmodule
