// Logisim project HD Compressor.circ as structural Verilog: 1 circuit, main circuit main
module main (
  output [15:0] out_1
);

  wire clock_1_out, d_ff_1_q, d_ff_1_qn, d_ff_2_q, d_ff_2_qn, decoder_1_out0, decoder_1_out1, decoder_1_out2,
       decoder_1_out3, decoder_2_out0, decoder_2_out1, decoder_2_out2, decoder_2_out3, decoder_2_out4,
       decoder_2_out5, decoder_2_out6, decoder_2_out7, decoder_2_out8, decoder_2_out9, decoder_2_out10,
       decoder_2_out11, decoder_2_out12, decoder_2_out13, decoder_2_out14, decoder_2_out15, nand_1_out,
       On_out, or_2_out, or_3_out, or_4_out, undriven, undriven_2, undriven_3;
  wire [3:0] adder_2_out, register_2_q;
  wire [7:0] multiplexer_2_out, ram_1_data, register_3_q, register_4_q, register_5_q, register_6_q;
  wire [15:0] adder_1_out, multiplexer_1_out, xor_1_out;
  wire [31:0] multiplexer_3_out, ram_2_data;

  Button On (.out(On_out));
  Clock clock_1 (.out(clock_1_out));
  Register #(.width(16)) register_1 (.D(adder_1_out), .en(or_3_out), .Q(out_1), .clk(clock_1_out), .clr(nand_1_out));
  D_Flip_Flop d_ff_1 (
    .clk(clock_1_out), .D(On_out), .Q(d_ff_1_q), .Qn(d_ff_1_qn), .en(undriven), .reset(undriven_2));  // open: preset
  D_Flip_Flop d_ff_2 (
    .clk(clock_1_out), .D(d_ff_1_q), .Q(d_ff_2_q), .Qn(d_ff_2_qn), .en(d_ff_1_q), .reset(nand_1_out));  // open: preset
  // OR_Gate or_1 has open pins: in0=decoder_1_out1, in1=decoder_1_out2, out=open
  Multiplexer #(.width(16), .enable("false")) multiplexer_1 (
    .in0({16{1'b0}}), .in1(out_1), .out(multiplexer_1_out), .sel(or_3_out));
  or or_2 (or_2_out, decoder_2_out2, decoder_2_out3, decoder_2_out5, decoder_2_out6, decoder_2_out8, decoder_2_out9, decoder_2_out11, decoder_2_out12);
  or or_3 (or_3_out, decoder_2_out3, decoder_2_out6, decoder_2_out9, decoder_2_out14);
  Register #(.width(4)) register_2 (
    .D(adder_2_out), .en(d_ff_2_q), .Q(register_2_q), .clk(clock_1_out), .clr(nand_1_out));
  Decoder #(.select(2), .disabled(0)) decoder_1 (
    .out0(decoder_1_out0), .out1(decoder_1_out1), .out2(decoder_1_out2), .out3(decoder_1_out3), .en(d_ff_2_q));  // open: sel
  Decoder #(.select(4), .disabled(0)) decoder_2 (
    .out0(decoder_2_out0), .out1(decoder_2_out1), .out2(decoder_2_out2), .out3(decoder_2_out3),
    .out4(decoder_2_out4), .out5(decoder_2_out5), .out6(decoder_2_out6), .out7(decoder_2_out7),
    .out8(decoder_2_out8), .out9(decoder_2_out9), .out10(decoder_2_out10), .out11(decoder_2_out11),
    .out12(decoder_2_out12), .out13(decoder_2_out13), .out14(decoder_2_out14), .out15(decoder_2_out15),
    .sel(register_2_q), .en(d_ff_2_q));
  nand nand_1 (nand_1_out, or_4_out, or_4_out);
  Adder #(.width(16)) adder_1 (.a({16{1'b0}}), .b(multiplexer_1_out), .out(adder_1_out), .cin(or_3_out));  // open: cout
  Adder #(.width(4)) adder_2 (.a(4'b0000), .b(register_2_q), .out(adder_2_out), .cin(1'b1));  // open: cout
  or or_4 (or_4_out, xor_1_out[0], xor_1_out[1], xor_1_out[2], xor_1_out[3], xor_1_out[4], xor_1_out[5], xor_1_out[6], xor_1_out[7], xor_1_out[8], xor_1_out[9], xor_1_out[10], xor_1_out[11], xor_1_out[12], xor_1_out[13], xor_1_out[14], xor_1_out[15]);
  Decoder #(.select(2), .disabled(0)) decoder_3 (.sel(out_1[1:0]));  // open: out0, out1, out2, out3, en
  assign xor_1_out = 16'h3fff ^ out_1;  // XOR_Gate xor_1, 16 bits wide
  Multiplexer #(.width(8), .enable("false")) multiplexer_2 (
    .in0({8{1'b0}}), .in1(ram_1_data), .out(multiplexer_2_out), .sel(or_2_out));
  RAM #(.addrWidth(16), .bus("separate")) ram_1 (
    .addr(out_1), .data(ram_1_data), .str(1'b0), .clk(clock_1_out), .ld(or_2_out));  // open: din, sel, clr
  Register register_3 (
    .D(multiplexer_2_out), .en(decoder_2_out3), .Q(register_3_q), .clk(decoder_2_out3));  // open: clr
  Register register_4 (
    .D(multiplexer_2_out), .en(decoder_2_out6), .Q(register_4_q), .clk(decoder_2_out6));  // open: clr
  Register register_5 (
    .D(multiplexer_2_out), .en(decoder_2_out9), .Q(register_5_q), .clk(decoder_2_out9));  // open: clr
  Register register_6 (
    .D(multiplexer_2_out), .en(decoder_2_out12), .Q(register_6_q), .clk(decoder_2_out12));  // open: clr
  RAM #(.addrWidth(12), .dataWidth(32), .bus("separate")) ram_2 (
    .addr(out_1[13:2]), .din({register_3_q, register_4_q, register_5_q, register_6_q}), .data(ram_2_data),
    .str(decoder_2_out13), .clk(clock_1_out), .ld(undriven_3));  // open: sel, clr
  Multiplexer #(.width(32), .enable("false")) multiplexer_3 (
    .in0({32{1'b0}}), .in1(ram_2_data), .out(multiplexer_3_out), .sel(undriven_3));

  // Notes on the sheet:
  //   16Kb HD 64 bites/page 256 pages
  //   HD
endmodule
